// Logisim project mycirc.circ as structural Verilog: 1 circuit, main circuit main
module main (
  input  Midi___Buzzer,
  input  [7:0] in_2,
  input  [6:0] Volume,
  output [7:0] Church_Organ,
  output [7:0] out_5,
  output [15:0] out_6,
  output [7:0] Tubular_Bell,
  output [7:0] Vibraphone
);

  wire advanced_buzzer_1_p4, BE, controlled_buffer_2_out, not_1_out;
  wire [7:0] controlled_buffer_1_out, mckeyboard_1_p1, mckeyboard_1_p2, mckeyboard_1_p3, mckeyboard_1_p4,
       mckeyboard_2_p3, mckeyboard_2_p4, mckeyboard_2_p5, mckeyboard_2_p6, mckeyboard_3_p1, mckeyboard_3_p2,
       mckeyboard_3_p3, mckeyboard_3_p4;

  // sound_emitter sound_emitter_1: pin names not known; wires that end beside it: out_5
  assign out_5 = mckeyboard_2_p5 | mckeyboard_3_p3 | mckeyboard_1_p3;  // OR_Gate or_1, 8 bits wide
  assign Tubular_Bell = mckeyboard_2_p4 | mckeyboard_3_p2 | mckeyboard_1_p2;  // OR_Gate or_2, 8 bits wide
  // sound_emitter sound_emitter_2: pin names not known; wires that end beside it: Tubular_Bell
  // sound_emitter sound_emitter_3: pin names not known
  assign Vibraphone = mckeyboard_2_p3 | mckeyboard_3_p1 | mckeyboard_1_p1;  // OR_Gate or_3, 8 bits wide
  // MCKeyboard mckeyboard_1: pin names not known; wires that end beside it: mckeyboard_1_p1, mckeyboard_1_p2, mckeyboard_1_p3, mckeyboard_1_p4
  // MCKeyboard mckeyboard_2: pin names not known; wires that end beside it: BE, out_6, mckeyboard_2_p3, mckeyboard_2_p4, mckeyboard_2_p5, mckeyboard_2_p6
  // MCKeyboard mckeyboard_3: pin names not known; wires that end beside it: mckeyboard_3_p1, mckeyboard_3_p2, mckeyboard_3_p3, mckeyboard_3_p4
  assign controlled_buffer_1_out = not_1_out ? mckeyboard_1_p4 : 8'bz;  // Controlled_Buffer controlled_buffer_1
  not not_1 (not_1_out, Midi___Buzzer);
  // Probe on Vibraphone
  assign Church_Organ = mckeyboard_3_p4 | mckeyboard_2_p6 | controlled_buffer_1_out;  // OR_Gate or_4, 8 bits wide
  assign controlled_buffer_2_out = Midi___Buzzer ? BE : 1'bz;  // Controlled_Buffer controlled_buffer_2
  // sound_emitter sound_emitter_4: pin names not known; wires that end beside it: Church_Organ
  // Advanced_buzzer advanced_buzzer_1: pin names not known; wires that end beside it: out_6, controlled_buffer_2_out, Volume, advanced_buzzer_1_p4
  Clock #(.highDuration(1), .lowDuration(1)) clock_1 (.out(advanced_buzzer_1_p4));

  // Other names for the same wires on the sheet: BF[15:0] = out_6

  // Notes on the sheet:
  //   Percussion
  //   Close Encounters of the Third Kind is:
  //   D6 E6 C6 C5 G5
  //   D8 E8 C8 C7 G7
  //   or:
  //   etc.
endmodule
