// Logisim project cpu单周期+流水线+扩展指令+动态分支预测+流水多级中断.circ as structural Verilog: 22 circuits, main circuit ◇单周期MIPS
module \单周期MIPS  (
  output RegWrite,
  output MemWrite,
  output [31:0] PC,
  output [31:0] IR,
  output [31:0] RDin,
  output [31:0] MDin
);

  wire and_1_out, and_2_out, and_3_out, and_4_out, and_7_out, and_8_out, and_9_out, CLK, comparator_1_eq,
       comparator_2_eq, comparator_3_eq, comparator_4_eq, comparator_5_eq, comparator_6_eq, comparator_7_eq,
       comparator_8_gt, comparator_9_eq, \CPU中断请求 , d_ff_1_q, d_ff_2_q, d_ff_3_q, demultiplexer_1_out1,
       demultiplexer_1_out2, demultiplexer_1_out3, ERET, Go, IE, IR1, IR1_q, IR2, IR2_q, IR3, IR3_q, MFC0,
       MTC0, nand_1_out, not_1_out, or_1_out, or_3_out, or_7_out, or_8_out, or_9_out, or_10_out, or_11_out,
       RST, SignedExt, syscall, tunnel, W1, W2, W3, \单周期硬布线控制器_1_alu_src , \单周期硬布线控制器_1_beq ,
       \单周期硬布线控制器_1_bne , \单周期硬布线控制器_1_jal , \单周期硬布线控制器_1_jmp , \单周期硬布线控制器_1_jr , \单周期硬布线控制器_1_memtoreg ,
       \单周期硬布线控制器_1_regdst ;
  wire [1:0] counter_4_q, priority_encoder_1_out, register_1_q, subtractor_1_out;
  wire [3:0] \单周期硬布线控制器_1_alu_op ;
  wire [4:0] multiplexer_6_out, multiplexer_7_out, multiplexer_8_out, multiplexer_9_out;
  wire [15:0] \总周期数 , \无条件分支数 , \条件分支成功数 ;
  wire [27:0] adder_1_out_2;
  wire [31:0] adder_2_out, adder_3_out, bit_extender_1_out, bit_extender_2_out, EPC_2_q, EPC_3_q, EPC_q,
       LedData, mips_alu_1_result, mips_regifile_1_r1, multiplexer_1_out, multiplexer_2_out,
       multiplexer_3_out, multiplexer_4_out, multiplexer_5_out, multiplexer_10_out, multiplexer_11_out,
       multiplexer_13_out, multiplexer_14_out, multiplexer_15_out, multiplexer_16_out, ram_1_data,
       shifter_1_out;
  wire [31:28] adder_1_out;

  Clock #(.highDuration(1), .lowDuration(1)) clock_1 (.out(CLK));
  Button _1 (.out(IR1));
  Button _2 (.out(IR2));
  Button _3 (.out(IR3));
  Button \u_总复位  (.out(RST));
  Register #(.width(32), .trigger("rising"), .Select("low")) u_PC (
    .D(multiplexer_2_out), .en(nand_1_out), .Q(PC), .clk(CLK), .clr(RST));
  Multiplexer #(.select(1), .width(32), .disabled("Z"), .enable("false")) multiplexer_1 (
    .in0(multiplexer_3_out), .in1(mips_regifile_1_r1), .out(multiplexer_1_out), .sel(\单周期硬布线控制器_1_jr ));
  Multiplexer #(.select(1), .width(32), .disabled("Z"), .enable("false")) multiplexer_2 (
    .in0(multiplexer_4_out), .in1(EPC_q), .out(multiplexer_2_out), .sel(ERET));
  // Probe on multiplexer_2_out
  Button \u_继续运行  (.out(Go));
  LED #(.active("true")) led_1 (.in(W1));
  LED #(.active("true")) led_2 (.in(W2));
  LED #(.active("true")) led_3 (.in(W3));
  Multiplexer #(.select(1), .width(32), .disabled("Z"), .enable("false")) multiplexer_3 (
    .in0(multiplexer_5_out), .in1({adder_1_out, IR[25:0], 2'b00}), .out(multiplexer_3_out), .sel(or_1_out));
  or or_1 (or_1_out, \单周期硬布线控制器_1_jal , \单周期硬布线控制器_1_jmp );
  Multiplexer #(.select(1), .width(32), .disabled("Z"), .enable("false")) multiplexer_4 (
    .in0(multiplexer_1_out), .in1(multiplexer_16_out), .out(multiplexer_4_out), .sel(\CPU中断请求 ));
  Hex_Digit_Display hex_digit_display_1 (.value(LedData[31:28]));  // open: dp
  ROM #(.addrWidth(10), .dataWidth(32), .Select("high")) rom_1 (.addr(PC[11:2]), .data(IR));
  Adder #(.width(32)) adder_1 (.a(PC), .b(32'h4), .out({adder_1_out, adder_1_out_2}));  // open: cin, cout
  Multiplexer #(.select(1), .width(32), .disabled("Z"), .enable("false")) multiplexer_5 (
    .in0({adder_1_out, adder_1_out_2}), .in1(adder_2_out), .out(multiplexer_5_out), .sel(or_3_out));
  Hex_Digit_Display hex_digit_display_2 (.value(LedData[27:24]));  // open: dp
  Hex_Digit_Display hex_digit_display_3 (.value(LedData[23:20]));  // open: dp
  Multiplexer #(.select(1), .width(5), .disabled("Z"), .enable("false")) multiplexer_6 (
    .in0(IR[25:21]), .in1(5'b00100), .out(multiplexer_6_out), .sel(syscall));
  Multiplexer #(.select(1), .width(5), .disabled("Z"), .enable("false")) multiplexer_7 (
    .in0(IR[20:16]), .in1(5'b00010), .out(multiplexer_7_out), .sel(syscall));
  Hex_Digit_Display hex_digit_display_4 (.value(LedData[19:16]));  // open: dp
  Hex_Digit_Display hex_digit_display_5 (.value(LedData[15:12]));  // open: dp
  Multiplexer #(.select(1), .width(5), .disabled("Z"), .enable("false")) multiplexer_8 (
    .in0(IR[20:16]), .in1(IR[15:11]), .out(multiplexer_8_out), .sel(\单周期硬布线控制器_1_regdst ));
  assign bit_extender_1_out = {{16{IR[15]}}, IR[15:0]};  // Bit_Extender bit_extender_1
  assign bit_extender_2_out = {{16{1'b0}}, IR[15:0]};  // Bit_Extender bit_extender_2
  Comparator #(.width(32), .mode("twosComplement")) comparator_1 (
    .a(MDin), .b(32'h22), .eq(comparator_1_eq));  // open: gt, lt
  Counter #(.width(16), .max('hffff), .ongoal("wrap"), .trigger("rising"), .behavior("old")) counter_1 (
    .count(nand_1_out), .Q(\总周期数 ), .clk(CLK), .clr(RST));  // open: load, D, carry, preset
  Hex_Digit_Display hex_digit_display_6 (.value(LedData[7:4]));  // open: dp
  Hex_Digit_Display hex_digit_display_7 (.value(LedData[11:8]));  // open: dp
  // Probe on \总周期数 
  MIPS_Regifile mips_regifile_1 (
    .Din(RDin), .Clk(CLK), .R1(mips_regifile_1_r1), .R2(MDin), .WE(RegWrite), .W_num(multiplexer_9_out),
    .R1_num(multiplexer_6_out), .R2_num(multiplexer_7_out));
  Multiplexer #(.select(1), .width(5), .disabled("Z"), .enable("false")) multiplexer_9 (
    .in0(multiplexer_8_out), .in1({5{1'b1}}), .out(multiplexer_9_out), .sel(\单周期硬布线控制器_1_jal ));
  Shifter #(.width(32), .shift("ll")) shifter_1 (.in(bit_extender_1_out), .\dist (5'b00010), .out(shifter_1_out));
  Multiplexer #(.select(1), .width(32), .disabled("Z"), .enable("false")) multiplexer_10 (
    .in0(bit_extender_2_out), .in1(bit_extender_1_out), .out(multiplexer_10_out), .sel(SignedExt));
  and and_1 (and_1_out, comparator_1_eq, syscall);
  and and_2 (and_2_out, syscall, ~comparator_1_eq);  // AND_Gate
  Hex_Digit_Display hex_digit_display_8 (.value(LedData[3:0]));  // open: dp
  Multiplexer #(.select(1), .width(32), .disabled("Z"), .enable("false")) multiplexer_11 (
    .in0(MDin), .in1(multiplexer_10_out), .out(multiplexer_11_out), .sel(\单周期硬布线控制器_1_alu_src ));
  Multiplexer #(.select(1), .width(32), .disabled("Z"), .enable("false")) multiplexer_12 (
    .in0(multiplexer_13_out), .in1({adder_1_out, adder_1_out_2}), .out(RDin), .sel(\单周期硬布线控制器_1_jal ));
  Adder #(.width(32)) adder_2 (
    .a(shifter_1_out), .b({adder_1_out, adder_1_out_2}), .out(adder_2_out));  // open: cin, cout
  nand nand_1 (nand_1_out, and_2_out, ~Go);  // NAND_Gate
  // Probe on PC
  MIPS_ALU mips_alu_1 (
    .X(mips_regifile_1_r1), .Y(multiplexer_11_out), .AluOP(\单周期硬布线控制器_1_alu_op ), .Equal(tunnel),
    .Result(mips_alu_1_result), .shamt(IR[10:6]));  // open: Result_2
  Register #(.width(32), .trigger("rising"), .Select("low")) u_leddata (
    .D(mips_regifile_1_r1), .en(and_1_out), .Q(LedData), .clk(CLK), .clr(RST));
  Multiplexer #(.select(1), .width(32), .disabled("Z"), .enable("false")) multiplexer_13 (
    .in0(mips_alu_1_result), .in1(ram_1_data), .out(multiplexer_13_out), .sel(\单周期硬布线控制器_1_memtoreg ));
  RAM #(.addrWidth(11), .dataWidth(32), .bus("separate"), .Select("high")) ram_1 (
    .addr(mips_alu_1_result[12:2]), .din(MDin), .data(ram_1_data), .str(MemWrite), .clk(CLK), .clr(RST));  // open: sel, ld
  // OR_Gate or_2 has open pins: in0=or_1_out, out=open
  \单周期硬布线控制器  \u_单周期硬布线控制器_1  (
    .Func(IR[5:0]), .OP(IR[31:26]), .ALU_OP(\单周期硬布线控制器_1_alu_op ), .MemToReg(\单周期硬布线控制器_1_memtoreg ),
    .MemWrite(MemWrite), .ALU_SRC(\单周期硬布线控制器_1_alu_src ), .RegWrite(RegWrite), .SysCALL(syscall),
    .SignedExt(SignedExt), .RegDst(\单周期硬布线控制器_1_regdst ), .JR(\单周期硬布线控制器_1_jr ), .JMP(\单周期硬布线控制器_1_jmp ),
    .Beq(\单周期硬布线控制器_1_beq ), .JAL(\单周期硬布线控制器_1_jal ), .Bne(\单周期硬布线控制器_1_bne ));
  and and_3 (and_3_out, \单周期硬布线控制器_1_bne , ~tunnel);  // AND_Gate
  or or_3 (or_3_out, and_3_out, and_4_out);
  and and_4 (and_4_out, \单周期硬布线控制器_1_beq , tunnel);
  Counter #(.width(16), .max('hffff), .ongoal("wrap"), .trigger("rising"), .behavior("old")) counter_2 (
    .count(or_3_out), .Q(\条件分支成功数 ), .clk(CLK), .clr(RST));  // open: load, D, carry, preset
  Counter #(.width(16), .max('hffff), .ongoal("wrap"), .trigger("rising"), .behavior("old")) counter_3 (
    .count(\单周期硬布线控制器_1_jr ), .Q(\无条件分支数 ), .clk(CLK), .clr(RST));  // open: load, D, carry, preset
  Comparator #(.width(6), .mode("twosComplement")) comparator_2 (
    .a(IR[31:26]), .b(6'b010000), .eq(comparator_2_eq));  // open: gt, lt
  Comparator #(.width(6), .mode("twosComplement")) comparator_3 (
    .a(IR[5:0]), .b(6'b011000), .eq(comparator_3_eq));  // open: gt, lt
  // Probe on comparator_3_eq
  or or_4 (W1, IR1_q, d_ff_1_q);
  or or_5 (W2, IR2_q, d_ff_2_q);
  or or_6 (W3, IR3_q, d_ff_3_q);
  and and_5 (ERET, comparator_2_eq, comparator_3_eq);
  // Probe on ERET
  or or_7 (or_7_out, \CPU中断请求 , ERET);
  D_Flip_Flop #(.trigger("rising"), .Pre_Clr_Positions("LEGACY"), .NegatePresetClear("false"), .enable("true"), .NewFFLayout("false")) d_ff_1 (
    .clk(IR1), .D(1'b1), .Q(d_ff_1_q), .reset(IR1_q));  // open: Qn, preset, en
  D_Flip_Flop #(.trigger("rising"), .Pre_Clr_Positions("LEGACY"), .NegatePresetClear("false"), .enable("true"), .NewFFLayout("false")) d_ff_2 (
    .clk(IR2), .D(1'b1), .Q(d_ff_2_q), .reset(IR2_q));  // open: Qn, preset, en
  D_Flip_Flop #(.trigger("rising"), .Pre_Clr_Positions("LEGACY"), .NegatePresetClear("false"), .enable("true"), .NewFFLayout("false")) d_ff_3 (
    .clk(IR3), .D(1'b1), .Q(d_ff_3_q), .reset(IR3_q));  // open: Qn, preset, en
  or or_8 (or_8_out, d_ff_1_q, IR1_q);
  or or_9 (or_9_out, d_ff_2_q, IR2_q);
  or or_10 (or_10_out, d_ff_3_q, IR3_q);
  Comparator #(.width(6), .mode("twosComplement")) comparator_4 (
    .a(IR[31:26]), .b(6'b010000), .eq(comparator_4_eq));  // open: gt, lt
  and and_6 (MTC0, comparator_4_eq, comparator_5_eq);
  // Probe on MTC0
  Comparator #(.width(5), .mode("twosComplement")) comparator_5 (
    .a(IR[25:21]), .b(5'b00100), .eq(comparator_5_eq));  // open: gt, lt
  Adder #(.width(32)) adder_3 (.a(PC), .b(32'h4), .out(adder_3_out));  // open: cin, cout
  and and_7 (and_7_out, or_8_out, ~demultiplexer_1_out1);  // AND_Gate
  and and_8 (and_8_out, or_9_out, ~demultiplexer_1_out2);  // AND_Gate
  and and_9 (and_9_out, or_10_out, ~demultiplexer_1_out3);  // AND_Gate
  Comparator #(.width(6), .mode("twosComplement")) comparator_6 (
    .a(IR[31:26]), .b(6'b010000), .eq(comparator_6_eq));  // open: gt, lt
  and and_10 (MFC0, comparator_6_eq, comparator_7_eq);
  // Probe on MFC0
  Comparator #(.width(5), .mode("twosComplement")) comparator_7 (
    .a(IR[25:21]), .b({5{1'b0}}), .eq(comparator_7_eq));  // open: gt, lt
  Multiplexer #(.select(1), .width(32), .disabled("Z"), .enable("false")) multiplexer_14 (
    .in0(EPC_2_q), .in1(adder_3_out), .out(multiplexer_14_out), .sel(\CPU中断请求 ));
  D_Flip_Flop #(.trigger("rising"), .Pre_Clr_Positions("LEGACY"), .NegatePresetClear("false"), .enable("true"), .NewFFLayout("false")) u_IR1 (
    .clk(CLK), .D(and_7_out), .Q(IR1_q));  // open: Qn, preset, en, reset
  D_Flip_Flop #(.trigger("rising"), .Pre_Clr_Positions("LEGACY"), .NegatePresetClear("false"), .enable("true"), .NewFFLayout("false")) u_IR2 (
    .clk(CLK), .D(and_8_out), .Q(IR2_q));  // open: Qn, preset, en, reset
  D_Flip_Flop #(.trigger("rising"), .Pre_Clr_Positions("LEGACY"), .NegatePresetClear("false"), .enable("true"), .NewFFLayout("false")) u_IR3 (
    .clk(CLK), .D(and_9_out), .Q(IR3_q));  // open: Qn, preset, en, reset
  not not_1 (not_1_out, IE);
  Register #(.width(32), .trigger("rising"), .Select("low")) EPC (
    .D(multiplexer_14_out), .en(or_7_out), .Q(EPC_q), .clk(CLK));  // open: clr
  // Probe on EPC_q
  // Probe on demultiplexer_1_out3
  Priority_Encoder #(.select(2), .disabled("Z")) priority_encoder_1 (
    .in0(1'b1), .in1(IR1_q), .in2(IR2_q), .in3(IR3_q), .out(priority_encoder_1_out));  // open: gs, en_out, en_in
  Register #(.width(1), .trigger("rising"), .Select("low")) u_IE (
    .D(\CPU中断请求 ), .en(not_1_out), .Q(IE), .clk(CLK), .clr(or_11_out), .preset(MTC0));  // open: cs
  Multiplexer #(.select(1), .width(32), .disabled("Z"), .enable("false")) multiplexer_15 (
    .in0(EPC_3_q), .in1(EPC_q), .out(multiplexer_15_out), .sel(\CPU中断请求 ));
  Demultiplexer #(.select(2), .width(1), .tristate("false"), .disabled("Z"), .enable("false")) demultiplexer_1 (
    .out1(demultiplexer_1_out1), .out2(demultiplexer_1_out2), .out3(demultiplexer_1_out3), .in(ERET),
    .sel(priority_encoder_1_out));  // open: out0
  // Probe on priority_encoder_1_out
  and and_11 (\CPU中断请求 , comparator_8_gt, ~IE);  // AND_Gate
  // Probe on \CPU中断请求 
  or or_11 (or_11_out, ERET, MFC0);
  Register #(.width(32), .trigger("rising"), .Select("low")) EPC_2 (
    .D(multiplexer_15_out), .en(or_7_out), .Q(EPC_2_q), .clk(CLK));  // open: clr
  // Probe on EPC_2_q
  Multiplexer #(.select(2), .width(32), .disabled("Z"), .enable("false")) multiplexer_16 (
    .in1(32'hc00), .in2(32'hc80), .in3(32'hd00), .out(multiplexer_16_out), .sel(priority_encoder_1_out));  // open: in0
  // Probe on priority_encoder_1_out
  Register #(.width(2), .trigger("rising"), .Select("low")) register_1 (
    .D(priority_encoder_1_out), .Q(register_1_q), .clk(CLK), .clr(comparator_9_eq));  // open: en
  Register #(.width(32), .trigger("rising"), .Select("low")) EPC_3 (
    .D(EPC_2_q), .en(or_7_out), .Q(EPC_3_q), .clk(CLK));  // open: clr
  // Probe on register_1_q
  Comparator #(.width(2), .mode("unsigned")) comparator_8 (
    .a(priority_encoder_1_out), .b(register_1_q), .gt(comparator_8_gt));  // open: eq, lt
  // Probe on comparator_8_gt
  Counter #(.width(2), .max('h3), .ongoal("wrap"), .trigger("rising"), .behavior("old")) counter_4 (
    .load(ERET), .D(subtractor_1_out), .count(\CPU中断请求 ), .Q(counter_4_q), .clk(CLK));  // open: carry, clr, preset
  Subtractor #(.width(2)) subtractor_1 (.a(counter_4_q), .b(2'b01), .out(subtractor_1_out));  // open: bin, bout
  Comparator #(.width(2), .mode("twosComplement")) comparator_9 (
    .a(2'b00), .b(counter_4_q), .eq(comparator_9_eq));  // open: gt, lt
  // Probe on counter_4_q

  // Other names for the same wires on the sheet: RS[4:0] = IR[25:21]

  // Notes on the sheet:
  //   中断源
  //   中断等待指示
  //   总复位信号应将除ROM以外所有存储组件全部清零
  //   指令存储器
  //   contents of rom_1 (hex, n*v repeats v):
  //   20110001 8000c05 20110001 20120002 20130003 8000c09 20110001 20120002 20130003 8000c0d 20110001
  //   20120002 20130003 8000c11 20110001 20120002 20130003 c000cb8 20100001 20110001 118fc0 112020
  //   20020022 c 118882 12200001 8000c15 112020 20020022 c 20110001 118880 112020 20020022 c 12200001
  //   8000c1f 20110001 118fc0 112020 20020022 c 1188c3 112020 20020022 c 118903 112020 20020022 c 118903
  //   112020 20020022 c 118903 112020 20020022 c 118903 112020 20020022 c 118903 112020 20020022 c 118903
  //   112020 20020022 c 118903 112020 20020022 c 20100001 109fc0 139fc3 8021 2012000c 24160003 26100001
  //   3210000f 20080008 20090001 139900 2709825 132020 20020022 c 1094022 1500fff9 22100001 2018000f
  //   2188024 108700 20080008 20090001 139902 2709825 132021 20020022 c 1094022 1500fff9 108702 2c9b022
  //   12c00001 8000c50 4020 1084027 84400 3508ffff 82021 20020022 c 2010ffff 20110000 ae300000 22100001
  //   22310004 ae300000 22100001 22310004 ae300000 22100001 22310004 ae300000 22100001 22310004 ae300000
  //   22100001 22310004 ae300000 22100001 22310004 ae300000 22100001 22310004 ae300000 22100001 22310004
  //   ae300000 22100001 22310004 ae300000 22100001 22310004 ae300000 22100001 22310004 ae300000 22100001
  //   22310004 ae300000 22100001 22310004 ae300000 22100001 22310004 ae300000 22100001 22310004 ae300000
  //   22100001 22310004 22100001 8020 2011003c 8e130000 8e340000 274402a 11000002 ae330000 ae140000
  //   2231fffc 1611fff8 102020 20020022 c 22100004 2011003c 1611fff2 20020032 c 20100000 22100001 102020
  //   20020022 c 22100002 102020 20020022 c 22100003 102020 20020022 c 22100004 102020 20020022 c 22100005
  //   102020 20020022 c 22100006 102020 20020022 c 22100007 102020 20020022 c 22100008 102020 20020022
  //   20020022 c 3e00008 549*0 ac161c00 ac141c04 ac151c08 ac101c0c ac131c10 ac041c14 ac021c18 40000000
  //   20160001 20140006 20150001 168020 108100 2149825 132020 20020022 c 1600fffa 295a022 1680fff7
  //   40800000 8c161c00 8c141c04 8c151c08 8c101c0c 8c131c10 8c041c14 8c021c18 42000018 0 0 0 ac161c20
  //   ac141c24 ac151c28 ac101c2c ac131c30 ac041c34 ac021c38 40000000 20160002 20140006 20150001 168020
  //   108100 2149825 132020 20020022 c 1600fffa 295a022 1680fff7 40800000 8c161c20 8c141c24 8c151c28
  //   8c101c2c 8c131c30 8c041c34 8c021c38 42000018 0 0 0 ac161c40 ac141c44 ac151c48 ac101c4c ac131c50
  //   ac041c54 ac021c58 40000000 20160003 20140006 20150001 168020 108100 2149825 132020 20020022 c
  //   1600fffa 295a022 1680fff7 40800000 8c161c40 8c141c44 8c151c48 8c101c4c 8c131c50 8c041c54 8c021c58
  //   42000018
  //   OP
  //   Func
  //   rs
  //   指令字
  //   rt
  //   rd
  //   数码管输出
  //   数码管输出应该用寄存器锁存，否则显示数据只能一闪而过
  //   为方便自动评测，需要输出PC，IR，寄存器文件写入端口RDin，内存写入端口MDin等信号
  //   JMP
  //   JR
  //   OP
  //   Func
  //   Syscall
  //   Beq
  //   Bne
  //   MemToReg
  //   MemWrite
  //   AluOP
  //   AluSrcB
  //   RegWrite
  //   JAL
  //   RegDst
  //   指令存储器
  //   Reset 
  //   Reset 
  //   Reset 
endmodule

// 单周期硬布线控制器
module \单周期硬布线控制器  (
  input  [5:0] OP,
  input  [5:0] Func,
  output [3:0] ALU_OP,
  output MemToReg,
  output MemWrite,
  output ALU_SRC,
  output RegWrite,
  output SysCALL,
  output SignedExt,
  output RegDst,
  output Beq,
  output Bne,
  output JR,
  output JMP,
  output JAL
);

  \运算控制器自动生成  \u_运算控制器自动生成_1  (
    .OP0(OP[0]), .OP1(OP[1]), .OP2(OP[2]), .OP3(OP[3]), .OP4(OP[4]), .OP5(OP[5]), .F0(Func[0]), .F1(Func[1]),
    .F2(Func[2]), .F3(Func[3]), .F4(Func[4]), .F5(Func[5]), .S0(ALU_OP[0]), .S1(ALU_OP[1]), .S2(ALU_OP[2]),
    .S3(ALU_OP[3]));
  \控制信号自动生成  \u_控制信号自动生成_1  (
    .OP0(OP[0]), .OP1(OP[1]), .OP2(OP[2]), .OP3(OP[3]), .OP4(OP[4]), .OP5(OP[5]), .F0(Func[0]), .F1(Func[1]),
    .F2(Func[2]), .F3(Func[3]), .F4(Func[4]), .F5(Func[5]), .MemToReg(MemToReg), .MemWrite(MemWrite),
    .ALU_SRC(ALU_SRC), .RegWrite(RegWrite), .SysCALL(SysCALL), .SignedExt(SignedExt), .RegDst(RegDst),
    .BEQ(Beq), .BNE(Bne), .JR(JR), .JUMP(JMP), .JAL(JAL));

  // Other names for the same wires on the sheet: OP_CODE[5:0] = OP

  // Notes on the sheet:
  //   运算器控制器，根据指令生成运算器功能选择信号
  //   控制信号生成，产生数据通路需要的其他控制信号
endmodule

// 运算器控制器
module \运算控制器自动生成  (
  input  OP0,
  input  OP1,
  input  OP2,
  input  OP3,
  input  OP4,
  input  OP5,
  input  F0,
  input  F1,
  input  F2,
  input  F3,
  input  F4,
  input  F5,
  output S0,
  output S1,
  output S2,
  output S3
);

  wire and_1_out, and_2_out, and_3_out, and_4_out, and_5_out, and_6_out, and_7_out, and_8_out, and_9_out,
       and_10_out, and_11_out, and_12_out, and_13_out, and_14_out, and_15_out, and_16_out, and_17_out,
       and_18_out, and_19_out, and_20_out, and_21_out, and_22_out, and_23_out, and_24_out, and_25_out,
       and_26_out, and_27_out, and_28_out, and_29_out, and_30_out, and_31_out, and_32_out, and_33_out,
       and_34_out, and_35_out, and_36_out, and_37_out, and_38_out, and_39_out, and_40_out, and_41_out,
       and_42_out, and_43_out, and_44_out, and_45_out, and_46_out, and_47_out, and_48_out, and_49_out,
       and_50_out, and_51_out, and_52_out, not_1_out, not_2_out, not_3_out, not_4_out, not_5_out, not_6_out,
       not_7_out, not_8_out, not_9_out, not_10_out, not_11_out, not_12_out, not_13_out, not_14_out,
       not_15_out, not_16_out, not_17_out, not_18_out, not_19_out, not_20_out, not_21_out, not_22_out,
       not_23_out, not_24_out, not_25_out, not_26_out, not_27_out, not_28_out, not_29_out, not_30_out,
       not_31_out, not_32_out, not_33_out, not_34_out, not_35_out, not_36_out, not_37_out, not_38_out,
       not_39_out, not_40_out, not_41_out, not_42_out, not_43_out, not_44_out, not_45_out, not_46_out,
       not_47_out, not_48_out, not_49_out, not_50_out, not_51_out, not_52_out, not_53_out, not_54_out,
       not_55_out, not_56_out, not_57_out, not_58_out, not_59_out, not_60_out, not_61_out, not_62_out,
       not_63_out, not_64_out, not_65_out, not_66_out, not_67_out, not_68_out, not_69_out, not_70_out,
       not_71_out, not_72_out, not_73_out, not_74_out, not_75_out, not_76_out, not_77_out, not_78_out,
       not_79_out, not_80_out, not_81_out, not_82_out, not_83_out, not_84_out, not_85_out, not_86_out,
       not_87_out, not_88_out, not_89_out, not_90_out, not_91_out, not_92_out, not_93_out, not_94_out,
       not_95_out, not_96_out, not_97_out, not_98_out, not_99_out, not_100_out, not_101_out, not_102_out,
       not_103_out, not_104_out, not_105_out, not_106_out, not_107_out, not_108_out, not_109_out,
       not_110_out, not_111_out, not_112_out, not_113_out, not_114_out, not_115_out, not_116_out,
       not_117_out, not_118_out, not_119_out, not_120_out, not_121_out, not_122_out, not_123_out,
       not_124_out, not_125_out, not_126_out, not_127_out, not_128_out, not_129_out, not_130_out,
       not_131_out, not_132_out, not_133_out, not_134_out, not_135_out, not_136_out, not_137_out,
       not_138_out, not_139_out, not_140_out, not_141_out, not_142_out, not_143_out, not_144_out,
       not_145_out, not_146_out, not_147_out, not_148_out, not_149_out, not_150_out, not_151_out,
       not_152_out, not_153_out, not_154_out, not_155_out, not_156_out, not_157_out, not_158_out,
       not_159_out, not_160_out, not_161_out, not_162_out, not_163_out, not_164_out, not_165_out,
       not_166_out, not_167_out, not_168_out, not_169_out, not_170_out, not_171_out, not_172_out,
       not_173_out, not_174_out, not_175_out, not_176_out, not_177_out, not_178_out, not_179_out,
       not_180_out, not_181_out, not_182_out, not_183_out, not_184_out, not_185_out, not_186_out,
       not_187_out, not_188_out, not_189_out, not_190_out, not_191_out, not_192_out, not_193_out,
       not_194_out, not_195_out, not_196_out, not_197_out, not_198_out, not_199_out, not_200_out,
       not_201_out, not_202_out, not_203_out, not_204_out, not_205_out, not_206_out, not_207_out,
       not_208_out, not_209_out, not_210_out, not_211_out, not_212_out, not_213_out, not_214_out,
       not_215_out, not_216_out, not_217_out, not_218_out, not_219_out, not_220_out, not_221_out,
       not_222_out, not_223_out, not_224_out, not_225_out, not_226_out, not_227_out, not_228_out,
       not_229_out, not_230_out, not_231_out, not_232_out, not_233_out, not_234_out, not_235_out,
       not_236_out, not_237_out, not_238_out, not_239_out, not_240_out, not_241_out, not_242_out,
       not_243_out, not_244_out, not_245_out, not_246_out, not_247_out, not_248_out, not_249_out,
       not_250_out, not_251_out, not_252_out, not_253_out, not_254_out, not_255_out, not_256_out,
       not_257_out, not_258_out, not_259_out, not_260_out, not_261_out, not_262_out, not_263_out,
       not_264_out, not_265_out, not_266_out, not_267_out, not_268_out, not_269_out, not_270_out,
       not_271_out, not_272_out, not_273_out, not_274_out, not_275_out, not_276_out, not_277_out,
       not_278_out, not_279_out, not_280_out, not_281_out, not_282_out, not_283_out, not_284_out,
       not_285_out, not_286_out, not_287_out, not_288_out, not_289_out, not_290_out, not_291_out,
       not_292_out, not_293_out, not_294_out, not_295_out, not_296_out, not_297_out, not_298_out,
       not_299_out, not_300_out, not_301_out, not_302_out, not_303_out, not_304_out, not_305_out,
       not_306_out, not_307_out, not_308_out, not_309_out, not_310_out, not_311_out, not_312_out,
       not_313_out, not_314_out, not_315_out, not_316_out, not_317_out, not_318_out, not_319_out,
       not_320_out, not_321_out, not_322_out, not_323_out, not_324_out, not_325_out, not_326_out,
       not_327_out, not_328_out, not_329_out, not_330_out, not_331_out, not_332_out, not_333_out,
       not_334_out, not_335_out, not_336_out;

  not not_1 (not_1_out, OP5);
  not not_2 (not_2_out, OP4);
  not not_3 (not_3_out, OP3);
  not not_4 (not_4_out, OP2);
  not not_5 (not_5_out, OP1);
  not not_6 (not_6_out, OP0);
  not not_7 (not_7_out, F5);
  not not_8 (not_8_out, F4);
  not not_9 (not_9_out, F3);
  not not_10 (not_10_out, F2);
  not not_11 (not_11_out, OP5);
  not not_12 (not_12_out, OP4);
  not not_13 (not_13_out, OP3);
  not not_14 (not_14_out, OP2);
  not not_15 (not_15_out, OP1);
  not not_16 (not_16_out, OP0);
  not not_17 (not_17_out, F4);
  not not_18 (not_18_out, F3);
  not not_19 (not_19_out, F2);
  not not_20 (not_20_out, F1);
  not not_21 (not_21_out, F0);
  not not_22 (not_22_out, OP5);
  not not_23 (not_23_out, OP4);
  not not_24 (not_24_out, OP3);
  not not_25 (not_25_out, OP2);
  not not_26 (not_26_out, OP1);
  not not_27 (not_27_out, OP0);
  not not_28 (not_28_out, F4);
  not not_29 (not_29_out, F3);
  not not_30 (not_30_out, F2);
  not not_31 (not_31_out, F1);
  not not_32 (not_32_out, OP5);
  not not_33 (not_33_out, OP4);
  not not_34 (not_34_out, OP3);
  not not_35 (not_35_out, OP2);
  not not_36 (not_36_out, OP1);
  not not_37 (not_37_out, OP0);
  not not_38 (not_38_out, F4);
  not not_39 (not_39_out, F3);
  not not_40 (not_40_out, F1);
  not not_41 (not_41_out, F0);
  not not_42 (not_42_out, OP5);
  not not_43 (not_43_out, OP4);
  not not_44 (not_44_out, OP3);
  not not_45 (not_45_out, OP2);
  not not_46 (not_46_out, OP1);
  not not_47 (not_47_out, OP0);
  not not_48 (not_48_out, F4);
  not not_49 (not_49_out, F2);
  not not_50 (not_50_out, F0);
  not not_51 (not_51_out, OP5);
  not not_52 (not_52_out, OP4);
  not not_53 (not_53_out, OP3);
  not not_54 (not_54_out, OP2);
  not not_55 (not_55_out, OP1);
  not not_56 (not_56_out, OP0);
  not not_57 (not_57_out, F5);
  not not_58 (not_58_out, F4);
  not not_59 (not_59_out, F2);
  not not_60 (not_60_out, F1);
  not not_61 (not_61_out, F0);
  not not_62 (not_62_out, OP5);
  not not_63 (not_63_out, OP4);
  not not_64 (not_64_out, OP3);
  not not_65 (not_65_out, OP2);
  not not_66 (not_66_out, OP1);
  not not_67 (not_67_out, OP0);
  not not_68 (not_68_out, F5);
  not not_69 (not_69_out, F4);
  not not_70 (not_70_out, F1);
  not not_71 (not_71_out, F0);
  not not_72 (not_72_out, OP5);
  not not_73 (not_73_out, OP4);
  not not_74 (not_74_out, OP3);
  not not_75 (not_75_out, OP2);
  not not_76 (not_76_out, OP0);
  not not_77 (not_77_out, OP5);
  not not_78 (not_78_out, OP4);
  not not_79 (not_79_out, OP3);
  not not_80 (not_80_out, OP2);
  not not_81 (not_81_out, OP5);
  not not_82 (not_82_out, OP4);
  not not_83 (not_83_out, OP2);
  not not_84 (not_84_out, OP1);
  not not_85 (not_85_out, OP0);
  not not_86 (not_86_out, OP5);
  not not_87 (not_87_out, OP4);
  not not_88 (not_88_out, OP1);
  not not_89 (not_89_out, OP0);
  not not_90 (not_90_out, OP5);
  not not_91 (not_91_out, OP4);
  not not_92 (not_92_out, OP2);
  not not_93 (not_93_out, OP1);
  not not_94 (not_94_out, OP5);
  not not_95 (not_95_out, OP4);
  not not_96 (not_96_out, OP2);
  not not_97 (not_97_out, OP0);
  not not_98 (not_98_out, OP4);
  not not_99 (not_99_out, OP3);
  not not_100 (not_100_out, OP2);
  not not_101 (not_101_out, OP4);
  not not_102 (not_102_out, OP2);
  not not_103 (not_103_out, OP5);
  not not_104 (not_104_out, OP4);
  not not_105 (not_105_out, OP0);
  not not_106 (not_106_out, OP4);
  not not_107 (not_107_out, OP3);
  not not_108 (not_108_out, OP1);
  not not_109 (not_109_out, OP5);
  not not_110 (not_110_out, OP4);
  not not_111 (not_111_out, OP3);
  not not_112 (not_112_out, OP2);
  not not_113 (not_113_out, OP1);
  not not_114 (not_114_out, OP0);
  not not_115 (not_115_out, F5);
  not not_116 (not_116_out, F4);
  not not_117 (not_117_out, F3);
  not not_118 (not_118_out, F2);
  not not_119 (not_119_out, F0);
  not not_120 (not_120_out, OP5);
  not not_121 (not_121_out, OP4);
  not not_122 (not_122_out, OP3);
  not not_123 (not_123_out, OP2);
  not not_124 (not_124_out, OP1);
  not not_125 (not_125_out, OP0);
  not not_126 (not_126_out, F4);
  not not_127 (not_127_out, F3);
  not not_128 (not_128_out, F2);
  not not_129 (not_129_out, F0);
  not not_130 (not_130_out, OP5);
  not not_131 (not_131_out, OP4);
  not not_132 (not_132_out, OP3);
  not not_133 (not_133_out, OP2);
  not not_134 (not_134_out, OP1);
  not not_135 (not_135_out, OP0);
  not not_136 (not_136_out, F4);
  not not_137 (not_137_out, F3);
  not not_138 (not_138_out, F1);
  not not_139 (not_139_out, F0);
  not not_140 (not_140_out, OP5);
  not not_141 (not_141_out, OP4);
  not not_142 (not_142_out, OP3);
  not not_143 (not_143_out, OP2);
  not not_144 (not_144_out, OP1);
  not not_145 (not_145_out, OP0);
  not not_146 (not_146_out, F4);
  not not_147 (not_147_out, F3);
  not not_148 (not_148_out, OP5);
  not not_149 (not_149_out, OP4);
  not not_150 (not_150_out, OP3);
  not not_151 (not_151_out, OP2);
  not not_152 (not_152_out, OP1);
  not not_153 (not_153_out, OP0);
  not not_154 (not_154_out, F4);
  not not_155 (not_155_out, F2);
  not not_156 (not_156_out, F0);
  not not_157 (not_157_out, OP5);
  not not_158 (not_158_out, OP4);
  not not_159 (not_159_out, OP3);
  not not_160 (not_160_out, OP1);
  not not_161 (not_161_out, OP0);
  not not_162 (not_162_out, OP5);
  not not_163 (not_163_out, OP4);
  not not_164 (not_164_out, OP3);
  not not_165 (not_165_out, OP1);
  not not_166 (not_166_out, OP5);
  not not_167 (not_167_out, OP4);
  not not_168 (not_168_out, OP1);
  not not_169 (not_169_out, OP0);
  not not_170 (not_170_out, OP5);
  not not_171 (not_171_out, OP4);
  not not_172 (not_172_out, OP2);
  not not_173 (not_173_out, OP0);
  not not_174 (not_174_out, OP5);
  not not_175 (not_175_out, OP4);
  not not_176 (not_176_out, OP3);
  not not_177 (not_177_out, OP2);
  not not_178 (not_178_out, OP1);
  not not_179 (not_179_out, OP5);
  not not_180 (not_180_out, OP4);
  not not_181 (not_181_out, OP3);
  not not_182 (not_182_out, OP2);
  not not_183 (not_183_out, OP1);
  not not_184 (not_184_out, OP0);
  not not_185 (not_185_out, F4);
  not not_186 (not_186_out, F3);
  not not_187 (not_187_out, F2);
  not not_188 (not_188_out, F1);
  not not_189 (not_189_out, F0);
  not not_190 (not_190_out, OP5);
  not not_191 (not_191_out, OP4);
  not not_192 (not_192_out, OP3);
  not not_193 (not_193_out, OP2);
  not not_194 (not_194_out, OP1);
  not not_195 (not_195_out, OP0);
  not not_196 (not_196_out, F4);
  not not_197 (not_197_out, F3);
  not not_198 (not_198_out, F2);
  not not_199 (not_199_out, F1);
  not not_200 (not_200_out, OP5);
  not not_201 (not_201_out, OP4);
  not not_202 (not_202_out, OP3);
  not not_203 (not_203_out, OP2);
  not not_204 (not_204_out, OP1);
  not not_205 (not_205_out, OP0);
  not not_206 (not_206_out, F4);
  not not_207 (not_207_out, F3);
  not not_208 (not_208_out, F2);
  not not_209 (not_209_out, F0);
  not not_210 (not_210_out, OP5);
  not not_211 (not_211_out, OP4);
  not not_212 (not_212_out, OP3);
  not not_213 (not_213_out, OP2);
  not not_214 (not_214_out, OP1);
  not not_215 (not_215_out, OP0);
  not not_216 (not_216_out, F4);
  not not_217 (not_217_out, F3);
  not not_218 (not_218_out, F1);
  not not_219 (not_219_out, F0);
  not not_220 (not_220_out, OP5);
  not not_221 (not_221_out, OP4);
  not not_222 (not_222_out, OP3);
  not not_223 (not_223_out, OP2);
  not not_224 (not_224_out, OP1);
  not not_225 (not_225_out, OP0);
  not not_226 (not_226_out, F4);
  not not_227 (not_227_out, F2);
  not not_228 (not_228_out, OP5);
  not not_229 (not_229_out, OP4);
  not not_230 (not_230_out, OP3);
  not not_231 (not_231_out, OP2);
  not not_232 (not_232_out, OP1);
  not not_233 (not_233_out, OP0);
  not not_234 (not_234_out, F5);
  not not_235 (not_235_out, F4);
  not not_236 (not_236_out, F2);
  not not_237 (not_237_out, F1);
  not not_238 (not_238_out, F0);
  not not_239 (not_239_out, OP5);
  not not_240 (not_240_out, OP4);
  not not_241 (not_241_out, OP3);
  not not_242 (not_242_out, OP2);
  not not_243 (not_243_out, OP1);
  not not_244 (not_244_out, OP0);
  not not_245 (not_245_out, F5);
  not not_246 (not_246_out, F4);
  not not_247 (not_247_out, F1);
  not not_248 (not_248_out, F0);
  not not_249 (not_249_out, OP5);
  not not_250 (not_250_out, OP4);
  not not_251 (not_251_out, OP3);
  not not_252 (not_252_out, OP2);
  not not_253 (not_253_out, OP0);
  not not_254 (not_254_out, OP5);
  not not_255 (not_255_out, OP4);
  not not_256 (not_256_out, OP3);
  not not_257 (not_257_out, OP2);
  not not_258 (not_258_out, OP5);
  not not_259 (not_259_out, OP4);
  not not_260 (not_260_out, OP3);
  not not_261 (not_261_out, OP1);
  not not_262 (not_262_out, OP0);
  not not_263 (not_263_out, OP5);
  not not_264 (not_264_out, OP4);
  not not_265 (not_265_out, OP3);
  not not_266 (not_266_out, OP1);
  not not_267 (not_267_out, OP5);
  not not_268 (not_268_out, OP4);
  not not_269 (not_269_out, OP2);
  not not_270 (not_270_out, OP1);
  not not_271 (not_271_out, OP0);
  not not_272 (not_272_out, OP5);
  not not_273 (not_273_out, OP4);
  not not_274 (not_274_out, OP1);
  not not_275 (not_275_out, OP0);
  not not_276 (not_276_out, OP5);
  not not_277 (not_277_out, OP4);
  not not_278 (not_278_out, OP2);
  not not_279 (not_279_out, OP1);
  not not_280 (not_280_out, OP4);
  not not_281 (not_281_out, OP3);
  not not_282 (not_282_out, OP2);
  not not_283 (not_283_out, OP4);
  not not_284 (not_284_out, OP2);
  not not_285 (not_285_out, OP4);
  not not_286 (not_286_out, OP3);
  not not_287 (not_287_out, OP1);
  not not_288 (not_288_out, OP5);
  not not_289 (not_289_out, OP4);
  not not_290 (not_290_out, OP3);
  not not_291 (not_291_out, OP2);
  not not_292 (not_292_out, OP1);
  not not_293 (not_293_out, OP5);
  not not_294 (not_294_out, OP4);
  not not_295 (not_295_out, OP3);
  not not_296 (not_296_out, OP2);
  not not_297 (not_297_out, OP1);
  not not_298 (not_298_out, OP0);
  not not_299 (not_299_out, F4);
  not not_300 (not_300_out, F3);
  not not_301 (not_301_out, F1);
  not not_302 (not_302_out, OP5);
  not not_303 (not_303_out, OP4);
  not not_304 (not_304_out, OP3);
  not not_305 (not_305_out, OP2);
  not not_306 (not_306_out, OP1);
  not not_307 (not_307_out, OP0);
  not not_308 (not_308_out, F4);
  not not_309 (not_309_out, F3);
  not not_310 (not_310_out, OP5);
  not not_311 (not_311_out, OP4);
  not not_312 (not_312_out, OP3);
  not not_313 (not_313_out, OP2);
  not not_314 (not_314_out, OP1);
  not not_315 (not_315_out, OP0);
  not not_316 (not_316_out, F4);
  not not_317 (not_317_out, F2);
  not not_318 (not_318_out, F0);
  not not_319 (not_319_out, OP5);
  not not_320 (not_320_out, OP4);
  not not_321 (not_321_out, OP3);
  not not_322 (not_322_out, OP2);
  not not_323 (not_323_out, OP1);
  not not_324 (not_324_out, OP0);
  not not_325 (not_325_out, F4);
  not not_326 (not_326_out, F2);
  not not_327 (not_327_out, OP5);
  not not_328 (not_328_out, OP4);
  not not_329 (not_329_out, OP2);
  not not_330 (not_330_out, OP0);
  not not_331 (not_331_out, OP5);
  not not_332 (not_332_out, OP4);
  not not_333 (not_333_out, OP1);
  not not_334 (not_334_out, OP5);
  not not_335 (not_335_out, OP4);
  not not_336 (not_336_out, OP0);
  and and_1 (and_1_out, not_1_out, not_2_out, not_3_out, not_4_out, not_5_out, not_6_out, not_7_out, not_8_out, not_9_out, not_10_out, F1, F0);
  and and_2 (and_2_out, not_11_out, not_12_out, not_13_out, not_14_out, not_15_out, not_16_out, F5, not_17_out, not_18_out, not_19_out, not_20_out, not_21_out);
  and and_3 (and_3_out, not_22_out, not_23_out, not_24_out, not_25_out, not_26_out, not_27_out, F5, not_28_out, not_29_out, not_30_out, not_31_out, F0);
  and and_4 (and_4_out, not_32_out, not_33_out, not_34_out, not_35_out, not_36_out, not_37_out, F5, not_38_out, not_39_out, F2, not_40_out, not_41_out);
  and and_5 (and_5_out, not_42_out, not_43_out, not_44_out, not_45_out, not_46_out, not_47_out, F5, not_48_out, F3, not_49_out, F1, not_50_out);
  and and_6 (and_6_out, not_51_out, not_52_out, not_53_out, not_54_out, not_55_out, not_56_out, not_57_out, not_58_out, F3, not_59_out, not_60_out, not_61_out);
  and and_7 (and_7_out, not_62_out, not_63_out, not_64_out, not_65_out, not_66_out, not_67_out, not_68_out, not_69_out, F3, F2, not_70_out, not_71_out);
  and and_8 (and_8_out, not_72_out, not_73_out, not_74_out, not_75_out, OP1, not_76_out);
  and and_9 (and_9_out, not_77_out, not_78_out, not_79_out, not_80_out, OP1, OP0);
  and and_10 (and_10_out, not_81_out, not_82_out, OP3, not_83_out, not_84_out, not_85_out);
  and and_11 (and_11_out, not_86_out, not_87_out, OP3, OP2, not_88_out, not_89_out);
  and and_12 (and_12_out, not_90_out, not_91_out, OP3, not_92_out, not_93_out, OP0);
  and and_13 (and_13_out, not_94_out, not_95_out, OP3, not_96_out, OP1, not_97_out);
  and and_14 (and_14_out, OP5, not_98_out, not_99_out, not_100_out, OP1, OP0);
  and and_15 (and_15_out, OP5, not_101_out, OP3, not_102_out, OP1, OP0);
  and and_16 (and_16_out, not_103_out, not_104_out, OP3, OP2, OP1, not_105_out);
  and and_17 (and_17_out, OP5, not_106_out, not_107_out, OP2, not_108_out, OP0);
  and and_18 (and_18_out, not_109_out, not_110_out, not_111_out, not_112_out, not_113_out, not_114_out, not_115_out, not_116_out, not_117_out, not_118_out, F1, not_119_out);
  and and_19 (and_19_out, not_120_out, not_121_out, not_122_out, not_123_out, not_124_out, not_125_out, F5, not_126_out, not_127_out, not_128_out, F1, not_129_out);
  and and_20 (and_20_out, not_130_out, not_131_out, not_132_out, not_133_out, not_134_out, not_135_out, F5, not_136_out, not_137_out, F2, not_138_out, not_139_out);
  and and_21 (and_21_out, not_140_out, not_141_out, not_142_out, not_143_out, not_144_out, not_145_out, F5, not_146_out, not_147_out, F2, F1, F0);
  and and_22 (and_22_out, not_148_out, not_149_out, not_150_out, not_151_out, not_152_out, not_153_out, F5, not_154_out, F3, not_155_out, F1, not_156_out);
  and and_23 (and_23_out, not_157_out, not_158_out, not_159_out, OP2, not_160_out, not_161_out);
  and and_24 (and_24_out, not_162_out, not_163_out, not_164_out, OP2, not_165_out, OP0);
  and and_25 (and_25_out, not_166_out, not_167_out, OP3, OP2, not_168_out, not_169_out);
  and and_26 (and_26_out, not_170_out, not_171_out, OP3, not_172_out, OP1, not_173_out);
  and and_27 (and_27_out, not_174_out, not_175_out, not_176_out, not_177_out, not_178_out, OP0);
  and and_28 (and_28_out, not_179_out, not_180_out, not_181_out, not_182_out, not_183_out, not_184_out, F5, not_185_out, not_186_out, not_187_out, not_188_out, not_189_out);
  and and_29 (and_29_out, not_190_out, not_191_out, not_192_out, not_193_out, not_194_out, not_195_out, F5, not_196_out, not_197_out, not_198_out, not_199_out, F0);
  and and_30 (and_30_out, not_200_out, not_201_out, not_202_out, not_203_out, not_204_out, not_205_out, F5, not_206_out, not_207_out, not_208_out, F1, not_209_out);
  and and_31 (and_31_out, not_210_out, not_211_out, not_212_out, not_213_out, not_214_out, not_215_out, F5, not_216_out, not_217_out, F2, not_218_out, not_219_out);
  and and_32 (and_32_out, not_220_out, not_221_out, not_222_out, not_223_out, not_224_out, not_225_out, F5, not_226_out, F3, not_227_out, F1, F0);
  and and_33 (and_33_out, not_228_out, not_229_out, not_230_out, not_231_out, not_232_out, not_233_out, not_234_out, not_235_out, F3, not_236_out, not_237_out, not_238_out);
  and and_34 (and_34_out, not_239_out, not_240_out, not_241_out, not_242_out, not_243_out, not_244_out, not_245_out, not_246_out, F3, F2, not_247_out, not_248_out);
  and and_35 (and_35_out, not_249_out, not_250_out, not_251_out, not_252_out, OP1, not_253_out);
  and and_36 (and_36_out, not_254_out, not_255_out, not_256_out, not_257_out, OP1, OP0);
  and and_37 (and_37_out, not_258_out, not_259_out, not_260_out, OP2, not_261_out, not_262_out);
  and and_38 (and_38_out, not_263_out, not_264_out, not_265_out, OP2, not_266_out, OP0);
  and and_39 (and_39_out, not_267_out, not_268_out, OP3, not_269_out, not_270_out, not_271_out);
  and and_40 (and_40_out, not_272_out, not_273_out, OP3, OP2, not_274_out, not_275_out);
  and and_41 (and_41_out, not_276_out, not_277_out, OP3, not_278_out, not_279_out, OP0);
  and and_42 (and_42_out, OP5, not_280_out, not_281_out, not_282_out, OP1, OP0);
  and and_43 (and_43_out, OP5, not_283_out, OP3, not_284_out, OP1, OP0);
  and and_44 (and_44_out, OP5, not_285_out, not_286_out, OP2, not_287_out, OP0);
  and and_45 (and_45_out, not_288_out, not_289_out, not_290_out, not_291_out, not_292_out, OP0);
  and and_46 (and_46_out, not_293_out, not_294_out, not_295_out, not_296_out, not_297_out, not_298_out, F5, not_299_out, not_300_out, F2, not_301_out, F0);
  and and_47 (and_47_out, not_302_out, not_303_out, not_304_out, not_305_out, not_306_out, not_307_out, F5, not_308_out, not_309_out, F2, F1, F0);
  and and_48 (and_48_out, not_310_out, not_311_out, not_312_out, not_313_out, not_314_out, not_315_out, F5, not_316_out, F3, not_317_out, F1, not_318_out);
  and and_49 (and_49_out, not_319_out, not_320_out, not_321_out, not_322_out, not_323_out, not_324_out, F5, not_325_out, F3, not_326_out, F1, F0);
  and and_50 (and_50_out, not_327_out, not_328_out, OP3, not_329_out, OP1, not_330_out);
  and and_51 (and_51_out, not_331_out, not_332_out, OP3, OP2, not_333_out, OP0);
  and and_52 (and_52_out, not_334_out, not_335_out, OP3, OP2, OP1, not_336_out);
  or or_1 (S1, and_18_out, and_19_out, and_20_out, and_21_out, and_22_out, and_23_out, and_24_out, and_25_out, and_26_out, and_27_out);
  or or_2 (S3, and_46_out, and_47_out, and_48_out, and_49_out, and_50_out, and_51_out, and_52_out);
  or or_3 (S0, and_1_out, and_2_out, and_3_out, and_4_out, and_5_out, and_6_out, and_7_out, and_8_out, and_9_out, and_10_out, and_11_out, and_12_out, and_13_out, and_14_out, and_15_out, and_16_out, and_17_out);
  or or_4 (S2, and_28_out, and_29_out, and_30_out, and_31_out, and_32_out, and_33_out, and_34_out, and_35_out, and_36_out, and_37_out, and_38_out, and_39_out, and_40_out, and_41_out, and_42_out, and_43_out, and_44_out, and_45_out);
endmodule

// 控制信号生成
module \控制信号自动生成  (
  input  OP0,
  input  OP1,
  input  OP2,
  input  OP3,
  input  OP4,
  input  OP5,
  input  F0,
  input  F1,
  input  F2,
  input  F3,
  input  F4,
  input  F5,
  output MemToReg,
  output MemWrite,
  output ALU_SRC,
  output RegWrite,
  output SysCALL,
  output SignedExt,
  output RegDst,
  output BEQ,
  output BNE,
  output JR,
  output JUMP,
  output JAL
);

  wire and_1_out, and_2_out, and_4_out, and_5_out, and_6_out, and_7_out, and_8_out, and_9_out, and_10_out,
       and_11_out, and_12_out, and_13_out, and_14_out, and_15_out, and_16_out, and_17_out, and_19_out,
       and_20_out, and_21_out, and_22_out, and_23_out, and_24_out, and_25_out, and_26_out, and_27_out,
       and_28_out, and_29_out, and_33_out, and_34_out, and_35_out, not_1_out, not_2_out, not_3_out,
       not_4_out, not_5_out, not_6_out, not_7_out, not_8_out, not_9_out, not_10_out, not_11_out, not_12_out,
       not_13_out, not_14_out, not_15_out, not_16_out, not_17_out, not_18_out, not_19_out, not_20_out,
       not_21_out, not_22_out, not_23_out, not_24_out, not_25_out, not_26_out, not_27_out, not_28_out,
       not_29_out, not_30_out, not_31_out, not_32_out, not_33_out, not_34_out, not_35_out, not_36_out,
       not_37_out, not_38_out, not_39_out, not_40_out, not_41_out, not_42_out, not_43_out, not_44_out,
       not_45_out, not_46_out, not_47_out, not_48_out, not_49_out, not_50_out, not_51_out, not_52_out,
       not_53_out, not_54_out, not_55_out, not_56_out, not_57_out, not_58_out, not_59_out, not_60_out,
       not_61_out, not_62_out, not_63_out, not_64_out, not_65_out, not_66_out, not_67_out, not_68_out,
       not_69_out, not_70_out, not_71_out, not_72_out, not_73_out, not_74_out, not_75_out, not_76_out,
       not_77_out, not_78_out, not_79_out, not_80_out, not_81_out, not_82_out, not_83_out, not_84_out,
       not_85_out, not_86_out, not_87_out, not_88_out, not_89_out, not_90_out, not_91_out, not_92_out,
       not_93_out, not_94_out, not_95_out, not_96_out, not_97_out, not_98_out, not_99_out, not_100_out,
       not_101_out, not_102_out, not_103_out, not_104_out, not_105_out, not_106_out, not_107_out,
       not_108_out, not_109_out, not_110_out, not_111_out, not_112_out, not_113_out, not_114_out,
       not_115_out, not_116_out, not_117_out, not_118_out, not_119_out, not_120_out, not_121_out,
       not_122_out, not_123_out, not_124_out, not_125_out, not_126_out, not_127_out, not_128_out,
       not_129_out, not_130_out, not_131_out, not_132_out, not_133_out, not_134_out, not_135_out,
       not_136_out, not_137_out, not_138_out, not_139_out, not_140_out, not_141_out, not_142_out,
       not_143_out, not_144_out, not_145_out, not_146_out, not_147_out, not_148_out, not_149_out,
       not_150_out, not_151_out, not_152_out, not_153_out, not_154_out, not_155_out, not_156_out,
       not_157_out, not_158_out, not_159_out, not_160_out, not_161_out, not_162_out, not_163_out,
       not_164_out, not_165_out, not_166_out, not_167_out, not_168_out, not_169_out, not_170_out,
       not_171_out, not_172_out, not_173_out, not_174_out, not_175_out, not_176_out, not_177_out,
       not_178_out, not_179_out, not_180_out, not_181_out, not_182_out, not_183_out, not_184_out,
       not_185_out, not_186_out, not_187_out, not_188_out, not_189_out, not_190_out, not_191_out,
       not_192_out, not_193_out, not_194_out, not_195_out, not_196_out, not_197_out, not_198_out,
       not_199_out, not_200_out, not_201_out, not_202_out, not_203_out, not_204_out, not_205_out, not_206_out;

  not not_1 (not_1_out, OP1);
  not not_2 (not_2_out, OP3);
  not not_3 (not_3_out, OP4);
  not not_4 (not_4_out, OP2);
  not not_5 (not_5_out, OP3);
  not not_6 (not_6_out, OP4);
  not not_7 (not_7_out, OP2);
  not not_8 (not_8_out, OP4);
  not not_9 (not_9_out, OP0);
  not not_10 (not_10_out, OP4);
  not not_11 (not_11_out, OP5);
  not not_12 (not_12_out, OP1);
  not not_13 (not_13_out, OP4);
  not not_14 (not_14_out, OP5);
  not not_15 (not_15_out, OP1);
  not not_16 (not_16_out, OP3);
  not not_17 (not_17_out, OP4);
  not not_18 (not_18_out, OP2);
  not not_19 (not_19_out, OP4);
  not not_20 (not_20_out, OP0);
  not not_21 (not_21_out, OP1);
  not not_22 (not_22_out, OP2);
  not not_23 (not_23_out, OP4);
  not not_24 (not_24_out, OP5);
  not not_25 (not_25_out, F0);
  not not_26 (not_26_out, F1);
  not not_27 (not_27_out, F3);
  not not_28 (not_28_out, F4);
  not not_29 (not_29_out, OP0);
  not not_30 (not_30_out, OP1);
  not not_31 (not_31_out, OP2);
  not not_32 (not_32_out, OP4);
  not not_33 (not_33_out, OP5);
  not not_34 (not_34_out, F0);
  not not_35 (not_35_out, F2);
  not not_36 (not_36_out, F3);
  not not_37 (not_37_out, F4);
  not not_38 (not_38_out, OP0);
  not not_39 (not_39_out, OP1);
  not not_40 (not_40_out, OP2);
  not not_41 (not_41_out, OP4);
  not not_42 (not_42_out, OP5);
  not not_43 (not_43_out, F1);
  not not_44 (not_44_out, F3);
  not not_45 (not_45_out, F4);
  not not_46 (not_46_out, OP0);
  not not_47 (not_47_out, OP1);
  not not_48 (not_48_out, OP2);
  not not_49 (not_49_out, OP4);
  not not_50 (not_50_out, OP5);
  not not_51 (not_51_out, F2);
  not not_52 (not_52_out, F3);
  not not_53 (not_53_out, F4);
  not not_54 (not_54_out, F5);
  not not_55 (not_55_out, OP0);
  not not_56 (not_56_out, OP1);
  not not_57 (not_57_out, OP2);
  not not_58 (not_58_out, OP4);
  not not_59 (not_59_out, OP5);
  not not_60 (not_60_out, F2);
  not not_61 (not_61_out, F4);
  not not_62 (not_62_out, OP0);
  not not_63 (not_63_out, OP1);
  not not_64 (not_64_out, OP2);
  not not_65 (not_65_out, OP4);
  not not_66 (not_66_out, OP5);
  not not_67 (not_67_out, F3);
  not not_68 (not_68_out, F4);
  not not_69 (not_69_out, OP0);
  not not_70 (not_70_out, OP4);
  not not_71 (not_71_out, OP5);
  not not_72 (not_72_out, OP1);
  not not_73 (not_73_out, OP4);
  not not_74 (not_74_out, OP5);
  not not_75 (not_75_out, OP1);
  not not_76 (not_76_out, OP3);
  not not_77 (not_77_out, OP4);
  not not_78 (not_78_out, OP2);
  not not_79 (not_79_out, OP3);
  not not_80 (not_80_out, OP4);
  not not_81 (not_81_out, OP0);
  not not_82 (not_82_out, OP1);
  not not_83 (not_83_out, OP2);
  not not_84 (not_84_out, OP3);
  not not_85 (not_85_out, OP4);
  not not_86 (not_86_out, OP5);
  not not_87 (not_87_out, F0);
  not not_88 (not_88_out, F1);
  not not_89 (not_89_out, F4);
  not not_90 (not_90_out, F5);
  not not_91 (not_91_out, OP0);
  not not_92 (not_92_out, OP2);
  not not_93 (not_93_out, OP4);
  not not_94 (not_94_out, OP5);
  not not_95 (not_95_out, OP1);
  not not_96 (not_96_out, OP3);
  not not_97 (not_97_out, OP4);
  not not_98 (not_98_out, OP5);
  not not_99 (not_99_out, OP1);
  not not_100 (not_100_out, OP2);
  not not_101 (not_101_out, OP4);
  not not_102 (not_102_out, OP5);
  not not_103 (not_103_out, OP1);
  not not_104 (not_104_out, OP3);
  not not_105 (not_105_out, OP4);
  not not_106 (not_106_out, OP2);
  not not_107 (not_107_out, OP4);
  not not_108 (not_108_out, OP0);
  not not_109 (not_109_out, OP1);
  not not_110 (not_110_out, OP2);
  not not_111 (not_111_out, OP3);
  not not_112 (not_112_out, OP4);
  not not_113 (not_113_out, OP5);
  not not_114 (not_114_out, F0);
  not not_115 (not_115_out, F1);
  not not_116 (not_116_out, F4);
  not not_117 (not_117_out, F5);
  not not_118 (not_118_out, OP0);
  not not_119 (not_119_out, OP1);
  not not_120 (not_120_out, OP2);
  not not_121 (not_121_out, OP3);
  not not_122 (not_122_out, OP4);
  not not_123 (not_123_out, OP5);
  not not_124 (not_124_out, F0);
  not not_125 (not_125_out, F2);
  not not_126 (not_126_out, F3);
  not not_127 (not_127_out, F4);
  not not_128 (not_128_out, OP0);
  not not_129 (not_129_out, OP1);
  not not_130 (not_130_out, OP2);
  not not_131 (not_131_out, OP3);
  not not_132 (not_132_out, OP4);
  not not_133 (not_133_out, OP5);
  not not_134 (not_134_out, F1);
  not not_135 (not_135_out, F3);
  not not_136 (not_136_out, F4);
  not not_137 (not_137_out, OP0);
  not not_138 (not_138_out, OP1);
  not not_139 (not_139_out, OP2);
  not not_140 (not_140_out, OP3);
  not not_141 (not_141_out, OP4);
  not not_142 (not_142_out, OP5);
  not not_143 (not_143_out, F2);
  not not_144 (not_144_out, F3);
  not not_145 (not_145_out, F4);
  not not_146 (not_146_out, F5);
  not not_147 (not_147_out, OP0);
  not not_148 (not_148_out, OP1);
  not not_149 (not_149_out, OP2);
  not not_150 (not_150_out, OP3);
  not not_151 (not_151_out, OP4);
  not not_152 (not_152_out, OP5);
  not not_153 (not_153_out, F2);
  not not_154 (not_154_out, F4);
  not not_155 (not_155_out, OP0);
  not not_156 (not_156_out, OP1);
  not not_157 (not_157_out, OP2);
  not not_158 (not_158_out, OP3);
  not not_159 (not_159_out, OP4);
  not not_160 (not_160_out, OP5);
  not not_161 (not_161_out, F3);
  not not_162 (not_162_out, F4);
  not not_163 (not_163_out, OP0);
  not not_164 (not_164_out, OP1);
  not not_165 (not_165_out, OP3);
  not not_166 (not_166_out, OP4);
  not not_167 (not_167_out, OP5);
  not not_168 (not_168_out, OP1);
  not not_169 (not_169_out, OP3);
  not not_170 (not_170_out, OP4);
  not not_171 (not_171_out, OP5);
  not not_172 (not_172_out, OP0);
  not not_173 (not_173_out, OP1);
  not not_174 (not_174_out, OP2);
  not not_175 (not_175_out, OP3);
  not not_176 (not_176_out, OP4);
  not not_177 (not_177_out, OP5);
  not not_178 (not_178_out, F0);
  not not_179 (not_179_out, F1);
  not not_180 (not_180_out, F2);
  not not_181 (not_181_out, F4);
  not not_182 (not_182_out, F5);
  not not_183 (not_183_out, OP5);
  not not_184 (not_184_out, OP4);
  not not_185 (not_185_out, OP3);
  not not_186 (not_186_out, OP2);
  not not_187 (not_187_out, OP1);
  not not_188 (not_188_out, OP0);
  not not_189 (not_189_out, F5);
  not not_190 (not_190_out, F4);
  not not_191 (not_191_out, F2);
  not not_192 (not_192_out, F1);
  not not_193 (not_193_out, F0);
  not not_194 (not_194_out, OP5);
  not not_195 (not_195_out, OP4);
  not not_196 (not_196_out, OP3);
  not not_197 (not_197_out, OP2);
  not not_198 (not_198_out, OP0);
  not not_199 (not_199_out, OP5);
  not not_200 (not_200_out, OP4);
  not not_201 (not_201_out, OP3);
  not not_202 (not_202_out, OP2);
  not not_203 (not_203_out, OP2);
  not not_204 (not_204_out, OP3);
  not not_205 (not_205_out, OP4);
  not not_206 (not_206_out, OP5);
  and and_1 (and_1_out, OP0, not_1_out, OP2, not_2_out, not_3_out, OP5);
  and and_2 (and_2_out, OP0, OP1, not_4_out, not_5_out, not_6_out, OP5);
  and and_3 (MemWrite, OP0, OP1, not_7_out, OP3, not_8_out, OP5);
  and and_4 (and_4_out, not_9_out, OP3, not_10_out, not_11_out);
  and and_5 (and_5_out, not_12_out, OP3, not_13_out, not_14_out);
  and and_6 (and_6_out, OP0, not_15_out, OP2, not_16_out, not_17_out, OP5);
  and and_7 (and_7_out, OP0, OP1, not_18_out, not_19_out, OP5);
  and and_8 (and_8_out, not_20_out, not_21_out, not_22_out, not_23_out, not_24_out, not_25_out, not_26_out, not_27_out, not_28_out);
  and and_9 (and_9_out, not_29_out, not_30_out, not_31_out, not_32_out, not_33_out, not_34_out, not_35_out, not_36_out, not_37_out);
  and and_10 (and_10_out, not_38_out, not_39_out, not_40_out, not_41_out, not_42_out, not_43_out, not_44_out, not_45_out, F5);
  and and_11 (and_11_out, not_46_out, not_47_out, not_48_out, not_49_out, not_50_out, F1, not_51_out, not_52_out, not_53_out, not_54_out);
  and and_12 (and_12_out, not_55_out, not_56_out, not_57_out, not_58_out, not_59_out, F1, not_60_out, F3, not_61_out, F5);
  and and_13 (and_13_out, not_62_out, not_63_out, not_64_out, not_65_out, not_66_out, F0, F2, not_67_out, not_68_out, F5);
  and and_14 (and_14_out, not_69_out, OP3, not_70_out, not_71_out);
  and and_15 (and_15_out, not_72_out, OP3, not_73_out, not_74_out);
  and and_16 (and_16_out, OP0, not_75_out, OP2, not_76_out, not_77_out, OP5);
  and and_17 (and_17_out, OP0, OP1, not_78_out, not_79_out, not_80_out);
  and and_18 (SysCALL, not_81_out, not_82_out, not_83_out, not_84_out, not_85_out, not_86_out, not_87_out, not_88_out, F2, F3, not_89_out, not_90_out);
  and and_19 (and_19_out, not_91_out, not_92_out, OP3, not_93_out, not_94_out);
  and and_20 (and_20_out, not_95_out, OP2, not_96_out, not_97_out, not_98_out);
  and and_21 (and_21_out, OP0, not_99_out, not_100_out, not_101_out, not_102_out);
  and and_22 (and_22_out, OP0, not_103_out, OP2, not_104_out, not_105_out);
  and and_23 (and_23_out, OP0, OP1, not_106_out, not_107_out, OP5);
  and and_24 (and_24_out, not_108_out, not_109_out, not_110_out, not_111_out, not_112_out, not_113_out, not_114_out, not_115_out, not_116_out, not_117_out);
  and and_25 (and_25_out, not_118_out, not_119_out, not_120_out, not_121_out, not_122_out, not_123_out, not_124_out, not_125_out, not_126_out, not_127_out);
  and and_26 (and_26_out, not_128_out, not_129_out, not_130_out, not_131_out, not_132_out, not_133_out, not_134_out, not_135_out, not_136_out, F5);
  and and_27 (and_27_out, not_137_out, not_138_out, not_139_out, not_140_out, not_141_out, not_142_out, F1, not_143_out, not_144_out, not_145_out, not_146_out);
  and and_28 (and_28_out, not_147_out, not_148_out, not_149_out, not_150_out, not_151_out, not_152_out, F1, not_153_out, F3, not_154_out, F5);
  and and_29 (and_29_out, not_155_out, not_156_out, not_157_out, not_158_out, not_159_out, not_160_out, F0, F2, not_161_out, not_162_out, F5);
  and and_30 (BEQ, not_163_out, not_164_out, OP2, not_165_out, not_166_out, not_167_out);
  and and_31 (BNE, OP0, not_168_out, OP2, not_169_out, not_170_out, not_171_out);
  and and_32 (JR, not_172_out, not_173_out, not_174_out, not_175_out, not_176_out, not_177_out, not_178_out, not_179_out, not_180_out, F3, not_181_out, not_182_out);
  and and_33 (and_33_out, not_183_out, not_184_out, not_185_out, not_186_out, not_187_out, not_188_out, not_189_out, not_190_out, F3, not_191_out, not_192_out, not_193_out);
  and and_34 (and_34_out, not_194_out, not_195_out, not_196_out, not_197_out, OP1, not_198_out);
  and and_35 (and_35_out, not_199_out, not_200_out, not_201_out, not_202_out, OP1, OP0);
  and and_36 (JAL, OP0, OP1, not_203_out, not_204_out, not_205_out, not_206_out);
  or or_1 (MemToReg, and_1_out, and_2_out);
  or or_2 (ALU_SRC, and_4_out, and_5_out, and_6_out, and_7_out);
  or or_3 (RegWrite, and_8_out, and_9_out, and_10_out, and_11_out, and_12_out, and_13_out, and_14_out, and_15_out, and_16_out, and_17_out);
  or or_4 (SignedExt, and_19_out, and_20_out, and_21_out, and_22_out, and_23_out);
  or or_5 (RegDst, and_24_out, and_25_out, and_26_out, and_27_out, and_28_out, and_29_out);
  or or_6 (JUMP, and_33_out, and_34_out, and_35_out);
endmodule

// ALU
module MIPS_ALU (
  input  [4:0] shamt,
  input  [31:0] X,
  input  [31:0] Y,
  input  [3:0] AluOP,
  output Equal,
  output [31:0] Result,
  output [31:0] Result_2
);

  wire [0:0] comparator_1_lt, comparator_2_lt;
  wire [31:0] adder_1_out, AND_out, divider_1_out, divider_1_rem, multiplier_1_cout, multiplier_1_out,
       NOR_out, OR_out, shifter_1_out, shifter_2_out, shifter_3_out, subtractor_1_out, XOR_out;

  assign AND_out = X & Y;  // AND_Gate AND, 32 bits wide
  assign OR_out = X | Y;  // OR_Gate OR, 32 bits wide
  Shifter #(.width(32), .shift("ll")) shifter_1 (.in(Y), .\dist (shamt), .out(shifter_1_out));
  Shifter #(.width(32), .shift("ar")) shifter_2 (.in(Y), .\dist (shamt), .out(shifter_2_out));
  Shifter #(.width(32), .shift("lr")) shifter_3 (.in(Y), .\dist (shamt), .out(shifter_3_out));
  Multiplier #(.width(32)) multiplier_1 (.a(X), .b(Y), .out(multiplier_1_out), .cout(multiplier_1_cout));  // open: cin
  Divider #(.width(32)) divider_1 (.a(X), .b(Y), .out(divider_1_out), .rem(divider_1_rem));  // open: upper
  Adder #(.width(32)) adder_1 (.a(X), .b(Y), .out(adder_1_out));  // open: cin, cout
  Subtractor #(.width(32)) subtractor_1 (.a(X), .b(Y), .out(subtractor_1_out));  // open: bin, bout
  assign XOR_out = X ^ Y;  // XOR_Gate XOR, 32 bits wide
  assign NOR_out = ~(X | Y);  // NOR_Gate NOR, 32 bits wide
  Comparator #(.width(32), .mode("twosComplement")) comparator_1 (
    .a(X), .b(Y), .eq(Equal), .lt(comparator_1_lt[0]));  // open: gt
  Comparator #(.width(32), .mode("unsigned")) comparator_2 (.a(X), .b(Y), .lt(comparator_2_lt[0]));  // open: gt, eq
  Multiplexer #(.select(4), .width(32), .disabled("Z"), .enable("false")) multiplexer_1 (
    .in0(shifter_1_out), .in1(shifter_2_out), .in2(shifter_3_out), .in3(multiplier_1_out),
    .in4(divider_1_out), .in5(adder_1_out), .in6(subtractor_1_out), .in7(AND_out), .in8(OR_out),
    .in9(XOR_out), .in10(NOR_out), .in11({{31{1'b0}}, comparator_1_lt[0]}),
    .in12({{31{1'b0}}, comparator_2_lt[0]}), .in13({32{1'b0}}), .in14({32{1'b0}}), .in15({32{1'b0}}),
    .out(Result), .sel(AluOP));
  Multiplexer #(.select(4), .width(32), .disabled("Z"), .enable("false")) multiplexer_2 (
    .in0({32{1'b0}}), .in1({32{1'b0}}), .in2({32{1'b0}}), .in3(multiplier_1_cout), .in4(divider_1_rem),
    .in5({32{1'b0}}), .in6({32{1'b0}}), .in7({32{1'b0}}), .in8({32{1'b0}}), .in9({32{1'b0}}),
    .in10({32{1'b0}}), .in11({32{1'b0}}), .in12({32{1'b0}}), .in13({32{1'b0}}), .in14({32{1'b0}}),
    .in15({32{1'b0}}), .out(Result_2), .sel(AluOP));

  // Other names for the same wires on the sheet: Result2[31:0] = Result_2; S[3:0] = AluOP

  // Notes on the sheet:
  //   不要改变此引脚区域内容，也不要改变ALU封装形式
  //   输入引脚
  //   输出引脚
endmodule

module MIPS_Regifile (
  input  [31:0] Din,
  input  Clk,
  input  WE,
  input  [4:0] R1_num,
  input  [4:0] W_num,
  input  [4:0] R2_num,
  output [31:0] R1,
  output [31:0] R2
);

  // RegisterFile registerfile_1: pin names not known; wires that end beside it: Din, Clk, WE, W_num, R1_num, R2_num, R1, R2
endmodule

module \理想流水线  (
  output RegWrite,
  output MemWrite,
  output [31:0] IF_PC,
  output [31:0] ID_PC,
  output [31:0] EX_PC,
  output [31:0] M_PC,
  output [31:0] WB_PC,
  output [31:0] RDin,
  output [31:0] MDin,
  output [31:0] LedData
);

  wire and_1_out, and_2_out, and_3_out, and_4_out, and_5_out, and_6_out, CLK, comparator_1_eq,
       comparator_2_eq, END, ex_mem_1_out_20, ex_mem_1_out_21, ex_mem_1_out_22, ex_mem_1_out_23,
       ex_mem_1_out_24, Go, id_ex_1_out_35, id_ex_1_out_36, id_ex_1_out_37, id_ex_1_out_38, id_ex_1_out_39,
       id_ex_1_out_40, id_ex_1_out_41, id_ex_1_out_42, id_ex_1_out_43, id_ex_1_out_44, id_ex_1_out_46, IR1,
       IR2, IR3, mem_wb_1_p13, mem_wb_1_p14, mem_wb_1_p15, mem_wb_1_p21, mips_alu_1_equal, nand_1_out,
       not_1_out, not_2_out, or_1_out, or_2_out, or_3_out, or_4_out, RST, SignedExt, syscall, W1, W2, W3,
       \单周期硬布线控制器_1_alu_src , \单周期硬布线控制器_1_beq , \单周期硬布线控制器_1_bne , \单周期硬布线控制器_1_jal , \单周期硬布线控制器_1_jmp ,
       \单周期硬布线控制器_1_jr , \单周期硬布线控制器_1_memtoreg , \单周期硬布线控制器_1_memwrite , \单周期硬布线控制器_1_regdst ,
       \单周期硬布线控制器_1_regwrite ;
  wire [3:0] adder_2_out, id_ex_1_out_45, \单周期硬布线控制器_1_alu_op ;
  wire [4:0] id_ex_1_out_30_2, multiplexer_5_out, multiplexer_6_out, multiplexer_7_out, multiplexer_8_out;
  wire [15:0] \LoadUse次数 , \总周期数 , \插入气泡数 , \无条件分支数 , \条件分支成功数 ;
  wire [26:0] id_ex_1_out_30;
  wire [27:0] adder_2_out_2;
  wire [31:0] adder_1_out, adder_3_out, adder_4_out, bit_extender_1_out, bit_extender_2_out, ex_mem_1_out_14,
       ex_mem_1_out_17, id_ex_1_out_28, id_ex_1_out_32, id_ex_1_out_33, id_ex_1_out_34, if_id_1_out_9, IR,
       mem_wb_1_p17, mem_wb_1_p19, mem_wb_1_p20, mem_wb_1_p22, mips_alu_1_result, mips_regifile_1_r1,
       mips_regifile_1_r2, multiplexer_1_out, multiplexer_2_out, multiplexer_3_out, multiplexer_4_out,
       multiplexer_9_out, multiplexer_10_out, ram_1_data, shifter_1_out;

  Button \u_总复位  (.out(RST));
  Button _1 (.out(IR1));
  Button _2 (.out(IR2));
  Button _3 (.out(IR3));
  Register #(.width(32), .trigger("rising"), .Select("low")) PC (
    .D(multiplexer_1_out), .en(and_1_out), .Q(IF_PC), .clk(CLK), .clr(RST));
  Multiplexer #(.select(1), .width(32), .disabled("Z"), .enable("false")) multiplexer_1 (
    .in0(multiplexer_2_out), .in1(id_ex_1_out_32), .out(multiplexer_1_out), .sel(id_ex_1_out_36));
  Button \u_继续运行  (.out(Go));
  LED #(.active("true")) led_1 (.in(W1));
  LED #(.active("true")) led_2 (.in(W2));
  LED #(.active("true")) led_3 (.in(W3));
  Multiplexer #(.select(1), .width(32), .disabled("Z"), .enable("false")) multiplexer_2 (
    .in0(multiplexer_3_out),
    .in1({adder_2_out, id_ex_1_out_30[20:6], id_ex_1_out_30_2, id_ex_1_out_30[5:0], 2'b00}),
    .out(multiplexer_2_out), .sel(or_1_out));
  or or_1 (or_1_out, id_ex_1_out_35, id_ex_1_out_37);
  Hex_Digit_Display hex_digit_display_1 (.value(LedData[31:28]));  // open: dp
  ROM #(.addrWidth(10), .dataWidth(32), .Select("high")) rom_1 (.addr(IF_PC[11:2]), .data(IR));
  Adder #(.width(32)) adder_1 (.a(IF_PC), .b(32'h4), .out(adder_1_out));  // open: cin, cout
  Multiplexer #(.select(1), .width(32), .disabled("Z"), .enable("false")) multiplexer_3 (
    .in0(adder_1_out), .in1(adder_3_out), .out(multiplexer_3_out), .sel(or_4_out));
  and and_1 (and_1_out, ~END, nand_1_out);  // AND_Gate
  Hex_Digit_Display hex_digit_display_2 (.value(LedData[27:24]));  // open: dp
  Hex_Digit_Display hex_digit_display_3 (.value(LedData[23:20]));  // open: dp
  Hex_Digit_Display hex_digit_display_4 (.value(LedData[19:16]));  // open: dp
  Hex_Digit_Display hex_digit_display_5 (.value(LedData[15:12]));  // open: dp
  IF_ID if_id_1 (
    .CLK(CLK), .out_9(if_id_1_out_9), .\使能端_低电平有效_stall_高电平有效 (and_1_out), .in_5(IF_PC), .out_11(ID_PC),
    .in_1(IR));  // open: 传输状态Out_表明当前传输数据有效, 同步清零_气泡_高电平有效, in_6, out_12, in_7, out_13, in_8, out_14
  Hex_Digit_Display hex_digit_display_6 (.value(LedData[7:4]));  // open: dp
  Hex_Digit_Display hex_digit_display_7 (.value(LedData[11:8]));  // open: dp
  Clock #(.highDuration(1), .lowDuration(1)) clock_1 (.out(CLK));
  assign bit_extender_1_out = {{16{if_id_1_out_9[15]}}, if_id_1_out_9[15:0]};  // Bit_Extender bit_extender_1
  assign bit_extender_2_out = {{16{1'b0}}, if_id_1_out_9[15:0]};  // Bit_Extender bit_extender_2
  or or_2 (or_2_out, nand_1_out, mem_wb_1_p21);
  Hex_Digit_Display hex_digit_display_8 (.value(LedData[3:0]));  // open: dp
  Shifter #(.width(32), .shift("ll")) shifter_1 (.in(bit_extender_1_out), .\dist (5'b00010), .out(shifter_1_out));
  Multiplexer #(.select(1), .width(32), .disabled("Z"), .enable("false")) multiplexer_4 (
    .in0(bit_extender_2_out), .in1(bit_extender_1_out), .out(multiplexer_4_out), .sel(SignedExt));
  Multiplexer #(.select(1), .width(5), .disabled("Z"), .enable("false")) multiplexer_5 (
    .in0(multiplexer_6_out), .in1({5{1'b1}}), .out(multiplexer_5_out), .sel(mem_wb_1_p14));
  Multiplexer #(.select(1), .width(5), .disabled("Z"), .enable("false")) multiplexer_6 (
    .in0(mem_wb_1_p17[20:16]), .in1(mem_wb_1_p17[15:11]), .out(multiplexer_6_out), .sel(mem_wb_1_p13));
  and and_2 (and_2_out, ~END, or_2_out);  // AND_Gate
  // Probe on \总周期数 
  // Probe on \无条件分支数 
  // Probe on \条件分支成功数 
  // Probe on \插入气泡数 
  // Probe on \LoadUse次数 
  \单周期硬布线控制器  \u_单周期硬布线控制器_1  (
    .Func(if_id_1_out_9[5:0]), .OP(if_id_1_out_9[31:26]), .ALU_OP(\单周期硬布线控制器_1_alu_op ),
    .MemToReg(\单周期硬布线控制器_1_memtoreg ), .MemWrite(\单周期硬布线控制器_1_memwrite ), .ALU_SRC(\单周期硬布线控制器_1_alu_src ),
    .RegWrite(\单周期硬布线控制器_1_regwrite ), .SysCALL(syscall), .SignedExt(SignedExt),
    .RegDst(\单周期硬布线控制器_1_regdst ), .JR(\单周期硬布线控制器_1_jr ), .JMP(\单周期硬布线控制器_1_jmp ), .Beq(\单周期硬布线控制器_1_beq ),
    .JAL(\单周期硬布线控制器_1_jal ), .Bne(\单周期硬布线控制器_1_bne ));
  Multiplexer #(.select(1), .width(5), .disabled("Z"), .enable("false")) multiplexer_7 (
    .in0(if_id_1_out_9[25:21]), .in1(5'b00100), .out(multiplexer_7_out), .sel(syscall));
  Multiplexer #(.select(1), .width(5), .disabled("Z"), .enable("false")) multiplexer_8 (
    .in0(if_id_1_out_9[20:16]), .in1(5'b00010), .out(multiplexer_8_out), .sel(syscall));
  Comparator #(.width(32), .mode("twosComplement")) comparator_1 (
    .a(id_ex_1_out_33), .b(32'h22), .eq(comparator_1_eq));  // open: gt, lt
  Comparator #(.width(32), .mode("twosComplement")) comparator_2 (
    .a(mem_wb_1_p22), .b(32'h22), .eq(comparator_2_eq));  // open: gt, lt
  Counter #(.width(16), .max('hffff), .ongoal("wrap"), .trigger("rising"), .behavior("old")) counter_1 (
    .count(and_2_out), .Q(\总周期数 ), .clk(CLK), .clr(RST));  // open: load, D, carry, preset
  // Probe on IF_PC[11:0]
  MIPS_Regifile mips_regifile_1 (
    .Din(RDin), .Clk(CLK), .R1(mips_regifile_1_r1), .R2(mips_regifile_1_r2), .WE(RegWrite),
    .W_num(multiplexer_5_out), .R1_num(multiplexer_7_out), .R2_num(multiplexer_8_out));
  and and_3 (and_3_out, comparator_1_eq, syscall);
  and and_4 (and_4_out, mem_wb_1_p21, ~comparator_2_eq);  // AND_Gate
  // Probe on EX_PC[11:0]
  // Probe on ID_PC[11:0]
  not not_1 (not_1_out, END);
  Register #(.width(32), .trigger("rising"), .Select("low")) register_1 (
    .D(id_ex_1_out_32), .en(and_3_out), .Q(LedData), .clk(CLK), .clr(RST));
  nand nand_1 (nand_1_out, and_4_out, ~Go);  // NAND_Gate
  // Probe on M_PC[11:0]
  ID_EX id_ex_1 (
    .CLK(CLK), .in_6(if_id_1_out_9), .in_7(ID_PC), .in_8(mips_regifile_1_r1), .in_9(mips_regifile_1_r2),
    .in_11(\单周期硬布线控制器_1_jmp ), .in_12(\单周期硬布线控制器_1_jr ), .in_13(\单周期硬布线控制器_1_jal ),
    .in_14(\单周期硬布线控制器_1_alu_src ), .in_15(\单周期硬布线控制器_1_bne ), .in_16(\单周期硬布线控制器_1_beq ),
    .in_17(\单周期硬布线控制器_1_memwrite ), .in_18(\单周期硬布线控制器_1_regwrite ), .in_19(\单周期硬布线控制器_1_memtoreg ),
    .in_21(\单周期硬布线控制器_1_alu_op ), .out_28(id_ex_1_out_28),
    .out_30({id_ex_1_out_30[26:6], id_ex_1_out_30_2, id_ex_1_out_30[5:0]}), .out_31(EX_PC),
    .out_32(id_ex_1_out_32), .out_33(id_ex_1_out_33), .out_35(id_ex_1_out_35), .out_36(id_ex_1_out_36),
    .out_37(id_ex_1_out_37), .out_38(id_ex_1_out_38), .out_39(id_ex_1_out_39), .out_40(id_ex_1_out_40),
    .out_41(id_ex_1_out_41), .out_42(id_ex_1_out_42), .out_43(id_ex_1_out_43), .out_45(id_ex_1_out_45),
    .\使能端_低电平有效_stall_高电平有效 (not_1_out), .in_1(multiplexer_4_out), .in_20(\单周期硬布线控制器_1_regdst ),
    .out_44(id_ex_1_out_44), .in_10(shifter_1_out), .out_34(id_ex_1_out_34), .in_22(syscall),
    .out_46(id_ex_1_out_46));  // open: 传输状态Out_表明当前传输数据有效, 同步清零_气泡_高电平有效, in_23, out_47, in_24, out_48, 异步清零, in_25, out_49, in_26, out_50, in_27, out_51
  // Probe on WB_PC[11:0]
  Adder #(.width(32)) adder_2 (.a(EX_PC), .b(32'h4), .out({adder_2_out, adder_2_out_2}));  // open: cin, cout
  or or_3 (or_3_out, id_ex_1_out_36, or_1_out);
  Multiplexer #(.select(1), .width(32), .disabled("Z"), .enable("false")) multiplexer_9 (
    .in0(id_ex_1_out_33), .in1(id_ex_1_out_28), .out(multiplexer_9_out), .sel(id_ex_1_out_38));
  Adder #(.width(32)) adder_3 (
    .a({adder_2_out, adder_2_out_2}), .b(id_ex_1_out_34), .out(adder_3_out));  // open: cin, cout
  and and_5 (and_5_out, mips_alu_1_equal, id_ex_1_out_40);
  and and_6 (and_6_out, id_ex_1_out_39, ~mips_alu_1_equal);  // AND_Gate
  MIPS_ALU mips_alu_1 (
    .X(id_ex_1_out_32), .Y(multiplexer_9_out), .AluOP(id_ex_1_out_45), .Equal(mips_alu_1_equal),
    .Result(mips_alu_1_result), .shamt(id_ex_1_out_30_2));  // open: Result_2
  Counter #(.width(16), .max('hffff), .ongoal("wrap"), .trigger("rising"), .behavior("old")) counter_2 (
    .count(or_4_out), .Q(\条件分支成功数 ), .clk(CLK), .clr(RST));  // open: load, D, carry, preset
  Counter #(.width(16), .max('hffff), .ongoal("wrap"), .trigger("rising"), .behavior("old")) counter_3 (
    .count(or_3_out), .Q(\无条件分支数 ), .clk(CLK), .clr(RST));  // open: load, D, carry, preset
  or or_4 (or_4_out, and_5_out, and_6_out);
  EX_MEM ex_mem_1 (
    .in_1({id_ex_1_out_30[26:6], id_ex_1_out_30_2, id_ex_1_out_30[5:0]}), .CLK(CLK), .in_4(EX_PC),
    .in_5(mips_alu_1_result), .in_6(id_ex_1_out_33), .in_7(id_ex_1_out_41), .in_8(id_ex_1_out_42),
    .in_9(id_ex_1_out_43), .in_10(id_ex_1_out_44), .out_14(ex_mem_1_out_14), .out_16(M_PC),
    .out_17(ex_mem_1_out_17), .out_18(MDin), .out_19(MemWrite), .out_20(ex_mem_1_out_20),
    .out_21(ex_mem_1_out_21), .out_22(ex_mem_1_out_22), .\使能端_低电平有效_stall_高电平有效 (not_1_out),
    .in_11(id_ex_1_out_37), .out_23(ex_mem_1_out_23), .in_13(id_ex_1_out_46), .out_24(ex_mem_1_out_24));  // open: 传输状态Out_表明当前传输数据有效, 同步清零_气泡_高电平有效
  not not_2 (not_2_out, MemWrite);
  RAM #(.addrWidth(10), .dataWidth(32), .bus("separate"), .Select("high")) ram_1 (
    .addr(ex_mem_1_out_17[11:2]), .din(MDin), .data(ram_1_data), .str(MemWrite), .clk(CLK), .ld(not_2_out),
    .clr(RST));  // open: sel
  // MEM_WB mem_wb_1: pin names not known; wires that end beside it: ex_mem_1_out_22, ex_mem_1_out_23, ex_mem_1_out_21, ex_mem_1_out_20, ex_mem_1_out_14, M_PC, ex_mem_1_out_17, ram_1_data, ex_mem_1_out_24, MDin, not_1_out, CLK, mem_wb_1_p13, mem_wb_1_p14, mem_wb_1_p15, RegWrite, mem_wb_1_p17, WB_PC, mem_wb_1_p19, mem_wb_1_p20, mem_wb_1_p21, mem_wb_1_p22
  Multiplexer #(.select(1), .width(32), .disabled("Z"), .enable("false")) multiplexer_10 (
    .in0(mem_wb_1_p19), .in1(mem_wb_1_p20), .out(multiplexer_10_out), .sel(mem_wb_1_p15));
  Multiplexer #(.select(1), .width(32), .disabled("Z"), .enable("false")) multiplexer_11 (
    .in0(multiplexer_10_out), .in1(adder_4_out), .out(RDin), .sel(mem_wb_1_p14));
  Adder #(.width(32)) adder_4 (.a(WB_PC), .b(32'h4), .out(adder_4_out));  // open: cin, cout
  Comparator #(.width(16), .mode("twosComplement")) comparator_3 (.a(16'h15), .b(\总周期数 ), .eq(END));  // open: gt, lt

  // Other names for the same wires on the sheet: MEM_PC[31:0] = M_PC

  // Notes on the sheet:
  //   中断源
  //   中断等待指示
  //   指令存储器
  //   contents of rom_1 (hex, n*v repeats v):
  //   20100000 20110000 20120000 20130000 36100000 36310001 36520002 36730003 ae100000 ae110004 ae120008
  //   ae13000c 2002000a 20110000 20120000 20130000 c
  //   指令字
  //   数码管输出
  //   OP
  //   rs
  //   rd
  //   Func
  //   rt
  //   JR
  //   Beq
  //   JMP
  //   Bne
  //   OP
  //   JAL
  //   Func
  //   Syscall
  //   MemToReg
  //   MemWrite
  //   AluOP
  //   AluSrcB
  //   RegWrite
  //   RegDst
  //   流水调试日志用
  //   为方便自动评测，需要输出流水线各段保存的PC值，注意是PC不是PC+4，另外ID段寄存器写入信息，Mem段内存写入信息也要输出
  //   OP
  //   rs
  //   rt
  //   rd
endmodule

module \分支相关流水线  (
  output RegWrite,
  output MemWrite,
  output [31:0] PC,
  output [31:0] IR,
  output [31:0] RDin,
  output [31:0] MDin
);

  wire and_1_out, and_2_out, and_3_out, and_4_out, CLK, comparator_1_eq, ex_mem_1_out_20, ex_mem_1_out_21,
       ex_mem_1_out_22, ex_mem_1_out_23, \ex_mem_1_传输状态out_表明当前传输数据有效 , Go, id_ex_1_out_35, id_ex_1_out_36,
       id_ex_1_out_37, id_ex_1_out_38, id_ex_1_out_39, id_ex_1_out_40, id_ex_1_out_41, id_ex_1_out_42,
       id_ex_1_out_43, id_ex_1_out_44, \id_ex_1_传输状态out_表明当前传输数据有效 , \if_id_1_传输状态out_表明当前传输数据有效 , IR1, IR2,
       IR3, mem_wb_1_out_19, mem_wb_1_out_20, mem_wb_1_out_21, \mem_wb_1_传输状态out_表明当前传输数据有效 ,
       mips_alu_1_equal, nand_1_out, not_1_out, or_1_out, or_2_out, or_3_out, RST, SignedExt, syscall, W1,
       W2, W3, \单周期硬布线控制器_1_alu_src , \单周期硬布线控制器_1_beq , \单周期硬布线控制器_1_bne , \单周期硬布线控制器_1_jal ,
       \单周期硬布线控制器_1_jmp , \单周期硬布线控制器_1_jr , \单周期硬布线控制器_1_memtoreg , \单周期硬布线控制器_1_memwrite ,
       \单周期硬布线控制器_1_regdst , \单周期硬布线控制器_1_regwrite ;
  wire [3:0] id_ex_1_out_45, \单周期硬布线控制器_1_alu_op ;
  wire [4:0] multiplexer_4_out, multiplexer_5_out, multiplexer_6_out, multiplexer_8_out;
  wire [15:0] \总周期数 , \无条件分支数 , \条件分支成功数 ;
  wire [26:21] id_ex_1_out_30_2;
  wire [27:0] adder_2_out;
  wire [31:0] adder_1_out, adder_3_out, adder_4_out, bit_extender_1_out, bit_extender_2_out, ex_mem_1_out_14,
       ex_mem_1_out_16, ex_mem_1_out_17, id_ex_1_out_28, id_ex_1_out_31, id_ex_1_out_32, id_ex_1_out_33,
       id_ex_1_out_34, if_id_1_out_9, if_id_1_out_11, LedData, mem_wb_1_out_13, mem_wb_1_out_15,
       mem_wb_1_out_16, mem_wb_1_out_17, mips_alu_1_result, mips_regifile_1_r1, mips_regifile_1_r2,
       multiplexer_1_out, multiplexer_2_out, multiplexer_3_out, multiplexer_7_out, multiplexer_9_out,
       multiplexer_10_out, ram_1_data, shifter_1_out;
  wire [31:2] id_ex_1_out_30;

  Clock #(.highDuration(1), .lowDuration(1)) clock_1 (.out(CLK));
  Button _1 (.out(IR1));
  Button _2 (.out(IR2));
  Button _3 (.out(IR3));
  Button \u_总复位  (.out(RST));
  Register #(.width(32), .trigger("rising"), .Select("low")) u_PC (
    .D(multiplexer_1_out), .en(nand_1_out), .Q(PC), .clk(CLK), .clr(RST));
  Multiplexer #(.select(1), .width(32), .disabled("Z"), .enable("false")) multiplexer_1 (
    .in0(multiplexer_3_out), .in1(multiplexer_2_out), .out(multiplexer_1_out), .sel(id_ex_1_out_35));
  Multiplexer #(.select(1), .width(32), .disabled("Z"), .enable("false")) multiplexer_2 (
    .in0({id_ex_1_out_30, 2'b00}), .in1(id_ex_1_out_32), .out(multiplexer_2_out), .sel(id_ex_1_out_36));
  Button \u_继续运行  (.out(Go));
  LED #(.active("true")) led_1 (.in(W1));
  LED #(.active("true")) led_2 (.in(W2));
  LED #(.active("true")) led_3 (.in(W3));
  Hex_Digit_Display hex_digit_display_1 (.value(LedData[31:28]));  // open: dp
  Adder #(.width(32)) adder_1 (.a(PC), .b(32'h4), .out(adder_1_out));  // open: cin, cout
  Multiplexer #(.select(1), .width(32), .disabled("Z"), .enable("false")) multiplexer_3 (
    .in0(adder_1_out), .in1(adder_3_out), .out(multiplexer_3_out), .sel(or_3_out));
  Hex_Digit_Display hex_digit_display_2 (.value(LedData[27:24]));  // open: dp
  Hex_Digit_Display hex_digit_display_3 (.value(LedData[23:20]));  // open: dp
  ROM #(.addrWidth(10), .dataWidth(32), .Select("high")) rom_1 (.addr(PC[11:2]), .data(IR));
  Hex_Digit_Display hex_digit_display_4 (.value(LedData[15:12]));  // open: dp
  Hex_Digit_Display hex_digit_display_5 (.value(LedData[19:16]));  // open: dp
  IF_ID if_id_1 (
    .CLK(CLK), .out_9(if_id_1_out_9), .\传输状态Out_表明当前传输数据有效 (\if_id_1_传输状态out_表明当前传输数据有效 ),
    .\同步清零_气泡_高电平有效 (or_2_out), .\使能端_低电平有效_stall_高电平有效 (nand_1_out), .in_5(PC), .out_11(if_id_1_out_11),
    .in_1(IR));  // open: in_6, out_12, in_7, out_13, in_8, out_14
  Hex_Digit_Display hex_digit_display_6 (.value(LedData[7:4]));  // open: dp
  Hex_Digit_Display hex_digit_display_7 (.value(LedData[11:8]));  // open: dp
  Hex_Digit_Display hex_digit_display_8 (.value(LedData[3:0]));  // open: dp
  // Probe on \总周期数 
  Multiplexer #(.select(1), .width(5), .disabled("Z"), .enable("false")) multiplexer_4 (
    .in0(if_id_1_out_9[25:21]), .in1(5'b00010), .out(multiplexer_4_out), .sel(syscall));
  Multiplexer #(.select(1), .width(5), .disabled("Z"), .enable("false")) multiplexer_5 (
    .in0(if_id_1_out_9[20:16]), .in1(5'b00100), .out(multiplexer_5_out), .sel(syscall));
  Multiplexer #(.select(1), .width(5), .disabled("Z"), .enable("false")) multiplexer_6 (
    .in0(mem_wb_1_out_13[20:16]), .in1(mem_wb_1_out_13[15:11]), .out(multiplexer_6_out), .sel(mem_wb_1_out_20));
  assign bit_extender_1_out = {{16{if_id_1_out_9[15]}}, if_id_1_out_9[15:0]};  // Bit_Extender bit_extender_1
  assign bit_extender_2_out = {{16{1'b0}}, if_id_1_out_9[15:0]};  // Bit_Extender bit_extender_2
  Multiplexer #(.select(1), .width(32), .disabled("Z"), .enable("false")) multiplexer_7 (
    .in0(bit_extender_2_out), .in1(bit_extender_1_out), .out(multiplexer_7_out), .sel(SignedExt));
  Multiplexer #(.select(1), .width(5), .disabled("Z"), .enable("false")) multiplexer_8 (
    .in0(multiplexer_6_out), .in1({5{1'b1}}), .out(multiplexer_8_out), .sel(mem_wb_1_out_21));
  Shifter #(.width(32), .shift("ll")) shifter_1 (.in(multiplexer_7_out), .\dist (5'b00010), .out(shifter_1_out));
  or or_1 (or_1_out, nand_1_out, \mem_wb_1_传输状态out_表明当前传输数据有效 );
  \单周期硬布线控制器  \u_单周期硬布线控制器_1  (
    .Func(if_id_1_out_9[5:0]), .OP(if_id_1_out_9[31:26]), .ALU_OP(\单周期硬布线控制器_1_alu_op ),
    .MemToReg(\单周期硬布线控制器_1_memtoreg ), .MemWrite(\单周期硬布线控制器_1_memwrite ), .ALU_SRC(\单周期硬布线控制器_1_alu_src ),
    .RegWrite(\单周期硬布线控制器_1_regwrite ), .SysCALL(syscall), .SignedExt(SignedExt),
    .RegDst(\单周期硬布线控制器_1_regdst ), .JR(\单周期硬布线控制器_1_jr ), .JMP(\单周期硬布线控制器_1_jmp ), .Beq(\单周期硬布线控制器_1_beq ),
    .JAL(\单周期硬布线控制器_1_jal ), .Bne(\单周期硬布线控制器_1_bne ));
  Comparator #(.width(32), .mode("twosComplement")) comparator_1 (
    .a(mips_regifile_1_r1), .b(32'h22), .eq(comparator_1_eq));  // open: gt, lt
  Counter #(.width(16), .max('hffff), .ongoal("wrap"), .trigger("rising"), .behavior("old")) counter_1 (
    .count(or_1_out), .Q(\总周期数 ), .clk(CLK), .clr(RST));  // open: load, D, carry, preset
  MIPS_Regifile mips_regifile_1 (
    .Din(RDin), .Clk(CLK), .R1(mips_regifile_1_r1), .R2(mips_regifile_1_r2), .WE(RegWrite),
    .W_num(multiplexer_8_out), .R1_num(multiplexer_4_out), .R2_num(multiplexer_5_out));
  and and_1 (and_1_out, comparator_1_eq, syscall);
  and and_2 (and_2_out, syscall, ~comparator_1_eq);  // AND_Gate
  nand nand_1 (nand_1_out, and_2_out, ~Go);  // NAND_Gate
  ID_EX id_ex_1 (
    .CLK(CLK), .in_6(if_id_1_out_9), .in_7(if_id_1_out_11), .in_8(mips_regifile_1_r1),
    .in_9(mips_regifile_1_r2), .in_11(\单周期硬布线控制器_1_jmp ), .in_12(\单周期硬布线控制器_1_jr ),
    .in_13(\单周期硬布线控制器_1_jal ), .in_14(\单周期硬布线控制器_1_alu_src ), .in_15(\单周期硬布线控制器_1_bne ),
    .in_16(\单周期硬布线控制器_1_beq ), .in_17(\单周期硬布线控制器_1_memwrite ), .in_18(\单周期硬布线控制器_1_regwrite ),
    .in_19(\单周期硬布线控制器_1_memtoreg ), .in_21(\单周期硬布线控制器_1_alu_op ), .out_28(id_ex_1_out_28),
    .\传输状态Out_表明当前传输数据有效 (\id_ex_1_传输状态out_表明当前传输数据有效 ), .out_30({id_ex_1_out_30_2, id_ex_1_out_30[27:2]}),
    .out_31(id_ex_1_out_31), .out_32(id_ex_1_out_32), .out_33(id_ex_1_out_33), .out_35(id_ex_1_out_35),
    .out_36(id_ex_1_out_36), .out_37(id_ex_1_out_37), .out_38(id_ex_1_out_38), .out_39(id_ex_1_out_39),
    .out_40(id_ex_1_out_40), .out_41(id_ex_1_out_41), .out_42(id_ex_1_out_42), .out_43(id_ex_1_out_43),
    .out_45(id_ex_1_out_45), .\同步清零_气泡_高电平有效 (or_2_out),
    .\使能端_低电平有效_stall_高电平有效 (\if_id_1_传输状态out_表明当前传输数据有效 ), .in_1(multiplexer_7_out),
    .in_20(\单周期硬布线控制器_1_regdst ), .out_44(id_ex_1_out_44), .in_10(shifter_1_out), .out_34(id_ex_1_out_34));  // open: in_22, out_46, in_23, out_47, in_24, out_48, 异步清零, in_25, out_49, in_26, out_50, in_27, out_51
  Register #(.width(32), .trigger("rising"), .Select("low")) register_1 (
    .D(mips_regifile_1_r2), .en(and_1_out), .Q(LedData), .clk(CLK), .clr(RST));
  Adder #(.width(32)) adder_2 (
    .a(id_ex_1_out_31), .b(32'h4), .out({id_ex_1_out_30[31:28], adder_2_out}));  // open: cin, cout
  Multiplexer #(.select(1), .width(32), .disabled("Z"), .enable("false")) multiplexer_9 (
    .in0(id_ex_1_out_33), .in1(id_ex_1_out_28), .out(multiplexer_9_out), .sel(id_ex_1_out_38));
  Adder #(.width(32)) adder_3 (
    .a({id_ex_1_out_30[31:28], adder_2_out}), .b(id_ex_1_out_34), .out(adder_3_out));  // open: cin, cout
  or or_2 (or_2_out, id_ex_1_out_35, or_3_out);
  and and_3 (and_3_out, mips_alu_1_equal, id_ex_1_out_40);
  and and_4 (and_4_out, id_ex_1_out_39, ~mips_alu_1_equal);  // AND_Gate
  MIPS_ALU mips_alu_1 (
    .X(id_ex_1_out_32), .Y(multiplexer_9_out), .AluOP(id_ex_1_out_45), .Equal(mips_alu_1_equal),
    .Result(mips_alu_1_result), .shamt(id_ex_1_out_30[12:8]));  // open: Result_2
  Counter #(.width(16), .max('hffff), .ongoal("wrap"), .trigger("rising"), .behavior("old")) counter_2 (
    .count(or_3_out), .Q(\条件分支成功数 ), .clk(CLK), .clr(RST));  // open: load, D, carry, preset
  Counter #(.width(16), .max('hffff), .ongoal("wrap"), .trigger("rising"), .behavior("old")) counter_3 (
    .count(id_ex_1_out_35), .Q(\无条件分支数 ), .clk(CLK), .clr(RST));  // open: load, D, carry, preset
  or or_3 (or_3_out, and_3_out, and_4_out);
  // Probe on \无条件分支数 
  // Probe on \条件分支成功数 
  EX_MEM ex_mem_1 (
    .in_1({id_ex_1_out_30_2, id_ex_1_out_30[27:2]}), .CLK(CLK), .in_4(id_ex_1_out_31),
    .in_5(mips_alu_1_result), .in_6(id_ex_1_out_33), .in_7(id_ex_1_out_41), .in_8(id_ex_1_out_42),
    .in_9(id_ex_1_out_43), .in_10(id_ex_1_out_44), .out_14(ex_mem_1_out_14),
    .\传输状态Out_表明当前传输数据有效 (\ex_mem_1_传输状态out_表明当前传输数据有效 ), .out_16(ex_mem_1_out_16), .out_17(ex_mem_1_out_17),
    .out_18(MDin), .out_19(MemWrite), .out_20(ex_mem_1_out_20), .out_21(ex_mem_1_out_21),
    .out_22(ex_mem_1_out_22), .\使能端_低电平有效_stall_高电平有效 (\id_ex_1_传输状态out_表明当前传输数据有效 ), .in_11(id_ex_1_out_37),
    .out_23(ex_mem_1_out_23));  // open: 同步清零_气泡_高电平有效, in_13, out_24
  not not_1 (not_1_out, MemWrite);
  RAM #(.addrWidth(10), .dataWidth(32), .bus("separate"), .Select("high")) ram_1 (
    .addr(ex_mem_1_out_17[11:2]), .din(MDin), .data(ram_1_data), .str(MemWrite), .clk(CLK), .ld(not_1_out),
    .clr(RST));  // open: sel
  MEM_WB mem_wb_1 (
    .in_1(ex_mem_1_out_14), .CLK(CLK), .in_4(ex_mem_1_out_16), .in_5(ex_mem_1_out_17), .in_6(ram_1_data),
    .in_7(ex_mem_1_out_20), .in_8(ex_mem_1_out_21), .in_9(ex_mem_1_out_22), .out_13(mem_wb_1_out_13),
    .\传输状态Out_表明当前传输数据有效 (\mem_wb_1_传输状态out_表明当前传输数据有效 ), .out_15(mem_wb_1_out_15), .out_16(mem_wb_1_out_16),
    .out_17(mem_wb_1_out_17), .out_18(RegWrite), .out_19(mem_wb_1_out_19), .out_20(mem_wb_1_out_20),
    .\使能端_低电平有效_stall_高电平有效 (\ex_mem_1_传输状态out_表明当前传输数据有效 ), .in_10(ex_mem_1_out_23), .out_21(mem_wb_1_out_21));  // open: 同步清零_气泡_高电平有效, in_12, out_22
  Multiplexer #(.select(1), .width(32), .disabled("Z"), .enable("false")) multiplexer_10 (
    .in0(mem_wb_1_out_16), .in1(mem_wb_1_out_17), .out(multiplexer_10_out), .sel(mem_wb_1_out_19));
  Multiplexer #(.select(1), .width(32), .disabled("Z"), .enable("false")) multiplexer_11 (
    .in0(multiplexer_10_out), .in1(adder_4_out), .out(RDin), .sel(mem_wb_1_out_21));
  Adder #(.width(32)) adder_4 (.a(mem_wb_1_out_15), .b(32'h4), .out(adder_4_out));  // open: cin, cout

  // Notes on the sheet:
  //   中断源
  //   中断等待指示
  //   总复位信号应将除ROM以外所有存储组件全部清零
  //   指令存储器
  //   指令字
  //   contents of rom_1 (hex, n*v repeats v):
  //   20110020 20020022 8000c06 20110000 20110000 2002000a 10000003 20110000 20110000 2002000a 14110003
  //   20110000 20110000 2002000a c000c14 2002000a 0 0 0 c 2231ffff 0 0 0 112020 0 0 0 c 1620fff6 3e00008
  //   数码管输出
  //   数码管输出应该用寄存器锁存，否则显示数据只能一闪而过
  //   OP
  //   Func
  //   rs
  //   rt
  //   rd
  //   JMP
  //   JR
  //   OP
  //   Func
  //   Beq
  //   Bne
  //   MemToReg
  //   MemWrite
  //   AluOP
  //   AluSrcB
  //   RegWrite
  //   JAL
  //   RegDst
  //   Syscall
  //   为方便自动评测，需要输出PC，IR，寄存器文件写入端口RDin，内存写入端口MDin等信号
  //   OP
  //   rs
  //   rt
  //   rd
endmodule

module \气泡流水线  (
  output RegWrite,
  output MemWrite,
  output [31:0] IF_PC,
  output [31:0] ID_PC,
  output [31:0] EX_PC,
  output [31:0] M_PC,
  output [31:0] WB_PC,
  output [31:0] RDin,
  output [31:0] MDin,
  output [31:0] LedData
);

  wire and_1_out, and_2_out, and_3_out, and_4_out, and_5_out, and_6_out, and_7_out, CLK, comparator_1_eq,
       comparator_2_eq, comparator_3_eq, END, ex_mem_1_p15, ex_mem_1_p16, ex_mem_1_p17, ex_mem_1_p18,
       ex_mem_1_p24, ex_mem_1_p25, Go, id_ex_1_out_35, id_ex_1_out_36, id_ex_1_out_37, id_ex_1_out_38,
       id_ex_1_out_39, id_ex_1_out_40, id_ex_1_out_41, id_ex_1_out_42, id_ex_1_out_43, id_ex_1_out_44,
       id_ex_1_out_46, IR1, IR2, IR3, mem_wb_1_p14, mem_wb_1_p15, mem_wb_1_p16, mem_wb_1_p22,
       mips_alu_1_equal, nand_1_out, not_1_out, not_2_out, not_3_out, or_1_out, or_2_out, or_3_out, or_4_out,
       or_5_out, RST, SignedExt, syscall, W1, W2, W3, \单周期硬布线控制器_1_alu_src , \单周期硬布线控制器_1_beq ,
       \单周期硬布线控制器_1_bne , \单周期硬布线控制器_1_jal , \单周期硬布线控制器_1_jmp , \单周期硬布线控制器_1_jr , \单周期硬布线控制器_1_memtoreg ,
       \单周期硬布线控制器_1_memwrite , \单周期硬布线控制器_1_regdst , \单周期硬布线控制器_1_regwrite , \数据相关 ;
  wire [3:0] adder_2_out_2, id_ex_1_out_45, \单周期硬布线控制器_1_alu_op ;
  wire [4:0] multiplexer_6_out, multiplexer_8_out, multiplexer_10_out, multiplexer_11_out,
       multiplexer_12_out, multiplexer_13_out, R1, R2;
  wire [5:0] FUNC, OP;
  wire [15:0] adder_4_out, \LoadUse次数 , \总周期数 , \插入气泡数 , \无条件分支数 , \条件分支成功数 ;
  wire [25:6] if_id_1_out_9;
  wire [27:0] adder_2_out;
  wire [31:0] adder_1_out, adder_3_out, adder_5_out, bit_extender_1_out, bit_extender_2_out, ex_mem_1_p20,
       ex_mem_1_p22, id_ex_1_out_28, id_ex_1_out_30, id_ex_1_out_32, id_ex_1_out_33, id_ex_1_out_34, IR,
       mem_wb_1_p18, mem_wb_1_p20, mem_wb_1_p21, mem_wb_1_p23, mips_alu_1_result, mips_regifile_1_r1,
       mips_regifile_1_r2, multiplexer_1_out, multiplexer_2_out, multiplexer_3_out, multiplexer_7_out,
       multiplexer_9_out, multiplexer_14_out, ram_1_data, shifter_1_out;

  Button \u_总复位  (.out(RST));
  Button _1 (.out(IR1));
  Button _2 (.out(IR2));
  Button _3 (.out(IR3));
  Register #(.width(32), .trigger("rising"), .Select("low")) PC (
    .D(multiplexer_1_out), .en(and_1_out), .Q(IF_PC), .clk(CLK), .clr(RST));
  Multiplexer #(.select(1), .width(32), .disabled("Z"), .enable("false")) multiplexer_1 (
    .in0(multiplexer_3_out), .in1(multiplexer_2_out), .out(multiplexer_1_out), .sel(id_ex_1_out_35));
  Multiplexer #(.select(1), .width(32), .disabled("Z"), .enable("false")) multiplexer_2 (
    .in0({adder_2_out_2, id_ex_1_out_30[25:0], 2'b00}), .in1(id_ex_1_out_32), .out(multiplexer_2_out),
    .sel(id_ex_1_out_36));
  Button \u_继续运行  (.out(Go));
  LED #(.active("true")) led_1 (.in(W1));
  LED #(.active("true")) led_2 (.in(W2));
  LED #(.active("true")) led_3 (.in(W3));
  Hex_Digit_Display hex_digit_display_1 (.value(LedData[31:28]));  // open: dp
  ROM #(.addrWidth(10), .dataWidth(32), .Select("high")) rom_1 (.addr(IF_PC[11:2]), .data(IR));
  Adder #(.width(32)) adder_1 (.a(IF_PC), .b(32'h4), .out(adder_1_out));  // open: cin, cout
  Multiplexer #(.select(1), .width(32), .disabled("Z"), .enable("false")) multiplexer_3 (
    .in0(adder_1_out), .in1(adder_3_out), .out(multiplexer_3_out), .sel(or_5_out));
  and and_1 (and_1_out, ~END, and_2_out);  // AND_Gate
  Hex_Digit_Display hex_digit_display_2 (.value(LedData[27:24]));  // open: dp
  Hex_Digit_Display hex_digit_display_3 (.value(LedData[23:20]));  // open: dp
  Hex_Digit_Display hex_digit_display_4 (.value(LedData[19:16]));  // open: dp
  Hex_Digit_Display hex_digit_display_5 (.value(LedData[15:12]));  // open: dp
  or or_1 (or_1_out, RST, or_4_out);
  IF_ID if_id_1 (
    .CLK(CLK), .out_9({OP, if_id_1_out_9, FUNC}), .\同步清零_气泡_高电平有效 (or_1_out),
    .\使能端_低电平有效_stall_高电平有效 (and_1_out), .in_5(IF_PC), .out_11(ID_PC), .in_1(IR));  // open: 传输状态Out_表明当前传输数据有效, in_6, out_12, in_7, out_13, in_8, out_14
  and and_2 (and_2_out, ~\数据相关 , nand_1_out);  // AND_Gate
  Hex_Digit_Display hex_digit_display_6 (.value(LedData[11:8]));  // open: dp
  Hex_Digit_Display hex_digit_display_7 (.value(LedData[7:4]));  // open: dp
  Clock #(.highDuration(1), .lowDuration(1)) clock_1 (.out(CLK));
  assign bit_extender_1_out = {{16{if_id_1_out_9[15]}}, {if_id_1_out_9[15:6], FUNC}};  // Bit_Extender bit_extender_1
  assign bit_extender_2_out = {{16{1'b0}}, {if_id_1_out_9[15:6], FUNC}};  // Bit_Extender bit_extender_2
  \数据相关检测  \u_数据相关检测_1  (
    .OP(OP), .EX_WriteReg_num(multiplexer_11_out), .EX_RegWrite(id_ex_1_out_42),
    .MEM_WriteReg_num(multiplexer_13_out), .MEM_RegWrite(ex_mem_1_p18), .\数据相关 (\数据相关 ), .Func(FUNC),
    .ID_R1_num(R1), .ID_R2_num(R2));
  Hex_Digit_Display hex_digit_display_8 (.value(LedData[3:0]));  // open: dp
  Multiplexer #(.select(1), .width(5), .disabled("Z"), .enable("false")) multiplexer_4 (
    .in0(if_id_1_out_9[25:21]), .in1(5'b00010), .out(R1), .sel(syscall));
  Multiplexer #(.select(1), .width(5), .disabled("Z"), .enable("false")) multiplexer_5 (
    .in0(if_id_1_out_9[20:16]), .in1(5'b00100), .out(R2), .sel(syscall));
  Multiplexer #(.select(1), .width(5), .disabled("Z"), .enable("false")) multiplexer_6 (
    .in0(mem_wb_1_p18[20:16]), .in1(mem_wb_1_p18[15:11]), .out(multiplexer_6_out), .sel(mem_wb_1_p14));
  Multiplexer #(.select(1), .width(32), .disabled("Z"), .enable("false")) multiplexer_7 (
    .in0(bit_extender_2_out), .in1(bit_extender_1_out), .out(multiplexer_7_out), .sel(SignedExt));
  or or_2 (or_2_out, nand_1_out, mem_wb_1_p22);
  Multiplexer #(.select(1), .width(5), .disabled("Z"), .enable("false")) multiplexer_8 (
    .in0(multiplexer_6_out), .in1({5{1'b1}}), .out(multiplexer_8_out), .sel(mem_wb_1_p15));
  Shifter #(.width(32), .shift("ll")) shifter_1 (.in(multiplexer_7_out), .\dist (5'b00010), .out(shifter_1_out));
  and and_3 (and_3_out, or_2_out, ~END);  // AND_Gate
  // Probe on \总周期数 
  // Probe on \无条件分支数 
  // Probe on \条件分支成功数 
  // Probe on \插入气泡数 
  // Probe on \LoadUse次数 
  \单周期硬布线控制器  \u_单周期硬布线控制器_1  (
    .Func(FUNC), .OP(OP), .ALU_OP(\单周期硬布线控制器_1_alu_op ), .MemToReg(\单周期硬布线控制器_1_memtoreg ),
    .MemWrite(\单周期硬布线控制器_1_memwrite ), .ALU_SRC(\单周期硬布线控制器_1_alu_src ), .RegWrite(\单周期硬布线控制器_1_regwrite ),
    .SysCALL(syscall), .SignedExt(SignedExt), .RegDst(\单周期硬布线控制器_1_regdst ), .JR(\单周期硬布线控制器_1_jr ),
    .JMP(\单周期硬布线控制器_1_jmp ), .Beq(\单周期硬布线控制器_1_beq ), .JAL(\单周期硬布线控制器_1_jal ), .Bne(\单周期硬布线控制器_1_bne ));
  Comparator #(.width(32), .mode("twosComplement")) comparator_1 (
    .a(mips_regifile_1_r1), .b(32'h22), .eq(comparator_1_eq));  // open: gt, lt
  Comparator #(.width(32), .mode("twosComplement")) comparator_2 (
    .a(mem_wb_1_p23), .b(32'h22), .eq(comparator_2_eq));  // open: gt, lt
  Counter #(.width(16), .max('hffff), .ongoal("wrap"), .trigger("rising"), .behavior("old")) counter_1 (
    .count(and_3_out), .Q(\总周期数 ), .clk(CLK), .clr(RST));  // open: load, D, carry, preset
  // Probe on IF_PC[11:0]
  MIPS_Regifile mips_regifile_1 (
    .Din(RDin), .Clk(CLK), .R1(mips_regifile_1_r1), .R2(mips_regifile_1_r2), .WE(RegWrite),
    .W_num(multiplexer_8_out), .R1_num(R1), .R2_num(R2));
  not not_1 (not_1_out, END);
  and and_4 (and_4_out, comparator_1_eq, syscall);
  and and_5 (and_5_out, mem_wb_1_p22, ~comparator_2_eq);  // AND_Gate
  // Probe on ID_PC[11:0]
  // Probe on EX_PC[11:0]
  Register #(.width(32), .trigger("rising"), .Select("low")) register_1 (
    .D(mips_regifile_1_r2), .en(and_4_out), .Q(LedData), .clk(CLK), .clr(RST));
  nand nand_1 (nand_1_out, and_5_out, ~Go);  // NAND_Gate
  // Probe on M_PC[11:0]
  or or_3 (or_3_out, or_4_out, RST, \数据相关 );
  ID_EX id_ex_1 (
    .CLK(CLK), .in_6({OP, if_id_1_out_9, FUNC}), .in_7(ID_PC), .in_8(mips_regifile_1_r1),
    .in_9(mips_regifile_1_r2), .in_11(\单周期硬布线控制器_1_jmp ), .in_12(\单周期硬布线控制器_1_jr ),
    .in_13(\单周期硬布线控制器_1_jal ), .in_14(\单周期硬布线控制器_1_alu_src ), .in_15(\单周期硬布线控制器_1_bne ),
    .in_16(\单周期硬布线控制器_1_beq ), .in_17(\单周期硬布线控制器_1_memwrite ), .in_18(\单周期硬布线控制器_1_regwrite ),
    .in_19(\单周期硬布线控制器_1_memtoreg ), .in_21(\单周期硬布线控制器_1_alu_op ), .out_28(id_ex_1_out_28),
    .out_30(id_ex_1_out_30), .out_31(EX_PC), .out_32(id_ex_1_out_32), .out_33(id_ex_1_out_33),
    .out_35(id_ex_1_out_35), .out_36(id_ex_1_out_36), .out_37(id_ex_1_out_37), .out_38(id_ex_1_out_38),
    .out_39(id_ex_1_out_39), .out_40(id_ex_1_out_40), .out_41(id_ex_1_out_41), .out_42(id_ex_1_out_42),
    .out_43(id_ex_1_out_43), .out_45(id_ex_1_out_45), .\同步清零_气泡_高电平有效 (or_3_out),
    .\使能端_低电平有效_stall_高电平有效 (not_1_out), .in_1(multiplexer_7_out), .in_20(\单周期硬布线控制器_1_regdst ),
    .out_44(id_ex_1_out_44), .in_10(shifter_1_out), .out_34(id_ex_1_out_34), .in_22(syscall),
    .out_46(id_ex_1_out_46));  // open: 传输状态Out_表明当前传输数据有效, in_23, out_47, in_24, out_48, 异步清零, in_25, out_49, in_26, out_50, in_27, out_51
  // Probe on WB_PC[11:0]
  Adder #(.width(32)) adder_2 (.a(EX_PC), .b(32'h4), .out({adder_2_out_2, adder_2_out}));  // open: cin, cout
  Multiplexer #(.select(1), .width(32), .disabled("Z"), .enable("false")) multiplexer_9 (
    .in0(id_ex_1_out_33), .in1(id_ex_1_out_28), .out(multiplexer_9_out), .sel(id_ex_1_out_38));
  Adder #(.width(32)) adder_3 (
    .a({adder_2_out_2, adder_2_out}), .b(id_ex_1_out_34), .out(adder_3_out));  // open: cin, cout
  or or_4 (or_4_out, id_ex_1_out_35, or_5_out);
  and and_6 (and_6_out, mips_alu_1_equal, id_ex_1_out_40);
  and and_7 (and_7_out, id_ex_1_out_39, ~mips_alu_1_equal);  // AND_Gate
  MIPS_ALU mips_alu_1 (
    .X(id_ex_1_out_32), .Y(multiplexer_9_out), .AluOP(id_ex_1_out_45), .Equal(mips_alu_1_equal),
    .Result(mips_alu_1_result), .shamt(id_ex_1_out_30[10:6]));  // open: Result_2
  Counter #(.width(16), .max('hffff), .ongoal("wrap"), .trigger("rising"), .behavior("old")) counter_2 (
    .count(or_5_out), .Q(\条件分支成功数 ), .clk(CLK), .clr(RST));  // open: load, D, carry, preset
  Counter #(.width(16), .max('hffff), .ongoal("wrap"), .trigger("rising"), .behavior("old")) counter_3 (
    .count(id_ex_1_out_35), .Q(\无条件分支数 ), .clk(CLK), .clr(RST));  // open: load, D, carry, preset
  or or_5 (or_5_out, and_6_out, and_7_out);
  Multiplexer #(.select(1), .width(5), .disabled("Z"), .enable("false")) multiplexer_10 (
    .in0(id_ex_1_out_30[20:16]), .in1(id_ex_1_out_30[15:11]), .out(multiplexer_10_out), .sel(id_ex_1_out_44));
  not not_2 (not_2_out, END);
  Multiplexer #(.select(1), .width(5), .disabled("Z"), .enable("false")) multiplexer_11 (
    .in0(multiplexer_10_out), .in1({5{1'b1}}), .out(multiplexer_11_out), .sel(id_ex_1_out_37));
  // EX_MEM ex_mem_1: pin names not known; wires that end beside it: id_ex_1_out_44, id_ex_1_out_37, id_ex_1_out_43, id_ex_1_out_42, id_ex_1_out_41, id_ex_1_out_30, EX_PC, mips_alu_1_result, id_ex_1_out_33, id_ex_1_out_46, id_ex_1_out_32, not_2_out, RST, CLK, ex_mem_1_p15, ex_mem_1_p16, ex_mem_1_p17, ex_mem_1_p18, MemWrite, ex_mem_1_p20, M_PC, ex_mem_1_p22, MDin, ex_mem_1_p24, ex_mem_1_p25
  not not_3 (not_3_out, MemWrite);
  RAM #(.addrWidth(10), .dataWidth(32), .bus("separate"), .Select("high")) ram_1 (
    .addr(ex_mem_1_p22[11:2]), .din(MDin), .data(ram_1_data), .str(MemWrite), .clk(CLK), .ld(not_3_out),
    .clr(RST));  // open: sel
  Multiplexer #(.select(1), .width(5), .disabled("Z"), .enable("false")) multiplexer_12 (
    .in0(ex_mem_1_p20[20:16]), .in1(ex_mem_1_p20[15:11]), .out(multiplexer_12_out), .sel(ex_mem_1_p15));
  // MEM_WB mem_wb_1: pin names not known; wires that end beside it: ex_mem_1_p15, ex_mem_1_p16, ex_mem_1_p17, ex_mem_1_p18, ex_mem_1_p20, M_PC, ex_mem_1_p22, ram_1_data, ex_mem_1_p24, ex_mem_1_p25, not_2_out, RST, CLK, mem_wb_1_p14, mem_wb_1_p15, mem_wb_1_p16, RegWrite, mem_wb_1_p18, WB_PC, mem_wb_1_p20, mem_wb_1_p21, mem_wb_1_p22, mem_wb_1_p23
  Multiplexer #(.select(1), .width(5), .disabled("Z"), .enable("false")) multiplexer_13 (
    .in0(multiplexer_12_out), .in1({5{1'b1}}), .out(multiplexer_13_out), .sel(ex_mem_1_p16));
  Multiplexer #(.select(1), .width(32), .disabled("Z"), .enable("false")) multiplexer_14 (
    .in0(mem_wb_1_p20), .in1(mem_wb_1_p21), .out(multiplexer_14_out), .sel(mem_wb_1_p16));
  Multiplexer #(.select(1), .width(32), .disabled("Z"), .enable("false")) multiplexer_15 (
    .in0(multiplexer_14_out), .in1(adder_5_out), .out(RDin), .sel(mem_wb_1_p15));
  Counter #(.width(16), .max('hffff), .ongoal("wrap"), .trigger("rising"), .behavior("old")) counter_4 (
    .count(\数据相关 ), .Q(\插入气泡数 ), .clk(CLK), .clr(RST));  // open: load, D, carry, preset
  Comparator #(.width(16), .mode("twosComplement")) comparator_3 (
    .a(\插入气泡数 ), .b({16{1'b0}}), .eq(comparator_3_eq));  // open: gt, lt
  Adder #(.width(16)) adder_4 (.a(\插入气泡数 ), .b(16'h1), .out(adder_4_out));  // open: cin, cout
  Adder #(.width(32)) adder_5 (.a(WB_PC), .b(32'h4), .out(adder_5_out));  // open: cin, cout
  Comparator #(.width(16), .mode("twosComplement")) comparator_4 (.a(16'he28), .b(\总周期数 ), .eq(END));  // open: gt, lt
  Multiplexer #(.select(1), .width(16), .disabled("Z"), .enable("false")) multiplexer_16 (
    .in0(adder_4_out), .in1({16{1'b0}}), .sel(comparator_3_eq));  // open: out

  // Other names for the same wires on the sheet: MEM_PC[31:0] = M_PC; PC[31:0] = IF_PC

  // Notes on the sheet:
  //   中断源
  //   中断等待指示
  //   总复位信号应将除ROM以外所有存储组件全部清零
  //   指令存储器
  //   contents of rom_1 (hex, n*v repeats v):
  //   20110001 8000c05 20110001 20120002 20130003 8000c09 20110001 20120002 20130003 8000c0d 20110001
  //   20120002 20130003 8000c11 20110001 20120002 20130003 c000cb8 20100001 20110001 118fc0 112020
  //   20020022 c 118882 12200001 8000c15 112020 20020022 c 20110001 118880 112020 20020022 c 12200001
  //   8000c1f 20110001 118fc0 112020 20020022 c 1188c3 112020 20020022 c 118903 112020 20020022 c 118903
  //   112020 20020022 c 118903 112020 20020022 c 118903 112020 20020022 c 118903 112020 20020022 c 118903
  //   112020 20020022 c 118903 112020 20020022 c 20100001 109fc0 139fc3 8021 2012000c 24160003 26100001
  //   3210000f 20080008 20090001 139900 2709825 132020 20020022 c 1094022 1500fff9 22100001 2018000f
  //   2188024 108700 20080008 20090001 139902 2709825 132021 20020022 c 1094022 1500fff9 108702 2c9b022
  //   12c00001 8000c50 4020 1084027 84400 3508ffff 82021 20020022 c 2010ffff 20110000 ae300000 22100001
  //   22310004 ae300000 22100001 22310004 ae300000 22100001 22310004 ae300000 22100001 22310004 ae300000
  //   22100001 22310004 ae300000 22100001 22310004 ae300000 22100001 22310004 ae300000 22100001 22310004
  //   ae300000 22100001 22310004 ae300000 22100001 22310004 ae300000 22100001 22310004 ae300000 22100001
  //   22310004 ae300000 22100001 22310004 ae300000 22100001 22310004 ae300000 22100001 22310004 ae300000
  //   22100001 22310004 22100001 8020 2011003c 8e130000 8e340000 274402a 11000002 ae330000 ae140000
  //   2231fffc 1611fff8 102020 20020022 c 22100004 2011003c 1611fff2 20020032 c 20100000 22100001 102020
  //   20020022 c 22100002 102020 20020022 c 22100003 102020 20020022 c 22100004 102020 20020022 c 22100005
  //   102020 20020022 c 22100006 102020 20020022 c 22100007 102020 20020022 c 22100008 102020 20020022
  //   20020022 c 3e00008
  //   指令字
  //   数码管输出
  //   OP
  //   rs
  //   rd
  //   数码管输出应该用寄存器锁存，否则显示数据只能一闪而过
  //   Func
  //   rt
  //   JR
  //   Beq
  //   JMP
  //   Bne
  //   OP
  //   JAL
  //   Func
  //   Syscall
  //   MemToReg
  //   MemWrite
  //   AluOP
  //   AluSrcB
  //   RegWrite
  //   RegDst
  //   流水调试日志用
  //   rs
  //   rt
  //   rd
  //   为方便自动评测，需要输出流水线各段保存的PC值，注意是PC不是PC+4，另外ID段寄存器写入信息，Mem段内存写入信息也要输出
  //   rs
  //   rt
  //   rd
  //   OP
  //   rs
  //   rt
  //   rd
endmodule
// 源寄存器使用情况
module \源寄存器使用情况  (
  input  OP0,
  input  OP1,
  input  OP2,
  input  OP3,
  input  OP4,
  input  OP5,
  input  F0,
  input  F1,
  input  F2,
  input  F3,
  input  F4,
  input  F5,
  output R1_Used,
  output R2_Used
);

  wire and_1_out, and_2_out, and_3_out, and_4_out, and_5_out, and_6_out, and_7_out, and_8_out, and_9_out,
       and_10_out, and_11_out, and_12_out, and_13_out, and_14_out, and_15_out, and_16_out, and_17_out,
       and_18_out, and_19_out, and_20_out, and_21_out, and_22_out, and_23_out, and_24_out, and_25_out,
       and_26_out, and_27_out, and_28_out, and_29_out, and_30_out, and_31_out, and_32_out, and_33_out,
       and_34_out, and_35_out, and_36_out, and_37_out, and_38_out, and_39_out, not_1_out, not_2_out,
       not_3_out, not_4_out, not_5_out, not_6_out, not_7_out, not_8_out, not_9_out, not_10_out, not_11_out,
       not_12_out, not_13_out, not_14_out, not_15_out, not_16_out, not_17_out, not_18_out, not_19_out,
       not_20_out, not_21_out, not_22_out, not_23_out, not_24_out, not_25_out, not_26_out, not_27_out,
       not_28_out, not_29_out, not_30_out, not_31_out, not_32_out, not_33_out, not_34_out, not_35_out,
       not_36_out, not_37_out, not_38_out, not_39_out, not_40_out, not_41_out, not_42_out, not_43_out,
       not_44_out, not_45_out, not_46_out, not_47_out, not_48_out, not_49_out, not_50_out, not_51_out,
       not_52_out, not_53_out, not_54_out, not_55_out, not_56_out, not_57_out, not_58_out, not_59_out,
       not_60_out, not_61_out, not_62_out, not_63_out, not_64_out, not_65_out, not_66_out, not_67_out,
       not_68_out, not_69_out, not_70_out, not_71_out, not_72_out, not_73_out, not_74_out, not_75_out,
       not_76_out, not_77_out, not_78_out, not_79_out, not_80_out, not_81_out, not_82_out, not_83_out,
       not_84_out, not_85_out, not_86_out, not_87_out, not_88_out, not_89_out, not_90_out, not_91_out,
       not_92_out, not_93_out, not_94_out, not_95_out, not_96_out, not_97_out, not_98_out, not_99_out,
       not_100_out, not_101_out, not_102_out, not_103_out, not_104_out, not_105_out, not_106_out,
       not_107_out, not_108_out, not_109_out, not_110_out, not_111_out, not_112_out, not_113_out,
       not_114_out, not_115_out, not_116_out, not_117_out, not_118_out, not_119_out, not_120_out,
       not_121_out, not_122_out, not_123_out, not_124_out, not_125_out, not_126_out, not_127_out,
       not_128_out, not_129_out, not_130_out, not_131_out, not_132_out, not_133_out, not_134_out,
       not_135_out, not_136_out, not_137_out, not_138_out, not_139_out, not_140_out, not_141_out,
       not_142_out, not_143_out, not_144_out, not_145_out, not_146_out, not_147_out, not_148_out,
       not_149_out, not_150_out, not_151_out, not_152_out, not_153_out, not_154_out, not_155_out,
       not_156_out, not_157_out, not_158_out, not_159_out, not_160_out, not_161_out, not_162_out,
       not_163_out, not_164_out, not_165_out, not_166_out, not_167_out, not_168_out, not_169_out,
       not_170_out, not_171_out, not_172_out, not_173_out, not_174_out, not_175_out, not_176_out,
       not_177_out, not_178_out, not_179_out, not_180_out, not_181_out, not_182_out, not_183_out,
       not_184_out, not_185_out, not_186_out, not_187_out, not_188_out, not_189_out, not_190_out,
       not_191_out, not_192_out, not_193_out, not_194_out, not_195_out, not_196_out, not_197_out,
       not_198_out, not_199_out, not_200_out, not_201_out, not_202_out, not_203_out, not_204_out,
       not_205_out, not_206_out, not_207_out, not_208_out, not_209_out, not_210_out, not_211_out,
       not_212_out, not_213_out, not_214_out, not_215_out, not_216_out, not_217_out, not_218_out,
       not_219_out, not_220_out, not_221_out, not_222_out, not_223_out, not_224_out, not_225_out,
       not_226_out, not_227_out, not_228_out, not_229_out, not_230_out, not_231_out, not_232_out,
       not_233_out, not_234_out, not_235_out, not_236_out, not_237_out, not_238_out, not_239_out,
       not_240_out, not_241_out, not_242_out, not_243_out, not_244_out, not_245_out, not_246_out,
       not_247_out, not_248_out, not_249_out, not_250_out, not_251_out, not_252_out, not_253_out,
       not_254_out, not_255_out, not_256_out, not_257_out, not_258_out, not_259_out, not_260_out,
       not_261_out, not_262_out, not_263_out, not_264_out, not_265_out, not_266_out, not_267_out,
       not_268_out, not_269_out, not_270_out, not_271_out, not_272_out, not_273_out, not_274_out,
       not_275_out, not_276_out, not_277_out, not_278_out, not_279_out, not_280_out, not_281_out,
       not_282_out, not_283_out, not_284_out, not_285_out, not_286_out, not_287_out, not_288_out,
       not_289_out, not_290_out, not_291_out, not_292_out;

  not not_1 (not_1_out, OP5);
  not not_2 (not_2_out, OP4);
  not not_3 (not_3_out, OP3);
  not not_4 (not_4_out, OP2);
  not not_5 (not_5_out, OP1);
  not not_6 (not_6_out, OP0);
  not not_7 (not_7_out, F4);
  not not_8 (not_8_out, F3);
  not not_9 (not_9_out, F2);
  not not_10 (not_10_out, F1);
  not not_11 (not_11_out, F0);
  not not_12 (not_12_out, OP5);
  not not_13 (not_13_out, OP4);
  not not_14 (not_14_out, OP3);
  not not_15 (not_15_out, OP2);
  not not_16 (not_16_out, OP1);
  not not_17 (not_17_out, OP0);
  not not_18 (not_18_out, F4);
  not not_19 (not_19_out, F3);
  not not_20 (not_20_out, F2);
  not not_21 (not_21_out, F1);
  not not_22 (not_22_out, OP5);
  not not_23 (not_23_out, OP4);
  not not_24 (not_24_out, OP3);
  not not_25 (not_25_out, OP2);
  not not_26 (not_26_out, OP1);
  not not_27 (not_27_out, OP0);
  not not_28 (not_28_out, F4);
  not not_29 (not_29_out, F3);
  not not_30 (not_30_out, F2);
  not not_31 (not_31_out, F0);
  not not_32 (not_32_out, OP5);
  not not_33 (not_33_out, OP4);
  not not_34 (not_34_out, OP3);
  not not_35 (not_35_out, OP2);
  not not_36 (not_36_out, OP1);
  not not_37 (not_37_out, OP0);
  not not_38 (not_38_out, F4);
  not not_39 (not_39_out, F3);
  not not_40 (not_40_out, F1);
  not not_41 (not_41_out, F0);
  not not_42 (not_42_out, OP5);
  not not_43 (not_43_out, OP4);
  not not_44 (not_44_out, OP3);
  not not_45 (not_45_out, OP2);
  not not_46 (not_46_out, OP1);
  not not_47 (not_47_out, OP0);
  not not_48 (not_48_out, F4);
  not not_49 (not_49_out, F3);
  not not_50 (not_50_out, F1);
  not not_51 (not_51_out, OP5);
  not not_52 (not_52_out, OP4);
  not not_53 (not_53_out, OP3);
  not not_54 (not_54_out, OP2);
  not not_55 (not_55_out, OP1);
  not not_56 (not_56_out, OP0);
  not not_57 (not_57_out, F4);
  not not_58 (not_58_out, F3);
  not not_59 (not_59_out, OP5);
  not not_60 (not_60_out, OP4);
  not not_61 (not_61_out, OP3);
  not not_62 (not_62_out, OP2);
  not not_63 (not_63_out, OP1);
  not not_64 (not_64_out, OP0);
  not not_65 (not_65_out, F4);
  not not_66 (not_66_out, F2);
  not not_67 (not_67_out, F0);
  not not_68 (not_68_out, OP5);
  not not_69 (not_69_out, OP4);
  not not_70 (not_70_out, OP3);
  not not_71 (not_71_out, OP2);
  not not_72 (not_72_out, OP1);
  not not_73 (not_73_out, OP0);
  not not_74 (not_74_out, F4);
  not not_75 (not_75_out, F2);
  not not_76 (not_76_out, OP5);
  not not_77 (not_77_out, OP4);
  not not_78 (not_78_out, OP3);
  not not_79 (not_79_out, OP2);
  not not_80 (not_80_out, OP1);
  not not_81 (not_81_out, OP0);
  not not_82 (not_82_out, F5);
  not not_83 (not_83_out, F4);
  not not_84 (not_84_out, F2);
  not not_85 (not_85_out, F1);
  not not_86 (not_86_out, F0);
  not not_87 (not_87_out, OP5);
  not not_88 (not_88_out, OP4);
  not not_89 (not_89_out, OP3);
  not not_90 (not_90_out, OP2);
  not not_91 (not_91_out, OP1);
  not not_92 (not_92_out, OP0);
  not not_93 (not_93_out, F5);
  not not_94 (not_94_out, F4);
  not not_95 (not_95_out, F1);
  not not_96 (not_96_out, F0);
  not not_97 (not_97_out, OP5);
  not not_98 (not_98_out, OP4);
  not not_99 (not_99_out, OP3);
  not not_100 (not_100_out, OP1);
  not not_101 (not_101_out, OP0);
  not not_102 (not_102_out, OP5);
  not not_103 (not_103_out, OP4);
  not not_104 (not_104_out, OP3);
  not not_105 (not_105_out, OP1);
  not not_106 (not_106_out, OP5);
  not not_107 (not_107_out, OP4);
  not not_108 (not_108_out, OP2);
  not not_109 (not_109_out, OP1);
  not not_110 (not_110_out, OP0);
  not not_111 (not_111_out, OP5);
  not not_112 (not_112_out, OP4);
  not not_113 (not_113_out, OP1);
  not not_114 (not_114_out, OP0);
  not not_115 (not_115_out, OP5);
  not not_116 (not_116_out, OP4);
  not not_117 (not_117_out, OP2);
  not not_118 (not_118_out, OP1);
  not not_119 (not_119_out, OP5);
  not not_120 (not_120_out, OP4);
  not not_121 (not_121_out, OP2);
  not not_122 (not_122_out, OP0);
  not not_123 (not_123_out, OP5);
  not not_124 (not_124_out, OP4);
  not not_125 (not_125_out, OP1);
  not not_126 (not_126_out, OP4);
  not not_127 (not_127_out, OP3);
  not not_128 (not_128_out, OP2);
  not not_129 (not_129_out, OP4);
  not not_130 (not_130_out, OP2);
  not not_131 (not_131_out, OP5);
  not not_132 (not_132_out, OP4);
  not not_133 (not_133_out, OP3);
  not not_134 (not_134_out, OP2);
  not not_135 (not_135_out, OP1);
  not not_136 (not_136_out, OP0);
  not not_137 (not_137_out, F5);
  not not_138 (not_138_out, F4);
  not not_139 (not_139_out, F3);
  not not_140 (not_140_out, F1);
  not not_141 (not_141_out, F0);
  not not_142 (not_142_out, OP5);
  not not_143 (not_143_out, OP4);
  not not_144 (not_144_out, OP0);
  not not_145 (not_145_out, OP4);
  not not_146 (not_146_out, OP3);
  not not_147 (not_147_out, OP1);
  not not_148 (not_148_out, OP5);
  not not_149 (not_149_out, OP4);
  not not_150 (not_150_out, OP3);
  not not_151 (not_151_out, OP2);
  not not_152 (not_152_out, OP1);
  not not_153 (not_153_out, OP5);
  not not_154 (not_154_out, OP4);
  not not_155 (not_155_out, OP3);
  not not_156 (not_156_out, OP2);
  not not_157 (not_157_out, OP1);
  not not_158 (not_158_out, OP0);
  not not_159 (not_159_out, F5);
  not not_160 (not_160_out, F4);
  not not_161 (not_161_out, F3);
  not not_162 (not_162_out, F2);
  not not_163 (not_163_out, F1);
  not not_164 (not_164_out, F0);
  not not_165 (not_165_out, OP5);
  not not_166 (not_166_out, OP4);
  not not_167 (not_167_out, OP3);
  not not_168 (not_168_out, OP2);
  not not_169 (not_169_out, OP1);
  not not_170 (not_170_out, OP0);
  not not_171 (not_171_out, F5);
  not not_172 (not_172_out, F4);
  not not_173 (not_173_out, F3);
  not not_174 (not_174_out, F2);
  not not_175 (not_175_out, OP5);
  not not_176 (not_176_out, OP4);
  not not_177 (not_177_out, OP3);
  not not_178 (not_178_out, OP2);
  not not_179 (not_179_out, OP1);
  not not_180 (not_180_out, OP0);
  not not_181 (not_181_out, F5);
  not not_182 (not_182_out, F4);
  not not_183 (not_183_out, F3);
  not not_184 (not_184_out, F2);
  not not_185 (not_185_out, F0);
  not not_186 (not_186_out, OP5);
  not not_187 (not_187_out, OP4);
  not not_188 (not_188_out, OP3);
  not not_189 (not_189_out, OP2);
  not not_190 (not_190_out, OP1);
  not not_191 (not_191_out, OP0);
  not not_192 (not_192_out, F4);
  not not_193 (not_193_out, F3);
  not not_194 (not_194_out, F2);
  not not_195 (not_195_out, F1);
  not not_196 (not_196_out, F0);
  not not_197 (not_197_out, OP5);
  not not_198 (not_198_out, OP4);
  not not_199 (not_199_out, OP3);
  not not_200 (not_200_out, OP2);
  not not_201 (not_201_out, OP1);
  not not_202 (not_202_out, OP0);
  not not_203 (not_203_out, F4);
  not not_204 (not_204_out, F3);
  not not_205 (not_205_out, F2);
  not not_206 (not_206_out, F1);
  not not_207 (not_207_out, OP5);
  not not_208 (not_208_out, OP4);
  not not_209 (not_209_out, OP3);
  not not_210 (not_210_out, OP2);
  not not_211 (not_211_out, OP1);
  not not_212 (not_212_out, OP0);
  not not_213 (not_213_out, F4);
  not not_214 (not_214_out, F3);
  not not_215 (not_215_out, F2);
  not not_216 (not_216_out, F0);
  not not_217 (not_217_out, OP5);
  not not_218 (not_218_out, OP4);
  not not_219 (not_219_out, OP3);
  not not_220 (not_220_out, OP2);
  not not_221 (not_221_out, OP1);
  not not_222 (not_222_out, OP0);
  not not_223 (not_223_out, F4);
  not not_224 (not_224_out, F3);
  not not_225 (not_225_out, F1);
  not not_226 (not_226_out, F0);
  not not_227 (not_227_out, OP5);
  not not_228 (not_228_out, OP4);
  not not_229 (not_229_out, OP3);
  not not_230 (not_230_out, OP2);
  not not_231 (not_231_out, OP1);
  not not_232 (not_232_out, OP0);
  not not_233 (not_233_out, F4);
  not not_234 (not_234_out, F3);
  not not_235 (not_235_out, F1);
  not not_236 (not_236_out, OP5);
  not not_237 (not_237_out, OP4);
  not not_238 (not_238_out, OP3);
  not not_239 (not_239_out, OP2);
  not not_240 (not_240_out, OP1);
  not not_241 (not_241_out, OP0);
  not not_242 (not_242_out, F4);
  not not_243 (not_243_out, F3);
  not not_244 (not_244_out, OP5);
  not not_245 (not_245_out, OP4);
  not not_246 (not_246_out, OP3);
  not not_247 (not_247_out, OP2);
  not not_248 (not_248_out, OP1);
  not not_249 (not_249_out, OP0);
  not not_250 (not_250_out, F4);
  not not_251 (not_251_out, F2);
  not not_252 (not_252_out, F0);
  not not_253 (not_253_out, OP5);
  not not_254 (not_254_out, OP4);
  not not_255 (not_255_out, OP3);
  not not_256 (not_256_out, OP2);
  not not_257 (not_257_out, OP1);
  not not_258 (not_258_out, OP0);
  not not_259 (not_259_out, F4);
  not not_260 (not_260_out, F2);
  not not_261 (not_261_out, OP5);
  not not_262 (not_262_out, OP4);
  not not_263 (not_263_out, OP3);
  not not_264 (not_264_out, OP2);
  not not_265 (not_265_out, OP1);
  not not_266 (not_266_out, OP0);
  not not_267 (not_267_out, F5);
  not not_268 (not_268_out, F4);
  not not_269 (not_269_out, F1);
  not not_270 (not_270_out, F0);
  not not_271 (not_271_out, OP5);
  not not_272 (not_272_out, OP4);
  not not_273 (not_273_out, OP3);
  not not_274 (not_274_out, OP1);
  not not_275 (not_275_out, OP0);
  not not_276 (not_276_out, OP5);
  not not_277 (not_277_out, OP4);
  not not_278 (not_278_out, OP3);
  not not_279 (not_279_out, OP1);
  not not_280 (not_280_out, OP4);
  not not_281 (not_281_out, OP2);
  not not_282 (not_282_out, OP5);
  not not_283 (not_283_out, OP4);
  not not_284 (not_284_out, OP3);
  not not_285 (not_285_out, OP2);
  not not_286 (not_286_out, OP1);
  not not_287 (not_287_out, OP0);
  not not_288 (not_288_out, F5);
  not not_289 (not_289_out, F4);
  not not_290 (not_290_out, F3);
  not not_291 (not_291_out, F1);
  not not_292 (not_292_out, F0);
  and and_1 (and_1_out, not_1_out, not_2_out, not_3_out, not_4_out, not_5_out, not_6_out, F5, not_7_out, not_8_out, not_9_out, not_10_out, not_11_out);
  and and_2 (and_2_out, not_12_out, not_13_out, not_14_out, not_15_out, not_16_out, not_17_out, F5, not_18_out, not_19_out, not_20_out, not_21_out, F0);
  and and_3 (and_3_out, not_22_out, not_23_out, not_24_out, not_25_out, not_26_out, not_27_out, F5, not_28_out, not_29_out, not_30_out, F1, not_31_out);
  and and_4 (and_4_out, not_32_out, not_33_out, not_34_out, not_35_out, not_36_out, not_37_out, F5, not_38_out, not_39_out, F2, not_40_out, not_41_out);
  and and_5 (and_5_out, not_42_out, not_43_out, not_44_out, not_45_out, not_46_out, not_47_out, F5, not_48_out, not_49_out, F2, not_50_out, F0);
  and and_6 (and_6_out, not_51_out, not_52_out, not_53_out, not_54_out, not_55_out, not_56_out, F5, not_57_out, not_58_out, F2, F1, F0);
  and and_7 (and_7_out, not_59_out, not_60_out, not_61_out, not_62_out, not_63_out, not_64_out, F5, not_65_out, F3, not_66_out, F1, not_67_out);
  and and_8 (and_8_out, not_68_out, not_69_out, not_70_out, not_71_out, not_72_out, not_73_out, F5, not_74_out, F3, not_75_out, F1, F0);
  and and_9 (and_9_out, not_76_out, not_77_out, not_78_out, not_79_out, not_80_out, not_81_out, not_82_out, not_83_out, F3, not_84_out, not_85_out, not_86_out);
  and and_10 (and_10_out, not_87_out, not_88_out, not_89_out, not_90_out, not_91_out, not_92_out, not_93_out, not_94_out, F3, F2, not_95_out, not_96_out);
  and and_11 (and_11_out, not_97_out, not_98_out, not_99_out, OP2, not_100_out, not_101_out);
  and and_12 (and_12_out, not_102_out, not_103_out, not_104_out, OP2, not_105_out, OP0);
  and and_13 (and_13_out, not_106_out, not_107_out, OP3, not_108_out, not_109_out, not_110_out);
  and and_14 (and_14_out, not_111_out, not_112_out, OP3, OP2, not_113_out, not_114_out);
  and and_15 (and_15_out, not_115_out, not_116_out, OP3, not_117_out, not_118_out, OP0);
  and and_16 (and_16_out, not_119_out, not_120_out, OP3, not_121_out, OP1, not_122_out);
  and and_17 (and_17_out, not_123_out, not_124_out, OP3, OP2, not_125_out, OP0);
  and and_18 (and_18_out, OP5, not_126_out, not_127_out, not_128_out, OP1, OP0);
  and and_19 (and_19_out, OP5, not_129_out, OP3, not_130_out, OP1, OP0);
  and and_20 (and_20_out, not_131_out, not_132_out, not_133_out, not_134_out, not_135_out, not_136_out, not_137_out, not_138_out, not_139_out, F2, not_140_out, not_141_out);
  and and_21 (and_21_out, not_142_out, not_143_out, OP3, OP2, OP1, not_144_out);
  and and_22 (and_22_out, OP5, not_145_out, not_146_out, OP2, not_147_out, OP0);
  and and_23 (and_23_out, not_148_out, not_149_out, not_150_out, not_151_out, not_152_out, OP0);
  and and_24 (and_24_out, not_153_out, not_154_out, not_155_out, not_156_out, not_157_out, not_158_out, not_159_out, not_160_out, not_161_out, not_162_out, not_163_out, not_164_out);
  and and_25 (and_25_out, not_165_out, not_166_out, not_167_out, not_168_out, not_169_out, not_170_out, not_171_out, not_172_out, not_173_out, not_174_out, F1, F0);
  and and_26 (and_26_out, not_175_out, not_176_out, not_177_out, not_178_out, not_179_out, not_180_out, not_181_out, not_182_out, not_183_out, not_184_out, F1, not_185_out);
  and and_27 (and_27_out, not_186_out, not_187_out, not_188_out, not_189_out, not_190_out, not_191_out, F5, not_192_out, not_193_out, not_194_out, not_195_out, not_196_out);
  and and_28 (and_28_out, not_197_out, not_198_out, not_199_out, not_200_out, not_201_out, not_202_out, F5, not_203_out, not_204_out, not_205_out, not_206_out, F0);
  and and_29 (and_29_out, not_207_out, not_208_out, not_209_out, not_210_out, not_211_out, not_212_out, F5, not_213_out, not_214_out, not_215_out, F1, not_216_out);
  and and_30 (and_30_out, not_217_out, not_218_out, not_219_out, not_220_out, not_221_out, not_222_out, F5, not_223_out, not_224_out, F2, not_225_out, not_226_out);
  and and_31 (and_31_out, not_227_out, not_228_out, not_229_out, not_230_out, not_231_out, not_232_out, F5, not_233_out, not_234_out, F2, not_235_out, F0);
  and and_32 (and_32_out, not_236_out, not_237_out, not_238_out, not_239_out, not_240_out, not_241_out, F5, not_242_out, not_243_out, F2, F1, F0);
  and and_33 (and_33_out, not_244_out, not_245_out, not_246_out, not_247_out, not_248_out, not_249_out, F5, not_250_out, F3, not_251_out, F1, not_252_out);
  and and_34 (and_34_out, not_253_out, not_254_out, not_255_out, not_256_out, not_257_out, not_258_out, F5, not_259_out, F3, not_260_out, F1, F0);
  and and_35 (and_35_out, not_261_out, not_262_out, not_263_out, not_264_out, not_265_out, not_266_out, not_267_out, not_268_out, F3, F2, not_269_out, not_270_out);
  and and_36 (and_36_out, not_271_out, not_272_out, not_273_out, OP2, not_274_out, not_275_out);
  and and_37 (and_37_out, not_276_out, not_277_out, not_278_out, OP2, not_279_out, OP0);
  and and_38 (and_38_out, OP5, not_280_out, OP3, not_281_out, OP1, OP0);
  and and_39 (and_39_out, not_282_out, not_283_out, not_284_out, not_285_out, not_286_out, not_287_out, not_288_out, not_289_out, not_290_out, F2, not_291_out, not_292_out);
  or or_1 (R1_Used, and_1_out, and_2_out, and_3_out, and_4_out, and_5_out, and_6_out, and_7_out, and_8_out, and_9_out, and_10_out, and_11_out, and_12_out, and_13_out, and_14_out, and_15_out, and_16_out, and_17_out, and_18_out, and_19_out, and_20_out, and_21_out, and_22_out, and_23_out);
  or or_2 (R2_Used, and_24_out, and_25_out, and_26_out, and_27_out, and_28_out, and_29_out, and_30_out, and_31_out, and_32_out, and_33_out, and_34_out, and_35_out, and_36_out, and_37_out, and_38_out, and_39_out);
endmodule

module \数据相关检测  (
  input  [5:0] OP,
  input  [4:0] EX_WriteReg_num,
  input  EX_RegWrite,
  input  [4:0] MEM_WriteReg_num,
  input  MEM_RegWrite,
  input  [5:0] Func,
  input  [4:0] ID_R1_num,
  input  [4:0] ID_R2_num,
  output \数据相关 
);

  wire and_1_out, and_2_out, and_3_out, and_4_out, comparator_1_eq, comparator_2_eq, comparator_3_eq,
       comparator_4_eq, comparator_5_eq, comparator_6_eq, not_1_out, not_2_out, \源寄存器使用情况_1_r1_used ,
       \源寄存器使用情况_1_r2_used ;

  \源寄存器使用情况  \u_源寄存器使用情况_1  (
    .OP0(OP[0]), .OP1(OP[1]), .OP2(OP[2]), .OP3(OP[3]), .OP4(OP[4]), .OP5(OP[5]), .F0(Func[0]), .F1(Func[1]),
    .F2(Func[2]), .F3(Func[3]), .F4(Func[4]), .F5(Func[5]), .R1_Used(\源寄存器使用情况_1_r1_used ),
    .R2_Used(\源寄存器使用情况_1_r2_used ));
  Comparator #(.width(5), .mode("twosComplement")) comparator_1 (
    .a(ID_R1_num), .b({5{1'b0}}), .eq(comparator_1_eq));  // open: gt, lt
  Comparator #(.width(5), .mode("twosComplement")) comparator_2 (
    .a(ID_R2_num), .b({5{1'b0}}), .eq(comparator_2_eq));  // open: gt, lt
  not not_1 (not_1_out, comparator_1_eq);
  not not_2 (not_2_out, comparator_2_eq);
  Comparator #(.width(5), .mode("twosComplement")) comparator_3 (
    .a(ID_R1_num), .b(MEM_WriteReg_num), .eq(comparator_3_eq));  // open: gt, lt
  Comparator #(.width(5), .mode("twosComplement")) comparator_4 (
    .a(ID_R2_num), .b(MEM_WriteReg_num), .eq(comparator_4_eq));  // open: gt, lt
  Comparator #(.width(5), .mode("twosComplement")) comparator_5 (
    .a(ID_R1_num), .b(EX_WriteReg_num), .eq(comparator_5_eq));  // open: gt, lt
  Comparator #(.width(5), .mode("twosComplement")) comparator_6 (
    .a(ID_R2_num), .b(EX_WriteReg_num), .eq(comparator_6_eq));  // open: gt, lt
  and and_1 (and_1_out, not_1_out, EX_RegWrite, comparator_5_eq, \源寄存器使用情况_1_r1_used );
  and and_2 (and_2_out, not_1_out, MEM_RegWrite, comparator_3_eq, \源寄存器使用情况_1_r1_used );
  and and_3 (and_3_out, not_2_out, EX_RegWrite, comparator_6_eq, \源寄存器使用情况_1_r2_used );
  and and_4 (and_4_out, not_2_out, MEM_RegWrite, comparator_4_eq, \源寄存器使用情况_1_r2_used );
  or or_1 (\数据相关 , and_1_out, and_2_out, and_3_out, and_4_out);

  // Other names for the same wires on the sheet: OP_CODE[5:0] = OP
endmodule

module \重定向流水线  (
  output RegWrite,
  output MemWrite,
  output [31:0] IF_PC,
  output [31:0] ID_PC,
  output [31:0] EX_PC,
  output [31:0] M_PC,
  output [31:0] WB_PC,
  output [31:0] RDin,
  output [31:0] MDin,
  output [31:0] LedData
);

  wire and_1_out, and_2_out, and_3_out, and_4_out, and_5_out, and_6_out, and_7_out, and_8_out, and_9_out,
       and_10_out, and_11_out, and_12_out, and_13_out, and_14_out, and_15_out, and_16_out, CLK,
       comparator_1_eq, comparator_2_eq, comparator_3_eq, comparator_4_eq, comparator_5_eq, comparator_6_eq,
       comparator_7_eq, comparator_8_eq, comparator_9_eq, comparator_10_eq, END, ex_mem_1_p14, ex_mem_1_p15,
       ex_mem_1_p23, ex_mem_1_p24, EX_MEMTOREG, EX_syscall, Go, id_ex_1_out_35, id_ex_1_out_36,
       id_ex_1_out_37, id_ex_1_out_38, id_ex_1_out_39, id_ex_1_out_40, id_ex_1_out_41, id_ex_1_out_44, IR1,
       IR2, IR3, LOADUSE, MEM_RegWrite, mem_wb_1_p13, mem_wb_1_p14, mem_wb_1_p15, mem_wb_1_p21, MEMTOREG,
       mips_alu_1_equal, nand_1_out, not_1_out, not_2_out, not_3_out, not_4_out, not_5_out, or_1_out,
       or_2_out, or_3_out, or_4_out, RST, SignedExt, syscall, W1, W2, W3, WB_RegWrite, \单周期硬布线控制器_1_alu_src ,
       \单周期硬布线控制器_1_beq , \单周期硬布线控制器_1_bne , \单周期硬布线控制器_1_jal , \单周期硬布线控制器_1_jmp , \单周期硬布线控制器_1_jr ,
       \单周期硬布线控制器_1_memtoreg , \单周期硬布线控制器_1_memwrite , \单周期硬布线控制器_1_regdst , \单周期硬布线控制器_1_regwrite ,
       \源寄存器使用情况_1_r1_used , \源寄存器使用情况_1_r2_used ;
  wire [1:0] EX_FWA, EX_FWB, multiplexer_9_out, multiplexer_10_out, multiplexer_11_out, multiplexer_12_out,
       SA, SB;
  wire [3:0] id_ex_1_out_45, \单周期硬布线控制器_1_alu_op ;
  wire [4:0] ex_mem_1_p19_3, ex_mem_1_p19_4, ex_mem_1_p19_5, id_ex_1_out_30_2, ID_R1_num, ID_R2_num,
       MEM_WriteReg_num, multiplexer_6_out, multiplexer_8_out, multiplexer_16_out, multiplexer_18_out,
       WB_WriteReg_num;
  wire [5:0] ex_mem_1_p19, ex_mem_1_p19_6, FUNC, OP_CODE;
  wire [10:6] ex_mem_1_p19_2;
  wire [15:0] \LoadUse次数 , \总周期数 , \插入气泡数 , \无条件分支数 , \条件分支成功数 ;
  wire [25:6] if_id_1_out_9;
  wire [26:0] id_ex_1_out_30;
  wire [31:0] A, adder_1_out, adder_2_out, adder_3_out, adder_4_out, B, bit_extender_1_out,
       bit_extender_2_out, EXR1, EXR2, id_ex_1_out_28, id_ex_1_out_34, IR, mem_wb_1_p17, mem_wb_1_p22,
       MEMALU, mips_alu_1_result, mips_regifile_1_r1, mips_regifile_1_r2, multiplexer_1_out,
       multiplexer_2_out, multiplexer_3_out, multiplexer_7_out, multiplexer_13_out, multiplexer_20_out,
       ram_1_data, shifter_1_out, WBALU, WBRD;

  Button \u_总复位  (.out(RST));
  Button _1 (.out(IR1));
  Button _2 (.out(IR2));
  Button _3 (.out(IR3));
  Register #(.width(32), .trigger("rising"), .Select("low")) PC (
    .D(multiplexer_1_out), .en(and_1_out), .Q(IF_PC), .clk(CLK), .clr(RST));
  Multiplexer #(.select(1), .width(32), .disabled("Z"), .enable("false")) multiplexer_1 (
    .in0(multiplexer_3_out), .in1(multiplexer_2_out), .out(multiplexer_1_out), .sel(id_ex_1_out_35));
  Multiplexer #(.select(1), .width(32), .disabled("Z"), .enable("false")) multiplexer_2 (
    .in0({adder_2_out[31:28], id_ex_1_out_30[20:6], id_ex_1_out_30_2, id_ex_1_out_30[5:0], 2'b00}), .in1(A),
    .out(multiplexer_2_out), .sel(id_ex_1_out_36));
  Button \u_继续运行  (.out(Go));
  LED #(.active("true")) led_1 (.in(W1));
  LED #(.active("true")) led_2 (.in(W2));
  LED #(.active("true")) led_3 (.in(W3));
  Hex_Digit_Display hex_digit_display_1 (.value(LedData[31:28]));  // open: dp
  Adder #(.width(32)) adder_1 (.a(IF_PC), .b(32'h4), .out(adder_1_out));  // open: cin, cout
  Multiplexer #(.select(1), .width(32), .disabled("Z"), .enable("false")) multiplexer_3 (
    .in0(adder_1_out), .in1(adder_3_out), .out(multiplexer_3_out), .sel(or_4_out));
  and and_1 (and_1_out, ~END, and_2_out);  // AND_Gate
  Hex_Digit_Display hex_digit_display_2 (.value(LedData[27:24]));  // open: dp
  Hex_Digit_Display hex_digit_display_3 (.value(LedData[23:20]));  // open: dp
  ROM #(.addrWidth(10), .dataWidth(32), .Select("high")) rom_1 (.addr(IF_PC[11:2]), .data(IR));
  \源寄存器使用情况  \u_源寄存器使用情况_1  (
    .OP0(OP_CODE[0]), .OP1(OP_CODE[1]), .OP2(OP_CODE[2]), .OP3(OP_CODE[3]), .OP4(OP_CODE[4]),
    .OP5(OP_CODE[5]), .F0(FUNC[0]), .F1(FUNC[1]), .F2(FUNC[2]), .F3(FUNC[3]), .F4(FUNC[4]), .F5(FUNC[5]),
    .R1_Used(\源寄存器使用情况_1_r1_used ), .R2_Used(\源寄存器使用情况_1_r2_used ));
  Hex_Digit_Display hex_digit_display_4 (.value(LedData[19:16]));  // open: dp
  Hex_Digit_Display hex_digit_display_5 (.value(LedData[15:12]));  // open: dp
  IF_ID if_id_1 (
    .CLK(CLK), .out_9({OP_CODE, if_id_1_out_9, FUNC}), .\同步清零_气泡_高电平有效 (or_3_out),
    .\使能端_低电平有效_stall_高电平有效 (and_1_out), .in_5(IF_PC), .out_11(ID_PC), .in_1(IR));  // open: 传输状态Out_表明当前传输数据有效, in_6, out_12, in_7, out_13, in_8, out_14
  Hex_Digit_Display hex_digit_display_6 (.value(LedData[7:4]));  // open: dp
  Hex_Digit_Display hex_digit_display_7 (.value(LedData[11:8]));  // open: dp
  Clock #(.highDuration(1), .lowDuration(1)) clock_1 (.out(CLK));
  and and_2 (and_2_out, nand_1_out, ~LOADUSE);  // AND_Gate
  Hex_Digit_Display hex_digit_display_8 (.value(LedData[3:0]));  // open: dp
  Multiplexer #(.select(1), .width(5), .disabled("Z"), .enable("false")) multiplexer_4 (
    .in0(if_id_1_out_9[25:21]), .in1(5'b00010), .out(ID_R1_num), .sel(syscall));
  Multiplexer #(.select(1), .width(5), .disabled("Z"), .enable("false")) multiplexer_5 (
    .in0(if_id_1_out_9[20:16]), .in1(5'b00100), .out(ID_R2_num), .sel(syscall));
  Multiplexer #(.select(1), .width(5), .disabled("Z"), .enable("false")) multiplexer_6 (
    .in0(mem_wb_1_p17[20:16]), .in1(mem_wb_1_p17[15:11]), .out(multiplexer_6_out), .sel(mem_wb_1_p13));
  assign bit_extender_1_out = {{16{if_id_1_out_9[15]}}, {if_id_1_out_9[15:6], FUNC}};  // Bit_Extender bit_extender_1
  assign bit_extender_2_out = {{16{1'b0}}, {if_id_1_out_9[15:6], FUNC}};  // Bit_Extender bit_extender_2
  Multiplexer #(.select(1), .width(32), .disabled("Z"), .enable("false")) multiplexer_7 (
    .in0(bit_extender_2_out), .in1(bit_extender_1_out), .out(multiplexer_7_out), .sel(SignedExt));
  or or_1 (or_1_out, nand_1_out, mem_wb_1_p21);
  Multiplexer #(.select(1), .width(5), .disabled("Z"), .enable("false")) multiplexer_8 (
    .in0(multiplexer_6_out), .in1({5{1'b1}}), .out(multiplexer_8_out), .sel(mem_wb_1_p14));
  Shifter #(.width(32), .shift("ll")) shifter_1 (.in(multiplexer_7_out), .\dist (5'b00010), .out(shifter_1_out));
  and and_3 (and_3_out, or_1_out, ~END);  // AND_Gate
  not not_1 (not_1_out, comparator_1_eq);
  Comparator #(.width(5), .mode("twosComplement")) comparator_1 (
    .a(ID_R1_num), .b({5{1'b0}}), .eq(comparator_1_eq));  // open: gt, lt
  Comparator #(.width(5), .mode("twosComplement")) comparator_2 (
    .a(ID_R1_num), .b(WB_WriteReg_num), .eq(comparator_2_eq));  // open: gt, lt
  Comparator #(.width(5), .mode("twosComplement")) comparator_3 (
    .a(ID_R1_num), .b(WB_WriteReg_num), .eq(comparator_3_eq));  // open: gt, lt
  Comparator #(.width(5), .mode("twosComplement")) comparator_4 (
    .a(ID_R2_num), .b({5{1'b0}}), .eq(comparator_4_eq));  // open: gt, lt
  not not_2 (not_2_out, comparator_4_eq);
  Comparator #(.width(5), .mode("twosComplement")) comparator_5 (
    .a(ID_R2_num), .b(WB_WriteReg_num), .eq(comparator_5_eq));  // open: gt, lt
  Comparator #(.width(5), .mode("twosComplement")) comparator_6 (
    .a(ID_R2_num), .b(WB_WriteReg_num), .eq(comparator_6_eq));  // open: gt, lt
  // Probe on \总周期数 
  // Probe on \无条件分支数 
  // Probe on \条件分支成功数 
  // Probe on \插入气泡数 
  // Probe on \LoadUse次数 
  \单周期硬布线控制器  \u_单周期硬布线控制器_1  (
    .Func(FUNC), .OP(OP_CODE), .ALU_OP(\单周期硬布线控制器_1_alu_op ), .MemToReg(\单周期硬布线控制器_1_memtoreg ),
    .MemWrite(\单周期硬布线控制器_1_memwrite ), .ALU_SRC(\单周期硬布线控制器_1_alu_src ), .RegWrite(\单周期硬布线控制器_1_regwrite ),
    .SysCALL(syscall), .SignedExt(SignedExt), .RegDst(\单周期硬布线控制器_1_regdst ), .JR(\单周期硬布线控制器_1_jr ),
    .JMP(\单周期硬布线控制器_1_jmp ), .Beq(\单周期硬布线控制器_1_beq ), .JAL(\单周期硬布线控制器_1_jal ), .Bne(\单周期硬布线控制器_1_bne ));
  Comparator #(.width(32), .mode("twosComplement")) comparator_7 (
    .a(A), .b(32'h22), .eq(comparator_7_eq));  // open: gt, lt
  Comparator #(.width(32), .mode("twosComplement")) comparator_8 (
    .a(mem_wb_1_p22), .b(32'h22), .eq(comparator_8_eq));  // open: gt, lt
  Counter #(.width(16), .max('hffff), .ongoal("wrap"), .trigger("rising"), .behavior("old")) counter_1 (
    .count(and_3_out), .Q(\总周期数 ), .clk(CLK), .clr(RST));  // open: load, D, carry, preset
  // Probe on IF_PC[11:0]
  MIPS_Regifile mips_regifile_1 (
    .Din(RDin), .Clk(CLK), .R1(mips_regifile_1_r1), .R2(mips_regifile_1_r2), .WE(RegWrite),
    .W_num(multiplexer_8_out), .R1_num(ID_R1_num), .R2_num(ID_R2_num));
  and and_4 (and_4_out, comparator_7_eq, EX_syscall);
  and and_5 (and_5_out, mem_wb_1_p21, ~comparator_8_eq);  // AND_Gate
  Comparator #(.width(5), .mode("twosComplement")) comparator_9 (
    .a(ID_R1_num), .b(MEM_WriteReg_num), .eq(comparator_9_eq));  // open: gt, lt
  Comparator #(.width(5), .mode("twosComplement")) comparator_10 (
    .a(ID_R2_num), .b(MEM_WriteReg_num), .eq(comparator_10_eq));  // open: gt, lt
  // Probe on EX_PC[11:0]
  // Probe on ID_PC[11:0]
  nand nand_1 (nand_1_out, and_5_out, ~Go);  // NAND_Gate
  and and_6 (and_6_out, not_1_out, MEM_RegWrite, comparator_9_eq, \源寄存器使用情况_1_r1_used );
  and and_7 (and_7_out, not_1_out, WB_RegWrite, comparator_2_eq, \源寄存器使用情况_1_r1_used );
  and and_8 (and_8_out, not_1_out, WB_RegWrite, MEMTOREG, comparator_3_eq, \源寄存器使用情况_1_r1_used );
  and and_9 (and_9_out, not_2_out, MEM_RegWrite, comparator_10_eq, \源寄存器使用情况_1_r2_used );
  and and_10 (and_10_out, not_2_out, WB_RegWrite, comparator_5_eq, \源寄存器使用情况_1_r2_used );
  and and_11 (and_11_out, not_2_out, WB_RegWrite, MEMTOREG, comparator_6_eq, \源寄存器使用情况_1_r2_used );
  // Probe on M_PC[11:0]
  or or_2 (or_2_out, or_3_out, LOADUSE);
  ID_EX id_ex_1 (
    .CLK(CLK), .in_6({OP_CODE, if_id_1_out_9, FUNC}), .in_7(ID_PC), .in_8(mips_regifile_1_r1),
    .in_9(mips_regifile_1_r2), .in_11(\单周期硬布线控制器_1_jmp ), .in_12(\单周期硬布线控制器_1_jr ),
    .in_13(\单周期硬布线控制器_1_jal ), .in_14(\单周期硬布线控制器_1_alu_src ), .in_15(\单周期硬布线控制器_1_bne ),
    .in_16(\单周期硬布线控制器_1_beq ), .in_17(\单周期硬布线控制器_1_memwrite ), .in_18(\单周期硬布线控制器_1_regwrite ),
    .in_19(\单周期硬布线控制器_1_memtoreg ), .in_21(\单周期硬布线控制器_1_alu_op ), .out_28(id_ex_1_out_28),
    .out_30({id_ex_1_out_30[26:6], id_ex_1_out_30_2, id_ex_1_out_30[5:0]}), .out_31(EX_PC), .out_32(EXR1),
    .out_33(EXR2), .out_35(id_ex_1_out_35), .out_36(id_ex_1_out_36), .out_37(id_ex_1_out_37),
    .out_38(id_ex_1_out_38), .out_39(id_ex_1_out_39), .out_40(id_ex_1_out_40), .out_41(id_ex_1_out_41),
    .out_42(MEM_RegWrite), .out_43(EX_MEMTOREG), .out_45(id_ex_1_out_45), .\同步清零_气泡_高电平有效 (or_2_out),
    .\使能端_低电平有效_stall_高电平有效 (and_12_out), .in_1(multiplexer_7_out), .in_20(\单周期硬布线控制器_1_regdst ),
    .out_44(id_ex_1_out_44), .in_10(shifter_1_out), .out_34(id_ex_1_out_34), .in_22(syscall),
    .out_46(EX_syscall), .in_23(SA), .out_47(EX_FWA), .in_24(SB), .out_48(EX_FWB));  // open: 传输状态Out_表明当前传输数据有效, 异步清零, in_25, out_49, in_26, out_50, in_27, out_51
  and and_12 (and_12_out, ~END, nand_1_out);  // AND_Gate
  Register #(.width(32), .trigger("rising"), .Select("low")) register_1 (
    .D(B), .en(and_4_out), .Q(LedData), .clk(CLK), .clr(RST));
  // Probe on WB_PC[11:0]
  Adder #(.width(32)) adder_2 (.a(EX_PC), .b(32'h4), .out(adder_2_out));  // open: cin, cout
  and and_13 (and_13_out, EX_MEMTOREG, and_6_out);
  Multiplexer #(.select(1), .width(2), .disabled("Z"), .enable("false")) multiplexer_9 (
    .in0(2'b00), .in1(2'b10), .out(multiplexer_9_out), .sel(and_7_out));
  Multiplexer #(.select(1), .width(2), .disabled("Z"), .enable("false")) multiplexer_10 (
    .in0(multiplexer_9_out), .in1(2'b11), .out(multiplexer_10_out), .sel(and_8_out));
  and and_14 (and_14_out, EX_MEMTOREG, and_9_out);
  Multiplexer #(.select(1), .width(2), .disabled("Z"), .enable("false")) multiplexer_11 (
    .in0(2'b00), .in1(2'b10), .out(multiplexer_11_out), .sel(and_10_out));
  Multiplexer #(.select(1), .width(2), .disabled("Z"), .enable("false")) multiplexer_12 (
    .in0(multiplexer_11_out), .in1(2'b11), .out(multiplexer_12_out), .sel(and_11_out));
  Multiplexer #(.select(1), .width(32), .disabled("Z"), .enable("false")) multiplexer_13 (
    .in0(B), .in1(id_ex_1_out_28), .out(multiplexer_13_out), .sel(id_ex_1_out_38));
  Adder #(.width(32)) adder_3 (.a(adder_2_out), .b(id_ex_1_out_34), .out(adder_3_out));  // open: cin, cout
  Multiplexer #(.select(1), .width(2), .disabled("Z"), .enable("false")) multiplexer_14 (
    .in0(multiplexer_10_out), .in1(2'b01), .out(SA), .sel(and_6_out));
  Multiplexer #(.select(1), .width(2), .disabled("Z"), .enable("false")) multiplexer_15 (
    .in0(multiplexer_12_out), .in1(2'b01), .out(SB), .sel(and_9_out));
  or or_3 (or_3_out, id_ex_1_out_35, or_4_out);
  and and_15 (and_15_out, mips_alu_1_equal, id_ex_1_out_40);
  and and_16 (and_16_out, id_ex_1_out_39, ~mips_alu_1_equal);  // AND_Gate
  MIPS_ALU mips_alu_1 (
    .X(A), .Y(multiplexer_13_out), .AluOP(id_ex_1_out_45), .Equal(mips_alu_1_equal),
    .Result(mips_alu_1_result), .shamt(id_ex_1_out_30_2));  // open: Result_2
  Counter #(.width(16), .max('hffff), .ongoal("wrap"), .trigger("rising"), .behavior("old")) counter_2 (
    .count(or_4_out), .Q(\条件分支成功数 ), .clk(CLK), .clr(RST));  // open: load, D, carry, preset
  Counter #(.width(16), .max('hffff), .ongoal("wrap"), .trigger("rising"), .behavior("old")) counter_3 (
    .count(id_ex_1_out_35), .Q(\无条件分支数 ), .clk(CLK), .clr(RST));  // open: load, D, carry, preset
  or or_4 (or_4_out, and_15_out, and_16_out);
  or or_5 (LOADUSE, and_13_out, and_14_out);
  not not_3 (not_3_out, END);
  Multiplexer #(.select(1), .width(5), .disabled("Z"), .enable("false")) multiplexer_16 (
    .in0(id_ex_1_out_30[15:11]), .in1(id_ex_1_out_30[10:6]), .out(multiplexer_16_out), .sel(id_ex_1_out_44));
  // EX_MEM ex_mem_1: pin names not known; wires that end beside it: id_ex_1_out_44, id_ex_1_out_37, EX_MEMTOREG, MEM_RegWrite, id_ex_1_out_41, {id_ex_1_out_30[26:6], id_ex_1_out_30_2, id_ex_1_out_30[5:0]}, EX_PC, mips_alu_1_result, B, EX_syscall, A, not_3_out, CLK, ex_mem_1_p14, ex_mem_1_p15, MEMTOREG, WB_RegWrite, MemWrite, {ex_mem_1_p19_6, ex_mem_1_p19_5, ex_mem_1_p19_4, ex_mem_1_p19_3, ex_mem_1_p19_2, ex_mem_1_p19}, M_PC, MEMALU, MDin, ex_mem_1_p23, ex_mem_1_p24
  Multiplexer #(.select(1), .width(5), .disabled("Z"), .enable("false")) multiplexer_17 (
    .in0(multiplexer_16_out), .in1({5{1'b1}}), .out(MEM_WriteReg_num), .sel(id_ex_1_out_37));
  not not_4 (not_4_out, MemWrite);
  Multiplexer #(.select(1), .width(5), .disabled("Z"), .enable("false")) multiplexer_18 (
    .in0(ex_mem_1_p19_4), .in1(ex_mem_1_p19_3), .out(multiplexer_18_out), .sel(ex_mem_1_p14));
  RAM #(.addrWidth(10), .dataWidth(32), .bus("separate"), .Select("high")) ram_1 (
    .addr(MEMALU[11:2]), .din(MDin), .data(ram_1_data), .str(MemWrite), .clk(CLK), .ld(not_4_out), .clr(RST));  // open: sel
  not not_5 (not_5_out, END);
  Multiplexer #(.select(1), .width(5), .disabled("Z"), .enable("false")) multiplexer_19 (
    .in0(multiplexer_18_out), .in1({5{1'b1}}), .out(WB_WriteReg_num), .sel(ex_mem_1_p15));
  // MEM_WB mem_wb_1: pin names not known; wires that end beside it: ex_mem_1_p14, ex_mem_1_p15, MEMTOREG, WB_RegWrite, {ex_mem_1_p19_6, ex_mem_1_p19_5, ex_mem_1_p19_4, ex_mem_1_p19_3, ex_mem_1_p19_2, ex_mem_1_p19}, M_PC, MEMALU, ram_1_data, ex_mem_1_p23, ex_mem_1_p24, not_5_out, CLK, mem_wb_1_p13, mem_wb_1_p14, mem_wb_1_p15, RegWrite, mem_wb_1_p17, WB_PC, WBALU, WBRD, mem_wb_1_p21, mem_wb_1_p22
  Multiplexer #(.select(1), .width(32), .disabled("Z"), .enable("false")) multiplexer_20 (
    .in0(WBALU), .in1(WBRD), .out(multiplexer_20_out), .sel(mem_wb_1_p15));
  Multiplexer #(.select(1), .width(32), .disabled("Z"), .enable("false")) multiplexer_21 (
    .in0(multiplexer_20_out), .in1(adder_4_out), .out(RDin), .sel(mem_wb_1_p14));
  Adder #(.width(32)) adder_4 (.a(WB_PC), .b(32'h4), .out(adder_4_out));  // open: cin, cout
  Comparator #(.width(16), .mode("twosComplement")) comparator_11 (.a(16'h8fa), .b(\总周期数 ), .eq(END));  // open: gt, lt
  Counter #(.width(16), .max('hffff), .ongoal("wrap"), .trigger("rising"), .behavior("old")) counter_4 (
    .count(LOADUSE), .Q(\LoadUse次数 ), .clk(CLK), .clr(RST));  // open: load, D, carry, preset
  Multiplexer #(.select(2), .width(32), .disabled("Z"), .enable("false")) multiplexer_22 (
    .in0(EXR1), .in1(MEMALU), .in2(WBALU), .in3(WBRD), .out(A), .sel(EX_FWA));
  Multiplexer #(.select(2), .width(32), .disabled("Z"), .enable("false")) multiplexer_23 (
    .in0(EXR2), .in1(MEMALU), .in2(WBALU), .in3(WBRD), .out(B), .sel(EX_FWB));

  // Other names for the same wires on the sheet: MEM_PC[31:0] = M_PC; PC[31:0] = IF_PC

  // Notes on the sheet:
  //   中断源
  //   中断等待指示
  //   总复位信号应将除ROM以外所有存储组件全部清零
  //   指令存储器
  //   指令字
  //   contents of rom_1 (hex, n*v repeats v):
  //   20110001 8000c05 20110001 20120002 20130003 8000c09 20110001 20120002 20130003 8000c0d 20110001
  //   20120002 20130003 8000c11 20110001 20120002 20130003 c000cb8 20100001 20110001 118fc0 112020
  //   20020022 c 118882 12200001 8000c15 112020 20020022 c 20110001 118880 112020 20020022 c 12200001
  //   8000c1f 20110001 118fc0 112020 20020022 c 1188c3 112020 20020022 c 118903 112020 20020022 c 118903
  //   112020 20020022 c 118903 112020 20020022 c 118903 112020 20020022 c 118903 112020 20020022 c 118903
  //   112020 20020022 c 118903 112020 20020022 c 20100001 109fc0 139fc3 8021 2012000c 24160003 26100001
  //   3210000f 20080008 20090001 139900 2709825 132020 20020022 c 1094022 1500fff9 22100001 2018000f
  //   2188024 108700 20080008 20090001 139902 2709825 132021 20020022 c 1094022 1500fff9 108702 2c9b022
  //   12c00001 8000c50 4020 1084027 84400 3508ffff 82021 20020022 c 2010ffff 20110000 ae300000 22100001
  //   22310004 ae300000 22100001 22310004 ae300000 22100001 22310004 ae300000 22100001 22310004 ae300000
  //   22100001 22310004 ae300000 22100001 22310004 ae300000 22100001 22310004 ae300000 22100001 22310004
  //   ae300000 22100001 22310004 ae300000 22100001 22310004 ae300000 22100001 22310004 ae300000 22100001
  //   22310004 ae300000 22100001 22310004 ae300000 22100001 22310004 ae300000 22100001 22310004 ae300000
  //   22100001 22310004 22100001 8020 2011003c 8e130000 8e340000 274402a 11000002 ae330000 ae140000
  //   2231fffc 1611fff8 102020 20020022 c 22100004 2011003c 1611fff2 20020032 c 20100000 22100001 102020
  //   20020022 c 22100002 102020 20020022 c 22100003 102020 20020022 c 22100004 102020 20020022 c 22100005
  //   102020 20020022 c 22100006 102020 20020022 c 22100007 102020 20020022 c 22100008 102020 20020022
  //   20020022 c 3e00008
  //   数码管输出
  //   数码管输出应该用寄存器锁存，否则显示数据只能一闪而过
  //   OP
  //   Func
  //   rs
  //   rt
  //   rd
  //   JMP
  //   JR
  //   OP
  //   Func
  //   Beq
  //   Bne
  //   MemToReg
  //   MemWrite
  //   AluOP
  //   AluSrcB
  //   RegWrite
  //   JAL
  //   RegDst
  //   Syscall
  //   流水调试日志用
  //   OP
  //   rs
  //   rt
  //   rd
  //   为方便自动评测，需要输出流水线各段保存的PC值，注意是PC不是PC+4，另外ID段寄存器写入信息，Mem段内存写入信息也要输出
  //   OP
  //   rs
  //   rt
  //   rd
  //   OP
  //   rs
  //   rt
  //   rd
endmodule

module \扩展指令_流水中断  (
  output RegWrite,
  output MemWrite,
  output [31:0] PC,
  output [31:0] IR,
  output [31:0] RDin,
  output [31:0] MDin
);

  wire and_1_out, and_2_out, and_3_out, and_4_out, and_5_out, and_6_out, and_7_out, and_8_out, and_9_out,
       and_10_out, and_11_out, and_12_out, and_13_out, and_15_out, and_17_out, and_19_out, and_20_out,
       and_21_out, BGEZ, CLK, comparator_1_eq, comparator_2_eq, comparator_3_eq, comparator_4_eq,
       comparator_5_eq, comparator_6_eq, comparator_7_eq, comparator_8_eq, comparator_9_eq, comparator_10_eq,
       comparator_11_eq, comparator_12_eq, comparator_12_gt, comparator_13_eq, comparator_14_eq,
       comparator_15_eq, comparator_16_eq, comparator_17_gt, comparator_18_eq, comparator_19_eq,
       comparator_20_eq, comparator_21_eq, comparator_22_eq, comparator_23_eq, comparator_24_eq,
       comparator_25_eq, comparator_26_gt, comparator_27_eq, \CPU中断请求 , d_ff_1_q, d_ff_2_q, d_ff_3_q,
       demultiplexer_1_out1, demultiplexer_1_out2, demultiplexer_1_out3, ERET, ex_mem_1_out_22,
       ex_mem_1_out_23, ex_mem_1_out_24, \ex_mem_1_传输状态out_表明当前传输数据有效 , EX_MEMTOREG, EX_syscall, Go,
       id_ex_1_out_35, id_ex_1_out_36, id_ex_1_out_37, id_ex_1_out_38, id_ex_1_out_39, id_ex_1_out_40,
       id_ex_1_out_41, id_ex_1_out_44, \id_ex_1_传输状态out_表明当前传输数据有效 , IE, IR1, IR1_q, IR2, IR2_q, IR3, IR3_q,
       LOADUSE, MEM_RegWrite, mem_wb_1_out_19, mem_wb_1_out_20, mem_wb_1_out_21, mem_wb_1_out_22, MEMTOREG,
       MFC0, mips_alu_1_equal, MTC0, nand_1_out, not_1_out, not_2_out, not_3_out, not_4_out, not_5_out,
       not_6_out, or_1_out, or_2_out, or_3_out, or_4_out, or_5_out, or_7_out, or_9_out, or_12_out, or_13_out,
       or_14_out, or_15_out, RST, SignedExt, SLLV, syscall, W1, W2, W3, WB_RegWrite, \单周期硬布线控制器_1_alu_src ,
       \单周期硬布线控制器_1_beq , \单周期硬布线控制器_1_bne , \单周期硬布线控制器_1_jal , \单周期硬布线控制器_1_jmp , \单周期硬布线控制器_1_jr ,
       \单周期硬布线控制器_1_memtoreg , \单周期硬布线控制器_1_memwrite , \单周期硬布线控制器_1_regdst , \单周期硬布线控制器_1_regwrite ,
       \源寄存器使用情况_1_r1_used , \源寄存器使用情况_1_r2_used ;
  wire [1:0] counter_5_q, EX_FWA, EX_FWB, multiplexer_11_out, multiplexer_12_out, multiplexer_13_out,
       multiplexer_14_out, priority_encoder_1_out, register_2_q, SA, SB, subtractor_1_out;
  wire [3:0] id_ex_1_out_45, \单周期硬布线控制器_1_alu_op ;
  wire [4:0] ex_mem_1_out_14_3, ex_mem_1_out_14_4, ex_mem_1_out_14_5, id_ex_1_out_30_2, ID_R1_num, ID_R2_num,
       MEM_WriteReg_num, multiplexer_8_out, multiplexer_10_out, multiplexer_18_out, multiplexer_21_out,
       SHAMT, WB_WriteReg_num;
  wire [5:0] ex_mem_1_out_14, ex_mem_1_out_14_6, FUNC, id_ex_1_out_30_3, OP_CODE;
  wire [10:6] ex_mem_1_out_14_2;
  wire [15:0] \LoadUse次数 , multiplexer_22_out, shifter_1_out, \总周期数 , \无条件分支数 , \条件分支成功数 ;
  wire [25:0] id_ex_1_out_30;
  wire [25:6] if_id_1_out_9;
  wire [31:0] A, adder_1_out, adder_2_out, adder_3_out, adder_4_out, B, bit_extender_1_out,
       bit_extender_2_out, bit_extender_3_out, EPC, EPC_2_q, EPC_3_q, EX_PC, EXR1, EXR2, id_ex_1_out_28,
       id_ex_1_out_34, ID_PC, LedData, MEM_PC, mem_wb_1_out_13, MEMALU, mips_alu_1_result,
       mips_regifile_1_r1, mips_regifile_1_r2, multiplexer_1_out, multiplexer_2_out, multiplexer_3_out,
       multiplexer_4_out, multiplexer_5_out, multiplexer_9_out, multiplexer_17_out, multiplexer_24_out,
       multiplexer_25_out, multiplexer_28_out, multiplexer_30_out, multiplexer_31_out, RDOUT, WB_PC, WBALU,
       WBRD, ZPC;

  Clock #(.highDuration(1), .lowDuration(1)) clock_1 (.out(CLK));
  Button _1 (.out(IR1));
  Button _2 (.out(IR2));
  Button _3 (.out(IR3));
  Button \u_总复位  (.out(RST));
  Register #(.width(32), .trigger("rising"), .Select("low")) u_PC (
    .D(multiplexer_3_out), .en(and_1_out), .Q(PC), .clk(CLK), .clr(RST));
  Multiplexer #(.select(1), .width(32), .disabled("Z"), .enable("false")) multiplexer_1 (
    .in0(multiplexer_5_out), .in1(multiplexer_2_out), .out(multiplexer_1_out), .sel(id_ex_1_out_35));
  Multiplexer #(.select(1), .width(32), .disabled("Z"), .enable("false")) multiplexer_2 (
    .in0({adder_2_out[31:28], id_ex_1_out_30[25:21], id_ex_1_out_30_2, id_ex_1_out_30[15:0], 2'b00}),
    .in1(A), .out(multiplexer_2_out), .sel(id_ex_1_out_36));
  Multiplexer #(.select(1), .width(32), .disabled("Z"), .enable("false")) multiplexer_3 (
    .in0(multiplexer_4_out), .in1(EPC), .out(multiplexer_3_out), .sel(ERET));
  // Probe on multiplexer_3_out
  Button \u_继续运行  (.out(Go));
  LED #(.active("true")) led_1 (.in(W1));
  LED #(.active("true")) led_2 (.in(W2));
  LED #(.active("true")) led_3 (.in(W3));
  Multiplexer #(.select(1), .width(32), .disabled("Z"), .enable("false")) multiplexer_4 (
    .in0(multiplexer_1_out), .in1(ZPC), .out(multiplexer_4_out), .sel(\CPU中断请求 ));
  Hex_Digit_Display hex_digit_display_1 (.value(LedData[31:28]));  // open: dp
  Adder #(.width(32)) adder_1 (.a(PC), .b(32'h4), .out(adder_1_out));  // open: cin, cout
  Multiplexer #(.select(1), .width(32), .disabled("Z"), .enable("false")) multiplexer_5 (
    .in0(adder_1_out), .in1(adder_3_out), .out(multiplexer_5_out), .sel(or_7_out));
  \源寄存器使用情况  \u_源寄存器使用情况_1  (
    .OP0(OP_CODE[0]), .OP1(OP_CODE[1]), .OP2(OP_CODE[2]), .OP3(OP_CODE[3]), .OP4(OP_CODE[4]),
    .OP5(OP_CODE[5]), .F0(FUNC[0]), .F1(FUNC[1]), .F2(FUNC[2]), .F3(FUNC[3]), .F4(FUNC[4]), .F5(FUNC[5]),
    .R1_Used(\源寄存器使用情况_1_r1_used ), .R2_Used(\源寄存器使用情况_1_r2_used ));
  Hex_Digit_Display hex_digit_display_2 (.value(LedData[27:24]));  // open: dp
  Hex_Digit_Display hex_digit_display_3 (.value(LedData[23:20]));  // open: dp
  ROM #(.addrWidth(10), .dataWidth(32), .Select("high")) rom_1 (.addr(PC[11:2]), .data(IR));
  Hex_Digit_Display hex_digit_display_4 (.value(LedData[19:16]));  // open: dp
  Hex_Digit_Display hex_digit_display_5 (.value(LedData[15:12]));  // open: dp
  or or_1 (or_1_out, or_5_out, \CPU中断请求 );
  IF_ID if_id_1 (
    .CLK(CLK), .out_9({OP_CODE, if_id_1_out_9, FUNC}), .\同步清零_气泡_高电平有效 (or_1_out),
    .\使能端_低电平有效_stall_高电平有效 (and_1_out), .in_5(PC), .out_11(ID_PC), .in_1(IR));  // open: 传输状态Out_表明当前传输数据有效, in_6, out_12, in_7, out_13, in_8, out_14
  Hex_Digit_Display hex_digit_display_6 (.value(LedData[7:4]));  // open: dp
  Hex_Digit_Display hex_digit_display_7 (.value(LedData[11:8]));  // open: dp
  and and_1 (and_1_out, nand_1_out, ~LOADUSE);  // AND_Gate
  Comparator #(.width(5), .mode("twosComplement")) comparator_1 (
    .a(ID_R1_num), .b({5{1'b0}}), .eq(comparator_1_eq));  // open: gt, lt
  Comparator #(.width(5), .mode("twosComplement")) comparator_2 (
    .a(ID_R1_num), .b(WB_WriteReg_num), .eq(comparator_2_eq));  // open: gt, lt
  Comparator #(.width(5), .mode("twosComplement")) comparator_3 (
    .a(ID_R2_num), .b({5{1'b0}}), .eq(comparator_3_eq));  // open: gt, lt
  Comparator #(.width(5), .mode("twosComplement")) comparator_4 (
    .a(ID_R2_num), .b(WB_WriteReg_num), .eq(comparator_4_eq));  // open: gt, lt
  Hex_Digit_Display hex_digit_display_8 (.value(LedData[3:0]));  // open: dp
  // Probe on \总周期数 
  Multiplexer #(.select(1), .width(5), .disabled("Z"), .enable("false")) multiplexer_6 (
    .in0(if_id_1_out_9[25:21]), .in1(5'b00010), .out(ID_R1_num), .sel(syscall));
  Multiplexer #(.select(1), .width(5), .disabled("Z"), .enable("false")) multiplexer_7 (
    .in0(if_id_1_out_9[20:16]), .in1(5'b00100), .out(ID_R2_num), .sel(syscall));
  Multiplexer #(.select(1), .width(5), .disabled("Z"), .enable("false")) multiplexer_8 (
    .in0(mem_wb_1_out_13[20:16]), .in1(mem_wb_1_out_13[15:11]), .out(multiplexer_8_out), .sel(mem_wb_1_out_20));
  assign bit_extender_1_out = {{16{if_id_1_out_9[15]}}, {if_id_1_out_9[15:6], FUNC}};  // Bit_Extender bit_extender_1
  assign bit_extender_2_out = {{16{1'b0}}, {if_id_1_out_9[15:6], FUNC}};  // Bit_Extender bit_extender_2
  Multiplexer #(.select(1), .width(32), .disabled("Z"), .enable("false")) multiplexer_9 (
    .in0(bit_extender_2_out), .in1(bit_extender_1_out), .out(multiplexer_9_out), .sel(SignedExt));
  not not_1 (not_1_out, comparator_1_eq);
  Comparator #(.width(5), .mode("twosComplement")) comparator_5 (
    .a(ID_R1_num), .b(WB_WriteReg_num), .eq(comparator_5_eq));  // open: gt, lt
  not not_2 (not_2_out, comparator_3_eq);
  Comparator #(.width(5), .mode("twosComplement")) comparator_6 (
    .a(ID_R2_num), .b(WB_WriteReg_num), .eq(comparator_6_eq));  // open: gt, lt
  Multiplexer #(.select(1), .width(5), .disabled("Z"), .enable("false")) multiplexer_10 (
    .in0(multiplexer_8_out), .in1({5{1'b1}}), .out(multiplexer_10_out), .sel(mem_wb_1_out_21));
  Shifter #(.width(16), .shift("ll")) shifter_1 (
    .in({if_id_1_out_9[15:6], FUNC}), .\dist (4'b0010), .out(shifter_1_out));
  or or_2 (or_2_out, nand_1_out, ~mem_wb_1_out_22);  // OR_Gate
  \单周期硬布线控制器  \u_单周期硬布线控制器_1  (
    .Func(FUNC), .OP(OP_CODE), .ALU_OP(\单周期硬布线控制器_1_alu_op ), .MemToReg(\单周期硬布线控制器_1_memtoreg ),
    .MemWrite(\单周期硬布线控制器_1_memwrite ), .ALU_SRC(\单周期硬布线控制器_1_alu_src ), .RegWrite(\单周期硬布线控制器_1_regwrite ),
    .SysCALL(syscall), .SignedExt(SignedExt), .RegDst(\单周期硬布线控制器_1_regdst ), .JR(\单周期硬布线控制器_1_jr ),
    .JMP(\单周期硬布线控制器_1_jmp ), .Beq(\单周期硬布线控制器_1_beq ), .JAL(\单周期硬布线控制器_1_jal ), .Bne(\单周期硬布线控制器_1_bne ));
  assign bit_extender_3_out = {{16{shifter_1_out[15]}}, shifter_1_out};  // Bit_Extender bit_extender_3
  Comparator #(.width(32), .mode("twosComplement")) comparator_7 (
    .a(A), .b(32'h22), .eq(comparator_7_eq));  // open: gt, lt
  Counter #(.width(16), .max('hffff), .ongoal("wrap"), .trigger("rising"), .behavior("old")) counter_1 (
    .count(or_2_out), .Q(\总周期数 ), .clk(CLK), .clr(RST));  // open: load, D, carry, preset
  Comparator #(.width(5), .mode("twosComplement")) comparator_8 (
    .a(ID_R1_num), .b(MEM_WriteReg_num), .eq(comparator_8_eq));  // open: gt, lt
  Comparator #(.width(5), .mode("twosComplement")) comparator_9 (
    .a(ID_R2_num), .b(MEM_WriteReg_num), .eq(comparator_9_eq));  // open: gt, lt
  MIPS_Regifile mips_regifile_1 (
    .Din(RDin), .Clk(CLK), .R1(mips_regifile_1_r1), .R2(mips_regifile_1_r2), .WE(RegWrite),
    .W_num(multiplexer_10_out), .R1_num(ID_R1_num), .R2_num(ID_R2_num));
  and and_2 (and_2_out, comparator_7_eq, EX_syscall);
  and and_3 (and_3_out, EX_syscall, ~comparator_7_eq);  // AND_Gate
  and and_4 (and_4_out, not_1_out, MEM_RegWrite, comparator_8_eq, \源寄存器使用情况_1_r1_used );
  and and_5 (and_5_out, not_1_out, WB_RegWrite, comparator_2_eq, \源寄存器使用情况_1_r1_used );
  and and_6 (and_6_out, not_1_out, WB_RegWrite, MEMTOREG, comparator_5_eq, \源寄存器使用情况_1_r1_used );
  and and_7 (and_7_out, not_2_out, MEM_RegWrite, comparator_9_eq, \源寄存器使用情况_1_r2_used );
  and and_8 (and_8_out, not_2_out, WB_RegWrite, comparator_4_eq, \源寄存器使用情况_1_r2_used );
  and and_9 (and_9_out, not_2_out, WB_RegWrite, MEMTOREG, comparator_6_eq, \源寄存器使用情况_1_r2_used );
  nand nand_1 (nand_1_out, and_3_out, ~Go);  // NAND_Gate
  Multiplexer #(.select(1), .width(2), .disabled("Z"), .enable("false")) multiplexer_11 (
    .in0(2'b00), .in1(2'b10), .out(multiplexer_11_out), .sel(and_5_out));
  Multiplexer #(.select(1), .width(2), .disabled("Z"), .enable("false")) multiplexer_12 (
    .in0(2'b00), .in1(2'b10), .out(multiplexer_12_out), .sel(and_8_out));
  or or_3 (or_3_out, or_5_out, \CPU中断请求 , LOADUSE);
  ID_EX id_ex_1 (
    .CLK(CLK), .in_6({OP_CODE, if_id_1_out_9, FUNC}), .in_7(ID_PC), .in_8(mips_regifile_1_r1),
    .in_9(mips_regifile_1_r2), .in_11(\单周期硬布线控制器_1_jmp ), .in_12(\单周期硬布线控制器_1_jr ),
    .in_13(\单周期硬布线控制器_1_jal ), .in_14(\单周期硬布线控制器_1_alu_src ), .in_15(\单周期硬布线控制器_1_bne ),
    .in_16(\单周期硬布线控制器_1_beq ), .in_17(\单周期硬布线控制器_1_memwrite ), .in_18(\单周期硬布线控制器_1_regwrite ),
    .in_19(\单周期硬布线控制器_1_memtoreg ), .in_21(\单周期硬布线控制器_1_alu_op ), .out_28(id_ex_1_out_28),
    .\传输状态Out_表明当前传输数据有效 (\id_ex_1_传输状态out_表明当前传输数据有效 ),
    .out_30({id_ex_1_out_30_3, id_ex_1_out_30[25:21], id_ex_1_out_30_2, id_ex_1_out_30[15:0]}),
    .out_31(EX_PC), .out_32(EXR1), .out_33(EXR2), .out_35(id_ex_1_out_35), .out_36(id_ex_1_out_36),
    .out_37(id_ex_1_out_37), .out_38(id_ex_1_out_38), .out_39(id_ex_1_out_39), .out_40(id_ex_1_out_40),
    .out_41(id_ex_1_out_41), .out_42(MEM_RegWrite), .out_43(EX_MEMTOREG), .out_45(id_ex_1_out_45),
    .\同步清零_气泡_高电平有效 (or_3_out), .\使能端_低电平有效_stall_高电平有效 (nand_1_out), .in_1(multiplexer_9_out),
    .in_20(\单周期硬布线控制器_1_regdst ), .out_44(id_ex_1_out_44), .in_10(bit_extender_3_out),
    .out_34(id_ex_1_out_34), .in_22(syscall), .out_46(EX_syscall), .in_23(SA), .out_47(EX_FWA), .in_24(SB),
    .out_48(EX_FWB), .\异步清零 (\CPU中断请求 ));  // open: in_25, out_49, in_26, out_50, in_27, out_51
  Register #(.width(32), .trigger("rising"), .Select("low")) register_1 (
    .D(B), .en(and_2_out), .Q(LedData), .clk(CLK), .clr(RST));
  Counter #(.width(16), .max('hffff), .ongoal("wrap"), .trigger("rising"), .behavior("old")) counter_2 (
    .count(id_ex_1_out_35), .Q(\无条件分支数 ), .clk(CLK), .clr(RST));  // open: load, D, carry, preset
  and and_10 (and_10_out, EX_MEMTOREG, and_4_out);
  Multiplexer #(.select(1), .width(2), .disabled("Z"), .enable("false")) multiplexer_13 (
    .in0(multiplexer_11_out), .in1(2'b11), .out(multiplexer_13_out), .sel(and_6_out));
  and and_11 (and_11_out, EX_MEMTOREG, and_7_out);
  Multiplexer #(.select(1), .width(2), .disabled("Z"), .enable("false")) multiplexer_14 (
    .in0(multiplexer_12_out), .in1(2'b11), .out(multiplexer_14_out), .sel(and_9_out));
  Adder #(.width(32)) adder_2 (.a(EX_PC), .b(32'h4), .out(adder_2_out));  // open: cin, cout
  Multiplexer #(.select(1), .width(2), .disabled("Z"), .enable("false")) multiplexer_15 (
    .in0(multiplexer_13_out), .in1(2'b01), .out(SA), .sel(and_4_out));
  Multiplexer #(.select(1), .width(2), .disabled("Z"), .enable("false")) multiplexer_16 (
    .in0(multiplexer_14_out), .in1(2'b01), .out(SB), .sel(and_7_out));
  Multiplexer #(.select(1), .width(32), .disabled("Z"), .enable("false")) multiplexer_17 (
    .in0(B), .in1(id_ex_1_out_28), .out(multiplexer_17_out), .sel(id_ex_1_out_38));
  Adder #(.width(32)) adder_3 (.a(adder_2_out), .b(id_ex_1_out_34), .out(adder_3_out));  // open: cin, cout
  Counter #(.width(16), .max('hffff), .ongoal("wrap"), .trigger("rising"), .behavior("old")) counter_3 (
    .count(or_7_out), .Q(\条件分支成功数 ), .clk(CLK), .clr(RST));  // open: load, D, carry, preset
  Comparator #(.width(6), .mode("twosComplement")) comparator_10 (
    .a(id_ex_1_out_30_3), .b(6'b000001), .eq(comparator_10_eq));  // open: gt, lt
  Comparator #(.width(5), .mode("twosComplement")) comparator_11 (
    .a(5'b00001), .b(id_ex_1_out_30_2), .eq(comparator_11_eq));  // open: gt, lt
  Comparator #(.width(32), .mode("twosComplement")) comparator_12 (
    .a(A), .b({32{1'b0}}), .gt(comparator_12_gt), .eq(comparator_12_eq));  // open: lt
  or or_4 (or_4_out, comparator_12_gt, comparator_12_eq);
  or or_5 (or_5_out, id_ex_1_out_35, or_7_out);
  and and_12 (and_12_out, mips_alu_1_equal, id_ex_1_out_40);
  and and_13 (and_13_out, id_ex_1_out_39, ~mips_alu_1_equal);  // AND_Gate
  MIPS_ALU mips_alu_1 (
    .X(A), .Y(multiplexer_17_out), .AluOP(id_ex_1_out_45), .Equal(mips_alu_1_equal),
    .Result(mips_alu_1_result), .shamt(SHAMT));  // open: Result_2
  and and_14 (BGEZ, comparator_10_eq, comparator_11_eq);
  or or_6 (LOADUSE, and_10_out, and_11_out);
  and and_15 (and_15_out, BGEZ, or_4_out);
  or or_7 (or_7_out, and_12_out, and_15_out, and_13_out);
  // Probe on ID_PC[11:0]
  // Probe on PC[11:0]
  // Probe on EX_PC[11:0]
  Multiplexer #(.select(1), .width(5), .disabled("Z"), .enable("false")) multiplexer_18 (
    .in0(id_ex_1_out_30_2), .in1(id_ex_1_out_30[15:11]), .out(multiplexer_18_out), .sel(id_ex_1_out_44));
  Comparator #(.width(6), .mode("twosComplement")) comparator_13 (
    .a(id_ex_1_out_30_3), .b({6{1'b0}}), .eq(comparator_13_eq));  // open: gt, lt
  Comparator #(.width(6), .mode("twosComplement")) comparator_14 (
    .a(id_ex_1_out_30[5:0]), .b(6'b000100), .eq(comparator_14_eq));  // open: gt, lt
  // Probe on MEM_PC[11:0]
  // Probe on WB_PC[11:0]
  EX_MEM ex_mem_1 (
    .in_1({id_ex_1_out_30_3, id_ex_1_out_30[25:21], id_ex_1_out_30_2, id_ex_1_out_30[15:0]}), .CLK(CLK),
    .in_4(EX_PC), .in_5(mips_alu_1_result), .in_6(B), .in_7(id_ex_1_out_41), .in_8(MEM_RegWrite),
    .in_9(EX_MEMTOREG), .in_10(id_ex_1_out_44),
    .out_14({ex_mem_1_out_14_6, ex_mem_1_out_14_5, ex_mem_1_out_14_4, ex_mem_1_out_14_3, ex_mem_1_out_14_2, ex_mem_1_out_14}),
    .\传输状态Out_表明当前传输数据有效 (\ex_mem_1_传输状态out_表明当前传输数据有效 ), .out_16(MEM_PC), .out_17(MEMALU), .out_18(MDin),
    .out_19(MemWrite), .out_20(WB_RegWrite), .out_21(MEMTOREG), .out_22(ex_mem_1_out_22),
    .\同步清零_气泡_高电平有效 (\CPU中断请求 ), .\使能端_低电平有效_stall_高电平有效 (\id_ex_1_传输状态out_表明当前传输数据有效 ),
    .in_11(id_ex_1_out_37), .out_23(ex_mem_1_out_23), .in_13(EX_syscall), .out_24(ex_mem_1_out_24));
  Multiplexer #(.select(1), .width(5), .disabled("Z"), .enable("false")) multiplexer_19 (
    .in0(multiplexer_18_out), .in1({5{1'b1}}), .out(MEM_WriteReg_num), .sel(id_ex_1_out_37));
  and and_16 (SLLV, comparator_13_eq, comparator_14_eq);
  Multiplexer #(.select(1), .width(5), .disabled("Z"), .enable("false")) multiplexer_20 (
    .in0(id_ex_1_out_30[10:6]), .in1(A[4:0]), .out(SHAMT), .sel(SLLV));
  not not_3 (not_3_out, MemWrite);
  Comparator #(.width(6), .mode("twosComplement")) comparator_15 (
    .a(ex_mem_1_out_14_6), .b(6'b100101), .eq(comparator_15_eq));  // open: gt, lt
  Multiplexer #(.select(1), .width(5), .disabled("Z"), .enable("false")) multiplexer_21 (
    .in0(ex_mem_1_out_14_4), .in1(ex_mem_1_out_14_3), .out(multiplexer_21_out), .sel(ex_mem_1_out_22));
  // Probe on \总周期数 
  // Probe on \无条件分支数 
  // Probe on \条件分支成功数 
  // Probe on \LoadUse次数 
  RAM #(.addrWidth(11), .dataWidth(32), .bus("separate"), .Select("high")) ram_1 (
    .addr(MEMALU[12:2]), .din(MDin), .data(RDOUT), .str(MemWrite), .clk(CLK), .ld(not_3_out), .clr(RST));  // open: sel
  Multiplexer #(.select(1), .width(16), .disabled("Z"), .enable("false")) multiplexer_22 (
    .in0(RDOUT[15:0]), .in1(RDOUT[31:16]), .out(multiplexer_22_out), .sel(MEMALU[1]));
  Multiplexer #(.select(1), .width(5), .disabled("Z"), .enable("false")) multiplexer_23 (
    .in0(multiplexer_21_out), .in1({5{1'b1}}), .out(WB_WriteReg_num), .sel(ex_mem_1_out_23));
  MEM_WB mem_wb_1 (
    .in_1({ex_mem_1_out_14_6, ex_mem_1_out_14_5, ex_mem_1_out_14_4, ex_mem_1_out_14_3, ex_mem_1_out_14_2, ex_mem_1_out_14}),
    .CLK(CLK), .in_4(MEM_PC), .in_5(MEMALU), .in_6(multiplexer_24_out), .in_7(WB_RegWrite), .in_8(MEMTOREG),
    .in_9(ex_mem_1_out_22), .out_13(mem_wb_1_out_13), .out_15(WB_PC), .out_16(WBALU), .out_17(WBRD),
    .out_18(RegWrite), .out_19(mem_wb_1_out_19), .out_20(mem_wb_1_out_20), .\同步清零_气泡_高电平有效 (\CPU中断请求 ),
    .\使能端_低电平有效_stall_高电平有效 (\ex_mem_1_传输状态out_表明当前传输数据有效 ), .in_10(ex_mem_1_out_23),
    .out_21(mem_wb_1_out_21), .in_12(ex_mem_1_out_24), .out_22(mem_wb_1_out_22));  // open: 传输状态Out_表明当前传输数据有效
  Multiplexer #(.select(1), .width(32), .disabled("Z"), .enable("false")) multiplexer_24 (
    .in0(RDOUT), .in1({{16{1'b0}}, multiplexer_22_out}), .out(multiplexer_24_out), .sel(comparator_15_eq));
  Counter #(.width(16), .max('hffff), .ongoal("wrap"), .trigger("rising"), .behavior("old")) counter_4 (
    .count(LOADUSE), .Q(\LoadUse次数 ), .clk(CLK), .clr(RST));  // open: load, D, carry, preset
  Multiplexer #(.select(1), .width(32), .disabled("Z"), .enable("false")) multiplexer_25 (
    .in0(WBALU), .in1(WBRD), .out(multiplexer_25_out), .sel(mem_wb_1_out_19));
  Multiplexer #(.select(1), .width(32), .disabled("Z"), .enable("false")) multiplexer_26 (
    .in0(multiplexer_25_out), .in1(adder_4_out), .out(RDin), .sel(mem_wb_1_out_21));
  Adder #(.width(32)) adder_4 (.a(WB_PC), .b(32'h4), .out(adder_4_out));  // open: cin, cout
  Comparator #(.width(4), .mode("unsigned")) comparator_16 (
    .a(4'b1100), .b(PC[11:8]), .eq(comparator_16_eq));  // open: gt, lt
  not not_4 (not_4_out, comparator_17_gt);
  Comparator #(.width(4), .mode("unsigned")) comparator_17 (
    .a(PC[15:12]), .b(4'b0011), .gt(comparator_17_gt));  // open: eq, lt
  Comparator #(.width(4), .mode("unsigned")) comparator_18 (
    .a(WB_PC[11:8]), .b(4'b1100), .eq(comparator_18_eq));  // open: gt, lt
  Comparator #(.width(4), .mode("unsigned")) comparator_19 (
    .a(WB_PC[15:12]), .b(4'b0000), .eq(comparator_19_eq));  // open: gt, lt
  not not_5 (not_5_out, comparator_16_eq);
  and and_17 (and_17_out, not_4_out, not_5_out, comparator_18_eq, comparator_19_eq);
  Multiplexer #(.select(2), .width(32), .disabled("Z"), .enable("false")) multiplexer_27 (
    .in0(EXR1), .in1(MEMALU), .in2(WBALU), .in3(WBRD), .out(A), .sel(EX_FWA));
  or or_8 (W1, IR1_q, d_ff_1_q);
  Comparator #(.width(6), .mode("twosComplement")) comparator_20 (
    .a(mem_wb_1_out_13[31:26]), .b(6'b010000), .eq(comparator_20_eq));  // open: gt, lt
  and and_18 (ERET, comparator_20_eq, comparator_21_eq);
  Comparator #(.width(6), .mode("twosComplement")) comparator_21 (
    .a(mem_wb_1_out_13[5:0]), .b(6'b011000), .eq(comparator_21_eq));  // open: gt, lt
  or or_9 (or_9_out, \CPU中断请求 , ERET);
  D_Flip_Flop #(.trigger("rising"), .Pre_Clr_Positions("LEGACY"), .NegatePresetClear("false"), .enable("true"), .NewFFLayout("false")) d_ff_1 (
    .clk(IR1), .D(1'b1), .Q(d_ff_1_q), .reset(IR1_q));  // open: Qn, preset, en
  D_Flip_Flop #(.trigger("rising"), .Pre_Clr_Positions("LEGACY"), .NegatePresetClear("false"), .enable("true"), .NewFFLayout("false")) d_ff_2 (
    .clk(IR2), .D(1'b1), .Q(d_ff_2_q), .reset(IR2_q));  // open: Qn, preset, en
  or or_10 (W2, IR2_q, d_ff_2_q);
  D_Flip_Flop #(.trigger("rising"), .Pre_Clr_Positions("LEGACY"), .NegatePresetClear("false"), .enable("true"), .NewFFLayout("false")) d_ff_3 (
    .clk(IR3), .D(1'b1), .Q(d_ff_3_q), .reset(IR3_q));  // open: Qn, preset, en
  or or_11 (W3, IR3_q, d_ff_3_q);
  Multiplexer #(.select(1), .width(32), .disabled("Z"), .enable("false")) multiplexer_28 (
    .in0(WB_PC), .in1(PC), .out(multiplexer_28_out), .sel(and_17_out));
  or or_12 (or_12_out, d_ff_1_q, IR1_q);
  or or_13 (or_13_out, d_ff_3_q, IR3_q);
  Comparator #(.width(6), .mode("twosComplement")) comparator_22 (
    .a(mem_wb_1_out_13[31:26]), .b(6'b010000), .eq(comparator_22_eq));  // open: gt, lt
  Comparator #(.width(5), .mode("twosComplement")) comparator_23 (
    .a(mem_wb_1_out_13[25:21]), .b(5'b00100), .eq(comparator_23_eq));  // open: gt, lt
  Multiplexer #(.select(2), .width(32), .disabled("Z"), .enable("false")) multiplexer_29 (
    .in0(EXR2), .in1(MEMALU), .in2(WBALU), .in3(WBRD), .out(B), .sel(EX_FWB));
  and and_19 (and_19_out, or_12_out, ~demultiplexer_1_out1);  // AND_Gate
  or or_14 (or_14_out, d_ff_2_q, IR2_q);
  and and_20 (and_20_out, or_14_out, ~demultiplexer_1_out2);  // AND_Gate
  and and_21 (and_21_out, or_13_out, ~demultiplexer_1_out3);  // AND_Gate
  and and_22 (MTC0, comparator_22_eq, comparator_23_eq);
  Comparator #(.width(6), .mode("twosComplement")) comparator_24 (
    .a(mem_wb_1_out_13[31:26]), .b(6'b010000), .eq(comparator_24_eq));  // open: gt, lt
  Comparator #(.width(5), .mode("twosComplement")) comparator_25 (
    .a(mem_wb_1_out_13[25:21]), .b({5{1'b0}}), .eq(comparator_25_eq));  // open: gt, lt
  Multiplexer #(.select(1), .width(32), .disabled("Z"), .enable("false")) multiplexer_30 (
    .in0(EPC_2_q), .in1(multiplexer_28_out), .out(multiplexer_30_out), .sel(\CPU中断请求 ));
  Register #(.width(32), .trigger("rising"), .Select("low")) u_EPC (
    .D(multiplexer_30_out), .en(or_9_out), .Q(EPC), .clk(CLK));  // open: clr
  // Probe on EPC
  D_Flip_Flop #(.trigger("rising"), .Pre_Clr_Positions("LEGACY"), .NegatePresetClear("false"), .enable("true"), .NewFFLayout("false")) u_IR1 (
    .clk(CLK), .D(and_19_out), .Q(IR1_q));  // open: Qn, preset, en, reset
  D_Flip_Flop #(.trigger("rising"), .Pre_Clr_Positions("LEGACY"), .NegatePresetClear("false"), .enable("true"), .NewFFLayout("false")) u_IR2 (
    .clk(CLK), .D(and_20_out), .Q(IR2_q));  // open: Qn, preset, en, reset
  D_Flip_Flop #(.trigger("rising"), .Pre_Clr_Positions("LEGACY"), .NegatePresetClear("false"), .enable("true"), .NewFFLayout("false")) u_IR3 (
    .clk(CLK), .D(and_21_out), .Q(IR3_q));  // open: Qn, preset, en, reset
  and and_23 (MFC0, comparator_24_eq, comparator_25_eq);
  Register #(.width(1), .trigger("rising"), .Select("low")) u_IE (
    .D(\CPU中断请求 ), .en(not_6_out), .Q(IE), .clk(CLK), .clr(or_15_out), .preset(MTC0));  // open: cs
  not not_6 (not_6_out, IE);
  Register #(.width(32), .trigger("rising"), .Select("low")) EPC_2 (
    .D(multiplexer_31_out), .en(or_9_out), .Q(EPC_2_q), .clk(CLK));  // open: clr
  Multiplexer #(.select(1), .width(32), .disabled("Z"), .enable("false")) multiplexer_31 (
    .in0(EPC_3_q), .in1(EPC), .out(multiplexer_31_out), .sel(\CPU中断请求 ));
  // Probe on EPC_2_q
  Demultiplexer #(.select(2), .width(1), .tristate("false"), .disabled("Z"), .enable("false")) demultiplexer_1 (
    .out1(demultiplexer_1_out1), .out2(demultiplexer_1_out2), .out3(demultiplexer_1_out3), .in(ERET),
    .sel(priority_encoder_1_out));  // open: out0
  Priority_Encoder #(.select(2), .disabled("Z")) priority_encoder_1 (
    .in0(1'b1), .in1(IR1_q), .in2(IR2_q), .in3(IR3_q), .out(priority_encoder_1_out));  // open: gs, en_out, en_in
  and and_24 (\CPU中断请求 , comparator_26_gt, ~IE);  // AND_Gate
  or or_15 (or_15_out, ERET, MFC0);
  Register #(.width(32), .trigger("rising"), .Select("low")) EPC_3 (
    .D(EPC_2_q), .en(or_9_out), .Q(EPC_3_q), .clk(CLK));  // open: clr
  Multiplexer #(.select(2), .width(32), .disabled("Z"), .enable("false")) multiplexer_32 (
    .in1(32'hc00), .in2(32'hc80), .in3(32'hd00), .out(ZPC), .sel(priority_encoder_1_out));  // open: in0
  Register #(.width(2), .trigger("rising"), .Select("low")) register_2 (
    .D(priority_encoder_1_out), .Q(register_2_q), .clk(CLK), .clr(comparator_27_eq));  // open: en
  Counter #(.width(2), .max('h3), .ongoal("wrap"), .trigger("rising"), .behavior("old")) counter_5 (
    .load(ERET), .D(subtractor_1_out), .count(\CPU中断请求 ), .Q(counter_5_q), .clk(CLK));  // open: carry, clr, preset
  Subtractor #(.width(2)) subtractor_1 (.a(counter_5_q), .b(2'b01), .out(subtractor_1_out));  // open: bin, bout
  Comparator #(.width(2), .mode("unsigned")) comparator_26 (
    .a(priority_encoder_1_out), .b(register_2_q), .gt(comparator_26_gt));  // open: eq, lt
  Comparator #(.width(2), .mode("twosComplement")) comparator_27 (
    .a(2'b00), .b(counter_5_q), .eq(comparator_27_eq));  // open: gt, lt

  // Other names for the same wires on the sheet: IF_PC[31:0] = PC

  // Notes on the sheet:
  //   中断源
  //   中断等待指示
  //   总复位信号应将除ROM以外所有存储组件全部清零
  //   指令存储器
  //   指令字
  //   contents of rom_1 (hex, n*v repeats v):
  //   20110001 8000c05 20110001 20120002 20130003 8000c09 20110001 20120002 20130003 8000c0d 20110001
  //   20120002 20130003 8000c11 20110001 20120002 20130003 c000cf8 20100001 20110001 118fc0 112020
  //   20020022 c 118882 12200001 8000c15 112020 20020022 c 20110001 118880 112020 20020022 c 12200001
  //   8000c1f 20110001 118fc0 112020 20020022 c 1188c3 112020 20020022 c 118903 112020 20020022 c 118903
  //   112020 20020022 c 118903 112020 20020022 c 118903 112020 20020022 c 118903 112020 20020022 c 118903
  //   112020 20020022 c 118903 112020 20020022 c 20100001 109fc0 139fc3 8021 2012000c 24160003 26100001
  //   3210000f 20080008 20090001 139900 2709825 132020 20020022 c 1094022 1500fff9 22100001 2018000f
  //   2188024 108700 20080008 20090001 139902 2709825 132021 20020022 c 1094022 1500fff9 108702 2c9b022
  //   12c00001 8000c50 4020 1084027 84400 3508ffff 82021 20020022 c 2010ffff 20110000 ae300000 22100001
  //   22310004 ae300000 22100001 22310004 ae300000 22100001 22310004 ae300000 22100001 22310004 ae300000
  //   22100001 22310004 ae300000 22100001 22310004 ae300000 22100001 22310004 ae300000 22100001 22310004
  //   ae300000 22100001 22310004 ae300000 22100001 22310004 ae300000 22100001 22310004 ae300000 22100001
  //   22310004 ae300000 22100001 22310004 ae300000 22100001 22310004 ae300000 22100001 22310004 ae300000
  //   22100001 22310004 22100001 8020 2011003c 8e130000 8e340000 274402a 11000002 ae330000 ae140000
  //   2231fffc 1611fff8 102020 20020022 c 22100004 2011003c 1611fff2 20020032 c 20080001 20090003 20110876
  //   112020 20020022 c 200b0008 1118804 1318804 112020 20020022 c 216bffff 1560fff9 2002000a c 2008ffff
  //   20117777 112020 20020022 c 200b0010 3a31ffff 112020 20020022 c 216bffff 1560fffa 2002000a c 20090000
  //   200b0010 34118483 20120404 118c00 129400 36318281 22520404 ad310000 2328820 21290004 216bffff
  //   1560fffb 200b0020 20090000 95310000 112020 20020022 c 21290002 216bffff 1560fff9 2002000a c 2011000f
  //   112020 20020022 c 2231ffff 621fffb 2002000a c 2002000a c 20100000 22100001 102020 20020022 c
  //   22100002 102020 20020022 c 22100003 102020 20020022 c 22100004 102020 20020022 c 22100005 102020
  //   20020022 c 22100006 102020 20020022 c 22100007 102020 20020022 c 22100008 102020 20020022 20020022 c
  //   3e00008
  //   数码管输出
  //   数码管输出应该用寄存器锁存，否则显示数据只能一闪而过
  //   OP
  //   Func
  //   rs
  //   rt
  //   rd
  //   JMP
  //   JR
  //   OP
  //   Func
  //   Beq
  //   Bne
  //   MemToReg
  //   MemWrite
  //   AluOP
  //   AluSrcB
  //   RegWrite
  //   JAL
  //   RegDst
  //   Syscall
  //   为方便自动评测，需要输出PC，IR，寄存器文件写入端口RDin，内存写入端口MDin等信号
  //   OP
  //   rs
  //   rt
  //   rd
  //   OP
  //   rs
  //   rt
  //   rd
  //   OP
  //   rs
  //   rt
  //   rd
  //   Reset 
  //   Reset 
  //   Reset 
endmodule
module \动态分支预测_流水中断  (
  output RegWrite,
  output MemWrite,
  output [31:0] PC,
  output [31:0] IR,
  output [31:0] RDin,
  output [31:0] MDin
);

  wire and_1_out, and_2_out, and_3_out, and_4_out, and_5_out, and_6_out, and_7_out, and_8_out, and_10_out,
       and_11_out, and_12_out, and_13_out, and_15_out, and_16_out, and_18_out, and_19_out, and_20_out,
       and_21_out, and_22_out, and_23_out, and_24_out, and_25_out, and_26_out, and_28_out, and_29_out, BGEZ,
       bht_1_miss, CLK, comparator_1_eq, comparator_2_eq, comparator_3_eq, comparator_4_eq, comparator_4_gt,
       comparator_5_eq, comparator_6_eq, comparator_7_eq, comparator_8_eq, comparator_9_gt, comparator_10_eq,
       comparator_11_eq, comparator_12_eq, comparator_13_eq, comparator_14_eq, comparator_15_eq,
       comparator_16_eq, comparator_17_eq, comparator_18_eq, comparator_19_eq, comparator_20_eq,
       comparator_21_eq, comparator_22_eq, comparator_23_eq, comparator_24_eq, comparator_25_eq,
       comparator_26_gt, comparator_27_eq, \CPU中断请求 , d_ff_1_q, d_ff_2_q, d_ff_3_q, demultiplexer_1_out1,
       demultiplexer_1_out2, demultiplexer_1_out3, ERET, EX_BEQ, EX_BNE, ex_mem_1_out_22, ex_mem_1_out_23,
       ex_mem_1_out_24, \ex_mem_1_传输状态out_表明当前传输数据有效 , EX_MEMTOREG, EX_syscall, Go, id_ex_1_out_35,
       id_ex_1_out_37, id_ex_1_out_38, id_ex_1_out_41, id_ex_1_out_44, \id_ex_1_传输状态out_表明当前传输数据有效 , IE,
       if_id_1_out_13, IR1, IR1_q, IR2, IR2_q, IR3, IR3_q, JR_ex, LOADUSE, MEM_RegWrite, mem_wb_1_out_19,
       mem_wb_1_out_20, mem_wb_1_out_21, mem_wb_1_out_22, MEMTOREG, MFC0, mips_alu_1_equal, miss, MTC0,
       nand_1_out, nand_2_out, not_1_out, not_2_out, not_3_out, not_4_out, not_5_out, not_6_out, or_1_out,
       or_2_out, or_3_out, or_4_out, or_5_out, or_6_out, or_7_out, or_8_out, or_10_out, or_14_out, or_15_out,
       or_16_out, or_18_out, RST, SignedExt, SLLV, syscall, W1, W2, W3, WB_RegWrite, \单周期硬布线控制器_1_alu_src ,
       \单周期硬布线控制器_1_beq , \单周期硬布线控制器_1_bne , \单周期硬布线控制器_1_jal , \单周期硬布线控制器_1_jmp , \单周期硬布线控制器_1_jr ,
       \单周期硬布线控制器_1_memtoreg , \单周期硬布线控制器_1_memwrite , \单周期硬布线控制器_1_regdst , \单周期硬布线控制器_1_regwrite ,
       \源寄存器使用情况_1_r1_used , \源寄存器使用情况_1_r2_used , \预测失败 ;
  wire [1:0] bht_1_branch_after, counter_6_q, EX_FWA, EX_FWB, if_id_1_out_12, multiplexer_15_out,
       multiplexer_16_out, multiplexer_18_out, multiplexer_31_out, multiplexer_32_out, multiplexer_33_out,
       multiplexer_34_out, priority_encoder_1_out, register_2_q, SA, SB, subtractor_1_out, \双位预测fsm_1_新0 ,
       \预测位 ;
  wire [3:0] id_ex_1_out_45, \单周期硬布线控制器_1_alu_op ;
  wire [4:0] ex_mem_1_out_14_3, ex_mem_1_out_14_4, ex_mem_1_out_14_5, id_ex_1_out_30_2, ID_R1_num, ID_R2_num,
       MEM_WriteReg_num, multiplexer_9_out, multiplexer_12_out, multiplexer_19_out, multiplexer_22_out,
       SHAMT, WB_WriteReg_num;
  wire [5:0] ex_mem_1_out_14, ex_mem_1_out_14_6, FUNC, id_ex_1_out_30_3, OP_CODE;
  wire [10:6] ex_mem_1_out_14_2;
  wire [15:0] \LoadUse次数 , multiplexer_23_out, shifter_1_out, \总周期数 , \无条件分支数 , \条件分支成功数 , \预测失败次数 ;
  wire [25:0] id_ex_1_out_30;
  wire [25:6] if_id_1_out_9;
  wire [31:0] A, adder_1_out, adder_2_out, adder_3_out, adder_4_out, adder_5_out, B, bht_1_sd,
       bit_extender_1_out, bit_extender_2_out, bit_extender_3_out, EPC, EPC_2_q, EPC_3_q, EX_PC, EXR1, EXR2,
       id_ex_1_out_28, id_ex_1_out_34, ID_PC, LedData, MEM_PC, mem_wb_1_out_13, MEMALU, mips_alu_1_result,
       mips_regifile_1_r1, mips_regifile_1_r2, multiplexer_1_out, multiplexer_2_out, multiplexer_3_out,
       multiplexer_4_out, multiplexer_5_out, multiplexer_6_out, multiplexer_10_out, multiplexer_11_out,
       multiplexer_13_out, multiplexer_14_out, multiplexer_17_out, multiplexer_25_out, multiplexer_26_out,
       multiplexer_29_out, multiplexer_30_out, multiplexer_35_out, pre_ex, pre_id, RDOUT, WB_PC, WBALU, WBRD,
       ZPC;

  Clock #(.highDuration(1), .lowDuration(1)) clock_1 (.out(CLK));
  Button _1 (.out(IR1));
  Button _2 (.out(IR2));
  Button _3 (.out(IR3));
  Button \u_总复位  (.out(RST));
  Register #(.width(32), .trigger("rising"), .Select("low")) u_PC (
    .D(multiplexer_3_out), .en(and_1_out), .Q(PC), .clk(CLK), .clr(RST));
  Multiplexer #(.select(1), .width(32), .disabled("Z"), .enable("false")) multiplexer_1 (
    .in0(multiplexer_6_out), .in1(multiplexer_2_out), .out(multiplexer_1_out), .sel(id_ex_1_out_35));
  Multiplexer #(.select(1), .width(32), .disabled("Z"), .enable("false")) multiplexer_2 (
    .in0({adder_3_out[31:28], id_ex_1_out_30[25:21], id_ex_1_out_30_2, id_ex_1_out_30[15:0], 2'b00}),
    .in1(A), .out(multiplexer_2_out), .sel(JR_ex));
  Multiplexer #(.select(1), .width(32), .disabled("Z"), .enable("false")) multiplexer_3 (
    .in0(multiplexer_4_out), .in1(EPC), .out(multiplexer_3_out), .sel(ERET));
  Button \u_继续运行  (.out(Go));
  LED #(.active("true")) led_1 (.in(W1));
  LED #(.active("true")) led_2 (.in(W2));
  LED #(.active("true")) led_3 (.in(W3));
  // Probe on {adder_3_out[31:28], id_ex_1_out_30[25:21], id_ex_1_out_30_2, id_ex_1_out_30[15:0], 2'b00}
  Multiplexer #(.select(1), .width(32), .disabled("Z"), .enable("false")) multiplexer_4 (
    .in0(multiplexer_5_out), .in1(ZPC), .out(multiplexer_4_out), .sel(\CPU中断请求 ));
  // Probe on multiplexer_5_out
  Multiplexer #(.select(1), .width(32), .disabled("Z"), .enable("false")) multiplexer_5 (
    .in0(multiplexer_11_out), .in1(multiplexer_1_out), .out(multiplexer_5_out), .sel(\预测失败 ));
  Hex_Digit_Display hex_digit_display_1 (.value(LedData[31:28]));  // open: dp
  Adder #(.width(32)) adder_1 (.a(PC), .b(32'h4), .out(adder_1_out));  // open: cin, cout
  Multiplexer #(.select(1), .width(32), .disabled("Z"), .enable("false")) multiplexer_6 (
    .in0(adder_2_out), .in1(adder_4_out), .out(multiplexer_6_out), .sel(or_7_out));
  // Probe on adder_1_out
  // Probe on multiplexer_1_out
  Hex_Digit_Display hex_digit_display_2 (.value(LedData[23:20]));  // open: dp
  Hex_Digit_Display hex_digit_display_3 (.value(LedData[27:24]));  // open: dp
  ROM #(.addrWidth(10), .dataWidth(32), .Select("high")) rom_1 (.addr(PC[11:2]), .data(IR));
  Adder #(.width(32)) adder_2 (.a(EX_PC), .b(32'h4), .out(adder_2_out));  // open: cin, cout
  // Probe on multiplexer_11_out
  // Probe on PC
  // Probe on EX_PC
  Hex_Digit_Display hex_digit_display_4 (.value(LedData[19:16]));  // open: dp
  Hex_Digit_Display hex_digit_display_5 (.value(LedData[15:12]));  // open: dp
  or or_1 (or_1_out, \预测失败 , \CPU中断请求 );
  IF_ID if_id_1 (
    .CLK(CLK), .out_9({OP_CODE, if_id_1_out_9, FUNC}), .\同步清零_气泡_高电平有效 (or_1_out),
    .\使能端_低电平有效_stall_高电平有效 (and_1_out), .in_5(PC), .out_11(ID_PC), .in_1(IR), .in_6(bht_1_branch_after),
    .out_12(if_id_1_out_12), .in_7(bht_1_miss), .out_13(if_id_1_out_13), .in_8(bht_1_sd), .out_14(pre_id));  // open: 传输状态Out_表明当前传输数据有效
  Hex_Digit_Display hex_digit_display_6 (.value(LedData[11:8]));  // open: dp
  Hex_Digit_Display hex_digit_display_7 (.value(LedData[7:4]));  // open: dp
  and and_1 (and_1_out, nand_1_out, ~LOADUSE);  // AND_Gate
  BHT bht_1 (
    .BlockDataIn(multiplexer_13_out), .Addr(PC), .CLK(CLK), .BlkDataReady(or_8_out),
    .branch_pre(multiplexer_15_out), .Miss(bht_1_miss), .branch_after(bht_1_branch_after), .sd(bht_1_sd),
    .pcready(1'b0), .in_3(EX_PC));
  Hex_Digit_Display hex_digit_display_8 (.value(LedData[3:0]));  // open: dp
  // Probe on \总周期数 
  Multiplexer #(.select(1), .width(5), .disabled("Z"), .enable("false")) multiplexer_7 (
    .in0(if_id_1_out_9[25:21]), .in1(5'b00010), .out(ID_R1_num), .sel(syscall));
  Multiplexer #(.select(1), .width(5), .disabled("Z"), .enable("false")) multiplexer_8 (
    .in0(if_id_1_out_9[20:16]), .in1(5'b00100), .out(ID_R2_num), .sel(syscall));
  Multiplexer #(.select(1), .width(5), .disabled("Z"), .enable("false")) multiplexer_9 (
    .in0(mem_wb_1_out_13[20:16]), .in1(mem_wb_1_out_13[15:11]), .out(multiplexer_9_out), .sel(mem_wb_1_out_20));
  assign bit_extender_1_out = {{16{if_id_1_out_9[15]}}, {if_id_1_out_9[15:6], FUNC}};  // Bit_Extender bit_extender_1
  assign bit_extender_2_out = {{16{1'b0}}, {if_id_1_out_9[15:6], FUNC}};  // Bit_Extender bit_extender_2
  Multiplexer #(.select(1), .width(32), .disabled("Z"), .enable("false")) multiplexer_10 (
    .in0(bit_extender_2_out), .in1(bit_extender_1_out), .out(multiplexer_10_out), .sel(SignedExt));
  Multiplexer #(.select(1), .width(32), .disabled("Z"), .enable("false")) multiplexer_11 (
    .in0(adder_1_out), .in1(bht_1_sd), .out(multiplexer_11_out), .sel(and_2_out));
  Multiplexer #(.select(1), .width(5), .disabled("Z"), .enable("false")) multiplexer_12 (
    .in0(multiplexer_9_out), .in1({5{1'b1}}), .out(multiplexer_12_out), .sel(mem_wb_1_out_21));
  Shifter #(.width(16), .shift("ll")) shifter_1 (
    .in({if_id_1_out_9[15:6], FUNC}), .\dist (4'b0010), .out(shifter_1_out));
  or or_2 (or_2_out, nand_1_out, ~mem_wb_1_out_22);  // OR_Gate
  \单周期硬布线控制器  \u_单周期硬布线控制器_1  (
    .Func(FUNC), .OP(OP_CODE), .ALU_OP(\单周期硬布线控制器_1_alu_op ), .MemToReg(\单周期硬布线控制器_1_memtoreg ),
    .MemWrite(\单周期硬布线控制器_1_memwrite ), .ALU_SRC(\单周期硬布线控制器_1_alu_src ), .RegWrite(\单周期硬布线控制器_1_regwrite ),
    .SysCALL(syscall), .SignedExt(SignedExt), .RegDst(\单周期硬布线控制器_1_regdst ), .JR(\单周期硬布线控制器_1_jr ),
    .JMP(\单周期硬布线控制器_1_jmp ), .Beq(\单周期硬布线控制器_1_beq ), .JAL(\单周期硬布线控制器_1_jal ), .Bne(\单周期硬布线控制器_1_bne ));
  assign bit_extender_3_out = {{16{shifter_1_out[15]}}, shifter_1_out};  // Bit_Extender bit_extender_3
  Comparator #(.width(32), .mode("twosComplement")) comparator_1 (
    .a(A), .b(32'h22), .eq(comparator_1_eq));  // open: gt, lt
  Counter #(.width(16), .max('hffff), .ongoal("wrap"), .trigger("rising"), .behavior("old")) counter_1 (
    .count(or_2_out), .Q(\总周期数 ), .clk(CLK), .clr(RST));  // open: load, D, carry, preset
  and and_2 (and_2_out, ~bht_1_miss, bht_1_branch_after[1]);  // AND_Gate
  // Probe on multiplexer_13_out
  MIPS_Regifile mips_regifile_1 (
    .Din(RDin), .Clk(CLK), .R1(mips_regifile_1_r1), .R2(mips_regifile_1_r2), .WE(RegWrite),
    .W_num(multiplexer_12_out), .R1_num(ID_R1_num), .R2_num(ID_R2_num));
  and and_3 (and_3_out, comparator_1_eq, EX_syscall);
  and and_4 (and_4_out, EX_syscall, ~comparator_1_eq);  // AND_Gate
  Multiplexer #(.select(1), .width(32), .disabled("Z"), .enable("false")) multiplexer_13 (
    .in0(multiplexer_14_out), .in1(adder_4_out), .out(multiplexer_13_out), .sel(or_3_out));
  or or_3 (or_3_out, BGEZ, EX_BEQ, EX_BNE);
  nand nand_1 (nand_1_out, and_4_out, ~Go);  // NAND_Gate
  Multiplexer #(.select(1), .width(32), .disabled("Z"), .enable("false")) multiplexer_14 (
    .in0({adder_3_out[31:28], id_ex_1_out_30[25:21], id_ex_1_out_30_2, id_ex_1_out_30[15:0], 2'b00}),
    .in1(A), .out(multiplexer_14_out), .sel(JR_ex));
  or or_4 (or_4_out, \预测失败 , \CPU中断请求 , LOADUSE);
  ID_EX id_ex_1 (
    .CLK(CLK), .in_6({OP_CODE, if_id_1_out_9, FUNC}), .in_7(ID_PC), .in_8(mips_regifile_1_r1),
    .in_9(mips_regifile_1_r2), .in_11(\单周期硬布线控制器_1_jmp ), .in_12(\单周期硬布线控制器_1_jr ),
    .in_13(\单周期硬布线控制器_1_jal ), .in_14(\单周期硬布线控制器_1_alu_src ), .in_15(\单周期硬布线控制器_1_bne ),
    .in_16(\单周期硬布线控制器_1_beq ), .in_17(\单周期硬布线控制器_1_memwrite ), .in_18(\单周期硬布线控制器_1_regwrite ),
    .in_19(\单周期硬布线控制器_1_memtoreg ), .in_21(\单周期硬布线控制器_1_alu_op ), .out_28(id_ex_1_out_28),
    .\传输状态Out_表明当前传输数据有效 (\id_ex_1_传输状态out_表明当前传输数据有效 ),
    .out_30({id_ex_1_out_30_3, id_ex_1_out_30[25:21], id_ex_1_out_30_2, id_ex_1_out_30[15:0]}),
    .out_31(EX_PC), .out_32(EXR1), .out_33(EXR2), .out_35(id_ex_1_out_35), .out_36(JR_ex),
    .out_37(id_ex_1_out_37), .out_38(id_ex_1_out_38), .out_39(EX_BNE), .out_40(EX_BEQ),
    .out_41(id_ex_1_out_41), .out_42(MEM_RegWrite), .out_43(EX_MEMTOREG), .out_45(id_ex_1_out_45),
    .\同步清零_气泡_高电平有效 (or_4_out), .\使能端_低电平有效_stall_高电平有效 (nand_1_out), .in_1(multiplexer_10_out),
    .in_20(\单周期硬布线控制器_1_regdst ), .out_44(id_ex_1_out_44), .in_10(bit_extender_3_out),
    .out_34(id_ex_1_out_34), .in_22(syscall), .out_46(EX_syscall), .in_23(SA), .out_47(EX_FWA), .in_24(SB),
    .out_48(EX_FWB), .\异步清零 (\CPU中断请求 ), .in_25(if_id_1_out_12), .out_49(\预测位 ), .in_26(if_id_1_out_13),
    .out_50(miss), .in_27(pre_id), .out_51(pre_ex));
  Register #(.width(32), .trigger("rising"), .Select("low")) register_1 (
    .D(B), .en(and_3_out), .Q(LedData), .clk(CLK), .clr(RST));
  Counter #(.width(16), .max('hffff), .ongoal("wrap"), .trigger("rising"), .behavior("old")) counter_2 (
    .count(id_ex_1_out_35), .Q(\无条件分支数 ), .clk(CLK), .clr(RST));  // open: load, D, carry, preset
  and and_5 (and_5_out, ~id_ex_1_out_35, ~or_7_out, or_8_out, miss);  // AND_Gate
  Multiplexer #(.select(1), .width(2), .disabled("Z"), .enable("false")) multiplexer_15 (
    .in0(multiplexer_16_out), .in1(2'b01), .out(multiplexer_15_out), .sel(and_5_out));
  Adder #(.width(32)) adder_3 (.a(EX_PC), .b(32'h4), .out(adder_3_out));  // open: cin, cout
  Multiplexer #(.select(1), .width(2), .disabled("Z"), .enable("false")) multiplexer_16 (
    .in0(multiplexer_18_out), .in1(2'b11), .out(multiplexer_16_out), .sel(and_6_out));
  Multiplexer #(.select(1), .width(32), .disabled("Z"), .enable("false")) multiplexer_17 (
    .in0(B), .in1(id_ex_1_out_28), .out(multiplexer_17_out), .sel(id_ex_1_out_38));
  Adder #(.width(32)) adder_4 (.a(adder_3_out), .b(id_ex_1_out_34), .out(adder_4_out));  // open: cin, cout
  Counter #(.width(16), .max('hffff), .ongoal("wrap"), .trigger("rising"), .behavior("old")) counter_3 (
    .count(or_7_out), .Q(\条件分支成功数 ), .clk(CLK), .clr(RST));  // open: load, D, carry, preset
  Comparator #(.width(6), .mode("twosComplement")) comparator_2 (
    .a(id_ex_1_out_30_3), .b(6'b000001), .eq(comparator_2_eq));  // open: gt, lt
  Comparator #(.width(5), .mode("twosComplement")) comparator_3 (
    .a(5'b00001), .b(id_ex_1_out_30_2), .eq(comparator_3_eq));  // open: gt, lt
  or or_5 (or_5_out, or_7_out, id_ex_1_out_35);
  and and_6 (and_6_out, or_7_out, miss);
  Comparator #(.width(32), .mode("twosComplement")) comparator_4 (
    .a(A), .b({32{1'b0}}), .gt(comparator_4_gt), .eq(comparator_4_eq));  // open: lt
  or or_6 (or_6_out, comparator_4_gt, comparator_4_eq);
  and and_7 (and_7_out, mips_alu_1_equal, EX_BEQ);
  and and_8 (and_8_out, EX_BNE, ~mips_alu_1_equal);  // AND_Gate
  MIPS_ALU mips_alu_1 (
    .X(A), .Y(multiplexer_17_out), .AluOP(id_ex_1_out_45), .Equal(mips_alu_1_equal),
    .Result(mips_alu_1_result), .shamt(SHAMT));  // open: Result_2
  and and_9 (BGEZ, comparator_2_eq, comparator_3_eq);
  and and_10 (and_10_out, BGEZ, or_6_out);
  or or_7 (or_7_out, and_7_out, and_10_out, and_8_out);
  and and_11 (and_11_out, id_ex_1_out_35, miss);
  Multiplexer #(.select(1), .width(2), .disabled("Z"), .enable("false")) multiplexer_18 (
    .in0(\双位预测fsm_1_新0 ), .in1(2'b10), .out(multiplexer_18_out), .sel(and_11_out));
  // Probe on PC[11:0]
  // Probe on ID_PC[11:0]
  nand nand_2 (nand_2_out, \预测位 [1], ~miss);  // NAND_Gate
  // Probe on EX_PC[11:0]
  Multiplexer #(.select(1), .width(5), .disabled("Z"), .enable("false")) multiplexer_19 (
    .in0(id_ex_1_out_30_2), .in1(id_ex_1_out_30[15:11]), .out(multiplexer_19_out), .sel(id_ex_1_out_44));
  Comparator #(.width(6), .mode("twosComplement")) comparator_5 (
    .a(id_ex_1_out_30_3), .b({6{1'b0}}), .eq(comparator_5_eq));  // open: gt, lt
  Comparator #(.width(6), .mode("twosComplement")) comparator_6 (
    .a(id_ex_1_out_30[5:0]), .b(6'b000100), .eq(comparator_6_eq));  // open: gt, lt
  and and_12 (and_12_out, nand_2_out, and_15_out);
  and and_13 (and_13_out, \预测位 [1], ~miss, ~and_15_out);  // AND_Gate
  // Probe on MEM_PC[11:0]
  // Probe on WB_PC[11:0]
  EX_MEM ex_mem_1 (
    .in_1({id_ex_1_out_30_3, id_ex_1_out_30[25:21], id_ex_1_out_30_2, id_ex_1_out_30[15:0]}), .CLK(CLK),
    .in_4(EX_PC), .in_5(mips_alu_1_result), .in_6(B), .in_7(id_ex_1_out_41), .in_8(MEM_RegWrite),
    .in_9(EX_MEMTOREG), .in_10(id_ex_1_out_44),
    .out_14({ex_mem_1_out_14_6, ex_mem_1_out_14_5, ex_mem_1_out_14_4, ex_mem_1_out_14_3, ex_mem_1_out_14_2, ex_mem_1_out_14}),
    .\传输状态Out_表明当前传输数据有效 (\ex_mem_1_传输状态out_表明当前传输数据有效 ), .out_16(MEM_PC), .out_17(MEMALU), .out_18(MDin),
    .out_19(MemWrite), .out_20(WB_RegWrite), .out_21(MEMTOREG), .out_22(ex_mem_1_out_22),
    .\同步清零_气泡_高电平有效 (\CPU中断请求 ), .\使能端_低电平有效_stall_高电平有效 (\id_ex_1_传输状态out_表明当前传输数据有效 ),
    .in_11(id_ex_1_out_37), .out_23(ex_mem_1_out_23), .in_13(EX_syscall), .out_24(ex_mem_1_out_24));
  Multiplexer #(.select(1), .width(5), .disabled("Z"), .enable("false")) multiplexer_20 (
    .in0(multiplexer_19_out), .in1({5{1'b1}}), .out(MEM_WriteReg_num), .sel(id_ex_1_out_37));
  and and_14 (SLLV, comparator_5_eq, comparator_6_eq);
  or or_8 (or_8_out, EX_BNE, EX_BEQ, id_ex_1_out_35, BGEZ);
  and and_15 (and_15_out, or_5_out, or_8_out);
  or or_9 (\预测失败 , and_12_out, and_13_out);
  Multiplexer #(.select(1), .width(5), .disabled("Z"), .enable("false")) multiplexer_21 (
    .in0(id_ex_1_out_30[10:6]), .in1(A[4:0]), .out(SHAMT), .sel(SLLV));
  \双位预测FSM  \u_双位预测fsm_1  (
    .\原1 (\预测位 [1]), .\原0 (\预测位 [0]), .\实际跳转 (and_15_out), .\新1 (\双位预测fsm_1_新0 [1]), .\新0 (\双位预测fsm_1_新0 [0]));
  not not_1 (not_1_out, MemWrite);
  Comparator #(.width(6), .mode("twosComplement")) comparator_7 (
    .a(ex_mem_1_out_14_6), .b(6'b100101), .eq(comparator_7_eq));  // open: gt, lt
  Multiplexer #(.select(1), .width(5), .disabled("Z"), .enable("false")) multiplexer_22 (
    .in0(ex_mem_1_out_14_4), .in1(ex_mem_1_out_14_3), .out(multiplexer_22_out), .sel(ex_mem_1_out_22));
  // Probe on \总周期数 
  // Probe on \无条件分支数 
  // Probe on \条件分支成功数 
  // Probe on \LoadUse次数 
  // Probe on \预测失败次数 
  RAM #(.addrWidth(11), .dataWidth(32), .bus("separate"), .Select("high")) ram_1 (
    .addr(MEMALU[12:2]), .din(MDin), .data(RDOUT), .str(MemWrite), .clk(CLK), .ld(not_1_out), .clr(RST));  // open: sel
  Multiplexer #(.select(1), .width(16), .disabled("Z"), .enable("false")) multiplexer_23 (
    .in0(RDOUT[15:0]), .in1(RDOUT[31:16]), .out(multiplexer_23_out), .sel(MEMALU[1]));
  Multiplexer #(.select(1), .width(5), .disabled("Z"), .enable("false")) multiplexer_24 (
    .in0(multiplexer_22_out), .in1({5{1'b1}}), .out(WB_WriteReg_num), .sel(ex_mem_1_out_23));
  Counter #(.width(16), .max('hffff), .ongoal("wrap"), .trigger("rising"), .behavior("old")) counter_4 (
    .count(\预测失败 ), .Q(\预测失败次数 ), .clk(CLK), .clr(RST));  // open: load, D, carry, preset
  MEM_WB mem_wb_1 (
    .in_1({ex_mem_1_out_14_6, ex_mem_1_out_14_5, ex_mem_1_out_14_4, ex_mem_1_out_14_3, ex_mem_1_out_14_2, ex_mem_1_out_14}),
    .CLK(CLK), .in_4(MEM_PC), .in_5(MEMALU), .in_6(multiplexer_25_out), .in_7(WB_RegWrite), .in_8(MEMTOREG),
    .in_9(ex_mem_1_out_22), .out_13(mem_wb_1_out_13), .out_15(WB_PC), .out_16(WBALU), .out_17(WBRD),
    .out_18(RegWrite), .out_19(mem_wb_1_out_19), .out_20(mem_wb_1_out_20), .\同步清零_气泡_高电平有效 (\CPU中断请求 ),
    .\使能端_低电平有效_stall_高电平有效 (\ex_mem_1_传输状态out_表明当前传输数据有效 ), .in_10(ex_mem_1_out_23),
    .out_21(mem_wb_1_out_21), .in_12(ex_mem_1_out_24), .out_22(mem_wb_1_out_22));  // open: 传输状态Out_表明当前传输数据有效
  Multiplexer #(.select(1), .width(32), .disabled("Z"), .enable("false")) multiplexer_25 (
    .in0(RDOUT), .in1({{16{1'b0}}, multiplexer_23_out}), .out(multiplexer_25_out), .sel(comparator_7_eq));
  \源寄存器使用情况  \u_源寄存器使用情况_1  (
    .OP0(OP_CODE[0]), .OP1(OP_CODE[1]), .OP2(OP_CODE[2]), .OP3(OP_CODE[3]), .OP4(OP_CODE[4]),
    .OP5(OP_CODE[5]), .F0(FUNC[0]), .F1(FUNC[1]), .F2(FUNC[2]), .F3(FUNC[3]), .F4(FUNC[4]), .F5(FUNC[5]),
    .R1_Used(\源寄存器使用情况_1_r1_used ), .R2_Used(\源寄存器使用情况_1_r2_used ));
  Counter #(.width(16), .max('hffff), .ongoal("wrap"), .trigger("rising"), .behavior("old")) counter_5 (
    .count(LOADUSE), .Q(\LoadUse次数 ), .clk(CLK), .clr(RST));  // open: load, D, carry, preset
  Multiplexer #(.select(1), .width(32), .disabled("Z"), .enable("false")) multiplexer_26 (
    .in0(WBALU), .in1(WBRD), .out(multiplexer_26_out), .sel(mem_wb_1_out_19));
  Multiplexer #(.select(1), .width(32), .disabled("Z"), .enable("false")) multiplexer_27 (
    .in0(multiplexer_26_out), .in1(adder_5_out), .out(RDin), .sel(mem_wb_1_out_21));
  Adder #(.width(32)) adder_5 (.a(WB_PC), .b(32'h4), .out(adder_5_out));  // open: cin, cout
  not not_2 (not_2_out, comparator_8_eq);
  Comparator #(.width(4), .mode("unsigned")) comparator_8 (
    .a(4'b1100), .b(PC[11:8]), .eq(comparator_8_eq));  // open: gt, lt
  not not_3 (not_3_out, comparator_9_gt);
  Comparator #(.width(4), .mode("unsigned")) comparator_9 (
    .a(PC[15:12]), .b(4'b0011), .gt(comparator_9_gt));  // open: eq, lt
  Comparator #(.width(4), .mode("unsigned")) comparator_10 (
    .a(WB_PC[11:8]), .b(4'b1100), .eq(comparator_10_eq));  // open: gt, lt
  Comparator #(.width(4), .mode("unsigned")) comparator_11 (
    .a(WB_PC[15:12]), .b(4'b0000), .eq(comparator_11_eq));  // open: gt, lt
  Comparator #(.width(5), .mode("twosComplement")) comparator_12 (
    .a(ID_R1_num), .b({5{1'b0}}), .eq(comparator_12_eq));  // open: gt, lt
  Comparator #(.width(5), .mode("twosComplement")) comparator_13 (
    .a(ID_R1_num), .b(WB_WriteReg_num), .eq(comparator_13_eq));  // open: gt, lt
  Comparator #(.width(5), .mode("twosComplement")) comparator_14 (
    .a(ID_R2_num), .b({5{1'b0}}), .eq(comparator_14_eq));  // open: gt, lt
  Comparator #(.width(5), .mode("twosComplement")) comparator_15 (
    .a(ID_R2_num), .b(WB_WriteReg_num), .eq(comparator_15_eq));  // open: gt, lt
  and and_16 (and_16_out, not_3_out, not_2_out, comparator_10_eq, comparator_11_eq);
  not not_4 (not_4_out, comparator_12_eq);
  Comparator #(.width(5), .mode("twosComplement")) comparator_16 (
    .a(ID_R1_num), .b(WB_WriteReg_num), .eq(comparator_16_eq));  // open: gt, lt
  not not_5 (not_5_out, comparator_14_eq);
  Comparator #(.width(5), .mode("twosComplement")) comparator_17 (
    .a(ID_R2_num), .b(WB_WriteReg_num), .eq(comparator_17_eq));  // open: gt, lt
  or or_10 (or_10_out, \CPU中断请求 , ERET);
  Multiplexer #(.select(2), .width(32), .disabled("Z"), .enable("false")) multiplexer_28 (
    .in0(EXR1), .in1(MEMALU), .in2(WBALU), .in3(WBRD), .out(A), .sel(EX_FWA));
  Comparator #(.width(5), .mode("twosComplement")) comparator_18 (
    .a(ID_R1_num), .b(MEM_WriteReg_num), .eq(comparator_18_eq));  // open: gt, lt
  Comparator #(.width(5), .mode("twosComplement")) comparator_19 (
    .a(ID_R2_num), .b(MEM_WriteReg_num), .eq(comparator_19_eq));  // open: gt, lt
  or or_11 (W1, IR1_q, d_ff_1_q);
  Comparator #(.width(6), .mode("twosComplement")) comparator_20 (
    .a(mem_wb_1_out_13[31:26]), .b(6'b010000), .eq(comparator_20_eq));  // open: gt, lt
  and and_17 (ERET, comparator_20_eq, comparator_21_eq);
  Comparator #(.width(6), .mode("twosComplement")) comparator_21 (
    .a(mem_wb_1_out_13[5:0]), .b(6'b011000), .eq(comparator_21_eq));  // open: gt, lt
  // Probe on ERET
  // Probe on comparator_21_eq
  D_Flip_Flop #(.trigger("rising"), .Pre_Clr_Positions("LEGACY"), .NegatePresetClear("false"), .enable("true"), .NewFFLayout("false")) d_ff_1 (
    .clk(IR1), .D(1'b1), .Q(d_ff_1_q), .reset(IR1_q));  // open: Qn, preset, en
  D_Flip_Flop #(.trigger("rising"), .Pre_Clr_Positions("LEGACY"), .NegatePresetClear("false"), .enable("true"), .NewFFLayout("false")) d_ff_2 (
    .clk(IR2), .D(1'b1), .Q(d_ff_2_q), .reset(IR2_q));  // open: Qn, preset, en
  or or_12 (W2, IR2_q, d_ff_2_q);
  D_Flip_Flop #(.trigger("rising"), .Pre_Clr_Positions("LEGACY"), .NegatePresetClear("false"), .enable("true"), .NewFFLayout("false")) d_ff_3 (
    .clk(IR3), .D(1'b1), .Q(d_ff_3_q), .reset(IR3_q));  // open: Qn, preset, en
  or or_13 (W3, IR3_q, d_ff_3_q);
  Multiplexer #(.select(1), .width(32), .disabled("Z"), .enable("false")) multiplexer_29 (
    .in0(WB_PC), .in1(PC), .out(multiplexer_29_out), .sel(and_16_out));
  and and_18 (and_18_out, not_4_out, MEM_RegWrite, comparator_18_eq, \源寄存器使用情况_1_r1_used );
  and and_19 (and_19_out, not_4_out, WB_RegWrite, comparator_13_eq, \源寄存器使用情况_1_r1_used );
  and and_20 (and_20_out, not_4_out, WB_RegWrite, MEMTOREG, comparator_16_eq, \源寄存器使用情况_1_r1_used );
  and and_21 (and_21_out, not_5_out, MEM_RegWrite, comparator_19_eq, \源寄存器使用情况_1_r2_used );
  and and_22 (and_22_out, not_5_out, WB_RegWrite, comparator_15_eq, \源寄存器使用情况_1_r2_used );
  and and_23 (and_23_out, not_5_out, WB_RegWrite, MEMTOREG, comparator_17_eq, \源寄存器使用情况_1_r2_used );
  or or_14 (or_14_out, d_ff_1_q, IR1_q);
  or or_15 (or_15_out, d_ff_3_q, IR3_q);
  Comparator #(.width(6), .mode("twosComplement")) comparator_22 (
    .a(mem_wb_1_out_13[31:26]), .b(6'b010000), .eq(comparator_22_eq));  // open: gt, lt
  Comparator #(.width(5), .mode("twosComplement")) comparator_23 (
    .a(mem_wb_1_out_13[25:21]), .b(5'b00100), .eq(comparator_23_eq));  // open: gt, lt
  Multiplexer #(.select(1), .width(32), .disabled("Z"), .enable("false")) multiplexer_30 (
    .in0(EPC_2_q), .in1(multiplexer_29_out), .out(multiplexer_30_out), .sel(\CPU中断请求 ));
  Multiplexer #(.select(1), .width(2), .disabled("Z"), .enable("false")) multiplexer_31 (
    .in0(2'b00), .in1(2'b10), .out(multiplexer_31_out), .sel(and_19_out));
  Multiplexer #(.select(1), .width(2), .disabled("Z"), .enable("false")) multiplexer_32 (
    .in0(2'b00), .in1(2'b10), .out(multiplexer_32_out), .sel(and_22_out));
  and and_24 (and_24_out, or_14_out, ~demultiplexer_1_out1);  // AND_Gate
  or or_16 (or_16_out, d_ff_2_q, IR2_q);
  and and_25 (and_25_out, or_16_out, ~demultiplexer_1_out2);  // AND_Gate
  and and_26 (and_26_out, or_15_out, ~demultiplexer_1_out3);  // AND_Gate
  and and_27 (MTC0, comparator_22_eq, comparator_23_eq);
  // Probe on MTC0
  Comparator #(.width(6), .mode("twosComplement")) comparator_24 (
    .a(mem_wb_1_out_13[31:26]), .b(6'b010000), .eq(comparator_24_eq));  // open: gt, lt
  Comparator #(.width(5), .mode("twosComplement")) comparator_25 (
    .a(mem_wb_1_out_13[25:21]), .b({5{1'b0}}), .eq(comparator_25_eq));  // open: gt, lt
  Register #(.width(32), .trigger("rising"), .Select("low")) u_EPC (
    .D(multiplexer_30_out), .en(or_10_out), .Q(EPC), .clk(CLK));  // open: clr
  // Probe on EPC
  and and_28 (and_28_out, EX_MEMTOREG, and_18_out);
  Multiplexer #(.select(1), .width(2), .disabled("Z"), .enable("false")) multiplexer_33 (
    .in0(multiplexer_31_out), .in1(2'b11), .out(multiplexer_33_out), .sel(and_20_out));
  and and_29 (and_29_out, EX_MEMTOREG, and_21_out);
  Multiplexer #(.select(1), .width(2), .disabled("Z"), .enable("false")) multiplexer_34 (
    .in0(multiplexer_32_out), .in1(2'b11), .out(multiplexer_34_out), .sel(and_23_out));
  D_Flip_Flop #(.trigger("rising"), .Pre_Clr_Positions("LEGACY"), .NegatePresetClear("false"), .enable("true"), .NewFFLayout("false")) u_IR1 (
    .clk(CLK), .D(and_24_out), .Q(IR1_q));  // open: Qn, preset, en, reset
  D_Flip_Flop #(.trigger("rising"), .Pre_Clr_Positions("LEGACY"), .NegatePresetClear("false"), .enable("true"), .NewFFLayout("false")) u_IR2 (
    .clk(CLK), .D(and_25_out), .Q(IR2_q));  // open: Qn, preset, en, reset
  D_Flip_Flop #(.trigger("rising"), .Pre_Clr_Positions("LEGACY"), .NegatePresetClear("false"), .enable("true"), .NewFFLayout("false")) u_IR3 (
    .clk(CLK), .D(and_26_out), .Q(IR3_q));  // open: Qn, preset, en, reset
  and and_30 (MFC0, comparator_24_eq, comparator_25_eq);
  // Probe on MFC0
  Multiplexer #(.select(1), .width(32), .disabled("Z"), .enable("false")) multiplexer_35 (
    .in0(EPC_3_q), .in1(EPC), .out(multiplexer_35_out), .sel(\CPU中断请求 ));
  Multiplexer #(.select(1), .width(2), .disabled("Z"), .enable("false")) multiplexer_36 (
    .in0(multiplexer_33_out), .in1(2'b01), .out(SA), .sel(and_18_out));
  Multiplexer #(.select(1), .width(2), .disabled("Z"), .enable("false")) multiplexer_37 (
    .in0(multiplexer_34_out), .in1(2'b01), .out(SB), .sel(and_21_out));
  Register #(.width(1), .trigger("rising"), .Select("low")) u_IE (
    .D(\CPU中断请求 ), .en(not_6_out), .Q(IE), .clk(CLK), .clr(or_18_out), .preset(MTC0));  // open: cs
  not not_6 (not_6_out, IE);
  Register #(.width(32), .trigger("rising"), .Select("low")) EPC_2 (
    .D(multiplexer_35_out), .en(or_10_out), .Q(EPC_2_q), .clk(CLK));  // open: clr
  // Probe on EPC_2_q
  or or_17 (LOADUSE, and_28_out, and_29_out);
  Demultiplexer #(.select(2), .width(1), .tristate("false"), .disabled("Z"), .enable("false")) demultiplexer_1 (
    .out1(demultiplexer_1_out1), .out2(demultiplexer_1_out2), .out3(demultiplexer_1_out3), .in(ERET),
    .sel(priority_encoder_1_out));  // open: out0
  // Probe on demultiplexer_1_out3
  Priority_Encoder #(.select(2), .disabled("Z")) priority_encoder_1 (
    .in0(1'b1), .in1(IR1_q), .in2(IR2_q), .in3(IR3_q), .out(priority_encoder_1_out));  // open: gs, en_out, en_in
  // Probe on priority_encoder_1_out
  and and_31 (\CPU中断请求 , comparator_26_gt, ~IE);  // AND_Gate
  or or_18 (or_18_out, ERET, MFC0);
  Multiplexer #(.select(2), .width(32), .disabled("Z"), .enable("false")) multiplexer_38 (
    .in0(EXR2), .in1(MEMALU), .in2(WBALU), .in3(WBRD), .out(B), .sel(EX_FWB));
  // Probe on \CPU中断请求 
  Register #(.width(32), .trigger("rising"), .Select("low")) EPC_3 (
    .D(EPC_2_q), .en(or_10_out), .Q(EPC_3_q), .clk(CLK));  // open: clr
  Multiplexer #(.select(2), .width(32), .disabled("Z"), .enable("false")) multiplexer_39 (
    .in1(32'hc00), .in2(32'hc80), .in3(32'hd00), .out(ZPC), .sel(priority_encoder_1_out));  // open: in0
  // Probe on priority_encoder_1_out
  // Probe on register_2_q
  Register #(.width(2), .trigger("rising"), .Select("low")) register_2 (
    .D(priority_encoder_1_out), .Q(register_2_q), .clk(CLK), .clr(comparator_27_eq));  // open: en
  // Probe on comparator_26_gt
  Subtractor #(.width(2)) subtractor_1 (.a(counter_6_q), .b(2'b01), .out(subtractor_1_out));  // open: bin, bout
  Comparator #(.width(2), .mode("unsigned")) comparator_26 (
    .a(priority_encoder_1_out), .b(register_2_q), .gt(comparator_26_gt));  // open: eq, lt
  Counter #(.width(2), .max('h3), .ongoal("wrap"), .trigger("rising"), .behavior("old")) counter_6 (
    .load(ERET), .D(subtractor_1_out), .count(\CPU中断请求 ), .Q(counter_6_q), .clk(CLK));  // open: carry, clr, preset
  // Probe on counter_6_q
  Comparator #(.width(2), .mode("twosComplement")) comparator_27 (
    .a(2'b00), .b(counter_6_q), .eq(comparator_27_eq));  // open: gt, lt

  // Other names for the same wires on the sheet: IF_PC[31:0] = PC

  // Notes on the sheet:
  //   中断源
  //   中断等待指示
  //   总复位信号应将除ROM以外所有存储组件全部清零
  //   指令存储器
  //   指令字
  //   contents of rom_1 (hex, n*v repeats v):
  //   20110001 8000c05 20110001 20120002 20130003 8000c09 20110001 20120002 20130003 8000c0d 20110001
  //   20120002 20130003 8000c11 20110001 20120002 20130003 c000cb8 20100001 20110001 118fc0 112020
  //   20020022 c 118882 12200001 8000c15 112020 20020022 c 20110001 118880 112020 20020022 c 12200001
  //   8000c1f 20110001 118fc0 112020 20020022 c 1188c3 112020 20020022 c 118903 112020 20020022 c 118903
  //   112020 20020022 c 118903 112020 20020022 c 118903 112020 20020022 c 118903 112020 20020022 c 118903
  //   112020 20020022 c 118903 112020 20020022 c 20100001 109fc0 139fc3 8021 2012000c 24160003 26100001
  //   3210000f 20080008 20090001 139900 2709825 132020 20020022 c 1094022 1500fff9 22100001 2018000f
  //   2188024 108700 20080008 20090001 139902 2709825 132021 20020022 c 1094022 1500fff9 108702 2c9b022
  //   12c00001 8000c50 4020 1084027 84400 3508ffff 82021 20020022 c 2010ffff 20110000 ae300000 22100001
  //   22310004 ae300000 22100001 22310004 ae300000 22100001 22310004 ae300000 22100001 22310004 ae300000
  //   22100001 22310004 ae300000 22100001 22310004 ae300000 22100001 22310004 ae300000 22100001 22310004
  //   ae300000 22100001 22310004 ae300000 22100001 22310004 ae300000 22100001 22310004 ae300000 22100001
  //   22310004 ae300000 22100001 22310004 ae300000 22100001 22310004 ae300000 22100001 22310004 ae300000
  //   22100001 22310004 22100001 8020 2011003c 8e130000 8e340000 274402a 11000002 ae330000 ae140000
  //   2231fffc 1611fff8 102020 20020022 c 22100004 2011003c 1611fff2 20020032 c 20100000 22100001 102020
  //   20020022 c 22100002 102020 20020022 c 22100003 102020 20020022 c 22100004 102020 20020022 c 22100005
  //   102020 20020022 c 22100006 102020 20020022 c 22100007 102020 20020022 c 22100008 102020 20020022
  //   20020022 c 3e00008 549*0 ac161c00 ac141c04 ac151c08 ac101c0c ac131c10 ac041c14 ac021c18 20160001
  //   20140006 20150001 168020 108100 2149825 132020 20020022 c 1600fffa 295a022 1680fff7 8c161c00
  //   8c141c04 8c151c08 8c101c0c 8c131c10 8c041c14 8c021c18 42000018 5*0 ac161c00 ac141c04 ac151c08
  //   ac101c0c ac131c10 ac041c14 ac021c18 20160002 20140006 20150001 168020 108100 2149825 132020 20020022
  //   c 1600fffa 295a022 1680fff7 8c161c00 8c141c04 8c151c08 8c101c0c 8c131c10 8c041c14 8c021c18 42000018
  //   5*0 ac161c00 ac141c04 ac151c08 ac101c0c ac131c10 ac041c14 ac021c18 20160003 20140006 20150001 168020
  //   108100 2149825 132020 20020022 c 1600fffa 295a022 1680fff7 8c161c00 8c141c04 8c151c08 8c101c0c
  //   8c131c10 8c041c14 8c021c18 42001018
  //   数码管输出
  //   数码管输出应该用寄存器锁存，否则显示数据只能一闪而过
  //   OP
  //   Func
  //   rs
  //   rt
  //   rd
  //   JMP
  //   JR
  //   OP
  //   Func
  //   Beq
  //   Bne
  //   MemToReg
  //   MemWrite
  //   AluOP
  //   AluSrcB
  //   RegWrite
  //   JAL
  //   RegDst
  //   Syscall
  //   为方便自动评测，需要输出PC，IR，寄存器文件写入端口RDin，内存写入端口MDin等信号
  //   OP
  //   rs
  //   rt
  //   rd
  //   OP
  //   rs
  //   rt
  //   rd
  //   OP
  //   rs
  //   rt
  //   rd
  //   Reset 
  //   Reset 
  //   Reset 
endmodule

module \双位预测FSM  (
  input  \原1 ,
  input  \原0 ,
  input  \实际跳转 ,
  output \新1 ,
  output \新0 
);

  wire and_1_out, and_2_out, and_3_out, and_4_out, not_1_out, not_2_out, not_3_out, not_4_out, not_5_out;

  not not_1 (not_1_out, \原0 );
  not not_2 (not_2_out, \原1 );
  not not_3 (not_3_out, \原0 );
  not not_4 (not_4_out, \原0 );
  not not_5 (not_5_out, \实际跳转 );
  and and_1 (and_1_out, \原0 , \实际跳转 );
  and and_2 (and_2_out, \原1 , not_1_out);
  and and_3 (and_3_out, not_2_out, not_3_out, \实际跳转 );
  and and_4 (and_4_out, \原1 , not_4_out, not_5_out);
  or or_1 (\新1 , and_1_out, and_2_out);
  or or_2 (\新0 , and_3_out, and_4_out);
endmodule

module BHT (
  input  [31:0] BlockDataIn,
  input  [31:0] Addr,
  input  [31:0] in_3,
  input  CLK,
  input  BlkDataReady,
  input  [1:0] branch_pre,
  input  pcready,
  output Miss,
  output [1:0] branch_after,
  output [31:0] sd
);

  wire and_1_out, and_2_out, and_3_out, and_4_out, and_5_out, and_7_out, and_8_out, and_10_out, and_11_out,
       and_12_out, and_13_out, and_14_out, and_15_out, and_16_out, and_17_out, and_18_out, and_19_out,
       and_20_out, and_21_out, and_22_out, and_23_out, and_24_out, and_25_out, and_26_out, and_28_out,
       and_29_out, and_30_out, and_31_out, and_41_out, and_42_out, and_43_out, and_53_out, and_54_out,
       and_55_out, and_56_out, and_57_out, and_58_out, and_60_out, and_61_out, and_63_out, comparator_1_eq,
       comparator_2_eq, comparator_3_eq, comparator_4_eq, comparator_5_eq, comparator_6_eq, comparator_7_eq,
       comparator_8_eq, comparator_9_eq, comparator_10_eq, comparator_11_eq, comparator_12_eq,
       comparator_13_eq, comparator_14_eq, comparator_15_eq, comparator_16_eq, comparator_17_eq,
       comparator_18_eq, comparator_19_eq, comparator_20_eq, comparator_21_eq, comparator_22_eq,
       comparator_23_eq, comparator_24_eq, HIT, L0, L1, L2, L3, L4, L5, L6, L7, Lx0, Lx1, Lx2, Lx3, Lx4, Lx5,
       Lx6, Lx7, Miss_t, or_1_out, or_2_out, or_3_out, or_4_out, or_5_out, or_6_out, or_7_out, or_8_out,
       or_9_out, or_10_out, or_11_out, or_12_out, or_13_out, or_14_out, or_15_out, or_16_out, or_17_out,
       or_18_out, or_19_out, or_20_out, or_21_out, or_22_out, or_23_out, or_24_out, or_25_out, or_26_out,
       or_27_out, or_28_out, or_29_out, or_30_out, or_31_out, or_32_out, or_34_out, V0, V1, V2, V3, V4, V5,
       V6, V7, WriteL0, WriteL1, WriteL2, WriteL3, WriteL4, WriteL5, WriteL6, WriteL7;
  wire [1:0] register_8_q, register_9_q, register_10_q, register_11_q, register_12_q, register_13_q,
       register_14_q, register_15_q;
  wire [2:0] max3_1_max_num, max3_2_max_num, max3_3_max_num, max3_4_max_num, max3_5_max_num, max3_6_max_num,
       max3_7_max_num, max3_8_max_num, max3_9_max_num, max3_10_max_num, max3_11_max_num, max3_12_max_num,
       max3_13_max_num, max3_14_max_num, max3_15_max_num, max3_16_max_num, max3_17_max_num, max3_18_max_num,
       max3_19_max_num, max3_20_max_num, max3_21_max_num, max3_22_max_num, max3_23_max_num, max3_24_max_num,
       max3_25_max_num, max3_26_max_num, max3_27_max_num, max3_28_max_num, max3_29_max_num, max3_30_max_num,
       max3_31_max_num, max3_32_max_num, max3_33_max_num, max3_34_max_num, max3_35_max_num, max3_36_max_num,
       max3_37_max_num, max3_38_max_num, max3_39_max_num, max3_40_max_num, max3_41_max_num, max3_42_max_num,
       max3_43_max_num, max3_44_max_num, max3_45_max_num, max3_46_max_num, max3_47_max_num, max3_48_max_num,
       max3_49_max_num, max3_50_max_num, max3_51_max_num, max3_52_max_num, max3_53_max_num, max3_54_max_num,
       max3_55_max_num, max3_56_max_num;
  wire [15:0] adder_1_out, adder_2_out, adder_3_out, adder_4_out, adder_5_out, adder_6_out, adder_7_out,
       adder_8_out, C0, C1, C2, C3, C4, C5, C6, C7, max3_1_max, max3_2_max, max3_3_max, max3_4_max,
       max3_5_max, max3_6_max, max3_7_max, max3_8_max, max3_9_max, max3_10_max, max3_12_max, max3_13_max,
       max3_15_max, max3_16_max, max3_17_max, max3_18_max, max3_19_max, max3_20_max, max3_22_max,
       max3_23_max, max3_24_max, max3_25_max, max3_26_max, max3_27_max, max3_29_max, max3_30_max,
       max3_31_max, max3_32_max, max3_33_max, max3_35_max, max3_36_max, max3_37_max, max3_38_max,
       max3_39_max, max3_40_max, max3_41_max, max3_42_max, max3_43_max, max3_44_max, max3_46_max,
       max3_47_max, max3_48_max, max3_49_max, max3_50_max, max3_51_max, max3_52_max, max3_54_max,
       max3_55_max, multiplexer_1_out, multiplexer_2_out, multiplexer_3_out, multiplexer_4_out,
       multiplexer_5_out, multiplexer_6_out, multiplexer_7_out, multiplexer_8_out;
  wire [31:0] Tag0, Tag1, Tag2, Tag3, Tag4, Tag5, Tag6, Tag7, \数据副本_2_q , \数据副本_3_q , \数据副本_4_q , \数据副本_5_q ,
       \数据副本_6_q , \数据副本_7_q , \数据副本_8_q , \数据副本_q ;

  Register #(.width(1), .trigger("rising"), .Select("low")) VALID (
    .D(1'b1), .en(WriteL0), .Q(V0), .clk(CLK));  // open: clr
  Register #(.width(1), .trigger("rising"), .Select("low")) VALID_2 (
    .D(1'b1), .en(WriteL1), .Q(V1), .clk(CLK));  // open: clr
  Register #(.width(1), .trigger("rising"), .Select("low")) VALID_3 (
    .D(1'b1), .en(WriteL2), .Q(V2), .clk(CLK));  // open: clr
  Register #(.width(1), .trigger("rising"), .Select("low")) VALID_4 (
    .D(1'b1), .en(WriteL3), .Q(V3), .clk(CLK));  // open: clr
  Register #(.width(1), .trigger("rising"), .Select("low")) VALID_5 (
    .D(1'b1), .en(WriteL4), .Q(V4), .clk(CLK));  // open: clr
  Register #(.width(1), .trigger("rising"), .Select("low")) VALID_6 (
    .D(1'b1), .en(WriteL5), .Q(V5), .clk(CLK));  // open: clr
  Register #(.width(1), .trigger("rising"), .Select("low")) VALID_7 (
    .D(1'b1), .en(WriteL6), .Q(V6), .clk(CLK));  // open: clr
  Register #(.width(1), .trigger("rising"), .Select("low")) VALID_8 (
    .D(1'b1), .en(WriteL7), .Q(V7), .clk(CLK));  // open: clr
  // Probe on Addr
  // Probe on V1
  // Probe on Tag4
  // Probe on Tag5
  // Probe on Tag6
  // Probe on Tag7
  max3 max3_1 (.Y(C1), .MAX(max3_1_max), .X(C0), .Y_num(3'b001), .Max_num(max3_1_max_num), .X_num(3'b000));
  max3 max3_2 (
    .Y(max3_3_max), .MAX(max3_2_max), .X(max3_1_max), .Y_num(max3_3_max_num), .Max_num(max3_2_max_num),
    .X_num(max3_1_max_num));
  max3 max3_3 (.Y(C3), .MAX(max3_3_max), .X(C2), .Y_num(3'b011), .Max_num(max3_3_max_num), .X_num(3'b010));
  max3 max3_4 (.Y(C5), .MAX(max3_4_max), .X(C4), .Y_num(3'b101), .Max_num(max3_4_max_num), .X_num(3'b100));
  max3 max3_5 (
    .Y(max3_6_max), .MAX(max3_5_max), .X(max3_4_max), .Y_num(max3_6_max_num), .Max_num(max3_5_max_num),
    .X_num(max3_4_max_num));
  max3 max3_6 (.Y(C7), .MAX(max3_6_max), .X(C6), .Y_num(3'b111), .Max_num(max3_6_max_num), .X_num(3'b110));
  max3 max3_7 (.Y(C1), .MAX(max3_7_max), .X(C0), .Y_num(3'b001), .Max_num(max3_7_max_num), .X_num(3'b000));
  max3 max3_8 (.Y(C3), .MAX(max3_8_max), .X(C2), .Y_num(3'b011), .Max_num(max3_8_max_num), .X_num(3'b010));
  max3 max3_9 (.Y(C5), .MAX(max3_9_max), .X(C4), .Y_num(3'b101), .Max_num(max3_9_max_num), .X_num(3'b100));
  max3 max3_10 (.Y(C7), .MAX(max3_10_max), .X(C6), .Y_num(3'b111), .Max_num(max3_10_max_num), .X_num(3'b110));
  // Probe on Tag0
  Register #(.width(32), .trigger("rising"), .Select("low")) TAG (
    .D(in_3), .en(WriteL0), .Q(Tag0), .clk(CLK));  // open: clr
  // Probe on Tag1
  Register #(.width(32), .trigger("rising"), .Select("low")) TAG_2 (
    .D(in_3), .en(WriteL1), .Q(Tag1), .clk(CLK));  // open: clr
  // Probe on Tag2
  Register #(.width(32), .trigger("rising"), .Select("low")) TAG_3 (
    .D(in_3), .en(WriteL2), .Q(Tag2), .clk(CLK));  // open: clr
  // Probe on Tag3
  Register #(.width(32), .trigger("rising"), .Select("low")) TAG_4 (
    .D(in_3), .en(WriteL3), .Q(Tag3), .clk(CLK));  // open: clr
  Register #(.width(32), .trigger("rising"), .Select("low")) TAG_5 (
    .D(in_3), .en(WriteL4), .Q(Tag4), .clk(CLK));  // open: clr
  Register #(.width(32), .trigger("rising"), .Select("low")) TAG_6 (
    .D(in_3), .en(WriteL5), .Q(Tag5), .clk(CLK));  // open: clr
  Register #(.width(32), .trigger("rising"), .Select("low")) TAG_7 (
    .D(in_3), .en(WriteL6), .Q(Tag6), .clk(CLK));  // open: clr
  Register #(.width(32), .trigger("rising"), .Select("low")) TAG_8 (
    .D(in_3), .en(WriteL7), .Q(Tag7), .clk(CLK));  // open: clr
  max3 max3_11 (
    .Y(max3_5_max), .X(max3_2_max), .Y_num(max3_5_max_num), .Max_num(max3_11_max_num), .X_num(max3_2_max_num));  // open: MAX
  max3 max3_12 (
    .Y(max3_8_max), .MAX(max3_12_max), .X(max3_7_max), .Y_num(max3_8_max_num), .Max_num(max3_12_max_num),
    .X_num(max3_7_max_num));
  max3 max3_13 (
    .Y(max3_10_max), .MAX(max3_13_max), .X(max3_9_max), .Y_num(max3_10_max_num), .Max_num(max3_13_max_num),
    .X_num(max3_9_max_num));
  // Probe on BlockDataIn
  Adder #(.width(16)) adder_1 (.a(C3), .b(16'h1), .out(adder_1_out));  // open: cin, cout
  Adder #(.width(16)) adder_2 (.a(C4), .b(16'h1), .out(adder_2_out));  // open: cin, cout
  Adder #(.width(16)) adder_3 (.a(C5), .b(16'h1), .out(adder_3_out));  // open: cin, cout
  Adder #(.width(16)) adder_4 (.a(C6), .b(16'h1), .out(adder_4_out));  // open: cin, cout
  Adder #(.width(16)) adder_5 (.a(C7), .b(16'h1), .out(adder_5_out));  // open: cin, cout
  and and_1 (and_1_out, Miss_t, V0, ~V1);  // AND_Gate
  and and_2 (and_2_out, Miss_t, V0, V1, V2, V3, V4, V5, V6, V7);
  Comparator #(.width(3), .mode("twosComplement")) comparator_1 (
    .a(max3_11_max_num), .b(3'b001), .eq(comparator_1_eq));  // open: gt, lt
  max3 max3_14 (
    .Y(max3_13_max), .X(max3_12_max), .Y_num(max3_13_max_num), .Max_num(max3_14_max_num),
    .X_num(max3_12_max_num));  // open: MAX
  Adder #(.width(16)) adder_6 (.a(C0), .b(16'h1), .out(adder_6_out));  // open: cin, cout
  Multiplexer #(.select(1), .width(16), .disabled("Z"), .enable("false")) multiplexer_1 (
    .in0(adder_6_out), .in1({16{1'b0}}), .out(multiplexer_1_out), .sel(or_1_out));
  Adder #(.width(16)) adder_7 (.a(C1), .b(16'h1), .out(adder_7_out));  // open: cin, cout
  Multiplexer #(.select(1), .width(16), .disabled("Z"), .enable("false")) multiplexer_2 (
    .in0(adder_7_out), .in1({16{1'b0}}), .out(multiplexer_2_out), .sel(or_2_out));
  Adder #(.width(16)) adder_8 (.a(C2), .b(16'h1), .out(adder_8_out));  // open: cin, cout
  Multiplexer #(.select(1), .width(16), .disabled("Z"), .enable("false")) multiplexer_3 (
    .in0(adder_8_out), .in1({16{1'b0}}), .out(multiplexer_3_out), .sel(or_3_out));
  // Probe on C3
  Multiplexer #(.select(1), .width(16), .disabled("Z"), .enable("false")) multiplexer_4 (
    .in0(adder_1_out), .in1({16{1'b0}}), .out(multiplexer_4_out), .sel(or_4_out));
  // Probe on C4
  Multiplexer #(.select(1), .width(16), .disabled("Z"), .enable("false")) multiplexer_5 (
    .in0(adder_2_out), .in1({16{1'b0}}), .out(multiplexer_5_out), .sel(or_5_out));
  // Probe on C5
  Multiplexer #(.select(1), .width(16), .disabled("Z"), .enable("false")) multiplexer_6 (
    .in0(adder_3_out), .in1({16{1'b0}}), .out(multiplexer_6_out), .sel(or_6_out));
  // Probe on C6
  Multiplexer #(.select(1), .width(16), .disabled("Z"), .enable("false")) multiplexer_7 (
    .in0(adder_4_out), .in1({16{1'b0}}), .out(multiplexer_7_out), .sel(or_7_out));
  // Probe on C7
  Multiplexer #(.select(1), .width(16), .disabled("Z"), .enable("false")) multiplexer_8 (
    .in0(adder_5_out), .in1({16{1'b0}}), .out(multiplexer_8_out), .sel(or_8_out));
  and and_3 (and_3_out, and_2_out, comparator_1_eq);
  and and_4 (and_4_out, Miss_t, V0, V1, V2, V3, ~V4);  // AND_Gate
  and and_5 (and_5_out, Miss_t, V0, V1, V2, V3, V4, V5, V6, V7);
  Comparator #(.width(3), .mode("twosComplement")) comparator_2 (
    .a(max3_14_max_num), .b(3'b100), .eq(comparator_2_eq));  // open: gt, lt
  // Probe on C0
  Register #(.width(16), .trigger("rising"), .Select("low")) \u_淘汰计数  (
    .D(multiplexer_1_out), .en(V0), .Q(C0), .clk(CLK));  // open: clr
  or or_1 (or_1_out, and_30_out, L0, WriteL0);
  // Probe on C1
  Register #(.width(16), .trigger("rising"), .Select("low")) register_1 (
    .D(multiplexer_2_out), .en(V1), .Q(C1), .clk(CLK));  // open: clr
  or or_2 (or_2_out, and_13_out, L1, WriteL1);
  // Probe on C2
  Register #(.width(16), .trigger("rising"), .Select("low")) register_2 (
    .D(multiplexer_3_out), .en(V2), .Q(C2), .clk(CLK));  // open: clr
  or or_3 (or_3_out, and_15_out, L2, WriteL2);
  Register #(.width(16), .trigger("rising"), .Select("low")) register_3 (
    .D(multiplexer_4_out), .en(V3), .Q(C3), .clk(CLK));  // open: clr
  or or_4 (or_4_out, and_17_out, L3, WriteL3);
  Register #(.width(16), .trigger("rising"), .Select("low")) register_4 (
    .D(multiplexer_5_out), .en(V4), .Q(C4), .clk(CLK));  // open: clr
  or or_5 (or_5_out, and_19_out, L4, WriteL4);
  Register #(.width(16), .trigger("rising"), .Select("low")) register_5 (
    .D(multiplexer_6_out), .en(V5), .Q(C5), .clk(CLK));  // open: clr
  or or_6 (or_6_out, WriteL5, L5, WriteL5);
  Register #(.width(16), .trigger("rising"), .Select("low")) register_6 (
    .D(multiplexer_7_out), .en(V6), .Q(C6), .clk(CLK));  // open: clr
  or or_7 (or_7_out, and_23_out, L6, WriteL6);
  Register #(.width(16), .trigger("rising"), .Select("low")) register_7 (
    .D(multiplexer_8_out), .en(V7), .Q(C7), .clk(CLK));  // open: clr
  or or_8 (or_8_out, and_25_out, L7, WriteL7);
  and and_6 (WriteL1, BlkDataReady, or_9_out);
  or or_9 (or_9_out, and_1_out, and_3_out);
  and and_7 (and_7_out, and_5_out, comparator_2_eq);
  Pull_Resistor #(.pull(0)) pull_resistor_1 (.node(branch_after));
  Pull_Resistor #(.pull(0)) pull_resistor_2 (.node(sd));
  and and_8 (and_8_out, pcready, L0);
  and and_9 (WriteL4, BlkDataReady, or_10_out);
  or or_10 (or_10_out, and_4_out, and_7_out);
  Register #(.width(32), .trigger("rising"), .Select("low")) \u_数据副本  (
    .D(BlockDataIn), .en(or_11_out), .Q(\数据副本_q ), .clk(CLK));  // open: clr
  or or_11 (or_11_out, and_8_out, WriteL0);
  Register #(.width(32), .trigger("rising"), .Select("low")) \u_数据副本_2  (
    .D(BlockDataIn), .en(or_12_out), .Q(\数据副本_2_q ), .clk(CLK));  // open: clr
  or or_12 (or_12_out, and_14_out, WriteL1);
  Register #(.width(32), .trigger("rising"), .Select("low")) \u_数据副本_3  (
    .D(BlockDataIn), .en(or_13_out), .Q(\数据副本_3_q ), .clk(CLK));  // open: clr
  or or_13 (or_13_out, and_16_out, WriteL2);
  // Probe on \数据副本_4_q 
  Register #(.width(32), .trigger("rising"), .Select("low")) \u_数据副本_4  (
    .D(BlockDataIn), .en(or_14_out), .Q(\数据副本_4_q ), .clk(CLK));  // open: clr
  or or_14 (or_14_out, and_18_out, WriteL3);
  // Probe on \数据副本_5_q 
  Register #(.width(32), .trigger("rising"), .Select("low")) \u_数据副本_5  (
    .D(BlockDataIn), .en(or_15_out), .Q(\数据副本_5_q ), .clk(CLK));  // open: clr
  or or_15 (or_15_out, and_20_out, WriteL4);
  // Probe on \数据副本_6_q 
  Register #(.width(32), .trigger("rising"), .Select("low")) \u_数据副本_6  (
    .D(BlockDataIn), .en(or_16_out), .Q(\数据副本_6_q ), .clk(CLK));  // open: clr
  or or_16 (or_16_out, and_22_out, WriteL5);
  // Probe on \数据副本_7_q 
  Register #(.width(32), .trigger("rising"), .Select("low")) \u_数据副本_7  (
    .D(BlockDataIn), .en(or_17_out), .Q(\数据副本_7_q ), .clk(CLK));  // open: clr
  or or_17 (or_17_out, and_24_out, WriteL6);
  // Probe on \数据副本_8_q 
  Register #(.width(32), .trigger("rising"), .Select("low")) \u_数据副本_8  (
    .D(BlockDataIn), .en(or_18_out), .Q(\数据副本_8_q ), .clk(CLK));  // open: clr
  or or_18 (or_18_out, and_26_out, WriteL7);
  max3 max3_15 (.Y(C1), .MAX(max3_15_max), .X(C0), .Y_num(3'b001), .Max_num(max3_15_max_num), .X_num(3'b000));
  max3 max3_16 (.Y(C3), .MAX(max3_16_max), .X(C2), .Y_num(3'b011), .Max_num(max3_16_max_num), .X_num(3'b010));
  max3 max3_17 (.Y(C5), .MAX(max3_17_max), .X(C4), .Y_num(3'b101), .Max_num(max3_17_max_num), .X_num(3'b100));
  max3 max3_18 (.Y(C7), .MAX(max3_18_max), .X(C6), .Y_num(3'b111), .Max_num(max3_18_max_num), .X_num(3'b110));
  // Probe on \数据副本_q 
  assign sd = L0 ? \数据副本_q  : 32'bz;  // Controlled_Buffer controlled_buffer_1
  // Probe on \数据副本_2_q 
  assign sd = L1 ? \数据副本_2_q  : 32'bz;  // Controlled_Buffer controlled_buffer_2
  // Probe on \数据副本_3_q 
  assign sd = L2 ? \数据副本_3_q  : 32'bz;  // Controlled_Buffer controlled_buffer_3
  assign sd = L3 ? \数据副本_4_q  : 32'bz;  // Controlled_Buffer controlled_buffer_4
  assign sd = L4 ? \数据副本_5_q  : 32'bz;  // Controlled_Buffer controlled_buffer_5
  assign sd = L5 ? \数据副本_6_q  : 32'bz;  // Controlled_Buffer controlled_buffer_6
  assign sd = L6 ? \数据副本_7_q  : 32'bz;  // Controlled_Buffer controlled_buffer_7
  assign sd = L7 ? \数据副本_8_q  : 32'bz;  // Controlled_Buffer controlled_buffer_8
  max3 max3_19 (
    .Y(max3_16_max), .MAX(max3_19_max), .X(max3_15_max), .Y_num(max3_16_max_num), .Max_num(max3_19_max_num),
    .X_num(max3_15_max_num));
  max3 max3_20 (
    .Y(max3_18_max), .MAX(max3_20_max), .X(max3_17_max), .Y_num(max3_18_max_num), .Max_num(max3_20_max_num),
    .X_num(max3_17_max_num));
  max3 max3_21 (
    .Y(max3_20_max), .X(max3_19_max), .Y_num(max3_20_max_num), .Max_num(max3_21_max_num),
    .X_num(max3_19_max_num));  // open: MAX
  max3 max3_22 (.Y(C1), .MAX(max3_22_max), .X(C0), .Y_num(3'b001), .Max_num(max3_22_max_num), .X_num(3'b000));
  max3 max3_23 (.Y(C3), .MAX(max3_23_max), .X(C2), .Y_num(3'b011), .Max_num(max3_23_max_num), .X_num(3'b010));
  max3 max3_24 (.Y(C5), .MAX(max3_24_max), .X(C4), .Y_num(3'b101), .Max_num(max3_24_max_num), .X_num(3'b100));
  max3 max3_25 (.Y(C7), .MAX(max3_25_max), .X(C6), .Y_num(3'b111), .Max_num(max3_25_max_num), .X_num(3'b110));
  or or_19 (or_19_out, WriteL0, and_30_out);
  or or_20 (or_20_out, WriteL1, and_13_out);
  or or_21 (or_21_out, WriteL2, and_15_out);
  Register #(.width(2), .trigger("rising"), .Select("low")) register_8 (
    .D(branch_pre), .en(or_22_out), .Q(register_8_q), .clk(CLK));  // open: clr
  or or_22 (or_22_out, WriteL3, and_17_out);
  Register #(.width(2), .trigger("rising"), .Select("low")) register_9 (
    .D(branch_pre), .en(or_23_out), .Q(register_9_q), .clk(CLK));  // open: clr
  or or_23 (or_23_out, WriteL4, and_19_out);
  Register #(.width(2), .trigger("rising"), .Select("low")) register_10 (
    .D(branch_pre), .en(or_24_out), .Q(register_10_q), .clk(CLK));  // open: clr
  or or_24 (or_24_out, WriteL5, and_21_out);
  Register #(.width(2), .trigger("rising"), .Select("low")) register_11 (
    .D(branch_pre), .en(or_25_out), .Q(register_11_q), .clk(CLK));  // open: clr
  or or_25 (or_25_out, WriteL6, and_23_out);
  Register #(.width(2), .trigger("rising"), .Select("low")) register_12 (
    .D(branch_pre), .en(or_26_out), .Q(register_12_q), .clk(CLK));  // open: clr
  or or_26 (or_26_out, WriteL7, and_25_out);
  and and_10 (and_10_out, V0, Miss_t, V1, ~V2);  // AND_Gate
  and and_11 (and_11_out, Miss_t, V0, V1, V2, V3, V4, V5, V6, V7);
  Comparator #(.width(3), .mode("twosComplement")) comparator_3 (
    .a(max3_21_max_num), .b(3'b010), .eq(comparator_3_eq));  // open: gt, lt
  max3 max3_26 (
    .Y(max3_23_max), .MAX(max3_26_max), .X(max3_22_max), .Y_num(max3_23_max_num), .Max_num(max3_26_max_num),
    .X_num(max3_22_max_num));
  max3 max3_27 (
    .Y(max3_25_max), .MAX(max3_27_max), .X(max3_24_max), .Y_num(max3_25_max_num), .Max_num(max3_27_max_num),
    .X_num(max3_24_max_num));
  // Probe on register_13_q
  Register #(.width(2), .trigger("rising"), .Select("low")) register_13 (
    .D(branch_pre), .en(or_19_out), .Q(register_13_q), .clk(CLK));  // open: clr
  assign branch_after = L0 ? register_13_q : 2'bz;  // Controlled_Buffer controlled_buffer_9
  assign branch_after = L1 ? register_14_q : 2'bz;  // Controlled_Buffer controlled_buffer_10
  Register #(.width(2), .trigger("rising"), .Select("low")) register_14 (
    .D(branch_pre), .en(or_20_out), .Q(register_14_q), .clk(CLK));  // open: clr
  Register #(.width(2), .trigger("rising"), .Select("low")) register_15 (
    .D(branch_pre), .en(or_21_out), .Q(register_15_q), .clk(CLK));  // open: clr
  assign branch_after = L2 ? register_15_q : 2'bz;  // Controlled_Buffer controlled_buffer_11
  assign branch_after = L3 ? register_8_q : 2'bz;  // Controlled_Buffer controlled_buffer_12
  assign branch_after = L4 ? register_9_q : 2'bz;  // Controlled_Buffer controlled_buffer_13
  assign branch_after = L5 ? register_10_q : 2'bz;  // Controlled_Buffer controlled_buffer_14
  assign branch_after = L6 ? register_11_q : 2'bz;  // Controlled_Buffer controlled_buffer_15
  assign branch_after = L7 ? register_12_q : 2'bz;  // Controlled_Buffer controlled_buffer_16
  or or_27 (or_27_out, and_10_out, and_12_out);
  and and_12 (and_12_out, and_11_out, comparator_3_eq);
  max3 max3_28 (
    .Y(max3_27_max), .X(max3_26_max), .Y_num(max3_27_max_num), .Max_num(max3_28_max_num),
    .X_num(max3_26_max_num));  // open: MAX
  and and_13 (and_13_out, BlkDataReady, Lx1);
  and and_14 (and_14_out, pcready, L1);
  and and_15 (and_15_out, BlkDataReady, Lx2);
  and and_16 (and_16_out, pcready, L2);
  and and_17 (and_17_out, BlkDataReady, Lx3);
  and and_18 (and_18_out, pcready, L3);
  and and_19 (and_19_out, BlkDataReady, Lx4);
  and and_20 (and_20_out, pcready, L4);
  and and_21 (and_21_out, BlkDataReady, Lx5);
  and and_22 (and_22_out, pcready, L5);
  and and_23 (and_23_out, BlkDataReady, Lx6);
  and and_24 (and_24_out, pcready, L6);
  and and_25 (and_25_out, BlkDataReady, Lx7);
  and and_26 (and_26_out, pcready, L7);
  and and_27 (WriteL2, BlkDataReady, or_27_out);
  and and_28 (and_28_out, Miss_t, V0, V1, V2, V3, V4, ~V5);  // AND_Gate
  and and_29 (and_29_out, Miss_t, V0, V1, V2, V3, V4, V5, V6, V7);
  Comparator #(.width(3), .mode("twosComplement")) comparator_4 (
    .a(max3_28_max_num), .b(3'b101), .eq(comparator_4_eq));  // open: gt, lt
  and and_30 (and_30_out, BlkDataReady, Lx0);
  or or_28 (or_28_out, and_28_out, and_31_out);
  and and_31 (and_31_out, and_29_out, comparator_4_eq);
  max3 max3_29 (.Y(C1), .MAX(max3_29_max), .X(C0), .Y_num(3'b001), .Max_num(max3_29_max_num), .X_num(3'b000));
  max3 max3_30 (.Y(C3), .MAX(max3_30_max), .X(C2), .Y_num(3'b011), .Max_num(max3_30_max_num), .X_num(3'b010));
  max3 max3_31 (.Y(C5), .MAX(max3_31_max), .X(C4), .Y_num(3'b101), .Max_num(max3_31_max_num), .X_num(3'b100));
  max3 max3_32 (.Y(C7), .MAX(max3_32_max), .X(C6), .Y_num(3'b111), .Max_num(max3_32_max_num), .X_num(3'b110));
  and and_32 (WriteL5, BlkDataReady, or_28_out);
  Comparator #(.width(32), .mode("twosComplement")) comparator_5 (
    .a(Tag0), .b(Addr), .eq(comparator_5_eq));  // open: gt, lt
  Comparator #(.width(32), .mode("twosComplement")) comparator_6 (
    .a(Tag1), .b(Addr), .eq(comparator_6_eq));  // open: gt, lt
  Comparator #(.width(32), .mode("twosComplement")) comparator_7 (
    .a(Tag2), .b(Addr), .eq(comparator_7_eq));  // open: gt, lt
  Comparator #(.width(32), .mode("twosComplement")) comparator_8 (
    .a(Tag3), .b(Addr), .eq(comparator_8_eq));  // open: gt, lt
  Comparator #(.width(32), .mode("twosComplement")) comparator_9 (
    .a(Tag4), .b(Addr), .eq(comparator_9_eq));  // open: gt, lt
  Comparator #(.width(32), .mode("twosComplement")) comparator_10 (
    .a(Tag5), .b(Addr), .eq(comparator_10_eq));  // open: gt, lt
  Comparator #(.width(32), .mode("twosComplement")) comparator_11 (
    .a(Tag6), .b(Addr), .eq(comparator_11_eq));  // open: gt, lt
  Comparator #(.width(32), .mode("twosComplement")) comparator_12 (
    .a(Tag7), .b(Addr), .eq(comparator_12_eq));  // open: gt, lt
  max3 max3_33 (
    .Y(max3_30_max), .MAX(max3_33_max), .X(max3_29_max), .Y_num(max3_30_max_num), .Max_num(max3_33_max_num),
    .X_num(max3_29_max_num));
  max3 max3_34 (
    .Y(max3_35_max), .X(max3_33_max), .Y_num(max3_35_max_num), .Max_num(max3_34_max_num),
    .X_num(max3_33_max_num));  // open: MAX
  max3 max3_35 (
    .Y(max3_32_max), .MAX(max3_35_max), .X(max3_31_max), .Y_num(max3_32_max_num), .Max_num(max3_35_max_num),
    .X_num(max3_31_max_num));
  and and_33 (L0, V0, comparator_5_eq);
  and and_34 (L1, V1, comparator_6_eq);
  and and_35 (L2, V2, comparator_7_eq);
  and and_36 (L3, V3, comparator_8_eq);
  and and_37 (L4, V4, comparator_9_eq);
  and and_38 (L5, V5, comparator_10_eq);
  and and_39 (L6, V6, comparator_11_eq);
  and and_40 (L7, V7, comparator_12_eq);
  and and_41 (and_41_out, Miss_t, V0, V1, V2, V3, V4, V5, V6, V7);
  Comparator #(.width(3), .mode("twosComplement")) comparator_13 (
    .a(max3_34_max_num), .b(3'b011), .eq(comparator_13_eq));  // open: gt, lt
  and and_42 (and_42_out, V1, Miss_t, V0, V2, ~V3);  // AND_Gate
  and and_43 (and_43_out, and_41_out, comparator_13_eq);
  or or_29 (or_29_out, and_42_out, and_43_out);
  or or_30 (or_30_out, Lx0, Lx1, Lx2, Lx3, Lx4, Lx5, Lx6, Lx7);
  not not_1 (Miss_t, or_30_out);
  and and_44 (WriteL3, BlkDataReady, or_29_out);
  max3 max3_36 (.Y(C1), .MAX(max3_36_max), .X(C0), .Y_num(3'b001), .Max_num(max3_36_max_num), .X_num(3'b000));
  max3 max3_37 (.Y(C3), .MAX(max3_37_max), .X(C2), .Y_num(3'b011), .Max_num(max3_37_max_num), .X_num(3'b010));
  max3 max3_38 (.Y(C5), .MAX(max3_38_max), .X(C4), .Y_num(3'b101), .Max_num(max3_38_max_num), .X_num(3'b100));
  max3 max3_39 (.Y(C7), .MAX(max3_39_max), .X(C6), .Y_num(3'b111), .Max_num(max3_39_max_num), .X_num(3'b110));
  max3 max3_40 (.Y(C1), .MAX(max3_40_max), .X(C0), .Y_num(3'b001), .Max_num(max3_40_max_num), .X_num(3'b000));
  max3 max3_41 (.Y(C3), .MAX(max3_41_max), .X(C2), .Y_num(3'b011), .Max_num(max3_41_max_num), .X_num(3'b010));
  max3 max3_42 (.Y(C5), .MAX(max3_42_max), .X(C4), .Y_num(3'b101), .Max_num(max3_42_max_num), .X_num(3'b100));
  max3 max3_43 (.Y(C7), .MAX(max3_43_max), .X(C6), .Y_num(3'b111), .Max_num(max3_43_max_num), .X_num(3'b110));
  max3 max3_44 (
    .Y(max3_37_max), .MAX(max3_44_max), .X(max3_36_max), .Y_num(max3_37_max_num), .Max_num(max3_44_max_num),
    .X_num(max3_36_max_num));
  max3 max3_45 (
    .Y(max3_46_max), .X(max3_44_max), .Y_num(max3_46_max_num), .Max_num(max3_45_max_num),
    .X_num(max3_44_max_num));  // open: MAX
  max3 max3_46 (
    .Y(max3_39_max), .MAX(max3_46_max), .X(max3_38_max), .Y_num(max3_39_max_num), .Max_num(max3_46_max_num),
    .X_num(max3_38_max_num));
  // Probe on C0
  max3 max3_47 (
    .Y(max3_41_max), .MAX(max3_47_max), .X(max3_40_max), .Y_num(max3_41_max_num), .Max_num(max3_47_max_num),
    .X_num(max3_40_max_num));
  max3 max3_48 (
    .Y(max3_43_max), .MAX(max3_48_max), .X(max3_42_max), .Y_num(max3_43_max_num), .Max_num(max3_48_max_num),
    .X_num(max3_42_max_num));
  and and_45 (Lx0, V0, comparator_14_eq);
  Comparator #(.width(32), .mode("twosComplement")) comparator_14 (
    .a(Tag0), .b(in_3), .eq(comparator_14_eq));  // open: gt, lt
  and and_46 (Lx1, V1, comparator_15_eq);
  Comparator #(.width(32), .mode("twosComplement")) comparator_15 (
    .a(Tag1), .b(in_3), .eq(comparator_15_eq));  // open: gt, lt
  and and_47 (Lx2, V2, comparator_16_eq);
  Comparator #(.width(32), .mode("twosComplement")) comparator_16 (
    .a(Tag2), .b(in_3), .eq(comparator_16_eq));  // open: gt, lt
  and and_48 (Lx3, V3, comparator_17_eq);
  Comparator #(.width(32), .mode("twosComplement")) comparator_17 (
    .a(Tag3), .b(in_3), .eq(comparator_17_eq));  // open: gt, lt
  and and_49 (Lx4, V4, comparator_18_eq);
  Comparator #(.width(32), .mode("twosComplement")) comparator_18 (
    .a(Tag4), .b(in_3), .eq(comparator_18_eq));  // open: gt, lt
  and and_50 (Lx5, V5, comparator_19_eq);
  Comparator #(.width(32), .mode("twosComplement")) comparator_19 (
    .a(Tag5), .b(in_3), .eq(comparator_19_eq));  // open: gt, lt
  and and_51 (Lx6, V6, comparator_20_eq);
  Comparator #(.width(32), .mode("twosComplement")) comparator_20 (
    .a(Tag6), .b(in_3), .eq(comparator_20_eq));  // open: gt, lt
  and and_52 (Lx7, V7, comparator_21_eq);
  Comparator #(.width(32), .mode("twosComplement")) comparator_21 (
    .a(Tag7), .b(in_3), .eq(comparator_21_eq));  // open: gt, lt
  max3 max3_49 (.Y(C1), .MAX(max3_49_max), .X(C0), .Y_num(3'b001), .Max_num(max3_49_max_num), .X_num(3'b000));
  max3 max3_50 (.Y(C3), .MAX(max3_50_max), .X(C2), .Y_num(3'b011), .Max_num(max3_50_max_num), .X_num(3'b010));
  max3 max3_51 (.Y(C5), .MAX(max3_51_max), .X(C4), .Y_num(3'b101), .Max_num(max3_51_max_num), .X_num(3'b100));
  max3 max3_52 (.Y(C7), .MAX(max3_52_max), .X(C6), .Y_num(3'b111), .Max_num(max3_52_max_num), .X_num(3'b110));
  max3 max3_53 (
    .Y(max3_48_max), .X(max3_47_max), .Y_num(max3_48_max_num), .Max_num(max3_53_max_num),
    .X_num(max3_47_max_num));  // open: MAX
  and and_53 (and_53_out, Miss_t, V0, V1, V2, V3, V4, V5, V6, ~V7);  // AND_Gate
  and and_54 (and_54_out, Miss_t, V0, V1, V2, V3, V4, V5, V6, V7);
  and and_55 (and_55_out, and_54_out, comparator_22_eq);
  Comparator #(.width(3), .mode("twosComplement")) comparator_22 (
    .a(max3_45_max_num), .b(3'b111), .eq(comparator_22_eq));  // open: gt, lt
  max3 max3_54 (
    .Y(max3_50_max), .MAX(max3_54_max), .X(max3_49_max), .Y_num(max3_50_max_num), .Max_num(max3_54_max_num),
    .X_num(max3_49_max_num));
  max3 max3_55 (
    .Y(max3_52_max), .MAX(max3_55_max), .X(max3_51_max), .Y_num(max3_52_max_num), .Max_num(max3_55_max_num),
    .X_num(max3_51_max_num));
  and and_56 (and_56_out, Miss_t, V0, V1, V2, V3, V4, V5, ~V6);  // AND_Gate
  and and_57 (and_57_out, Miss_t, V0, V1, V2, V3, V4, V5, V6, V7);
  and and_58 (and_58_out, and_57_out, comparator_23_eq);
  Comparator #(.width(3), .mode("twosComplement")) comparator_23 (
    .a(max3_53_max_num), .b(3'b110), .eq(comparator_23_eq));  // open: gt, lt
  or or_31 (or_31_out, and_53_out, and_55_out);
  max3 max3_56 (
    .Y(max3_55_max), .X(max3_54_max), .Y_num(max3_55_max_num), .Max_num(max3_56_max_num),
    .X_num(max3_54_max_num));  // open: MAX
  or or_32 (or_32_out, and_56_out, and_58_out);
  and and_59 (WriteL7, BlkDataReady, or_31_out);
  and and_60 (and_60_out, Miss_t, ~V0);  // AND_Gate
  and and_61 (and_61_out, Miss_t, V0, V1, V2, V3, V4, V5, V6, V7);
  Comparator #(.width(3), .mode("twosComplement")) comparator_24 (
    .a(max3_56_max_num), .b(3'b000), .eq(comparator_24_eq));  // open: gt, lt
  and and_62 (WriteL6, BlkDataReady, or_32_out);
  or or_33 (HIT, L0, L1, L2, L3, L4, L5, L6, L7);
  or or_34 (or_34_out, and_60_out, and_63_out);
  and and_63 (and_63_out, and_61_out, comparator_24_eq);
  not not_2 (Miss, HIT);
  and and_64 (WriteL0, BlkDataReady, or_34_out);

  // Other names for the same wires on the sheet: Blk[31:0] = BlockDataIn; BlkReady = BlkDataReady; Missx = Miss;
  //   SlotData[31:0] = sd; Tag[31:0] = Addr; Tag_x[31:0] = in_3

  // Notes on the sheet:
  //   输入引脚区
  //   请勿增改引脚，请勿修改子电路封装
  //   电路功能：利用上面给定的隧道构建8行的Cache，cache映射方式自选
  //   请在下方利用上方输入输出引脚的隧道信号构建电路，ctrl+d复制选择部件
  //   输出引脚区
endmodule

module IF_ID (
  input  [31:0] in_1,
  input  CLK,
  input  \同步清零_气泡_高电平有效 ,
  input  \使能端_低电平有效_stall_高电平有效 ,
  input  [31:0] in_5,
  input  [1:0] in_6,
  input  in_7,
  input  [31:0] in_8,
  output [31:0] out_9,
  output \传输状态Out_表明当前传输数据有效 ,
  output [31:0] out_11,
  output [1:0] out_12,
  output out_13,
  output [31:0] out_14
);

  wire multiplexer_4_out;
  wire [1:0] multiplexer_3_out;
  wire [31:0] multiplexer_1_out, multiplexer_2_out, multiplexer_5_out;

  Multiplexer #(.select(1), .width(32), .disabled("Z"), .enable("false")) multiplexer_1 (
    .in0(in_1), .in1({32{1'b0}}), .out(multiplexer_1_out), .sel(\同步清零_气泡_高电平有效 ));
  Multiplexer #(.select(1), .width(32), .disabled("Z"), .enable("false")) multiplexer_2 (
    .in0(in_5), .in1({32{1'b0}}), .out(multiplexer_2_out), .sel(\同步清零_气泡_高电平有效 ));
  Multiplexer #(.select(1), .width(2), .disabled("Z"), .enable("false")) multiplexer_3 (
    .in0(in_6), .in1(2'b00), .out(multiplexer_3_out), .sel(\同步清零_气泡_高电平有效 ));
  Multiplexer #(.select(1), .width(1), .disabled("Z"), .enable("false")) multiplexer_4 (
    .in0(in_7), .in1(1'b0), .out(multiplexer_4_out), .sel(\同步清零_气泡_高电平有效 ));
  Multiplexer #(.select(1), .width(32), .disabled("Z"), .enable("false")) multiplexer_5 (
    .in0(in_8), .in1({32{1'b0}}), .out(multiplexer_5_out), .sel(\同步清零_气泡_高电平有效 ));
  Pull_Resistor #(.pull(0)) pull_resistor_1 (.node(\同步清零_气泡_高电平有效 ));
  Register #(.width(32), .trigger("rising"), .Select("low")) register_1 (
    .D(multiplexer_1_out), .en(\使能端_低电平有效_stall_高电平有效 ), .Q(out_9), .clk(CLK));  // open: clr
  Register #(.width(1), .trigger("rising"), .Select("low")) register_2 (
    .D(\使能端_低电平有效_stall_高电平有效 ), .Q(\传输状态Out_表明当前传输数据有效 ), .clk(CLK));  // open: en, clr
  Register #(.width(32), .trigger("rising"), .Select("low")) register_3 (
    .D(multiplexer_2_out), .en(\使能端_低电平有效_stall_高电平有效 ), .Q(out_11), .clk(CLK));  // open: clr
  Register #(.width(2), .trigger("rising"), .Select("low")) register_4 (
    .D(multiplexer_3_out), .en(\使能端_低电平有效_stall_高电平有效 ), .Q(out_12), .clk(CLK));  // open: clr
  Register #(.width(1), .trigger("rising"), .Select("low")) register_5 (
    .D(multiplexer_4_out), .en(\使能端_低电平有效_stall_高电平有效 ), .Q(out_13), .clk(CLK));  // open: clr
  Register #(.width(32), .trigger("rising"), .Select("low")) register_6 (
    .D(multiplexer_5_out), .en(\使能端_低电平有效_stall_高电平有效 ), .Q(out_14), .clk(CLK));  // open: clr
endmodule

module ID_EX (
  input  [31:0] in_1,
  input  \异步清零 ,
  input  CLK,
  input  \同步清零_气泡_高电平有效 ,
  input  \使能端_低电平有效_stall_高电平有效 ,
  input  [31:0] in_6,
  input  [31:0] in_7,
  input  [31:0] in_8,
  input  [31:0] in_9,
  input  [31:0] in_10,
  input  in_11,
  input  in_12,
  input  in_13,
  input  in_14,
  input  in_15,
  input  in_16,
  input  in_17,
  input  in_18,
  input  in_19,
  input  in_20,
  input  [3:0] in_21,
  input  in_22,
  input  [1:0] in_23,
  input  [1:0] in_24,
  input  [1:0] in_25,
  input  in_26,
  input  [31:0] in_27,
  output [31:0] out_28,
  output \传输状态Out_表明当前传输数据有效 ,
  output [31:0] out_30,
  output [31:0] out_31,
  output [31:0] out_32,
  output [31:0] out_33,
  output [31:0] out_34,
  output out_35,
  output out_36,
  output out_37,
  output out_38,
  output out_39,
  output out_40,
  output out_41,
  output out_42,
  output out_43,
  output out_44,
  output [3:0] out_45,
  output out_46,
  output [1:0] out_47,
  output [1:0] out_48,
  output [1:0] out_49,
  output out_50,
  output [31:0] out_51
);

  wire multiplexer_7_out, multiplexer_8_out, multiplexer_9_out, multiplexer_10_out, multiplexer_11_out,
       multiplexer_12_out, multiplexer_13_out, multiplexer_14_out, multiplexer_15_out, multiplexer_16_out,
       multiplexer_18_out, multiplexer_22_out;
  wire [1:0] multiplexer_19_out, multiplexer_20_out, multiplexer_21_out;
  wire [3:0] multiplexer_17_out;
  wire [31:0] multiplexer_1_out, multiplexer_2_out, multiplexer_3_out, multiplexer_4_out, multiplexer_5_out,
       multiplexer_6_out, multiplexer_23_out;

  Multiplexer #(.select(1), .width(32), .disabled("Z"), .enable("false")) multiplexer_1 (
    .in0(in_1), .in1({32{1'b0}}), .out(multiplexer_1_out), .sel(\同步清零_气泡_高电平有效 ));
  Multiplexer #(.select(1), .width(32), .disabled("Z"), .enable("false")) multiplexer_2 (
    .in0(in_6), .in1({32{1'b0}}), .out(multiplexer_2_out), .sel(\同步清零_气泡_高电平有效 ));
  Multiplexer #(.select(1), .width(32), .disabled("Z"), .enable("false")) multiplexer_3 (
    .in0(in_7), .in1({32{1'b0}}), .out(multiplexer_3_out), .sel(\同步清零_气泡_高电平有效 ));
  Multiplexer #(.select(1), .width(32), .disabled("Z"), .enable("false")) multiplexer_4 (
    .in0(in_8), .in1({32{1'b0}}), .out(multiplexer_4_out), .sel(\同步清零_气泡_高电平有效 ));
  Multiplexer #(.select(1), .width(32), .disabled("Z"), .enable("false")) multiplexer_5 (
    .in0(in_9), .in1({32{1'b0}}), .out(multiplexer_5_out), .sel(\同步清零_气泡_高电平有效 ));
  Multiplexer #(.select(1), .width(32), .disabled("Z"), .enable("false")) multiplexer_6 (
    .in0(in_10), .in1({32{1'b0}}), .out(multiplexer_6_out), .sel(\同步清零_气泡_高电平有效 ));
  Multiplexer #(.select(1), .width(1), .disabled("Z"), .enable("false")) multiplexer_7 (
    .in0(in_11), .in1(1'b0), .out(multiplexer_7_out), .sel(\同步清零_气泡_高电平有效 ));
  Multiplexer #(.select(1), .width(1), .disabled("Z"), .enable("false")) multiplexer_8 (
    .in0(in_12), .in1(1'b0), .out(multiplexer_8_out), .sel(\同步清零_气泡_高电平有效 ));
  Multiplexer #(.select(1), .width(1), .disabled("Z"), .enable("false")) multiplexer_9 (
    .in0(in_13), .in1(1'b0), .out(multiplexer_9_out), .sel(\同步清零_气泡_高电平有效 ));
  Multiplexer #(.select(1), .width(1), .disabled("Z"), .enable("false")) multiplexer_10 (
    .in0(in_14), .in1(1'b0), .out(multiplexer_10_out), .sel(\同步清零_气泡_高电平有效 ));
  Multiplexer #(.select(1), .width(1), .disabled("Z"), .enable("false")) multiplexer_11 (
    .in0(in_15), .in1(1'b0), .out(multiplexer_11_out), .sel(\同步清零_气泡_高电平有效 ));
  Multiplexer #(.select(1), .width(1), .disabled("Z"), .enable("false")) multiplexer_12 (
    .in0(in_16), .in1(1'b0), .out(multiplexer_12_out), .sel(\同步清零_气泡_高电平有效 ));
  Multiplexer #(.select(1), .width(1), .disabled("Z"), .enable("false")) multiplexer_13 (
    .in0(in_17), .in1(1'b0), .out(multiplexer_13_out), .sel(\同步清零_气泡_高电平有效 ));
  Multiplexer #(.select(1), .width(1), .disabled("Z"), .enable("false")) multiplexer_14 (
    .in0(in_18), .in1(1'b0), .out(multiplexer_14_out), .sel(\同步清零_气泡_高电平有效 ));
  Multiplexer #(.select(1), .width(1), .disabled("Z"), .enable("false")) multiplexer_15 (
    .in0(in_19), .in1(1'b0), .out(multiplexer_15_out), .sel(\同步清零_气泡_高电平有效 ));
  Multiplexer #(.select(1), .width(1), .disabled("Z"), .enable("false")) multiplexer_16 (
    .in0(in_20), .in1(1'b0), .out(multiplexer_16_out), .sel(\同步清零_气泡_高电平有效 ));
  Multiplexer #(.select(1), .width(4), .disabled("Z"), .enable("false")) multiplexer_17 (
    .in0(in_21), .in1(4'b0000), .out(multiplexer_17_out), .sel(\同步清零_气泡_高电平有效 ));
  Multiplexer #(.select(1), .width(1), .disabled("Z"), .enable("false")) multiplexer_18 (
    .in0(in_22), .in1(1'b0), .out(multiplexer_18_out), .sel(\同步清零_气泡_高电平有效 ));
  Multiplexer #(.select(1), .width(2), .disabled("Z"), .enable("false")) multiplexer_19 (
    .in0(in_23), .in1(2'b00), .out(multiplexer_19_out), .sel(\同步清零_气泡_高电平有效 ));
  Multiplexer #(.select(1), .width(2), .disabled("Z"), .enable("false")) multiplexer_20 (
    .in0(in_24), .in1(2'b00), .out(multiplexer_20_out), .sel(\同步清零_气泡_高电平有效 ));
  Multiplexer #(.select(1), .width(2), .disabled("Z"), .enable("false")) multiplexer_21 (
    .in0(in_25), .in1(2'b00), .out(multiplexer_21_out), .sel(\同步清零_气泡_高电平有效 ));
  Multiplexer #(.select(1), .width(1), .disabled("Z"), .enable("false")) multiplexer_22 (
    .in0(in_26), .in1(1'b0), .out(multiplexer_22_out), .sel(\同步清零_气泡_高电平有效 ));
  Multiplexer #(.select(1), .width(32), .disabled("Z"), .enable("false")) multiplexer_23 (
    .in0(in_27), .in1({32{1'b0}}), .out(multiplexer_23_out), .sel(\同步清零_气泡_高电平有效 ));
  Pull_Resistor #(.pull(0)) pull_resistor_1 (.node(\同步清零_气泡_高电平有效 ));
  Register #(.width(32), .trigger("rising"), .Select("low")) register_1 (
    .D(multiplexer_1_out), .en(\使能端_低电平有效_stall_高电平有效 ), .Q(out_28), .clk(CLK), .clr(\异步清零 ));
  Register #(.width(1), .trigger("rising"), .Select("low")) register_2 (
    .D(\使能端_低电平有效_stall_高电平有效 ), .Q(\传输状态Out_表明当前传输数据有效 ), .clk(CLK), .clr(\异步清零 ));  // open: en
  Register #(.width(32), .trigger("rising"), .Select("low")) register_3 (
    .D(multiplexer_2_out), .en(\使能端_低电平有效_stall_高电平有效 ), .Q(out_30), .clk(CLK), .clr(\异步清零 ));
  Register #(.width(32), .trigger("rising"), .Select("low")) register_4 (
    .D(multiplexer_3_out), .en(\使能端_低电平有效_stall_高电平有效 ), .Q(out_31), .clk(CLK), .clr(\异步清零 ));
  Register #(.width(32), .trigger("rising"), .Select("low")) register_5 (
    .D(multiplexer_4_out), .en(\使能端_低电平有效_stall_高电平有效 ), .Q(out_32), .clk(CLK), .clr(\异步清零 ));
  Register #(.width(32), .trigger("rising"), .Select("low")) register_6 (
    .D(multiplexer_5_out), .en(\使能端_低电平有效_stall_高电平有效 ), .Q(out_33), .clk(CLK), .clr(\异步清零 ));
  Register #(.width(32), .trigger("rising"), .Select("low")) register_7 (
    .D(multiplexer_6_out), .en(\使能端_低电平有效_stall_高电平有效 ), .Q(out_34), .clk(CLK), .clr(\异步清零 ));
  Register #(.width(1), .trigger("rising"), .Select("low")) register_8 (
    .D(multiplexer_7_out), .en(\使能端_低电平有效_stall_高电平有效 ), .Q(out_35), .clk(CLK), .clr(\异步清零 ));
  Register #(.width(1), .trigger("rising"), .Select("low")) register_9 (
    .D(multiplexer_8_out), .en(\使能端_低电平有效_stall_高电平有效 ), .Q(out_36), .clk(CLK), .clr(\异步清零 ));
  Register #(.width(1), .trigger("rising"), .Select("low")) register_10 (
    .D(multiplexer_9_out), .en(\使能端_低电平有效_stall_高电平有效 ), .Q(out_37), .clk(CLK), .clr(\异步清零 ));
  Register #(.width(1), .trigger("rising"), .Select("low")) register_11 (
    .D(multiplexer_10_out), .en(\使能端_低电平有效_stall_高电平有效 ), .Q(out_38), .clk(CLK), .clr(\异步清零 ));
  Register #(.width(1), .trigger("rising"), .Select("low")) register_12 (
    .D(multiplexer_11_out), .en(\使能端_低电平有效_stall_高电平有效 ), .Q(out_39), .clk(CLK), .clr(\异步清零 ));
  Register #(.width(1), .trigger("rising"), .Select("low")) register_13 (
    .D(multiplexer_12_out), .en(\使能端_低电平有效_stall_高电平有效 ), .Q(out_40), .clk(CLK), .clr(\异步清零 ));
  Register #(.width(1), .trigger("rising"), .Select("low")) register_14 (
    .D(multiplexer_13_out), .en(\使能端_低电平有效_stall_高电平有效 ), .Q(out_41), .clk(CLK), .clr(\异步清零 ));
  Register #(.width(1), .trigger("rising"), .Select("low")) register_15 (
    .D(multiplexer_14_out), .en(\使能端_低电平有效_stall_高电平有效 ), .Q(out_42), .clk(CLK), .clr(\异步清零 ));
  Register #(.width(1), .trigger("rising"), .Select("low")) register_16 (
    .D(multiplexer_15_out), .en(\使能端_低电平有效_stall_高电平有效 ), .Q(out_43), .clk(CLK), .clr(\异步清零 ));
  Register #(.width(1), .trigger("rising"), .Select("low")) register_17 (
    .D(multiplexer_16_out), .en(\使能端_低电平有效_stall_高电平有效 ), .Q(out_44), .clk(CLK), .clr(\异步清零 ));
  Register #(.width(4), .trigger("rising"), .Select("low")) register_18 (
    .D(multiplexer_17_out), .en(\使能端_低电平有效_stall_高电平有效 ), .Q(out_45), .clk(CLK), .clr(\异步清零 ));
  Register #(.width(1), .trigger("rising"), .Select("low")) register_19 (
    .D(multiplexer_18_out), .en(\使能端_低电平有效_stall_高电平有效 ), .Q(out_46), .clk(CLK), .clr(\异步清零 ));
  Register #(.width(2), .trigger("rising"), .Select("low")) register_20 (
    .D(multiplexer_19_out), .en(\使能端_低电平有效_stall_高电平有效 ), .Q(out_47), .clk(CLK), .clr(\异步清零 ));
  Register #(.width(2), .trigger("rising"), .Select("low")) register_21 (
    .D(multiplexer_20_out), .en(\使能端_低电平有效_stall_高电平有效 ), .Q(out_48), .clk(CLK), .clr(\异步清零 ));
  Register #(.width(2), .trigger("rising"), .Select("low")) register_22 (
    .D(multiplexer_21_out), .en(\使能端_低电平有效_stall_高电平有效 ), .Q(out_49), .clk(CLK), .clr(\异步清零 ));
  Register #(.width(1), .trigger("rising"), .Select("low")) register_23 (
    .D(multiplexer_22_out), .en(\使能端_低电平有效_stall_高电平有效 ), .Q(out_50), .clk(CLK), .clr(\异步清零 ));
  Register #(.width(32), .trigger("rising"), .Select("low")) register_24 (
    .D(multiplexer_23_out), .en(\使能端_低电平有效_stall_高电平有效 ), .Q(out_51), .clk(CLK), .clr(\异步清零 ));
  Pull_Resistor #(.pull(0)) pull_resistor_2 (.node(\异步清零 ));
endmodule

module EX_MEM (
  input  [31:0] in_1,
  input  CLK,
  input  \使能端_低电平有效_stall_高电平有效 ,
  input  [31:0] in_4,
  input  [31:0] in_5,
  input  [31:0] in_6,
  input  in_7,
  input  in_8,
  input  in_9,
  input  in_10,
  input  in_11,
  input  \同步清零_气泡_高电平有效 ,
  input  in_13,
  output [31:0] out_14,
  output \传输状态Out_表明当前传输数据有效 ,
  output [31:0] out_16,
  output [31:0] out_17,
  output [31:0] out_18,
  output out_19,
  output out_20,
  output out_21,
  output out_22,
  output out_23,
  output out_24
);

  wire undriven;

  Pull_Resistor #(.pull(0)) pull_resistor_1 (.node(\同步清零_气泡_高电平有效 ));
  Register #(.width(32), .trigger("rising"), .Select("low")) register_1 (
    .D(in_1), .en(\使能端_低电平有效_stall_高电平有效 ), .Q(out_14), .clk(CLK), .clr(\同步清零_气泡_高电平有效 ));
  Register #(.width(1), .trigger("rising"), .Select("low")) register_2 (
    .D(\使能端_低电平有效_stall_高电平有效 ), .Q(\传输状态Out_表明当前传输数据有效 ), .clk(CLK), .clr(\同步清零_气泡_高电平有效 ), .preset(undriven));  // open: en, cs
  Register #(.width(32), .trigger("rising"), .Select("low")) register_3 (
    .D(in_4), .en(\使能端_低电平有效_stall_高电平有效 ), .Q(out_16), .clk(CLK), .clr(\同步清零_气泡_高电平有效 ));
  Register #(.width(32), .trigger("rising"), .Select("low")) register_4 (
    .D(in_5), .en(\使能端_低电平有效_stall_高电平有效 ), .Q(out_17), .clk(CLK), .clr(\同步清零_气泡_高电平有效 ));
  Register #(.width(32), .trigger("rising"), .Select("low")) register_5 (
    .D(in_6), .en(\使能端_低电平有效_stall_高电平有效 ), .Q(out_18), .clk(CLK), .clr(\同步清零_气泡_高电平有效 ));
  Register #(.width(1), .trigger("rising"), .Select("low")) register_6 (
    .D(in_7), .en(\使能端_低电平有效_stall_高电平有效 ), .Q(out_19), .clk(CLK), .clr(\同步清零_气泡_高电平有效 ));
  Register #(.width(1), .trigger("rising"), .Select("low")) register_7 (
    .D(in_8), .en(\使能端_低电平有效_stall_高电平有效 ), .Q(out_20), .clk(CLK), .clr(\同步清零_气泡_高电平有效 ));
  Register #(.width(1), .trigger("rising"), .Select("low")) register_8 (
    .D(in_9), .en(\使能端_低电平有效_stall_高电平有效 ), .Q(out_21), .clk(CLK), .clr(\同步清零_气泡_高电平有效 ));
  Register #(.width(1), .trigger("rising"), .Select("low")) register_9 (
    .D(in_10), .en(\使能端_低电平有效_stall_高电平有效 ), .Q(out_22), .clk(CLK), .clr(\同步清零_气泡_高电平有效 ));
  Register #(.width(1), .trigger("rising"), .Select("low")) register_10 (
    .D(in_11), .en(\使能端_低电平有效_stall_高电平有效 ), .Q(out_23), .clk(CLK), .clr(\同步清零_气泡_高电平有效 ));
  Register #(.width(1), .trigger("rising"), .Select("low")) register_11 (
    .D(in_13), .en(\使能端_低电平有效_stall_高电平有效 ), .Q(out_24), .clk(CLK), .clr(\同步清零_气泡_高电平有效 ));
endmodule

module MEM_WB (
  input  [31:0] in_1,
  input  CLK,
  input  \使能端_低电平有效_stall_高电平有效 ,
  input  [31:0] in_4,
  input  [31:0] in_5,
  input  [31:0] in_6,
  input  in_7,
  input  in_8,
  input  in_9,
  input  in_10,
  input  \同步清零_气泡_高电平有效 ,
  input  in_12,
  output [31:0] out_13,
  output \传输状态Out_表明当前传输数据有效 ,
  output [31:0] out_15,
  output [31:0] out_16,
  output [31:0] out_17,
  output out_18,
  output out_19,
  output out_20,
  output out_21,
  output out_22
);

  wire undriven, undriven_2;

  Pull_Resistor #(.pull(0)) pull_resistor_1 (.node(\同步清零_气泡_高电平有效 ));
  Register #(.width(32), .trigger("rising"), .Select("low")) register_1 (
    .D(in_1), .en(\使能端_低电平有效_stall_高电平有效 ), .Q(out_13), .clk(CLK), .clr(\同步清零_气泡_高电平有效 ));
  Register #(.width(1), .trigger("rising"), .Select("low")) register_2 (
    .D(\使能端_低电平有效_stall_高电平有效 ), .Q(\传输状态Out_表明当前传输数据有效 ), .clk(CLK), .clr(\同步清零_气泡_高电平有效 ));  // open: en
  Register #(.width(32), .trigger("rising"), .Select("low")) register_3 (
    .D(in_4), .en(\使能端_低电平有效_stall_高电平有效 ), .Q(out_15), .clk(CLK));  // open: clr
  Register #(.width(32), .trigger("rising"), .Select("low")) register_4 (
    .D(in_5), .en(\使能端_低电平有效_stall_高电平有效 ), .Q(out_16), .clk(CLK), .clr(\同步清零_气泡_高电平有效 ));
  Register #(.width(32), .trigger("rising"), .Select("low")) register_5 (
    .D(in_6), .en(\使能端_低电平有效_stall_高电平有效 ), .Q(out_17), .clk(CLK), .clr(\同步清零_气泡_高电平有效 ), .preset(undriven));  // open: cs
  Register #(.width(1), .trigger("rising"), .Select("low")) register_6 (
    .D(in_7), .en(\使能端_低电平有效_stall_高电平有效 ), .Q(out_18), .clk(CLK), .clr(\同步清零_气泡_高电平有效 ));
  Register #(.width(1), .trigger("rising"), .Select("low")) register_7 (
    .D(in_8), .en(\使能端_低电平有效_stall_高电平有效 ), .Q(out_19), .clk(CLK), .clr(\同步清零_气泡_高电平有效 ));
  Register #(.width(1), .trigger("rising"), .Select("low")) register_8 (
    .D(in_9), .en(\使能端_低电平有效_stall_高电平有效 ), .Q(out_20), .clk(CLK), .clr(\同步清零_气泡_高电平有效 ), .preset(undriven_2));  // open: cs
  Register #(.width(1), .trigger("rising"), .Select("low")) register_9 (
    .D(in_10), .en(\使能端_低电平有效_stall_高电平有效 ), .Q(out_21), .clk(CLK), .clr(\同步清零_气泡_高电平有效 ));
  Register #(.width(1), .trigger("rising"), .Select("low")) register_10 (
    .D(in_12), .en(\使能端_低电平有效_stall_高电平有效 ), .Q(out_22), .clk(CLK), .clr(\同步清零_气泡_高电平有效 ));
endmodule

module \中断按键参考电路  (
  input  \同步清零信号 ,
  output \与中断屏蔽位与 
);

  wire \_1号中断_out , and_1_out, clock_1_out, d_ff_1_q, or_1_out, or_2_out;

  Clock #(.highDuration(1), .lowDuration(1)) clock_1 (.out(clock_1_out));
  Button \_1号中断  (.out(\_1号中断_out ));
  LED #(.active("true")) \_1号中断等待指示灯  (.in(or_1_out));
  or or_1 (or_1_out, \与中断屏蔽位与 , d_ff_1_q);
  D_Flip_Flop #(.trigger("rising"), .Pre_Clr_Positions("LEGACY"), .NegatePresetClear("false"), .enable("true"), .NewFFLayout("false")) d_ff_1 (
    .clk(\_1号中断_out ), .D(1'b1), .Q(d_ff_1_q), .reset(\与中断屏蔽位与 ));  // open: Qn, preset, en
  or or_2 (or_2_out, d_ff_1_q, \与中断屏蔽位与 );
  and and_1 (and_1_out, or_2_out, ~\同步清零信号 );  // AND_Gate
  D_Flip_Flop #(.trigger("rising"), .Pre_Clr_Positions("LEGACY"), .NegatePresetClear("false"), .enable("true"), .NewFFLayout("false")) IR1 (
    .clk(clock_1_out), .D(and_1_out), .Q(\与中断屏蔽位与 ));  // open: Qn, preset, en, reset

  // Notes on the sheet:
  //   中断信号采样参考电路
  //   Reset 
endmodule

// Max3
module max3 (
  input  [15:0] Y,
  input  [15:0] X,
  input  [2:0] Y_num,
  input  [2:0] X_num,
  output [15:0] MAX,
  output [2:0] Max_num
);

  wire comparator_1_eq, comparator_1_gt, or_1_out;

  Multiplexer #(.select(1), .width(16), .disabled("Z"), .enable("false")) multiplexer_1 (
    .in0(Y), .in1(X), .out(MAX), .sel(or_1_out));
  Comparator #(.width(16), .mode("unsigned")) comparator_1 (
    .a(X), .b(Y), .gt(comparator_1_gt), .eq(comparator_1_eq));  // open: lt
  or or_1 (or_1_out, comparator_1_gt, comparator_1_eq);
  Multiplexer #(.select(1), .width(3), .disabled("Z"), .enable("false")) multiplexer_2 (
    .in0(Y_num), .in1(X_num), .out(Max_num), .sel(or_1_out));

  // Notes on the sheet:
  //   输出两个输入中的较大值，并输出较大值的3位编号
endmodule
