// Logisim project cpu多级中断.circ as structural Verilog: 18 circuits, main circuit ◇单周期MIPS+多级中断
module \单周期MIPS_多级中断  (
  input  IR1,
  input  IR2,
  input  IR3,
  output RegWrite,
  output MemWrite,
  output [31:0] PC,
  output [31:0] IR,
  output [31:0] RDin,
  output [31:0] MDin,
  output [31:0] LedData
);

  wire and_1_out, and_2_out, and_3_out, and_4_out, and_7_out, and_9_out, and_10_out, and_11_out, BGEZ, CLK,
       comparator_1_eq, comparator_2_eq, comparator_3_eq, comparator_4_eq, comparator_5_eq, comparator_6_eq,
       comparator_7_eq, comparator_7_gt, comparator_8_eq, comparator_9_eq, comparator_10_eq,
       comparator_11_eq, comparator_12_eq, comparator_13_eq, comparator_14_gt, \CPU中断请求 , d_ff_1_q, d_ff_2_q,
       d_ff_3_q, demultiplexer_1_out1, demultiplexer_1_out2, demultiplexer_1_out3, ERET, Go, IE, IR1_q,
       IR1_t, IR2_q, IR2_t, IR3_q, IR3_t, IRA, IRB, IRC, MFC0, MTC0, multiplexer_16_out, multiplexer_18_out,
       multiplexer_19_out, nand_1_out, not_1_out, or_1_out, or_4_out, or_5_out, or_10_out, or_11_out,
       or_12_out, or_13_out, or_14_out, or_15_out, or_16_out, or_17_out, RST, SignedExt, SLLV, syscall,
       tunnel, W1, W2, W3, \单周期硬布线控制器_1_alu_src , \单周期硬布线控制器_1_beq , \单周期硬布线控制器_1_bne , \单周期硬布线控制器_1_jal ,
       \单周期硬布线控制器_1_jmp , \单周期硬布线控制器_1_jr , \单周期硬布线控制器_1_memtoreg , \单周期硬布线控制器_1_regdst ;
  wire [1:0] multiplexer_23_out, multiplexer_24_out, multiplexer_25_out, priority_encoder_1_out,
       register_1_q, register_2_q, register_3_q, register_4_q;
  wire [3:0] \单周期硬布线控制器_1_alu_op ;
  wire [4:0] multiplexer_6_out, multiplexer_7_out, multiplexer_8_out, multiplexer_9_out, SHAMT;
  wire [15:0] multiplexer_14_out, \总周期数 , \无条件分支数 , \条件分支成功数 ;
  wire [27:0] adder_1_out_2;
  wire [31:0] adder_2_out, bit_extender_1_out, bit_extender_2_out, EPC_2_q, EPC_3_q, EPC_q,
       mips_alu_1_result, multiplexer_2_out, multiplexer_3_out, multiplexer_4_out, multiplexer_5_out,
       multiplexer_10_out, multiplexer_11_out, multiplexer_13_out, multiplexer_15_out, multiplexer_17_out,
       multiplexer_21_out, multiplexer_22_out, R1, RDOUT, realnextpc, shifter_1_out;
  wire [31:28] adder_1_out;

  Clock #(.highDuration(1), .lowDuration(1)) clock_1 (.out(CLK));
  Button _1 (.out(IRA));
  Button _2 (.out(IRB));
  Button _3 (.out(IRC));
  Button \u_总复位  (.out(RST));
  Register #(.width(32), .trigger("rising"), .Select("low")) u_PC (
    .D(multiplexer_2_out), .en(nand_1_out), .Q(PC), .clk(CLK), .clr(RST));
  Multiplexer #(.select(1), .width(32), .disabled("Z"), .enable("false")) multiplexer_1 (
    .in0(multiplexer_3_out), .in1(R1), .out(realnextpc), .sel(\单周期硬布线控制器_1_jr ));
  Multiplexer #(.select(1), .width(32), .disabled("Z"), .enable("false")) multiplexer_2 (
    .in0(multiplexer_4_out), .in1(EPC_q), .out(multiplexer_2_out), .sel(ERET));
  // Probe on multiplexer_2_out
  Button \u_继续运行  (.out(Go));
  LED #(.active("true")) led_1 (.in(W1));
  LED #(.active("true")) led_2 (.in(W2));
  LED #(.active("true")) led_3 (.in(W3));
  // Probe on PC
  Multiplexer #(.select(1), .width(32), .disabled("Z"), .enable("false")) multiplexer_3 (
    .in0(multiplexer_5_out), .in1({adder_1_out, IR[25:0], 2'b00}), .out(multiplexer_3_out), .sel(or_1_out));
  or or_1 (or_1_out, \单周期硬布线控制器_1_jal , \单周期硬布线控制器_1_jmp );
  Multiplexer #(.select(1), .width(32), .disabled("Z"), .enable("false")) multiplexer_4 (
    .in0(realnextpc), .in1(multiplexer_22_out), .out(multiplexer_4_out), .sel(\CPU中断请求 ));
  Hex_Digit_Display hex_digit_display_1 (.value(LedData[31:28]));  // open: dp
  ROM #(.addrWidth(10), .dataWidth(32), .Select("high")) rom_1 (.addr(PC[11:2]), .data(IR));
  Adder #(.width(32)) adder_1 (.a(PC), .b(32'h4), .out({adder_1_out, adder_1_out_2}));  // open: cin, cout
  Multiplexer #(.select(1), .width(32), .disabled("Z"), .enable("false")) multiplexer_5 (
    .in0({adder_1_out, adder_1_out_2}), .in1(adder_2_out), .out(multiplexer_5_out), .sel(or_5_out));
  Hex_Digit_Display hex_digit_display_2 (.value(LedData[27:24]));  // open: dp
  Hex_Digit_Display hex_digit_display_3 (.value(LedData[23:20]));  // open: dp
  Multiplexer #(.select(1), .width(5), .disabled("Z"), .enable("false")) multiplexer_6 (
    .in0(IR[25:21]), .in1(5'b00100), .out(multiplexer_6_out), .sel(syscall));
  Multiplexer #(.select(1), .width(5), .disabled("Z"), .enable("false")) multiplexer_7 (
    .in0(IR[20:16]), .in1(5'b00010), .out(multiplexer_7_out), .sel(syscall));
  Hex_Digit_Display hex_digit_display_4 (.value(LedData[19:16]));  // open: dp
  Hex_Digit_Display hex_digit_display_5 (.value(LedData[15:12]));  // open: dp
  Multiplexer #(.select(1), .width(5), .disabled("Z"), .enable("false")) multiplexer_8 (
    .in0(IR[20:16]), .in1(IR[15:11]), .out(multiplexer_8_out), .sel(\单周期硬布线控制器_1_regdst ));
  assign bit_extender_1_out = {{16{IR[15]}}, IR[15:0]};  // Bit_Extender bit_extender_1
  assign bit_extender_2_out = {{16{1'b0}}, IR[15:0]};  // Bit_Extender bit_extender_2
  Comparator #(.width(32), .mode("twosComplement")) comparator_1 (
    .a(MDin), .b(32'h22), .eq(comparator_1_eq));  // open: gt, lt
  Counter #(.width(16), .max('hffff), .ongoal("wrap"), .trigger("rising"), .behavior("old")) counter_1 (
    .count(nand_1_out), .Q(\总周期数 ), .clk(CLK), .clr(RST));  // open: load, D, carry, preset
  Hex_Digit_Display hex_digit_display_6 (.value(LedData[11:8]));  // open: dp
  Hex_Digit_Display hex_digit_display_7 (.value(LedData[7:4]));  // open: dp
  // Probe on \总周期数 
  MIPS_Regifile mips_regifile_1 (
    .Din(RDin), .Clk(CLK), .R1(R1), .R2(MDin), .WE(RegWrite), .W_num(multiplexer_9_out),
    .R1_num(multiplexer_6_out), .R2_num(multiplexer_7_out));
  Multiplexer #(.select(1), .width(5), .disabled("Z"), .enable("false")) multiplexer_9 (
    .in0(multiplexer_8_out), .in1({5{1'b1}}), .out(multiplexer_9_out), .sel(\单周期硬布线控制器_1_jal ));
  Shifter #(.width(32), .shift("ll")) shifter_1 (.in(bit_extender_1_out), .\dist (5'b00010), .out(shifter_1_out));
  Multiplexer #(.select(1), .width(32), .disabled("Z"), .enable("false")) multiplexer_10 (
    .in0(bit_extender_2_out), .in1(bit_extender_1_out), .out(multiplexer_10_out), .sel(SignedExt));
  and and_1 (and_1_out, comparator_1_eq, syscall);
  and and_2 (and_2_out, syscall, ~comparator_1_eq);  // AND_Gate
  Hex_Digit_Display hex_digit_display_8 (.value(LedData[3:0]));  // open: dp
  Multiplexer #(.select(1), .width(32), .disabled("Z"), .enable("false")) multiplexer_11 (
    .in0(MDin), .in1(multiplexer_10_out), .out(multiplexer_11_out), .sel(\单周期硬布线控制器_1_alu_src ));
  Multiplexer #(.select(1), .width(32), .disabled("Z"), .enable("false")) multiplexer_12 (
    .in0(multiplexer_13_out), .in1({adder_1_out, adder_1_out_2}), .out(RDin), .sel(\单周期硬布线控制器_1_jal ));
  Adder #(.width(32)) adder_2 (
    .a(shifter_1_out), .b({adder_1_out, adder_1_out_2}), .out(adder_2_out));  // open: cin, cout
  nand nand_1 (nand_1_out, and_2_out, ~Go);  // NAND_Gate
  MIPS_ALU mips_alu_1 (
    .X(R1), .Y(multiplexer_11_out), .AluOP(\单周期硬布线控制器_1_alu_op ), .Equal(tunnel), .Result(mips_alu_1_result),
    .shamt(SHAMT));  // open: Result_2
  Register #(.width(32), .trigger("rising"), .Select("low")) u_leddata (
    .D(R1), .en(and_1_out), .Q(LedData), .clk(CLK), .clr(RST));
  or or_2 (IR1_t, IR1, IRA);
  Multiplexer #(.select(1), .width(32), .disabled("Z"), .enable("false")) multiplexer_13 (
    .in0(mips_alu_1_result), .in1(multiplexer_15_out), .out(multiplexer_13_out), .sel(\单周期硬布线控制器_1_memtoreg ));
  Comparator #(.width(6), .mode("twosComplement")) comparator_2 (
    .a(IR[31:26]), .b(6'b100101), .eq(comparator_2_eq));  // open: gt, lt
  or or_3 (IR2_t, IR2, IRB);
  RAM #(.addrWidth(11), .dataWidth(32), .bus("separate"), .Select("high")) ram_1 (
    .addr(mips_alu_1_result[12:2]), .din(MDin), .data(RDOUT), .str(MemWrite), .clk(CLK), .clr(RST));  // open: sel, ld
  or or_4 (or_4_out, or_1_out, \单周期硬布线控制器_1_jr );
  Multiplexer #(.select(1), .width(16), .disabled("Z"), .enable("false")) multiplexer_14 (
    .in0(RDOUT[15:0]), .in1(RDOUT[31:16]), .out(multiplexer_14_out), .sel(mips_alu_1_result[1]));
  \单周期硬布线控制器  \u_单周期硬布线控制器_1  (
    .Func(IR[5:0]), .OP(IR[31:26]), .ALU_OP(\单周期硬布线控制器_1_alu_op ), .MemToReg(\单周期硬布线控制器_1_memtoreg ),
    .MemWrite(MemWrite), .ALU_SRC(\单周期硬布线控制器_1_alu_src ), .RegWrite(RegWrite), .SysCALL(syscall),
    .SignedExt(SignedExt), .RegDst(\单周期硬布线控制器_1_regdst ), .JR(\单周期硬布线控制器_1_jr ), .JMP(\单周期硬布线控制器_1_jmp ),
    .Beq(\单周期硬布线控制器_1_beq ), .JAL(\单周期硬布线控制器_1_jal ), .Bne(\单周期硬布线控制器_1_bne ));
  and and_3 (and_3_out, \单周期硬布线控制器_1_bne , ~tunnel);  // AND_Gate
  or or_5 (or_5_out, and_3_out, and_7_out, and_4_out);
  and and_4 (and_4_out, \单周期硬布线控制器_1_beq , tunnel);
  Counter #(.width(16), .max('hffff), .ongoal("wrap"), .trigger("rising"), .behavior("old")) counter_2 (
    .count(or_5_out), .Q(\条件分支成功数 ), .clk(CLK), .clr(RST));  // open: load, D, carry, preset
  Counter #(.width(16), .max('hffff), .ongoal("wrap"), .trigger("rising"), .behavior("old")) counter_3 (
    .count(or_4_out), .Q(\无条件分支数 ), .clk(CLK), .clr(RST));  // open: load, D, carry, preset
  or or_6 (IR3_t, IR3, IRC);
  Multiplexer #(.select(1), .width(32), .disabled("Z"), .enable("false")) multiplexer_15 (
    .in0(RDOUT), .in1({{16{1'b0}}, multiplexer_14_out}), .out(multiplexer_15_out), .sel(comparator_2_eq));
  Comparator #(.width(6), .mode("twosComplement")) comparator_3 (
    .a(IR[31:26]), .b(6'b010000), .eq(comparator_3_eq));  // open: gt, lt
  Comparator #(.width(6), .mode("twosComplement")) comparator_4 (
    .a(IR[5:0]), .b(6'b011000), .eq(comparator_4_eq));  // open: gt, lt
  // Probe on comparator_4_eq
  Comparator #(.width(6), .mode("twosComplement")) comparator_5 (
    .a(IR[31:26]), .b(6'b000001), .eq(comparator_5_eq));  // open: gt, lt
  Comparator #(.width(5), .mode("twosComplement")) comparator_6 (
    .a(5'b00001), .b(IR[20:16]), .eq(comparator_6_eq));  // open: gt, lt
  Comparator #(.width(32), .mode("twosComplement")) comparator_7 (
    .a(R1), .b({32{1'b0}}), .gt(comparator_7_gt), .eq(comparator_7_eq));  // open: lt
  or or_7 (W1, IR1_q, d_ff_1_q);
  or or_8 (W2, IR2_q, d_ff_2_q);
  or or_9 (W3, IR3_q, d_ff_3_q);
  and and_5 (ERET, comparator_3_eq, comparator_4_eq);
  // Probe on ERET
  and and_6 (BGEZ, comparator_5_eq, comparator_6_eq);
  or or_10 (or_10_out, \CPU中断请求 , ERET);
  or or_11 (or_11_out, comparator_7_gt, comparator_7_eq);
  D_Flip_Flop #(.trigger("rising"), .Pre_Clr_Positions("LEGACY"), .NegatePresetClear("false"), .enable("true"), .NewFFLayout("false")) d_ff_1 (
    .clk(IR1_t), .D(1'b1), .Q(d_ff_1_q), .reset(IR1_q));  // open: Qn, preset, en
  D_Flip_Flop #(.trigger("rising"), .Pre_Clr_Positions("LEGACY"), .NegatePresetClear("false"), .enable("true"), .NewFFLayout("false")) d_ff_2 (
    .clk(IR2_t), .D(1'b1), .Q(d_ff_2_q), .reset(IR2_q));  // open: Qn, preset, en
  D_Flip_Flop #(.trigger("rising"), .Pre_Clr_Positions("LEGACY"), .NegatePresetClear("false"), .enable("true"), .NewFFLayout("false")) d_ff_3 (
    .clk(IR3_t), .D(1'b1), .Q(d_ff_3_q), .reset(IR3_q));  // open: Qn, preset, en
  and and_7 (and_7_out, BGEZ, or_11_out);
  or or_12 (or_12_out, d_ff_1_q, IR1_q);
  or or_13 (or_13_out, d_ff_2_q, IR2_q);
  or or_14 (or_14_out, d_ff_3_q, IR3_q);
  Comparator #(.width(6), .mode("twosComplement")) comparator_8 (
    .a(IR[31:26]), .b(6'b010000), .eq(comparator_8_eq));  // open: gt, lt
  and and_8 (MTC0, comparator_8_eq, comparator_9_eq);
  Comparator #(.width(5), .mode("twosComplement")) comparator_9 (
    .a(IR[25:21]), .b(5'b00100), .eq(comparator_9_eq));  // open: gt, lt
  // Probe on MTC0
  and and_9 (and_9_out, or_12_out, ~demultiplexer_1_out1);  // AND_Gate
  and and_10 (and_10_out, or_13_out, ~demultiplexer_1_out2);  // AND_Gate
  and and_11 (and_11_out, or_14_out, ~demultiplexer_1_out3);  // AND_Gate
  Multiplexer #(.select(1), .width(1), .disabled("Z"), .enable("false")) multiplexer_16 (
    .in0(\CPU中断请求 ), .in1(1'b0), .out(multiplexer_16_out), .sel(or_16_out));
  Comparator #(.width(6), .mode("twosComplement")) comparator_10 (
    .a(IR[31:26]), .b(6'b010000), .eq(comparator_10_eq));  // open: gt, lt
  and and_12 (MFC0, comparator_10_eq, comparator_11_eq);
  // Probe on MFC0
  Comparator #(.width(5), .mode("twosComplement")) comparator_11 (
    .a(IR[25:21]), .b({5{1'b0}}), .eq(comparator_11_eq));  // open: gt, lt
  Comparator #(.width(6), .mode("twosComplement")) comparator_12 (
    .a(IR[31:26]), .b({6{1'b0}}), .eq(comparator_12_eq));  // open: gt, lt
  and and_13 (SLLV, comparator_12_eq, comparator_13_eq);
  Comparator #(.width(6), .mode("twosComplement")) comparator_13 (
    .a(IR[5:0]), .b(6'b000100), .eq(comparator_13_eq));  // open: gt, lt
  Multiplexer #(.select(1), .width(32), .disabled("Z"), .enable("false")) multiplexer_17 (
    .in0(EPC_2_q), .in1(realnextpc), .out(multiplexer_17_out), .sel(\CPU中断请求 ));
  D_Flip_Flop #(.trigger("rising"), .Pre_Clr_Positions("LEGACY"), .NegatePresetClear("false"), .enable("true"), .NewFFLayout("false")) u_IR1 (
    .clk(CLK), .D(and_9_out), .Q(IR1_q));  // open: Qn, preset, en, reset
  D_Flip_Flop #(.trigger("rising"), .Pre_Clr_Positions("LEGACY"), .NegatePresetClear("false"), .enable("true"), .NewFFLayout("false")) u_IR2 (
    .clk(CLK), .D(and_10_out), .Q(IR2_q));  // open: Qn, preset, en, reset
  D_Flip_Flop #(.trigger("rising"), .Pre_Clr_Positions("LEGACY"), .NegatePresetClear("false"), .enable("true"), .NewFFLayout("false")) u_IR3 (
    .clk(CLK), .D(and_11_out), .Q(IR3_q));  // open: Qn, preset, en, reset
  Multiplexer #(.select(1), .width(1), .disabled("Z"), .enable("false")) multiplexer_18 (
    .in0(multiplexer_16_out), .in1(1'b1), .out(multiplexer_18_out), .sel(MTC0));
  Multiplexer #(.select(1), .width(1), .disabled("Z"), .enable("false")) multiplexer_19 (
    .in0(not_1_out), .in1(1'b1), .out(multiplexer_19_out), .sel(or_15_out));
  Register #(.width(32), .trigger("rising"), .Select("low")) EPC (
    .D(multiplexer_17_out), .en(or_10_out), .Q(EPC_q), .clk(CLK));  // open: clr
  // Probe on EPC_q
  // Probe on demultiplexer_1_out3
  Priority_Encoder #(.select(2), .disabled("Z")) priority_encoder_1 (
    .in0(1'b1), .in1(IR1_q), .in2(IR2_q), .in3(IR3_q), .out(priority_encoder_1_out));  // open: gs, en_out, en_in
  Register #(.width(1), .trigger("rising"), .Select("low")) u_IE (
    .D(multiplexer_18_out), .en(multiplexer_19_out), .Q(IE), .clk(CLK));  // open: clr
  not not_1 (not_1_out, IE);
  or or_15 (or_15_out, or_16_out, MTC0);
  Multiplexer #(.select(1), .width(5), .disabled("Z"), .enable("false")) multiplexer_20 (
    .in0(IR[10:6]), .in1(R1[4:0]), .out(SHAMT), .sel(SLLV));
  Multiplexer #(.select(1), .width(32), .disabled("Z"), .enable("false")) multiplexer_21 (
    .in0(EPC_3_q), .in1(EPC_q), .out(multiplexer_21_out), .sel(\CPU中断请求 ));
  Demultiplexer #(.select(2), .width(1), .tristate("false"), .disabled("Z"), .enable("false")) demultiplexer_1 (
    .out1(demultiplexer_1_out1), .out2(demultiplexer_1_out2), .out3(demultiplexer_1_out3), .in(ERET),
    .sel(register_1_q));  // open: out0
  // Probe on priority_encoder_1_out
  and and_14 (\CPU中断请求 , comparator_14_gt, ~IE);  // AND_Gate
  // Probe on \CPU中断请求 
  or or_16 (or_16_out, ERET, MFC0);
  Register #(.width(32), .trigger("rising"), .Select("low")) EPC_2 (
    .D(multiplexer_21_out), .en(or_10_out), .Q(EPC_2_q), .clk(CLK));  // open: clr
  // Probe on EPC_2_q
  // Probe on priority_encoder_1_out
  Multiplexer #(.select(2), .width(32), .disabled("Z"), .enable("false")) multiplexer_22 (
    .in1(32'h30ac), .in2(32'h3158), .in3(32'h3204), .out(multiplexer_22_out), .sel(priority_encoder_1_out));  // open: in0
  Multiplexer #(.select(1), .width(2), .disabled("Z"), .enable("false")) multiplexer_23 (
    .in0(register_2_q), .in1(priority_encoder_1_out), .out(multiplexer_23_out), .sel(\CPU中断请求 ));
  Register #(.width(2), .trigger("rising"), .Select("low")) register_1 (
    .D(multiplexer_23_out), .en(or_17_out), .Q(register_1_q), .clk(CLK));  // open: clr
  or or_17 (or_17_out, \CPU中断请求 , ERET);
  Register #(.width(32), .trigger("rising"), .Select("low")) EPC_3 (
    .D(EPC_2_q), .en(or_10_out), .Q(EPC_3_q), .clk(CLK));  // open: clr
  // Probe on register_1_q
  Comparator #(.width(2), .mode("unsigned")) comparator_14 (
    .a(priority_encoder_1_out), .b(register_1_q), .gt(comparator_14_gt));  // open: eq, lt
  // Probe on comparator_14_gt
  // Probe on register_2_q
  Multiplexer #(.select(1), .width(2), .disabled("Z"), .enable("false")) multiplexer_24 (
    .in0(register_3_q), .in1(register_1_q), .out(multiplexer_24_out), .sel(\CPU中断请求 ));
  Register #(.width(2), .trigger("rising"), .Select("low")) register_2 (
    .D(multiplexer_24_out), .en(or_17_out), .Q(register_2_q), .clk(CLK));  // open: clr
  Multiplexer #(.select(1), .width(2), .disabled("Z"), .enable("false")) multiplexer_25 (
    .in0(register_4_q), .in1(register_2_q), .out(multiplexer_25_out), .sel(\CPU中断请求 ));
  // Probe on register_4_q
  Register #(.width(2), .trigger("rising"), .Select("low")) register_3 (
    .D(multiplexer_25_out), .en(or_17_out), .Q(register_3_q), .clk(CLK));  // open: clr
  Register #(.width(2), .trigger("rising"), .Select("low")) register_4 (
    .D(register_3_q), .en(or_17_out), .Q(register_4_q), .clk(CLK));  // open: clr

  // Other names for the same wires on the sheet: RT[4:0] = IR[20:16]; RS[4:0] = IR[25:21]

  // Notes on the sheet:
  //   中断源
  //   中断等待指示
  //   总复位信号应将除ROM以外所有存储组件全部清零
  //   指令存储器
  //   contents of rom_1 (hex, n*v repeats v):
  //   201d07d0 20100001 109fc0 139fc3 8021 2012000c 24160008 26100001 3210000f 20080008 20090001 139900
  //   2709825 132020 20020022 c 1094022 1500fff9 22100001 2018000f 2188024 108700 20080008 20090001 139902
  //   2709825 132021 20020022 c 1094022 1500fff9 108702 2c9b022 12c00001 8000c07 4020 1084027 84400
  //   3508ffff 82021 20020022 c 8000c01 afa20000 23bd0004 afa40000 23bd0004 afb00000 23bd0004 afb30000
  //   23bd0004 afb40000 23bd0004 afb50000 23bd0004 afb60000 23bd0004 40000000 20160001 20140003 20150001
  //   168020 108100 2149825 132020 20020022 c 1600fffa 295a022 1680fff7 40800000 23bdfffc 8fb60000
  //   23bdfffc 8fb50000 23bdfffc 8fb40000 23bdfffc 8fb30000 23bdfffc 8fb00000 23bdfffc 8fa40000 23bdfffc
  //   8fa20000 42000018 afa20000 23bd0004 afa40000 23bd0004 afb00000 23bd0004 afb30000 23bd0004 afb40000
  //   23bd0004 afb50000 23bd0004 afb60000 23bd0004 40000000 20160002 20140003 20150001 168020 108100
  //   2149825 132020 20020022 c 1600fffa 295a022 1680fff7 40800000 23bdfffc 8fb60000 23bdfffc 8fb50000
  //   23bdfffc 8fb40000 23bdfffc 8fb30000 23bdfffc 8fb00000 23bdfffc 8fa40000 23bdfffc 8fa20000 42000018
  //   afa20000 23bd0004 afa40000 23bd0004 afb00000 23bd0004 afb30000 23bd0004 afb40000 23bd0004 afb50000
  //   23bd0004 afb60000 23bd0004 40000000 20160003 20140003 20150001 168020 108100 2149825 132020 20020022
  //   c 1600fffa 295a022 1680fff7 40800000 23bdfffc 8fb60000 23bdfffc 8fb50000 23bdfffc 8fb40000 23bdfffc
  //   8fb30000 23bdfffc 8fb00000 23bdfffc 8fa40000 23bdfffc 8fa20000 42000018
  //   OP
  //   Func
  //   rs
  //   指令字
  //   rt
  //   rd
  //   数码管输出
  //   数码管输出应该用寄存器锁存，否则显示数据只能一闪而过
  //   OP
  //   rs
  //   rt
  //   JMP
  //   JR
  //   OP
  //   Func
  //   Syscall
  //   Beq
  //   Bne
  //   MemToReg
  //   MemWrite
  //   AluOP
  //   AluSrcB
  //   RegWrite
  //   JAL
  //   RegDst
  //   为方便自动评测，需要输出PC，IR，寄存器堆写如数据RDin
  //   RAM写使能MemWrite、RAM写入数据MDin等信号
  //   Reset 
  //   Reset 
  //   Reset 
  //   多级中断信号产生
endmodule

// 单周期硬布线控制器
module \单周期硬布线控制器  (
  input  [5:0] OP,
  input  [5:0] Func,
  output [3:0] ALU_OP,
  output MemToReg,
  output MemWrite,
  output ALU_SRC,
  output RegWrite,
  output SysCALL,
  output SignedExt,
  output RegDst,
  output Beq,
  output Bne,
  output JR,
  output JMP,
  output JAL
);

  \运算控制器自动生成  \u_运算控制器自动生成_1  (
    .OP0(OP[0]), .OP1(OP[1]), .OP2(OP[2]), .OP3(OP[3]), .OP4(OP[4]), .OP5(OP[5]), .F0(Func[0]), .F1(Func[1]),
    .F2(Func[2]), .F3(Func[3]), .F4(Func[4]), .F5(Func[5]), .S0(ALU_OP[0]), .S1(ALU_OP[1]), .S2(ALU_OP[2]),
    .S3(ALU_OP[3]));
  \控制信号自动生成  \u_控制信号自动生成_1  (
    .OP0(OP[0]), .OP1(OP[1]), .OP2(OP[2]), .OP3(OP[3]), .OP4(OP[4]), .OP5(OP[5]), .F0(Func[0]), .F1(Func[1]),
    .F2(Func[2]), .F3(Func[3]), .F4(Func[4]), .F5(Func[5]), .MemToReg(MemToReg), .MemWrite(MemWrite),
    .ALU_SRC(ALU_SRC), .RegWrite(RegWrite), .SysCALL(SysCALL), .SignedExt(SignedExt), .RegDst(RegDst),
    .BEQ(Beq), .BNE(Bne), .JR(JR), .JUMP(JMP), .JAL(JAL));

  // Other names for the same wires on the sheet: OP_CODE[5:0] = OP

  // Notes on the sheet:
  //   运算器控制器，根据指令生成运算器功能选择信号
  //   控制信号生成，产生数据通路需要的其他控制信号
endmodule

// 运算器控制器
module \运算控制器自动生成  (
  input  OP0,
  input  OP1,
  input  OP2,
  input  OP3,
  input  OP4,
  input  OP5,
  input  F0,
  input  F1,
  input  F2,
  input  F3,
  input  F4,
  input  F5,
  output S0,
  output S1,
  output S2,
  output S3
);

  wire and_1_out, and_2_out, and_3_out, and_4_out, and_5_out, and_6_out, and_7_out, and_8_out, and_9_out,
       and_10_out, and_11_out, and_12_out, and_13_out, and_14_out, and_15_out, and_16_out, and_17_out,
       and_18_out, and_19_out, and_20_out, and_21_out, and_22_out, and_23_out, and_24_out, and_25_out,
       and_26_out, and_27_out, and_28_out, and_29_out, and_30_out, and_31_out, and_32_out, and_33_out,
       and_34_out, and_35_out, and_36_out, and_37_out, and_38_out, and_39_out, and_40_out, and_41_out,
       and_42_out, and_43_out, and_44_out, and_45_out, and_46_out, and_47_out, and_48_out, and_49_out,
       and_50_out, and_51_out, and_52_out, not_1_out, not_2_out, not_3_out, not_4_out, not_5_out, not_6_out,
       not_7_out, not_8_out, not_9_out, not_10_out, not_11_out, not_12_out, not_13_out, not_14_out,
       not_15_out, not_16_out, not_17_out, not_18_out, not_19_out, not_20_out, not_21_out, not_22_out,
       not_23_out, not_24_out, not_25_out, not_26_out, not_27_out, not_28_out, not_29_out, not_30_out,
       not_31_out, not_32_out, not_33_out, not_34_out, not_35_out, not_36_out, not_37_out, not_38_out,
       not_39_out, not_40_out, not_41_out, not_42_out, not_43_out, not_44_out, not_45_out, not_46_out,
       not_47_out, not_48_out, not_49_out, not_50_out, not_51_out, not_52_out, not_53_out, not_54_out,
       not_55_out, not_56_out, not_57_out, not_58_out, not_59_out, not_60_out, not_61_out, not_62_out,
       not_63_out, not_64_out, not_65_out, not_66_out, not_67_out, not_68_out, not_69_out, not_70_out,
       not_71_out, not_72_out, not_73_out, not_74_out, not_75_out, not_76_out, not_77_out, not_78_out,
       not_79_out, not_80_out, not_81_out, not_82_out, not_83_out, not_84_out, not_85_out, not_86_out,
       not_87_out, not_88_out, not_89_out, not_90_out, not_91_out, not_92_out, not_93_out, not_94_out,
       not_95_out, not_96_out, not_97_out, not_98_out, not_99_out, not_100_out, not_101_out, not_102_out,
       not_103_out, not_104_out, not_105_out, not_106_out, not_107_out, not_108_out, not_109_out,
       not_110_out, not_111_out, not_112_out, not_113_out, not_114_out, not_115_out, not_116_out,
       not_117_out, not_118_out, not_119_out, not_120_out, not_121_out, not_122_out, not_123_out,
       not_124_out, not_125_out, not_126_out, not_127_out, not_128_out, not_129_out, not_130_out,
       not_131_out, not_132_out, not_133_out, not_134_out, not_135_out, not_136_out, not_137_out,
       not_138_out, not_139_out, not_140_out, not_141_out, not_142_out, not_143_out, not_144_out,
       not_145_out, not_146_out, not_147_out, not_148_out, not_149_out, not_150_out, not_151_out,
       not_152_out, not_153_out, not_154_out, not_155_out, not_156_out, not_157_out, not_158_out,
       not_159_out, not_160_out, not_161_out, not_162_out, not_163_out, not_164_out, not_165_out,
       not_166_out, not_167_out, not_168_out, not_169_out, not_170_out, not_171_out, not_172_out,
       not_173_out, not_174_out, not_175_out, not_176_out, not_177_out, not_178_out, not_179_out,
       not_180_out, not_181_out, not_182_out, not_183_out, not_184_out, not_185_out, not_186_out,
       not_187_out, not_188_out, not_189_out, not_190_out, not_191_out, not_192_out, not_193_out,
       not_194_out, not_195_out, not_196_out, not_197_out, not_198_out, not_199_out, not_200_out,
       not_201_out, not_202_out, not_203_out, not_204_out, not_205_out, not_206_out, not_207_out,
       not_208_out, not_209_out, not_210_out, not_211_out, not_212_out, not_213_out, not_214_out,
       not_215_out, not_216_out, not_217_out, not_218_out, not_219_out, not_220_out, not_221_out,
       not_222_out, not_223_out, not_224_out, not_225_out, not_226_out, not_227_out, not_228_out,
       not_229_out, not_230_out, not_231_out, not_232_out, not_233_out, not_234_out, not_235_out,
       not_236_out, not_237_out, not_238_out, not_239_out, not_240_out, not_241_out, not_242_out,
       not_243_out, not_244_out, not_245_out, not_246_out, not_247_out, not_248_out, not_249_out,
       not_250_out, not_251_out, not_252_out, not_253_out, not_254_out, not_255_out, not_256_out,
       not_257_out, not_258_out, not_259_out, not_260_out, not_261_out, not_262_out, not_263_out,
       not_264_out, not_265_out, not_266_out, not_267_out, not_268_out, not_269_out, not_270_out,
       not_271_out, not_272_out, not_273_out, not_274_out, not_275_out, not_276_out, not_277_out,
       not_278_out, not_279_out, not_280_out, not_281_out, not_282_out, not_283_out, not_284_out,
       not_285_out, not_286_out, not_287_out, not_288_out, not_289_out, not_290_out, not_291_out,
       not_292_out, not_293_out, not_294_out, not_295_out, not_296_out, not_297_out, not_298_out,
       not_299_out, not_300_out, not_301_out, not_302_out, not_303_out, not_304_out, not_305_out,
       not_306_out, not_307_out, not_308_out, not_309_out, not_310_out, not_311_out, not_312_out,
       not_313_out, not_314_out, not_315_out, not_316_out, not_317_out, not_318_out, not_319_out,
       not_320_out, not_321_out, not_322_out, not_323_out, not_324_out, not_325_out, not_326_out,
       not_327_out, not_328_out, not_329_out, not_330_out, not_331_out, not_332_out, not_333_out,
       not_334_out, not_335_out, not_336_out;

  not not_1 (not_1_out, OP5);
  not not_2 (not_2_out, OP4);
  not not_3 (not_3_out, OP3);
  not not_4 (not_4_out, OP2);
  not not_5 (not_5_out, OP1);
  not not_6 (not_6_out, OP0);
  not not_7 (not_7_out, F5);
  not not_8 (not_8_out, F4);
  not not_9 (not_9_out, F3);
  not not_10 (not_10_out, F2);
  not not_11 (not_11_out, OP5);
  not not_12 (not_12_out, OP4);
  not not_13 (not_13_out, OP3);
  not not_14 (not_14_out, OP2);
  not not_15 (not_15_out, OP1);
  not not_16 (not_16_out, OP0);
  not not_17 (not_17_out, F4);
  not not_18 (not_18_out, F3);
  not not_19 (not_19_out, F2);
  not not_20 (not_20_out, F1);
  not not_21 (not_21_out, F0);
  not not_22 (not_22_out, OP5);
  not not_23 (not_23_out, OP4);
  not not_24 (not_24_out, OP3);
  not not_25 (not_25_out, OP2);
  not not_26 (not_26_out, OP1);
  not not_27 (not_27_out, OP0);
  not not_28 (not_28_out, F4);
  not not_29 (not_29_out, F3);
  not not_30 (not_30_out, F2);
  not not_31 (not_31_out, F1);
  not not_32 (not_32_out, OP5);
  not not_33 (not_33_out, OP4);
  not not_34 (not_34_out, OP3);
  not not_35 (not_35_out, OP2);
  not not_36 (not_36_out, OP1);
  not not_37 (not_37_out, OP0);
  not not_38 (not_38_out, F4);
  not not_39 (not_39_out, F3);
  not not_40 (not_40_out, F1);
  not not_41 (not_41_out, F0);
  not not_42 (not_42_out, OP5);
  not not_43 (not_43_out, OP4);
  not not_44 (not_44_out, OP3);
  not not_45 (not_45_out, OP2);
  not not_46 (not_46_out, OP1);
  not not_47 (not_47_out, OP0);
  not not_48 (not_48_out, F4);
  not not_49 (not_49_out, F2);
  not not_50 (not_50_out, F0);
  not not_51 (not_51_out, OP5);
  not not_52 (not_52_out, OP4);
  not not_53 (not_53_out, OP3);
  not not_54 (not_54_out, OP2);
  not not_55 (not_55_out, OP1);
  not not_56 (not_56_out, OP0);
  not not_57 (not_57_out, F5);
  not not_58 (not_58_out, F4);
  not not_59 (not_59_out, F2);
  not not_60 (not_60_out, F1);
  not not_61 (not_61_out, F0);
  not not_62 (not_62_out, OP5);
  not not_63 (not_63_out, OP4);
  not not_64 (not_64_out, OP3);
  not not_65 (not_65_out, OP2);
  not not_66 (not_66_out, OP1);
  not not_67 (not_67_out, OP0);
  not not_68 (not_68_out, F5);
  not not_69 (not_69_out, F4);
  not not_70 (not_70_out, F1);
  not not_71 (not_71_out, F0);
  not not_72 (not_72_out, OP5);
  not not_73 (not_73_out, OP4);
  not not_74 (not_74_out, OP3);
  not not_75 (not_75_out, OP2);
  not not_76 (not_76_out, OP0);
  not not_77 (not_77_out, OP5);
  not not_78 (not_78_out, OP4);
  not not_79 (not_79_out, OP3);
  not not_80 (not_80_out, OP2);
  not not_81 (not_81_out, OP5);
  not not_82 (not_82_out, OP4);
  not not_83 (not_83_out, OP2);
  not not_84 (not_84_out, OP1);
  not not_85 (not_85_out, OP0);
  not not_86 (not_86_out, OP5);
  not not_87 (not_87_out, OP4);
  not not_88 (not_88_out, OP1);
  not not_89 (not_89_out, OP0);
  not not_90 (not_90_out, OP5);
  not not_91 (not_91_out, OP4);
  not not_92 (not_92_out, OP2);
  not not_93 (not_93_out, OP1);
  not not_94 (not_94_out, OP5);
  not not_95 (not_95_out, OP4);
  not not_96 (not_96_out, OP2);
  not not_97 (not_97_out, OP0);
  not not_98 (not_98_out, OP4);
  not not_99 (not_99_out, OP3);
  not not_100 (not_100_out, OP2);
  not not_101 (not_101_out, OP4);
  not not_102 (not_102_out, OP2);
  not not_103 (not_103_out, OP5);
  not not_104 (not_104_out, OP4);
  not not_105 (not_105_out, OP0);
  not not_106 (not_106_out, OP4);
  not not_107 (not_107_out, OP3);
  not not_108 (not_108_out, OP1);
  not not_109 (not_109_out, OP5);
  not not_110 (not_110_out, OP4);
  not not_111 (not_111_out, OP3);
  not not_112 (not_112_out, OP2);
  not not_113 (not_113_out, OP1);
  not not_114 (not_114_out, OP0);
  not not_115 (not_115_out, F5);
  not not_116 (not_116_out, F4);
  not not_117 (not_117_out, F3);
  not not_118 (not_118_out, F2);
  not not_119 (not_119_out, F0);
  not not_120 (not_120_out, OP5);
  not not_121 (not_121_out, OP4);
  not not_122 (not_122_out, OP3);
  not not_123 (not_123_out, OP2);
  not not_124 (not_124_out, OP1);
  not not_125 (not_125_out, OP0);
  not not_126 (not_126_out, F4);
  not not_127 (not_127_out, F3);
  not not_128 (not_128_out, F2);
  not not_129 (not_129_out, F0);
  not not_130 (not_130_out, OP5);
  not not_131 (not_131_out, OP4);
  not not_132 (not_132_out, OP3);
  not not_133 (not_133_out, OP2);
  not not_134 (not_134_out, OP1);
  not not_135 (not_135_out, OP0);
  not not_136 (not_136_out, F4);
  not not_137 (not_137_out, F3);
  not not_138 (not_138_out, F1);
  not not_139 (not_139_out, F0);
  not not_140 (not_140_out, OP5);
  not not_141 (not_141_out, OP4);
  not not_142 (not_142_out, OP3);
  not not_143 (not_143_out, OP2);
  not not_144 (not_144_out, OP1);
  not not_145 (not_145_out, OP0);
  not not_146 (not_146_out, F4);
  not not_147 (not_147_out, F3);
  not not_148 (not_148_out, OP5);
  not not_149 (not_149_out, OP4);
  not not_150 (not_150_out, OP3);
  not not_151 (not_151_out, OP2);
  not not_152 (not_152_out, OP1);
  not not_153 (not_153_out, OP0);
  not not_154 (not_154_out, F4);
  not not_155 (not_155_out, F2);
  not not_156 (not_156_out, F0);
  not not_157 (not_157_out, OP5);
  not not_158 (not_158_out, OP4);
  not not_159 (not_159_out, OP3);
  not not_160 (not_160_out, OP1);
  not not_161 (not_161_out, OP0);
  not not_162 (not_162_out, OP5);
  not not_163 (not_163_out, OP4);
  not not_164 (not_164_out, OP3);
  not not_165 (not_165_out, OP1);
  not not_166 (not_166_out, OP5);
  not not_167 (not_167_out, OP4);
  not not_168 (not_168_out, OP1);
  not not_169 (not_169_out, OP0);
  not not_170 (not_170_out, OP5);
  not not_171 (not_171_out, OP4);
  not not_172 (not_172_out, OP2);
  not not_173 (not_173_out, OP0);
  not not_174 (not_174_out, OP5);
  not not_175 (not_175_out, OP4);
  not not_176 (not_176_out, OP3);
  not not_177 (not_177_out, OP2);
  not not_178 (not_178_out, OP1);
  not not_179 (not_179_out, OP5);
  not not_180 (not_180_out, OP4);
  not not_181 (not_181_out, OP3);
  not not_182 (not_182_out, OP2);
  not not_183 (not_183_out, OP1);
  not not_184 (not_184_out, OP0);
  not not_185 (not_185_out, F4);
  not not_186 (not_186_out, F3);
  not not_187 (not_187_out, F2);
  not not_188 (not_188_out, F1);
  not not_189 (not_189_out, F0);
  not not_190 (not_190_out, OP5);
  not not_191 (not_191_out, OP4);
  not not_192 (not_192_out, OP3);
  not not_193 (not_193_out, OP2);
  not not_194 (not_194_out, OP1);
  not not_195 (not_195_out, OP0);
  not not_196 (not_196_out, F4);
  not not_197 (not_197_out, F3);
  not not_198 (not_198_out, F2);
  not not_199 (not_199_out, F1);
  not not_200 (not_200_out, OP5);
  not not_201 (not_201_out, OP4);
  not not_202 (not_202_out, OP3);
  not not_203 (not_203_out, OP2);
  not not_204 (not_204_out, OP1);
  not not_205 (not_205_out, OP0);
  not not_206 (not_206_out, F4);
  not not_207 (not_207_out, F3);
  not not_208 (not_208_out, F2);
  not not_209 (not_209_out, F0);
  not not_210 (not_210_out, OP5);
  not not_211 (not_211_out, OP4);
  not not_212 (not_212_out, OP3);
  not not_213 (not_213_out, OP2);
  not not_214 (not_214_out, OP1);
  not not_215 (not_215_out, OP0);
  not not_216 (not_216_out, F4);
  not not_217 (not_217_out, F3);
  not not_218 (not_218_out, F1);
  not not_219 (not_219_out, F0);
  not not_220 (not_220_out, OP5);
  not not_221 (not_221_out, OP4);
  not not_222 (not_222_out, OP3);
  not not_223 (not_223_out, OP2);
  not not_224 (not_224_out, OP1);
  not not_225 (not_225_out, OP0);
  not not_226 (not_226_out, F4);
  not not_227 (not_227_out, F2);
  not not_228 (not_228_out, OP5);
  not not_229 (not_229_out, OP4);
  not not_230 (not_230_out, OP3);
  not not_231 (not_231_out, OP2);
  not not_232 (not_232_out, OP1);
  not not_233 (not_233_out, OP0);
  not not_234 (not_234_out, F5);
  not not_235 (not_235_out, F4);
  not not_236 (not_236_out, F2);
  not not_237 (not_237_out, F1);
  not not_238 (not_238_out, F0);
  not not_239 (not_239_out, OP5);
  not not_240 (not_240_out, OP4);
  not not_241 (not_241_out, OP3);
  not not_242 (not_242_out, OP2);
  not not_243 (not_243_out, OP1);
  not not_244 (not_244_out, OP0);
  not not_245 (not_245_out, F5);
  not not_246 (not_246_out, F4);
  not not_247 (not_247_out, F1);
  not not_248 (not_248_out, F0);
  not not_249 (not_249_out, OP5);
  not not_250 (not_250_out, OP4);
  not not_251 (not_251_out, OP3);
  not not_252 (not_252_out, OP2);
  not not_253 (not_253_out, OP0);
  not not_254 (not_254_out, OP5);
  not not_255 (not_255_out, OP4);
  not not_256 (not_256_out, OP3);
  not not_257 (not_257_out, OP2);
  not not_258 (not_258_out, OP5);
  not not_259 (not_259_out, OP4);
  not not_260 (not_260_out, OP3);
  not not_261 (not_261_out, OP1);
  not not_262 (not_262_out, OP0);
  not not_263 (not_263_out, OP5);
  not not_264 (not_264_out, OP4);
  not not_265 (not_265_out, OP3);
  not not_266 (not_266_out, OP1);
  not not_267 (not_267_out, OP5);
  not not_268 (not_268_out, OP4);
  not not_269 (not_269_out, OP2);
  not not_270 (not_270_out, OP1);
  not not_271 (not_271_out, OP0);
  not not_272 (not_272_out, OP5);
  not not_273 (not_273_out, OP4);
  not not_274 (not_274_out, OP1);
  not not_275 (not_275_out, OP0);
  not not_276 (not_276_out, OP5);
  not not_277 (not_277_out, OP4);
  not not_278 (not_278_out, OP2);
  not not_279 (not_279_out, OP1);
  not not_280 (not_280_out, OP4);
  not not_281 (not_281_out, OP3);
  not not_282 (not_282_out, OP2);
  not not_283 (not_283_out, OP4);
  not not_284 (not_284_out, OP2);
  not not_285 (not_285_out, OP4);
  not not_286 (not_286_out, OP3);
  not not_287 (not_287_out, OP1);
  not not_288 (not_288_out, OP5);
  not not_289 (not_289_out, OP4);
  not not_290 (not_290_out, OP3);
  not not_291 (not_291_out, OP2);
  not not_292 (not_292_out, OP1);
  not not_293 (not_293_out, OP5);
  not not_294 (not_294_out, OP4);
  not not_295 (not_295_out, OP3);
  not not_296 (not_296_out, OP2);
  not not_297 (not_297_out, OP1);
  not not_298 (not_298_out, OP0);
  not not_299 (not_299_out, F4);
  not not_300 (not_300_out, F3);
  not not_301 (not_301_out, F1);
  not not_302 (not_302_out, OP5);
  not not_303 (not_303_out, OP4);
  not not_304 (not_304_out, OP3);
  not not_305 (not_305_out, OP2);
  not not_306 (not_306_out, OP1);
  not not_307 (not_307_out, OP0);
  not not_308 (not_308_out, F4);
  not not_309 (not_309_out, F3);
  not not_310 (not_310_out, OP5);
  not not_311 (not_311_out, OP4);
  not not_312 (not_312_out, OP3);
  not not_313 (not_313_out, OP2);
  not not_314 (not_314_out, OP1);
  not not_315 (not_315_out, OP0);
  not not_316 (not_316_out, F4);
  not not_317 (not_317_out, F2);
  not not_318 (not_318_out, F0);
  not not_319 (not_319_out, OP5);
  not not_320 (not_320_out, OP4);
  not not_321 (not_321_out, OP3);
  not not_322 (not_322_out, OP2);
  not not_323 (not_323_out, OP1);
  not not_324 (not_324_out, OP0);
  not not_325 (not_325_out, F4);
  not not_326 (not_326_out, F2);
  not not_327 (not_327_out, OP5);
  not not_328 (not_328_out, OP4);
  not not_329 (not_329_out, OP2);
  not not_330 (not_330_out, OP0);
  not not_331 (not_331_out, OP5);
  not not_332 (not_332_out, OP4);
  not not_333 (not_333_out, OP1);
  not not_334 (not_334_out, OP5);
  not not_335 (not_335_out, OP4);
  not not_336 (not_336_out, OP0);
  and and_1 (and_1_out, not_1_out, not_2_out, not_3_out, not_4_out, not_5_out, not_6_out, not_7_out, not_8_out, not_9_out, not_10_out, F1, F0);
  and and_2 (and_2_out, not_11_out, not_12_out, not_13_out, not_14_out, not_15_out, not_16_out, F5, not_17_out, not_18_out, not_19_out, not_20_out, not_21_out);
  and and_3 (and_3_out, not_22_out, not_23_out, not_24_out, not_25_out, not_26_out, not_27_out, F5, not_28_out, not_29_out, not_30_out, not_31_out, F0);
  and and_4 (and_4_out, not_32_out, not_33_out, not_34_out, not_35_out, not_36_out, not_37_out, F5, not_38_out, not_39_out, F2, not_40_out, not_41_out);
  and and_5 (and_5_out, not_42_out, not_43_out, not_44_out, not_45_out, not_46_out, not_47_out, F5, not_48_out, F3, not_49_out, F1, not_50_out);
  and and_6 (and_6_out, not_51_out, not_52_out, not_53_out, not_54_out, not_55_out, not_56_out, not_57_out, not_58_out, F3, not_59_out, not_60_out, not_61_out);
  and and_7 (and_7_out, not_62_out, not_63_out, not_64_out, not_65_out, not_66_out, not_67_out, not_68_out, not_69_out, F3, F2, not_70_out, not_71_out);
  and and_8 (and_8_out, not_72_out, not_73_out, not_74_out, not_75_out, OP1, not_76_out);
  and and_9 (and_9_out, not_77_out, not_78_out, not_79_out, not_80_out, OP1, OP0);
  and and_10 (and_10_out, not_81_out, not_82_out, OP3, not_83_out, not_84_out, not_85_out);
  and and_11 (and_11_out, not_86_out, not_87_out, OP3, OP2, not_88_out, not_89_out);
  and and_12 (and_12_out, not_90_out, not_91_out, OP3, not_92_out, not_93_out, OP0);
  and and_13 (and_13_out, not_94_out, not_95_out, OP3, not_96_out, OP1, not_97_out);
  and and_14 (and_14_out, OP5, not_98_out, not_99_out, not_100_out, OP1, OP0);
  and and_15 (and_15_out, OP5, not_101_out, OP3, not_102_out, OP1, OP0);
  and and_16 (and_16_out, not_103_out, not_104_out, OP3, OP2, OP1, not_105_out);
  and and_17 (and_17_out, OP5, not_106_out, not_107_out, OP2, not_108_out, OP0);
  and and_18 (and_18_out, not_109_out, not_110_out, not_111_out, not_112_out, not_113_out, not_114_out, not_115_out, not_116_out, not_117_out, not_118_out, F1, not_119_out);
  and and_19 (and_19_out, not_120_out, not_121_out, not_122_out, not_123_out, not_124_out, not_125_out, F5, not_126_out, not_127_out, not_128_out, F1, not_129_out);
  and and_20 (and_20_out, not_130_out, not_131_out, not_132_out, not_133_out, not_134_out, not_135_out, F5, not_136_out, not_137_out, F2, not_138_out, not_139_out);
  and and_21 (and_21_out, not_140_out, not_141_out, not_142_out, not_143_out, not_144_out, not_145_out, F5, not_146_out, not_147_out, F2, F1, F0);
  and and_22 (and_22_out, not_148_out, not_149_out, not_150_out, not_151_out, not_152_out, not_153_out, F5, not_154_out, F3, not_155_out, F1, not_156_out);
  and and_23 (and_23_out, not_157_out, not_158_out, not_159_out, OP2, not_160_out, not_161_out);
  and and_24 (and_24_out, not_162_out, not_163_out, not_164_out, OP2, not_165_out, OP0);
  and and_25 (and_25_out, not_166_out, not_167_out, OP3, OP2, not_168_out, not_169_out);
  and and_26 (and_26_out, not_170_out, not_171_out, OP3, not_172_out, OP1, not_173_out);
  and and_27 (and_27_out, not_174_out, not_175_out, not_176_out, not_177_out, not_178_out, OP0);
  and and_28 (and_28_out, not_179_out, not_180_out, not_181_out, not_182_out, not_183_out, not_184_out, F5, not_185_out, not_186_out, not_187_out, not_188_out, not_189_out);
  and and_29 (and_29_out, not_190_out, not_191_out, not_192_out, not_193_out, not_194_out, not_195_out, F5, not_196_out, not_197_out, not_198_out, not_199_out, F0);
  and and_30 (and_30_out, not_200_out, not_201_out, not_202_out, not_203_out, not_204_out, not_205_out, F5, not_206_out, not_207_out, not_208_out, F1, not_209_out);
  and and_31 (and_31_out, not_210_out, not_211_out, not_212_out, not_213_out, not_214_out, not_215_out, F5, not_216_out, not_217_out, F2, not_218_out, not_219_out);
  and and_32 (and_32_out, not_220_out, not_221_out, not_222_out, not_223_out, not_224_out, not_225_out, F5, not_226_out, F3, not_227_out, F1, F0);
  and and_33 (and_33_out, not_228_out, not_229_out, not_230_out, not_231_out, not_232_out, not_233_out, not_234_out, not_235_out, F3, not_236_out, not_237_out, not_238_out);
  and and_34 (and_34_out, not_239_out, not_240_out, not_241_out, not_242_out, not_243_out, not_244_out, not_245_out, not_246_out, F3, F2, not_247_out, not_248_out);
  and and_35 (and_35_out, not_249_out, not_250_out, not_251_out, not_252_out, OP1, not_253_out);
  and and_36 (and_36_out, not_254_out, not_255_out, not_256_out, not_257_out, OP1, OP0);
  and and_37 (and_37_out, not_258_out, not_259_out, not_260_out, OP2, not_261_out, not_262_out);
  and and_38 (and_38_out, not_263_out, not_264_out, not_265_out, OP2, not_266_out, OP0);
  and and_39 (and_39_out, not_267_out, not_268_out, OP3, not_269_out, not_270_out, not_271_out);
  and and_40 (and_40_out, not_272_out, not_273_out, OP3, OP2, not_274_out, not_275_out);
  and and_41 (and_41_out, not_276_out, not_277_out, OP3, not_278_out, not_279_out, OP0);
  and and_42 (and_42_out, OP5, not_280_out, not_281_out, not_282_out, OP1, OP0);
  and and_43 (and_43_out, OP5, not_283_out, OP3, not_284_out, OP1, OP0);
  and and_44 (and_44_out, OP5, not_285_out, not_286_out, OP2, not_287_out, OP0);
  and and_45 (and_45_out, not_288_out, not_289_out, not_290_out, not_291_out, not_292_out, OP0);
  and and_46 (and_46_out, not_293_out, not_294_out, not_295_out, not_296_out, not_297_out, not_298_out, F5, not_299_out, not_300_out, F2, not_301_out, F0);
  and and_47 (and_47_out, not_302_out, not_303_out, not_304_out, not_305_out, not_306_out, not_307_out, F5, not_308_out, not_309_out, F2, F1, F0);
  and and_48 (and_48_out, not_310_out, not_311_out, not_312_out, not_313_out, not_314_out, not_315_out, F5, not_316_out, F3, not_317_out, F1, not_318_out);
  and and_49 (and_49_out, not_319_out, not_320_out, not_321_out, not_322_out, not_323_out, not_324_out, F5, not_325_out, F3, not_326_out, F1, F0);
  and and_50 (and_50_out, not_327_out, not_328_out, OP3, not_329_out, OP1, not_330_out);
  and and_51 (and_51_out, not_331_out, not_332_out, OP3, OP2, not_333_out, OP0);
  and and_52 (and_52_out, not_334_out, not_335_out, OP3, OP2, OP1, not_336_out);
  or or_1 (S1, and_18_out, and_19_out, and_20_out, and_21_out, and_22_out, and_23_out, and_24_out, and_25_out, and_26_out, and_27_out);
  or or_2 (S3, and_46_out, and_47_out, and_48_out, and_49_out, and_50_out, and_51_out, and_52_out);
  or or_3 (S0, and_1_out, and_2_out, and_3_out, and_4_out, and_5_out, and_6_out, and_7_out, and_8_out, and_9_out, and_10_out, and_11_out, and_12_out, and_13_out, and_14_out, and_15_out, and_16_out, and_17_out);
  or or_4 (S2, and_28_out, and_29_out, and_30_out, and_31_out, and_32_out, and_33_out, and_34_out, and_35_out, and_36_out, and_37_out, and_38_out, and_39_out, and_40_out, and_41_out, and_42_out, and_43_out, and_44_out, and_45_out);
endmodule

// 控制信号生成
module \控制信号自动生成  (
  input  OP0,
  input  OP1,
  input  OP2,
  input  OP3,
  input  OP4,
  input  OP5,
  input  F0,
  input  F1,
  input  F2,
  input  F3,
  input  F4,
  input  F5,
  output MemToReg,
  output MemWrite,
  output ALU_SRC,
  output RegWrite,
  output SysCALL,
  output SignedExt,
  output RegDst,
  output BEQ,
  output BNE,
  output JR,
  output JUMP,
  output JAL
);

  wire and_1_out, and_2_out, and_4_out, and_5_out, and_6_out, and_7_out, and_8_out, and_9_out, and_10_out,
       and_11_out, and_12_out, and_13_out, and_14_out, and_15_out, and_16_out, and_17_out, and_18_out,
       and_19_out, and_20_out, and_21_out, and_22_out, and_23_out, and_24_out, and_25_out, and_26_out,
       and_27_out, and_28_out, and_29_out, and_30_out, and_31_out, and_32_out, and_33_out, and_35_out,
       and_36_out, and_37_out, and_38_out, and_39_out, and_40_out, and_41_out, and_42_out, and_43_out,
       and_44_out, and_45_out, and_46_out, and_47_out, and_48_out, and_49_out, and_50_out, and_51_out,
       and_52_out, and_53_out, and_54_out, and_55_out, and_56_out, and_57_out, and_61_out, and_62_out,
       not_1_out, not_2_out, not_3_out, not_4_out, not_5_out, not_6_out, not_7_out, not_8_out, not_9_out,
       not_10_out, not_11_out, not_12_out, not_13_out, not_14_out, not_15_out, not_16_out, not_17_out,
       not_18_out, not_19_out, not_20_out, not_21_out, not_22_out, not_23_out, not_24_out, not_25_out,
       not_26_out, not_27_out, not_28_out, not_29_out, not_30_out, not_31_out, not_32_out, not_33_out,
       not_34_out, not_35_out, not_36_out, not_37_out, not_38_out, not_39_out, not_40_out, not_41_out,
       not_42_out, not_43_out, not_44_out, not_45_out, not_46_out, not_47_out, not_48_out, not_49_out,
       not_50_out, not_51_out, not_52_out, not_53_out, not_54_out, not_55_out, not_56_out, not_57_out,
       not_58_out, not_59_out, not_60_out, not_61_out, not_62_out, not_63_out, not_64_out, not_65_out,
       not_66_out, not_67_out, not_68_out, not_69_out, not_70_out, not_71_out, not_72_out, not_73_out,
       not_74_out, not_75_out, not_76_out, not_77_out, not_78_out, not_79_out, not_80_out, not_81_out,
       not_82_out, not_83_out, not_84_out, not_85_out, not_86_out, not_87_out, not_88_out, not_89_out,
       not_90_out, not_91_out, not_92_out, not_93_out, not_94_out, not_95_out, not_96_out, not_97_out,
       not_98_out, not_99_out, not_100_out, not_101_out, not_102_out, not_103_out, not_104_out, not_105_out,
       not_106_out, not_107_out, not_108_out, not_109_out, not_110_out, not_111_out, not_112_out,
       not_113_out, not_114_out, not_115_out, not_116_out, not_117_out, not_118_out, not_119_out,
       not_120_out, not_121_out, not_122_out, not_123_out, not_124_out, not_125_out, not_126_out,
       not_127_out, not_128_out, not_129_out, not_130_out, not_131_out, not_132_out, not_133_out,
       not_134_out, not_135_out, not_136_out, not_137_out, not_138_out, not_139_out, not_140_out,
       not_141_out, not_142_out, not_143_out, not_144_out, not_145_out, not_146_out, not_147_out,
       not_148_out, not_149_out, not_150_out, not_151_out, not_152_out, not_153_out, not_154_out,
       not_155_out, not_156_out, not_157_out, not_158_out, not_159_out, not_160_out, not_161_out,
       not_162_out, not_163_out, not_164_out, not_165_out, not_166_out, not_167_out, not_168_out,
       not_169_out, not_170_out, not_171_out, not_172_out, not_173_out, not_174_out, not_175_out,
       not_176_out, not_177_out, not_178_out, not_179_out, not_180_out, not_181_out, not_182_out,
       not_183_out, not_184_out, not_185_out, not_186_out, not_187_out, not_188_out, not_189_out,
       not_190_out, not_191_out, not_192_out, not_193_out, not_194_out, not_195_out, not_196_out,
       not_197_out, not_198_out, not_199_out, not_200_out, not_201_out, not_202_out, not_203_out,
       not_204_out, not_205_out, not_206_out, not_207_out, not_208_out, not_209_out, not_210_out,
       not_211_out, not_212_out, not_213_out, not_214_out, not_215_out, not_216_out, not_217_out,
       not_218_out, not_219_out, not_220_out, not_221_out, not_222_out, not_223_out, not_224_out,
       not_225_out, not_226_out, not_227_out, not_228_out, not_229_out, not_230_out, not_231_out,
       not_232_out, not_233_out, not_234_out, not_235_out, not_236_out, not_237_out, not_238_out,
       not_239_out, not_240_out, not_241_out, not_242_out, not_243_out, not_244_out, not_245_out,
       not_246_out, not_247_out, not_248_out, not_249_out, not_250_out, not_251_out, not_252_out,
       not_253_out, not_254_out, not_255_out, not_256_out, not_257_out, not_258_out, not_259_out,
       not_260_out, not_261_out, not_262_out, not_263_out, not_264_out, not_265_out, not_266_out,
       not_267_out, not_268_out, not_269_out, not_270_out, not_271_out, not_272_out, not_273_out,
       not_274_out, not_275_out, not_276_out, not_277_out, not_278_out, not_279_out, not_280_out,
       not_281_out, not_282_out, not_283_out, not_284_out, not_285_out, not_286_out, not_287_out,
       not_288_out, not_289_out, not_290_out, not_291_out, not_292_out, not_293_out, not_294_out,
       not_295_out, not_296_out, not_297_out, not_298_out, not_299_out, not_300_out, not_301_out,
       not_302_out, not_303_out, not_304_out, not_305_out, not_306_out, not_307_out, not_308_out,
       not_309_out, not_310_out, not_311_out, not_312_out, not_313_out, not_314_out, not_315_out,
       not_316_out, not_317_out, not_318_out, not_319_out, not_320_out, not_321_out, not_322_out,
       not_323_out, not_324_out, not_325_out, not_326_out, not_327_out, not_328_out, not_329_out,
       not_330_out, not_331_out, not_332_out, not_333_out, not_334_out, not_335_out, not_336_out,
       not_337_out, not_338_out, not_339_out, not_340_out, not_341_out, not_342_out, not_343_out,
       not_344_out, not_345_out, not_346_out, not_347_out, not_348_out, not_349_out, not_350_out,
       not_351_out, not_352_out, not_353_out, not_354_out, not_355_out, not_356_out, not_357_out,
       not_358_out, not_359_out, not_360_out, not_361_out, not_362_out, not_363_out, not_364_out,
       not_365_out, not_366_out, not_367_out, not_368_out, not_369_out, not_370_out, not_371_out,
       not_372_out, not_373_out, not_374_out, not_375_out, not_376_out, not_377_out, not_378_out,
       not_379_out, not_380_out, not_381_out, not_382_out, not_383_out, not_384_out, not_385_out,
       not_386_out, not_387_out, not_388_out, not_389_out, not_390_out, not_391_out, not_392_out,
       not_393_out, not_394_out, not_395_out, not_396_out, not_397_out, not_398_out, not_399_out,
       not_400_out, not_401_out, not_402_out, not_403_out, not_404_out, not_405_out, not_406_out,
       not_407_out, not_408_out, not_409_out, not_410_out, not_411_out, not_412_out, not_413_out, not_414_out;

  not not_1 (not_1_out, OP4);
  not not_2 (not_2_out, OP3);
  not not_3 (not_3_out, OP2);
  not not_4 (not_4_out, OP4);
  not not_5 (not_5_out, OP3);
  not not_6 (not_6_out, OP1);
  not not_7 (not_7_out, OP4);
  not not_8 (not_8_out, OP2);
  not not_9 (not_9_out, OP5);
  not not_10 (not_10_out, OP4);
  not not_11 (not_11_out, OP2);
  not not_12 (not_12_out, OP1);
  not not_13 (not_13_out, OP0);
  not not_14 (not_14_out, OP5);
  not not_15 (not_15_out, OP4);
  not not_16 (not_16_out, OP1);
  not not_17 (not_17_out, OP0);
  not not_18 (not_18_out, OP5);
  not not_19 (not_19_out, OP4);
  not not_20 (not_20_out, OP2);
  not not_21 (not_21_out, OP1);
  not not_22 (not_22_out, OP5);
  not not_23 (not_23_out, OP4);
  not not_24 (not_24_out, OP2);
  not not_25 (not_25_out, OP0);
  not not_26 (not_26_out, OP5);
  not not_27 (not_27_out, OP4);
  not not_28 (not_28_out, OP1);
  not not_29 (not_29_out, OP4);
  not not_30 (not_30_out, OP3);
  not not_31 (not_31_out, OP2);
  not not_32 (not_32_out, OP4);
  not not_33 (not_33_out, OP2);
  not not_34 (not_34_out, OP5);
  not not_35 (not_35_out, OP4);
  not not_36 (not_36_out, OP0);
  not not_37 (not_37_out, OP4);
  not not_38 (not_38_out, OP3);
  not not_39 (not_39_out, OP1);
  not not_40 (not_40_out, OP5);
  not not_41 (not_41_out, OP4);
  not not_42 (not_42_out, OP3);
  not not_43 (not_43_out, OP2);
  not not_44 (not_44_out, OP1);
  not not_45 (not_45_out, OP0);
  not not_46 (not_46_out, F5);
  not not_47 (not_47_out, F4);
  not not_48 (not_48_out, F3);
  not not_49 (not_49_out, F2);
  not not_50 (not_50_out, F1);
  not not_51 (not_51_out, F0);
  not not_52 (not_52_out, OP5);
  not not_53 (not_53_out, OP4);
  not not_54 (not_54_out, OP3);
  not not_55 (not_55_out, OP2);
  not not_56 (not_56_out, OP1);
  not not_57 (not_57_out, OP0);
  not not_58 (not_58_out, F5);
  not not_59 (not_59_out, F4);
  not not_60 (not_60_out, F3);
  not not_61 (not_61_out, F2);
  not not_62 (not_62_out, OP5);
  not not_63 (not_63_out, OP4);
  not not_64 (not_64_out, OP3);
  not not_65 (not_65_out, OP2);
  not not_66 (not_66_out, OP1);
  not not_67 (not_67_out, OP0);
  not not_68 (not_68_out, F5);
  not not_69 (not_69_out, F4);
  not not_70 (not_70_out, F3);
  not not_71 (not_71_out, F2);
  not not_72 (not_72_out, F0);
  not not_73 (not_73_out, OP5);
  not not_74 (not_74_out, OP4);
  not not_75 (not_75_out, OP3);
  not not_76 (not_76_out, OP2);
  not not_77 (not_77_out, OP1);
  not not_78 (not_78_out, OP0);
  not not_79 (not_79_out, F4);
  not not_80 (not_80_out, F3);
  not not_81 (not_81_out, F2);
  not not_82 (not_82_out, F1);
  not not_83 (not_83_out, F0);
  not not_84 (not_84_out, OP5);
  not not_85 (not_85_out, OP4);
  not not_86 (not_86_out, OP3);
  not not_87 (not_87_out, OP2);
  not not_88 (not_88_out, OP1);
  not not_89 (not_89_out, OP0);
  not not_90 (not_90_out, F4);
  not not_91 (not_91_out, F3);
  not not_92 (not_92_out, F2);
  not not_93 (not_93_out, F1);
  not not_94 (not_94_out, OP5);
  not not_95 (not_95_out, OP4);
  not not_96 (not_96_out, OP3);
  not not_97 (not_97_out, OP2);
  not not_98 (not_98_out, OP1);
  not not_99 (not_99_out, OP0);
  not not_100 (not_100_out, F4);
  not not_101 (not_101_out, F3);
  not not_102 (not_102_out, F2);
  not not_103 (not_103_out, F0);
  not not_104 (not_104_out, OP5);
  not not_105 (not_105_out, OP4);
  not not_106 (not_106_out, OP3);
  not not_107 (not_107_out, OP2);
  not not_108 (not_108_out, OP1);
  not not_109 (not_109_out, OP0);
  not not_110 (not_110_out, F4);
  not not_111 (not_111_out, F3);
  not not_112 (not_112_out, F1);
  not not_113 (not_113_out, F0);
  not not_114 (not_114_out, OP5);
  not not_115 (not_115_out, OP4);
  not not_116 (not_116_out, OP3);
  not not_117 (not_117_out, OP2);
  not not_118 (not_118_out, OP1);
  not not_119 (not_119_out, OP0);
  not not_120 (not_120_out, F4);
  not not_121 (not_121_out, F3);
  not not_122 (not_122_out, F1);
  not not_123 (not_123_out, OP5);
  not not_124 (not_124_out, OP4);
  not not_125 (not_125_out, OP3);
  not not_126 (not_126_out, OP2);
  not not_127 (not_127_out, OP1);
  not not_128 (not_128_out, OP0);
  not not_129 (not_129_out, F4);
  not not_130 (not_130_out, F3);
  not not_131 (not_131_out, OP5);
  not not_132 (not_132_out, OP4);
  not not_133 (not_133_out, OP3);
  not not_134 (not_134_out, OP2);
  not not_135 (not_135_out, OP1);
  not not_136 (not_136_out, OP0);
  not not_137 (not_137_out, F4);
  not not_138 (not_138_out, F2);
  not not_139 (not_139_out, F0);
  not not_140 (not_140_out, OP5);
  not not_141 (not_141_out, OP4);
  not not_142 (not_142_out, OP3);
  not not_143 (not_143_out, OP2);
  not not_144 (not_144_out, OP1);
  not not_145 (not_145_out, OP0);
  not not_146 (not_146_out, F4);
  not not_147 (not_147_out, F2);
  not not_148 (not_148_out, OP5);
  not not_149 (not_149_out, OP4);
  not not_150 (not_150_out, OP3);
  not not_151 (not_151_out, OP2);
  not not_152 (not_152_out, OP5);
  not not_153 (not_153_out, OP4);
  not not_154 (not_154_out, OP2);
  not not_155 (not_155_out, OP1);
  not not_156 (not_156_out, OP0);
  not not_157 (not_157_out, OP5);
  not not_158 (not_158_out, OP4);
  not not_159 (not_159_out, OP1);
  not not_160 (not_160_out, OP0);
  not not_161 (not_161_out, OP5);
  not not_162 (not_162_out, OP4);
  not not_163 (not_163_out, OP2);
  not not_164 (not_164_out, OP1);
  not not_165 (not_165_out, OP5);
  not not_166 (not_166_out, OP4);
  not not_167 (not_167_out, OP2);
  not not_168 (not_168_out, OP0);
  not not_169 (not_169_out, OP5);
  not not_170 (not_170_out, OP4);
  not not_171 (not_171_out, OP1);
  not not_172 (not_172_out, OP4);
  not not_173 (not_173_out, OP3);
  not not_174 (not_174_out, OP2);
  not not_175 (not_175_out, OP5);
  not not_176 (not_176_out, OP4);
  not not_177 (not_177_out, OP3);
  not not_178 (not_178_out, OP2);
  not not_179 (not_179_out, OP1);
  not not_180 (not_180_out, OP0);
  not not_181 (not_181_out, F5);
  not not_182 (not_182_out, F4);
  not not_183 (not_183_out, F3);
  not not_184 (not_184_out, F1);
  not not_185 (not_185_out, F0);
  not not_186 (not_186_out, OP5);
  not not_187 (not_187_out, OP4);
  not not_188 (not_188_out, OP0);
  not not_189 (not_189_out, OP4);
  not not_190 (not_190_out, OP3);
  not not_191 (not_191_out, OP1);
  not not_192 (not_192_out, OP5);
  not not_193 (not_193_out, OP4);
  not not_194 (not_194_out, OP3);
  not not_195 (not_195_out, OP2);
  not not_196 (not_196_out, OP1);
  not not_197 (not_197_out, OP0);
  not not_198 (not_198_out, F5);
  not not_199 (not_199_out, F4);
  not not_200 (not_200_out, F1);
  not not_201 (not_201_out, F0);
  not not_202 (not_202_out, OP5);
  not not_203 (not_203_out, OP4);
  not not_204 (not_204_out, OP3);
  not not_205 (not_205_out, OP1);
  not not_206 (not_206_out, OP0);
  not not_207 (not_207_out, OP5);
  not not_208 (not_208_out, OP4);
  not not_209 (not_209_out, OP3);
  not not_210 (not_210_out, OP1);
  not not_211 (not_211_out, OP5);
  not not_212 (not_212_out, OP4);
  not not_213 (not_213_out, OP2);
  not not_214 (not_214_out, OP1);
  not not_215 (not_215_out, OP0);
  not not_216 (not_216_out, OP5);
  not not_217 (not_217_out, OP4);
  not not_218 (not_218_out, OP2);
  not not_219 (not_219_out, OP1);
  not not_220 (not_220_out, OP5);
  not not_221 (not_221_out, OP4);
  not not_222 (not_222_out, OP2);
  not not_223 (not_223_out, OP0);
  not not_224 (not_224_out, OP4);
  not not_225 (not_225_out, OP3);
  not not_226 (not_226_out, OP2);
  not not_227 (not_227_out, OP4);
  not not_228 (not_228_out, OP2);
  not not_229 (not_229_out, OP4);
  not not_230 (not_230_out, OP3);
  not not_231 (not_231_out, OP1);
  not not_232 (not_232_out, OP5);
  not not_233 (not_233_out, OP4);
  not not_234 (not_234_out, OP3);
  not not_235 (not_235_out, OP2);
  not not_236 (not_236_out, OP1);
  not not_237 (not_237_out, OP5);
  not not_238 (not_238_out, OP4);
  not not_239 (not_239_out, OP3);
  not not_240 (not_240_out, OP2);
  not not_241 (not_241_out, OP1);
  not not_242 (not_242_out, OP0);
  not not_243 (not_243_out, F5);
  not not_244 (not_244_out, F4);
  not not_245 (not_245_out, F3);
  not not_246 (not_246_out, F2);
  not not_247 (not_247_out, F1);
  not not_248 (not_248_out, F0);
  not not_249 (not_249_out, OP5);
  not not_250 (not_250_out, OP4);
  not not_251 (not_251_out, OP3);
  not not_252 (not_252_out, OP2);
  not not_253 (not_253_out, OP1);
  not not_254 (not_254_out, OP0);
  not not_255 (not_255_out, F5);
  not not_256 (not_256_out, F4);
  not not_257 (not_257_out, F3);
  not not_258 (not_258_out, F2);
  not not_259 (not_259_out, OP5);
  not not_260 (not_260_out, OP4);
  not not_261 (not_261_out, OP3);
  not not_262 (not_262_out, OP2);
  not not_263 (not_263_out, OP1);
  not not_264 (not_264_out, OP0);
  not not_265 (not_265_out, F5);
  not not_266 (not_266_out, F4);
  not not_267 (not_267_out, F3);
  not not_268 (not_268_out, F2);
  not not_269 (not_269_out, F0);
  not not_270 (not_270_out, OP5);
  not not_271 (not_271_out, OP4);
  not not_272 (not_272_out, OP3);
  not not_273 (not_273_out, OP2);
  not not_274 (not_274_out, OP1);
  not not_275 (not_275_out, OP0);
  not not_276 (not_276_out, F4);
  not not_277 (not_277_out, F3);
  not not_278 (not_278_out, F2);
  not not_279 (not_279_out, F1);
  not not_280 (not_280_out, F0);
  not not_281 (not_281_out, OP5);
  not not_282 (not_282_out, OP4);
  not not_283 (not_283_out, OP3);
  not not_284 (not_284_out, OP2);
  not not_285 (not_285_out, OP1);
  not not_286 (not_286_out, OP0);
  not not_287 (not_287_out, F4);
  not not_288 (not_288_out, F3);
  not not_289 (not_289_out, F2);
  not not_290 (not_290_out, F1);
  not not_291 (not_291_out, OP5);
  not not_292 (not_292_out, OP4);
  not not_293 (not_293_out, OP3);
  not not_294 (not_294_out, OP2);
  not not_295 (not_295_out, OP1);
  not not_296 (not_296_out, OP0);
  not not_297 (not_297_out, F4);
  not not_298 (not_298_out, F3);
  not not_299 (not_299_out, F2);
  not not_300 (not_300_out, F0);
  not not_301 (not_301_out, OP5);
  not not_302 (not_302_out, OP4);
  not not_303 (not_303_out, OP3);
  not not_304 (not_304_out, OP2);
  not not_305 (not_305_out, OP1);
  not not_306 (not_306_out, OP0);
  not not_307 (not_307_out, F4);
  not not_308 (not_308_out, F3);
  not not_309 (not_309_out, F1);
  not not_310 (not_310_out, F0);
  not not_311 (not_311_out, OP5);
  not not_312 (not_312_out, OP4);
  not not_313 (not_313_out, OP3);
  not not_314 (not_314_out, OP2);
  not not_315 (not_315_out, OP1);
  not not_316 (not_316_out, OP0);
  not not_317 (not_317_out, F4);
  not not_318 (not_318_out, F3);
  not not_319 (not_319_out, F1);
  not not_320 (not_320_out, OP5);
  not not_321 (not_321_out, OP4);
  not not_322 (not_322_out, OP3);
  not not_323 (not_323_out, OP2);
  not not_324 (not_324_out, OP1);
  not not_325 (not_325_out, OP0);
  not not_326 (not_326_out, F4);
  not not_327 (not_327_out, F3);
  not not_328 (not_328_out, OP5);
  not not_329 (not_329_out, OP4);
  not not_330 (not_330_out, OP3);
  not not_331 (not_331_out, OP2);
  not not_332 (not_332_out, OP1);
  not not_333 (not_333_out, OP0);
  not not_334 (not_334_out, F4);
  not not_335 (not_335_out, F2);
  not not_336 (not_336_out, F0);
  not not_337 (not_337_out, OP5);
  not not_338 (not_338_out, OP4);
  not not_339 (not_339_out, OP3);
  not not_340 (not_340_out, OP2);
  not not_341 (not_341_out, OP1);
  not not_342 (not_342_out, OP0);
  not not_343 (not_343_out, F4);
  not not_344 (not_344_out, F2);
  not not_345 (not_345_out, OP5);
  not not_346 (not_346_out, OP4);
  not not_347 (not_347_out, OP3);
  not not_348 (not_348_out, OP2);
  not not_349 (not_349_out, OP1);
  not not_350 (not_350_out, OP0);
  not not_351 (not_351_out, F5);
  not not_352 (not_352_out, F4);
  not not_353 (not_353_out, F2);
  not not_354 (not_354_out, F1);
  not not_355 (not_355_out, F0);
  not not_356 (not_356_out, OP5);
  not not_357 (not_357_out, OP4);
  not not_358 (not_358_out, OP3);
  not not_359 (not_359_out, OP2);
  not not_360 (not_360_out, OP1);
  not not_361 (not_361_out, OP0);
  not not_362 (not_362_out, F5);
  not not_363 (not_363_out, F4);
  not not_364 (not_364_out, F1);
  not not_365 (not_365_out, F0);
  not not_366 (not_366_out, OP5);
  not not_367 (not_367_out, OP4);
  not not_368 (not_368_out, OP3);
  not not_369 (not_369_out, OP2);
  not not_370 (not_370_out, OP1);
  not not_371 (not_371_out, OP0);
  not not_372 (not_372_out, F5);
  not not_373 (not_373_out, F4);
  not not_374 (not_374_out, F3);
  not not_375 (not_375_out, F1);
  not not_376 (not_376_out, F0);
  not not_377 (not_377_out, OP5);
  not not_378 (not_378_out, OP4);
  not not_379 (not_379_out, OP3);
  not not_380 (not_380_out, OP1);
  not not_381 (not_381_out, OP0);
  not not_382 (not_382_out, OP5);
  not not_383 (not_383_out, OP4);
  not not_384 (not_384_out, OP3);
  not not_385 (not_385_out, OP1);
  not not_386 (not_386_out, OP5);
  not not_387 (not_387_out, OP4);
  not not_388 (not_388_out, OP3);
  not not_389 (not_389_out, OP2);
  not not_390 (not_390_out, OP1);
  not not_391 (not_391_out, OP0);
  not not_392 (not_392_out, F5);
  not not_393 (not_393_out, F4);
  not not_394 (not_394_out, F2);
  not not_395 (not_395_out, F1);
  not not_396 (not_396_out, F0);
  not not_397 (not_397_out, OP0);
  not not_398 (not_398_out, OP2);
  not not_399 (not_399_out, OP3);
  not not_400 (not_400_out, OP4);
  not not_401 (not_401_out, OP5);
  not not_402 (not_402_out, F0);
  not not_403 (not_403_out, F1);
  not not_404 (not_404_out, F2);
  not not_405 (not_405_out, F4);
  not not_406 (not_406_out, F5);
  not not_407 (not_407_out, OP2);
  not not_408 (not_408_out, OP3);
  not not_409 (not_409_out, OP4);
  not not_410 (not_410_out, OP5);
  not not_411 (not_411_out, OP2);
  not not_412 (not_412_out, OP3);
  not not_413 (not_413_out, OP4);
  not not_414 (not_414_out, OP5);
  and and_1 (and_1_out, OP5, not_1_out, not_2_out, not_3_out, OP1, OP0);
  and and_2 (and_2_out, OP5, not_4_out, not_5_out, OP2, not_6_out, OP0);
  and and_3 (MemWrite, OP5, not_7_out, OP3, not_8_out, OP1, OP0);
  and and_4 (and_4_out, not_9_out, not_10_out, OP3, not_11_out, not_12_out, not_13_out);
  and and_5 (and_5_out, not_14_out, not_15_out, OP3, OP2, not_16_out, not_17_out);
  and and_6 (and_6_out, not_18_out, not_19_out, OP3, not_20_out, not_21_out, OP0);
  and and_7 (and_7_out, not_22_out, not_23_out, OP3, not_24_out, OP1, not_25_out);
  and and_8 (and_8_out, not_26_out, not_27_out, OP3, OP2, not_28_out, OP0);
  and and_9 (and_9_out, OP5, not_29_out, not_30_out, not_31_out, OP1, OP0);
  and and_10 (and_10_out, OP5, not_32_out, OP3, not_33_out, OP1, OP0);
  and and_11 (and_11_out, not_34_out, not_35_out, OP3, OP2, OP1, not_36_out);
  and and_12 (and_12_out, OP5, not_37_out, not_38_out, OP2, not_39_out, OP0);
  and and_13 (and_13_out, not_40_out, not_41_out, not_42_out, not_43_out, not_44_out, not_45_out, not_46_out, not_47_out, not_48_out, not_49_out, not_50_out, not_51_out);
  and and_14 (and_14_out, not_52_out, not_53_out, not_54_out, not_55_out, not_56_out, not_57_out, not_58_out, not_59_out, not_60_out, not_61_out, F1, F0);
  and and_15 (and_15_out, not_62_out, not_63_out, not_64_out, not_65_out, not_66_out, not_67_out, not_68_out, not_69_out, not_70_out, not_71_out, F1, not_72_out);
  and and_16 (and_16_out, not_73_out, not_74_out, not_75_out, not_76_out, not_77_out, not_78_out, F5, not_79_out, not_80_out, not_81_out, not_82_out, not_83_out);
  and and_17 (and_17_out, not_84_out, not_85_out, not_86_out, not_87_out, not_88_out, not_89_out, F5, not_90_out, not_91_out, not_92_out, not_93_out, F0);
  and and_18 (and_18_out, not_94_out, not_95_out, not_96_out, not_97_out, not_98_out, not_99_out, F5, not_100_out, not_101_out, not_102_out, F1, not_103_out);
  and and_19 (and_19_out, not_104_out, not_105_out, not_106_out, not_107_out, not_108_out, not_109_out, F5, not_110_out, not_111_out, F2, not_112_out, not_113_out);
  and and_20 (and_20_out, not_114_out, not_115_out, not_116_out, not_117_out, not_118_out, not_119_out, F5, not_120_out, not_121_out, F2, not_122_out, F0);
  and and_21 (and_21_out, not_123_out, not_124_out, not_125_out, not_126_out, not_127_out, not_128_out, F5, not_129_out, not_130_out, F2, F1, F0);
  and and_22 (and_22_out, not_131_out, not_132_out, not_133_out, not_134_out, not_135_out, not_136_out, F5, not_137_out, F3, not_138_out, F1, not_139_out);
  and and_23 (and_23_out, not_140_out, not_141_out, not_142_out, not_143_out, not_144_out, not_145_out, F5, not_146_out, F3, not_147_out, F1, F0);
  and and_24 (and_24_out, not_148_out, not_149_out, not_150_out, not_151_out, OP1, OP0);
  and and_25 (and_25_out, not_152_out, not_153_out, OP3, not_154_out, not_155_out, not_156_out);
  and and_26 (and_26_out, not_157_out, not_158_out, OP3, OP2, not_159_out, not_160_out);
  and and_27 (and_27_out, not_161_out, not_162_out, OP3, not_163_out, not_164_out, OP0);
  and and_28 (and_28_out, not_165_out, not_166_out, OP3, not_167_out, OP1, not_168_out);
  and and_29 (and_29_out, not_169_out, not_170_out, OP3, OP2, not_171_out, OP0);
  and and_30 (and_30_out, OP5, not_172_out, not_173_out, not_174_out, OP1, OP0);
  and and_31 (and_31_out, not_175_out, not_176_out, not_177_out, not_178_out, not_179_out, not_180_out, not_181_out, not_182_out, not_183_out, F2, not_184_out, not_185_out);
  and and_32 (and_32_out, not_186_out, not_187_out, OP3, OP2, OP1, not_188_out);
  and and_33 (and_33_out, OP5, not_189_out, not_190_out, OP2, not_191_out, OP0);
  and and_34 (SysCALL, not_192_out, not_193_out, not_194_out, not_195_out, not_196_out, not_197_out, not_198_out, not_199_out, F3, F2, not_200_out, not_201_out);
  and and_35 (and_35_out, not_202_out, not_203_out, not_204_out, OP2, not_205_out, not_206_out);
  and and_36 (and_36_out, not_207_out, not_208_out, not_209_out, OP2, not_210_out, OP0);
  and and_37 (and_37_out, not_211_out, not_212_out, OP3, not_213_out, not_214_out, not_215_out);
  and and_38 (and_38_out, not_216_out, not_217_out, OP3, not_218_out, not_219_out, OP0);
  and and_39 (and_39_out, not_220_out, not_221_out, OP3, not_222_out, OP1, not_223_out);
  and and_40 (and_40_out, OP5, not_224_out, not_225_out, not_226_out, OP1, OP0);
  and and_41 (and_41_out, OP5, not_227_out, OP3, not_228_out, OP1, OP0);
  and and_42 (and_42_out, OP5, not_229_out, not_230_out, OP2, not_231_out, OP0);
  and and_43 (and_43_out, not_232_out, not_233_out, not_234_out, not_235_out, not_236_out, OP0);
  and and_44 (and_44_out, not_237_out, not_238_out, not_239_out, not_240_out, not_241_out, not_242_out, not_243_out, not_244_out, not_245_out, not_246_out, not_247_out, not_248_out);
  and and_45 (and_45_out, not_249_out, not_250_out, not_251_out, not_252_out, not_253_out, not_254_out, not_255_out, not_256_out, not_257_out, not_258_out, F1, F0);
  and and_46 (and_46_out, not_259_out, not_260_out, not_261_out, not_262_out, not_263_out, not_264_out, not_265_out, not_266_out, not_267_out, not_268_out, F1, not_269_out);
  and and_47 (and_47_out, not_270_out, not_271_out, not_272_out, not_273_out, not_274_out, not_275_out, F5, not_276_out, not_277_out, not_278_out, not_279_out, not_280_out);
  and and_48 (and_48_out, not_281_out, not_282_out, not_283_out, not_284_out, not_285_out, not_286_out, F5, not_287_out, not_288_out, not_289_out, not_290_out, F0);
  and and_49 (and_49_out, not_291_out, not_292_out, not_293_out, not_294_out, not_295_out, not_296_out, F5, not_297_out, not_298_out, not_299_out, F1, not_300_out);
  and and_50 (and_50_out, not_301_out, not_302_out, not_303_out, not_304_out, not_305_out, not_306_out, F5, not_307_out, not_308_out, F2, not_309_out, not_310_out);
  and and_51 (and_51_out, not_311_out, not_312_out, not_313_out, not_314_out, not_315_out, not_316_out, F5, not_317_out, not_318_out, F2, not_319_out, F0);
  and and_52 (and_52_out, not_320_out, not_321_out, not_322_out, not_323_out, not_324_out, not_325_out, F5, not_326_out, not_327_out, F2, F1, F0);
  and and_53 (and_53_out, not_328_out, not_329_out, not_330_out, not_331_out, not_332_out, not_333_out, F5, not_334_out, F3, not_335_out, F1, not_336_out);
  and and_54 (and_54_out, not_337_out, not_338_out, not_339_out, not_340_out, not_341_out, not_342_out, F5, not_343_out, F3, not_344_out, F1, F0);
  and and_55 (and_55_out, not_345_out, not_346_out, not_347_out, not_348_out, not_349_out, not_350_out, not_351_out, not_352_out, F3, not_353_out, not_354_out, not_355_out);
  and and_56 (and_56_out, not_356_out, not_357_out, not_358_out, not_359_out, not_360_out, not_361_out, not_362_out, not_363_out, F3, F2, not_364_out, not_365_out);
  and and_57 (and_57_out, not_366_out, not_367_out, not_368_out, not_369_out, not_370_out, not_371_out, not_372_out, not_373_out, not_374_out, F2, not_375_out, not_376_out);
  and and_58 (BEQ, not_377_out, not_378_out, not_379_out, OP2, not_380_out, not_381_out);
  and and_59 (BNE, not_382_out, not_383_out, not_384_out, OP2, not_385_out, OP0);
  and and_60 (JR, not_386_out, not_387_out, not_388_out, not_389_out, not_390_out, not_391_out, not_392_out, not_393_out, F3, not_394_out, not_395_out, not_396_out);
  and and_61 (and_61_out, not_397_out, not_398_out, not_399_out, not_400_out, not_401_out, not_402_out, not_403_out, not_404_out, F3, not_405_out, not_406_out);
  and and_62 (and_62_out, OP1, not_407_out, not_408_out, not_409_out, not_410_out);
  and and_63 (JAL, OP0, OP1, not_411_out, not_412_out, not_413_out, not_414_out);
  or or_1 (MemToReg, and_1_out, and_2_out);
  or or_2 (ALU_SRC, and_4_out, and_5_out, and_6_out, and_7_out, and_8_out, and_9_out, and_10_out, and_11_out, and_12_out);
  or or_3 (SignedExt, and_35_out, and_36_out, and_37_out, and_38_out, and_39_out, and_40_out, and_41_out, and_42_out, and_43_out);
  or or_4 (JUMP, and_61_out, and_62_out);
  or or_5 (RegWrite, and_13_out, and_14_out, and_15_out, and_16_out, and_17_out, and_18_out, and_19_out, and_20_out, and_21_out, and_22_out, and_23_out, and_24_out, and_25_out, and_26_out, and_27_out, and_28_out, and_29_out, and_30_out, and_31_out, and_32_out, and_33_out);
  or or_6 (RegDst, and_44_out, and_45_out, and_46_out, and_47_out, and_48_out, and_49_out, and_50_out, and_51_out, and_52_out, and_53_out, and_54_out, and_55_out, and_56_out, and_57_out);
endmodule

// ALU
module MIPS_ALU (
  input  [4:0] shamt,
  input  [31:0] X,
  input  [31:0] Y,
  input  [3:0] AluOP,
  output Equal,
  output [31:0] Result,
  output [31:0] Result_2
);

  wire [0:0] comparator_1_lt, comparator_2_lt;
  wire [31:0] adder_1_out, AND_out, divider_1_out, divider_1_rem, multiplier_1_cout, multiplier_1_out,
       NOR_out, OR_out, shifter_1_out, shifter_2_out, shifter_3_out, subtractor_1_out, XOR_out;

  assign AND_out = X & Y;  // AND_Gate AND, 32 bits wide
  assign OR_out = X | Y;  // OR_Gate OR, 32 bits wide
  Shifter #(.width(32), .shift("ll")) shifter_1 (.in(Y), .\dist (shamt), .out(shifter_1_out));
  Shifter #(.width(32), .shift("ar")) shifter_2 (.in(Y), .\dist (shamt), .out(shifter_2_out));
  Shifter #(.width(32), .shift("lr")) shifter_3 (.in(Y), .\dist (shamt), .out(shifter_3_out));
  Multiplier #(.width(32)) multiplier_1 (.a(X), .b(Y), .out(multiplier_1_out), .cout(multiplier_1_cout));  // open: cin
  Divider #(.width(32)) divider_1 (.a(X), .b(Y), .out(divider_1_out), .rem(divider_1_rem));  // open: upper
  Adder #(.width(32)) adder_1 (.a(X), .b(Y), .out(adder_1_out));  // open: cin, cout
  Subtractor #(.width(32)) subtractor_1 (.a(X), .b(Y), .out(subtractor_1_out));  // open: bin, bout
  assign XOR_out = X ^ Y;  // XOR_Gate XOR, 32 bits wide
  assign NOR_out = ~(X | Y);  // NOR_Gate NOR, 32 bits wide
  Comparator #(.width(32), .mode("twosComplement")) comparator_1 (
    .a(X), .b(Y), .eq(Equal), .lt(comparator_1_lt[0]));  // open: gt
  Comparator #(.width(32), .mode("unsigned")) comparator_2 (.a(X), .b(Y), .lt(comparator_2_lt[0]));  // open: gt, eq
  Multiplexer #(.select(4), .width(32), .disabled("Z"), .enable("false")) multiplexer_1 (
    .in0(shifter_1_out), .in1(shifter_2_out), .in2(shifter_3_out), .in3(multiplier_1_out),
    .in4(divider_1_out), .in5(adder_1_out), .in6(subtractor_1_out), .in7(AND_out), .in8(OR_out),
    .in9(XOR_out), .in10(NOR_out), .in11({{31{1'b0}}, comparator_1_lt[0]}),
    .in12({{31{1'b0}}, comparator_2_lt[0]}), .in13({32{1'b0}}), .in14({32{1'b0}}), .in15({32{1'b0}}),
    .out(Result), .sel(AluOP));
  Multiplexer #(.select(4), .width(32), .disabled("Z"), .enable("false")) multiplexer_2 (
    .in0({32{1'b0}}), .in1({32{1'b0}}), .in2({32{1'b0}}), .in3(multiplier_1_cout), .in4(divider_1_rem),
    .in5({32{1'b0}}), .in6({32{1'b0}}), .in7({32{1'b0}}), .in8({32{1'b0}}), .in9({32{1'b0}}),
    .in10({32{1'b0}}), .in11({32{1'b0}}), .in12({32{1'b0}}), .in13({32{1'b0}}), .in14({32{1'b0}}),
    .in15({32{1'b0}}), .out(Result_2), .sel(AluOP));

  // Other names for the same wires on the sheet: Result2[31:0] = Result_2; S[3:0] = AluOP

  // Notes on the sheet:
  //   不要改变此引脚区域内容，也不要改变ALU封装形式
  //   输入引脚
  //   输出引脚
endmodule

module MIPS_Regifile (
  input  [31:0] Din,
  input  Clk,
  input  WE,
  input  [4:0] R1_num,
  input  [4:0] W_num,
  input  [4:0] R2_num,
  output [31:0] R1,
  output [31:0] R2
);

  // RegisterFile registerfile_1: pin names not known; wires that end beside it: Din, Clk, WE, W_num, R1_num, R2_num, R1, R2
endmodule

module \理想流水线  (
);

  wire and_1_out, and_2_out, and_3_out, and_4_out, CLK, comparator_1_eq, ex_mem_1_out_19, ex_mem_1_out_20,
       ex_mem_1_out_21, ex_mem_1_out_22, ex_mem_1_out_23, \ex_mem_1_传输状态out_表明当前传输数据有效 , Go, id_ex_1_out_31,
       id_ex_1_out_32, id_ex_1_out_33, id_ex_1_out_34, id_ex_1_out_35, id_ex_1_out_36, id_ex_1_out_37,
       id_ex_1_out_38, id_ex_1_out_39, id_ex_1_out_40, \id_ex_1_传输状态out_表明当前传输数据有效 ,
       \if_id_1_传输状态out_表明当前传输数据有效 , IR1, IR2, IR3, mem_wb_1_out_18, mem_wb_1_out_19, mem_wb_1_out_20,
       mem_wb_1_out_21, \mem_wb_1_传输状态out_表明当前传输数据有效 , mips_alu_1_equal, nand_1_out, not_1_out, or_1_out,
       or_2_out, or_3_out, or_4_out, RST, SignedExt, syscall, W1, W2, W3, \单周期硬布线控制器_1_alu_src ,
       \单周期硬布线控制器_1_beq , \单周期硬布线控制器_1_bne , \单周期硬布线控制器_1_jal , \单周期硬布线控制器_1_jmp , \单周期硬布线控制器_1_jr ,
       \单周期硬布线控制器_1_memtoreg , \单周期硬布线控制器_1_memwrite , \单周期硬布线控制器_1_regdst , \单周期硬布线控制器_1_regwrite ;
  wire [3:0] id_ex_1_out_41, \单周期硬布线控制器_1_alu_op ;
  wire [4:0] id_ex_1_out_26_2, multiplexer_4_out, multiplexer_5_out, multiplexer_6_out, multiplexer_8_out;
  wire [15:0] \LoadUse次数 , \总周期数 , \插入气泡数 , \无条件分支数 , \条件分支成功数 ;
  wire [26:0] id_ex_1_out_26;
  wire [31:0] adder_1_out, adder_2_out, adder_3_out, adder_4_out, bit_extender_1_out, bit_extender_2_out,
       ex_mem_1_out_14, ex_mem_1_out_17, ex_mem_1_out_18, EX_PC, id_ex_1_out_24, id_ex_1_out_28,
       id_ex_1_out_29, id_ex_1_out_30, ID_PC, if_id_1_out_6, IF_PC, IR, LedData, MEM_PC, mem_wb_1_out_13,
       mem_wb_1_out_16, mem_wb_1_out_17, mips_alu_1_result, mips_regifile_1_r1, mips_regifile_1_r2,
       multiplexer_1_out, multiplexer_2_out, multiplexer_3_out, multiplexer_7_out, multiplexer_9_out,
       multiplexer_10_out, multiplexer_11_out, ram_1_data, shifter_1_out, WB_PC;

  Clock #(.highDuration(1), .lowDuration(1)) clock_1 (.out(CLK));
  Button _1 (.out(IR1));
  Button _2 (.out(IR2));
  Button _3 (.out(IR3));
  Button \u_总复位  (.out(RST));
  Register #(.width(32), .trigger("rising"), .Select("low")) PC (
    .D(multiplexer_1_out), .en(nand_1_out), .Q(IF_PC), .clk(CLK), .clr(RST));
  Multiplexer #(.select(1), .width(32), .disabled("Z"), .enable("false")) multiplexer_1 (
    .in0(multiplexer_2_out), .in1(id_ex_1_out_28), .out(multiplexer_1_out), .sel(id_ex_1_out_32));
  Button \u_继续运行  (.out(Go));
  LED #(.active("true")) led_1 (.in(W1));
  LED #(.active("true")) led_2 (.in(W2));
  LED #(.active("true")) led_3 (.in(W3));
  Multiplexer #(.select(1), .width(32), .disabled("Z"), .enable("false")) multiplexer_2 (
    .in0(multiplexer_3_out),
    .in1({adder_2_out[31:28], id_ex_1_out_26[20:6], id_ex_1_out_26_2, id_ex_1_out_26[5:0], 2'b00}),
    .out(multiplexer_2_out), .sel(or_1_out));
  or or_1 (or_1_out, id_ex_1_out_31, id_ex_1_out_33);
  Hex_Digit_Display hex_digit_display_1 (.value(LedData[31:28]));  // open: dp
  ROM #(.addrWidth(10), .dataWidth(32), .Select("high")) rom_1 (.addr(IF_PC[11:2]), .data(IR));
  Adder #(.width(32)) adder_1 (.a(IF_PC), .b(32'h4), .out(adder_1_out));  // open: cin, cout
  Multiplexer #(.select(1), .width(32), .disabled("Z"), .enable("false")) multiplexer_3 (
    .in0(adder_1_out), .in1(adder_3_out), .out(multiplexer_3_out), .sel(or_4_out));
  Hex_Digit_Display hex_digit_display_2 (.value(LedData[23:20]));  // open: dp
  Hex_Digit_Display hex_digit_display_3 (.value(LedData[27:24]));  // open: dp
  Hex_Digit_Display hex_digit_display_4 (.value(LedData[15:12]));  // open: dp
  Hex_Digit_Display hex_digit_display_5 (.value(LedData[19:16]));  // open: dp
  IF_ID if_id_1 (
    .CLK(CLK), .out_6(if_id_1_out_6), .\传输状态Out_表明当前传输数据有效 (\if_id_1_传输状态out_表明当前传输数据有效 ),
    .\使能端_低电平有效_stall_高电平有效 (nand_1_out), .in_5(IF_PC), .out_8(ID_PC), .in_1(IR));  // open: 同步清零_气泡_高电平有效
  Hex_Digit_Display hex_digit_display_6 (.value(LedData[11:8]));  // open: dp
  Hex_Digit_Display hex_digit_display_7 (.value(LedData[7:4]));  // open: dp
  Clock #(.highDuration(1), .lowDuration(1)) clock_2 (.out(CLK));
  assign bit_extender_1_out = {{16{if_id_1_out_6[15]}}, if_id_1_out_6[15:0]};  // Bit_Extender bit_extender_1
  assign bit_extender_2_out = {{16{1'b0}}, if_id_1_out_6[15:0]};  // Bit_Extender bit_extender_2
  Hex_Digit_Display hex_digit_display_8 (.value(LedData[3:0]));  // open: dp
  Multiplexer #(.select(1), .width(5), .disabled("Z"), .enable("false")) multiplexer_4 (
    .in0(if_id_1_out_6[25:21]), .in1(5'b00100), .out(multiplexer_4_out), .sel(syscall));
  Multiplexer #(.select(1), .width(5), .disabled("Z"), .enable("false")) multiplexer_5 (
    .in0(if_id_1_out_6[20:16]), .in1(5'b00010), .out(multiplexer_5_out), .sel(syscall));
  Multiplexer #(.select(1), .width(5), .disabled("Z"), .enable("false")) multiplexer_6 (
    .in0(mem_wb_1_out_13[20:16]), .in1(mem_wb_1_out_13[15:11]), .out(multiplexer_6_out), .sel(mem_wb_1_out_20));
  Shifter #(.width(32), .shift("ll")) shifter_1 (.in(bit_extender_1_out), .\dist (5'b00010), .out(shifter_1_out));
  Multiplexer #(.select(1), .width(32), .disabled("Z"), .enable("false")) multiplexer_7 (
    .in0(bit_extender_2_out), .in1(bit_extender_1_out), .out(multiplexer_7_out), .sel(SignedExt));
  Multiplexer #(.select(1), .width(5), .disabled("Z"), .enable("false")) multiplexer_8 (
    .in0(multiplexer_6_out), .in1({5{1'b1}}), .out(multiplexer_8_out), .sel(mem_wb_1_out_21));
  or or_2 (or_2_out, nand_1_out, \mem_wb_1_传输状态out_表明当前传输数据有效 );
  // Probe on \总周期数 
  // Probe on \无条件分支数 
  // Probe on \条件分支成功数 
  // Probe on \插入气泡数 
  // Probe on \LoadUse次数 
  \单周期硬布线控制器  \u_单周期硬布线控制器_1  (
    .Func(if_id_1_out_6[5:0]), .OP(if_id_1_out_6[31:26]), .ALU_OP(\单周期硬布线控制器_1_alu_op ),
    .MemToReg(\单周期硬布线控制器_1_memtoreg ), .MemWrite(\单周期硬布线控制器_1_memwrite ), .ALU_SRC(\单周期硬布线控制器_1_alu_src ),
    .RegWrite(\单周期硬布线控制器_1_regwrite ), .SysCALL(syscall), .SignedExt(SignedExt),
    .RegDst(\单周期硬布线控制器_1_regdst ), .JR(\单周期硬布线控制器_1_jr ), .JMP(\单周期硬布线控制器_1_jmp ), .Beq(\单周期硬布线控制器_1_beq ),
    .JAL(\单周期硬布线控制器_1_jal ), .Bne(\单周期硬布线控制器_1_bne ));
  Comparator #(.width(32), .mode("twosComplement")) comparator_1 (
    .a(id_ex_1_out_29), .b(32'h22), .eq(comparator_1_eq));  // open: gt, lt
  Counter #(.width(16), .max('hffff), .ongoal("wrap"), .trigger("rising"), .behavior("old")) counter_1 (
    .count(or_2_out), .Q(\总周期数 ), .clk(CLK), .clr(RST));  // open: load, D, carry, preset
  // Probe on IF_PC[11:0]
  MIPS_Regifile mips_regifile_1 (
    .Din(multiplexer_11_out), .Clk(CLK), .R1(mips_regifile_1_r1), .R2(mips_regifile_1_r2),
    .WE(mem_wb_1_out_18), .W_num(multiplexer_8_out), .R1_num(multiplexer_4_out), .R2_num(multiplexer_5_out));
  and and_1 (and_1_out, comparator_1_eq, syscall);
  and and_2 (and_2_out, syscall, ~comparator_1_eq);  // AND_Gate
  // Probe on ID_PC[11:0]
  // Probe on EX_PC[11:0]
  Register #(.width(32), .trigger("rising"), .Select("low")) register_1 (
    .D(id_ex_1_out_28), .en(and_1_out), .Q(LedData), .clk(CLK), .clr(RST));
  nand nand_1 (nand_1_out, and_2_out, ~Go);  // NAND_Gate
  // Probe on MEM_PC[11:0]
  ID_EX id_ex_1 (
    .CLK(CLK), .in_5(if_id_1_out_6), .in_6(ID_PC), .in_7(mips_regifile_1_r1), .in_8(mips_regifile_1_r2),
    .in_10(\单周期硬布线控制器_1_jmp ), .in_11(\单周期硬布线控制器_1_jr ), .in_12(\单周期硬布线控制器_1_jal ),
    .in_13(\单周期硬布线控制器_1_alu_src ), .in_14(\单周期硬布线控制器_1_bne ), .in_15(\单周期硬布线控制器_1_beq ),
    .in_16(\单周期硬布线控制器_1_memwrite ), .in_17(\单周期硬布线控制器_1_regwrite ), .in_18(\单周期硬布线控制器_1_memtoreg ),
    .in_20(\单周期硬布线控制器_1_alu_op ), .out_24(id_ex_1_out_24),
    .\传输状态Out_表明当前传输数据有效 (\id_ex_1_传输状态out_表明当前传输数据有效 ),
    .out_26({id_ex_1_out_26[26:6], id_ex_1_out_26_2, id_ex_1_out_26[5:0]}), .out_27(EX_PC),
    .out_28(id_ex_1_out_28), .out_29(id_ex_1_out_29), .out_31(id_ex_1_out_31), .out_32(id_ex_1_out_32),
    .out_33(id_ex_1_out_33), .out_34(id_ex_1_out_34), .out_35(id_ex_1_out_35), .out_36(id_ex_1_out_36),
    .out_37(id_ex_1_out_37), .out_38(id_ex_1_out_38), .out_39(id_ex_1_out_39), .out_41(id_ex_1_out_41),
    .\使能端_低电平有效_stall_高电平有效 (\if_id_1_传输状态out_表明当前传输数据有效 ), .in_1(multiplexer_7_out),
    .in_19(\单周期硬布线控制器_1_regdst ), .out_40(id_ex_1_out_40), .in_9(shifter_1_out), .out_30(id_ex_1_out_30));  // open: 同步清零_气泡_高电平有效, in_21, out_42, in_22, out_43, in_23, out_44
  // Probe on WB_PC[11:0]
  Adder #(.width(32)) adder_2 (.a(EX_PC), .b(32'h4), .out(adder_2_out));  // open: cin, cout
  or or_3 (or_3_out, id_ex_1_out_32, or_1_out);
  Multiplexer #(.select(1), .width(32), .disabled("Z"), .enable("false")) multiplexer_9 (
    .in0(id_ex_1_out_29), .in1(id_ex_1_out_24), .out(multiplexer_9_out), .sel(id_ex_1_out_34));
  Adder #(.width(32)) adder_3 (.a(adder_2_out), .b(id_ex_1_out_30), .out(adder_3_out));  // open: cin, cout
  and and_3 (and_3_out, mips_alu_1_equal, id_ex_1_out_36);
  and and_4 (and_4_out, id_ex_1_out_35, ~mips_alu_1_equal);  // AND_Gate
  MIPS_ALU mips_alu_1 (
    .X(id_ex_1_out_28), .Y(multiplexer_9_out), .AluOP(id_ex_1_out_41), .Equal(mips_alu_1_equal),
    .Result(mips_alu_1_result), .shamt(id_ex_1_out_26_2));  // open: Result_2
  Counter #(.width(16), .max('hffff), .ongoal("wrap"), .trigger("rising"), .behavior("old")) counter_2 (
    .count(or_4_out), .Q(\条件分支成功数 ), .clk(CLK), .clr(RST));  // open: load, D, carry, preset
  Counter #(.width(16), .max('hffff), .ongoal("wrap"), .trigger("rising"), .behavior("old")) counter_3 (
    .count(or_3_out), .Q(\无条件分支数 ), .clk(CLK), .clr(RST));  // open: load, D, carry, preset
  or or_4 (or_4_out, and_3_out, and_4_out);
  EX_MEM ex_mem_1 (
    .in_1({id_ex_1_out_26[26:6], id_ex_1_out_26_2, id_ex_1_out_26[5:0]}), .CLK(CLK), .in_4(EX_PC),
    .in_5(mips_alu_1_result), .in_6(id_ex_1_out_29), .in_7(id_ex_1_out_37), .in_8(id_ex_1_out_38),
    .in_9(id_ex_1_out_39), .in_10(id_ex_1_out_40), .out_14(ex_mem_1_out_14),
    .\传输状态Out_表明当前传输数据有效 (\ex_mem_1_传输状态out_表明当前传输数据有效 ), .out_16(MEM_PC), .out_17(ex_mem_1_out_17),
    .out_18(ex_mem_1_out_18), .out_19(ex_mem_1_out_19), .out_20(ex_mem_1_out_20), .out_21(ex_mem_1_out_21),
    .out_22(ex_mem_1_out_22), .\使能端_低电平有效_stall_高电平有效 (\id_ex_1_传输状态out_表明当前传输数据有效 ), .in_11(id_ex_1_out_33),
    .out_23(ex_mem_1_out_23));  // open: 同步清零_气泡_高电平有效, in_13, out_24
  not not_1 (not_1_out, ex_mem_1_out_19);
  RAM #(.addrWidth(10), .dataWidth(32), .bus("separate"), .Select("high")) ram_1 (
    .addr(ex_mem_1_out_17[11:2]), .din(ex_mem_1_out_18), .data(ram_1_data), .str(ex_mem_1_out_19), .clk(CLK),
    .ld(not_1_out), .clr(RST));  // open: sel
  MEM_WB mem_wb_1 (
    .in_1(ex_mem_1_out_14), .CLK(CLK), .in_4(MEM_PC), .in_5(ex_mem_1_out_17), .in_6(ram_1_data),
    .in_7(ex_mem_1_out_20), .in_8(ex_mem_1_out_21), .in_9(ex_mem_1_out_22), .out_13(mem_wb_1_out_13),
    .\传输状态Out_表明当前传输数据有效 (\mem_wb_1_传输状态out_表明当前传输数据有效 ), .out_15(WB_PC), .out_16(mem_wb_1_out_16),
    .out_17(mem_wb_1_out_17), .out_18(mem_wb_1_out_18), .out_19(mem_wb_1_out_19), .out_20(mem_wb_1_out_20),
    .\使能端_低电平有效_stall_高电平有效 (\ex_mem_1_传输状态out_表明当前传输数据有效 ), .in_10(ex_mem_1_out_23), .out_21(mem_wb_1_out_21));  // open: 同步清零_气泡_高电平有效, in_12, out_22
  Multiplexer #(.select(1), .width(32), .disabled("Z"), .enable("false")) multiplexer_10 (
    .in0(mem_wb_1_out_16), .in1(mem_wb_1_out_17), .out(multiplexer_10_out), .sel(mem_wb_1_out_19));
  Multiplexer #(.select(1), .width(32), .disabled("Z"), .enable("false")) multiplexer_11 (
    .in0(multiplexer_10_out), .in1(adder_4_out), .out(multiplexer_11_out), .sel(mem_wb_1_out_21));
  Adder #(.width(32)) adder_4 (.a(WB_PC), .b(32'h4), .out(adder_4_out));  // open: cin, cout

  // Notes on the sheet:
  //   中断源
  //   中断等待指示
  //   指令存储器
  //   contents of rom_1 (hex, n*v repeats v):
  //   20100000 20110000 20120000 20130000 36100000 36310001 36520002 36730003 ae100000 ae110004 ae120008
  //   ae13000c 2002000a 20110000 20120000 20130000 c
  //   指令字
  //   数码管输出
  //   OP
  //   rs
  //   rd
  //   Func
  //   rt
  //   JR
  //   Beq
  //   JMP
  //   Bne
  //   OP
  //   JAL
  //   Func
  //   Syscall
  //   MemToReg
  //   MemWrite
  //   AluOP
  //   AluSrcB
  //   RegWrite
  //   RegDst
  //   流水调试日志用
  //   OP
  //   rs
  //   rt
  //   rd
endmodule
module \分支相关流水线  (
  output RegWrite,
  output MemWrite,
  output [31:0] PC,
  output [31:0] IR,
  output [31:0] RDin,
  output [31:0] MDin
);

  wire and_1_out, and_2_out, and_3_out, and_4_out, CLK, comparator_1_eq, ex_mem_1_out_20, ex_mem_1_out_21,
       ex_mem_1_out_22, ex_mem_1_out_23, \ex_mem_1_传输状态out_表明当前传输数据有效 , Go, id_ex_1_out_31, id_ex_1_out_32,
       id_ex_1_out_33, id_ex_1_out_34, id_ex_1_out_35, id_ex_1_out_36, id_ex_1_out_37, id_ex_1_out_38,
       id_ex_1_out_39, id_ex_1_out_40, \id_ex_1_传输状态out_表明当前传输数据有效 , \if_id_1_传输状态out_表明当前传输数据有效 , IR1, IR2,
       IR3, mem_wb_1_out_19, mem_wb_1_out_20, mem_wb_1_out_21, \mem_wb_1_传输状态out_表明当前传输数据有效 ,
       mips_alu_1_equal, nand_1_out, not_1_out, or_1_out, or_2_out, or_3_out, RST, SignedExt, syscall, W1,
       W2, W3, \单周期硬布线控制器_1_alu_src , \单周期硬布线控制器_1_beq , \单周期硬布线控制器_1_bne , \单周期硬布线控制器_1_jal ,
       \单周期硬布线控制器_1_jmp , \单周期硬布线控制器_1_jr , \单周期硬布线控制器_1_memtoreg , \单周期硬布线控制器_1_memwrite ,
       \单周期硬布线控制器_1_regdst , \单周期硬布线控制器_1_regwrite ;
  wire [3:0] id_ex_1_out_41, \单周期硬布线控制器_1_alu_op ;
  wire [4:0] multiplexer_4_out, multiplexer_5_out, multiplexer_6_out, multiplexer_8_out;
  wire [15:0] \总周期数 , \无条件分支数 , \条件分支成功数 ;
  wire [26:21] id_ex_1_out_26_2;
  wire [27:0] adder_2_out;
  wire [31:0] adder_1_out, adder_3_out, adder_4_out, bit_extender_1_out, bit_extender_2_out, ex_mem_1_out_14,
       ex_mem_1_out_16, ex_mem_1_out_17, id_ex_1_out_24, id_ex_1_out_27, id_ex_1_out_28, id_ex_1_out_29,
       id_ex_1_out_30, if_id_1_out_6, if_id_1_out_8, LedData, mem_wb_1_out_13, mem_wb_1_out_15,
       mem_wb_1_out_16, mem_wb_1_out_17, mips_alu_1_result, mips_regifile_1_r1, mips_regifile_1_r2,
       multiplexer_1_out, multiplexer_2_out, multiplexer_3_out, multiplexer_7_out, multiplexer_9_out,
       multiplexer_10_out, ram_1_data, shifter_1_out;
  wire [31:2] id_ex_1_out_26;

  Clock #(.highDuration(1), .lowDuration(1)) clock_1 (.out(CLK));
  Button _1 (.out(IR1));
  Button _2 (.out(IR2));
  Button _3 (.out(IR3));
  Button \u_总复位  (.out(RST));
  Register #(.width(32), .trigger("rising"), .Select("low")) u_PC (
    .D(multiplexer_1_out), .en(nand_1_out), .Q(PC), .clk(CLK), .clr(RST));
  Multiplexer #(.select(1), .width(32), .disabled("Z"), .enable("false")) multiplexer_1 (
    .in0(multiplexer_3_out), .in1(multiplexer_2_out), .out(multiplexer_1_out), .sel(id_ex_1_out_31));
  Multiplexer #(.select(1), .width(32), .disabled("Z"), .enable("false")) multiplexer_2 (
    .in0({id_ex_1_out_26, 2'b00}), .in1(id_ex_1_out_28), .out(multiplexer_2_out), .sel(id_ex_1_out_32));
  Button \u_继续运行  (.out(Go));
  LED #(.active("true")) led_1 (.in(W1));
  LED #(.active("true")) led_2 (.in(W2));
  LED #(.active("true")) led_3 (.in(W3));
  Hex_Digit_Display hex_digit_display_1 (.value(LedData[31:28]));  // open: dp
  Adder #(.width(32)) adder_1 (.a(PC), .b(32'h4), .out(adder_1_out));  // open: cin, cout
  Multiplexer #(.select(1), .width(32), .disabled("Z"), .enable("false")) multiplexer_3 (
    .in0(adder_1_out), .in1(adder_3_out), .out(multiplexer_3_out), .sel(or_3_out));
  Hex_Digit_Display hex_digit_display_2 (.value(LedData[27:24]));  // open: dp
  Hex_Digit_Display hex_digit_display_3 (.value(LedData[23:20]));  // open: dp
  ROM #(.addrWidth(10), .dataWidth(32), .Select("high")) rom_1 (.addr(PC[11:2]), .data(IR));
  Hex_Digit_Display hex_digit_display_4 (.value(LedData[15:12]));  // open: dp
  Hex_Digit_Display hex_digit_display_5 (.value(LedData[19:16]));  // open: dp
  IF_ID if_id_1 (
    .CLK(CLK), .out_6(if_id_1_out_6), .\传输状态Out_表明当前传输数据有效 (\if_id_1_传输状态out_表明当前传输数据有效 ),
    .\同步清零_气泡_高电平有效 (or_2_out), .\使能端_低电平有效_stall_高电平有效 (nand_1_out), .in_5(PC), .out_8(if_id_1_out_8),
    .in_1(IR));
  Hex_Digit_Display hex_digit_display_6 (.value(LedData[7:4]));  // open: dp
  Hex_Digit_Display hex_digit_display_7 (.value(LedData[11:8]));  // open: dp
  Hex_Digit_Display hex_digit_display_8 (.value(LedData[3:0]));  // open: dp
  // Probe on \总周期数 
  Multiplexer #(.select(1), .width(5), .disabled("Z"), .enable("false")) multiplexer_4 (
    .in0(if_id_1_out_6[25:21]), .in1(5'b00010), .out(multiplexer_4_out), .sel(syscall));
  Multiplexer #(.select(1), .width(5), .disabled("Z"), .enable("false")) multiplexer_5 (
    .in0(if_id_1_out_6[20:16]), .in1(5'b00100), .out(multiplexer_5_out), .sel(syscall));
  Multiplexer #(.select(1), .width(5), .disabled("Z"), .enable("false")) multiplexer_6 (
    .in0(mem_wb_1_out_13[20:16]), .in1(mem_wb_1_out_13[15:11]), .out(multiplexer_6_out), .sel(mem_wb_1_out_20));
  assign bit_extender_1_out = {{16{if_id_1_out_6[15]}}, if_id_1_out_6[15:0]};  // Bit_Extender bit_extender_1
  assign bit_extender_2_out = {{16{1'b0}}, if_id_1_out_6[15:0]};  // Bit_Extender bit_extender_2
  Multiplexer #(.select(1), .width(32), .disabled("Z"), .enable("false")) multiplexer_7 (
    .in0(bit_extender_2_out), .in1(bit_extender_1_out), .out(multiplexer_7_out), .sel(SignedExt));
  Multiplexer #(.select(1), .width(5), .disabled("Z"), .enable("false")) multiplexer_8 (
    .in0(multiplexer_6_out), .in1({5{1'b1}}), .out(multiplexer_8_out), .sel(mem_wb_1_out_21));
  Shifter #(.width(32), .shift("ll")) shifter_1 (.in(multiplexer_7_out), .\dist (5'b00010), .out(shifter_1_out));
  or or_1 (or_1_out, nand_1_out, \mem_wb_1_传输状态out_表明当前传输数据有效 );
  \单周期硬布线控制器  \u_单周期硬布线控制器_1  (
    .Func(if_id_1_out_6[5:0]), .OP(if_id_1_out_6[31:26]), .ALU_OP(\单周期硬布线控制器_1_alu_op ),
    .MemToReg(\单周期硬布线控制器_1_memtoreg ), .MemWrite(\单周期硬布线控制器_1_memwrite ), .ALU_SRC(\单周期硬布线控制器_1_alu_src ),
    .RegWrite(\单周期硬布线控制器_1_regwrite ), .SysCALL(syscall), .SignedExt(SignedExt),
    .RegDst(\单周期硬布线控制器_1_regdst ), .JR(\单周期硬布线控制器_1_jr ), .JMP(\单周期硬布线控制器_1_jmp ), .Beq(\单周期硬布线控制器_1_beq ),
    .JAL(\单周期硬布线控制器_1_jal ), .Bne(\单周期硬布线控制器_1_bne ));
  Comparator #(.width(32), .mode("twosComplement")) comparator_1 (
    .a(mips_regifile_1_r1), .b(32'h22), .eq(comparator_1_eq));  // open: gt, lt
  Counter #(.width(16), .max('hffff), .ongoal("wrap"), .trigger("rising"), .behavior("old")) counter_1 (
    .count(or_1_out), .Q(\总周期数 ), .clk(CLK), .clr(RST));  // open: load, D, carry, preset
  MIPS_Regifile mips_regifile_1 (
    .Din(RDin), .Clk(CLK), .R1(mips_regifile_1_r1), .R2(mips_regifile_1_r2), .WE(RegWrite),
    .W_num(multiplexer_8_out), .R1_num(multiplexer_4_out), .R2_num(multiplexer_5_out));
  and and_1 (and_1_out, comparator_1_eq, syscall);
  and and_2 (and_2_out, syscall, ~comparator_1_eq);  // AND_Gate
  nand nand_1 (nand_1_out, and_2_out, ~Go);  // NAND_Gate
  ID_EX id_ex_1 (
    .CLK(CLK), .in_5(if_id_1_out_6), .in_6(if_id_1_out_8), .in_7(mips_regifile_1_r1),
    .in_8(mips_regifile_1_r2), .in_10(\单周期硬布线控制器_1_jmp ), .in_11(\单周期硬布线控制器_1_jr ),
    .in_12(\单周期硬布线控制器_1_jal ), .in_13(\单周期硬布线控制器_1_alu_src ), .in_14(\单周期硬布线控制器_1_bne ),
    .in_15(\单周期硬布线控制器_1_beq ), .in_16(\单周期硬布线控制器_1_memwrite ), .in_17(\单周期硬布线控制器_1_regwrite ),
    .in_18(\单周期硬布线控制器_1_memtoreg ), .in_20(\单周期硬布线控制器_1_alu_op ), .out_24(id_ex_1_out_24),
    .\传输状态Out_表明当前传输数据有效 (\id_ex_1_传输状态out_表明当前传输数据有效 ), .out_26({id_ex_1_out_26_2, id_ex_1_out_26[27:2]}),
    .out_27(id_ex_1_out_27), .out_28(id_ex_1_out_28), .out_29(id_ex_1_out_29), .out_31(id_ex_1_out_31),
    .out_32(id_ex_1_out_32), .out_33(id_ex_1_out_33), .out_34(id_ex_1_out_34), .out_35(id_ex_1_out_35),
    .out_36(id_ex_1_out_36), .out_37(id_ex_1_out_37), .out_38(id_ex_1_out_38), .out_39(id_ex_1_out_39),
    .out_41(id_ex_1_out_41), .\同步清零_气泡_高电平有效 (or_2_out),
    .\使能端_低电平有效_stall_高电平有效 (\if_id_1_传输状态out_表明当前传输数据有效 ), .in_1(multiplexer_7_out),
    .in_19(\单周期硬布线控制器_1_regdst ), .out_40(id_ex_1_out_40), .in_9(shifter_1_out), .out_30(id_ex_1_out_30));  // open: in_21, out_42, in_22, out_43, in_23, out_44
  Register #(.width(32), .trigger("rising"), .Select("low")) register_1 (
    .D(mips_regifile_1_r2), .en(and_1_out), .Q(LedData), .clk(CLK), .clr(RST));
  Adder #(.width(32)) adder_2 (
    .a(id_ex_1_out_27), .b(32'h4), .out({id_ex_1_out_26[31:28], adder_2_out}));  // open: cin, cout
  Multiplexer #(.select(1), .width(32), .disabled("Z"), .enable("false")) multiplexer_9 (
    .in0(id_ex_1_out_29), .in1(id_ex_1_out_24), .out(multiplexer_9_out), .sel(id_ex_1_out_34));
  Adder #(.width(32)) adder_3 (
    .a({id_ex_1_out_26[31:28], adder_2_out}), .b(id_ex_1_out_30), .out(adder_3_out));  // open: cin, cout
  or or_2 (or_2_out, id_ex_1_out_31, or_3_out);
  and and_3 (and_3_out, mips_alu_1_equal, id_ex_1_out_36);
  and and_4 (and_4_out, id_ex_1_out_35, ~mips_alu_1_equal);  // AND_Gate
  MIPS_ALU mips_alu_1 (
    .X(id_ex_1_out_28), .Y(multiplexer_9_out), .AluOP(id_ex_1_out_41), .Equal(mips_alu_1_equal),
    .Result(mips_alu_1_result), .shamt(id_ex_1_out_26[12:8]));  // open: Result_2
  Counter #(.width(16), .max('hffff), .ongoal("wrap"), .trigger("rising"), .behavior("old")) counter_2 (
    .count(or_3_out), .Q(\条件分支成功数 ), .clk(CLK), .clr(RST));  // open: load, D, carry, preset
  Counter #(.width(16), .max('hffff), .ongoal("wrap"), .trigger("rising"), .behavior("old")) counter_3 (
    .count(id_ex_1_out_31), .Q(\无条件分支数 ), .clk(CLK), .clr(RST));  // open: load, D, carry, preset
  or or_3 (or_3_out, and_3_out, and_4_out);
  // Probe on \无条件分支数 
  // Probe on \条件分支成功数 
  EX_MEM ex_mem_1 (
    .in_1({id_ex_1_out_26_2, id_ex_1_out_26[27:2]}), .CLK(CLK), .in_4(id_ex_1_out_27),
    .in_5(mips_alu_1_result), .in_6(id_ex_1_out_29), .in_7(id_ex_1_out_37), .in_8(id_ex_1_out_38),
    .in_9(id_ex_1_out_39), .in_10(id_ex_1_out_40), .out_14(ex_mem_1_out_14),
    .\传输状态Out_表明当前传输数据有效 (\ex_mem_1_传输状态out_表明当前传输数据有效 ), .out_16(ex_mem_1_out_16), .out_17(ex_mem_1_out_17),
    .out_18(MDin), .out_19(MemWrite), .out_20(ex_mem_1_out_20), .out_21(ex_mem_1_out_21),
    .out_22(ex_mem_1_out_22), .\使能端_低电平有效_stall_高电平有效 (\id_ex_1_传输状态out_表明当前传输数据有效 ), .in_11(id_ex_1_out_33),
    .out_23(ex_mem_1_out_23));  // open: 同步清零_气泡_高电平有效, in_13, out_24
  not not_1 (not_1_out, MemWrite);
  RAM #(.addrWidth(10), .dataWidth(32), .bus("separate"), .Select("high")) ram_1 (
    .addr(ex_mem_1_out_17[11:2]), .din(MDin), .data(ram_1_data), .str(MemWrite), .clk(CLK), .ld(not_1_out),
    .clr(RST));  // open: sel
  MEM_WB mem_wb_1 (
    .in_1(ex_mem_1_out_14), .CLK(CLK), .in_4(ex_mem_1_out_16), .in_5(ex_mem_1_out_17), .in_6(ram_1_data),
    .in_7(ex_mem_1_out_20), .in_8(ex_mem_1_out_21), .in_9(ex_mem_1_out_22), .out_13(mem_wb_1_out_13),
    .\传输状态Out_表明当前传输数据有效 (\mem_wb_1_传输状态out_表明当前传输数据有效 ), .out_15(mem_wb_1_out_15), .out_16(mem_wb_1_out_16),
    .out_17(mem_wb_1_out_17), .out_18(RegWrite), .out_19(mem_wb_1_out_19), .out_20(mem_wb_1_out_20),
    .\使能端_低电平有效_stall_高电平有效 (\ex_mem_1_传输状态out_表明当前传输数据有效 ), .in_10(ex_mem_1_out_23), .out_21(mem_wb_1_out_21));  // open: 同步清零_气泡_高电平有效, in_12, out_22
  Multiplexer #(.select(1), .width(32), .disabled("Z"), .enable("false")) multiplexer_10 (
    .in0(mem_wb_1_out_16), .in1(mem_wb_1_out_17), .out(multiplexer_10_out), .sel(mem_wb_1_out_19));
  Multiplexer #(.select(1), .width(32), .disabled("Z"), .enable("false")) multiplexer_11 (
    .in0(multiplexer_10_out), .in1(adder_4_out), .out(RDin), .sel(mem_wb_1_out_21));
  Adder #(.width(32)) adder_4 (.a(mem_wb_1_out_15), .b(32'h4), .out(adder_4_out));  // open: cin, cout

  // Notes on the sheet:
  //   中断源
  //   中断等待指示
  //   总复位信号应将除ROM以外所有存储组件全部清零
  //   指令存储器
  //   指令字
  //   contents of rom_1 (hex, n*v repeats v):
  //   20110020 20020022 8000c06 20110000 20110000 2002000a 10000003 20110000 20110000 2002000a 14110003
  //   20110000 20110000 2002000a c000c14 2002000a 0 0 0 c 2231ffff 0 0 0 112020 0 0 0 c 1620fff6 3e00008
  //   数码管输出
  //   数码管输出应该用寄存器锁存，否则显示数据只能一闪而过
  //   OP
  //   Func
  //   rs
  //   rt
  //   rd
  //   JMP
  //   JR
  //   OP
  //   Func
  //   Beq
  //   Bne
  //   MemToReg
  //   MemWrite
  //   AluOP
  //   AluSrcB
  //   RegWrite
  //   JAL
  //   RegDst
  //   Syscall
  //   为方便自动评测，需要输出PC，IR，寄存器文件写入端口RDin，内存写入端口MDin等信号
  //   OP
  //   rs
  //   rt
  //   rd
endmodule

module \气泡流水线  (
  output RegWrite,
  output MemWrite,
  output [31:0] PC,
  output [31:0] IR,
  output [31:0] RDin,
  output [31:0] MDin
);

  wire and_1_out, and_2_out, and_3_out, and_4_out, and_5_out, CLK, comparator_1_eq, comparator_2_eq,
       ex_mem_1_out_20, ex_mem_1_out_21, ex_mem_1_out_22, ex_mem_1_out_23, ex_mem_1_out_24,
       \ex_mem_1_传输状态out_表明当前传输数据有效 , Go, id_ex_1_out_31, id_ex_1_out_32, id_ex_1_out_33, id_ex_1_out_34,
       id_ex_1_out_35, id_ex_1_out_36, id_ex_1_out_37, id_ex_1_out_38, id_ex_1_out_39, id_ex_1_out_40,
       id_ex_1_out_42, \id_ex_1_传输状态out_表明当前传输数据有效 , IR1, IR2, IR3, mem_wb_1_out_19, mem_wb_1_out_20,
       mem_wb_1_out_21, mem_wb_1_out_22, mips_alu_1_equal, nand_1_out, not_1_out, or_1_out, or_2_out,
       or_3_out, or_4_out, or_5_out, RST, SignedExt, syscall, W1, W2, W3, \单周期硬布线控制器_1_alu_src ,
       \单周期硬布线控制器_1_beq , \单周期硬布线控制器_1_bne , \单周期硬布线控制器_1_jal , \单周期硬布线控制器_1_jmp , \单周期硬布线控制器_1_jr ,
       \单周期硬布线控制器_1_memtoreg , \单周期硬布线控制器_1_memwrite , \单周期硬布线控制器_1_regdst , \单周期硬布线控制器_1_regwrite , \数据相关 ;
  wire [1:0] ex_mem_1_out_17;
  wire [3:0] id_ex_1_out_41, \单周期硬布线控制器_1_alu_op ;
  wire [4:0] id_ex_1_out_26_2, multiplexer_6_out, multiplexer_8_out, multiplexer_10_out, multiplexer_11_out,
       multiplexer_12_out, multiplexer_13_out, R1, R2;
  wire [5:0] FUNC, OP;
  wire [9:0] ex_mem_1_out_17_2;
  wire [15:0] adder_4_out, counter_4_q, \LoadUse次数 , \总周期数 , \插入气泡数 , \无条件分支数 , \条件分支成功数 ;
  wire [19:0] ex_mem_1_out_17_3;
  wire [25:6] if_id_1_out_6;
  wire [26:0] id_ex_1_out_26;
  wire [31:0] adder_1_out, adder_2_out, adder_3_out, adder_5_out, bit_extender_1_out, bit_extender_2_out,
       ex_mem_1_out_14, EX_PC, id_ex_1_out_24, id_ex_1_out_28, id_ex_1_out_29, id_ex_1_out_30, ID_PC,
       LedData, MEM_PC, mem_wb_1_out_13, mem_wb_1_out_16, mem_wb_1_out_17, mips_alu_1_result,
       mips_regifile_1_r1, mips_regifile_1_r2, multiplexer_1_out, multiplexer_2_out, multiplexer_3_out,
       multiplexer_7_out, multiplexer_9_out, multiplexer_14_out, ram_1_data, shifter_1_out, WB_PC;

  Clock #(.highDuration(1), .lowDuration(1)) clock_1 (.out(CLK));
  Button _1 (.out(IR1));
  Button _2 (.out(IR2));
  Button _3 (.out(IR3));
  Button \u_总复位  (.out(RST));
  Register #(.width(32), .trigger("rising"), .Select("low")) u_PC (
    .D(multiplexer_1_out), .en(and_1_out), .Q(PC), .clk(CLK), .clr(RST));
  Multiplexer #(.select(1), .width(32), .disabled("Z"), .enable("false")) multiplexer_1 (
    .in0(multiplexer_3_out), .in1(multiplexer_2_out), .out(multiplexer_1_out), .sel(id_ex_1_out_31));
  Multiplexer #(.select(1), .width(32), .disabled("Z"), .enable("false")) multiplexer_2 (
    .in0({adder_2_out[31:28], id_ex_1_out_26[20:6], id_ex_1_out_26_2, id_ex_1_out_26[5:0], 2'b00}),
    .in1(id_ex_1_out_28), .out(multiplexer_2_out), .sel(id_ex_1_out_32));
  Button \u_继续运行  (.out(Go));
  LED #(.active("true")) led_1 (.in(W1));
  LED #(.active("true")) led_2 (.in(W2));
  LED #(.active("true")) led_3 (.in(W3));
  Hex_Digit_Display hex_digit_display_1 (.value(LedData[31:28]));  // open: dp
  ROM #(.addrWidth(10), .dataWidth(32), .Select("high")) rom_1 (.addr(PC[11:2]), .data(IR));
  Adder #(.width(32)) adder_1 (.a(PC), .b(32'h4), .out(adder_1_out));  // open: cin, cout
  Multiplexer #(.select(1), .width(32), .disabled("Z"), .enable("false")) multiplexer_3 (
    .in0(adder_1_out), .in1(adder_3_out), .out(multiplexer_3_out), .sel(or_5_out));
  Hex_Digit_Display hex_digit_display_2 (.value(LedData[27:24]));  // open: dp
  Hex_Digit_Display hex_digit_display_3 (.value(LedData[23:20]));  // open: dp
  Hex_Digit_Display hex_digit_display_4 (.value(LedData[19:16]));  // open: dp
  Hex_Digit_Display hex_digit_display_5 (.value(LedData[15:12]));  // open: dp
  or or_1 (or_1_out, RST, or_4_out);
  IF_ID if_id_1 (
    .CLK(CLK), .out_6({OP, if_id_1_out_6, FUNC}), .\同步清零_气泡_高电平有效 (or_1_out),
    .\使能端_低电平有效_stall_高电平有效 (and_1_out), .in_5(PC), .out_8(ID_PC), .in_1(IR));  // open: 传输状态Out_表明当前传输数据有效
  Hex_Digit_Display hex_digit_display_6 (.value(LedData[7:4]));  // open: dp
  Hex_Digit_Display hex_digit_display_7 (.value(LedData[11:8]));  // open: dp
  // Probe on \总周期数 
  assign bit_extender_1_out = {{16{if_id_1_out_6[15]}}, {if_id_1_out_6[15:6], FUNC}};  // Bit_Extender bit_extender_1
  assign bit_extender_2_out = {{16{1'b0}}, {if_id_1_out_6[15:6], FUNC}};  // Bit_Extender bit_extender_2
  \数据相关检测  \u_数据相关检测_1  (
    .OP(OP), .EX_WriteReg_num(multiplexer_11_out), .EX_RegWrite(id_ex_1_out_38),
    .MEM_WriteReg_num(multiplexer_13_out), .MEM_RegWrite(ex_mem_1_out_20), .\数据相关 (\数据相关 ), .Func(FUNC),
    .ID_R1_num(R1), .ID_R2_num(R2));
  Hex_Digit_Display hex_digit_display_8 (.value(LedData[3:0]));  // open: dp
  Multiplexer #(.select(1), .width(5), .disabled("Z"), .enable("false")) multiplexer_4 (
    .in0(if_id_1_out_6[25:21]), .in1(5'b00010), .out(R1), .sel(syscall));
  Multiplexer #(.select(1), .width(5), .disabled("Z"), .enable("false")) multiplexer_5 (
    .in0(if_id_1_out_6[20:16]), .in1(5'b00100), .out(R2), .sel(syscall));
  Multiplexer #(.select(1), .width(5), .disabled("Z"), .enable("false")) multiplexer_6 (
    .in0(mem_wb_1_out_13[20:16]), .in1(mem_wb_1_out_13[15:11]), .out(multiplexer_6_out), .sel(mem_wb_1_out_20));
  Multiplexer #(.select(1), .width(32), .disabled("Z"), .enable("false")) multiplexer_7 (
    .in0(bit_extender_2_out), .in1(bit_extender_1_out), .out(multiplexer_7_out), .sel(SignedExt));
  and and_1 (and_1_out, ~\数据相关 , nand_1_out);  // AND_Gate
  Multiplexer #(.select(1), .width(5), .disabled("Z"), .enable("false")) multiplexer_8 (
    .in0(multiplexer_6_out), .in1({5{1'b1}}), .out(multiplexer_8_out), .sel(mem_wb_1_out_21));
  Shifter #(.width(32), .shift("ll")) shifter_1 (.in(multiplexer_7_out), .\dist (5'b00010), .out(shifter_1_out));
  or or_2 (or_2_out, nand_1_out, ~mem_wb_1_out_22);  // OR_Gate
  \单周期硬布线控制器  \u_单周期硬布线控制器_1  (
    .Func(FUNC), .OP(OP), .ALU_OP(\单周期硬布线控制器_1_alu_op ), .MemToReg(\单周期硬布线控制器_1_memtoreg ),
    .MemWrite(\单周期硬布线控制器_1_memwrite ), .ALU_SRC(\单周期硬布线控制器_1_alu_src ), .RegWrite(\单周期硬布线控制器_1_regwrite ),
    .SysCALL(syscall), .SignedExt(SignedExt), .RegDst(\单周期硬布线控制器_1_regdst ), .JR(\单周期硬布线控制器_1_jr ),
    .JMP(\单周期硬布线控制器_1_jmp ), .Beq(\单周期硬布线控制器_1_beq ), .JAL(\单周期硬布线控制器_1_jal ), .Bne(\单周期硬布线控制器_1_bne ));
  Comparator #(.width(32), .mode("twosComplement")) comparator_1 (
    .a(mips_regifile_1_r1), .b(32'h22), .eq(comparator_1_eq));  // open: gt, lt
  Counter #(.width(16), .max('hffff), .ongoal("wrap"), .trigger("rising"), .behavior("old")) counter_1 (
    .count(or_2_out), .Q(\总周期数 ), .clk(CLK), .clr(RST));  // open: load, D, carry, preset
  MIPS_Regifile mips_regifile_1 (
    .Din(RDin), .Clk(CLK), .R1(mips_regifile_1_r1), .R2(mips_regifile_1_r2), .WE(RegWrite),
    .W_num(multiplexer_8_out), .R1_num(R1), .R2_num(R2));
  and and_2 (and_2_out, comparator_1_eq, syscall);
  and and_3 (and_3_out, syscall, ~comparator_1_eq);  // AND_Gate
  Register #(.width(32), .trigger("rising"), .Select("low")) register_1 (
    .D(mips_regifile_1_r2), .en(and_2_out), .Q(LedData), .clk(CLK), .clr(RST));
  nand nand_1 (nand_1_out, and_3_out, ~Go);  // NAND_Gate
  or or_3 (or_3_out, or_4_out, RST, \数据相关 );
  ID_EX id_ex_1 (
    .CLK(CLK), .in_5({OP, if_id_1_out_6, FUNC}), .in_6(ID_PC), .in_7(mips_regifile_1_r1),
    .in_8(mips_regifile_1_r2), .in_10(\单周期硬布线控制器_1_jmp ), .in_11(\单周期硬布线控制器_1_jr ),
    .in_12(\单周期硬布线控制器_1_jal ), .in_13(\单周期硬布线控制器_1_alu_src ), .in_14(\单周期硬布线控制器_1_bne ),
    .in_15(\单周期硬布线控制器_1_beq ), .in_16(\单周期硬布线控制器_1_memwrite ), .in_17(\单周期硬布线控制器_1_regwrite ),
    .in_18(\单周期硬布线控制器_1_memtoreg ), .in_20(\单周期硬布线控制器_1_alu_op ), .out_24(id_ex_1_out_24),
    .\传输状态Out_表明当前传输数据有效 (\id_ex_1_传输状态out_表明当前传输数据有效 ),
    .out_26({id_ex_1_out_26[26:6], id_ex_1_out_26_2, id_ex_1_out_26[5:0]}), .out_27(EX_PC),
    .out_28(id_ex_1_out_28), .out_29(id_ex_1_out_29), .out_31(id_ex_1_out_31), .out_32(id_ex_1_out_32),
    .out_33(id_ex_1_out_33), .out_34(id_ex_1_out_34), .out_35(id_ex_1_out_35), .out_36(id_ex_1_out_36),
    .out_37(id_ex_1_out_37), .out_38(id_ex_1_out_38), .out_39(id_ex_1_out_39), .out_41(id_ex_1_out_41),
    .\同步清零_气泡_高电平有效 (or_3_out), .\使能端_低电平有效_stall_高电平有效 (1'b1), .in_1(multiplexer_7_out),
    .in_19(\单周期硬布线控制器_1_regdst ), .out_40(id_ex_1_out_40), .in_9(shifter_1_out), .out_30(id_ex_1_out_30),
    .in_21(syscall), .out_42(id_ex_1_out_42));  // open: in_22, out_43, in_23, out_44
  Adder #(.width(32)) adder_2 (.a(EX_PC), .b(32'h4), .out(adder_2_out));  // open: cin, cout
  Multiplexer #(.select(1), .width(32), .disabled("Z"), .enable("false")) multiplexer_9 (
    .in0(id_ex_1_out_29), .in1(id_ex_1_out_24), .out(multiplexer_9_out), .sel(id_ex_1_out_34));
  Adder #(.width(32)) adder_3 (.a(adder_2_out), .b(id_ex_1_out_30), .out(adder_3_out));  // open: cin, cout
  or or_4 (or_4_out, id_ex_1_out_31, or_5_out);
  and and_4 (and_4_out, mips_alu_1_equal, id_ex_1_out_36);
  and and_5 (and_5_out, id_ex_1_out_35, ~mips_alu_1_equal);  // AND_Gate
  MIPS_ALU mips_alu_1 (
    .X(id_ex_1_out_28), .Y(multiplexer_9_out), .AluOP(id_ex_1_out_41), .Equal(mips_alu_1_equal),
    .Result(mips_alu_1_result), .shamt(id_ex_1_out_26_2));  // open: Result_2
  Counter #(.width(16), .max('hffff), .ongoal("wrap"), .trigger("rising"), .behavior("old")) counter_2 (
    .count(or_5_out), .Q(\条件分支成功数 ), .clk(CLK), .clr(RST));  // open: load, D, carry, preset
  Counter #(.width(16), .max('hffff), .ongoal("wrap"), .trigger("rising"), .behavior("old")) counter_3 (
    .count(id_ex_1_out_31), .Q(\无条件分支数 ), .clk(CLK), .clr(RST));  // open: load, D, carry, preset
  or or_5 (or_5_out, and_4_out, and_5_out);
  Multiplexer #(.select(1), .width(5), .disabled("Z"), .enable("false")) multiplexer_10 (
    .in0(id_ex_1_out_26[15:11]), .in1(id_ex_1_out_26[10:6]), .out(multiplexer_10_out), .sel(id_ex_1_out_40));
  // Probe on PC[11:0]
  // Probe on ID_PC[11:0]
  Multiplexer #(.select(1), .width(5), .disabled("Z"), .enable("false")) multiplexer_11 (
    .in0(multiplexer_10_out), .in1({5{1'b1}}), .out(multiplexer_11_out), .sel(id_ex_1_out_33));
  // Probe on EX_PC[11:0]
  // Probe on MEM_PC[11:0]
  // Probe on WB_PC[11:0]
  EX_MEM ex_mem_1 (
    .in_1({id_ex_1_out_26[26:6], id_ex_1_out_26_2, id_ex_1_out_26[5:0]}), .CLK(CLK), .in_4(EX_PC),
    .in_5(mips_alu_1_result), .in_6(id_ex_1_out_29), .in_7(id_ex_1_out_37), .in_8(id_ex_1_out_38),
    .in_9(id_ex_1_out_39), .in_10(id_ex_1_out_40), .out_14(ex_mem_1_out_14),
    .\传输状态Out_表明当前传输数据有效 (\ex_mem_1_传输状态out_表明当前传输数据有效 ), .out_16(MEM_PC),
    .out_17({ex_mem_1_out_17_3, ex_mem_1_out_17_2, ex_mem_1_out_17}), .out_18(MDin), .out_19(MemWrite),
    .out_20(ex_mem_1_out_20), .out_21(ex_mem_1_out_21), .out_22(ex_mem_1_out_22), .\同步清零_气泡_高电平有效 (RST),
    .\使能端_低电平有效_stall_高电平有效 (\id_ex_1_传输状态out_表明当前传输数据有效 ), .in_11(id_ex_1_out_33), .out_23(ex_mem_1_out_23),
    .in_13(id_ex_1_out_42), .out_24(ex_mem_1_out_24));
  not not_1 (not_1_out, MemWrite);
  // Probe on \总周期数 
  // Probe on \无条件分支数 
  // Probe on \条件分支成功数 
  // Probe on \插入气泡数 
  // Probe on \LoadUse次数 
  RAM #(.addrWidth(10), .dataWidth(32), .bus("separate"), .Select("high")) ram_1 (
    .addr(ex_mem_1_out_17_2), .din(MDin), .data(ram_1_data), .str(MemWrite), .clk(CLK), .ld(not_1_out),
    .clr(RST));  // open: sel
  Multiplexer #(.select(1), .width(5), .disabled("Z"), .enable("false")) multiplexer_12 (
    .in0(ex_mem_1_out_14[20:16]), .in1(ex_mem_1_out_14[15:11]), .out(multiplexer_12_out),
    .sel(ex_mem_1_out_22));
  MEM_WB mem_wb_1 (
    .in_1(ex_mem_1_out_14), .CLK(CLK), .in_4(MEM_PC),
    .in_5({ex_mem_1_out_17_3, ex_mem_1_out_17_2, ex_mem_1_out_17}), .in_6(ram_1_data),
    .in_7(ex_mem_1_out_20), .in_8(ex_mem_1_out_21), .in_9(ex_mem_1_out_22), .out_13(mem_wb_1_out_13),
    .out_15(WB_PC), .out_16(mem_wb_1_out_16), .out_17(mem_wb_1_out_17), .out_18(RegWrite),
    .out_19(mem_wb_1_out_19), .out_20(mem_wb_1_out_20), .\同步清零_气泡_高电平有效 (RST),
    .\使能端_低电平有效_stall_高电平有效 (\ex_mem_1_传输状态out_表明当前传输数据有效 ), .in_10(ex_mem_1_out_23),
    .out_21(mem_wb_1_out_21), .in_12(ex_mem_1_out_24), .out_22(mem_wb_1_out_22));  // open: 传输状态Out_表明当前传输数据有效
  Multiplexer #(.select(1), .width(5), .disabled("Z"), .enable("false")) multiplexer_13 (
    .in0(multiplexer_12_out), .in1({5{1'b1}}), .out(multiplexer_13_out), .sel(ex_mem_1_out_23));
  Multiplexer #(.select(1), .width(32), .disabled("Z"), .enable("false")) multiplexer_14 (
    .in0(mem_wb_1_out_16), .in1(mem_wb_1_out_17), .out(multiplexer_14_out), .sel(mem_wb_1_out_19));
  Multiplexer #(.select(1), .width(32), .disabled("Z"), .enable("false")) multiplexer_15 (
    .in0(multiplexer_14_out), .in1(adder_5_out), .out(RDin), .sel(mem_wb_1_out_21));
  Counter #(.width(16), .max('hffff), .ongoal("wrap"), .trigger("rising"), .behavior("old")) counter_4 (
    .count(\数据相关 ), .Q(counter_4_q), .clk(CLK), .clr(RST));  // open: load, D, carry, preset
  Comparator #(.width(16), .mode("twosComplement")) comparator_2 (
    .a(counter_4_q), .b({16{1'b0}}), .eq(comparator_2_eq));  // open: gt, lt
  Adder #(.width(16)) adder_4 (.a(counter_4_q), .b(16'h1), .out(adder_4_out));  // open: cin, cout
  Adder #(.width(32)) adder_5 (.a(WB_PC), .b(32'h4), .out(adder_5_out));  // open: cin, cout
  Multiplexer #(.select(1), .width(16), .disabled("Z"), .enable("false")) multiplexer_16 (
    .in0(adder_4_out), .in1({16{1'b0}}), .out(\插入气泡数 ), .sel(comparator_2_eq));

  // Other names for the same wires on the sheet: IF_PC[31:0] = PC

  // Notes on the sheet:
  //   中断源
  //   中断等待指示
  //   总复位信号应将除ROM以外所有存储组件全部清零
  //   指令存储器
  //   contents of rom_1 (hex, n*v repeats v):
  //   20110001 8000c05 20110001 20120002 20130003 8000c09 20110001 20120002 20130003 8000c0d 20110001
  //   20120002 20130003 8000c11 20110001 20120002 20130003 c000cb8 20100001 20110001 118fc0 112020
  //   20020022 c 118882 12200001 8000c15 112020 20020022 c 20110001 118880 112020 20020022 c 12200001
  //   8000c1f 20110001 118fc0 112020 20020022 c 1188c3 112020 20020022 c 118903 112020 20020022 c 118903
  //   112020 20020022 c 118903 112020 20020022 c 118903 112020 20020022 c 118903 112020 20020022 c 118903
  //   112020 20020022 c 118903 112020 20020022 c 20100001 109fc0 139fc3 8021 2012000c 24160003 26100001
  //   3210000f 20080008 20090001 139900 2709825 132020 20020022 c 1094022 1500fff9 22100001 2018000f
  //   2188024 108700 20080008 20090001 139902 2709825 132021 20020022 c 1094022 1500fff9 108702 2c9b022
  //   12c00001 8000c50 4020 1084027 84400 3508ffff 82021 20020022 c 2010ffff 20110000 ae300000 22100001
  //   22310004 ae300000 22100001 22310004 ae300000 22100001 22310004 ae300000 22100001 22310004 ae300000
  //   22100001 22310004 ae300000 22100001 22310004 ae300000 22100001 22310004 ae300000 22100001 22310004
  //   ae300000 22100001 22310004 ae300000 22100001 22310004 ae300000 22100001 22310004 ae300000 22100001
  //   22310004 ae300000 22100001 22310004 ae300000 22100001 22310004 ae300000 22100001 22310004 ae300000
  //   22100001 22310004 22100001 8020 2011003c 8e130000 8e340000 274402a 11000002 ae330000 ae140000
  //   2231fffc 1611fff8 102020 20020022 c 22100004 2011003c 1611fff2 20020032 c 20100000 22100001 102020
  //   20020022 c 22100002 102020 20020022 c 22100003 102020 20020022 c 22100004 102020 20020022 c 22100005
  //   102020 20020022 c 22100006 102020 20020022 c 22100007 102020 20020022 c 22100008 102020 20020022
  //   20020022 c 3e00008
  //   指令字
  //   数码管输出
  //   OP
  //   rs
  //   rd
  //   数码管输出应该用寄存器锁存，否则显示数据只能一闪而过
  //   Func
  //   rt
  //   JR
  //   Beq
  //   JMP
  //   Bne
  //   OP
  //   JAL
  //   Func
  //   Syscall
  //   MemToReg
  //   MemWrite
  //   AluOP
  //   AluSrcB
  //   RegWrite
  //   RegDst
  //   为方便自动评测，需要输出PC，IR，寄存器文件写入端口RDin，内存写入端口MDin等信号
  //   rs
  //   rt
  //   rd
  //   rs
  //   rt
  //   rd
  //   OP
  //   rs
  //   rt
  //   rd
endmodule

// 源寄存器使用情况
module \源寄存器使用情况  (
  input  OP0,
  input  OP1,
  input  OP2,
  input  OP3,
  input  OP4,
  input  OP5,
  input  F0,
  input  F1,
  input  F2,
  input  F3,
  input  F4,
  input  F5,
  output R1_Used,
  output R2_Used
);

  wire and_1_out, and_2_out, and_3_out, and_4_out, and_5_out, and_6_out, and_7_out, and_8_out, and_9_out,
       and_10_out, and_11_out, and_12_out, and_13_out, and_14_out, and_15_out, and_16_out, and_17_out,
       and_18_out, and_19_out, and_20_out, and_21_out, and_22_out, and_23_out, and_24_out, and_25_out,
       and_26_out, and_27_out, and_28_out, and_29_out, and_30_out, and_31_out, and_32_out, and_33_out,
       and_34_out, and_35_out, and_36_out, and_37_out, and_38_out, and_39_out, not_1_out, not_2_out,
       not_3_out, not_4_out, not_5_out, not_6_out, not_7_out, not_8_out, not_9_out, not_10_out, not_11_out,
       not_12_out, not_13_out, not_14_out, not_15_out, not_16_out, not_17_out, not_18_out, not_19_out,
       not_20_out, not_21_out, not_22_out, not_23_out, not_24_out, not_25_out, not_26_out, not_27_out,
       not_28_out, not_29_out, not_30_out, not_31_out, not_32_out, not_33_out, not_34_out, not_35_out,
       not_36_out, not_37_out, not_38_out, not_39_out, not_40_out, not_41_out, not_42_out, not_43_out,
       not_44_out, not_45_out, not_46_out, not_47_out, not_48_out, not_49_out, not_50_out, not_51_out,
       not_52_out, not_53_out, not_54_out, not_55_out, not_56_out, not_57_out, not_58_out, not_59_out,
       not_60_out, not_61_out, not_62_out, not_63_out, not_64_out, not_65_out, not_66_out, not_67_out,
       not_68_out, not_69_out, not_70_out, not_71_out, not_72_out, not_73_out, not_74_out, not_75_out,
       not_76_out, not_77_out, not_78_out, not_79_out, not_80_out, not_81_out, not_82_out, not_83_out,
       not_84_out, not_85_out, not_86_out, not_87_out, not_88_out, not_89_out, not_90_out, not_91_out,
       not_92_out, not_93_out, not_94_out, not_95_out, not_96_out, not_97_out, not_98_out, not_99_out,
       not_100_out, not_101_out, not_102_out, not_103_out, not_104_out, not_105_out, not_106_out,
       not_107_out, not_108_out, not_109_out, not_110_out, not_111_out, not_112_out, not_113_out,
       not_114_out, not_115_out, not_116_out, not_117_out, not_118_out, not_119_out, not_120_out,
       not_121_out, not_122_out, not_123_out, not_124_out, not_125_out, not_126_out, not_127_out,
       not_128_out, not_129_out, not_130_out, not_131_out, not_132_out, not_133_out, not_134_out,
       not_135_out, not_136_out, not_137_out, not_138_out, not_139_out, not_140_out, not_141_out,
       not_142_out, not_143_out, not_144_out, not_145_out, not_146_out, not_147_out, not_148_out,
       not_149_out, not_150_out, not_151_out, not_152_out, not_153_out, not_154_out, not_155_out,
       not_156_out, not_157_out, not_158_out, not_159_out, not_160_out, not_161_out, not_162_out,
       not_163_out, not_164_out, not_165_out, not_166_out, not_167_out, not_168_out, not_169_out,
       not_170_out, not_171_out, not_172_out, not_173_out, not_174_out, not_175_out, not_176_out,
       not_177_out, not_178_out, not_179_out, not_180_out, not_181_out, not_182_out, not_183_out,
       not_184_out, not_185_out, not_186_out, not_187_out, not_188_out, not_189_out, not_190_out,
       not_191_out, not_192_out, not_193_out, not_194_out, not_195_out, not_196_out, not_197_out,
       not_198_out, not_199_out, not_200_out, not_201_out, not_202_out, not_203_out, not_204_out,
       not_205_out, not_206_out, not_207_out, not_208_out, not_209_out, not_210_out, not_211_out,
       not_212_out, not_213_out, not_214_out, not_215_out, not_216_out, not_217_out, not_218_out,
       not_219_out, not_220_out, not_221_out, not_222_out, not_223_out, not_224_out, not_225_out,
       not_226_out, not_227_out, not_228_out, not_229_out, not_230_out, not_231_out, not_232_out,
       not_233_out, not_234_out, not_235_out, not_236_out, not_237_out, not_238_out, not_239_out,
       not_240_out, not_241_out, not_242_out, not_243_out, not_244_out, not_245_out, not_246_out,
       not_247_out, not_248_out, not_249_out, not_250_out, not_251_out, not_252_out, not_253_out,
       not_254_out, not_255_out, not_256_out, not_257_out, not_258_out, not_259_out, not_260_out,
       not_261_out, not_262_out, not_263_out, not_264_out, not_265_out, not_266_out, not_267_out,
       not_268_out, not_269_out, not_270_out, not_271_out, not_272_out, not_273_out, not_274_out,
       not_275_out, not_276_out, not_277_out, not_278_out, not_279_out, not_280_out, not_281_out,
       not_282_out, not_283_out, not_284_out, not_285_out, not_286_out, not_287_out, not_288_out,
       not_289_out, not_290_out, not_291_out, not_292_out;

  not not_1 (not_1_out, OP5);
  not not_2 (not_2_out, OP4);
  not not_3 (not_3_out, OP3);
  not not_4 (not_4_out, OP2);
  not not_5 (not_5_out, OP1);
  not not_6 (not_6_out, OP0);
  not not_7 (not_7_out, F4);
  not not_8 (not_8_out, F3);
  not not_9 (not_9_out, F2);
  not not_10 (not_10_out, F1);
  not not_11 (not_11_out, F0);
  not not_12 (not_12_out, OP5);
  not not_13 (not_13_out, OP4);
  not not_14 (not_14_out, OP3);
  not not_15 (not_15_out, OP2);
  not not_16 (not_16_out, OP1);
  not not_17 (not_17_out, OP0);
  not not_18 (not_18_out, F4);
  not not_19 (not_19_out, F3);
  not not_20 (not_20_out, F2);
  not not_21 (not_21_out, F1);
  not not_22 (not_22_out, OP5);
  not not_23 (not_23_out, OP4);
  not not_24 (not_24_out, OP3);
  not not_25 (not_25_out, OP2);
  not not_26 (not_26_out, OP1);
  not not_27 (not_27_out, OP0);
  not not_28 (not_28_out, F4);
  not not_29 (not_29_out, F3);
  not not_30 (not_30_out, F2);
  not not_31 (not_31_out, F0);
  not not_32 (not_32_out, OP5);
  not not_33 (not_33_out, OP4);
  not not_34 (not_34_out, OP3);
  not not_35 (not_35_out, OP2);
  not not_36 (not_36_out, OP1);
  not not_37 (not_37_out, OP0);
  not not_38 (not_38_out, F4);
  not not_39 (not_39_out, F3);
  not not_40 (not_40_out, F1);
  not not_41 (not_41_out, F0);
  not not_42 (not_42_out, OP5);
  not not_43 (not_43_out, OP4);
  not not_44 (not_44_out, OP3);
  not not_45 (not_45_out, OP2);
  not not_46 (not_46_out, OP1);
  not not_47 (not_47_out, OP0);
  not not_48 (not_48_out, F4);
  not not_49 (not_49_out, F3);
  not not_50 (not_50_out, F1);
  not not_51 (not_51_out, OP5);
  not not_52 (not_52_out, OP4);
  not not_53 (not_53_out, OP3);
  not not_54 (not_54_out, OP2);
  not not_55 (not_55_out, OP1);
  not not_56 (not_56_out, OP0);
  not not_57 (not_57_out, F4);
  not not_58 (not_58_out, F3);
  not not_59 (not_59_out, OP5);
  not not_60 (not_60_out, OP4);
  not not_61 (not_61_out, OP3);
  not not_62 (not_62_out, OP2);
  not not_63 (not_63_out, OP1);
  not not_64 (not_64_out, OP0);
  not not_65 (not_65_out, F4);
  not not_66 (not_66_out, F2);
  not not_67 (not_67_out, F0);
  not not_68 (not_68_out, OP5);
  not not_69 (not_69_out, OP4);
  not not_70 (not_70_out, OP3);
  not not_71 (not_71_out, OP2);
  not not_72 (not_72_out, OP1);
  not not_73 (not_73_out, OP0);
  not not_74 (not_74_out, F4);
  not not_75 (not_75_out, F2);
  not not_76 (not_76_out, OP5);
  not not_77 (not_77_out, OP4);
  not not_78 (not_78_out, OP3);
  not not_79 (not_79_out, OP2);
  not not_80 (not_80_out, OP1);
  not not_81 (not_81_out, OP0);
  not not_82 (not_82_out, F5);
  not not_83 (not_83_out, F4);
  not not_84 (not_84_out, F2);
  not not_85 (not_85_out, F1);
  not not_86 (not_86_out, F0);
  not not_87 (not_87_out, OP5);
  not not_88 (not_88_out, OP4);
  not not_89 (not_89_out, OP3);
  not not_90 (not_90_out, OP2);
  not not_91 (not_91_out, OP1);
  not not_92 (not_92_out, OP0);
  not not_93 (not_93_out, F5);
  not not_94 (not_94_out, F4);
  not not_95 (not_95_out, F1);
  not not_96 (not_96_out, F0);
  not not_97 (not_97_out, OP5);
  not not_98 (not_98_out, OP4);
  not not_99 (not_99_out, OP3);
  not not_100 (not_100_out, OP1);
  not not_101 (not_101_out, OP0);
  not not_102 (not_102_out, OP5);
  not not_103 (not_103_out, OP4);
  not not_104 (not_104_out, OP3);
  not not_105 (not_105_out, OP1);
  not not_106 (not_106_out, OP5);
  not not_107 (not_107_out, OP4);
  not not_108 (not_108_out, OP2);
  not not_109 (not_109_out, OP1);
  not not_110 (not_110_out, OP0);
  not not_111 (not_111_out, OP5);
  not not_112 (not_112_out, OP4);
  not not_113 (not_113_out, OP1);
  not not_114 (not_114_out, OP0);
  not not_115 (not_115_out, OP5);
  not not_116 (not_116_out, OP4);
  not not_117 (not_117_out, OP2);
  not not_118 (not_118_out, OP1);
  not not_119 (not_119_out, OP5);
  not not_120 (not_120_out, OP4);
  not not_121 (not_121_out, OP2);
  not not_122 (not_122_out, OP0);
  not not_123 (not_123_out, OP5);
  not not_124 (not_124_out, OP4);
  not not_125 (not_125_out, OP1);
  not not_126 (not_126_out, OP4);
  not not_127 (not_127_out, OP3);
  not not_128 (not_128_out, OP2);
  not not_129 (not_129_out, OP4);
  not not_130 (not_130_out, OP2);
  not not_131 (not_131_out, OP5);
  not not_132 (not_132_out, OP4);
  not not_133 (not_133_out, OP3);
  not not_134 (not_134_out, OP2);
  not not_135 (not_135_out, OP1);
  not not_136 (not_136_out, OP0);
  not not_137 (not_137_out, F5);
  not not_138 (not_138_out, F4);
  not not_139 (not_139_out, F3);
  not not_140 (not_140_out, F1);
  not not_141 (not_141_out, F0);
  not not_142 (not_142_out, OP5);
  not not_143 (not_143_out, OP4);
  not not_144 (not_144_out, OP0);
  not not_145 (not_145_out, OP4);
  not not_146 (not_146_out, OP3);
  not not_147 (not_147_out, OP1);
  not not_148 (not_148_out, OP5);
  not not_149 (not_149_out, OP4);
  not not_150 (not_150_out, OP3);
  not not_151 (not_151_out, OP2);
  not not_152 (not_152_out, OP1);
  not not_153 (not_153_out, OP5);
  not not_154 (not_154_out, OP4);
  not not_155 (not_155_out, OP3);
  not not_156 (not_156_out, OP2);
  not not_157 (not_157_out, OP1);
  not not_158 (not_158_out, OP0);
  not not_159 (not_159_out, F5);
  not not_160 (not_160_out, F4);
  not not_161 (not_161_out, F3);
  not not_162 (not_162_out, F2);
  not not_163 (not_163_out, F1);
  not not_164 (not_164_out, F0);
  not not_165 (not_165_out, OP5);
  not not_166 (not_166_out, OP4);
  not not_167 (not_167_out, OP3);
  not not_168 (not_168_out, OP2);
  not not_169 (not_169_out, OP1);
  not not_170 (not_170_out, OP0);
  not not_171 (not_171_out, F5);
  not not_172 (not_172_out, F4);
  not not_173 (not_173_out, F3);
  not not_174 (not_174_out, F2);
  not not_175 (not_175_out, OP5);
  not not_176 (not_176_out, OP4);
  not not_177 (not_177_out, OP3);
  not not_178 (not_178_out, OP2);
  not not_179 (not_179_out, OP1);
  not not_180 (not_180_out, OP0);
  not not_181 (not_181_out, F5);
  not not_182 (not_182_out, F4);
  not not_183 (not_183_out, F3);
  not not_184 (not_184_out, F2);
  not not_185 (not_185_out, F0);
  not not_186 (not_186_out, OP5);
  not not_187 (not_187_out, OP4);
  not not_188 (not_188_out, OP3);
  not not_189 (not_189_out, OP2);
  not not_190 (not_190_out, OP1);
  not not_191 (not_191_out, OP0);
  not not_192 (not_192_out, F4);
  not not_193 (not_193_out, F3);
  not not_194 (not_194_out, F2);
  not not_195 (not_195_out, F1);
  not not_196 (not_196_out, F0);
  not not_197 (not_197_out, OP5);
  not not_198 (not_198_out, OP4);
  not not_199 (not_199_out, OP3);
  not not_200 (not_200_out, OP2);
  not not_201 (not_201_out, OP1);
  not not_202 (not_202_out, OP0);
  not not_203 (not_203_out, F4);
  not not_204 (not_204_out, F3);
  not not_205 (not_205_out, F2);
  not not_206 (not_206_out, F1);
  not not_207 (not_207_out, OP5);
  not not_208 (not_208_out, OP4);
  not not_209 (not_209_out, OP3);
  not not_210 (not_210_out, OP2);
  not not_211 (not_211_out, OP1);
  not not_212 (not_212_out, OP0);
  not not_213 (not_213_out, F4);
  not not_214 (not_214_out, F3);
  not not_215 (not_215_out, F2);
  not not_216 (not_216_out, F0);
  not not_217 (not_217_out, OP5);
  not not_218 (not_218_out, OP4);
  not not_219 (not_219_out, OP3);
  not not_220 (not_220_out, OP2);
  not not_221 (not_221_out, OP1);
  not not_222 (not_222_out, OP0);
  not not_223 (not_223_out, F4);
  not not_224 (not_224_out, F3);
  not not_225 (not_225_out, F1);
  not not_226 (not_226_out, F0);
  not not_227 (not_227_out, OP5);
  not not_228 (not_228_out, OP4);
  not not_229 (not_229_out, OP3);
  not not_230 (not_230_out, OP2);
  not not_231 (not_231_out, OP1);
  not not_232 (not_232_out, OP0);
  not not_233 (not_233_out, F4);
  not not_234 (not_234_out, F3);
  not not_235 (not_235_out, F1);
  not not_236 (not_236_out, OP5);
  not not_237 (not_237_out, OP4);
  not not_238 (not_238_out, OP3);
  not not_239 (not_239_out, OP2);
  not not_240 (not_240_out, OP1);
  not not_241 (not_241_out, OP0);
  not not_242 (not_242_out, F4);
  not not_243 (not_243_out, F3);
  not not_244 (not_244_out, OP5);
  not not_245 (not_245_out, OP4);
  not not_246 (not_246_out, OP3);
  not not_247 (not_247_out, OP2);
  not not_248 (not_248_out, OP1);
  not not_249 (not_249_out, OP0);
  not not_250 (not_250_out, F4);
  not not_251 (not_251_out, F2);
  not not_252 (not_252_out, F0);
  not not_253 (not_253_out, OP5);
  not not_254 (not_254_out, OP4);
  not not_255 (not_255_out, OP3);
  not not_256 (not_256_out, OP2);
  not not_257 (not_257_out, OP1);
  not not_258 (not_258_out, OP0);
  not not_259 (not_259_out, F4);
  not not_260 (not_260_out, F2);
  not not_261 (not_261_out, OP5);
  not not_262 (not_262_out, OP4);
  not not_263 (not_263_out, OP3);
  not not_264 (not_264_out, OP2);
  not not_265 (not_265_out, OP1);
  not not_266 (not_266_out, OP0);
  not not_267 (not_267_out, F5);
  not not_268 (not_268_out, F4);
  not not_269 (not_269_out, F1);
  not not_270 (not_270_out, F0);
  not not_271 (not_271_out, OP5);
  not not_272 (not_272_out, OP4);
  not not_273 (not_273_out, OP3);
  not not_274 (not_274_out, OP1);
  not not_275 (not_275_out, OP0);
  not not_276 (not_276_out, OP5);
  not not_277 (not_277_out, OP4);
  not not_278 (not_278_out, OP3);
  not not_279 (not_279_out, OP1);
  not not_280 (not_280_out, OP4);
  not not_281 (not_281_out, OP2);
  not not_282 (not_282_out, OP5);
  not not_283 (not_283_out, OP4);
  not not_284 (not_284_out, OP3);
  not not_285 (not_285_out, OP2);
  not not_286 (not_286_out, OP1);
  not not_287 (not_287_out, OP0);
  not not_288 (not_288_out, F5);
  not not_289 (not_289_out, F4);
  not not_290 (not_290_out, F3);
  not not_291 (not_291_out, F1);
  not not_292 (not_292_out, F0);
  and and_1 (and_1_out, not_1_out, not_2_out, not_3_out, not_4_out, not_5_out, not_6_out, F5, not_7_out, not_8_out, not_9_out, not_10_out, not_11_out);
  and and_2 (and_2_out, not_12_out, not_13_out, not_14_out, not_15_out, not_16_out, not_17_out, F5, not_18_out, not_19_out, not_20_out, not_21_out, F0);
  and and_3 (and_3_out, not_22_out, not_23_out, not_24_out, not_25_out, not_26_out, not_27_out, F5, not_28_out, not_29_out, not_30_out, F1, not_31_out);
  and and_4 (and_4_out, not_32_out, not_33_out, not_34_out, not_35_out, not_36_out, not_37_out, F5, not_38_out, not_39_out, F2, not_40_out, not_41_out);
  and and_5 (and_5_out, not_42_out, not_43_out, not_44_out, not_45_out, not_46_out, not_47_out, F5, not_48_out, not_49_out, F2, not_50_out, F0);
  and and_6 (and_6_out, not_51_out, not_52_out, not_53_out, not_54_out, not_55_out, not_56_out, F5, not_57_out, not_58_out, F2, F1, F0);
  and and_7 (and_7_out, not_59_out, not_60_out, not_61_out, not_62_out, not_63_out, not_64_out, F5, not_65_out, F3, not_66_out, F1, not_67_out);
  and and_8 (and_8_out, not_68_out, not_69_out, not_70_out, not_71_out, not_72_out, not_73_out, F5, not_74_out, F3, not_75_out, F1, F0);
  and and_9 (and_9_out, not_76_out, not_77_out, not_78_out, not_79_out, not_80_out, not_81_out, not_82_out, not_83_out, F3, not_84_out, not_85_out, not_86_out);
  and and_10 (and_10_out, not_87_out, not_88_out, not_89_out, not_90_out, not_91_out, not_92_out, not_93_out, not_94_out, F3, F2, not_95_out, not_96_out);
  and and_11 (and_11_out, not_97_out, not_98_out, not_99_out, OP2, not_100_out, not_101_out);
  and and_12 (and_12_out, not_102_out, not_103_out, not_104_out, OP2, not_105_out, OP0);
  and and_13 (and_13_out, not_106_out, not_107_out, OP3, not_108_out, not_109_out, not_110_out);
  and and_14 (and_14_out, not_111_out, not_112_out, OP3, OP2, not_113_out, not_114_out);
  and and_15 (and_15_out, not_115_out, not_116_out, OP3, not_117_out, not_118_out, OP0);
  and and_16 (and_16_out, not_119_out, not_120_out, OP3, not_121_out, OP1, not_122_out);
  and and_17 (and_17_out, not_123_out, not_124_out, OP3, OP2, not_125_out, OP0);
  and and_18 (and_18_out, OP5, not_126_out, not_127_out, not_128_out, OP1, OP0);
  and and_19 (and_19_out, OP5, not_129_out, OP3, not_130_out, OP1, OP0);
  and and_20 (and_20_out, not_131_out, not_132_out, not_133_out, not_134_out, not_135_out, not_136_out, not_137_out, not_138_out, not_139_out, F2, not_140_out, not_141_out);
  and and_21 (and_21_out, not_142_out, not_143_out, OP3, OP2, OP1, not_144_out);
  and and_22 (and_22_out, OP5, not_145_out, not_146_out, OP2, not_147_out, OP0);
  and and_23 (and_23_out, not_148_out, not_149_out, not_150_out, not_151_out, not_152_out, OP0);
  and and_24 (and_24_out, not_153_out, not_154_out, not_155_out, not_156_out, not_157_out, not_158_out, not_159_out, not_160_out, not_161_out, not_162_out, not_163_out, not_164_out);
  and and_25 (and_25_out, not_165_out, not_166_out, not_167_out, not_168_out, not_169_out, not_170_out, not_171_out, not_172_out, not_173_out, not_174_out, F1, F0);
  and and_26 (and_26_out, not_175_out, not_176_out, not_177_out, not_178_out, not_179_out, not_180_out, not_181_out, not_182_out, not_183_out, not_184_out, F1, not_185_out);
  and and_27 (and_27_out, not_186_out, not_187_out, not_188_out, not_189_out, not_190_out, not_191_out, F5, not_192_out, not_193_out, not_194_out, not_195_out, not_196_out);
  and and_28 (and_28_out, not_197_out, not_198_out, not_199_out, not_200_out, not_201_out, not_202_out, F5, not_203_out, not_204_out, not_205_out, not_206_out, F0);
  and and_29 (and_29_out, not_207_out, not_208_out, not_209_out, not_210_out, not_211_out, not_212_out, F5, not_213_out, not_214_out, not_215_out, F1, not_216_out);
  and and_30 (and_30_out, not_217_out, not_218_out, not_219_out, not_220_out, not_221_out, not_222_out, F5, not_223_out, not_224_out, F2, not_225_out, not_226_out);
  and and_31 (and_31_out, not_227_out, not_228_out, not_229_out, not_230_out, not_231_out, not_232_out, F5, not_233_out, not_234_out, F2, not_235_out, F0);
  and and_32 (and_32_out, not_236_out, not_237_out, not_238_out, not_239_out, not_240_out, not_241_out, F5, not_242_out, not_243_out, F2, F1, F0);
  and and_33 (and_33_out, not_244_out, not_245_out, not_246_out, not_247_out, not_248_out, not_249_out, F5, not_250_out, F3, not_251_out, F1, not_252_out);
  and and_34 (and_34_out, not_253_out, not_254_out, not_255_out, not_256_out, not_257_out, not_258_out, F5, not_259_out, F3, not_260_out, F1, F0);
  and and_35 (and_35_out, not_261_out, not_262_out, not_263_out, not_264_out, not_265_out, not_266_out, not_267_out, not_268_out, F3, F2, not_269_out, not_270_out);
  and and_36 (and_36_out, not_271_out, not_272_out, not_273_out, OP2, not_274_out, not_275_out);
  and and_37 (and_37_out, not_276_out, not_277_out, not_278_out, OP2, not_279_out, OP0);
  and and_38 (and_38_out, OP5, not_280_out, OP3, not_281_out, OP1, OP0);
  and and_39 (and_39_out, not_282_out, not_283_out, not_284_out, not_285_out, not_286_out, not_287_out, not_288_out, not_289_out, not_290_out, F2, not_291_out, not_292_out);
  or or_1 (R1_Used, and_1_out, and_2_out, and_3_out, and_4_out, and_5_out, and_6_out, and_7_out, and_8_out, and_9_out, and_10_out, and_11_out, and_12_out, and_13_out, and_14_out, and_15_out, and_16_out, and_17_out, and_18_out, and_19_out, and_20_out, and_21_out, and_22_out, and_23_out);
  or or_2 (R2_Used, and_24_out, and_25_out, and_26_out, and_27_out, and_28_out, and_29_out, and_30_out, and_31_out, and_32_out, and_33_out, and_34_out, and_35_out, and_36_out, and_37_out, and_38_out, and_39_out);
endmodule

module \数据相关检测  (
  input  [5:0] OP,
  input  [4:0] EX_WriteReg_num,
  input  EX_RegWrite,
  input  [4:0] MEM_WriteReg_num,
  input  MEM_RegWrite,
  input  [5:0] Func,
  input  [4:0] ID_R1_num,
  input  [4:0] ID_R2_num,
  output \数据相关 
);

  wire and_1_out, and_2_out, and_3_out, and_4_out, comparator_1_eq, comparator_2_eq, comparator_3_eq,
       comparator_4_eq, comparator_5_eq, comparator_6_eq, not_1_out, not_2_out, \源寄存器使用情况_1_r1_used ,
       \源寄存器使用情况_1_r2_used ;

  \源寄存器使用情况  \u_源寄存器使用情况_1  (
    .OP0(OP[0]), .OP1(OP[1]), .OP2(OP[2]), .OP3(OP[3]), .OP4(OP[4]), .OP5(OP[5]), .F0(Func[0]), .F1(Func[1]),
    .F2(Func[2]), .F3(Func[3]), .F4(Func[4]), .F5(Func[5]), .R1_Used(\源寄存器使用情况_1_r1_used ),
    .R2_Used(\源寄存器使用情况_1_r2_used ));
  Comparator #(.width(5), .mode("twosComplement")) comparator_1 (
    .a(ID_R1_num), .b({5{1'b0}}), .eq(comparator_1_eq));  // open: gt, lt
  Comparator #(.width(5), .mode("twosComplement")) comparator_2 (
    .a(ID_R2_num), .b({5{1'b0}}), .eq(comparator_2_eq));  // open: gt, lt
  not not_1 (not_1_out, comparator_1_eq);
  not not_2 (not_2_out, comparator_2_eq);
  Comparator #(.width(5), .mode("twosComplement")) comparator_3 (
    .a(ID_R1_num), .b(MEM_WriteReg_num), .eq(comparator_3_eq));  // open: gt, lt
  Comparator #(.width(5), .mode("twosComplement")) comparator_4 (
    .a(ID_R2_num), .b(MEM_WriteReg_num), .eq(comparator_4_eq));  // open: gt, lt
  Comparator #(.width(5), .mode("twosComplement")) comparator_5 (
    .a(ID_R1_num), .b(EX_WriteReg_num), .eq(comparator_5_eq));  // open: gt, lt
  Comparator #(.width(5), .mode("twosComplement")) comparator_6 (
    .a(ID_R2_num), .b(EX_WriteReg_num), .eq(comparator_6_eq));  // open: gt, lt
  and and_1 (and_1_out, not_1_out, EX_RegWrite, comparator_5_eq, \源寄存器使用情况_1_r1_used );
  and and_2 (and_2_out, not_1_out, MEM_RegWrite, comparator_3_eq, \源寄存器使用情况_1_r1_used );
  and and_3 (and_3_out, not_2_out, EX_RegWrite, comparator_6_eq, \源寄存器使用情况_1_r2_used );
  and and_4 (and_4_out, not_2_out, MEM_RegWrite, comparator_4_eq, \源寄存器使用情况_1_r2_used );
  or or_1 (\数据相关 , and_1_out, and_2_out, and_3_out, and_4_out);

  // Other names for the same wires on the sheet: OP_CODE[5:0] = OP
endmodule

module \重定向流水线  (
  output RegWrite,
  output MemWrite,
  output [31:0] PC,
  output [31:0] IR,
  output [31:0] RDin,
  output [31:0] MDin
);

  wire and_1_out, and_2_out, and_3_out, and_4_out, and_5_out, and_6_out, and_7_out, and_8_out, and_9_out,
       and_10_out, and_11_out, and_12_out, and_13_out, CLK, comparator_1_eq, comparator_2_eq,
       comparator_3_eq, comparator_4_eq, comparator_5_eq, comparator_6_eq, comparator_7_eq, comparator_8_eq,
       comparator_9_eq, ex_mem_1_out_22, ex_mem_1_out_23, ex_mem_1_out_24, \ex_mem_1_传输状态out_表明当前传输数据有效 ,
       EX_MEMTOREG, EX_syscall, Go, id_ex_1_out_31, id_ex_1_out_32, id_ex_1_out_33, id_ex_1_out_34,
       id_ex_1_out_35, id_ex_1_out_36, id_ex_1_out_37, id_ex_1_out_40, \id_ex_1_传输状态out_表明当前传输数据有效 , IR1,
       IR2, IR3, LOADUSE, MEM_RegWrite, mem_wb_1_out_19, mem_wb_1_out_20, mem_wb_1_out_21, mem_wb_1_out_22,
       MEMTOREG, mips_alu_1_equal, nand_1_out, not_1_out, not_2_out, not_3_out, or_1_out, or_2_out, or_3_out,
       or_4_out, RST, SignedExt, syscall, W1, W2, W3, WB_RegWrite, \单周期硬布线控制器_1_alu_src , \单周期硬布线控制器_1_beq ,
       \单周期硬布线控制器_1_bne , \单周期硬布线控制器_1_jal , \单周期硬布线控制器_1_jmp , \单周期硬布线控制器_1_jr , \单周期硬布线控制器_1_memtoreg ,
       \单周期硬布线控制器_1_memwrite , \单周期硬布线控制器_1_regdst , \单周期硬布线控制器_1_regwrite , \源寄存器使用情况_1_r1_used ,
       \源寄存器使用情况_1_r2_used ;
  wire [1:0] EX_FWA, EX_FWB, multiplexer_11_out, multiplexer_12_out, multiplexer_13_out, multiplexer_14_out,
       SA, SB;
  wire [3:0] id_ex_1_out_41, \单周期硬布线控制器_1_alu_op ;
  wire [4:0] ID_R1_num, ID_R2_num, MEM_WriteReg_num, multiplexer_6_out, multiplexer_8_out,
       multiplexer_17_out, multiplexer_19_out, WB_WriteReg_num;
  wire [5:0] FUNC, OP_CODE;
  wire [15:0] \LoadUse次数 , \总周期数 , \无条件分支数 , \条件分支成功数 ;
  wire [25:6] if_id_1_out_6;
  wire [26:21] id_ex_1_out_26_2;
  wire [27:0] adder_2_out;
  wire [31:0] A, adder_1_out, adder_3_out, adder_4_out, B, bit_extender_1_out, bit_extender_2_out,
       ex_mem_1_out_14, EX_PC, EXR1, EXR2, id_ex_1_out_24, id_ex_1_out_30, ID_PC, LedData, MEM_PC,
       mem_wb_1_out_13, MEMALU, mips_alu_1_result, mips_regifile_1_r1, mips_regifile_1_r2, multiplexer_1_out,
       multiplexer_2_out, multiplexer_3_out, multiplexer_7_out, multiplexer_9_out, multiplexer_22_out,
       ram_1_data, shifter_1_out, WB_PC, WBALU, WBRD;
  wire [31:2] id_ex_1_out_26;

  Clock #(.highDuration(1), .lowDuration(1)) clock_1 (.out(CLK));
  Button _1 (.out(IR1));
  Button _2 (.out(IR2));
  Button _3 (.out(IR3));
  Button \u_总复位  (.out(RST));
  Register #(.width(32), .trigger("rising"), .Select("low")) u_PC (
    .D(multiplexer_1_out), .en(and_1_out), .Q(PC), .clk(CLK), .clr(RST));
  Multiplexer #(.select(1), .width(32), .disabled("Z"), .enable("false")) multiplexer_1 (
    .in0(multiplexer_3_out), .in1(multiplexer_2_out), .out(multiplexer_1_out), .sel(id_ex_1_out_31));
  Multiplexer #(.select(1), .width(32), .disabled("Z"), .enable("false")) multiplexer_2 (
    .in0({id_ex_1_out_26, 2'b00}), .in1(A), .out(multiplexer_2_out), .sel(id_ex_1_out_32));
  Button \u_继续运行  (.out(Go));
  LED #(.active("true")) led_1 (.in(W1));
  LED #(.active("true")) led_2 (.in(W2));
  LED #(.active("true")) led_3 (.in(W3));
  Hex_Digit_Display hex_digit_display_1 (.value(LedData[31:28]));  // open: dp
  Adder #(.width(32)) adder_1 (.a(PC), .b(32'h4), .out(adder_1_out));  // open: cin, cout
  Multiplexer #(.select(1), .width(32), .disabled("Z"), .enable("false")) multiplexer_3 (
    .in0(adder_1_out), .in1(adder_3_out), .out(multiplexer_3_out), .sel(or_4_out));
  Hex_Digit_Display hex_digit_display_2 (.value(LedData[27:24]));  // open: dp
  Hex_Digit_Display hex_digit_display_3 (.value(LedData[23:20]));  // open: dp
  ROM #(.addrWidth(10), .dataWidth(32), .Select("high")) rom_1 (.addr(PC[11:2]), .data(IR));
  Hex_Digit_Display hex_digit_display_4 (.value(LedData[15:12]));  // open: dp
  Hex_Digit_Display hex_digit_display_5 (.value(LedData[19:16]));  // open: dp
  IF_ID if_id_1 (
    .CLK(CLK), .out_6({OP_CODE, if_id_1_out_6, FUNC}), .\同步清零_气泡_高电平有效 (or_3_out),
    .\使能端_低电平有效_stall_高电平有效 (and_1_out), .in_5(PC), .out_8(ID_PC), .in_1(IR));  // open: 传输状态Out_表明当前传输数据有效
  Hex_Digit_Display hex_digit_display_6 (.value(LedData[11:8]));  // open: dp
  Hex_Digit_Display hex_digit_display_7 (.value(LedData[7:4]));  // open: dp
  and and_1 (and_1_out, nand_1_out, ~LOADUSE);  // AND_Gate
  Hex_Digit_Display hex_digit_display_8 (.value(LedData[3:0]));  // open: dp
  // Probe on \总周期数 
  Multiplexer #(.select(1), .width(5), .disabled("Z"), .enable("false")) multiplexer_4 (
    .in0(if_id_1_out_6[25:21]), .in1(5'b00010), .out(ID_R1_num), .sel(syscall));
  Multiplexer #(.select(1), .width(5), .disabled("Z"), .enable("false")) multiplexer_5 (
    .in0(if_id_1_out_6[20:16]), .in1(5'b00100), .out(ID_R2_num), .sel(syscall));
  Multiplexer #(.select(1), .width(5), .disabled("Z"), .enable("false")) multiplexer_6 (
    .in0(mem_wb_1_out_13[20:16]), .in1(mem_wb_1_out_13[15:11]), .out(multiplexer_6_out), .sel(mem_wb_1_out_20));
  assign bit_extender_1_out = {{16{if_id_1_out_6[15]}}, {if_id_1_out_6[15:6], FUNC}};  // Bit_Extender bit_extender_1
  assign bit_extender_2_out = {{16{1'b0}}, {if_id_1_out_6[15:6], FUNC}};  // Bit_Extender bit_extender_2
  Multiplexer #(.select(1), .width(32), .disabled("Z"), .enable("false")) multiplexer_7 (
    .in0(bit_extender_2_out), .in1(bit_extender_1_out), .out(multiplexer_7_out), .sel(SignedExt));
  \源寄存器使用情况  \u_源寄存器使用情况_1  (
    .OP0(OP_CODE[0]), .OP1(OP_CODE[1]), .OP2(OP_CODE[2]), .OP3(OP_CODE[3]), .OP4(OP_CODE[4]),
    .OP5(OP_CODE[5]), .F0(FUNC[0]), .F1(FUNC[1]), .F2(FUNC[2]), .F3(FUNC[3]), .F4(FUNC[4]), .F5(FUNC[5]),
    .R1_Used(\源寄存器使用情况_1_r1_used ), .R2_Used(\源寄存器使用情况_1_r2_used ));
  Multiplexer #(.select(1), .width(5), .disabled("Z"), .enable("false")) multiplexer_8 (
    .in0(multiplexer_6_out), .in1({5{1'b1}}), .out(multiplexer_8_out), .sel(mem_wb_1_out_21));
  Shifter #(.width(32), .shift("ll")) shifter_1 (.in(multiplexer_7_out), .\dist (5'b00010), .out(shifter_1_out));
  or or_1 (or_1_out, nand_1_out, ~mem_wb_1_out_22);  // OR_Gate
  \单周期硬布线控制器  \u_单周期硬布线控制器_1  (
    .Func(FUNC), .OP(OP_CODE), .ALU_OP(\单周期硬布线控制器_1_alu_op ), .MemToReg(\单周期硬布线控制器_1_memtoreg ),
    .MemWrite(\单周期硬布线控制器_1_memwrite ), .ALU_SRC(\单周期硬布线控制器_1_alu_src ), .RegWrite(\单周期硬布线控制器_1_regwrite ),
    .SysCALL(syscall), .SignedExt(SignedExt), .RegDst(\单周期硬布线控制器_1_regdst ), .JR(\单周期硬布线控制器_1_jr ),
    .JMP(\单周期硬布线控制器_1_jmp ), .Beq(\单周期硬布线控制器_1_beq ), .JAL(\单周期硬布线控制器_1_jal ), .Bne(\单周期硬布线控制器_1_bne ));
  Comparator #(.width(32), .mode("twosComplement")) comparator_1 (
    .a(A), .b(32'h22), .eq(comparator_1_eq));  // open: gt, lt
  Counter #(.width(16), .max('hffff), .ongoal("wrap"), .trigger("rising"), .behavior("old")) counter_1 (
    .count(or_1_out), .Q(\总周期数 ), .clk(CLK), .clr(RST));  // open: load, D, carry, preset
  MIPS_Regifile mips_regifile_1 (
    .Din(RDin), .Clk(CLK), .R1(mips_regifile_1_r1), .R2(mips_regifile_1_r2), .WE(RegWrite),
    .W_num(multiplexer_8_out), .R1_num(ID_R1_num), .R2_num(ID_R2_num));
  and and_2 (and_2_out, comparator_1_eq, EX_syscall);
  and and_3 (and_3_out, EX_syscall, ~comparator_1_eq);  // AND_Gate
  Comparator #(.width(5), .mode("twosComplement")) comparator_2 (
    .a(ID_R1_num), .b({5{1'b0}}), .eq(comparator_2_eq));  // open: gt, lt
  Comparator #(.width(5), .mode("twosComplement")) comparator_3 (
    .a(ID_R1_num), .b(WB_WriteReg_num), .eq(comparator_3_eq));  // open: gt, lt
  Comparator #(.width(5), .mode("twosComplement")) comparator_4 (
    .a(ID_R2_num), .b({5{1'b0}}), .eq(comparator_4_eq));  // open: gt, lt
  Comparator #(.width(5), .mode("twosComplement")) comparator_5 (
    .a(ID_R2_num), .b(WB_WriteReg_num), .eq(comparator_5_eq));  // open: gt, lt
  nand nand_1 (nand_1_out, and_3_out, ~Go);  // NAND_Gate
  not not_1 (not_1_out, comparator_2_eq);
  Comparator #(.width(5), .mode("twosComplement")) comparator_6 (
    .a(ID_R1_num), .b(WB_WriteReg_num), .eq(comparator_6_eq));  // open: gt, lt
  not not_2 (not_2_out, comparator_4_eq);
  Comparator #(.width(5), .mode("twosComplement")) comparator_7 (
    .a(ID_R2_num), .b(WB_WriteReg_num), .eq(comparator_7_eq));  // open: gt, lt
  or or_2 (or_2_out, or_3_out, LOADUSE);
  ID_EX id_ex_1 (
    .CLK(CLK), .in_5({OP_CODE, if_id_1_out_6, FUNC}), .in_6(ID_PC), .in_7(mips_regifile_1_r1),
    .in_8(mips_regifile_1_r2), .in_10(\单周期硬布线控制器_1_jmp ), .in_11(\单周期硬布线控制器_1_jr ),
    .in_12(\单周期硬布线控制器_1_jal ), .in_13(\单周期硬布线控制器_1_alu_src ), .in_14(\单周期硬布线控制器_1_bne ),
    .in_15(\单周期硬布线控制器_1_beq ), .in_16(\单周期硬布线控制器_1_memwrite ), .in_17(\单周期硬布线控制器_1_regwrite ),
    .in_18(\单周期硬布线控制器_1_memtoreg ), .in_20(\单周期硬布线控制器_1_alu_op ), .out_24(id_ex_1_out_24),
    .\传输状态Out_表明当前传输数据有效 (\id_ex_1_传输状态out_表明当前传输数据有效 ), .out_26({id_ex_1_out_26_2, id_ex_1_out_26[27:2]}),
    .out_27(EX_PC), .out_28(EXR1), .out_29(EXR2), .out_31(id_ex_1_out_31), .out_32(id_ex_1_out_32),
    .out_33(id_ex_1_out_33), .out_34(id_ex_1_out_34), .out_35(id_ex_1_out_35), .out_36(id_ex_1_out_36),
    .out_37(id_ex_1_out_37), .out_38(MEM_RegWrite), .out_39(EX_MEMTOREG), .out_41(id_ex_1_out_41),
    .\同步清零_气泡_高电平有效 (or_2_out), .\使能端_低电平有效_stall_高电平有效 (nand_1_out), .in_1(multiplexer_7_out),
    .in_19(\单周期硬布线控制器_1_regdst ), .out_40(id_ex_1_out_40), .in_9(shifter_1_out), .out_30(id_ex_1_out_30),
    .in_21(syscall), .out_42(EX_syscall), .in_22(SA), .out_43(EX_FWA), .in_23(SB), .out_44(EX_FWB));
  Register #(.width(32), .trigger("rising"), .Select("low")) register_1 (
    .D(B), .en(and_2_out), .Q(LedData), .clk(CLK), .clr(RST));
  Comparator #(.width(5), .mode("twosComplement")) comparator_8 (
    .a(ID_R1_num), .b(MEM_WriteReg_num), .eq(comparator_8_eq));  // open: gt, lt
  Comparator #(.width(5), .mode("twosComplement")) comparator_9 (
    .a(ID_R2_num), .b(MEM_WriteReg_num), .eq(comparator_9_eq));  // open: gt, lt
  Adder #(.width(32)) adder_2 (.a(EX_PC), .b(32'h4), .out({id_ex_1_out_26[31:28], adder_2_out}));  // open: cin, cout
  Multiplexer #(.select(1), .width(32), .disabled("Z"), .enable("false")) multiplexer_9 (
    .in0(B), .in1(id_ex_1_out_24), .out(multiplexer_9_out), .sel(id_ex_1_out_34));
  Adder #(.width(32)) adder_3 (
    .a({id_ex_1_out_26[31:28], adder_2_out}), .b(id_ex_1_out_30), .out(adder_3_out));  // open: cin, cout
  and and_4 (and_4_out, not_1_out, MEM_RegWrite, comparator_8_eq, \源寄存器使用情况_1_r1_used );
  and and_5 (and_5_out, not_1_out, WB_RegWrite, comparator_3_eq, \源寄存器使用情况_1_r1_used );
  and and_6 (and_6_out, not_1_out, WB_RegWrite, MEMTOREG, comparator_6_eq, \源寄存器使用情况_1_r1_used );
  and and_7 (and_7_out, not_2_out, MEM_RegWrite, comparator_9_eq, \源寄存器使用情况_1_r2_used );
  and and_8 (and_8_out, not_2_out, WB_RegWrite, comparator_5_eq, \源寄存器使用情况_1_r2_used );
  and and_9 (and_9_out, not_2_out, WB_RegWrite, MEMTOREG, comparator_7_eq, \源寄存器使用情况_1_r2_used );
  or or_3 (or_3_out, id_ex_1_out_31, or_4_out);
  and and_10 (and_10_out, mips_alu_1_equal, id_ex_1_out_36);
  and and_11 (and_11_out, id_ex_1_out_35, ~mips_alu_1_equal);  // AND_Gate
  MIPS_ALU mips_alu_1 (
    .X(A), .Y(multiplexer_9_out), .AluOP(id_ex_1_out_41), .Equal(mips_alu_1_equal),
    .Result(mips_alu_1_result), .shamt(id_ex_1_out_26[12:8]));  // open: Result_2
  Counter #(.width(16), .max('hffff), .ongoal("wrap"), .trigger("rising"), .behavior("old")) counter_2 (
    .count(or_4_out), .Q(\条件分支成功数 ), .clk(CLK), .clr(RST));  // open: load, D, carry, preset
  Counter #(.width(16), .max('hffff), .ongoal("wrap"), .trigger("rising"), .behavior("old")) counter_3 (
    .count(id_ex_1_out_31), .Q(\无条件分支数 ), .clk(CLK), .clr(RST));  // open: load, D, carry, preset
  Multiplexer #(.select(2), .width(32), .disabled("Z"), .enable("false")) multiplexer_10 (
    .in0(EXR1), .in1(MEMALU), .in2(WBALU), .in3(WBRD), .out(A), .sel(EX_FWA));
  Multiplexer #(.select(1), .width(2), .disabled("Z"), .enable("false")) multiplexer_11 (
    .in0(2'b00), .in1(2'b10), .out(multiplexer_11_out), .sel(and_5_out));
  Multiplexer #(.select(1), .width(2), .disabled("Z"), .enable("false")) multiplexer_12 (
    .in0(2'b00), .in1(2'b10), .out(multiplexer_12_out), .sel(and_8_out));
  or or_4 (or_4_out, and_10_out, and_11_out);
  and and_12 (and_12_out, EX_MEMTOREG, and_4_out);
  Multiplexer #(.select(1), .width(2), .disabled("Z"), .enable("false")) multiplexer_13 (
    .in0(multiplexer_11_out), .in1(2'b11), .out(multiplexer_13_out), .sel(and_6_out));
  and and_13 (and_13_out, EX_MEMTOREG, and_7_out);
  Multiplexer #(.select(1), .width(2), .disabled("Z"), .enable("false")) multiplexer_14 (
    .in0(multiplexer_12_out), .in1(2'b11), .out(multiplexer_14_out), .sel(and_9_out));
  // Probe on ID_PC[11:0]
  // Probe on PC[11:0]
  Multiplexer #(.select(1), .width(2), .disabled("Z"), .enable("false")) multiplexer_15 (
    .in0(multiplexer_13_out), .in1(2'b01), .out(SA), .sel(and_4_out));
  Multiplexer #(.select(1), .width(2), .disabled("Z"), .enable("false")) multiplexer_16 (
    .in0(multiplexer_14_out), .in1(2'b01), .out(SB), .sel(and_7_out));
  // Probe on EX_PC[11:0]
  Multiplexer #(.select(1), .width(5), .disabled("Z"), .enable("false")) multiplexer_17 (
    .in0(id_ex_1_out_26[22:18]), .in1(id_ex_1_out_26[17:13]), .out(multiplexer_17_out), .sel(id_ex_1_out_40));
  or or_5 (LOADUSE, and_12_out, and_13_out);
  // Probe on MEM_PC[11:0]
  // Probe on WB_PC[11:0]
  EX_MEM ex_mem_1 (
    .in_1({id_ex_1_out_26_2, id_ex_1_out_26[27:2]}), .CLK(CLK), .in_4(EX_PC), .in_5(mips_alu_1_result),
    .in_6(B), .in_7(id_ex_1_out_37), .in_8(MEM_RegWrite), .in_9(EX_MEMTOREG), .in_10(id_ex_1_out_40),
    .out_14(ex_mem_1_out_14), .\传输状态Out_表明当前传输数据有效 (\ex_mem_1_传输状态out_表明当前传输数据有效 ), .out_16(MEM_PC),
    .out_17(MEMALU), .out_18(MDin), .out_19(MemWrite), .out_20(WB_RegWrite), .out_21(MEMTOREG),
    .out_22(ex_mem_1_out_22), .\使能端_低电平有效_stall_高电平有效 (\id_ex_1_传输状态out_表明当前传输数据有效 ), .in_11(id_ex_1_out_33),
    .out_23(ex_mem_1_out_23), .in_13(EX_syscall), .out_24(ex_mem_1_out_24));  // open: 同步清零_气泡_高电平有效
  Multiplexer #(.select(1), .width(5), .disabled("Z"), .enable("false")) multiplexer_18 (
    .in0(multiplexer_17_out), .in1({5{1'b1}}), .out(MEM_WriteReg_num), .sel(id_ex_1_out_33));
  not not_3 (not_3_out, MemWrite);
  Multiplexer #(.select(1), .width(5), .disabled("Z"), .enable("false")) multiplexer_19 (
    .in0(ex_mem_1_out_14[20:16]), .in1(ex_mem_1_out_14[15:11]), .out(multiplexer_19_out),
    .sel(ex_mem_1_out_22));
  // Probe on \总周期数 
  // Probe on \无条件分支数 
  // Probe on \条件分支成功数 
  // Probe on \LoadUse次数 
  RAM #(.addrWidth(10), .dataWidth(32), .bus("separate"), .Select("high")) ram_1 (
    .addr(MEMALU[11:2]), .din(MDin), .data(ram_1_data), .str(MemWrite), .clk(CLK), .ld(not_3_out), .clr(RST));  // open: sel
  Multiplexer #(.select(2), .width(32), .disabled("Z"), .enable("false")) multiplexer_20 (
    .in0(EXR2), .in1(MEMALU), .in2(WBALU), .in3(WBRD), .out(B), .sel(EX_FWB));
  Multiplexer #(.select(1), .width(5), .disabled("Z"), .enable("false")) multiplexer_21 (
    .in0(multiplexer_19_out), .in1({5{1'b1}}), .out(WB_WriteReg_num), .sel(ex_mem_1_out_23));
  MEM_WB mem_wb_1 (
    .in_1(ex_mem_1_out_14), .CLK(CLK), .in_4(MEM_PC), .in_5(MEMALU), .in_6(ram_1_data), .in_7(WB_RegWrite),
    .in_8(MEMTOREG), .in_9(ex_mem_1_out_22), .out_13(mem_wb_1_out_13), .out_15(WB_PC), .out_16(WBALU),
    .out_17(WBRD), .out_18(RegWrite), .out_19(mem_wb_1_out_19), .out_20(mem_wb_1_out_20),
    .\使能端_低电平有效_stall_高电平有效 (\ex_mem_1_传输状态out_表明当前传输数据有效 ), .in_10(ex_mem_1_out_23),
    .out_21(mem_wb_1_out_21), .in_12(ex_mem_1_out_24), .out_22(mem_wb_1_out_22));  // open: 传输状态Out_表明当前传输数据有效, 同步清零_气泡_高电平有效
  Counter #(.width(16), .max('hffff), .ongoal("wrap"), .trigger("rising"), .behavior("old")) counter_4 (
    .count(LOADUSE), .Q(\LoadUse次数 ), .clk(CLK), .clr(RST));  // open: load, D, carry, preset
  Multiplexer #(.select(1), .width(32), .disabled("Z"), .enable("false")) multiplexer_22 (
    .in0(WBALU), .in1(WBRD), .out(multiplexer_22_out), .sel(mem_wb_1_out_19));
  Multiplexer #(.select(1), .width(32), .disabled("Z"), .enable("false")) multiplexer_23 (
    .in0(multiplexer_22_out), .in1(adder_4_out), .out(RDin), .sel(mem_wb_1_out_21));
  Adder #(.width(32)) adder_4 (.a(WB_PC), .b(32'h4), .out(adder_4_out));  // open: cin, cout

  // Other names for the same wires on the sheet: IF_PC[31:0] = PC

  // Notes on the sheet:
  //   中断源
  //   中断等待指示
  //   总复位信号应将除ROM以外所有存储组件全部清零
  //   指令存储器
  //   指令字
  //   contents of rom_1 (hex, n*v repeats v):
  //   20110001 8000c05 20110001 20120002 20130003 8000c09 20110001 20120002 20130003 8000c0d 20110001
  //   20120002 20130003 8000c11 20110001 20120002 20130003 c000cb8 20100001 20110001 118fc0 112020
  //   20020022 c 118882 12200001 8000c15 112020 20020022 c 20110001 118880 112020 20020022 c 12200001
  //   8000c1f 20110001 118fc0 112020 20020022 c 1188c3 112020 20020022 c 118903 112020 20020022 c 118903
  //   112020 20020022 c 118903 112020 20020022 c 118903 112020 20020022 c 118903 112020 20020022 c 118903
  //   112020 20020022 c 118903 112020 20020022 c 20100001 109fc0 139fc3 8021 2012000c 24160003 26100001
  //   3210000f 20080008 20090001 139900 2709825 132020 20020022 c 1094022 1500fff9 22100001 2018000f
  //   2188024 108700 20080008 20090001 139902 2709825 132021 20020022 c 1094022 1500fff9 108702 2c9b022
  //   12c00001 8000c50 4020 1084027 84400 3508ffff 82021 20020022 c 2010ffff 20110000 ae300000 22100001
  //   22310004 ae300000 22100001 22310004 ae300000 22100001 22310004 ae300000 22100001 22310004 ae300000
  //   22100001 22310004 ae300000 22100001 22310004 ae300000 22100001 22310004 ae300000 22100001 22310004
  //   ae300000 22100001 22310004 ae300000 22100001 22310004 ae300000 22100001 22310004 ae300000 22100001
  //   22310004 ae300000 22100001 22310004 ae300000 22100001 22310004 ae300000 22100001 22310004 ae300000
  //   22100001 22310004 22100001 8020 2011003c 8e130000 8e340000 274402a 11000002 ae330000 ae140000
  //   2231fffc 1611fff8 102020 20020022 c 22100004 2011003c 1611fff2 20020032 c 20100000 22100001 102020
  //   20020022 c 22100002 102020 20020022 c 22100003 102020 20020022 c 22100004 102020 20020022 c 22100005
  //   102020 20020022 c 22100006 102020 20020022 c 22100007 102020 20020022 c 22100008 102020 20020022
  //   20020022 c 3e00008
  //   数码管输出
  //   数码管输出应该用寄存器锁存，否则显示数据只能一闪而过
  //   OP
  //   Func
  //   rs
  //   rt
  //   rd
  //   JMP
  //   JR
  //   OP
  //   Func
  //   Beq
  //   Bne
  //   MemToReg
  //   MemWrite
  //   AluOP
  //   AluSrcB
  //   RegWrite
  //   JAL
  //   RegDst
  //   Syscall
  //   为方便自动评测，需要输出PC，IR，寄存器文件写入端口RDin，内存写入端口MDin等信号
  //   OP
  //   rs
  //   rt
  //   rd
  //   OP
  //   rs
  //   rt
  //   rd
  //   OP
  //   rs
  //   rt
  //   rd
endmodule

module \扩展指令  (
  output RegWrite,
  output MemWrite,
  output [31:0] PC,
  output [31:0] IR,
  output [31:0] RDin,
  output [31:0] MDin
);

  wire and_1_out, and_2_out, and_3_out, and_4_out, and_5_out, and_6_out, and_7_out, and_8_out, and_9_out,
       and_10_out, and_11_out, and_13_out, and_14_out, and_15_out, BGEZ, CLK, comparator_1_eq,
       comparator_2_eq, comparator_3_eq, comparator_4_eq, comparator_5_eq, comparator_6_eq, comparator_7_eq,
       comparator_8_eq, comparator_9_eq, comparator_10_eq, comparator_11_eq, comparator_12_eq,
       comparator_12_gt, comparator_13_eq, comparator_14_eq, comparator_15_eq, ex_mem_1_out_22,
       ex_mem_1_out_23, ex_mem_1_out_24, \ex_mem_1_传输状态out_表明当前传输数据有效 , EX_MEMTOREG, EX_syscall, Go,
       id_ex_1_out_31, id_ex_1_out_32, id_ex_1_out_33, id_ex_1_out_34, id_ex_1_out_35, id_ex_1_out_36,
       id_ex_1_out_37, id_ex_1_out_40, \id_ex_1_传输状态out_表明当前传输数据有效 , IR1, IR2, IR3, LOADUSE, MEM_RegWrite,
       mem_wb_1_out_19, mem_wb_1_out_20, mem_wb_1_out_21, mem_wb_1_out_22, MEMTOREG, mips_alu_1_equal,
       nand_1_out, not_1_out, not_2_out, not_3_out, or_1_out, or_2_out, or_3_out, or_4_out, or_5_out, RST,
       SignedExt, SLLV, syscall, W1, W2, W3, WB_RegWrite, \单周期硬布线控制器_1_alu_src , \单周期硬布线控制器_1_beq ,
       \单周期硬布线控制器_1_bne , \单周期硬布线控制器_1_jal , \单周期硬布线控制器_1_jmp , \单周期硬布线控制器_1_jr , \单周期硬布线控制器_1_memtoreg ,
       \单周期硬布线控制器_1_memwrite , \单周期硬布线控制器_1_regdst , \单周期硬布线控制器_1_regwrite , \源寄存器使用情况_1_r1_used ,
       \源寄存器使用情况_1_r2_used ;
  wire [1:0] EX_FWA, EX_FWB, multiplexer_11_out, multiplexer_12_out, multiplexer_13_out, multiplexer_14_out,
       SA, SB;
  wire [3:0] id_ex_1_out_41, \单周期硬布线控制器_1_alu_op ;
  wire [4:0] ex_mem_1_out_14_3, ex_mem_1_out_14_4, ex_mem_1_out_14_5, id_ex_1_out_26_2, ID_R1_num, ID_R2_num,
       MEM_WriteReg_num, multiplexer_6_out, multiplexer_8_out, multiplexer_17_out, multiplexer_20_out, SHAMT,
       WB_WriteReg_num;
  wire [5:0] ex_mem_1_out_14, ex_mem_1_out_14_6, FUNC, id_ex_1_out_26_3, OP_CODE;
  wire [10:6] ex_mem_1_out_14_2;
  wire [15:0] \LoadUse次数 , multiplexer_21_out, shifter_1_out, \总周期数 , \无条件分支数 , \条件分支成功数 ;
  wire [25:0] id_ex_1_out_26;
  wire [25:6] if_id_1_out_6;
  wire [31:0] A, adder_1_out, adder_2_out, adder_3_out, adder_4_out, B, bit_extender_1_out,
       bit_extender_2_out, bit_extender_3_out, EX_PC, EXR1, EXR2, id_ex_1_out_24, id_ex_1_out_30, ID_PC,
       LedData, MEM_PC, mem_wb_1_out_13, MEMALU, mips_alu_1_result, mips_regifile_1_r1, mips_regifile_1_r2,
       multiplexer_1_out, multiplexer_2_out, multiplexer_3_out, multiplexer_7_out, multiplexer_9_out,
       multiplexer_24_out, multiplexer_25_out, RDOUT, WB_PC, WBALU, WBRD;

  Clock #(.highDuration(1), .lowDuration(1)) clock_1 (.out(CLK));
  Button _1 (.out(IR1));
  Button _2 (.out(IR2));
  Button _3 (.out(IR3));
  Button \u_总复位  (.out(RST));
  Register #(.width(32), .trigger("rising"), .Select("low")) u_PC (
    .D(multiplexer_1_out), .en(and_1_out), .Q(PC), .clk(CLK), .clr(RST));
  Multiplexer #(.select(1), .width(32), .disabled("Z"), .enable("false")) multiplexer_1 (
    .in0(multiplexer_3_out), .in1(multiplexer_2_out), .out(multiplexer_1_out), .sel(id_ex_1_out_31));
  Multiplexer #(.select(1), .width(32), .disabled("Z"), .enable("false")) multiplexer_2 (
    .in0({adder_2_out[31:28], id_ex_1_out_26[25:21], id_ex_1_out_26_2, id_ex_1_out_26[15:0], 2'b00}),
    .in1(A), .out(multiplexer_2_out), .sel(id_ex_1_out_32));
  Button \u_继续运行  (.out(Go));
  LED #(.active("true")) led_1 (.in(W1));
  LED #(.active("true")) led_2 (.in(W2));
  LED #(.active("true")) led_3 (.in(W3));
  Hex_Digit_Display hex_digit_display_1 (.value(LedData[31:28]));  // open: dp
  Adder #(.width(32)) adder_1 (.a(PC), .b(32'h4), .out(adder_1_out));  // open: cin, cout
  Multiplexer #(.select(1), .width(32), .disabled("Z"), .enable("false")) multiplexer_3 (
    .in0(adder_1_out), .in1(adder_3_out), .out(multiplexer_3_out), .sel(or_5_out));
  Hex_Digit_Display hex_digit_display_2 (.value(LedData[23:20]));  // open: dp
  Hex_Digit_Display hex_digit_display_3 (.value(LedData[27:24]));  // open: dp
  ROM #(.addrWidth(10), .dataWidth(32), .Select("high")) rom_1 (.addr(PC[11:2]), .data(IR));
  Hex_Digit_Display hex_digit_display_4 (.value(LedData[19:16]));  // open: dp
  Hex_Digit_Display hex_digit_display_5 (.value(LedData[15:12]));  // open: dp
  IF_ID if_id_1 (
    .CLK(CLK), .out_6({OP_CODE, if_id_1_out_6, FUNC}), .\同步清零_气泡_高电平有效 (or_4_out),
    .\使能端_低电平有效_stall_高电平有效 (and_1_out), .in_5(PC), .out_8(ID_PC), .in_1(IR));  // open: 传输状态Out_表明当前传输数据有效
  Hex_Digit_Display hex_digit_display_6 (.value(LedData[7:4]));  // open: dp
  Hex_Digit_Display hex_digit_display_7 (.value(LedData[11:8]));  // open: dp
  and and_1 (and_1_out, nand_1_out, ~LOADUSE);  // AND_Gate
  Hex_Digit_Display hex_digit_display_8 (.value(LedData[3:0]));  // open: dp
  // Probe on \总周期数 
  Multiplexer #(.select(1), .width(5), .disabled("Z"), .enable("false")) multiplexer_4 (
    .in0(if_id_1_out_6[25:21]), .in1(5'b00010), .out(ID_R1_num), .sel(syscall));
  Multiplexer #(.select(1), .width(5), .disabled("Z"), .enable("false")) multiplexer_5 (
    .in0(if_id_1_out_6[20:16]), .in1(5'b00100), .out(ID_R2_num), .sel(syscall));
  Multiplexer #(.select(1), .width(5), .disabled("Z"), .enable("false")) multiplexer_6 (
    .in0(mem_wb_1_out_13[20:16]), .in1(mem_wb_1_out_13[15:11]), .out(multiplexer_6_out), .sel(mem_wb_1_out_20));
  assign bit_extender_1_out = {{16{if_id_1_out_6[15]}}, {if_id_1_out_6[15:6], FUNC}};  // Bit_Extender bit_extender_1
  assign bit_extender_2_out = {{16{1'b0}}, {if_id_1_out_6[15:6], FUNC}};  // Bit_Extender bit_extender_2
  Multiplexer #(.select(1), .width(32), .disabled("Z"), .enable("false")) multiplexer_7 (
    .in0(bit_extender_2_out), .in1(bit_extender_1_out), .out(multiplexer_7_out), .sel(SignedExt));
  \源寄存器使用情况  \u_源寄存器使用情况_1  (
    .OP0(OP_CODE[0]), .OP1(OP_CODE[1]), .OP2(OP_CODE[2]), .OP3(OP_CODE[3]), .OP4(OP_CODE[4]),
    .OP5(OP_CODE[5]), .F0(FUNC[0]), .F1(FUNC[1]), .F2(FUNC[2]), .F3(FUNC[3]), .F4(FUNC[4]), .F5(FUNC[5]),
    .R1_Used(\源寄存器使用情况_1_r1_used ), .R2_Used(\源寄存器使用情况_1_r2_used ));
  Multiplexer #(.select(1), .width(5), .disabled("Z"), .enable("false")) multiplexer_8 (
    .in0(multiplexer_6_out), .in1({5{1'b1}}), .out(multiplexer_8_out), .sel(mem_wb_1_out_21));
  Shifter #(.width(16), .shift("ll")) shifter_1 (
    .in({if_id_1_out_6[15:6], FUNC}), .\dist (4'b0010), .out(shifter_1_out));
  or or_1 (or_1_out, nand_1_out, ~mem_wb_1_out_22);  // OR_Gate
  \单周期硬布线控制器  \u_单周期硬布线控制器_1  (
    .Func(FUNC), .OP(OP_CODE), .ALU_OP(\单周期硬布线控制器_1_alu_op ), .MemToReg(\单周期硬布线控制器_1_memtoreg ),
    .MemWrite(\单周期硬布线控制器_1_memwrite ), .ALU_SRC(\单周期硬布线控制器_1_alu_src ), .RegWrite(\单周期硬布线控制器_1_regwrite ),
    .SysCALL(syscall), .SignedExt(SignedExt), .RegDst(\单周期硬布线控制器_1_regdst ), .JR(\单周期硬布线控制器_1_jr ),
    .JMP(\单周期硬布线控制器_1_jmp ), .Beq(\单周期硬布线控制器_1_beq ), .JAL(\单周期硬布线控制器_1_jal ), .Bne(\单周期硬布线控制器_1_bne ));
  assign bit_extender_3_out = {{16{shifter_1_out[15]}}, shifter_1_out};  // Bit_Extender bit_extender_3
  Comparator #(.width(32), .mode("twosComplement")) comparator_1 (
    .a(A), .b(32'h22), .eq(comparator_1_eq));  // open: gt, lt
  Counter #(.width(16), .max('hffff), .ongoal("wrap"), .trigger("rising"), .behavior("old")) counter_1 (
    .count(or_1_out), .Q(\总周期数 ), .clk(CLK), .clr(RST));  // open: load, D, carry, preset
  MIPS_Regifile mips_regifile_1 (
    .Din(RDin), .Clk(CLK), .R1(mips_regifile_1_r1), .R2(mips_regifile_1_r2), .WE(RegWrite),
    .W_num(multiplexer_8_out), .R1_num(ID_R1_num), .R2_num(ID_R2_num));
  and and_2 (and_2_out, comparator_1_eq, EX_syscall);
  and and_3 (and_3_out, EX_syscall, ~comparator_1_eq);  // AND_Gate
  Comparator #(.width(5), .mode("twosComplement")) comparator_2 (
    .a(ID_R1_num), .b({5{1'b0}}), .eq(comparator_2_eq));  // open: gt, lt
  Comparator #(.width(5), .mode("twosComplement")) comparator_3 (
    .a(ID_R1_num), .b(WB_WriteReg_num), .eq(comparator_3_eq));  // open: gt, lt
  Comparator #(.width(5), .mode("twosComplement")) comparator_4 (
    .a(ID_R2_num), .b({5{1'b0}}), .eq(comparator_4_eq));  // open: gt, lt
  Comparator #(.width(5), .mode("twosComplement")) comparator_5 (
    .a(ID_R2_num), .b(WB_WriteReg_num), .eq(comparator_5_eq));  // open: gt, lt
  nand nand_1 (nand_1_out, and_3_out, ~Go);  // NAND_Gate
  not not_1 (not_1_out, comparator_2_eq);
  Comparator #(.width(5), .mode("twosComplement")) comparator_6 (
    .a(ID_R1_num), .b(WB_WriteReg_num), .eq(comparator_6_eq));  // open: gt, lt
  not not_2 (not_2_out, comparator_4_eq);
  Comparator #(.width(5), .mode("twosComplement")) comparator_7 (
    .a(ID_R2_num), .b(WB_WriteReg_num), .eq(comparator_7_eq));  // open: gt, lt
  or or_2 (or_2_out, or_4_out, LOADUSE);
  ID_EX id_ex_1 (
    .CLK(CLK), .in_5({OP_CODE, if_id_1_out_6, FUNC}), .in_6(ID_PC), .in_7(mips_regifile_1_r1),
    .in_8(mips_regifile_1_r2), .in_10(\单周期硬布线控制器_1_jmp ), .in_11(\单周期硬布线控制器_1_jr ),
    .in_12(\单周期硬布线控制器_1_jal ), .in_13(\单周期硬布线控制器_1_alu_src ), .in_14(\单周期硬布线控制器_1_bne ),
    .in_15(\单周期硬布线控制器_1_beq ), .in_16(\单周期硬布线控制器_1_memwrite ), .in_17(\单周期硬布线控制器_1_regwrite ),
    .in_18(\单周期硬布线控制器_1_memtoreg ), .in_20(\单周期硬布线控制器_1_alu_op ), .out_24(id_ex_1_out_24),
    .\传输状态Out_表明当前传输数据有效 (\id_ex_1_传输状态out_表明当前传输数据有效 ),
    .out_26({id_ex_1_out_26_3, id_ex_1_out_26[25:21], id_ex_1_out_26_2, id_ex_1_out_26[15:0]}),
    .out_27(EX_PC), .out_28(EXR1), .out_29(EXR2), .out_31(id_ex_1_out_31), .out_32(id_ex_1_out_32),
    .out_33(id_ex_1_out_33), .out_34(id_ex_1_out_34), .out_35(id_ex_1_out_35), .out_36(id_ex_1_out_36),
    .out_37(id_ex_1_out_37), .out_38(MEM_RegWrite), .out_39(EX_MEMTOREG), .out_41(id_ex_1_out_41),
    .\同步清零_气泡_高电平有效 (or_2_out), .\使能端_低电平有效_stall_高电平有效 (nand_1_out), .in_1(multiplexer_7_out),
    .in_19(\单周期硬布线控制器_1_regdst ), .out_40(id_ex_1_out_40), .in_9(bit_extender_3_out),
    .out_30(id_ex_1_out_30), .in_21(syscall), .out_42(EX_syscall), .in_22(SA), .out_43(EX_FWA), .in_23(SB),
    .out_44(EX_FWB));
  Register #(.width(32), .trigger("rising"), .Select("low")) register_1 (
    .D(B), .en(and_2_out), .Q(LedData), .clk(CLK), .clr(RST));
  Counter #(.width(16), .max('hffff), .ongoal("wrap"), .trigger("rising"), .behavior("old")) counter_2 (
    .count(id_ex_1_out_31), .Q(\无条件分支数 ), .clk(CLK), .clr(RST));  // open: load, D, carry, preset
  Comparator #(.width(5), .mode("twosComplement")) comparator_8 (
    .a(ID_R1_num), .b(MEM_WriteReg_num), .eq(comparator_8_eq));  // open: gt, lt
  Comparator #(.width(5), .mode("twosComplement")) comparator_9 (
    .a(ID_R2_num), .b(MEM_WriteReg_num), .eq(comparator_9_eq));  // open: gt, lt
  Adder #(.width(32)) adder_2 (.a(EX_PC), .b(32'h4), .out(adder_2_out));  // open: cin, cout
  Multiplexer #(.select(1), .width(32), .disabled("Z"), .enable("false")) multiplexer_9 (
    .in0(B), .in1(id_ex_1_out_24), .out(multiplexer_9_out), .sel(id_ex_1_out_34));
  Adder #(.width(32)) adder_3 (.a(adder_2_out), .b(id_ex_1_out_30), .out(adder_3_out));  // open: cin, cout
  Counter #(.width(16), .max('hffff), .ongoal("wrap"), .trigger("rising"), .behavior("old")) counter_3 (
    .count(or_5_out), .Q(\条件分支成功数 ), .clk(CLK), .clr(RST));  // open: load, D, carry, preset
  Comparator #(.width(6), .mode("twosComplement")) comparator_10 (
    .a(id_ex_1_out_26_3), .b(6'b000001), .eq(comparator_10_eq));  // open: gt, lt
  Comparator #(.width(5), .mode("twosComplement")) comparator_11 (
    .a(5'b00001), .b(id_ex_1_out_26_2), .eq(comparator_11_eq));  // open: gt, lt
  and and_4 (and_4_out, not_1_out, MEM_RegWrite, comparator_8_eq, \源寄存器使用情况_1_r1_used );
  and and_5 (and_5_out, not_1_out, WB_RegWrite, comparator_3_eq, \源寄存器使用情况_1_r1_used );
  and and_6 (and_6_out, not_1_out, WB_RegWrite, MEMTOREG, comparator_6_eq, \源寄存器使用情况_1_r1_used );
  and and_7 (and_7_out, not_2_out, MEM_RegWrite, comparator_9_eq, \源寄存器使用情况_1_r2_used );
  and and_8 (and_8_out, not_2_out, WB_RegWrite, comparator_5_eq, \源寄存器使用情况_1_r2_used );
  and and_9 (and_9_out, not_2_out, WB_RegWrite, MEMTOREG, comparator_7_eq, \源寄存器使用情况_1_r2_used );
  or or_3 (or_3_out, comparator_12_gt, comparator_12_eq);
  Comparator #(.width(32), .mode("twosComplement")) comparator_12 (
    .a(A), .b({32{1'b0}}), .gt(comparator_12_gt), .eq(comparator_12_eq));  // open: lt
  or or_4 (or_4_out, id_ex_1_out_31, or_5_out);
  and and_10 (and_10_out, mips_alu_1_equal, id_ex_1_out_36);
  and and_11 (and_11_out, id_ex_1_out_35, ~mips_alu_1_equal);  // AND_Gate
  MIPS_ALU mips_alu_1 (
    .X(A), .Y(multiplexer_9_out), .AluOP(id_ex_1_out_41), .Equal(mips_alu_1_equal),
    .Result(mips_alu_1_result), .shamt(SHAMT));  // open: Result_2
  and and_12 (BGEZ, comparator_10_eq, comparator_11_eq);
  Multiplexer #(.select(2), .width(32), .disabled("Z"), .enable("false")) multiplexer_10 (
    .in0(EXR1), .in1(MEMALU), .in2(WBALU), .in3(WBRD), .out(A), .sel(EX_FWA));
  Multiplexer #(.select(1), .width(2), .disabled("Z"), .enable("false")) multiplexer_11 (
    .in0(2'b00), .in1(2'b10), .out(multiplexer_11_out), .sel(and_5_out));
  Multiplexer #(.select(1), .width(2), .disabled("Z"), .enable("false")) multiplexer_12 (
    .in0(2'b00), .in1(2'b10), .out(multiplexer_12_out), .sel(and_8_out));
  and and_13 (and_13_out, BGEZ, or_3_out);
  or or_5 (or_5_out, and_10_out, and_13_out, and_11_out);
  and and_14 (and_14_out, EX_MEMTOREG, and_4_out);
  Multiplexer #(.select(1), .width(2), .disabled("Z"), .enable("false")) multiplexer_13 (
    .in0(multiplexer_11_out), .in1(2'b11), .out(multiplexer_13_out), .sel(and_6_out));
  and and_15 (and_15_out, EX_MEMTOREG, and_7_out);
  Multiplexer #(.select(1), .width(2), .disabled("Z"), .enable("false")) multiplexer_14 (
    .in0(multiplexer_12_out), .in1(2'b11), .out(multiplexer_14_out), .sel(and_9_out));
  // Probe on ID_PC[11:0]
  // Probe on PC[11:0]
  Multiplexer #(.select(1), .width(2), .disabled("Z"), .enable("false")) multiplexer_15 (
    .in0(multiplexer_13_out), .in1(2'b01), .out(SA), .sel(and_4_out));
  Multiplexer #(.select(1), .width(2), .disabled("Z"), .enable("false")) multiplexer_16 (
    .in0(multiplexer_14_out), .in1(2'b01), .out(SB), .sel(and_7_out));
  // Probe on EX_PC[11:0]
  Multiplexer #(.select(1), .width(5), .disabled("Z"), .enable("false")) multiplexer_17 (
    .in0(id_ex_1_out_26_2), .in1(id_ex_1_out_26[15:11]), .out(multiplexer_17_out), .sel(id_ex_1_out_40));
  Comparator #(.width(6), .mode("twosComplement")) comparator_13 (
    .a(id_ex_1_out_26_3), .b({6{1'b0}}), .eq(comparator_13_eq));  // open: gt, lt
  Comparator #(.width(6), .mode("twosComplement")) comparator_14 (
    .a(id_ex_1_out_26[5:0]), .b(6'b000100), .eq(comparator_14_eq));  // open: gt, lt
  or or_6 (LOADUSE, and_14_out, and_15_out);
  // Probe on MEM_PC[11:0]
  // Probe on WB_PC[11:0]
  EX_MEM ex_mem_1 (
    .in_1({id_ex_1_out_26_3, id_ex_1_out_26[25:21], id_ex_1_out_26_2, id_ex_1_out_26[15:0]}), .CLK(CLK),
    .in_4(EX_PC), .in_5(mips_alu_1_result), .in_6(B), .in_7(id_ex_1_out_37), .in_8(MEM_RegWrite),
    .in_9(EX_MEMTOREG), .in_10(id_ex_1_out_40),
    .out_14({ex_mem_1_out_14_6, ex_mem_1_out_14_5, ex_mem_1_out_14_4, ex_mem_1_out_14_3, ex_mem_1_out_14_2, ex_mem_1_out_14}),
    .\传输状态Out_表明当前传输数据有效 (\ex_mem_1_传输状态out_表明当前传输数据有效 ), .out_16(MEM_PC), .out_17(MEMALU), .out_18(MDin),
    .out_19(MemWrite), .out_20(WB_RegWrite), .out_21(MEMTOREG), .out_22(ex_mem_1_out_22),
    .\使能端_低电平有效_stall_高电平有效 (\id_ex_1_传输状态out_表明当前传输数据有效 ), .in_11(id_ex_1_out_33), .out_23(ex_mem_1_out_23),
    .in_13(EX_syscall), .out_24(ex_mem_1_out_24));  // open: 同步清零_气泡_高电平有效
  Multiplexer #(.select(1), .width(5), .disabled("Z"), .enable("false")) multiplexer_18 (
    .in0(multiplexer_17_out), .in1({5{1'b1}}), .out(MEM_WriteReg_num), .sel(id_ex_1_out_33));
  and and_16 (SLLV, comparator_13_eq, comparator_14_eq);
  Multiplexer #(.select(1), .width(5), .disabled("Z"), .enable("false")) multiplexer_19 (
    .in0(id_ex_1_out_26[10:6]), .in1(A[4:0]), .out(SHAMT), .sel(SLLV));
  not not_3 (not_3_out, MemWrite);
  Comparator #(.width(6), .mode("twosComplement")) comparator_15 (
    .a(ex_mem_1_out_14_6), .b(6'b100101), .eq(comparator_15_eq));  // open: gt, lt
  Multiplexer #(.select(1), .width(5), .disabled("Z"), .enable("false")) multiplexer_20 (
    .in0(ex_mem_1_out_14_4), .in1(ex_mem_1_out_14_3), .out(multiplexer_20_out), .sel(ex_mem_1_out_22));
  // Probe on \总周期数 
  // Probe on \无条件分支数 
  // Probe on \条件分支成功数 
  // Probe on \LoadUse次数 
  RAM #(.addrWidth(10), .dataWidth(32), .bus("separate"), .Select("high")) ram_1 (
    .addr(MEMALU[11:2]), .din(MDin), .data(RDOUT), .str(MemWrite), .clk(CLK), .ld(not_3_out), .clr(RST));  // open: sel
  Multiplexer #(.select(1), .width(16), .disabled("Z"), .enable("false")) multiplexer_21 (
    .in0(RDOUT[15:0]), .in1(RDOUT[31:16]), .out(multiplexer_21_out), .sel(MEMALU[1]));
  Multiplexer #(.select(2), .width(32), .disabled("Z"), .enable("false")) multiplexer_22 (
    .in0(EXR2), .in1(MEMALU), .in2(WBALU), .in3(WBRD), .out(B), .sel(EX_FWB));
  Multiplexer #(.select(1), .width(5), .disabled("Z"), .enable("false")) multiplexer_23 (
    .in0(multiplexer_20_out), .in1({5{1'b1}}), .out(WB_WriteReg_num), .sel(ex_mem_1_out_23));
  MEM_WB mem_wb_1 (
    .in_1({ex_mem_1_out_14_6, ex_mem_1_out_14_5, ex_mem_1_out_14_4, ex_mem_1_out_14_3, ex_mem_1_out_14_2, ex_mem_1_out_14}),
    .CLK(CLK), .in_4(MEM_PC), .in_5(MEMALU), .in_6(multiplexer_24_out), .in_7(WB_RegWrite), .in_8(MEMTOREG),
    .in_9(ex_mem_1_out_22), .out_13(mem_wb_1_out_13), .out_15(WB_PC), .out_16(WBALU), .out_17(WBRD),
    .out_18(RegWrite), .out_19(mem_wb_1_out_19), .out_20(mem_wb_1_out_20),
    .\使能端_低电平有效_stall_高电平有效 (\ex_mem_1_传输状态out_表明当前传输数据有效 ), .in_10(ex_mem_1_out_23),
    .out_21(mem_wb_1_out_21), .in_12(ex_mem_1_out_24), .out_22(mem_wb_1_out_22));  // open: 传输状态Out_表明当前传输数据有效, 同步清零_气泡_高电平有效
  Multiplexer #(.select(1), .width(32), .disabled("Z"), .enable("false")) multiplexer_24 (
    .in0(RDOUT), .in1({{16{1'b0}}, multiplexer_21_out}), .out(multiplexer_24_out), .sel(comparator_15_eq));
  Counter #(.width(16), .max('hffff), .ongoal("wrap"), .trigger("rising"), .behavior("old")) counter_4 (
    .count(LOADUSE), .Q(\LoadUse次数 ), .clk(CLK), .clr(RST));  // open: load, D, carry, preset
  Multiplexer #(.select(1), .width(32), .disabled("Z"), .enable("false")) multiplexer_25 (
    .in0(WBALU), .in1(WBRD), .out(multiplexer_25_out), .sel(mem_wb_1_out_19));
  Multiplexer #(.select(1), .width(32), .disabled("Z"), .enable("false")) multiplexer_26 (
    .in0(multiplexer_25_out), .in1(adder_4_out), .out(RDin), .sel(mem_wb_1_out_21));
  Adder #(.width(32)) adder_4 (.a(WB_PC), .b(32'h4), .out(adder_4_out));  // open: cin, cout

  // Other names for the same wires on the sheet: IF_PC[31:0] = PC

  // Notes on the sheet:
  //   中断源
  //   中断等待指示
  //   总复位信号应将除ROM以外所有存储组件全部清零
  //   指令存储器
  //   指令字
  //   contents of rom_1 (hex, n*v repeats v):
  //   20110001 8000c05 20110001 20120002 20130003 8000c09 20110001 20120002 20130003 8000c0d 20110001
  //   20120002 20130003 8000c11 20110001 20120002 20130003 c000cf8 20100001 20110001 118fc0 112020
  //   20020022 c 118882 12200001 8000c15 112020 20020022 c 20110001 118880 112020 20020022 c 12200001
  //   8000c1f 20110001 118fc0 112020 20020022 c 1188c3 112020 20020022 c 118903 112020 20020022 c 118903
  //   112020 20020022 c 118903 112020 20020022 c 118903 112020 20020022 c 118903 112020 20020022 c 118903
  //   112020 20020022 c 118903 112020 20020022 c 20100001 109fc0 139fc3 8021 2012000c 24160003 26100001
  //   3210000f 20080008 20090001 139900 2709825 132020 20020022 c 1094022 1500fff9 22100001 2018000f
  //   2188024 108700 20080008 20090001 139902 2709825 132021 20020022 c 1094022 1500fff9 108702 2c9b022
  //   12c00001 8000c50 4020 1084027 84400 3508ffff 82021 20020022 c 2010ffff 20110000 ae300000 22100001
  //   22310004 ae300000 22100001 22310004 ae300000 22100001 22310004 ae300000 22100001 22310004 ae300000
  //   22100001 22310004 ae300000 22100001 22310004 ae300000 22100001 22310004 ae300000 22100001 22310004
  //   ae300000 22100001 22310004 ae300000 22100001 22310004 ae300000 22100001 22310004 ae300000 22100001
  //   22310004 ae300000 22100001 22310004 ae300000 22100001 22310004 ae300000 22100001 22310004 ae300000
  //   22100001 22310004 22100001 8020 2011003c 8e130000 8e340000 274402a 11000002 ae330000 ae140000
  //   2231fffc 1611fff8 102020 20020022 c 22100004 2011003c 1611fff2 20020032 c 20080001 20090003 20110876
  //   112020 20020022 c 200b0008 1118804 1318804 112020 20020022 c 216bffff 1560fff9 2002000a c 2008ffff
  //   20117777 112020 20020022 c 200b0010 3a31ffff 112020 20020022 c 216bffff 1560fffa 2002000a c 20090000
  //   200b0010 34118483 20120404 118c00 129400 36318281 22520404 ad310000 2328820 21290004 216bffff
  //   1560fffb 200b0020 20090000 95310000 112020 20020022 c 21290002 216bffff 1560fff9 2002000a c 2011000f
  //   112020 20020022 c 2231ffff 621fffb 2002000a c 2002000a c 20100000 22100001 102020 20020022 c
  //   22100002 102020 20020022 c 22100003 102020 20020022 c 22100004 102020 20020022 c 22100005 102020
  //   20020022 c 22100006 102020 20020022 c 22100007 102020 20020022 c 22100008 102020 20020022 20020022 c
  //   3e00008
  //   数码管输出
  //   数码管输出应该用寄存器锁存，否则显示数据只能一闪而过
  //   OP
  //   Func
  //   rs
  //   rt
  //   rd
  //   JMP
  //   JR
  //   OP
  //   Func
  //   Beq
  //   Bne
  //   MemToReg
  //   MemWrite
  //   AluOP
  //   AluSrcB
  //   RegWrite
  //   JAL
  //   RegDst
  //   Syscall
  //   为方便自动评测，需要输出PC，IR，寄存器文件写入端口RDin，内存写入端口MDin等信号
  //   OP
  //   rs
  //   rt
  //   rd
  //   OP
  //   rs
  //   rt
  //   rd
  //   OP
  //   rs
  //   rt
  //   rd
endmodule

module \中断按键参考电路  (
  input  \同步清零信号 ,
  output \与中断屏蔽位与 
);

  wire \_1号中断_out , and_1_out, clock_1_out, d_ff_1_q, or_1_out, or_2_out;

  Clock #(.highDuration(1), .lowDuration(1)) clock_1 (.out(clock_1_out));
  Button \_1号中断  (.out(\_1号中断_out ));
  LED #(.active("true")) \_1号中断等待指示灯  (.in(or_1_out));
  or or_1 (or_1_out, \与中断屏蔽位与 , d_ff_1_q);
  D_Flip_Flop #(.trigger("rising"), .Pre_Clr_Positions("LEGACY"), .NegatePresetClear("false"), .enable("true"), .NewFFLayout("false")) d_ff_1 (
    .clk(\_1号中断_out ), .D(1'b1), .Q(d_ff_1_q), .reset(\与中断屏蔽位与 ));  // open: Qn, preset, en
  or or_2 (or_2_out, d_ff_1_q, \与中断屏蔽位与 );
  and and_1 (and_1_out, or_2_out, ~\同步清零信号 );  // AND_Gate
  D_Flip_Flop #(.trigger("rising"), .Pre_Clr_Positions("LEGACY"), .NegatePresetClear("false"), .enable("true"), .NewFFLayout("false")) IR1 (
    .clk(clock_1_out), .D(and_1_out), .Q(\与中断屏蔽位与 ));  // open: Qn, preset, en, reset

  // Notes on the sheet:
  //   中断信号采样参考电路
  //   Reset 
endmodule

module IF_ID (
  input  [31:0] in_1,
  input  CLK,
  input  \同步清零_气泡_高电平有效 ,
  input  \使能端_低电平有效_stall_高电平有效 ,
  input  [31:0] in_5,
  output [31:0] out_6,
  output \传输状态Out_表明当前传输数据有效 ,
  output [31:0] out_8
);

  wire [31:0] multiplexer_1_out, multiplexer_2_out;

  Multiplexer #(.select(1), .width(32), .disabled("Z"), .enable("false")) multiplexer_1 (
    .in0(in_1), .in1({32{1'b0}}), .out(multiplexer_1_out), .sel(\同步清零_气泡_高电平有效 ));
  Multiplexer #(.select(1), .width(32), .disabled("Z"), .enable("false")) multiplexer_2 (
    .in0(in_5), .in1({32{1'b0}}), .out(multiplexer_2_out), .sel(\同步清零_气泡_高电平有效 ));
  Pull_Resistor #(.pull(0)) pull_resistor_1 (.node(\同步清零_气泡_高电平有效 ));
  Register #(.width(32), .trigger("rising"), .Select("low")) register_1 (
    .D(multiplexer_1_out), .en(\使能端_低电平有效_stall_高电平有效 ), .Q(out_6), .clk(CLK));  // open: clr
  Register #(.width(1), .trigger("rising"), .Select("low")) register_2 (
    .D(\使能端_低电平有效_stall_高电平有效 ), .Q(\传输状态Out_表明当前传输数据有效 ), .clk(CLK));  // open: en, clr
  Register #(.width(32), .trigger("rising"), .Select("low")) register_3 (
    .D(multiplexer_2_out), .en(\使能端_低电平有效_stall_高电平有效 ), .Q(out_8), .clk(CLK));  // open: clr
endmodule
module ID_EX (
  input  [31:0] in_1,
  input  CLK,
  input  \同步清零_气泡_高电平有效 ,
  input  \使能端_低电平有效_stall_高电平有效 ,
  input  [31:0] in_5,
  input  [31:0] in_6,
  input  [31:0] in_7,
  input  [31:0] in_8,
  input  [31:0] in_9,
  input  in_10,
  input  in_11,
  input  in_12,
  input  in_13,
  input  in_14,
  input  in_15,
  input  in_16,
  input  in_17,
  input  in_18,
  input  in_19,
  input  [3:0] in_20,
  input  in_21,
  input  [1:0] in_22,
  input  [1:0] in_23,
  output [31:0] out_24,
  output \传输状态Out_表明当前传输数据有效 ,
  output [31:0] out_26,
  output [31:0] out_27,
  output [31:0] out_28,
  output [31:0] out_29,
  output [31:0] out_30,
  output out_31,
  output out_32,
  output out_33,
  output out_34,
  output out_35,
  output out_36,
  output out_37,
  output out_38,
  output out_39,
  output out_40,
  output [3:0] out_41,
  output out_42,
  output [1:0] out_43,
  output [1:0] out_44
);

  wire multiplexer_7_out, multiplexer_8_out, multiplexer_9_out, multiplexer_10_out, multiplexer_11_out,
       multiplexer_12_out, multiplexer_13_out, multiplexer_14_out, multiplexer_15_out, multiplexer_16_out,
       multiplexer_18_out;
  wire [1:0] multiplexer_19_out, multiplexer_20_out;
  wire [3:0] multiplexer_17_out;
  wire [31:0] multiplexer_1_out, multiplexer_2_out, multiplexer_3_out, multiplexer_4_out, multiplexer_5_out,
       multiplexer_6_out;

  Multiplexer #(.select(1), .width(32), .disabled("Z"), .enable("false")) multiplexer_1 (
    .in0(in_1), .in1({32{1'b0}}), .out(multiplexer_1_out), .sel(\同步清零_气泡_高电平有效 ));
  Multiplexer #(.select(1), .width(32), .disabled("Z"), .enable("false")) multiplexer_2 (
    .in0(in_5), .in1({32{1'b0}}), .out(multiplexer_2_out), .sel(\同步清零_气泡_高电平有效 ));
  Multiplexer #(.select(1), .width(32), .disabled("Z"), .enable("false")) multiplexer_3 (
    .in0(in_6), .in1({32{1'b0}}), .out(multiplexer_3_out), .sel(\同步清零_气泡_高电平有效 ));
  Multiplexer #(.select(1), .width(32), .disabled("Z"), .enable("false")) multiplexer_4 (
    .in0(in_7), .in1({32{1'b0}}), .out(multiplexer_4_out), .sel(\同步清零_气泡_高电平有效 ));
  Multiplexer #(.select(1), .width(32), .disabled("Z"), .enable("false")) multiplexer_5 (
    .in0(in_8), .in1({32{1'b0}}), .out(multiplexer_5_out), .sel(\同步清零_气泡_高电平有效 ));
  Multiplexer #(.select(1), .width(32), .disabled("Z"), .enable("false")) multiplexer_6 (
    .in0(in_9), .in1({32{1'b0}}), .out(multiplexer_6_out), .sel(\同步清零_气泡_高电平有效 ));
  Multiplexer #(.select(1), .width(1), .disabled("Z"), .enable("false")) multiplexer_7 (
    .in0(in_10), .in1(1'b0), .out(multiplexer_7_out), .sel(\同步清零_气泡_高电平有效 ));
  Multiplexer #(.select(1), .width(1), .disabled("Z"), .enable("false")) multiplexer_8 (
    .in0(in_11), .in1(1'b0), .out(multiplexer_8_out), .sel(\同步清零_气泡_高电平有效 ));
  Multiplexer #(.select(1), .width(1), .disabled("Z"), .enable("false")) multiplexer_9 (
    .in0(in_12), .in1(1'b0), .out(multiplexer_9_out), .sel(\同步清零_气泡_高电平有效 ));
  Multiplexer #(.select(1), .width(1), .disabled("Z"), .enable("false")) multiplexer_10 (
    .in0(in_13), .in1(1'b0), .out(multiplexer_10_out), .sel(\同步清零_气泡_高电平有效 ));
  Multiplexer #(.select(1), .width(1), .disabled("Z"), .enable("false")) multiplexer_11 (
    .in0(in_14), .in1(1'b0), .out(multiplexer_11_out), .sel(\同步清零_气泡_高电平有效 ));
  Multiplexer #(.select(1), .width(1), .disabled("Z"), .enable("false")) multiplexer_12 (
    .in0(in_15), .in1(1'b0), .out(multiplexer_12_out), .sel(\同步清零_气泡_高电平有效 ));
  Multiplexer #(.select(1), .width(1), .disabled("Z"), .enable("false")) multiplexer_13 (
    .in0(in_16), .in1(1'b0), .out(multiplexer_13_out), .sel(\同步清零_气泡_高电平有效 ));
  Multiplexer #(.select(1), .width(1), .disabled("Z"), .enable("false")) multiplexer_14 (
    .in0(in_17), .in1(1'b0), .out(multiplexer_14_out), .sel(\同步清零_气泡_高电平有效 ));
  Multiplexer #(.select(1), .width(1), .disabled("Z"), .enable("false")) multiplexer_15 (
    .in0(in_18), .in1(1'b0), .out(multiplexer_15_out), .sel(\同步清零_气泡_高电平有效 ));
  Multiplexer #(.select(1), .width(1), .disabled("Z"), .enable("false")) multiplexer_16 (
    .in0(in_19), .in1(1'b0), .out(multiplexer_16_out), .sel(\同步清零_气泡_高电平有效 ));
  Multiplexer #(.select(1), .width(4), .disabled("Z"), .enable("false")) multiplexer_17 (
    .in0(in_20), .in1(4'b0000), .out(multiplexer_17_out), .sel(\同步清零_气泡_高电平有效 ));
  Multiplexer #(.select(1), .width(1), .disabled("Z"), .enable("false")) multiplexer_18 (
    .in0(in_21), .in1(1'b0), .out(multiplexer_18_out), .sel(\同步清零_气泡_高电平有效 ));
  Multiplexer #(.select(1), .width(2), .disabled("Z"), .enable("false")) multiplexer_19 (
    .in0(in_22), .in1(2'b00), .out(multiplexer_19_out), .sel(\同步清零_气泡_高电平有效 ));
  Multiplexer #(.select(1), .width(2), .disabled("Z"), .enable("false")) multiplexer_20 (
    .in0(in_23), .in1(2'b00), .out(multiplexer_20_out), .sel(\同步清零_气泡_高电平有效 ));
  Pull_Resistor #(.pull(0)) pull_resistor_1 (.node(\同步清零_气泡_高电平有效 ));
  Register #(.width(32), .trigger("rising"), .Select("low")) register_1 (
    .D(multiplexer_1_out), .en(\使能端_低电平有效_stall_高电平有效 ), .Q(out_24), .clk(CLK));  // open: clr
  Register #(.width(1), .trigger("rising"), .Select("low")) register_2 (
    .D(\使能端_低电平有效_stall_高电平有效 ), .Q(\传输状态Out_表明当前传输数据有效 ), .clk(CLK));  // open: en, clr
  Register #(.width(32), .trigger("rising"), .Select("low")) register_3 (
    .D(multiplexer_2_out), .en(\使能端_低电平有效_stall_高电平有效 ), .Q(out_26), .clk(CLK));  // open: clr
  Register #(.width(32), .trigger("rising"), .Select("low")) register_4 (
    .D(multiplexer_3_out), .en(\使能端_低电平有效_stall_高电平有效 ), .Q(out_27), .clk(CLK));  // open: clr
  Register #(.width(32), .trigger("rising"), .Select("low")) register_5 (
    .D(multiplexer_4_out), .en(\使能端_低电平有效_stall_高电平有效 ), .Q(out_28), .clk(CLK));  // open: clr
  Register #(.width(32), .trigger("rising"), .Select("low")) register_6 (
    .D(multiplexer_5_out), .en(\使能端_低电平有效_stall_高电平有效 ), .Q(out_29), .clk(CLK));  // open: clr
  Register #(.width(32), .trigger("rising"), .Select("low")) register_7 (
    .D(multiplexer_6_out), .en(\使能端_低电平有效_stall_高电平有效 ), .Q(out_30), .clk(CLK));  // open: clr
  Register #(.width(1), .trigger("rising"), .Select("low")) register_8 (
    .D(multiplexer_7_out), .en(\使能端_低电平有效_stall_高电平有效 ), .Q(out_31), .clk(CLK));  // open: clr
  Register #(.width(1), .trigger("rising"), .Select("low")) register_9 (
    .D(multiplexer_8_out), .en(\使能端_低电平有效_stall_高电平有效 ), .Q(out_32), .clk(CLK));  // open: clr
  Register #(.width(1), .trigger("rising"), .Select("low")) register_10 (
    .D(multiplexer_9_out), .en(\使能端_低电平有效_stall_高电平有效 ), .Q(out_33), .clk(CLK));  // open: clr
  Register #(.width(1), .trigger("rising"), .Select("low")) register_11 (
    .D(multiplexer_10_out), .en(\使能端_低电平有效_stall_高电平有效 ), .Q(out_34), .clk(CLK));  // open: clr
  Register #(.width(1), .trigger("rising"), .Select("low")) register_12 (
    .D(multiplexer_11_out), .en(\使能端_低电平有效_stall_高电平有效 ), .Q(out_35), .clk(CLK));  // open: clr
  Register #(.width(1), .trigger("rising"), .Select("low")) register_13 (
    .D(multiplexer_12_out), .en(\使能端_低电平有效_stall_高电平有效 ), .Q(out_36), .clk(CLK));  // open: clr
  Register #(.width(1), .trigger("rising"), .Select("low")) register_14 (
    .D(multiplexer_13_out), .en(\使能端_低电平有效_stall_高电平有效 ), .Q(out_37), .clk(CLK));  // open: clr
  Register #(.width(1), .trigger("rising"), .Select("low")) register_15 (
    .D(multiplexer_14_out), .en(\使能端_低电平有效_stall_高电平有效 ), .Q(out_38), .clk(CLK));  // open: clr
  Register #(.width(1), .trigger("rising"), .Select("low")) register_16 (
    .D(multiplexer_15_out), .en(\使能端_低电平有效_stall_高电平有效 ), .Q(out_39), .clk(CLK));  // open: clr
  Register #(.width(1), .trigger("rising"), .Select("low")) register_17 (
    .D(multiplexer_16_out), .en(\使能端_低电平有效_stall_高电平有效 ), .Q(out_40), .clk(CLK));  // open: clr
  Register #(.width(4), .trigger("rising"), .Select("low")) register_18 (
    .D(multiplexer_17_out), .en(\使能端_低电平有效_stall_高电平有效 ), .Q(out_41), .clk(CLK));  // open: clr
  Register #(.width(1), .trigger("rising"), .Select("low")) register_19 (
    .D(multiplexer_18_out), .en(\使能端_低电平有效_stall_高电平有效 ), .Q(out_42), .clk(CLK));  // open: clr
  Register #(.width(2), .trigger("rising"), .Select("low")) register_20 (
    .D(multiplexer_19_out), .en(\使能端_低电平有效_stall_高电平有效 ), .Q(out_43), .clk(CLK));  // open: clr
  Register #(.width(2), .trigger("rising"), .Select("low")) register_21 (
    .D(multiplexer_20_out), .en(\使能端_低电平有效_stall_高电平有效 ), .Q(out_44), .clk(CLK));  // open: clr
endmodule

module EX_MEM (
  input  [31:0] in_1,
  input  CLK,
  input  \使能端_低电平有效_stall_高电平有效 ,
  input  [31:0] in_4,
  input  [31:0] in_5,
  input  [31:0] in_6,
  input  in_7,
  input  in_8,
  input  in_9,
  input  in_10,
  input  in_11,
  input  \同步清零_气泡_高电平有效 ,
  input  in_13,
  output [31:0] out_14,
  output \传输状态Out_表明当前传输数据有效 ,
  output [31:0] out_16,
  output [31:0] out_17,
  output [31:0] out_18,
  output out_19,
  output out_20,
  output out_21,
  output out_22,
  output out_23,
  output out_24
);

  wire undriven;

  Pull_Resistor #(.pull(0)) pull_resistor_1 (.node(\同步清零_气泡_高电平有效 ));
  Register #(.width(32), .trigger("rising"), .Select("low")) register_1 (
    .D(in_1), .en(\使能端_低电平有效_stall_高电平有效 ), .Q(out_14), .clk(CLK), .clr(\同步清零_气泡_高电平有效 ));
  Register #(.width(1), .trigger("rising"), .Select("low")) register_2 (
    .D(\使能端_低电平有效_stall_高电平有效 ), .Q(\传输状态Out_表明当前传输数据有效 ), .clk(CLK), .clr(\同步清零_气泡_高电平有效 ), .preset(undriven));  // open: en, cs
  Register #(.width(32), .trigger("rising"), .Select("low")) register_3 (
    .D(in_4), .en(\使能端_低电平有效_stall_高电平有效 ), .Q(out_16), .clk(CLK), .clr(\同步清零_气泡_高电平有效 ));
  Register #(.width(32), .trigger("rising"), .Select("low")) register_4 (
    .D(in_5), .en(\使能端_低电平有效_stall_高电平有效 ), .Q(out_17), .clk(CLK), .clr(\同步清零_气泡_高电平有效 ));
  Register #(.width(32), .trigger("rising"), .Select("low")) register_5 (
    .D(in_6), .en(\使能端_低电平有效_stall_高电平有效 ), .Q(out_18), .clk(CLK), .clr(\同步清零_气泡_高电平有效 ));
  Register #(.width(1), .trigger("rising"), .Select("low")) register_6 (
    .D(in_7), .en(\使能端_低电平有效_stall_高电平有效 ), .Q(out_19), .clk(CLK), .clr(\同步清零_气泡_高电平有效 ));
  Register #(.width(1), .trigger("rising"), .Select("low")) register_7 (
    .D(in_8), .en(\使能端_低电平有效_stall_高电平有效 ), .Q(out_20), .clk(CLK), .clr(\同步清零_气泡_高电平有效 ));
  Register #(.width(1), .trigger("rising"), .Select("low")) register_8 (
    .D(in_9), .en(\使能端_低电平有效_stall_高电平有效 ), .Q(out_21), .clk(CLK), .clr(\同步清零_气泡_高电平有效 ));
  Register #(.width(1), .trigger("rising"), .Select("low")) register_9 (
    .D(in_10), .en(\使能端_低电平有效_stall_高电平有效 ), .Q(out_22), .clk(CLK), .clr(\同步清零_气泡_高电平有效 ));
  Register #(.width(1), .trigger("rising"), .Select("low")) register_10 (
    .D(in_11), .en(\使能端_低电平有效_stall_高电平有效 ), .Q(out_23), .clk(CLK), .clr(\同步清零_气泡_高电平有效 ));
  Register #(.width(1), .trigger("rising"), .Select("low")) register_11 (
    .D(in_13), .en(\使能端_低电平有效_stall_高电平有效 ), .Q(out_24), .clk(CLK), .clr(\同步清零_气泡_高电平有效 ));
endmodule

module MEM_WB (
  input  [31:0] in_1,
  input  CLK,
  input  \使能端_低电平有效_stall_高电平有效 ,
  input  [31:0] in_4,
  input  [31:0] in_5,
  input  [31:0] in_6,
  input  in_7,
  input  in_8,
  input  in_9,
  input  in_10,
  input  \同步清零_气泡_高电平有效 ,
  input  in_12,
  output [31:0] out_13,
  output \传输状态Out_表明当前传输数据有效 ,
  output [31:0] out_15,
  output [31:0] out_16,
  output [31:0] out_17,
  output out_18,
  output out_19,
  output out_20,
  output out_21,
  output out_22
);

  wire undriven, undriven_2;

  Pull_Resistor #(.pull(0)) pull_resistor_1 (.node(\同步清零_气泡_高电平有效 ));
  Register #(.width(32), .trigger("rising"), .Select("low")) register_1 (
    .D(in_1), .en(\使能端_低电平有效_stall_高电平有效 ), .Q(out_13), .clk(CLK), .clr(\同步清零_气泡_高电平有效 ));
  Register #(.width(1), .trigger("rising"), .Select("low")) register_2 (
    .D(\使能端_低电平有效_stall_高电平有效 ), .Q(\传输状态Out_表明当前传输数据有效 ), .clk(CLK), .clr(\同步清零_气泡_高电平有效 ));  // open: en
  Register #(.width(32), .trigger("rising"), .Select("low")) register_3 (
    .D(in_4), .en(\使能端_低电平有效_stall_高电平有效 ), .Q(out_15), .clk(CLK), .clr(\同步清零_气泡_高电平有效 ));
  Register #(.width(32), .trigger("rising"), .Select("low")) register_4 (
    .D(in_5), .en(\使能端_低电平有效_stall_高电平有效 ), .Q(out_16), .clk(CLK), .clr(\同步清零_气泡_高电平有效 ));
  Register #(.width(32), .trigger("rising"), .Select("low")) register_5 (
    .D(in_6), .en(\使能端_低电平有效_stall_高电平有效 ), .Q(out_17), .clk(CLK), .clr(\同步清零_气泡_高电平有效 ), .preset(undriven));  // open: cs
  Register #(.width(1), .trigger("rising"), .Select("low")) register_6 (
    .D(in_7), .en(\使能端_低电平有效_stall_高电平有效 ), .Q(out_18), .clk(CLK), .clr(\同步清零_气泡_高电平有效 ));
  Register #(.width(1), .trigger("rising"), .Select("low")) register_7 (
    .D(in_8), .en(\使能端_低电平有效_stall_高电平有效 ), .Q(out_19), .clk(CLK), .clr(\同步清零_气泡_高电平有效 ));
  Register #(.width(1), .trigger("rising"), .Select("low")) register_8 (
    .D(in_9), .en(\使能端_低电平有效_stall_高电平有效 ), .Q(out_20), .clk(CLK), .clr(\同步清零_气泡_高电平有效 ), .preset(undriven_2));  // open: cs
  Register #(.width(1), .trigger("rising"), .Select("low")) register_9 (
    .D(in_10), .en(\使能端_低电平有效_stall_高电平有效 ), .Q(out_21), .clk(CLK), .clr(\同步清零_气泡_高电平有效 ));
  Register #(.width(1), .trigger("rising"), .Select("low")) register_10 (
    .D(in_12), .en(\使能端_低电平有效_stall_高电平有效 ), .Q(out_22), .clk(CLK), .clr(\同步清零_气泡_高电平有效 ));
endmodule
