// Logisim project 团队项目多媒体视听.circ as structural Verilog: 25 circuits, main circuit ◆单周期硬布线控制器
module \团队项目主界面  (
  input  [3:0] in_1,
  input  [6:0] in_2,
  output RegWrite,
  output MemWrite,
  output [31:0] PC,
  output [31:0] IR,
  output [31:0] RDin,
  output [31:0] MDin
);

  wire and_1_out, and_2_out, and_3_out, and_4_out, and_5_out, and_7_out, and_8_out, and_9_out, and_10_out,
       and_11_out, and_14_out, and_15_out, brk, \cache_全相联_1_first_write , CLK, comparator_2_gt,
       comparator_3_gt, comparator_4_gt, comparator_5_eq, comparator_6_eq, comparator_7_lt, comparator_8_eq,
       comparator_9_eq, comparator_10_gt, comparator_11_eq, comparator_12_eq, comparator_13_gt,
       comparator_14_gt, comparator_15_eq, comparator_16_eq, ERET, Go, HALT, IE, Int_hidden, IR1, IR2, IR3,
       JI, keyboard_1_avail, load_use, mips_alu_3_equal, or_2_out, or_3_out, or_4_out, or_5_out, or_11_out,
       or_12_out, restore_EPC, RST, RUNNING, W1, W2, W3, xor_1_out, \单周期硬布线控制器_1_clear_rs ,
       \单周期硬布线控制器_1_clear_rt , \单周期硬布线控制器_1_lui , \单周期硬布线控制器_1_regdst , \单周期硬布线控制器_1_signedext , \成功分支 ,
       \无条件分支 , \条件分支 , \清空预取指令 , \避免清空 , \需要跳转 ;
  wire [0:0] not_1_out;
  wire [1:0] \bht状态转换电路_1_次态 , bit_extender_4_out, bit_extender_9_out, bitselector_1_out,
       \cache_全相联_1_写指令分支预测历史 , \cache_全相联_1_读指令预测分支 , forward_rs, forward_rt, id_ex_1_out_19, if_id_1_out_8,
       IntNo, multiplexer_3_out, priority_encoder_1_out;
  wire [2:0] ex_mem_1_out_12, ex_mem_1_out_13, MEM, mem_wb_1_out_12, WB, \单周期硬布线控制器_1_memtoreg ,
       \单周期硬布线控制器_1_memwrite ;
  wire [3:0] bit_extender_10_out, controlled_buffer_2_out, controlled_buffer_5_out, multiplexer_19_out,
       multiplexer_20_out;
  wire [4:0] ex_mem_1_out_19, id_ex_1_out_32, id_ex_1_out_33, id_rs, id_rt, mem_wb_1_out_19,
       multiplexer_5_out, multiplexer_6_out, multiplexer_7_out, multiplexer_8_out, multiplexer_9_out,
       multiplexer_21_out, rs, rt;
  wire [6:0] bit_extender_5_out, bit_extender_6_out, bit_extender_8_out, keyboard_1_data;
  wire [7:0] adder_1_out, bit_extender_13_out, controlled_buffer_9_out;
  wire [14:0] controlled_buffer_1_out;
  wire [15:0] bit_extender_7_out, \LoadUse次数 , \减少分支清空总数 , \总周期数 , \无条件分支数 , \条件分支总数 , \条件分支成功数 ;
  wire [25:0] id_ex_1_out_23;
  wire [31:0] _0xffff00, _0xffff0a, _0xffff01, _0xffff04, _0xffff05, _0xffff06, _0xffff07, _0xffff08,
       _0xffff09, bit_extender_1_out, bit_extender_2_out, bit_extender_3_out, bit_extender_11_out,
       bit_extender_12_out, \cache_全相联_1_目标地址 , controlled_buffer_6_out, EPC, EX_IR, ex_mem_1_out_17,
       ex_mem_1_out_18, EX_PC, id_ex_1_out_22, id_ex_1_out_26, id_ex_1_out_27, id_ex_1_out_28,
       id_ex_1_out_29, ID_IR, ID_PC, if_id_1_out_10, IF_IR, IF_PC, LedData, MEM_IR, MEM_PC, mem_wb_1_out_17,
       mem_wb_1_out_18, mips_alu_1_result, mips_alu_2_result, mips_alu_3_result, mips_ram_1_p6,
       mips_regifile_1_r1, mips_regifile_1_r2, multiplexer_1_out, multiplexer_2_out, multiplexer_4_out,
       multiplexer_12_out, multiplexer_13_out, multiplexer_15_out, multiplexer_16_out, multiplexer_17_out,
       multiplexer_18_out, multiplexer_22_out, or_1_out, PC_next, rom_1_data, shifter_1_out, WB_IR, WB_PC,
       \单周期硬布线控制器_1_alu_op , \存入BHT的分支地址 , \断点地址 ;

  Clock #(.highDuration(1), .lowDuration(1)) clock_1 (.out(CLK));
  Button _1 ();  // open: out
  Button _2 (.out(IR2));
  Button _3 (.out(IR3));
  Button \u_继续运行  (.out(Go));
  LED #(.active("true")) led_1 (.in(W1));
  LED #(.active("true")) led_2 (.in(W2));
  LED #(.active("true")) led_3 (.in(W3));
  Hex_Digit_Display hex_digit_display_1 (.value(LedData[31:28]));  // open: dp
  LED #(.active("true")) led_4 (.in(HALT));
  // Probe on \总周期数 
  // Probe on \无条件分支数 
  // Probe on \条件分支成功数 
  // Probe on \LoadUse次数 
  // Probe on \条件分支总数 
  // Probe on \减少分支清空总数 
  LED #(.active("true")) led_5 (.in(IE));
  LED #(.active("true")) led_6 (.in(Int_hidden));
  // Probe on EPC
  // Probe on PC_next
  ROM #(.addrWidth(2), .dataWidth(32), .Select("high")) rom_1 (.addr(IntNo), .data(rom_1_data));
  Hex_Digit_Display hex_digit_display_2 (.value(LedData[27:24]));  // open: dp
  Hex_Digit_Display hex_digit_display_3 (.value(LedData[23:20]));  // open: dp
  Multiplexer #(.select(1), .width(32), .disabled("Z"), .enable("false")) multiplexer_1 (
    .in0(PC_next), .in1(\cache_全相联_1_目标地址 ), .out(multiplexer_1_out), .sel(and_1_out));
  Hex_Digit_Display hex_digit_display_4 (.value(LedData[19:16]));  // open: dp
  Hex_Digit_Display hex_digit_display_5 (.value(LedData[15:12]));  // open: dp
  // Probe on IF_PC
  and and_1 (and_1_out, \cache_全相联_1_读指令预测分支 [0], ~\清空预取指令 );  // AND_Gate
  Multiplexer #(.select(1), .width(32), .disabled("Z"), .enable("false")) multiplexer_2 (
    .in0(multiplexer_1_out), .in1(rom_1_data), .out(multiplexer_2_out), .sel(Int_hidden));
  Hex_Digit_Display hex_digit_display_6 (.value(LedData[7:4]));  // open: dp
  Hex_Digit_Display hex_digit_display_7 (.value(LedData[11:8]));  // open: dp
  // Probe on \总周期数 
  and and_2 (and_2_out, RUNNING, ~load_use);  // AND_Gate
  Hex_Digit_Display hex_digit_display_8 (.value(LedData[3:0]));  // open: dp
  // Probe on ID_PC
  Register #(.width(32), .trigger("rising"), .Select("low")) u_PC (
    .D(multiplexer_2_out), .en(and_2_out), .Q(IF_PC), .clk(CLK), .clr(RST));
  // Probe on EX_PC
  Comparator #(.width(32), .mode("twosComplement")) comparator_1 (.a(EX_PC), .b(32'h30c0));  // open: gt, eq, lt
  assign bit_extender_1_out = {{30{1'b0}}, \bht状态转换电路_1_次态 };  // Bit_Extender bit_extender_1
  Pull_Resistor #(.pull(0)) pull_resistor_1 (.node(brk));
  assign or_1_out = bit_extender_1_out | \存入BHT的分支地址 ;  // OR_Gate or_1, 32 bits wide
  // Probe on MEM_PC
  // Probe on WB_PC
  or or_2 (or_2_out, \条件分支 , JI);
  \Cache_全相联  \cache_全相联_1  (
    .\读指令地址 (IF_PC), .WE(or_2_out), .CLK(CLK), .\目标地址 (\cache_全相联_1_目标地址 ), .\写指令地址 (EX_PC),
    .HIT(\cache_全相联_1_读指令预测分支 [1]), .\读指令预测分支 (\cache_全相联_1_读指令预测分支 [0]),
    .\写指令分支预测历史 (\cache_全相联_1_写指令分支预测历史 ), .First_Write(\cache_全相联_1_first_write ), .\分支地址及双预测位 (or_1_out));
  or or_3 (or_3_out, \成功分支 , \无条件分支 );
  Multiplexer #(.select(1), .width(2), .disabled("Z"), .enable("false")) multiplexer_3 (
    .in0(\cache_全相联_1_写指令分支预测历史 ), .in1(2'b10), .out(multiplexer_3_out), .sel(\cache_全相联_1_first_write ));
  \BHT状态转换电路  \bht状态转换电路_1  (.\分支成功 (or_3_out), .\现态 (multiplexer_3_out), .\次态 (\bht状态转换电路_1_次态 ));
  MIPS_ALU mips_alu_1 (
    .X(32'h4), .Y(IF_PC), .AluOP(4'b0101), .Result(mips_alu_1_result));  // open: Equal, Result_2, shamt
  \指令存储器  \u_指令存储器_1  (.PC(IF_PC), .Instruction(IF_IR));
  or or_4 (or_4_out, load_use, HALT);
  D_Flip_Flop #(.trigger("rising"), .Pre_Clr_Positions("ABOVE_BELOW"), .NegatePresetClear("false"), .enable("true"), .NewFFLayout("true")) d_ff_1 (
    .clk(CLK), .D(brk), .Q(HALT), .Qn(RUNNING), .en(RUNNING), .reset(Go));  // open: preset
  IF_ID if_id_1 (
    .in_3(mips_alu_1_result), .in_4(IF_IR), .CLK(CLK), .out_10(if_id_1_out_10), .out_11(ID_IR),
    .\使能端 (or_4_out), .\同步清零 (\清空预取指令 ), .PC(IF_PC), .out_9(ID_PC), .\预测跳转 (\cache_全相联_1_读指令预测分支 ),
    .out_8(if_id_1_out_8));
  assign bit_extender_2_out = {{16{1'b0}}, ID_IR[15:0]};  // Bit_Extender bit_extender_2
  assign bit_extender_3_out = {{16{ID_IR[15]}}, ID_IR[15:0]};  // Bit_Extender bit_extender_3
  Multiplexer #(.select(1), .width(32), .disabled("Z"), .enable("false")) multiplexer_4 (
    .in0(bit_extender_2_out), .in1(bit_extender_3_out), .out(multiplexer_4_out), .sel(\单周期硬布线控制器_1_signedext ));
  Multiplexer #(.select(1), .width(5), .disabled("Z"), .enable("false")) multiplexer_5 (
    .in0(ID_IR[10:6]), .in1(5'b10000), .out(multiplexer_5_out), .sel(\单周期硬布线控制器_1_lui ));
  Multiplexer #(.select(1), .width(5), .disabled("Z"), .enable("false")) multiplexer_6 (
    .in0(ID_IR[25:21]), .in1(5'b00010), .out(multiplexer_6_out), .sel(\单周期硬布线控制器_1_alu_op [14]));
  \单周期硬布线控制器  \u_单周期硬布线控制器_1  (
    .Func(ID_IR[5:0]), .OP(ID_IR[31:26]), .ALU_OP(\单周期硬布线控制器_1_alu_op [3:0]),
    .MemToReg(\单周期硬布线控制器_1_memtoreg [0]), .MemWrite(\单周期硬布线控制器_1_memwrite [0]),
    .ALU_SRC(\单周期硬布线控制器_1_alu_op [6]), .RegWrite(\单周期硬布线控制器_1_memtoreg [1]),
    .SysCALL(\单周期硬布线控制器_1_alu_op [14]), .SignedExt(\单周期硬布线控制器_1_signedext ), .RegDst(\单周期硬布线控制器_1_regdst ),
    .JR(\单周期硬布线控制器_1_alu_op [9]), .JMP(\单周期硬布线控制器_1_alu_op [8]), .Beq(\单周期硬布线控制器_1_alu_op [4]),
    .JAL(\单周期硬布线控制器_1_alu_op [7]), .Bne(\单周期硬布线控制器_1_alu_op [5]), .BLTZ(\单周期硬布线控制器_1_alu_op [10]),
    .LHU(\单周期硬布线控制器_1_memwrite [1]), .LUI(\单周期硬布线控制器_1_lui ), .ERET(\单周期硬布线控制器_1_alu_op [11]),
    .clear_rt(\单周期硬布线控制器_1_clear_rt ), .clear_rs(\单周期硬布线控制器_1_clear_rs ), .MT_MF(ID_IR[23]),
    .MTC0(\单周期硬布线控制器_1_alu_op [12]), .MFC0(\单周期硬布线控制器_1_alu_op [13]), .LB(\单周期硬布线控制器_1_memwrite [2]));
  Multiplexer #(.select(1), .width(5), .disabled("Z"), .enable("false")) multiplexer_7 (
    .in0(ID_IR[20:16]), .in1(5'b00100), .out(multiplexer_7_out), .sel(\单周期硬布线控制器_1_alu_op [14]));
  Multiplexer #(.select(1), .width(5), .disabled("Z"), .enable("false")) multiplexer_8 (
    .in0(multiplexer_7_out), .in1(ID_IR[15:11]), .out(multiplexer_8_out), .sel(\单周期硬布线控制器_1_regdst ));
  BitSelector #(.width(32), .group(2)) bitselector_1 (.in(IF_PC), .out(bitselector_1_out), .sel(4'b1100));
  Multiplexer #(.select(1), .width(5), .disabled("Z"), .enable("false")) multiplexer_9 (
    .in0(multiplexer_8_out), .in1({5{1'b1}}), .out(multiplexer_9_out), .sel(\单周期硬布线控制器_1_alu_op [7]));
  Multiplexer #(.select(1), .width(5), .disabled("Z"), .enable("false")) multiplexer_10 (
    .in0(multiplexer_6_out), .in1({5{1'b0}}), .out(id_rs), .sel(\单周期硬布线控制器_1_clear_rs ));
  and and_3 (and_3_out, RUNNING, \条件分支 );
  \中断按键参考电路  \u_中断按键参考电路_1  (
    .CLK(CLK), .\_1号按键 (IR1), .IE(IE), .\_2号按键 (IR2), .\_3号按键 (IR3), .\中断号 (IntNo), .LED1(W1), .LED2(W2),
    .LED3(W3), .\中断隐周期 (Int_hidden), .ERET(ERET), .EPC(EPC), .\当前中断号 (bitselector_1_out),
    .restore_EPC(restore_EPC));
  Multiplexer #(.select(1), .width(5), .disabled("Z"), .enable("false")) multiplexer_11 (
    .in0(multiplexer_7_out), .in1({5{1'b0}}), .out(id_rt), .sel(\单周期硬布线控制器_1_clear_rt ));
  Counter #(.width(16), .max('hffff), .ongoal("wrap"), .trigger("rising"), .behavior("new")) counter_1 (
    .count(and_3_out), .Q(\条件分支总数 ), .clk(CLK));  // open: load, D, carry, clr, preset, down
  or or_5 (or_5_out, load_use, \清空预取指令 );
  MIPS_Regifile mips_regifile_1 (
    .Din(multiplexer_22_out), .Clk(CLK), .R1(mips_regifile_1_r1), .R2(mips_regifile_1_r2),
    .WE(mem_wb_1_out_12[1]), .W_num(mem_wb_1_out_19), .R1_num(multiplexer_6_out), .R2_num(multiplexer_7_out));
  and and_4 (and_4_out, RUNNING, \成功分支 );
  Counter #(.width(16), .max('hffff), .ongoal("wrap"), .trigger("rising"), .behavior("new")) counter_2 (
    .count(and_4_out), .Q(\条件分支成功数 ), .clk(CLK));  // open: load, D, carry, clr, preset, down
  ID_EX id_ex_1 (
    .in_9(if_id_1_out_10), .in_10(mips_regifile_1_r1), .CLK(CLK), .out_27(id_ex_1_out_27),
    .out_28(id_ex_1_out_28), .in_11(mips_regifile_1_r2), .out_29(id_ex_1_out_29), .in_14(multiplexer_5_out),
    .out_32(id_ex_1_out_32), .in_15(multiplexer_9_out), .out_33(id_ex_1_out_33), .in_8(multiplexer_4_out),
    .out_26(id_ex_1_out_26), .in_5(ID_IR[25:0]), .out_23(id_ex_1_out_23), .in_4(\单周期硬布线控制器_1_alu_op ),
    .out_22({id_ex_1_out_22[31:15], IR1, id_ex_1_out_22[13:12], ERET, id_ex_1_out_22[10:9], JI, id_ex_1_out_22[7:0]}),
    .in_3(\单周期硬布线控制器_1_memwrite ), .out_21(MEM), .in_2(\单周期硬布线控制器_1_memtoreg ), .out_20(WB),
    .\同步清零 (or_5_out), .\使能端 (HALT), .PC(ID_PC), .out_25(EX_PC), .in_13(id_rt), .out_31(rt), .in_12(id_rs),
    .out_30(rs), .\预测情况 (if_id_1_out_8), .out_19(id_ex_1_out_19), .IR(ID_IR), .out_24(EX_IR));
  and and_5 (and_5_out, RUNNING, \无条件分支 );
  Counter #(.width(16), .max('hffff), .ongoal("wrap"), .trigger("rising"), .behavior("new")) counter_3 (
    .count(and_5_out), .Q(\无条件分支数 ), .clk(CLK));  // open: load, D, carry, clr, preset, down
  Multiplexer #(.select(2), .width(32), .disabled("Z"), .enable("false")) multiplexer_12 (
    .in0(id_ex_1_out_28), .in1(ex_mem_1_out_17), .in2(multiplexer_22_out), .in3(ex_mem_1_out_17),
    .out(multiplexer_12_out), .sel(forward_rs));
  Comparator #(.width(32), .mode("twosComplement")) comparator_2 (
    .a(ID_PC), .b({32{1'b0}}), .gt(comparator_2_gt));  // open: eq, lt
  Comparator #(.width(32), .mode("twosComplement")) comparator_3 (
    .a(EX_PC), .b({32{1'b0}}), .gt(comparator_3_gt));  // open: eq, lt
  xor xor_1 (xor_1_out, \需要跳转 , id_ex_1_out_19[0]);
  and and_6 (\避免清空 , \需要跳转 , id_ex_1_out_19[0]);
  MIPS_ALU mips_alu_2 (
    .X(id_ex_1_out_27), .Y({id_ex_1_out_26[29:0], 2'b00}), .AluOP(4'b0101), .Result(mips_alu_2_result));  // open: Equal, Result_2, shamt
  and and_7 (and_7_out, RUNNING, load_use);
  not not_1 (not_1_out[0], xor_1_out);
  or or_6 (\清空预取指令 , xor_1_out, Int_hidden);
  Multiplexer #(.select(2), .width(32), .disabled("Z"), .enable("false")) multiplexer_13 (
    .in0(id_ex_1_out_29), .in1(ex_mem_1_out_17), .in2(multiplexer_22_out), .in3(ex_mem_1_out_17),
    .out(multiplexer_13_out), .sel(forward_rt));
  Counter #(.width(16), .max('hffff), .ongoal("wrap"), .trigger("rising"), .behavior("new")) counter_4 (
    .count(and_7_out), .Q(\LoadUse次数 ), .clk(CLK));  // open: load, D, carry, clr, preset, down
  Priority_Encoder #(.select(2), .disabled("Z")) priority_encoder_1 (
    .in0(1'b1), .in1(comparator_2_gt), .in2(comparator_3_gt), .out(priority_encoder_1_out));  // open: in3, gs, en_out, en_in
  Multiplexer #(.select(2), .width(32), .disabled("Z"), .enable("false")) multiplexer_14 (
    .in0(IF_PC), .in1(ID_PC), .in2(EX_PC), .out(\断点地址 ), .sel(priority_encoder_1_out));  // open: in3
  or or_7 (\条件分支 , id_ex_1_out_22[4], id_ex_1_out_22[5], id_ex_1_out_22[10]);
  Multiplexer #(.select(1), .width(32), .disabled("Z"), .enable("false")) multiplexer_15 (
    .in0(multiplexer_13_out), .in1(id_ex_1_out_26), .out(multiplexer_15_out), .sel(id_ex_1_out_22[6]));
  and and_8 (and_8_out, RUNNING, \避免清空 );
  MIPS_ALU mips_alu_3 (
    .X(multiplexer_12_out), .Y(multiplexer_15_out), .AluOP(id_ex_1_out_22[3:0]), .Equal(mips_alu_3_equal),
    .Result(mips_alu_3_result), .shamt(id_ex_1_out_32));  // open: Result_2
  Counter #(.width(16), .max('hffff), .ongoal("wrap"), .trigger("rising"), .behavior("new")) counter_5 (
    .count(and_8_out), .Q(\减少分支清空总数 ), .clk(CLK));  // open: load, D, carry, clr, preset, down
  or or_8 (\无条件分支 , id_ex_1_out_22[9], JI);
  and and_9 (and_9_out, id_ex_1_out_22[4], mips_alu_3_equal);
  and and_10 (and_10_out, id_ex_1_out_22[5], ~mips_alu_3_equal);  // AND_Gate
  and and_11 (and_11_out, id_ex_1_out_22[10], mips_alu_3_result[0]);
  Multiplexer #(.select(1), .width(32), .disabled("Z"), .enable("false")) multiplexer_16 (
    .in0(mips_alu_3_result), .in1(id_ex_1_out_27), .out(multiplexer_16_out), .sel(id_ex_1_out_22[7]));
  or or_9 (\成功分支 , and_9_out, and_10_out, and_11_out);
  Bit_Extender #(.in_width(32), .out_width(2), .\type ("zero")) bit_extender_4 (
    .in(_0xffff0a), .out(bit_extender_4_out));
  or or_10 (\需要跳转 , \无条件分支 , ERET, \成功分支 );
  Multiplexer #(.select(1), .width(32), .disabled("Z"), .enable("false")) multiplexer_17 (
    .in0(multiplexer_13_out), .in1(\断点地址 ), .out(multiplexer_17_out), .sel(Int_hidden));
  CP0 cp0_1 (
    .RDin(multiplexer_17_out), .WE(id_ex_1_out_22[12]), .W_num(id_ex_1_out_33), .CLK(CLK), .IE(IE),
    .EPC(EPC), .\同步置IE为1 (ERET), .\中断隐指令 (Int_hidden));
  Bit_Extender #(.in_width(32), .out_width(7), .\type ("zero")) bit_extender_5 (
    .in(_0xffff07), .out(bit_extender_5_out));
  Bit_Extender #(.in_width(32), .out_width(7), .\type ("zero")) bit_extender_6 (
    .in(_0xffff08), .out(bit_extender_6_out));
  Bit_Extender #(.in_width(32), .out_width(16), .\type ("zero")) bit_extender_7 (
    .in(_0xffff09), .out(bit_extender_7_out));
  and and_12 (restore_EPC, id_ex_1_out_33[0], id_ex_1_out_22[12]);
  Counter #(.width(16), .max('hffff), .ongoal("wrap"), .trigger("rising"), .behavior("new")) counter_6 (
    .count(RUNNING), .Q(\总周期数 ), .clk(CLK));  // open: load, D, carry, clr, preset, down
  NPC npc_1 (
    .\JR指令目标地址 (multiplexer_12_out), .JR(id_ex_1_out_22[9]),
    .\J与JAL指令目标地址 ({id_ex_1_out_27[31:28], id_ex_1_out_23, 2'b00}), .\J或JAL (JI),
    .\预测结果 ({id_ex_1_out_19[1], not_1_out[0]}), .\成功分支 (\成功分支 ), .\条件分支目标地址 (mips_alu_2_result),
    .EX_PC_4(id_ex_1_out_27), .IF_PC_4(mips_alu_1_result), .EPC(EPC), .ERET(ERET), .\BHT分支地址 (\存入BHT的分支地址 ),
    .PC_next(PC_next));
  Multiplexer #(.select(1), .width(32), .disabled("Z"), .enable("false")) multiplexer_18 (
    .in0(multiplexer_16_out), .in1(EPC), .out(multiplexer_18_out), .sel(id_ex_1_out_22[13]));
  Comparator #(.width(5), .mode("unsigned")) comparator_4 (
    .a(id_ex_1_out_33), .b({5{1'b0}}), .gt(comparator_4_gt));  // open: eq, lt
  Comparator #(.width(5), .mode("twosComplement")) comparator_5 (
    .a(id_ex_1_out_33), .b(id_rs), .eq(comparator_5_eq));  // open: gt, lt
  or or_11 (or_11_out, comparator_5_eq, comparator_6_eq);
  Comparator #(.width(5), .mode("twosComplement")) comparator_6 (
    .a(id_ex_1_out_33), .b(id_rt), .eq(comparator_6_eq));  // open: gt, lt
  // LCD_Video lcd_video_1: pin names not known; wires that end beside it: bit_extender_4_out[0], CLK, bit_extender_4_out[1], bit_extender_5_out, bit_extender_6_out, bit_extender_7_out
  and and_13 (load_use, WB[0], comparator_4_gt, or_11_out);
  EX_MEM ex_mem_1 (
    .in_6(multiplexer_18_out), .CLK(CLK), .out_17(ex_mem_1_out_17), .in_7(multiplexer_13_out),
    .out_18(ex_mem_1_out_18), .in_8(id_ex_1_out_33), .out_19(ex_mem_1_out_19), .in_2(WB),
    .out_13(ex_mem_1_out_13), .in_1(MEM), .out_12(ex_mem_1_out_12), .\同步清零 (Int_hidden), .\使能端 (HALT),
    .PC(EX_PC), .out_15(MEM_PC), .IR(EX_IR), .out_14(MEM_IR));  // open: in_5, out_16
  Bit_Extender #(.in_width(32), .out_width(7), .\type ("zero")) bit_extender_8 (
    .in(_0xffff01), .out(bit_extender_8_out));
  Bit_Extender #(.in_width(32), .out_width(2), .\type ("zero")) bit_extender_9 (
    .in(_0xffff00), .out(bit_extender_9_out));
  // Probe on bit_extender_8_out
  Keyboard #(.Char_bit_width(7), .buflen(32), .trigger("falling")) keyboard_1 (
    .clk(and_15_out), .avail(keyboard_1_avail), .data(keyboard_1_data));  // open: re, clr
  Multiplexer #(.select(2), .width(4), .disabled("Z"), .enable("false")) multiplexer_19 (
    .in0(4'b0001), .in1(4'b0010), .in2(4'b0100), .in3(4'b1000), .out(multiplexer_19_out),
    .sel(ex_mem_1_out_17[1:0]));
  TTY #(.Char_bit_width(7), .rows(8), .cols(32), .trigger("rising")) tty_1 (
    .data(bit_extender_8_out), .clk(bit_extender_9_out[0]), .clr(bit_extender_9_out[1]));  // open: we
  Bit_Extender #(.in_width(32), .out_width(4), .\type ("zero")) bit_extender_10 (
    .in(ex_mem_1_out_17), .out(bit_extender_10_out));
  Comparator #(.width(32), .mode("unsigned")) comparator_7 (
    .a(ex_mem_1_out_17), .b(32'hffff00), .lt(comparator_7_lt));  // open: gt, eq
  assign controlled_buffer_1_out = comparator_7_lt ? ex_mem_1_out_17[16:2] : 15'bz;  // Controlled_Buffer controlled_buffer_1
  assign controlled_buffer_2_out = ex_mem_1_out_12[2] ? multiplexer_19_out : 4'bz;  // Controlled_Buffer controlled_buffer_2
  Multiplexer #(.select(1), .width(4), .disabled("Z"), .enable("false")) multiplexer_20 (
    .in0(4'b0011), .in1(4'b1100), .out(multiplexer_20_out), .sel(ex_mem_1_out_17[1]));
  or or_12 (or_12_out, ex_mem_1_out_12[2], ex_mem_1_out_12[1]);
  assign controlled_buffer_2_out = ex_mem_1_out_12[1] ? multiplexer_20_out : 4'bz;  // Controlled_Buffer controlled_buffer_3
  assign bit_extender_11_out = {{25{1'b0}}, keyboard_1_data};  // Bit_Extender bit_extender_11
  assign bit_extender_12_out = {{31{1'b0}}, keyboard_1_avail};  // Bit_Extender bit_extender_12
  assign controlled_buffer_2_out = ~or_12_out ? 4'b1111 : 4'bz;  // Controlled_Buffer controlled_buffer_4
  Comparator #(.width(4), .mode("unsigned")) comparator_8 (
    .a(bit_extender_10_out), .b(4'b0010), .eq(comparator_8_eq));  // open: gt, lt
  Comparator #(.width(4), .mode("unsigned")) comparator_9 (
    .a(bit_extender_10_out), .b(4'b0011), .eq(comparator_9_eq));  // open: gt, lt
  assign controlled_buffer_5_out = ~comparator_7_lt ? bit_extender_10_out : 4'bz;  // Controlled_Buffer controlled_buffer_5
  Button button_1 (.out(RST));
  // MIPS_RAM_part mips_ram_1: pin names not known; wires that end beside it: controlled_buffer_1_out, ex_mem_1_out_18, ex_mem_1_out_12[0], controlled_buffer_2_out, CLK, mips_ram_1_p6
  Pull_Resistor #(.pull(0)) pull_resistor_2 (.node(mips_ram_1_p6));
  and and_14 (and_14_out, ~comparator_7_lt, comparator_8_eq);  // AND_Gate
  and and_15 (and_15_out, ~comparator_7_lt, comparator_9_eq);  // AND_Gate
  IO io_1 (
    .data(ex_mem_1_out_18), .addr(controlled_buffer_5_out), .CLK(CLK), .out_5(_0xffff00), .out_6(_0xffff01),
    .out_8(_0xffff05), .out_9(_0xffff06), .out_10(_0xffff07), .out_11(_0xffff08), .out_12(_0xffff09),
    .out_13(_0xffff0a), .EN(ex_mem_1_out_12[0]), .out_7(_0xffff04));  // open: out_14, out_15
  Multiplexer #(.select(2), .width(5), .disabled("Z"), .enable("false")) multiplexer_21 (
    .in0({5{1'b0}}), .in1(5'b01000), .in2(5'b10000), .in3(5'b11000), .out(multiplexer_21_out),
    .sel(ex_mem_1_out_17[1:0]));
  assign controlled_buffer_6_out = and_15_out ? bit_extender_11_out : 32'bz;  // Controlled_Buffer controlled_buffer_6
  assign controlled_buffer_6_out = and_14_out ? bit_extender_12_out : 32'bz;  // Controlled_Buffer controlled_buffer_7
  Shifter #(.width(32), .shift("lr")) shifter_1 (.in(mips_ram_1_p6), .\dist (multiplexer_21_out), .out(shifter_1_out));
  Bit_Extender #(.in_width(32), .out_width(8), .\type ("zero")) bit_extender_13 (
    .in(_0xffff06), .out(bit_extender_13_out));
  assign controlled_buffer_6_out = comparator_7_lt ? shifter_1_out : 32'bz;  // Controlled_Buffer controlled_buffer_8
  Comparator #(.width(5), .mode("unsigned")) comparator_10 (
    .a(ex_mem_1_out_19), .b({5{1'b0}}), .gt(comparator_10_gt));  // open: eq, lt
  Comparator #(.width(5), .mode("twosComplement")) comparator_11 (
    .a(ex_mem_1_out_19), .b(rs), .eq(comparator_11_eq));  // open: gt, lt
  Comparator #(.width(5), .mode("twosComplement")) comparator_12 (
    .a(ex_mem_1_out_19), .b(rt), .eq(comparator_12_eq));  // open: gt, lt
  and and_16 (forward_rs[0], ex_mem_1_out_13[1], comparator_10_gt, comparator_11_eq);
  and and_17 (forward_rt[0], ex_mem_1_out_13[1], comparator_10_gt, comparator_12_eq);
  Comparator #(.width(8), .mode("twosComplement")) comparator_13 (
    .a(bit_extender_13_out), .b({8{1'b0}}), .gt(comparator_13_gt));  // open: eq, lt
  Adder #(.width(8)) adder_1 (.a(bit_extender_13_out), .b(8'h40), .out(adder_1_out));  // open: cin, cout
  MEM_WB mem_wb_1 (
    .in_6(controlled_buffer_6_out), .in_7(ex_mem_1_out_17), .CLK(CLK), .out_17(mem_wb_1_out_17),
    .out_18(mem_wb_1_out_18), .in_8(ex_mem_1_out_19), .out_19(mem_wb_1_out_19), .in_1(ex_mem_1_out_13),
    .out_12(mem_wb_1_out_12), .\使能端 (HALT), .PC(MEM_PC), .out_14(WB_PC), .IR(MEM_IR), .out_13(WB_IR));  // open: in_5, out_16, in_4, out_15, 同步清零
  assign controlled_buffer_9_out = comparator_13_gt ? adder_1_out : 8'bz;  // Controlled_Buffer controlled_buffer_9
  assign controlled_buffer_9_out = ~comparator_13_gt ? 8'h80 : 8'bz;  // Controlled_Buffer controlled_buffer_10
  // sound_emitter sound_emitter_1: pin names not known; wires that end beside it: in_1, controlled_buffer_9_out, in_2, 8'hb0
  Multiplexer #(.select(1), .width(32), .disabled("Z"), .enable("false")) multiplexer_22 (
    .in0(mem_wb_1_out_18), .in1(mem_wb_1_out_17), .out(multiplexer_22_out), .sel(mem_wb_1_out_12[0]));
  Comparator #(.width(5), .mode("unsigned")) comparator_14 (
    .a(mem_wb_1_out_19), .b({5{1'b0}}), .gt(comparator_14_gt));  // open: eq, lt
  Comparator #(.width(5), .mode("twosComplement")) comparator_15 (
    .a(mem_wb_1_out_19), .b(rs), .eq(comparator_15_eq));  // open: gt, lt
  Comparator #(.width(5), .mode("twosComplement")) comparator_16 (
    .a(mem_wb_1_out_19), .b(rt), .eq(comparator_16_eq));  // open: gt, lt
  and and_18 (forward_rs[1], mem_wb_1_out_12[1], comparator_14_gt, comparator_15_eq);
  and and_19 (forward_rt[1], mem_wb_1_out_12[1], comparator_14_gt, comparator_16_eq);

  // Other names for the same wires on the sheet: syscall = IR1; mem_forward_rs = forward_rs[0];
  //   wb_forward_rs = forward_rs[1]; mem_forward_rt = forward_rt[0]; wb_forward_rt = forward_rt[1]

  // Notes on the sheet:
  //   中断等待指示
  //   中断向量表
  //   中断源
  //   contents of rom_1 (hex, n*v repeats v):
  //   0 1000000 2000000 3000000
  //   数码管输出
  //   为方便自动评测，需要输出PC，IR，寄存器文件写入端口RDin，内存写入端口MDin等信号
  //   流水调试日志用
  //   设置条件分支历史初值
  //   停机相关电路
  //   指令字
  //   Index
  //   PC+4
  //   OP
  //   Func
  //   MF/MT
  //   Imm
  //   rs
  //   rt
  //   rd
  //   sa
  //   SignedExt
  //   LUI
  //   JMPI
  //   JR
  //   BLTZ
  //   MFC0
  //   MTC0
  //   LHU
  //   LB
  //   OP
  //   Func
  //   ERET
  //   Beq
  //   clear rt
  //   clear rs
  //   Bne
  //   AluOP
  //   AluSrcB
  //   RegWrite
  //   JAL
  //   RegDst
  //   MemToReg
  //   MemWrite
  //   W#
  //   R1
  //   R2
  //   sa
  //   W#
  //   PC+4
  //   EX
  //   Imm
  //   预测跳转
  //   命中
  //   预测一致
  //   JR
  //   JMPI
  //   ERET
  //   BEQ
  //   BNE
  //   BLTZ
  //   MTC0
  //   JAL
  //   ALUOP
  //   ALUsrcB
  //   MFC0
  //   direct PC+4
  //   LHU
  //   LB
  //   Keyboard
  //   Play music 
endmodule

module \Cache_全相联  (
  input  WE,
  input  CLK,
  input  [31:0] \分支地址及双预测位 ,
  input  [31:0] \写指令地址 ,
  input  [31:0] \读指令地址 ,
  output [1:0] \写指令分支预测历史 ,
  output [31:0] \目标地址 ,
  output \读指令预测分支 ,
  output HIT,
  output First_Write
);

  wire already_exist, bitselector_2_out, comparator_1_eq, comparator_2_eq, comparator_3_eq, comparator_4_eq,
       comparator_5_eq, comparator_6_eq, comparator_7_eq, comparator_8_eq, comparator_9_eq, comparator_10_eq,
       comparator_11_eq, comparator_12_eq, comparator_13_eq, comparator_14_eq, comparator_15_eq,
       comparator_16_eq, decoder_1_out0, decoder_1_out1, decoder_1_out2, decoder_1_out3, decoder_1_out4,
       decoder_1_out5, decoder_1_out6, decoder_1_out7, not_1_out, not_2_out, not_3_out, not_4_out, not_5_out,
       not_6_out, not_7_out, not_8_out, not_9_out, or_3_out, or_4_out, or_5_out, or_6_out, or_7_out,
       or_8_out, or_9_out, or_10_out, priority_encoder_1_gs, priority_encoder_3_en_out;
  wire [2:0] \max3_归并比较_1_max_num , \max3_归并比较_2_max_num , \max3_归并比较_3_max_num , \max3_归并比较_4_max_num ,
       \max3_归并比较_5_max_num , \max3_归并比较_6_max_num , \max3_归并比较_7_max_num , multiplexer_2_out,
       priority_encoder_1_out, priority_encoder_2_out, rR, rW;
  wire [4:0] bit_extender_1_out, bit_extender_2_out;
  wire [15:0] counter_1_q, counter_2_q, counter_3_q, counter_4_q, counter_5_q, counter_6_q, counter_7_q,
       counter_8_q, \max3_归并比较_1_max , \max3_归并比较_2_max , \max3_归并比较_3_max , \max3_归并比较_5_max ,
       \max3_归并比较_6_max , \max3_归并比较_7_max ;
  wire [31:0] or_1_out, or_2_out, register_1_q, register_2_q, register_3_q, register_4_q, register_5_q,
       register_6_q, register_7_q, register_8_q, registerfile_1_p7, registerfile_1_p8;

  // Probe on \分支地址及双预测位 
  assign bit_extender_1_out = {{2{1'b1}}, rW};  // Bit_Extender bit_extender_1
  assign bit_extender_2_out = {{2{1'b1}}, rR};  // Bit_Extender bit_extender_2
  // RegisterFile registerfile_1: pin names not known; wires that end beside it: \分支地址及双预测位 , CLK, WE, bit_extender_1_out, bit_extender_1_out, bit_extender_2_out, registerfile_1_p7, registerfile_1_p8
  Decoder #(.select(3), .tristate("false"), .disabled(0), .enable("true")) decoder_1 (
    .out0(decoder_1_out0), .out1(decoder_1_out1), .out2(decoder_1_out2), .out3(decoder_1_out3),
    .out4(decoder_1_out4), .out5(decoder_1_out5), .out6(decoder_1_out6), .out7(decoder_1_out7), .sel(rW),
    .en(WE));
  Multiplexer #(.select(1), .width(3), .disabled("Z"), .enable("false")) multiplexer_1 (
    .in0(priority_encoder_2_out), .in1(multiplexer_2_out), .out(rW), .sel(not_1_out));
  not not_1 (not_1_out, already_exist);
  Multiplexer #(.select(1), .width(3), .disabled("Z"), .enable("false")) multiplexer_2 (
    .in0(\max3_归并比较_4_max_num ), .in1(priority_encoder_1_out), .out(multiplexer_2_out),
    .sel(priority_encoder_1_gs));
  Pull_Resistor #(.pull(0)) pull_resistor_1 (.node(registerfile_1_p8));
  Priority_Encoder #(.select(3), .disabled("Z")) priority_encoder_1 (
    .in0(not_2_out), .in1(not_3_out), .in2(not_4_out), .in3(not_5_out), .in4(not_6_out), .in5(not_7_out),
    .in6(not_8_out), .in7(not_9_out), .out(priority_encoder_1_out), .gs(priority_encoder_1_gs));  // open: en_out, en_in
  assign or_1_out = 32'h80000000 | \读指令地址 ;  // OR_Gate or_1, 32 bits wide
  assign or_2_out = 32'h80000000 | \写指令地址 ;  // OR_Gate or_2, 32 bits wide
  BitSelector #(.width(32), .group(2)) bitselector_1 (.in(registerfile_1_p7), .out(\写指令分支预测历史 ), .sel(4'b0000));
  BitSelector #(.width(32), .group(1)) bitselector_2 (.in(registerfile_1_p8), .out(bitselector_2_out), .sel(5'b00001));
  assign \目标地址  = registerfile_1_p8 & 32'hfffffffc;  // AND_Gate and_1, 32 bits wide
  and and_2 (\读指令预测分支 , bitselector_2_out, HIT);
  Register #(.width(32), .trigger("falling"), .Select("low")) register_1 (
    .D(or_2_out), .en(decoder_1_out0), .Q(register_1_q), .clk(CLK));  // open: clr
  Register #(.width(32), .trigger("falling"), .Select("low")) register_2 (
    .D(or_2_out), .en(decoder_1_out1), .Q(register_2_q), .clk(CLK));  // open: clr
  Register #(.width(32), .trigger("falling"), .Select("low")) register_3 (
    .D(or_2_out), .en(decoder_1_out2), .Q(register_3_q), .clk(CLK));  // open: clr
  Register #(.width(32), .trigger("falling"), .Select("low")) register_4 (
    .D(or_2_out), .en(decoder_1_out3), .Q(register_4_q), .clk(CLK));  // open: clr
  Register #(.width(32), .trigger("falling"), .Select("low")) register_5 (
    .D(or_2_out), .en(decoder_1_out4), .Q(register_5_q), .clk(CLK));  // open: clr
  Register #(.width(32), .trigger("falling"), .Select("low")) register_6 (
    .D(or_2_out), .en(decoder_1_out5), .Q(register_6_q), .clk(CLK));  // open: clr
  Register #(.width(32), .trigger("falling"), .Select("low")) register_7 (
    .D(or_2_out), .en(decoder_1_out6), .Q(register_7_q), .clk(CLK));  // open: clr
  Register #(.width(32), .trigger("falling"), .Select("low")) register_8 (
    .D(or_2_out), .en(decoder_1_out7), .Q(register_8_q), .clk(CLK));  // open: clr
  Comparator #(.width(32), .mode("twosComplement")) comparator_1 (
    .a(or_2_out), .b(register_1_q), .eq(comparator_1_eq));  // open: gt, lt
  Comparator #(.width(32), .mode("twosComplement")) comparator_2 (
    .a(or_2_out), .b(register_2_q), .eq(comparator_2_eq));  // open: gt, lt
  Comparator #(.width(32), .mode("twosComplement")) comparator_3 (
    .a(or_2_out), .b(register_3_q), .eq(comparator_3_eq));  // open: gt, lt
  Comparator #(.width(32), .mode("twosComplement")) comparator_4 (
    .a(or_2_out), .b(register_4_q), .eq(comparator_4_eq));  // open: gt, lt
  Comparator #(.width(32), .mode("twosComplement")) comparator_5 (
    .a(or_2_out), .b(register_5_q), .eq(comparator_5_eq));  // open: gt, lt
  Comparator #(.width(32), .mode("twosComplement")) comparator_6 (
    .a(or_2_out), .b(register_6_q), .eq(comparator_6_eq));  // open: gt, lt
  Comparator #(.width(32), .mode("twosComplement")) comparator_7 (
    .a(or_2_out), .b(register_7_q), .eq(comparator_7_eq));  // open: gt, lt
  Comparator #(.width(32), .mode("twosComplement")) comparator_8 (
    .a(or_2_out), .b(register_8_q), .eq(comparator_8_eq));  // open: gt, lt
  not not_2 (not_2_out, register_1_q[31]);
  not not_3 (not_3_out, register_2_q[31]);
  not not_4 (not_4_out, register_3_q[31]);
  not not_5 (not_5_out, register_4_q[31]);
  not not_6 (not_6_out, register_5_q[31]);
  not not_7 (not_7_out, register_6_q[31]);
  not not_8 (not_8_out, register_7_q[31]);
  not not_9 (not_9_out, register_8_q[31]);
  Priority_Encoder #(.select(3), .disabled("Z")) priority_encoder_2 (
    .in0(comparator_1_eq), .in1(comparator_2_eq), .in2(comparator_3_eq), .in3(comparator_4_eq),
    .in4(comparator_5_eq), .in5(comparator_6_eq), .in6(comparator_7_eq), .in7(comparator_8_eq),
    .out(priority_encoder_2_out), .gs(already_exist), .en_out(First_Write));  // open: en_in
  Comparator #(.width(32), .mode("twosComplement")) comparator_9 (
    .a(register_1_q), .b(or_1_out), .eq(comparator_9_eq));  // open: gt, lt
  Comparator #(.width(32), .mode("twosComplement")) comparator_10 (
    .a(register_2_q), .b(or_1_out), .eq(comparator_10_eq));  // open: gt, lt
  Comparator #(.width(32), .mode("twosComplement")) comparator_11 (
    .a(register_3_q), .b(or_1_out), .eq(comparator_11_eq));  // open: gt, lt
  Comparator #(.width(32), .mode("twosComplement")) comparator_12 (
    .a(register_4_q), .b(or_1_out), .eq(comparator_12_eq));  // open: gt, lt
  Comparator #(.width(32), .mode("twosComplement")) comparator_13 (
    .a(register_5_q), .b(or_1_out), .eq(comparator_13_eq));  // open: gt, lt
  Comparator #(.width(32), .mode("twosComplement")) comparator_14 (
    .a(register_6_q), .b(or_1_out), .eq(comparator_14_eq));  // open: gt, lt
  Comparator #(.width(32), .mode("twosComplement")) comparator_15 (
    .a(register_7_q), .b(or_1_out), .eq(comparator_15_eq));  // open: gt, lt
  Comparator #(.width(32), .mode("twosComplement")) comparator_16 (
    .a(register_8_q), .b(or_1_out), .eq(comparator_16_eq));  // open: gt, lt
  or or_3 (or_3_out, decoder_1_out0, comparator_9_eq);
  \Max3_归并比较  \max3_归并比较_1  (
    .Y(counter_2_q), .X(counter_1_q), .Y_num(3'b001), .X_num(3'b000), .MAX(\max3_归并比较_1_max ),
    .Max_num(\max3_归并比较_1_max_num ));
  Counter #(.width(16), .max('hffff), .ongoal("stay"), .trigger("falling"), .behavior("new")) counter_1 (
    .load(or_3_out), .D({16{1'b0}}), .Q(counter_1_q), .clk(CLK));  // open: count, carry, clr, preset, down
  or or_4 (or_4_out, decoder_1_out1, comparator_10_eq);
  \Max3_归并比较  \max3_归并比较_2  (
    .Y(\max3_归并比较_3_max ), .X(\max3_归并比较_1_max ), .Y_num(\max3_归并比较_3_max_num ),
    .X_num(\max3_归并比较_1_max_num ), .MAX(\max3_归并比较_2_max ), .Max_num(\max3_归并比较_2_max_num ));
  Counter #(.width(16), .max('hffff), .ongoal("stay"), .trigger("falling"), .behavior("new")) counter_2 (
    .load(or_4_out), .D({16{1'b0}}), .Q(counter_2_q), .clk(CLK));  // open: count, carry, clr, preset, down
  or or_5 (or_5_out, decoder_1_out2, comparator_11_eq);
  \Max3_归并比较  \max3_归并比较_3  (
    .Y(counter_4_q), .X(counter_3_q), .Y_num(3'b011), .X_num(3'b010), .MAX(\max3_归并比较_3_max ),
    .Max_num(\max3_归并比较_3_max_num ));
  Counter #(.width(16), .max('hffff), .ongoal("stay"), .trigger("falling"), .behavior("new")) counter_3 (
    .load(or_5_out), .D({16{1'b0}}), .Q(counter_3_q), .clk(CLK));  // open: count, carry, clr, preset, down
  or or_6 (or_6_out, decoder_1_out3, comparator_12_eq);
  \Max3_归并比较  \max3_归并比较_4  (
    .Y(\max3_归并比较_6_max ), .X(\max3_归并比较_2_max ), .Y_num(\max3_归并比较_6_max_num ),
    .X_num(\max3_归并比较_2_max_num ), .Max_num(\max3_归并比较_4_max_num ));  // open: MAX
  Counter #(.width(16), .max('hffff), .ongoal("stay"), .trigger("falling"), .behavior("new")) counter_4 (
    .load(or_6_out), .D({16{1'b0}}), .Q(counter_4_q), .clk(CLK));  // open: count, carry, clr, preset, down
  or or_7 (or_7_out, decoder_1_out4, comparator_13_eq);
  \Max3_归并比较  \max3_归并比较_5  (
    .Y(counter_6_q), .X(counter_5_q), .Y_num(3'b101), .X_num(3'b100), .MAX(\max3_归并比较_5_max ),
    .Max_num(\max3_归并比较_5_max_num ));
  Counter #(.width(16), .max('hffff), .ongoal("stay"), .trigger("falling"), .behavior("new")) counter_5 (
    .load(or_7_out), .D({16{1'b0}}), .Q(counter_5_q), .clk(CLK));  // open: count, carry, clr, preset, down
  or or_8 (or_8_out, decoder_1_out5, comparator_14_eq);
  // Probe on \max3_归并比较_4_max_num 
  \Max3_归并比较  \max3_归并比较_6  (
    .Y(\max3_归并比较_7_max ), .X(\max3_归并比较_5_max ), .Y_num(\max3_归并比较_7_max_num ),
    .X_num(\max3_归并比较_5_max_num ), .MAX(\max3_归并比较_6_max ), .Max_num(\max3_归并比较_6_max_num ));
  Counter #(.width(16), .max('hffff), .ongoal("stay"), .trigger("falling"), .behavior("new")) counter_6 (
    .load(or_8_out), .D({16{1'b0}}), .Q(counter_6_q), .clk(CLK));  // open: count, carry, clr, preset, down
  or or_9 (or_9_out, decoder_1_out6, comparator_15_eq);
  \Max3_归并比较  \max3_归并比较_7  (
    .Y(counter_8_q), .X(counter_7_q), .Y_num(3'b111), .X_num(3'b110), .MAX(\max3_归并比较_7_max ),
    .Max_num(\max3_归并比较_7_max_num ));
  Counter #(.width(16), .max('hffff), .ongoal("stay"), .trigger("falling"), .behavior("new")) counter_7 (
    .load(or_9_out), .D({16{1'b0}}), .Q(counter_7_q), .clk(CLK));  // open: count, carry, clr, preset, down
  or or_10 (or_10_out, decoder_1_out7, comparator_16_eq);
  Counter #(.width(16), .max('hffff), .ongoal("stay"), .trigger("falling"), .behavior("new")) counter_8 (
    .load(or_10_out), .D({16{1'b0}}), .Q(counter_8_q), .clk(CLK));  // open: count, carry, clr, preset, down
  Priority_Encoder #(.select(3), .disabled("Z")) priority_encoder_3 (
    .in0(comparator_9_eq), .in1(comparator_10_eq), .in2(comparator_11_eq), .in3(comparator_12_eq),
    .in4(comparator_13_eq), .in5(comparator_14_eq), .in6(comparator_15_eq), .in7(comparator_16_eq), .out(rR),
    .en_out(priority_encoder_3_en_out));  // open: gs, en_in
  not not_10 (HIT, priority_encoder_3_en_out);
endmodule

// 单周期硬布线控制器
module \单周期硬布线控制器  (
  input  [5:0] OP,
  input  [5:0] Func,
  input  MT_MF,
  output [3:0] ALU_OP,
  output MemToReg,
  output MemWrite,
  output ALU_SRC,
  output SysCALL,
  output RegWrite,
  output SignedExt,
  output Beq,
  output RegDst,
  output Bne,
  output JR,
  output JMP,
  output JAL,
  output BLTZ,
  output LHU,
  output LUI,
  output LB,
  output MFC0,
  output ERET,
  output MTC0,
  output clear_rt,
  output clear_rs
);

  wire \中断信号自动生成_1_mcp0 , \控制信号自动生成_1_regdst , \控制信号自动生成_1_regwrite ;

  \运算控制器自动生成  \u_运算控制器自动生成_1  (
    .OP0(OP[0]), .OP1(OP[1]), .OP2(OP[2]), .OP3(OP[3]), .OP4(OP[4]), .OP5(OP[5]), .F0(Func[0]), .F1(Func[1]),
    .F2(Func[2]), .F3(Func[3]), .F4(Func[4]), .F5(Func[5]), .S0(ALU_OP[0]), .S1(ALU_OP[1]), .S2(ALU_OP[2]),
    .S3(ALU_OP[3]));
  \控制信号自动生成  \u_控制信号自动生成_1  (
    .OP0(OP[0]), .OP1(OP[1]), .OP2(OP[2]), .OP3(OP[3]), .OP4(OP[4]), .OP5(OP[5]), .F0(Func[0]), .F1(Func[1]),
    .F2(Func[2]), .F3(Func[3]), .F4(Func[4]), .F5(Func[5]), .MemToReg(MemToReg), .MemWrite(MemWrite),
    .ALU_SRC(ALU_SRC), .RegWrite(\控制信号自动生成_1_regwrite ), .SysCALL(SysCALL), .SignedExt(SignedExt),
    .RegDst(\控制信号自动生成_1_regdst ), .BEQ(Beq), .BNE(Bne), .JR(JR), .JUMP(JMP), .JAL(JAL));
  \拓展信号自动生成  \u_拓展信号自动生成_1  (
    .OP0(OP[0]), .BLTZ(BLTZ), .OP1(OP[1]), .OP2(OP[2]), .OP3(OP[3]), .LHU(LHU), .OP4(OP[4]), .OP5(OP[5]),
    .LUI(LUI), .F0(Func[0]), .F1(Func[1]), .F2(Func[2]), .F3(Func[3]), .F4(Func[4]), .LB(LB), .F5(Func[5]));
  \中断信号自动生成  \u_中断信号自动生成_1  (
    .OP0(OP[0]), .OP1(OP[1]), .OP2(OP[2]), .OP3(OP[3]), .OP4(OP[4]), .OP5(OP[5]), .F0(Func[0]), .F1(Func[1]),
    .F2(Func[2]), .F3(Func[3]), .F4(Func[4]), .F5(Func[5]), .MCP0(\中断信号自动生成_1_mcp0 ), .ERET(ERET));
  \rs_rt清零  \rs_rt清零_1  (
    .OP0(OP[0]), .OP1(OP[1]), .OP2(OP[2]), .OP3(OP[3]), .OP4(OP[4]), .OP5(OP[5]), .F0(Func[0]), .F1(Func[1]),
    .F2(Func[2]), .F3(Func[3]), .F4(Func[4]), .F5(Func[5]), .clearRt(clear_rt), .clearRs(clear_rs));
  Demultiplexer #(.select(1), .width(1), .tristate("false"), .disabled("Z"), .enable("false")) demultiplexer_1 (
    .out0(MFC0), .out1(MTC0), .in(\中断信号自动生成_1_mcp0 ), .sel(MT_MF));
  or or_1 (RegDst, \控制信号自动生成_1_regdst , MTC0);
  or or_2 (RegWrite, \控制信号自动生成_1_regwrite , MFC0);

  // Other names for the same wires on the sheet: OP_CODE[5:0] = OP

  // Notes on the sheet:
  //   运算器控制器，根据指令生成运算器功能选择信号
  //   控制信号生成，产生数据通路需要的其他控制信号
endmodule

// Max3
module \Max3_归并比较  (
  input  [15:0] Y,
  input  [15:0] X,
  input  [2:0] Y_num,
  input  [2:0] X_num,
  output [15:0] MAX,
  output [2:0] Max_num
);

  wire comparator_1_eq, comparator_1_gt, or_1_out;

  Multiplexer #(.select(1), .width(16), .disabled("Z"), .enable("false")) multiplexer_1 (
    .in0(Y), .in1(X), .out(MAX), .sel(or_1_out));
  Comparator #(.width(16), .mode("unsigned")) comparator_1 (
    .a(X), .b(Y), .gt(comparator_1_gt), .eq(comparator_1_eq));  // open: lt
  or or_1 (or_1_out, comparator_1_gt, comparator_1_eq);
  Multiplexer #(.select(1), .width(3), .disabled("Z"), .enable("false")) multiplexer_2 (
    .in0(Y_num), .in1(X_num), .out(Max_num), .sel(or_1_out));

  // Notes on the sheet:
  //   输出两个输入中的较大值，并输出较大值的3位编号
endmodule

// 运算器控制器
module \运算控制器自动生成  (
  input  OP0,
  input  OP1,
  input  OP2,
  input  OP3,
  input  OP4,
  input  OP5,
  input  F0,
  input  F1,
  input  F2,
  input  F3,
  input  F4,
  input  F5,
  output S0,
  output S1,
  output S2,
  output S3
);

  wire and_1_out, and_2_out, and_3_out, and_4_out, and_5_out, and_6_out, and_7_out, and_8_out, and_9_out,
       and_10_out, and_11_out, and_12_out, and_13_out, and_14_out, and_15_out, and_16_out, and_17_out,
       and_18_out, and_19_out, and_20_out, and_21_out, and_22_out, and_23_out, and_24_out, and_25_out,
       and_26_out, and_27_out, and_28_out, and_29_out, and_30_out, and_31_out, and_32_out, and_33_out,
       and_34_out, and_35_out, and_36_out, and_37_out, and_38_out, and_39_out, not_1_out, not_2_out,
       not_3_out, not_4_out, not_5_out, not_6_out, not_7_out, not_8_out, not_9_out, not_10_out, not_11_out,
       not_12_out, not_13_out, not_14_out, not_15_out, not_16_out, not_17_out, not_18_out, not_19_out,
       not_20_out, not_21_out, not_22_out, not_23_out, not_24_out, not_25_out, not_26_out, not_27_out,
       not_28_out, not_29_out, not_30_out, not_31_out, not_32_out, not_33_out, not_34_out, not_35_out,
       not_36_out, not_37_out, not_38_out, not_39_out, not_40_out, not_41_out, not_42_out, not_43_out,
       not_44_out, not_45_out, not_46_out, not_47_out, not_48_out, not_49_out, not_50_out, not_51_out,
       not_52_out, not_53_out, not_54_out, not_55_out, not_56_out, not_57_out, not_58_out, not_59_out,
       not_60_out, not_61_out, not_62_out, not_63_out, not_64_out, not_65_out, not_66_out, not_67_out,
       not_68_out, not_69_out, not_70_out, not_71_out, not_72_out, not_73_out, not_74_out, not_75_out,
       not_76_out, not_77_out, not_78_out, not_79_out, not_80_out, not_81_out, not_82_out, not_83_out,
       not_84_out, not_85_out, not_86_out, not_87_out, not_88_out, not_89_out, not_90_out, not_91_out,
       not_92_out, not_93_out, not_94_out, not_95_out, not_96_out, not_97_out, not_98_out, not_99_out,
       not_100_out, not_101_out, not_102_out, not_103_out, not_104_out, not_105_out, not_106_out,
       not_107_out, not_108_out, not_109_out, not_110_out, not_111_out, not_112_out, not_113_out,
       not_114_out, not_115_out, not_116_out, not_117_out, not_118_out, not_119_out, not_120_out,
       not_121_out, not_122_out, not_123_out, not_124_out, not_125_out, not_126_out, not_127_out,
       not_128_out, not_129_out, not_130_out, not_131_out, not_132_out, not_133_out, not_134_out,
       not_135_out, not_136_out, not_137_out, not_138_out, not_139_out, not_140_out, not_141_out,
       not_142_out, not_143_out, not_144_out, not_145_out, not_146_out, not_147_out, not_148_out,
       not_149_out, not_150_out, not_151_out, not_152_out, not_153_out, not_154_out, not_155_out,
       not_156_out, not_157_out, not_158_out, not_159_out, not_160_out, not_161_out, not_162_out,
       not_163_out, not_164_out, not_165_out, not_166_out, not_167_out, not_168_out, not_169_out,
       not_170_out, not_171_out, not_172_out, not_173_out, not_174_out, not_175_out, not_176_out,
       not_177_out, not_178_out, not_179_out, not_180_out, not_181_out, not_182_out, not_183_out,
       not_184_out, not_185_out, not_186_out, not_187_out, not_188_out, not_189_out, not_190_out,
       not_191_out, not_192_out, not_193_out, not_194_out, not_195_out, not_196_out, not_197_out,
       not_198_out, not_199_out, not_200_out, not_201_out, not_202_out, not_203_out, not_204_out,
       not_205_out, not_206_out, not_207_out, not_208_out, not_209_out, not_210_out, not_211_out,
       not_212_out, not_213_out, not_214_out, not_215_out, not_216_out, not_217_out, not_218_out,
       not_219_out, not_220_out, not_221_out, not_222_out, not_223_out, not_224_out, not_225_out,
       not_226_out, not_227_out, not_228_out, not_229_out, not_230_out, not_231_out, not_232_out,
       not_233_out, not_234_out, not_235_out, not_236_out, not_237_out, not_238_out, not_239_out,
       not_240_out, not_241_out, not_242_out, not_243_out, not_244_out, not_245_out, not_246_out;

  not not_1 (not_1_out, OP5);
  not not_2 (not_2_out, OP4);
  not not_3 (not_3_out, OP3);
  not not_4 (not_4_out, OP2);
  not not_5 (not_5_out, OP1);
  not not_6 (not_6_out, OP0);
  not not_7 (not_7_out, F5);
  not not_8 (not_8_out, F4);
  not not_9 (not_9_out, F3);
  not not_10 (not_10_out, F2);
  not not_11 (not_11_out, OP5);
  not not_12 (not_12_out, OP4);
  not not_13 (not_13_out, OP3);
  not not_14 (not_14_out, OP2);
  not not_15 (not_15_out, OP1);
  not not_16 (not_16_out, OP0);
  not not_17 (not_17_out, F4);
  not not_18 (not_18_out, F3);
  not not_19 (not_19_out, F2);
  not not_20 (not_20_out, F1);
  not not_21 (not_21_out, F0);
  not not_22 (not_22_out, OP5);
  not not_23 (not_23_out, OP4);
  not not_24 (not_24_out, OP3);
  not not_25 (not_25_out, OP2);
  not not_26 (not_26_out, OP1);
  not not_27 (not_27_out, OP0);
  not not_28 (not_28_out, F4);
  not not_29 (not_29_out, F3);
  not not_30 (not_30_out, F2);
  not not_31 (not_31_out, F1);
  not not_32 (not_32_out, OP5);
  not not_33 (not_33_out, OP4);
  not not_34 (not_34_out, OP3);
  not not_35 (not_35_out, OP2);
  not not_36 (not_36_out, OP1);
  not not_37 (not_37_out, OP0);
  not not_38 (not_38_out, F4);
  not not_39 (not_39_out, F3);
  not not_40 (not_40_out, F1);
  not not_41 (not_41_out, F0);
  not not_42 (not_42_out, OP5);
  not not_43 (not_43_out, OP4);
  not not_44 (not_44_out, OP3);
  not not_45 (not_45_out, OP2);
  not not_46 (not_46_out, OP1);
  not not_47 (not_47_out, OP0);
  not not_48 (not_48_out, F4);
  not not_49 (not_49_out, F2);
  not not_50 (not_50_out, F0);
  not not_51 (not_51_out, OP5);
  not not_52 (not_52_out, OP4);
  not not_53 (not_53_out, OP2);
  not not_54 (not_54_out, OP1);
  not not_55 (not_55_out, OP0);
  not not_56 (not_56_out, OP5);
  not not_57 (not_57_out, OP4);
  not not_58 (not_58_out, OP1);
  not not_59 (not_59_out, OP0);
  not not_60 (not_60_out, OP5);
  not not_61 (not_61_out, OP4);
  not not_62 (not_62_out, OP2);
  not not_63 (not_63_out, OP1);
  not not_64 (not_64_out, OP5);
  not not_65 (not_65_out, OP4);
  not not_66 (not_66_out, OP2);
  not not_67 (not_67_out, OP0);
  not not_68 (not_68_out, OP4);
  not not_69 (not_69_out, OP3);
  not not_70 (not_70_out, OP2);
  not not_71 (not_71_out, OP4);
  not not_72 (not_72_out, OP2);
  not not_73 (not_73_out, OP5);
  not not_74 (not_74_out, OP4);
  not not_75 (not_75_out, OP0);
  not not_76 (not_76_out, OP4);
  not not_77 (not_77_out, OP3);
  not not_78 (not_78_out, OP1);
  not not_79 (not_79_out, OP5);
  not not_80 (not_80_out, OP4);
  not not_81 (not_81_out, OP3);
  not not_82 (not_82_out, OP2);
  not not_83 (not_83_out, OP1);
  not not_84 (not_84_out, OP4);
  not not_85 (not_85_out, OP3);
  not not_86 (not_86_out, OP2);
  not not_87 (not_87_out, OP1);
  not not_88 (not_88_out, OP0);
  not not_89 (not_89_out, F5);
  not not_90 (not_90_out, F4);
  not not_91 (not_91_out, F3);
  not not_92 (not_92_out, F2);
  not not_93 (not_93_out, F1);
  not not_94 (not_94_out, F0);
  not not_95 (not_95_out, OP1);
  not not_96 (not_96_out, OP2);
  not not_97 (not_97_out, OP3);
  not not_98 (not_98_out, OP4);
  not not_99 (not_99_out, OP5);
  not not_100 (not_100_out, F0);
  not not_101 (not_101_out, F1);
  not not_102 (not_102_out, F3);
  not not_103 (not_103_out, F4);
  not not_104 (not_104_out, OP1);
  not not_105 (not_105_out, OP2);
  not not_106 (not_106_out, OP3);
  not not_107 (not_107_out, OP4);
  not not_108 (not_108_out, OP5);
  not not_109 (not_109_out, F0);
  not not_110 (not_110_out, F2);
  not not_111 (not_111_out, F3);
  not not_112 (not_112_out, F4);
  not not_113 (not_113_out, OP1);
  not not_114 (not_114_out, OP2);
  not not_115 (not_115_out, OP3);
  not not_116 (not_116_out, OP4);
  not not_117 (not_117_out, OP5);
  not not_118 (not_118_out, F0);
  not not_119 (not_119_out, F2);
  not not_120 (not_120_out, F4);
  not not_121 (not_121_out, OP1);
  not not_122 (not_122_out, OP2);
  not not_123 (not_123_out, OP3);
  not not_124 (not_124_out, OP4);
  not not_125 (not_125_out, OP5);
  not not_126 (not_126_out, F3);
  not not_127 (not_127_out, F4);
  not not_128 (not_128_out, OP0);
  not not_129 (not_129_out, OP1);
  not not_130 (not_130_out, OP4);
  not not_131 (not_131_out, OP5);
  not not_132 (not_132_out, OP0);
  not not_133 (not_133_out, OP2);
  not not_134 (not_134_out, OP4);
  not not_135 (not_135_out, OP5);
  not not_136 (not_136_out, OP1);
  not not_137 (not_137_out, OP2);
  not not_138 (not_138_out, OP3);
  not not_139 (not_139_out, OP4);
  not not_140 (not_140_out, OP5);
  not not_141 (not_141_out, OP5);
  not not_142 (not_142_out, OP4);
  not not_143 (not_143_out, OP3);
  not not_144 (not_144_out, OP2);
  not not_145 (not_145_out, OP1);
  not not_146 (not_146_out, OP0);
  not not_147 (not_147_out, F4);
  not not_148 (not_148_out, F3);
  not not_149 (not_149_out, F2);
  not not_150 (not_150_out, F1);
  not not_151 (not_151_out, F0);
  not not_152 (not_152_out, OP5);
  not not_153 (not_153_out, OP4);
  not not_154 (not_154_out, OP3);
  not not_155 (not_155_out, OP2);
  not not_156 (not_156_out, OP1);
  not not_157 (not_157_out, OP0);
  not not_158 (not_158_out, F4);
  not not_159 (not_159_out, F3);
  not not_160 (not_160_out, F2);
  not not_161 (not_161_out, F1);
  not not_162 (not_162_out, OP5);
  not not_163 (not_163_out, OP4);
  not not_164 (not_164_out, OP3);
  not not_165 (not_165_out, OP2);
  not not_166 (not_166_out, OP1);
  not not_167 (not_167_out, OP0);
  not not_168 (not_168_out, F4);
  not not_169 (not_169_out, F3);
  not not_170 (not_170_out, F2);
  not not_171 (not_171_out, F0);
  not not_172 (not_172_out, OP5);
  not not_173 (not_173_out, OP4);
  not not_174 (not_174_out, OP3);
  not not_175 (not_175_out, OP2);
  not not_176 (not_176_out, OP1);
  not not_177 (not_177_out, OP0);
  not not_178 (not_178_out, F4);
  not not_179 (not_179_out, F3);
  not not_180 (not_180_out, F1);
  not not_181 (not_181_out, F0);
  not not_182 (not_182_out, OP5);
  not not_183 (not_183_out, OP4);
  not not_184 (not_184_out, OP3);
  not not_185 (not_185_out, OP2);
  not not_186 (not_186_out, OP1);
  not not_187 (not_187_out, OP0);
  not not_188 (not_188_out, F4);
  not not_189 (not_189_out, F2);
  not not_190 (not_190_out, OP5);
  not not_191 (not_191_out, OP4);
  not not_192 (not_192_out, OP2);
  not not_193 (not_193_out, OP1);
  not not_194 (not_194_out, OP0);
  not not_195 (not_195_out, OP5);
  not not_196 (not_196_out, OP4);
  not not_197 (not_197_out, OP1);
  not not_198 (not_198_out, OP0);
  not not_199 (not_199_out, OP5);
  not not_200 (not_200_out, OP4);
  not not_201 (not_201_out, OP2);
  not not_202 (not_202_out, OP1);
  not not_203 (not_203_out, OP4);
  not not_204 (not_204_out, OP3);
  not not_205 (not_205_out, OP2);
  not not_206 (not_206_out, OP4);
  not not_207 (not_207_out, OP2);
  not not_208 (not_208_out, OP4);
  not not_209 (not_209_out, OP3);
  not not_210 (not_210_out, OP1);
  not not_211 (not_211_out, OP4);
  not not_212 (not_212_out, OP3);
  not not_213 (not_213_out, OP2);
  not not_214 (not_214_out, OP1);
  not not_215 (not_215_out, OP0);
  not not_216 (not_216_out, F5);
  not not_217 (not_217_out, F4);
  not not_218 (not_218_out, F3);
  not not_219 (not_219_out, F2);
  not not_220 (not_220_out, F1);
  not not_221 (not_221_out, F0);
  not not_222 (not_222_out, OP1);
  not not_223 (not_223_out, OP2);
  not not_224 (not_224_out, OP3);
  not not_225 (not_225_out, OP4);
  not not_226 (not_226_out, OP5);
  not not_227 (not_227_out, F2);
  not not_228 (not_228_out, F4);
  not not_229 (not_229_out, OP1);
  not not_230 (not_230_out, OP2);
  not not_231 (not_231_out, OP3);
  not not_232 (not_232_out, OP4);
  not not_233 (not_233_out, OP5);
  not not_234 (not_234_out, F3);
  not not_235 (not_235_out, F4);
  not not_236 (not_236_out, OP0);
  not not_237 (not_237_out, OP4);
  not not_238 (not_238_out, OP5);
  not not_239 (not_239_out, OP1);
  not not_240 (not_240_out, OP2);
  not not_241 (not_241_out, OP3);
  not not_242 (not_242_out, OP4);
  not not_243 (not_243_out, OP5);
  not not_244 (not_244_out, OP1);
  not not_245 (not_245_out, OP4);
  not not_246 (not_246_out, OP5);
  and and_1 (and_1_out, not_1_out, not_2_out, not_3_out, not_4_out, not_5_out, not_6_out, not_7_out, not_8_out, not_9_out, not_10_out, F1, F0);
  and and_2 (and_2_out, not_11_out, not_12_out, not_13_out, not_14_out, not_15_out, not_16_out, F5, not_17_out, not_18_out, not_19_out, not_20_out, not_21_out);
  and and_3 (and_3_out, not_22_out, not_23_out, not_24_out, not_25_out, not_26_out, not_27_out, F5, not_28_out, not_29_out, not_30_out, not_31_out, F0);
  and and_4 (and_4_out, not_32_out, not_33_out, not_34_out, not_35_out, not_36_out, not_37_out, F5, not_38_out, not_39_out, F2, not_40_out, not_41_out);
  and and_5 (and_5_out, not_42_out, not_43_out, not_44_out, not_45_out, not_46_out, not_47_out, F5, not_48_out, F3, not_49_out, F1, not_50_out);
  and and_6 (and_6_out, not_51_out, not_52_out, OP3, not_53_out, not_54_out, not_55_out);
  and and_7 (and_7_out, not_56_out, not_57_out, OP3, OP2, not_58_out, not_59_out);
  and and_8 (and_8_out, not_60_out, not_61_out, OP3, not_62_out, not_63_out, OP0);
  and and_9 (and_9_out, not_64_out, not_65_out, OP3, not_66_out, OP1, not_67_out);
  and and_10 (and_10_out, OP5, not_68_out, not_69_out, not_70_out, OP1, OP0);
  and and_11 (and_11_out, OP5, not_71_out, OP3, not_72_out, OP1, OP0);
  and and_12 (and_12_out, not_73_out, not_74_out, OP3, OP2, OP1, not_75_out);
  and and_13 (and_13_out, OP5, not_76_out, not_77_out, OP2, not_78_out, OP0);
  and and_14 (and_14_out, not_79_out, not_80_out, not_81_out, not_82_out, not_83_out, OP0);
  and and_15 (and_15_out, OP5, not_84_out, not_85_out, not_86_out, not_87_out, not_88_out, not_89_out, not_90_out, not_91_out, not_92_out, not_93_out, not_94_out);
  and and_16 (and_16_out, not_95_out, not_96_out, not_97_out, not_98_out, not_99_out, not_100_out, not_101_out, F2, not_102_out, not_103_out, F5);
  and and_17 (and_17_out, not_104_out, not_105_out, not_106_out, not_107_out, not_108_out, not_109_out, F1, not_110_out, not_111_out, not_112_out);
  and and_18 (and_18_out, not_113_out, not_114_out, not_115_out, not_116_out, not_117_out, not_118_out, F1, not_119_out, not_120_out, F5);
  and and_19 (and_19_out, not_121_out, not_122_out, not_123_out, not_124_out, not_125_out, F0, F1, F2, not_126_out, not_127_out, F5);
  and and_20 (and_20_out, not_128_out, not_129_out, OP2, OP3, not_130_out, not_131_out);
  and and_21 (and_21_out, not_132_out, OP1, not_133_out, OP3, not_134_out, not_135_out);
  and and_22 (and_22_out, OP0, not_136_out, not_137_out, not_138_out, not_139_out, not_140_out);
  and and_23 (and_23_out, not_141_out, not_142_out, not_143_out, not_144_out, not_145_out, not_146_out, F5, not_147_out, not_148_out, not_149_out, not_150_out, not_151_out);
  and and_24 (and_24_out, not_152_out, not_153_out, not_154_out, not_155_out, not_156_out, not_157_out, F5, not_158_out, not_159_out, not_160_out, not_161_out, F0);
  and and_25 (and_25_out, not_162_out, not_163_out, not_164_out, not_165_out, not_166_out, not_167_out, F5, not_168_out, not_169_out, not_170_out, F1, not_171_out);
  and and_26 (and_26_out, not_172_out, not_173_out, not_174_out, not_175_out, not_176_out, not_177_out, F5, not_178_out, not_179_out, F2, not_180_out, not_181_out);
  and and_27 (and_27_out, not_182_out, not_183_out, not_184_out, not_185_out, not_186_out, not_187_out, F5, not_188_out, F3, not_189_out, F1, F0);
  and and_28 (and_28_out, not_190_out, not_191_out, OP3, not_192_out, not_193_out, not_194_out);
  and and_29 (and_29_out, not_195_out, not_196_out, OP3, OP2, not_197_out, not_198_out);
  and and_30 (and_30_out, not_199_out, not_200_out, OP3, not_201_out, not_202_out, OP0);
  and and_31 (and_31_out, OP5, not_203_out, not_204_out, not_205_out, OP1, OP0);
  and and_32 (and_32_out, OP5, not_206_out, OP3, not_207_out, OP1, OP0);
  and and_33 (and_33_out, OP5, not_208_out, not_209_out, OP2, not_210_out, OP0);
  and and_34 (and_34_out, OP5, not_211_out, not_212_out, not_213_out, not_214_out, not_215_out, not_216_out, not_217_out, not_218_out, not_219_out, not_220_out, not_221_out);
  and and_35 (and_35_out, not_222_out, not_223_out, not_224_out, not_225_out, not_226_out, F1, not_227_out, F3, not_228_out, F5);
  and and_36 (and_36_out, not_229_out, not_230_out, not_231_out, not_232_out, not_233_out, F0, F2, not_234_out, not_235_out, F5);
  and and_37 (and_37_out, not_236_out, OP1, OP3, not_237_out, not_238_out);
  and and_38 (and_38_out, OP0, not_239_out, not_240_out, not_241_out, not_242_out, not_243_out);
  and and_39 (and_39_out, OP0, not_244_out, OP2, OP3, not_245_out, not_246_out);
  or or_1 (S1, and_16_out, and_17_out, and_18_out, and_19_out, and_20_out, and_21_out, and_22_out);
  or or_2 (S3, and_35_out, and_36_out, and_37_out, and_38_out, and_39_out);
  or or_3 (S0, and_1_out, and_2_out, and_3_out, and_4_out, and_5_out, and_6_out, and_7_out, and_8_out, and_9_out, and_10_out, and_11_out, and_12_out, and_13_out, and_14_out, and_15_out);
  or or_4 (S2, and_23_out, and_24_out, and_25_out, and_26_out, and_27_out, and_28_out, and_29_out, and_30_out, and_31_out, and_32_out, and_33_out, and_34_out);
endmodule

// 控制信号生成
module \控制信号自动生成  (
  input  OP0,
  input  OP1,
  input  OP2,
  input  OP3,
  input  OP4,
  input  OP5,
  input  F0,
  input  F1,
  input  F2,
  input  F3,
  input  F4,
  input  F5,
  output MemToReg,
  output MemWrite,
  output ALU_SRC,
  output RegWrite,
  output SysCALL,
  output SignedExt,
  output RegDst,
  output BEQ,
  output BNE,
  output JR,
  output JUMP,
  output JAL
);

  wire and_1_out, and_2_out, and_3_out, and_5_out, and_6_out, and_7_out, and_8_out, and_9_out, and_10_out,
       and_11_out, and_12_out, and_13_out, and_14_out, and_15_out, and_16_out, and_17_out, and_18_out,
       and_19_out, and_20_out, and_21_out, and_22_out, and_23_out, and_24_out, and_25_out, and_26_out,
       and_27_out, and_28_out, and_29_out, and_30_out, and_31_out, and_32_out, and_33_out, and_34_out,
       and_35_out, and_36_out, and_37_out, and_39_out, and_40_out, and_41_out, and_42_out, and_43_out,
       and_44_out, and_45_out, and_46_out, and_47_out, and_48_out, and_49_out, and_50_out, and_51_out,
       and_52_out, and_53_out, not_1_out, not_2_out, not_3_out, not_4_out, not_5_out, not_6_out, not_7_out,
       not_8_out, not_9_out, not_10_out, not_11_out, not_12_out, not_13_out, not_14_out, not_15_out,
       not_16_out, not_17_out, not_18_out, not_19_out, not_20_out, not_21_out, not_22_out, not_23_out,
       not_24_out, not_25_out, not_26_out, not_27_out, not_28_out, not_29_out, not_30_out, not_31_out,
       not_32_out, not_33_out, not_34_out, not_35_out, not_36_out, not_37_out, not_38_out, not_39_out,
       not_40_out, not_41_out, not_42_out, not_43_out, not_44_out, not_45_out, not_46_out, not_47_out,
       not_48_out, not_49_out, not_50_out, not_51_out, not_52_out, not_53_out, not_54_out, not_55_out,
       not_56_out, not_57_out, not_58_out, not_59_out, not_60_out, not_61_out, not_62_out, not_63_out,
       not_64_out, not_65_out, not_66_out, not_67_out, not_68_out, not_69_out, not_70_out, not_71_out,
       not_72_out, not_73_out, not_74_out, not_75_out, not_76_out, not_77_out, not_78_out, not_79_out,
       not_80_out, not_81_out, not_82_out, not_83_out, not_84_out, not_85_out, not_86_out, not_87_out,
       not_88_out, not_89_out, not_90_out, not_91_out, not_92_out, not_93_out, not_94_out, not_95_out,
       not_96_out, not_97_out, not_98_out, not_99_out, not_100_out, not_101_out, not_102_out, not_103_out,
       not_104_out, not_105_out, not_106_out, not_107_out, not_108_out, not_109_out, not_110_out,
       not_111_out, not_112_out, not_113_out, not_114_out, not_115_out, not_116_out, not_117_out,
       not_118_out, not_119_out, not_120_out, not_121_out, not_122_out, not_123_out, not_124_out,
       not_125_out, not_126_out, not_127_out, not_128_out, not_129_out, not_130_out, not_131_out,
       not_132_out, not_133_out, not_134_out, not_135_out, not_136_out, not_137_out, not_138_out,
       not_139_out, not_140_out, not_141_out, not_142_out, not_143_out, not_144_out, not_145_out,
       not_146_out, not_147_out, not_148_out, not_149_out, not_150_out, not_151_out, not_152_out,
       not_153_out, not_154_out, not_155_out, not_156_out, not_157_out, not_158_out, not_159_out,
       not_160_out, not_161_out, not_162_out, not_163_out, not_164_out, not_165_out, not_166_out,
       not_167_out, not_168_out, not_169_out, not_170_out, not_171_out, not_172_out, not_173_out,
       not_174_out, not_175_out, not_176_out, not_177_out, not_178_out, not_179_out, not_180_out,
       not_181_out, not_182_out, not_183_out, not_184_out, not_185_out, not_186_out, not_187_out,
       not_188_out, not_189_out, not_190_out, not_191_out, not_192_out, not_193_out, not_194_out,
       not_195_out, not_196_out, not_197_out, not_198_out, not_199_out, not_200_out, not_201_out,
       not_202_out, not_203_out, not_204_out, not_205_out, not_206_out, not_207_out, not_208_out,
       not_209_out, not_210_out, not_211_out, not_212_out, not_213_out, not_214_out, not_215_out,
       not_216_out, not_217_out, not_218_out, not_219_out, not_220_out, not_221_out, not_222_out,
       not_223_out, not_224_out, not_225_out, not_226_out, not_227_out, not_228_out, not_229_out,
       not_230_out, not_231_out, not_232_out, not_233_out, not_234_out, not_235_out, not_236_out,
       not_237_out, not_238_out, not_239_out, not_240_out, not_241_out, not_242_out, not_243_out,
       not_244_out, not_245_out, not_246_out, not_247_out, not_248_out, not_249_out, not_250_out,
       not_251_out, not_252_out, not_253_out, not_254_out, not_255_out, not_256_out, not_257_out,
       not_258_out, not_259_out, not_260_out, not_261_out, not_262_out, not_263_out, not_264_out,
       not_265_out, not_266_out, not_267_out, not_268_out, not_269_out, not_270_out, not_271_out,
       not_272_out, not_273_out, not_274_out, not_275_out, not_276_out, not_277_out, not_278_out,
       not_279_out, not_280_out, not_281_out, not_282_out, not_283_out, not_284_out, not_285_out,
       not_286_out, not_287_out, not_288_out, not_289_out, not_290_out, not_291_out, not_292_out,
       not_293_out, not_294_out, not_295_out, not_296_out, not_297_out, not_298_out, not_299_out,
       not_300_out, not_301_out, not_302_out, not_303_out, not_304_out, not_305_out, not_306_out,
       not_307_out, not_308_out, not_309_out, not_310_out, not_311_out, not_312_out, not_313_out,
       not_314_out, not_315_out, not_316_out, not_317_out, not_318_out, not_319_out, not_320_out,
       not_321_out, not_322_out, not_323_out, not_324_out, not_325_out, not_326_out, not_327_out,
       not_328_out, not_329_out, not_330_out, not_331_out, not_332_out, not_333_out, not_334_out,
       not_335_out, not_336_out, not_337_out, not_338_out, not_339_out, not_340_out, not_341_out,
       not_342_out, not_343_out, not_344_out, not_345_out, not_346_out;

  not not_1 (not_1_out, OP4);
  not not_2 (not_2_out, OP3);
  not not_3 (not_3_out, OP2);
  not not_4 (not_4_out, OP4);
  not not_5 (not_5_out, OP3);
  not not_6 (not_6_out, OP1);
  not not_7 (not_7_out, OP4);
  not not_8 (not_8_out, OP3);
  not not_9 (not_9_out, OP2);
  not not_10 (not_10_out, OP1);
  not not_11 (not_11_out, OP0);
  not not_12 (not_12_out, F5);
  not not_13 (not_13_out, F4);
  not not_14 (not_14_out, F3);
  not not_15 (not_15_out, F2);
  not not_16 (not_16_out, F1);
  not not_17 (not_17_out, F0);
  not not_18 (not_18_out, OP2);
  not not_19 (not_19_out, OP4);
  not not_20 (not_20_out, OP5);
  not not_21 (not_21_out, OP4);
  not not_22 (not_22_out, OP2);
  not not_23 (not_23_out, OP1);
  not not_24 (not_24_out, OP0);
  not not_25 (not_25_out, OP5);
  not not_26 (not_26_out, OP4);
  not not_27 (not_27_out, OP1);
  not not_28 (not_28_out, OP0);
  not not_29 (not_29_out, OP5);
  not not_30 (not_30_out, OP4);
  not not_31 (not_31_out, OP2);
  not not_32 (not_32_out, OP1);
  not not_33 (not_33_out, OP5);
  not not_34 (not_34_out, OP4);
  not not_35 (not_35_out, OP2);
  not not_36 (not_36_out, OP0);
  not not_37 (not_37_out, OP5);
  not not_38 (not_38_out, OP4);
  not not_39 (not_39_out, OP1);
  not not_40 (not_40_out, OP4);
  not not_41 (not_41_out, OP3);
  not not_42 (not_42_out, OP2);
  not not_43 (not_43_out, OP4);
  not not_44 (not_44_out, OP2);
  not not_45 (not_45_out, OP5);
  not not_46 (not_46_out, OP4);
  not not_47 (not_47_out, OP0);
  not not_48 (not_48_out, OP5);
  not not_49 (not_49_out, OP4);
  not not_50 (not_50_out, OP4);
  not not_51 (not_51_out, OP3);
  not not_52 (not_52_out, OP1);
  not not_53 (not_53_out, OP4);
  not not_54 (not_54_out, OP3);
  not not_55 (not_55_out, OP2);
  not not_56 (not_56_out, OP1);
  not not_57 (not_57_out, OP0);
  not not_58 (not_58_out, F5);
  not not_59 (not_59_out, F4);
  not not_60 (not_60_out, F3);
  not not_61 (not_61_out, F2);
  not not_62 (not_62_out, F1);
  not not_63 (not_63_out, F0);
  not not_64 (not_64_out, OP5);
  not not_65 (not_65_out, OP4);
  not not_66 (not_66_out, OP3);
  not not_67 (not_67_out, OP2);
  not not_68 (not_68_out, OP1);
  not not_69 (not_69_out, OP0);
  not not_70 (not_70_out, F5);
  not not_71 (not_71_out, F4);
  not not_72 (not_72_out, F3);
  not not_73 (not_73_out, F2);
  not not_74 (not_74_out, F1);
  not not_75 (not_75_out, F0);
  not not_76 (not_76_out, OP5);
  not not_77 (not_77_out, OP4);
  not not_78 (not_78_out, OP3);
  not not_79 (not_79_out, OP2);
  not not_80 (not_80_out, OP1);
  not not_81 (not_81_out, OP0);
  not not_82 (not_82_out, F5);
  not not_83 (not_83_out, F4);
  not not_84 (not_84_out, F3);
  not not_85 (not_85_out, F2);
  not not_86 (not_86_out, OP5);
  not not_87 (not_87_out, OP4);
  not not_88 (not_88_out, OP3);
  not not_89 (not_89_out, OP2);
  not not_90 (not_90_out, OP1);
  not not_91 (not_91_out, OP0);
  not not_92 (not_92_out, F5);
  not not_93 (not_93_out, F4);
  not not_94 (not_94_out, F3);
  not not_95 (not_95_out, F2);
  not not_96 (not_96_out, F0);
  not not_97 (not_97_out, OP5);
  not not_98 (not_98_out, OP4);
  not not_99 (not_99_out, OP3);
  not not_100 (not_100_out, OP2);
  not not_101 (not_101_out, OP1);
  not not_102 (not_102_out, OP0);
  not not_103 (not_103_out, F4);
  not not_104 (not_104_out, F3);
  not not_105 (not_105_out, F2);
  not not_106 (not_106_out, F1);
  not not_107 (not_107_out, F0);
  not not_108 (not_108_out, OP5);
  not not_109 (not_109_out, OP4);
  not not_110 (not_110_out, OP3);
  not not_111 (not_111_out, OP2);
  not not_112 (not_112_out, OP1);
  not not_113 (not_113_out, OP0);
  not not_114 (not_114_out, F4);
  not not_115 (not_115_out, F3);
  not not_116 (not_116_out, F2);
  not not_117 (not_117_out, F1);
  not not_118 (not_118_out, OP5);
  not not_119 (not_119_out, OP4);
  not not_120 (not_120_out, OP3);
  not not_121 (not_121_out, OP2);
  not not_122 (not_122_out, OP1);
  not not_123 (not_123_out, OP0);
  not not_124 (not_124_out, F4);
  not not_125 (not_125_out, F3);
  not not_126 (not_126_out, F2);
  not not_127 (not_127_out, F0);
  not not_128 (not_128_out, OP5);
  not not_129 (not_129_out, OP4);
  not not_130 (not_130_out, OP3);
  not not_131 (not_131_out, OP2);
  not not_132 (not_132_out, OP1);
  not not_133 (not_133_out, OP0);
  not not_134 (not_134_out, F4);
  not not_135 (not_135_out, F3);
  not not_136 (not_136_out, F1);
  not not_137 (not_137_out, F0);
  not not_138 (not_138_out, OP5);
  not not_139 (not_139_out, OP4);
  not not_140 (not_140_out, OP3);
  not not_141 (not_141_out, OP2);
  not not_142 (not_142_out, OP1);
  not not_143 (not_143_out, OP0);
  not not_144 (not_144_out, F4);
  not not_145 (not_145_out, F3);
  not not_146 (not_146_out, F1);
  not not_147 (not_147_out, OP5);
  not not_148 (not_148_out, OP4);
  not not_149 (not_149_out, OP3);
  not not_150 (not_150_out, OP2);
  not not_151 (not_151_out, OP1);
  not not_152 (not_152_out, OP0);
  not not_153 (not_153_out, F4);
  not not_154 (not_154_out, F3);
  not not_155 (not_155_out, OP5);
  not not_156 (not_156_out, OP4);
  not not_157 (not_157_out, OP3);
  not not_158 (not_158_out, OP2);
  not not_159 (not_159_out, OP1);
  not not_160 (not_160_out, OP0);
  not not_161 (not_161_out, F4);
  not not_162 (not_162_out, F2);
  not not_163 (not_163_out, F0);
  not not_164 (not_164_out, OP5);
  not not_165 (not_165_out, OP4);
  not not_166 (not_166_out, OP3);
  not not_167 (not_167_out, OP2);
  not not_168 (not_168_out, OP1);
  not not_169 (not_169_out, OP0);
  not not_170 (not_170_out, F4);
  not not_171 (not_171_out, F2);
  not not_172 (not_172_out, OP5);
  not not_173 (not_173_out, OP4);
  not not_174 (not_174_out, OP3);
  not not_175 (not_175_out, OP2);
  not not_176 (not_176_out, OP5);
  not not_177 (not_177_out, OP4);
  not not_178 (not_178_out, OP2);
  not not_179 (not_179_out, OP1);
  not not_180 (not_180_out, OP0);
  not not_181 (not_181_out, OP5);
  not not_182 (not_182_out, OP4);
  not not_183 (not_183_out, OP1);
  not not_184 (not_184_out, OP0);
  not not_185 (not_185_out, OP5);
  not not_186 (not_186_out, OP4);
  not not_187 (not_187_out, OP2);
  not not_188 (not_188_out, OP1);
  not not_189 (not_189_out, OP5);
  not not_190 (not_190_out, OP4);
  not not_191 (not_191_out, OP2);
  not not_192 (not_192_out, OP0);
  not not_193 (not_193_out, OP5);
  not not_194 (not_194_out, OP4);
  not not_195 (not_195_out, OP1);
  not not_196 (not_196_out, OP4);
  not not_197 (not_197_out, OP3);
  not not_198 (not_198_out, OP2);
  not not_199 (not_199_out, OP5);
  not not_200 (not_200_out, OP4);
  not not_201 (not_201_out, OP0);
  not not_202 (not_202_out, OP5);
  not not_203 (not_203_out, OP4);
  not not_204 (not_204_out, OP4);
  not not_205 (not_205_out, OP3);
  not not_206 (not_206_out, OP1);
  not not_207 (not_207_out, OP4);
  not not_208 (not_208_out, OP3);
  not not_209 (not_209_out, OP2);
  not not_210 (not_210_out, OP1);
  not not_211 (not_211_out, OP0);
  not not_212 (not_212_out, F5);
  not not_213 (not_213_out, F4);
  not not_214 (not_214_out, F3);
  not not_215 (not_215_out, F2);
  not not_216 (not_216_out, F1);
  not not_217 (not_217_out, F0);
  not not_218 (not_218_out, OP0);
  not not_219 (not_219_out, OP1);
  not not_220 (not_220_out, OP2);
  not not_221 (not_221_out, OP3);
  not not_222 (not_222_out, OP4);
  not not_223 (not_223_out, OP5);
  not not_224 (not_224_out, F0);
  not not_225 (not_225_out, F1);
  not not_226 (not_226_out, F4);
  not not_227 (not_227_out, F5);
  not not_228 (not_228_out, OP5);
  not not_229 (not_229_out, OP4);
  not not_230 (not_230_out, OP3);
  not not_231 (not_231_out, OP1);
  not not_232 (not_232_out, OP0);
  not not_233 (not_233_out, OP5);
  not not_234 (not_234_out, OP4);
  not not_235 (not_235_out, OP3);
  not not_236 (not_236_out, OP1);
  not not_237 (not_237_out, OP5);
  not not_238 (not_238_out, OP4);
  not not_239 (not_239_out, OP2);
  not not_240 (not_240_out, OP1);
  not not_241 (not_241_out, OP0);
  not not_242 (not_242_out, OP5);
  not not_243 (not_243_out, OP4);
  not not_244 (not_244_out, OP2);
  not not_245 (not_245_out, OP1);
  not not_246 (not_246_out, OP5);
  not not_247 (not_247_out, OP4);
  not not_248 (not_248_out, OP2);
  not not_249 (not_249_out, OP0);
  not not_250 (not_250_out, OP4);
  not not_251 (not_251_out, OP3);
  not not_252 (not_252_out, OP2);
  not not_253 (not_253_out, OP4);
  not not_254 (not_254_out, OP2);
  not not_255 (not_255_out, OP4);
  not not_256 (not_256_out, OP3);
  not not_257 (not_257_out, OP1);
  not not_258 (not_258_out, OP5);
  not not_259 (not_259_out, OP4);
  not not_260 (not_260_out, OP3);
  not not_261 (not_261_out, OP2);
  not not_262 (not_262_out, OP1);
  not not_263 (not_263_out, OP4);
  not not_264 (not_264_out, OP3);
  not not_265 (not_265_out, OP2);
  not not_266 (not_266_out, OP1);
  not not_267 (not_267_out, OP0);
  not not_268 (not_268_out, F5);
  not not_269 (not_269_out, F4);
  not not_270 (not_270_out, F3);
  not not_271 (not_271_out, F2);
  not not_272 (not_272_out, F1);
  not not_273 (not_273_out, F0);
  not not_274 (not_274_out, OP0);
  not not_275 (not_275_out, OP1);
  not not_276 (not_276_out, OP2);
  not not_277 (not_277_out, OP3);
  not not_278 (not_278_out, OP4);
  not not_279 (not_279_out, OP5);
  not not_280 (not_280_out, F0);
  not not_281 (not_281_out, F2);
  not not_282 (not_282_out, F3);
  not not_283 (not_283_out, F4);
  not not_284 (not_284_out, OP0);
  not not_285 (not_285_out, OP1);
  not not_286 (not_286_out, OP2);
  not not_287 (not_287_out, OP3);
  not not_288 (not_288_out, OP4);
  not not_289 (not_289_out, OP5);
  not not_290 (not_290_out, F1);
  not not_291 (not_291_out, F3);
  not not_292 (not_292_out, F4);
  not not_293 (not_293_out, OP0);
  not not_294 (not_294_out, OP1);
  not not_295 (not_295_out, OP2);
  not not_296 (not_296_out, OP3);
  not not_297 (not_297_out, OP4);
  not not_298 (not_298_out, OP5);
  not not_299 (not_299_out, F2);
  not not_300 (not_300_out, F3);
  not not_301 (not_301_out, F4);
  not not_302 (not_302_out, F5);
  not not_303 (not_303_out, OP0);
  not not_304 (not_304_out, OP1);
  not not_305 (not_305_out, OP2);
  not not_306 (not_306_out, OP3);
  not not_307 (not_307_out, OP4);
  not not_308 (not_308_out, OP5);
  not not_309 (not_309_out, F2);
  not not_310 (not_310_out, F4);
  not not_311 (not_311_out, OP0);
  not not_312 (not_312_out, OP1);
  not not_313 (not_313_out, OP2);
  not not_314 (not_314_out, OP3);
  not not_315 (not_315_out, OP4);
  not not_316 (not_316_out, OP5);
  not not_317 (not_317_out, F3);
  not not_318 (not_318_out, F4);
  not not_319 (not_319_out, OP0);
  not not_320 (not_320_out, OP1);
  not not_321 (not_321_out, OP3);
  not not_322 (not_322_out, OP4);
  not not_323 (not_323_out, OP5);
  not not_324 (not_324_out, OP1);
  not not_325 (not_325_out, OP3);
  not not_326 (not_326_out, OP4);
  not not_327 (not_327_out, OP5);
  not not_328 (not_328_out, OP0);
  not not_329 (not_329_out, OP1);
  not not_330 (not_330_out, OP2);
  not not_331 (not_331_out, OP3);
  not not_332 (not_332_out, OP4);
  not not_333 (not_333_out, OP5);
  not not_334 (not_334_out, F0);
  not not_335 (not_335_out, F1);
  not not_336 (not_336_out, F2);
  not not_337 (not_337_out, F4);
  not not_338 (not_338_out, F5);
  not not_339 (not_339_out, OP2);
  not not_340 (not_340_out, OP3);
  not not_341 (not_341_out, OP4);
  not not_342 (not_342_out, OP5);
  not not_343 (not_343_out, OP2);
  not not_344 (not_344_out, OP3);
  not not_345 (not_345_out, OP4);
  not not_346 (not_346_out, OP5);
  and and_1 (and_1_out, OP5, not_1_out, not_2_out, not_3_out, OP1, OP0);
  and and_2 (and_2_out, OP5, not_4_out, not_5_out, OP2, not_6_out, OP0);
  and and_3 (and_3_out, OP5, not_7_out, not_8_out, not_9_out, not_10_out, not_11_out, not_12_out, not_13_out, not_14_out, not_15_out, not_16_out, not_17_out);
  and and_4 (MemWrite, OP0, OP1, not_18_out, OP3, not_19_out, OP5);
  and and_5 (and_5_out, not_20_out, not_21_out, OP3, not_22_out, not_23_out, not_24_out);
  and and_6 (and_6_out, not_25_out, not_26_out, OP3, OP2, not_27_out, not_28_out);
  and and_7 (and_7_out, not_29_out, not_30_out, OP3, not_31_out, not_32_out, OP0);
  and and_8 (and_8_out, not_33_out, not_34_out, OP3, not_35_out, OP1, not_36_out);
  and and_9 (and_9_out, not_37_out, not_38_out, OP3, OP2, not_39_out, OP0);
  and and_10 (and_10_out, OP5, not_40_out, not_41_out, not_42_out, OP1, OP0);
  and and_11 (and_11_out, OP5, not_43_out, OP3, not_44_out, OP1, OP0);
  and and_12 (and_12_out, not_45_out, not_46_out, OP3, OP2, OP1, not_47_out);
  and and_13 (and_13_out, not_48_out, not_49_out, OP3, OP2, OP1, OP0);
  and and_14 (and_14_out, OP5, not_50_out, not_51_out, OP2, not_52_out, OP0);
  and and_15 (and_15_out, OP5, not_53_out, not_54_out, not_55_out, not_56_out, not_57_out, not_58_out, not_59_out, not_60_out, not_61_out, not_62_out, not_63_out);
  and and_16 (and_16_out, not_64_out, not_65_out, not_66_out, not_67_out, not_68_out, not_69_out, not_70_out, not_71_out, not_72_out, not_73_out, not_74_out, not_75_out);
  and and_17 (and_17_out, not_76_out, not_77_out, not_78_out, not_79_out, not_80_out, not_81_out, not_82_out, not_83_out, not_84_out, not_85_out, F1, F0);
  and and_18 (and_18_out, not_86_out, not_87_out, not_88_out, not_89_out, not_90_out, not_91_out, not_92_out, not_93_out, not_94_out, not_95_out, F1, not_96_out);
  and and_19 (and_19_out, not_97_out, not_98_out, not_99_out, not_100_out, not_101_out, not_102_out, F5, not_103_out, not_104_out, not_105_out, not_106_out, not_107_out);
  and and_20 (and_20_out, not_108_out, not_109_out, not_110_out, not_111_out, not_112_out, not_113_out, F5, not_114_out, not_115_out, not_116_out, not_117_out, F0);
  and and_21 (and_21_out, not_118_out, not_119_out, not_120_out, not_121_out, not_122_out, not_123_out, F5, not_124_out, not_125_out, not_126_out, F1, not_127_out);
  and and_22 (and_22_out, not_128_out, not_129_out, not_130_out, not_131_out, not_132_out, not_133_out, F5, not_134_out, not_135_out, F2, not_136_out, not_137_out);
  and and_23 (and_23_out, not_138_out, not_139_out, not_140_out, not_141_out, not_142_out, not_143_out, F5, not_144_out, not_145_out, F2, not_146_out, F0);
  and and_24 (and_24_out, not_147_out, not_148_out, not_149_out, not_150_out, not_151_out, not_152_out, F5, not_153_out, not_154_out, F2, F1, F0);
  and and_25 (and_25_out, not_155_out, not_156_out, not_157_out, not_158_out, not_159_out, not_160_out, F5, not_161_out, F3, not_162_out, F1, not_163_out);
  and and_26 (and_26_out, not_164_out, not_165_out, not_166_out, not_167_out, not_168_out, not_169_out, F5, not_170_out, F3, not_171_out, F1, F0);
  and and_27 (and_27_out, not_172_out, not_173_out, not_174_out, not_175_out, OP1, OP0);
  and and_28 (and_28_out, not_176_out, not_177_out, OP3, not_178_out, not_179_out, not_180_out);
  and and_29 (and_29_out, not_181_out, not_182_out, OP3, OP2, not_183_out, not_184_out);
  and and_30 (and_30_out, not_185_out, not_186_out, OP3, not_187_out, not_188_out, OP0);
  and and_31 (and_31_out, not_189_out, not_190_out, OP3, not_191_out, OP1, not_192_out);
  and and_32 (and_32_out, not_193_out, not_194_out, OP3, OP2, not_195_out, OP0);
  and and_33 (and_33_out, OP5, not_196_out, not_197_out, not_198_out, OP1, OP0);
  and and_34 (and_34_out, not_199_out, not_200_out, OP3, OP2, OP1, not_201_out);
  and and_35 (and_35_out, not_202_out, not_203_out, OP3, OP2, OP1, OP0);
  and and_36 (and_36_out, OP5, not_204_out, not_205_out, OP2, not_206_out, OP0);
  and and_37 (and_37_out, OP5, not_207_out, not_208_out, not_209_out, not_210_out, not_211_out, not_212_out, not_213_out, not_214_out, not_215_out, not_216_out, not_217_out);
  and and_38 (SysCALL, not_218_out, not_219_out, not_220_out, not_221_out, not_222_out, not_223_out, not_224_out, not_225_out, F2, F3, not_226_out, not_227_out);
  and and_39 (and_39_out, not_228_out, not_229_out, not_230_out, OP2, not_231_out, not_232_out);
  and and_40 (and_40_out, not_233_out, not_234_out, not_235_out, OP2, not_236_out, OP0);
  and and_41 (and_41_out, not_237_out, not_238_out, OP3, not_239_out, not_240_out, not_241_out);
  and and_42 (and_42_out, not_242_out, not_243_out, OP3, not_244_out, not_245_out, OP0);
  and and_43 (and_43_out, not_246_out, not_247_out, OP3, not_248_out, OP1, not_249_out);
  and and_44 (and_44_out, OP5, not_250_out, not_251_out, not_252_out, OP1, OP0);
  and and_45 (and_45_out, OP5, not_253_out, OP3, not_254_out, OP1, OP0);
  and and_46 (and_46_out, OP5, not_255_out, not_256_out, OP2, not_257_out, OP0);
  and and_47 (and_47_out, not_258_out, not_259_out, not_260_out, not_261_out, not_262_out, OP0);
  and and_48 (and_48_out, OP5, not_263_out, not_264_out, not_265_out, not_266_out, not_267_out, not_268_out, not_269_out, not_270_out, not_271_out, not_272_out, not_273_out);
  and and_49 (and_49_out, not_274_out, not_275_out, not_276_out, not_277_out, not_278_out, not_279_out, not_280_out, not_281_out, not_282_out, not_283_out);
  and and_50 (and_50_out, not_284_out, not_285_out, not_286_out, not_287_out, not_288_out, not_289_out, not_290_out, not_291_out, not_292_out, F5);
  and and_51 (and_51_out, not_293_out, not_294_out, not_295_out, not_296_out, not_297_out, not_298_out, F1, not_299_out, not_300_out, not_301_out, not_302_out);
  and and_52 (and_52_out, not_303_out, not_304_out, not_305_out, not_306_out, not_307_out, not_308_out, F1, not_309_out, F3, not_310_out, F5);
  and and_53 (and_53_out, not_311_out, not_312_out, not_313_out, not_314_out, not_315_out, not_316_out, F0, F2, not_317_out, not_318_out, F5);
  and and_54 (BEQ, not_319_out, not_320_out, OP2, not_321_out, not_322_out, not_323_out);
  and and_55 (BNE, OP0, not_324_out, OP2, not_325_out, not_326_out, not_327_out);
  and and_56 (JR, not_328_out, not_329_out, not_330_out, not_331_out, not_332_out, not_333_out, not_334_out, not_335_out, not_336_out, F3, not_337_out, not_338_out);
  and and_57 (JUMP, OP1, not_339_out, not_340_out, not_341_out, not_342_out);
  and and_58 (JAL, OP0, OP1, not_343_out, not_344_out, not_345_out, not_346_out);
  or or_1 (MemToReg, and_1_out, and_2_out, and_3_out);
  or or_2 (ALU_SRC, and_5_out, and_6_out, and_7_out, and_8_out, and_9_out, and_10_out, and_11_out, and_12_out, and_13_out, and_14_out, and_15_out);
  or or_3 (SignedExt, and_39_out, and_40_out, and_41_out, and_42_out, and_43_out, and_44_out, and_45_out, and_46_out, and_47_out, and_48_out);
  or or_4 (RegDst, and_49_out, and_50_out, and_51_out, and_52_out, and_53_out);
  or or_5 (RegWrite, and_16_out, and_17_out, and_18_out, and_19_out, and_20_out, and_21_out, and_22_out, and_23_out, and_24_out, and_25_out, and_26_out, and_27_out, and_28_out, and_29_out, and_30_out, and_31_out, and_32_out, and_33_out, and_34_out, and_35_out, and_36_out, and_37_out);
endmodule

// 拓展信号生成
module \拓展信号自动生成  (
  input  OP0,
  input  OP1,
  input  OP2,
  input  OP3,
  input  OP4,
  input  OP5,
  input  F0,
  input  F1,
  input  F2,
  input  F3,
  input  F4,
  input  F5,
  output BLTZ,
  output LHU,
  output LUI,
  output LB
);

  wire not_1_out, not_2_out, not_3_out, not_4_out, not_5_out, not_6_out, not_7_out, not_8_out, not_9_out,
       not_10_out, not_11_out, not_12_out, not_13_out, not_14_out, not_15_out, not_16_out, not_17_out,
       not_18_out, not_19_out, not_20_out, not_21_out;

  not not_1 (not_1_out, OP1);
  not not_2 (not_2_out, OP2);
  not not_3 (not_3_out, OP3);
  not not_4 (not_4_out, OP4);
  not not_5 (not_5_out, OP5);
  not not_6 (not_6_out, OP1);
  not not_7 (not_7_out, OP3);
  not not_8 (not_8_out, OP4);
  not not_9 (not_9_out, OP4);
  not not_10 (not_10_out, OP5);
  not not_11 (not_11_out, OP4);
  not not_12 (not_12_out, OP3);
  not not_13 (not_13_out, OP2);
  not not_14 (not_14_out, OP1);
  not not_15 (not_15_out, OP0);
  not not_16 (not_16_out, F5);
  not not_17 (not_17_out, F4);
  not not_18 (not_18_out, F3);
  not not_19 (not_19_out, F2);
  not not_20 (not_20_out, F1);
  not not_21 (not_21_out, F0);
  and and_1 (BLTZ, OP0, not_1_out, not_2_out, not_3_out, not_4_out, not_5_out);
  and and_2 (LHU, OP0, not_6_out, OP2, not_7_out, not_8_out, OP5);
  and and_3 (LUI, OP0, OP1, OP2, OP3, not_9_out, not_10_out);
  and and_4 (LB, OP5, not_11_out, not_12_out, not_13_out, not_14_out, not_15_out, not_16_out, not_17_out, not_18_out, not_19_out, not_20_out, not_21_out);
endmodule

// ALU
module MIPS_ALU (
  input  [4:0] shamt,
  input  [31:0] X,
  input  [31:0] Y,
  input  [3:0] AluOP,
  output Equal,
  output [31:0] Result,
  output [31:0] Result_2
);

  wire [0:0] comparator_1_lt, comparator_2_lt;
  wire [31:0] adder_1_out, AND_out, divider_1_out, divider_1_rem, multiplier_1_cout, multiplier_1_out,
       NOR_out, OR_out, shifter_1_out, shifter_2_out, shifter_3_out, subtractor_1_out, XOR_out;

  assign AND_out = X & Y;  // AND_Gate AND, 32 bits wide
  assign OR_out = X | Y;  // OR_Gate OR, 32 bits wide
  Shifter #(.width(32), .shift("ll")) shifter_1 (.in(Y), .\dist (shamt), .out(shifter_1_out));
  Shifter #(.width(32), .shift("ar")) shifter_2 (.in(Y), .\dist (shamt), .out(shifter_2_out));
  Shifter #(.width(32), .shift("lr")) shifter_3 (.in(Y), .\dist (shamt), .out(shifter_3_out));
  Multiplier #(.width(32)) multiplier_1 (.a(X), .b(Y), .out(multiplier_1_out), .cout(multiplier_1_cout));  // open: cin
  Divider #(.width(32)) divider_1 (.a(X), .b(Y), .out(divider_1_out), .rem(divider_1_rem));  // open: upper
  Adder #(.width(32)) adder_1 (.a(X), .b(Y), .out(adder_1_out));  // open: cin, cout
  Subtractor #(.width(32)) subtractor_1 (.a(X), .b(Y), .out(subtractor_1_out));  // open: bin, bout
  assign XOR_out = X ^ Y;  // XOR_Gate XOR, 32 bits wide
  assign NOR_out = ~(X | Y);  // NOR_Gate NOR, 32 bits wide
  Comparator #(.width(32), .mode("twosComplement")) comparator_1 (
    .a(X), .b(Y), .eq(Equal), .lt(comparator_1_lt[0]));  // open: gt
  Comparator #(.width(32), .mode("unsigned")) comparator_2 (.a(X), .b(Y), .lt(comparator_2_lt[0]));  // open: gt, eq
  Multiplexer #(.select(4), .width(32), .disabled("Z"), .enable("false")) multiplexer_1 (
    .in0(shifter_1_out), .in1(shifter_2_out), .in2(shifter_3_out), .in3(multiplier_1_out),
    .in4(divider_1_out), .in5(adder_1_out), .in6(subtractor_1_out), .in7(AND_out), .in8(OR_out),
    .in9(XOR_out), .in10(NOR_out), .in11({{31{1'b0}}, comparator_1_lt[0]}),
    .in12({{31{1'b0}}, comparator_2_lt[0]}), .in13({32{1'b0}}), .in14({32{1'b0}}), .in15({32{1'b0}}),
    .out(Result), .sel(AluOP));
  Multiplexer #(.select(4), .width(32), .disabled("Z"), .enable("false")) multiplexer_2 (
    .in0({32{1'b0}}), .in1({32{1'b0}}), .in2({32{1'b0}}), .in3(multiplier_1_cout), .in4(divider_1_rem),
    .in5({32{1'b0}}), .in6({32{1'b0}}), .in7({32{1'b0}}), .in8({32{1'b0}}), .in9({32{1'b0}}),
    .in10({32{1'b0}}), .in11({32{1'b0}}), .in12({32{1'b0}}), .in13({32{1'b0}}), .in14({32{1'b0}}),
    .in15({32{1'b0}}), .out(Result_2), .sel(AluOP));

  // Other names for the same wires on the sheet: Result2[31:0] = Result_2; S[3:0] = AluOP

  // Notes on the sheet:
  //   不要改变此引脚区域内容，也不要改变ALU封装形式
  //   输入引脚
  //   输出引脚
endmodule

module MIPS_Regifile (
  input  [31:0] Din,
  input  Clk,
  input  WE,
  input  [4:0] R1_num,
  input  [4:0] W_num,
  input  [4:0] R2_num,
  output [31:0] R1,
  output [31:0] R2
);

  // RegisterFile registerfile_1: pin names not known; wires that end beside it: Din, Clk, WE, W_num, R1_num, R2_num, R1, R2
endmodule

// 中断按键电路
module \中断按键参考电路  (
  input  [31:0] EPC,
  input  CLK,
  input  IE,
  input  ERET,
  input  \_1号按键 ,
  input  [1:0] \当前中断号 ,
  input  \_2号按键 ,
  input  \_3号按键 ,
  input  restore_EPC,
  output \中断隐周期 ,
  output [1:0] \中断号 ,
  output LED1,
  output LED2,
  output LED3
);

  wire and_1_out, and_2_out, and_3_out, and_4_out, and_5_out, and_6_out, and_7_out, and_8_out, and_9_out,
       and_10_out, and_11_out, CIN_1, CIN_2, CIN_3, d_ff_1_q, d_ff_2_q, d_ff_3_q, d_ff_4_q, d_ff_4_qn,
       d_ff_5_q, d_ff_5_qn, d_ff_6_q, d_ff_6_qn, d_ff_7_qn, decoder_2_out1, decoder_2_out2, or_2_out,
       or_3_out, or_4_out, or_5_out, or_6_out, \目标中断号小于1 , \目标中断号小于2 , \目标中断号小于3 ;
  wire [1:0] bitselector_1_out;
  wire [15:0] counter_1_q, counter_2_q, counter_3_q, counter_4_q, counter_5_q, counter_6_q;

  Decoder #(.select(2), .tristate("false"), .disabled("Z"), .enable("false")) decoder_1 (
    .out1(CIN_1), .out2(CIN_2), .out3(CIN_3), .sel(\当前中断号 ));  // open: out0
  Counter #(.width(16), .max('hffff), .ongoal("wrap"), .trigger("rising"), .behavior("new")) counter_1 (
    .count(CIN_1), .Q(counter_1_q), .clk(restore_EPC));  // open: load, D, carry, clr, preset, down
  BitSelector #(.width(32), .group(2)) bitselector_1 (.in(EPC), .out(bitselector_1_out), .sel(4'b1100));
  Counter #(.width(16), .max('hffff), .ongoal("wrap"), .trigger("rising"), .behavior("new")) counter_2 (
    .count(CIN_2), .Q(counter_2_q), .clk(restore_EPC));  // open: load, D, carry, clr, preset, down
  Decoder #(.select(2), .tristate("false"), .disabled("Z"), .enable("false")) decoder_2 (
    .out0(\目标中断号小于1 ), .out1(decoder_2_out1), .out2(decoder_2_out2), .sel(bitselector_1_out));  // open: out3
  Counter #(.width(16), .max('hffff), .ongoal("wrap"), .trigger("rising"), .behavior("new")) counter_3 (
    .count(CIN_3), .Q(counter_3_q), .clk(restore_EPC));  // open: load, D, carry, clr, preset, down
  or or_1 (\目标中断号小于2 , \目标中断号小于1 , decoder_2_out1);
  not not_1 (\目标中断号小于3 , decoder_2_out2);
  Counter #(.width(16), .max('hffff), .ongoal("wrap"), .trigger("rising"), .behavior("new")) counter_4 (
    .Q(counter_4_q), .clk(\_1号按键 ));  // open: load, D, count, carry, clr, preset, down
  Counter #(.width(16), .max('hffff), .ongoal("wrap"), .trigger("rising"), .behavior("new")) counter_5 (
    .Q(counter_5_q), .clk(\_2号按键 ));  // open: load, D, count, carry, clr, preset, down
  Counter #(.width(16), .max('hffff), .ongoal("wrap"), .trigger("rising"), .behavior("new")) counter_6 (
    .Q(counter_6_q), .clk(\_3号按键 ));  // open: load, D, count, carry, clr, preset, down
  Comparator #(.width(16), .mode("unsigned")) comparator_1 (
    .a(counter_4_q), .b(counter_1_q), .gt(LED1));  // open: eq, lt
  Comparator #(.width(16), .mode("unsigned")) comparator_2 (
    .a(counter_5_q), .b(counter_2_q), .gt(LED2));  // open: eq, lt
  Comparator #(.width(16), .mode("unsigned")) comparator_3 (
    .a(counter_6_q), .b(counter_3_q), .gt(LED3));  // open: eq, lt
  and and_1 (and_1_out, \目标中断号小于1 , LED1, ERET);
  and and_2 (and_2_out, \_1号按键 , ~or_2_out);  // AND_Gate
  or or_2 (or_2_out, CIN_2, CIN_3);
  and and_3 (and_3_out, \目标中断号小于2 , LED2, ERET);
  and and_4 (and_4_out, \目标中断号小于3 , LED3, ERET);
  and and_5 (and_5_out, CIN_1, LED2);
  and and_6 (and_6_out, \_2号按键 , ~CIN_3);  // AND_Gate
  and and_7 (and_7_out, ~CIN_3, LED3);  // AND_Gate
  or or_3 (or_3_out, and_1_out, and_2_out);
  or or_4 (or_4_out, and_7_out, and_4_out, \_3号按键 );
  or or_5 (or_5_out, and_5_out, and_3_out, and_6_out);
  D_Flip_Flop #(.trigger("rising"), .Pre_Clr_Positions("BELOW_ABOVE"), .NegatePresetClear("false"), .enable("false"), .NewFFLayout("false")) d_ff_1 (
    .clk(CLK), .D(1'b0), .Q(d_ff_1_q), .preset(or_3_out));  // open: Qn, reset
  D_Flip_Flop #(.trigger("rising"), .Pre_Clr_Positions("BELOW_ABOVE"), .NegatePresetClear("false"), .enable("false"), .NewFFLayout("false")) d_ff_2 (
    .clk(CLK), .D(1'b0), .Q(d_ff_2_q), .preset(or_5_out));  // open: Qn, reset
  D_Flip_Flop #(.trigger("rising"), .Pre_Clr_Positions("BELOW_ABOVE"), .NegatePresetClear("false"), .enable("false"), .NewFFLayout("false")) d_ff_3 (
    .clk(CLK), .D(1'b0), .Q(d_ff_3_q), .preset(or_4_out));  // open: Qn, reset
  and and_8 (and_8_out, IE, d_ff_1_q, d_ff_4_qn);
  and and_9 (and_9_out, IE, d_ff_2_q, d_ff_5_qn);
  and and_10 (and_10_out, IE, d_ff_3_q, d_ff_6_qn);
  or or_6 (or_6_out, and_8_out, and_9_out, and_10_out);
  and and_11 (and_11_out, or_6_out, d_ff_7_qn);
  D_Flip_Flop #(.trigger("rising"), .Pre_Clr_Positions("BELOW_ABOVE"), .NegatePresetClear("false"), .enable("false"), .NewFFLayout("false")) d_ff_4 (
    .clk(CLK), .D(and_8_out), .Q(d_ff_4_q), .Qn(d_ff_4_qn));  // open: preset, reset
  D_Flip_Flop #(.trigger("rising"), .Pre_Clr_Positions("BELOW_ABOVE"), .NegatePresetClear("false"), .enable("false"), .NewFFLayout("false")) d_ff_5 (
    .clk(CLK), .D(and_9_out), .Q(d_ff_5_q), .Qn(d_ff_5_qn));  // open: preset, reset
  D_Flip_Flop #(.trigger("rising"), .Pre_Clr_Positions("BELOW_ABOVE"), .NegatePresetClear("false"), .enable("false"), .NewFFLayout("false")) d_ff_6 (
    .clk(CLK), .D(and_10_out), .Q(d_ff_6_q), .Qn(d_ff_6_qn));  // open: preset, reset
  D_Flip_Flop #(.trigger("rising"), .Pre_Clr_Positions("LEGACY"), .NegatePresetClear("false"), .enable("true"), .NewFFLayout("false")) d_ff_7 (
    .clk(CLK), .D(and_11_out), .Q(\中断隐周期 ), .Qn(d_ff_7_qn));  // open: preset, en, reset
  Priority_Encoder #(.select(2), .disabled("Z")) priority_encoder_1 (
    .in0(1'b1), .in1(d_ff_4_q), .in2(d_ff_5_q), .in3(d_ff_6_q), .out(\中断号 ));  // open: gs, en_out, en_in

  // Notes on the sheet:
  //   经过返回后，从等待队列中取出一个中断执行
endmodule

module MIPS_RAM (
  input  [25:0] \字节地址 ,
  input  [31:0] Din,
  input  CLK,
  input  WE,
  input  [1:0] Mode,
  output [31:0] DataOut
);

  wire and_1_out, and_2_out, and_3_out, and_4_out, and_5_out, and_6_out, and_7_out, and_8_out, \byte ,
       decoder_1_out0, decoder_1_out1, decoder_1_out2, decoder_1_out3, half_word, or_1_out, or_2_out,
       or_3_out, or_4_out, or_5_out, or_6_out, or_7_out, or_8_out, or_9_out, word;
  wire [7:0] controlled_buffer_1_out, controlled_buffer_4_out, controlled_buffer_10_out, ram_1_data,
       ram_2_data, ram_3_data, ram_4_data;
  wire [31:0] and_9_out, and_10_out, controlled_buffer_8_out;

  assign controlled_buffer_1_out = word ? Din[31:24] : 8'bz;  // Controlled_Buffer controlled_buffer_1
  assign controlled_buffer_1_out = half_word ? Din[15:8] : 8'bz;  // Controlled_Buffer controlled_buffer_2
  assign controlled_buffer_1_out = \byte  ? Din[7:0] : 8'bz;  // Controlled_Buffer controlled_buffer_3
  or or_1 (or_1_out, and_1_out, and_2_out, word);
  or or_2 (or_2_out, word, half_word);
  RAM #(.addrWidth(24), .dataWidth(8), .bus("separate"), .Select("high")) ram_1 (
    .addr(\字节地址 [25:2]), .din(controlled_buffer_1_out), .data(ram_1_data), .str(WE), .sel(or_1_out), .clk(CLK));  // open: ld, clr
  and and_1 (and_1_out, decoder_1_out3, \byte );
  and and_2 (and_2_out, \字节地址 [1], half_word);
  assign controlled_buffer_4_out = word ? Din[23:16] : 8'bz;  // Controlled_Buffer controlled_buffer_4
  or or_3 (or_3_out, half_word, \byte );
  assign controlled_buffer_8_out[15:8] = half_word ? ram_1_data : 8'bz;  // Controlled_Buffer controlled_buffer_5
  assign controlled_buffer_8_out[31:24] = or_2_out ? ram_1_data : 8'bz;  // Controlled_Buffer controlled_buffer_6
  assign controlled_buffer_4_out = or_3_out ? Din[7:0] : 8'bz;  // Controlled_Buffer controlled_buffer_7
  // Probe on DataOut
  assign controlled_buffer_8_out[7:0] = \byte  ? ram_1_data : 8'bz;  // Controlled_Buffer controlled_buffer_8
  or or_4 (or_4_out, and_3_out, and_4_out, word);
  assign controlled_buffer_8_out[23:16] = word ? ram_2_data : 8'bz;  // Controlled_Buffer controlled_buffer_9
  RAM #(.addrWidth(24), .dataWidth(8), .bus("separate"), .Select("high")) ram_2 (
    .addr(\字节地址 [25:2]), .din(controlled_buffer_4_out), .data(ram_2_data), .str(WE), .sel(or_4_out), .clk(CLK));  // open: ld, clr
  and and_3 (and_3_out, decoder_1_out2, \byte );
  and and_4 (and_4_out, \字节地址 [1], half_word);
  assign controlled_buffer_10_out = or_5_out ? Din[15:8] : 8'bz;  // Controlled_Buffer controlled_buffer_10
  assign controlled_buffer_10_out = \byte  ? Din[7:0] : 8'bz;  // Controlled_Buffer controlled_buffer_11
  or or_5 (or_5_out, word, half_word);
  assign controlled_buffer_8_out[7:0] = or_6_out ? ram_2_data : 8'bz;  // Controlled_Buffer controlled_buffer_12
  or or_6 (or_6_out, \byte , half_word);
  RAM #(.addrWidth(24), .dataWidth(8), .bus("separate"), .Select("high")) ram_3 (
    .addr(\字节地址 [25:2]), .din(controlled_buffer_10_out), .data(ram_3_data), .str(WE), .sel(or_7_out),
    .clk(CLK));  // open: ld, clr
  and and_5 (and_5_out, decoder_1_out1, \byte );
  and and_6 (and_6_out, ~\字节地址 [1], half_word);  // AND_Gate
  or or_7 (or_7_out, and_5_out, and_6_out, word);
  assign controlled_buffer_8_out[15:8] = or_8_out ? ram_3_data : 8'bz;  // Controlled_Buffer controlled_buffer_13
  or or_8 (or_8_out, word, half_word);
  assign controlled_buffer_8_out[7:0] = \byte  ? ram_3_data : 8'bz;  // Controlled_Buffer controlled_buffer_14
  RAM #(.addrWidth(24), .dataWidth(8), .bus("separate"), .Select("high")) ram_4 (
    .addr(\字节地址 [25:2]), .din(Din[7:0]), .data(ram_4_data), .str(WE), .sel(or_9_out), .clk(CLK));  // open: ld, clr
  and and_7 (and_7_out, decoder_1_out0, \byte );
  and and_8 (and_8_out, ~\字节地址 [1], half_word);  // AND_Gate
  or or_9 (or_9_out, and_7_out, and_8_out, word);
  assign controlled_buffer_8_out[7:0] = or_9_out ? ram_4_data : 8'bz;  // Controlled_Buffer controlled_buffer_15
  Decoder #(.select(2), .tristate("false"), .disabled("Z"), .enable("false")) decoder_1 (
    .out0(decoder_1_out0), .out1(decoder_1_out1), .out2(decoder_1_out2), .out3(decoder_1_out3),
    .sel(\字节地址 [1:0]));
  assign and_9_out = controlled_buffer_8_out & 32'hffff;  // AND_Gate and_9, 32 bits wide
  assign and_10_out = controlled_buffer_8_out & 32'hff;  // AND_Gate and_10, 32 bits wide
  assign DataOut = word ? controlled_buffer_8_out : 32'bz;  // Controlled_Buffer controlled_buffer_16
  assign DataOut = half_word ? and_9_out : 32'bz;  // Controlled_Buffer controlled_buffer_17
  assign DataOut = \byte  ? and_10_out : 32'bz;  // Controlled_Buffer controlled_buffer_18
  Decoder #(.select(2), .tristate("false"), .disabled("Z"), .enable("false")) decoder_2 (
    .out0(word), .out1(\byte ), .out2(half_word), .sel(Mode));  // open: out3

  // Other names for the same wires on the sheet: Dout[31:0] = DataOut; low_bits[1:0] = \字节地址 [1:0];
  //   second_bit = \字节地址 [1]; word_addr[23:0] = \字节地址 [25:2]

  // Notes on the sheet:
  //   输入引脚区
  //   请勿增改引脚，请勿修改子电路封装
  //   电路功能：利用下图中给定的RAM器件实现既既可以按照字节，也可以按照半字，也可以按照32位字访问的MIPS存储器
  //   请在下方利用上方输入输出引脚的隧道信号构建电路，ctrl+d复制选择部件
  //   输出引脚区
  //   提示：不要滥用多路选择器，这里不要超过3个多路选择器
endmodule
module \中断按键电路  (
  input  CLK,
  input  \_1号中断 ,
  input  EN,
  input  IE,
  input  \同步清零信号1 ,
  input  \_2号中断 ,
  input  \同步清零信号2 ,
  input  \_3号中断 ,
  input  \同步清零信号3 ,
  output IR,
  output [1:0] \中断号 ,
  output W1,
  output W2,
  output W3
);

  wire and_1_out, and_2_out, and_3_out, and_4_out, and_5_out, and_6_out, and_7_out, d_ff_1_q, d_ff_2_q,
       d_ff_3_q, d_ff_4_qn, d_ff_5_qn, d_ff_6_qn, IR1_q, IR2_q, IR3_q, or_4_out, or_5_out, or_6_out;

  and and_1 (and_1_out, EN, IE);
  D_Flip_Flop #(.trigger("rising"), .Pre_Clr_Positions("LEGACY"), .NegatePresetClear("false"), .enable("true"), .NewFFLayout("false")) d_ff_1 (
    .clk(\_1号中断 ), .D(1'b1), .Q(d_ff_1_q), .en(and_1_out), .reset(IR1_q));  // open: Qn, preset
  or or_1 (W1, IR1_q, d_ff_1_q);
  D_Flip_Flop #(.trigger("rising"), .Pre_Clr_Positions("LEGACY"), .NegatePresetClear("false"), .enable("true"), .NewFFLayout("false")) d_ff_2 (
    .clk(\_2号中断 ), .D(1'b1), .Q(d_ff_2_q), .en(and_1_out), .reset(IR2_q));  // open: Qn, preset
  or or_2 (W2, IR2_q, d_ff_2_q);
  D_Flip_Flop #(.trigger("rising"), .Pre_Clr_Positions("LEGACY"), .NegatePresetClear("false"), .enable("true"), .NewFFLayout("false")) d_ff_3 (
    .clk(\_3号中断 ), .D(1'b1), .Q(d_ff_3_q), .en(and_1_out), .reset(IR3_q));  // open: Qn, preset
  or or_3 (W3, IR3_q, d_ff_3_q);
  or or_4 (or_4_out, d_ff_1_q, IR1_q);
  or or_5 (or_5_out, d_ff_2_q, IR2_q);
  or or_6 (or_6_out, d_ff_3_q, IR3_q);
  and and_2 (and_2_out, or_4_out, ~\同步清零信号1 );  // AND_Gate
  and and_3 (and_3_out, or_5_out, ~\同步清零信号2 );  // AND_Gate
  and and_4 (and_4_out, or_6_out, ~\同步清零信号3 );  // AND_Gate
  D_Flip_Flop #(.trigger("rising"), .Pre_Clr_Positions("LEGACY"), .NegatePresetClear("false"), .enable("true"), .NewFFLayout("false")) IR1 (
    .clk(CLK), .D(and_2_out), .Q(IR1_q), .en(and_1_out));  // open: Qn, preset, reset
  D_Flip_Flop #(.trigger("rising"), .Pre_Clr_Positions("LEGACY"), .NegatePresetClear("false"), .enable("true"), .NewFFLayout("false")) IR2 (
    .clk(CLK), .D(and_3_out), .Q(IR2_q), .en(and_1_out));  // open: Qn, preset, reset
  D_Flip_Flop #(.trigger("rising"), .Pre_Clr_Positions("LEGACY"), .NegatePresetClear("false"), .enable("true"), .NewFFLayout("false")) IR3 (
    .clk(CLK), .D(and_4_out), .Q(IR3_q), .en(and_1_out));  // open: Qn, preset, reset
  D_Flip_Flop #(.trigger("rising"), .Pre_Clr_Positions("LEGACY"), .NegatePresetClear("false"), .enable("true"), .NewFFLayout("false")) d_ff_4 (
    .clk(CLK), .D(IR1_q), .Qn(d_ff_4_qn));  // open: Q, preset, en, reset
  D_Flip_Flop #(.trigger("rising"), .Pre_Clr_Positions("LEGACY"), .NegatePresetClear("false"), .enable("true"), .NewFFLayout("false")) d_ff_5 (
    .clk(CLK), .D(IR2_q), .Qn(d_ff_5_qn));  // open: Q, preset, en, reset
  D_Flip_Flop #(.trigger("rising"), .Pre_Clr_Positions("LEGACY"), .NegatePresetClear("false"), .enable("true"), .NewFFLayout("false")) d_ff_6 (
    .clk(CLK), .D(IR3_q), .Qn(d_ff_6_qn));  // open: Q, preset, en, reset
  Priority_Encoder #(.select(2), .disabled("Z")) priority_encoder_1 (
    .in0(1'b1), .in1(IR1_q), .in2(IR2_q), .in3(IR3_q), .out(\中断号 ));  // open: gs, en_out, en_in
  and and_5 (and_5_out, d_ff_4_qn, IR1_q);
  and and_6 (and_6_out, d_ff_5_qn, IR2_q);
  and and_7 (and_7_out, d_ff_6_qn, IR3_q);
  or or_7 (IR, and_5_out, and_6_out, and_7_out);

  // Notes on the sheet:
  //   Reset 
  //   Reset 
  //   Reset 
endmodule

// 中断信号生成
module \中断信号自动生成  (
  input  OP0,
  input  OP1,
  input  OP2,
  input  OP3,
  input  OP4,
  input  OP5,
  input  F0,
  input  F1,
  input  F2,
  input  F3,
  input  F4,
  input  F5,
  output MCP0,
  output ERET
);

  wire not_1_out, not_2_out, not_3_out, not_4_out, not_5_out, not_6_out, not_7_out, not_8_out, not_9_out,
       not_10_out, not_11_out, not_12_out, not_13_out, not_14_out, not_15_out, not_16_out, not_17_out,
       not_18_out, not_19_out, not_20_out;

  not not_1 (not_1_out, OP5);
  not not_2 (not_2_out, OP3);
  not not_3 (not_3_out, OP2);
  not not_4 (not_4_out, OP1);
  not not_5 (not_5_out, OP0);
  not not_6 (not_6_out, F5);
  not not_7 (not_7_out, F4);
  not not_8 (not_8_out, F3);
  not not_9 (not_9_out, F2);
  not not_10 (not_10_out, F1);
  not not_11 (not_11_out, F0);
  not not_12 (not_12_out, OP5);
  not not_13 (not_13_out, OP3);
  not not_14 (not_14_out, OP2);
  not not_15 (not_15_out, OP1);
  not not_16 (not_16_out, OP0);
  not not_17 (not_17_out, F5);
  not not_18 (not_18_out, F2);
  not not_19 (not_19_out, F1);
  not not_20 (not_20_out, F0);
  and and_1 (MCP0, not_1_out, OP4, not_2_out, not_3_out, not_4_out, not_5_out, not_6_out, not_7_out, not_8_out, not_9_out, not_10_out, not_11_out);
  and and_2 (ERET, not_12_out, OP4, not_13_out, not_14_out, not_15_out, not_16_out, not_17_out, F4, F3, not_18_out, not_19_out, not_20_out);
endmodule

module MEM_WB (
  input  [2:0] in_1,
  input  [31:0] IR,
  input  [31:0] PC,
  input  [31:0] in_4,
  input  [31:0] in_5,
  input  [31:0] in_6,
  input  [31:0] in_7,
  input  [4:0] in_8,
  input  \同步清零 ,
  input  \使能端 ,
  input  CLK,
  output [2:0] out_12,
  output [31:0] out_13,
  output [31:0] out_14,
  output [31:0] out_15,
  output [31:0] out_16,
  output [31:0] out_17,
  output [31:0] out_18,
  output [4:0] out_19
);

  wire not_1_out;
  wire [2:0] multiplexer_1_out;
  wire [4:0] multiplexer_8_out;
  wire [31:0] multiplexer_2_out, multiplexer_3_out, multiplexer_4_out, multiplexer_5_out, multiplexer_6_out,
       multiplexer_7_out;

  Pull_Resistor #(.pull(0)) pull_resistor_1 (.node(\同步清零 ));
  Pull_Resistor #(.pull(0)) pull_resistor_2 (.node(\使能端 ));
  not not_1 (not_1_out, \使能端 );
  Multiplexer #(.select(1), .width(3), .disabled("Z"), .enable("false")) multiplexer_1 (
    .in0(in_1), .in1(3'b000), .out(multiplexer_1_out), .sel(\同步清零 ));
  Multiplexer #(.select(1), .width(32), .disabled("Z"), .enable("false")) multiplexer_2 (
    .in0(IR), .in1({32{1'b0}}), .out(multiplexer_2_out), .sel(\同步清零 ));
  Multiplexer #(.select(1), .width(32), .disabled("Z"), .enable("false")) multiplexer_3 (
    .in0(PC), .in1({32{1'b0}}), .out(multiplexer_3_out), .sel(\同步清零 ));
  Multiplexer #(.select(1), .width(32), .disabled("Z"), .enable("false")) multiplexer_4 (
    .in0(in_4), .in1({32{1'b0}}), .out(multiplexer_4_out), .sel(\同步清零 ));
  Multiplexer #(.select(1), .width(32), .disabled("Z"), .enable("false")) multiplexer_5 (
    .in0(in_5), .in1({32{1'b0}}), .out(multiplexer_5_out), .sel(\同步清零 ));
  Multiplexer #(.select(1), .width(32), .disabled("Z"), .enable("false")) multiplexer_6 (
    .in0(in_6), .in1({32{1'b0}}), .out(multiplexer_6_out), .sel(\同步清零 ));
  Multiplexer #(.select(1), .width(32), .disabled("Z"), .enable("false")) multiplexer_7 (
    .in0(in_7), .in1({32{1'b0}}), .out(multiplexer_7_out), .sel(\同步清零 ));
  Multiplexer #(.select(1), .width(5), .disabled("Z"), .enable("false")) multiplexer_8 (
    .in0(in_8), .in1({5{1'b0}}), .out(multiplexer_8_out), .sel(\同步清零 ));
  Register #(.width(3), .trigger("rising"), .Select("low")) register_1 (
    .D(multiplexer_1_out), .en(not_1_out), .Q(out_12), .clk(CLK));  // open: clr
  Register #(.width(32), .trigger("rising"), .Select("low")) register_2 (
    .D(multiplexer_2_out), .en(not_1_out), .Q(out_13), .clk(CLK));  // open: clr
  Register #(.width(32), .trigger("rising"), .Select("low")) register_3 (
    .D(multiplexer_3_out), .en(not_1_out), .Q(out_14), .clk(CLK));  // open: clr
  Register #(.width(32), .trigger("rising"), .Select("low")) register_4 (
    .D(multiplexer_4_out), .en(not_1_out), .Q(out_15), .clk(CLK));  // open: clr
  Register #(.width(32), .trigger("rising"), .Select("low")) register_5 (
    .D(multiplexer_5_out), .en(not_1_out), .Q(out_16), .clk(CLK));  // open: clr
  Register #(.width(32), .trigger("rising"), .Select("low")) register_6 (
    .D(multiplexer_6_out), .en(not_1_out), .Q(out_17), .clk(CLK));  // open: clr
  Register #(.width(32), .trigger("rising"), .Select("low")) register_7 (
    .D(multiplexer_7_out), .en(not_1_out), .Q(out_18), .clk(CLK));  // open: clr
  Register #(.width(5), .trigger("rising"), .Select("low")) register_8 (
    .D(multiplexer_8_out), .en(not_1_out), .Q(out_19), .clk(CLK));  // open: clr
endmodule

module EX_MEM (
  input  [2:0] in_1,
  input  [2:0] in_2,
  input  [31:0] IR,
  input  [31:0] PC,
  input  [31:0] in_5,
  input  [31:0] in_6,
  input  [31:0] in_7,
  input  [4:0] in_8,
  input  \同步清零 ,
  input  \使能端 ,
  input  CLK,
  output [2:0] out_12,
  output [2:0] out_13,
  output [31:0] out_14,
  output [31:0] out_15,
  output [31:0] out_16,
  output [31:0] out_17,
  output [31:0] out_18,
  output [4:0] out_19
);

  wire not_1_out;
  wire [2:0] multiplexer_1_out, multiplexer_2_out;
  wire [4:0] multiplexer_8_out;
  wire [31:0] multiplexer_3_out, multiplexer_4_out, multiplexer_5_out, multiplexer_6_out, multiplexer_7_out;

  Pull_Resistor #(.pull(0)) pull_resistor_1 (.node(\同步清零 ));
  Pull_Resistor #(.pull(0)) pull_resistor_2 (.node(\使能端 ));
  Multiplexer #(.select(1), .width(3), .disabled("Z"), .enable("false")) multiplexer_1 (
    .in0(in_1), .in1(3'b000), .out(multiplexer_1_out), .sel(\同步清零 ));
  Multiplexer #(.select(1), .width(3), .disabled("Z"), .enable("false")) multiplexer_2 (
    .in0(in_2), .in1(3'b000), .out(multiplexer_2_out), .sel(\同步清零 ));
  Multiplexer #(.select(1), .width(32), .disabled("Z"), .enable("false")) multiplexer_3 (
    .in0(IR), .in1({32{1'b0}}), .out(multiplexer_3_out), .sel(\同步清零 ));
  Multiplexer #(.select(1), .width(32), .disabled("Z"), .enable("false")) multiplexer_4 (
    .in0(PC), .in1({32{1'b0}}), .out(multiplexer_4_out), .sel(\同步清零 ));
  Multiplexer #(.select(1), .width(32), .disabled("Z"), .enable("false")) multiplexer_5 (
    .in0(in_5), .in1({32{1'b0}}), .out(multiplexer_5_out), .sel(\同步清零 ));
  Multiplexer #(.select(1), .width(32), .disabled("Z"), .enable("false")) multiplexer_6 (
    .in0(in_6), .in1({32{1'b0}}), .out(multiplexer_6_out), .sel(\同步清零 ));
  Multiplexer #(.select(1), .width(32), .disabled("Z"), .enable("false")) multiplexer_7 (
    .in0(in_7), .in1({32{1'b0}}), .out(multiplexer_7_out), .sel(\同步清零 ));
  Multiplexer #(.select(1), .width(5), .disabled("Z"), .enable("false")) multiplexer_8 (
    .in0(in_8), .in1({5{1'b0}}), .out(multiplexer_8_out), .sel(\同步清零 ));
  not not_1 (not_1_out, \使能端 );
  Register #(.width(3), .trigger("rising"), .Select("low")) register_1 (
    .D(multiplexer_1_out), .en(not_1_out), .Q(out_12), .clk(CLK));  // open: clr
  Register #(.width(3), .trigger("rising"), .Select("low")) register_2 (
    .D(multiplexer_2_out), .en(not_1_out), .Q(out_13), .clk(CLK));  // open: clr
  Register #(.width(32), .trigger("rising"), .Select("low")) register_3 (
    .D(multiplexer_3_out), .en(not_1_out), .Q(out_14), .clk(CLK));  // open: clr
  Register #(.width(32), .trigger("rising"), .Select("low")) register_4 (
    .D(multiplexer_4_out), .en(not_1_out), .Q(out_15), .clk(CLK));  // open: clr
  Register #(.width(32), .trigger("rising"), .Select("low")) register_5 (
    .D(multiplexer_5_out), .en(not_1_out), .Q(out_16), .clk(CLK));  // open: clr
  Register #(.width(32), .trigger("rising"), .Select("low")) register_6 (
    .D(multiplexer_6_out), .en(not_1_out), .Q(out_17), .clk(CLK));  // open: clr
  Register #(.width(32), .trigger("rising"), .Select("low")) register_7 (
    .D(multiplexer_7_out), .en(not_1_out), .Q(out_18), .clk(CLK));  // open: clr
  Register #(.width(5), .trigger("rising"), .Select("low")) register_8 (
    .D(multiplexer_8_out), .en(not_1_out), .Q(out_19), .clk(CLK));  // open: clr
endmodule

module ID_EX (
  input  [1:0] \预测情况 ,
  input  [2:0] in_2,
  input  [2:0] in_3,
  input  [31:0] in_4,
  input  [25:0] in_5,
  input  [31:0] IR,
  input  [31:0] PC,
  input  [31:0] in_8,
  input  [31:0] in_9,
  input  [31:0] in_10,
  input  [31:0] in_11,
  input  [4:0] in_12,
  input  [4:0] in_13,
  input  [4:0] in_14,
  input  [4:0] in_15,
  input  \同步清零 ,
  input  \使能端 ,
  input  CLK,
  output [1:0] out_19,
  output [2:0] out_20,
  output [2:0] out_21,
  output [31:0] out_22,
  output [25:0] out_23,
  output [31:0] out_24,
  output [31:0] out_25,
  output [31:0] out_26,
  output [31:0] out_27,
  output [31:0] out_28,
  output [31:0] out_29,
  output [4:0] out_30,
  output [4:0] out_31,
  output [4:0] out_32,
  output [4:0] out_33
);

  wire not_1_out;
  wire [1:0] multiplexer_1_out;
  wire [2:0] multiplexer_2_out, multiplexer_3_out;
  wire [4:0] multiplexer_12_out, multiplexer_13_out, multiplexer_14_out, multiplexer_15_out;
  wire [25:0] multiplexer_5_out;
  wire [31:0] multiplexer_4_out, multiplexer_6_out, multiplexer_7_out, multiplexer_8_out, multiplexer_9_out,
       multiplexer_10_out, multiplexer_11_out;

  Pull_Resistor #(.pull(0)) pull_resistor_1 (.node(in_2));
  Pull_Resistor #(.pull(0)) pull_resistor_2 (.node(\同步清零 ));
  Pull_Resistor #(.pull(0)) pull_resistor_3 (.node(\使能端 ));
  Pull_Resistor #(.pull(0)) pull_resistor_4 (.node(in_4));
  Multiplexer #(.select(1), .width(2), .disabled("Z"), .enable("false")) multiplexer_1 (
    .in0(\预测情况 ), .in1(2'b00), .out(multiplexer_1_out), .sel(\同步清零 ));
  Multiplexer #(.select(1), .width(3), .disabled("Z"), .enable("false")) multiplexer_2 (
    .in0(in_2), .in1(3'b000), .out(multiplexer_2_out), .sel(\同步清零 ));
  Multiplexer #(.select(1), .width(3), .disabled("Z"), .enable("false")) multiplexer_3 (
    .in0(in_3), .in1(3'b000), .out(multiplexer_3_out), .sel(\同步清零 ));
  Multiplexer #(.select(1), .width(32), .disabled("Z"), .enable("false")) multiplexer_4 (
    .in0(in_4), .in1({32{1'b0}}), .out(multiplexer_4_out), .sel(\同步清零 ));
  Multiplexer #(.select(1), .width(26), .disabled("Z"), .enable("false")) multiplexer_5 (
    .in0(in_5), .in1({26{1'b0}}), .out(multiplexer_5_out), .sel(\同步清零 ));
  Multiplexer #(.select(1), .width(32), .disabled("Z"), .enable("false")) multiplexer_6 (
    .in0(IR), .in1({32{1'b0}}), .out(multiplexer_6_out), .sel(\同步清零 ));
  Multiplexer #(.select(1), .width(32), .disabled("Z"), .enable("false")) multiplexer_7 (
    .in0(PC), .in1({32{1'b0}}), .out(multiplexer_7_out), .sel(\同步清零 ));
  Multiplexer #(.select(1), .width(32), .disabled("Z"), .enable("false")) multiplexer_8 (
    .in0(in_8), .in1({32{1'b0}}), .out(multiplexer_8_out), .sel(\同步清零 ));
  Multiplexer #(.select(1), .width(32), .disabled("Z"), .enable("false")) multiplexer_9 (
    .in0(in_9), .in1({32{1'b0}}), .out(multiplexer_9_out), .sel(\同步清零 ));
  Multiplexer #(.select(1), .width(32), .disabled("Z"), .enable("false")) multiplexer_10 (
    .in0(in_10), .in1({32{1'b0}}), .out(multiplexer_10_out), .sel(\同步清零 ));
  Multiplexer #(.select(1), .width(32), .disabled("Z"), .enable("false")) multiplexer_11 (
    .in0(in_11), .in1({32{1'b0}}), .out(multiplexer_11_out), .sel(\同步清零 ));
  Multiplexer #(.select(1), .width(5), .disabled("Z"), .enable("false")) multiplexer_12 (
    .in0(in_12), .in1({5{1'b0}}), .out(multiplexer_12_out), .sel(\同步清零 ));
  Multiplexer #(.select(1), .width(5), .disabled("Z"), .enable("false")) multiplexer_13 (
    .in0(in_13), .in1({5{1'b0}}), .out(multiplexer_13_out), .sel(\同步清零 ));
  Multiplexer #(.select(1), .width(5), .disabled("Z"), .enable("false")) multiplexer_14 (
    .in0(in_14), .in1({5{1'b0}}), .out(multiplexer_14_out), .sel(\同步清零 ));
  Multiplexer #(.select(1), .width(5), .disabled("Z"), .enable("false")) multiplexer_15 (
    .in0(in_15), .in1({5{1'b0}}), .out(multiplexer_15_out), .sel(\同步清零 ));
  not not_1 (not_1_out, \使能端 );
  Register #(.width(2), .trigger("rising"), .Select("low")) register_1 (
    .D(multiplexer_1_out), .en(not_1_out), .Q(out_19), .clk(CLK));  // open: clr
  Register #(.width(3), .trigger("rising"), .Select("low")) register_2 (
    .D(multiplexer_2_out), .en(not_1_out), .Q(out_20), .clk(CLK));  // open: clr
  Register #(.width(3), .trigger("rising"), .Select("low")) register_3 (
    .D(multiplexer_3_out), .Q(out_21), .clk(CLK));  // open: en, clr
  Register #(.width(32), .trigger("rising"), .Select("low")) register_4 (
    .D(multiplexer_4_out), .en(not_1_out), .Q(out_22), .clk(CLK));  // open: clr
  Register #(.width(26), .trigger("rising"), .Select("low")) register_5 (
    .D(multiplexer_5_out), .en(not_1_out), .Q(out_23), .clk(CLK));  // open: clr
  Register #(.width(32), .trigger("rising"), .Select("low")) register_6 (
    .D(multiplexer_6_out), .en(not_1_out), .Q(out_24), .clk(CLK));  // open: clr
  Register #(.width(32), .trigger("rising"), .Select("low")) register_7 (
    .D(multiplexer_7_out), .en(not_1_out), .Q(out_25), .clk(CLK));  // open: clr
  Register #(.width(32), .trigger("rising"), .Select("low")) register_8 (
    .D(multiplexer_8_out), .en(not_1_out), .Q(out_26), .clk(CLK));  // open: clr
  Register #(.width(32), .trigger("rising"), .Select("low")) register_9 (
    .D(multiplexer_9_out), .en(not_1_out), .Q(out_27), .clk(CLK));  // open: clr
  Register #(.width(32), .trigger("rising"), .Select("low")) register_10 (
    .D(multiplexer_10_out), .en(not_1_out), .Q(out_28), .clk(CLK));  // open: clr
  Register #(.width(32), .trigger("rising"), .Select("low")) register_11 (
    .D(multiplexer_11_out), .en(not_1_out), .Q(out_29), .clk(CLK));  // open: clr
  Register #(.width(5), .trigger("rising"), .Select("low")) register_12 (
    .D(multiplexer_12_out), .en(not_1_out), .Q(out_30), .clk(CLK));  // open: clr
  Register #(.width(5), .trigger("rising"), .Select("low")) register_13 (
    .D(multiplexer_13_out), .en(not_1_out), .Q(out_31), .clk(CLK));  // open: clr
  Register #(.width(5), .trigger("rising"), .Select("low")) register_14 (
    .D(multiplexer_14_out), .en(not_1_out), .Q(out_32), .clk(CLK));  // open: clr
  Register #(.width(5), .trigger("rising"), .Select("low")) register_15 (
    .D(multiplexer_15_out), .en(not_1_out), .Q(out_33), .clk(CLK));  // open: clr
endmodule

module IF_ID (
  input  [1:0] \预测跳转 ,
  input  [31:0] PC,
  input  [31:0] in_3,
  input  [31:0] in_4,
  input  \同步清零 ,
  input  \使能端 ,
  input  CLK,
  output [1:0] out_8,
  output [31:0] out_9,
  output [31:0] out_10,
  output [31:0] out_11
);

  wire not_1_out;
  wire [1:0] multiplexer_1_out;
  wire [31:0] multiplexer_2_out, multiplexer_3_out, multiplexer_4_out;

  Pull_Resistor #(.pull(0)) pull_resistor_1 (.node(\同步清零 ));
  Multiplexer #(.select(1), .width(2), .disabled("Z"), .enable("false")) multiplexer_1 (
    .in0(\预测跳转 ), .in1(2'b00), .out(multiplexer_1_out), .sel(\同步清零 ));
  Multiplexer #(.select(1), .width(32), .disabled("Z"), .enable("false")) multiplexer_2 (
    .in0(PC), .in1({32{1'b0}}), .out(multiplexer_2_out), .sel(\同步清零 ));
  Multiplexer #(.select(1), .width(32), .disabled("Z"), .enable("false")) multiplexer_3 (
    .in0(in_3), .in1({32{1'b0}}), .out(multiplexer_3_out), .sel(\同步清零 ));
  Multiplexer #(.select(1), .width(32), .disabled("Z"), .enable("false")) multiplexer_4 (
    .in0(in_4), .in1({32{1'b0}}), .out(multiplexer_4_out), .sel(\同步清零 ));
  not not_1 (not_1_out, \使能端 );
  Register #(.width(2), .trigger("rising"), .Select("low")) register_1 (
    .D(multiplexer_1_out), .en(not_1_out), .Q(out_8), .clk(CLK));  // open: clr
  Register #(.width(32), .trigger("rising"), .Select("low")) register_2 (
    .D(multiplexer_2_out), .en(not_1_out), .Q(out_9), .clk(CLK));  // open: clr
  Register #(.width(32), .trigger("rising"), .Select("low")) register_3 (
    .D(multiplexer_3_out), .en(not_1_out), .Q(out_10), .clk(CLK));  // open: clr
  Register #(.width(32), .trigger("rising"), .Select("low")) register_4 (
    .D(multiplexer_4_out), .en(not_1_out), .Q(out_11), .clk(CLK));  // open: clr
  Pull_Resistor #(.pull(0)) pull_resistor_2 (.node(\使能端 ));
endmodule

module \指令存储器  (
  input  [31:0] PC,
  output [31:0] Instruction
);

  wire demultiplexer_1_out0, demultiplexer_1_out1, demultiplexer_1_out2, demultiplexer_1_out3,
       demultiplexer_2_out0, demultiplexer_2_out3;

  Demultiplexer #(.select(2), .width(1), .tristate("false"), .disabled("Z"), .enable("false")) demultiplexer_1 (
    .out0(demultiplexer_1_out0), .out1(demultiplexer_1_out1), .out2(demultiplexer_1_out2),
    .out3(demultiplexer_1_out3), .in(1'b1), .sel(PC[25:24]));
  Demultiplexer #(.select(2), .width(1), .tristate("false"), .disabled("Z"), .enable("false")) demultiplexer_2 (
    .out0(demultiplexer_2_out0), .out3(demultiplexer_2_out3), .in(demultiplexer_1_out0), .sel(PC[13:12]));  // open: out1, out2
  ROM #(.addrWidth(10), .dataWidth(32), .Select("high")) \BIOS存储器  (
    .addr(PC[11:2]), .data(Instruction), .sel(demultiplexer_2_out0));
  ROM #(.addrWidth(10), .dataWidth(32), .Select("high")) shell (
    .addr(PC[11:2]), .data(Instruction), .sel(demultiplexer_2_out3));
  ROM #(.addrWidth(22), .dataWidth(32), .Select("high")) \_1号中断服务程序存储器  (
    .addr(PC[23:2]), .data(Instruction), .sel(demultiplexer_1_out1));
  ROM #(.addrWidth(22), .dataWidth(32), .Select("high")) \_2号中断服务程序存储器  (
    .addr(PC[23:2]), .data(Instruction), .sel(demultiplexer_1_out2));
  ROM #(.addrWidth(22), .dataWidth(32), .Select("high")) \_3号中断服务程序存储器  (
    .addr(PC[23:2]), .data(Instruction), .sel(demultiplexer_1_out3));
  ROM #(.addrWidth(10), .dataWidth(32), .Select("high")) \u_排序指令存储器  ();  // open: addr, data
  ROM #(.addrWidth(10), .dataWidth(32), .Select("high")) \u_气泡流水线测试指令存储器  ();  // open: addr, data
  ROM #(.addrWidth(10), .dataWidth(32), .Select("high")) music ();  // open: addr, data
  ROM #(.addrWidth(10), .dataWidth(32), .Select("high")) \u_走马灯指令存储器  ();  // open: addr, data
  ROM #(.addrWidth(10), .dataWidth(32), .Select("high")) \benchmark指令存储器  ();  // open: addr, data
  ROM #(.addrWidth(10), .dataWidth(32), .Select("high")) \u_分支预测指令存储器  ();  // open: addr, data
  ROM #(.addrWidth(22), .dataWidth(32), .Select("high")) \_1号中断服务程序存储器_2  ();  // open: addr, data
  ROM #(.addrWidth(10), .dataWidth(32), .Select("high")) \benchmark_ccmb指令存储器  ();  // open: addr, data

  // Notes on the sheet:
  //   contents of BIOS存储器 (hex, n*v repeats v):
  //   0 3c0100ff 3421fefc 1e820 24100001 40900000 8000c00
  //   contents of shell (hex, n*v repeats v):
  //   24020004 20040000 c 24020004 2004000d c 24020004 2004001f c 24020004 20040033 c 2402000c c 28820
  //   20010030 1031000c 20010031 10310011 20010032 10310015 20010038 10310013 20010039 1031001a 24020004
  //   2004003b c 8000c0c 24020004 2004006a c 24040080 24050003 c000c52 8000c19 24020004 2004006d c
  //   24040380 c000c3b 8000c19 24020004 20040070 c 24090002 3c010100 ac29ff00 3c010100 ac20ff00 8000c00
  //   24020004 20040073 c 24020004 20040055 c 2402000a c 44820 200b0000 200c0080 200e0080 20070002
  //   200a0000 3c010100 ac2aff07 3c010100 ac2bff08 214a0001 8d260000 3c010100 ac26ff09 3c010100 ac27ff0a
  //   3c010100 ac20ff0a 21290004 154cfff2 216b0001 156effef 3e00008 44020 240effff 240f0080 24050028
  //   3c010100 ac25ff05 8d090000 112e0006 3c010100 ac2fff06 3c010100 ac29ff06 21080004 1000fff8 3c010100
  //   ac20ff04 3e00008
  //   contents of _1号中断服务程序存储器 (hex, n*v repeats v):
  //   40080800 afa80000 20010004 10220007 2001000a 10220017 2001000c 1022000f 20010032 10220015 10000017
  //   44020 24050001 81090000 11200013 3c010100 ac29ff01 3c010100 ac25ff00 3c010100 ac20ff00 21080001
  //   1000fff6 3c010100 8c28ff02 1100fffd 3c010100 8c22ff03 10000005 20083000 10000003 3c010100 8c28ffff
  //   1100fffd 8fa80000 40880800 42000018
  //   contents of _2号中断服务程序存储器 (hex, n*v repeats v):
  //   23bdffd8 afb70000 afb60004 afb50008 afb4000c afb30010 afb20014 afb10018 afb0001c afa20020 afa40024
  //   40100800 afb00028 20100001 40900000 20160002 20140006 20150001 168020 108100 2149825 132020 20020022
  //   c 1600fffa 295a022 1680fff7 40800000 8fb00028 40900800 8fa40024 8fa20020 8fb0001c 8fb10018 8fb20014
  //   8fb30010 8fb4000c 8fb50008 8fb60004 8fb70000 23bd0028 42000018
  //   contents of _3号中断服务程序存储器 (hex, n*v repeats v):
  //   23bdffd8 afb70000 afb60004 afb50008 afb4000c afb30010 afb20014 afb10018 afb0001c afa20020 afa40024
  //   40100800 afb00028 20100001 40900000 20160003 20140006 20150001 168020 108100 2149825 132020 20020022
  //   c 1600fffa 295a022 1680fff7 40800000 8fb00028 40900800 8fa40024 8fa20020 8fb0001c 8fb10018 8fb20014
  //   8fb30010 8fb4000c 8fb50008 8fb60004 8fb70000 23bd0028 42000018
  //   contents of 排序指令存储器 (hex, n*v repeats v):
  //   2010ffff 20110000 ae300000 22100001 22310004 ae300000 22100001 22310004 ae300000 22100001 22310004
  //   ae300000 22100001 22310004 ae300000 22100001 22310004 ae300000 22100001 22310004 ae300000 22100001
  //   22310004 ae300000 22100001 22310004 ae300000 22100001 22310004 ae300000 22100001 22310004 ae300000
  //   22100001 22310004 ae300000 22100001 22310004 ae300000 22100001 22310004 ae300000 22100001 22310004
  //   ae300000 22100001 22310004 ae300000 22100001 22310004 22100001 8020 2011003c 8e130000 8e340000
  //   274402a 11000002 ae330000 ae140000 2231fffc 1611fff8 102020 20020022 c 22100004 2011003c 1611fff2
  //   20020032 c
  //   contents of 气泡流水线测试指令存储器 (hex, n*v repeats v):
  //   20110004 ae310000 8e320000 2252fffc 20100000 22110001 2118020 22520004 ae500000 22310001 2118020
  //   22520004 ae500000 22310001 2118020 22520004 ae500000 22310001 2118020 22520004 ae500000 22310001
  //   2118020 22520004 ae500000 22310001 2118020 22520004 ae500000 22310001 2118020 22520004 ae500000
  //   20020032 20100000 20100000 20100000 c
  //   contents of music (hex, n*v repeats v):
  //   44020 240effff 240f0080 24050028 3c010100 ac25ff05 8d090000 112e0006 3c010100 ac2fff06 3c010100
  //   ac29ff06 21080004 1000fff8 3c010100 ac20ff04 3e00008
  //   contents of 走马灯指令存储器 (hex, n*v repeats v):
  //   20100001 109fc0 139fc3 8021 2012000c 24160003 26100001 3210000f 20080008 20090001 139900 2709825
  //   132020 20020022 c 1094022 1500fff9 22100001 2018000f 2188024 108700 20080008 20090001 139902 2709825
  //   132021 20020022 c 1094022 1500fff9 108702 2c9b022 12c00001 8000c06 4020 1084027 84400 3508ffff
  //   132021 20020022 c 0 8000c00
  //   contents of benchmark指令存储器 (hex, n*v repeats v):
  //   20110001 8000c05 20110001 20120002 20130003 8000c09 20110001 20120002 20130003 8000c0d 20110001
  //   20120002 20130003 8000c11 20110001 20120002 20130003 c000cb8 20100001 20110001 118fc0 112020
  //   20020022 c 118882 12200001 8000c15 112020 20020022 c 20110001 118880 112020 20020022 c 12200001
  //   8000c1f 20110001 118fc0 112020 20020022 c 1188c3 112020 20020022 c 118903 112020 20020022 c 118903
  //   112020 20020022 c 118903 112020 20020022 c 118903 112020 20020022 c 118903 112020 20020022 c 118903
  //   112020 20020022 c 118903 112020 20020022 c 20100001 109fc0 139fc3 8021 2012000c 24160003 26100001
  //   3210000f 20080008 20090001 139900 2709825 132020 20020022 c 1094022 1500fff9 22100001 2018000f
  //   2188024 108700 20080008 20090001 139902 2709825 132021 20020022 c 1094022 1500fff9 108702 2c9b022
  //   12c00001 8000c50 4020 1084027 84400 3508ffff 82021 20020022 c 2010ffff 20110000 ae300000 22100001
  //   22310004 ae300000 22100001 22310004 ae300000 22100001 22310004 ae300000 22100001 22310004 ae300000
  //   22100001 22310004 ae300000 22100001 22310004 ae300000 22100001 22310004 ae300000 22100001 22310004
  //   ae300000 22100001 22310004 ae300000 22100001 22310004 ae300000 22100001 22310004 ae300000 22100001
  //   22310004 ae300000 22100001 22310004 ae300000 22100001 22310004 ae300000 22100001 22310004 ae300000
  //   22100001 22310004 22100001 8020 2011003c 8e130000 8e340000 274402a 11000002 ae330000 ae140000
  //   2231fffc 1611fff8 102020 20020022 c 22100004 2011003c 1611fff2 20020032 c 20100000 22100001 102020
  //   20020022 c 22100002 102020 20020022 c 22100003 102020 20020022 c 22100004 102020 20020022 c 22100005
  //   102020 20020022 c 22100006 102020 20020022 c 22100007 102020 20020022 c 22100008 102020 20020022
  //   20020022 c 3e00008
  //   contents of 分支预测指令存储器 (hex, n*v repeats v):
  //   20110005 8000c06 20110001 20120002 20130003 20140004 8000c0b 20110001 20120002 20130003 20140004
  //   8000c10 20110001 20120002 20130003 20140004 8000c15 20110001 20120002 20130003 20140004 8000c1a
  //   20110001 20120002 20130003 20140004 8000c1f 20110001 20120002 20130003 20140004 8000c24 20110001
  //   20120002 20130003 20140004 8000c29 20110001 20120002 20130003 20140004 2231ffff 1620ffe0 20100001
  //   201200ff 20110001 20130003 12120005 12100004 20110001 20120002 20130003 20140004 16310004 16320003
  //   20110001 20120002 20130003 c000c3d 2002000a c 20100000 22100001 102020 20020022 c 3e00008
  //   contents of _1号中断服务程序存储器_2 (hex, n*v repeats v):
  //   23bdffd8 afb70000 afb60004 afb50008 afb4000c afb30010 afb20014 afb10018 afb0001c afa20020 afa40024
  //   40100800 afb00028 20100001 40900000 20160001 20140006 20150001 168020 108100 2149825 132020 20020022
  //   c 1600fffa 295a022 1680fff7 40800000 8fb00028 40900800 8fa40024 8fa20020 8fb0001c 8fb10018 8fb20014
  //   8fb30010 8fb4000c 8fb50008 8fb60004 8fb70000 23bd0028 42000018
  //   contents of benchmark_ccmb指令存储器 (hex, n*v repeats v):
  //   20110001 8000c05 20110001 20120002 20130003 8000c09 20110001 20120002 20130003 8000c0d 20110001
  //   20120002 20130003 8000c11 20110001 20120002 20130003 c000d36 20040000 20020032 c 4*0 20100001
  //   20110001 118fc0 112020 20020022 c 118882 12200001 8000c1c 112020 20020022 c 20040000 20020032 c 4*0
  //   20110001 118880 112020 20020022 c 12200008 8000c2d 20040000 20020032 c 4*0 20110001 118fc0 112020
  //   20020022 c 1188c3 112020 20020022 c 118903 112020 20020022 c 118903 112020 20020022 c 118903 112020
  //   20020022 c 118903 112020 20020022 c 118903 112020 20020022 c 118903 112020 20020022 c 118903 112020
  //   20020022 c 20040000 20020032 c 4*0 20100001 109fc0 139fc3 8021 2012000c 24160003 26100001 3210000f
  //   20080008 20090001 139900 2709825 132020 20020022 c 1094022 1500fff9 22100001 2018000f 2188024 108700
  //   20080008 20090001 139902 2709825 132021 20020022 c 1094022 1500fff9 108702 2c9b022 12c00001 8000c6c
  //   4020 1084027 84400 3508ffff 82021 20020022 c 20040000 20020032 c 4*0 2010ffff 20110000 ae300000
  //   22100001 22310004 ae300000 22100001 22310004 ae300000 22100001 22310004 ae300000 22100001 22310004
  //   ae300000 22100001 22310004 ae300000 22100001 22310004 ae300000 22100001 22310004 ae300000 22100001
  //   22310004 ae300000 22100001 22310004 ae300000 22100001 22310004 ae300000 22100001 22310004 ae300000
  //   22100001 22310004 ae300000 22100001 22310004 ae300000 22100001 22310004 ae300000 22100001 22310004
  //   ae300000 22100001 22310004 22100001 8020 2011003c 8e130000 8e340000 274402a 11000002 ae330000
  //   ae140000 2231fffc 1611fff8 102020 20020022 c 22100004 2011003c 1611fff2 20020032 c 4*0 2008ffff
  //   20117777 112020 20020022 c 200b0010 3a31ffff 112020 20020022 c 216bffff 1560fffa 20045000 20020032 c
  //   4*0 200b0008 3c11fedc 3631ffff 112020 20020022 c 3c11ba98 112020 c 3c117654 112020 c 3c113210 112020
  //   c 216bffff 1560fff0 20045008 20020032 c 4*0 20090000 200b0010 34118483 20120404 118c00 129400
  //   36318281 22520404 ad310000 2328820 21290004 216bffff 1560fffb 200b0020 20090000 95310000 112020
  //   20020022 c 21290002 216bffff 1560fff9 2004500c 20020032 c 4*0 2011fff1 112020 20020022 c 22310001
  //   620fffb 20045010 20020032 c 4*0 2002000a c 20100000 22100001 102020 20020022 c 22100002 102020
  //   20020022 c 22100003 102020 20020022 c 22100004 102020 20020022 c 22100005 102020 20020022 c 22100006
  //   102020 20020022 c 22100007 102020 20020022 c 22100008 102020 20020022 20020022 c 3e00008
endmodule

// 清零信号生成
module \rs_rt清零  (
  input  OP0,
  input  OP1,
  input  OP2,
  input  OP3,
  input  OP4,
  input  OP5,
  input  F0,
  input  F1,
  input  F2,
  input  F3,
  input  F4,
  input  F5,
  output clearRt,
  output clearRs
);

  wire and_1_out, and_2_out, and_3_out, and_4_out, and_5_out, and_6_out, and_7_out, and_8_out, and_9_out,
       and_10_out, and_11_out, and_12_out, and_13_out, and_14_out, and_15_out, and_16_out, and_17_out,
       not_1_out, not_2_out, not_3_out, not_4_out, not_5_out, not_6_out, not_7_out, not_8_out, not_9_out,
       not_10_out, not_11_out, not_12_out, not_13_out, not_14_out, not_15_out, not_16_out, not_17_out,
       not_18_out, not_19_out, not_20_out, not_21_out, not_22_out, not_23_out, not_24_out, not_25_out,
       not_26_out, not_27_out, not_28_out, not_29_out, not_30_out, not_31_out, not_32_out, not_33_out,
       not_34_out, not_35_out, not_36_out, not_37_out, not_38_out, not_39_out, not_40_out, not_41_out,
       not_42_out, not_43_out, not_44_out, not_45_out, not_46_out, not_47_out, not_48_out, not_49_out,
       not_50_out, not_51_out, not_52_out, not_53_out, not_54_out, not_55_out, not_56_out, not_57_out,
       not_58_out, not_59_out, not_60_out, not_61_out, not_62_out, not_63_out, not_64_out, not_65_out,
       not_66_out, not_67_out, not_68_out, not_69_out, not_70_out, not_71_out, not_72_out, not_73_out,
       not_74_out, not_75_out, not_76_out, not_77_out, not_78_out, not_79_out, not_80_out, not_81_out,
       not_82_out, not_83_out, not_84_out, not_85_out, not_86_out, not_87_out, not_88_out;

  not not_1 (not_1_out, OP5);
  not not_2 (not_2_out, OP4);
  not not_3 (not_3_out, OP3);
  not not_4 (not_4_out, OP2);
  not not_5 (not_5_out, OP1);
  not not_6 (not_6_out, OP0);
  not not_7 (not_7_out, F5);
  not not_8 (not_8_out, F4);
  not not_9 (not_9_out, F2);
  not not_10 (not_10_out, F1);
  not not_11 (not_11_out, F0);
  not not_12 (not_12_out, OP5);
  not not_13 (not_13_out, OP4);
  not not_14 (not_14_out, OP3);
  not not_15 (not_15_out, OP2);
  not not_16 (not_16_out, OP0);
  not not_17 (not_17_out, OP5);
  not not_18 (not_18_out, OP4);
  not not_19 (not_19_out, OP3);
  not not_20 (not_20_out, OP2);
  not not_21 (not_21_out, OP5);
  not not_22 (not_22_out, OP4);
  not not_23 (not_23_out, OP2);
  not not_24 (not_24_out, OP1);
  not not_25 (not_25_out, OP0);
  not not_26 (not_26_out, OP5);
  not not_27 (not_27_out, OP4);
  not not_28 (not_28_out, OP1);
  not not_29 (not_29_out, OP0);
  not not_30 (not_30_out, OP5);
  not not_31 (not_31_out, OP4);
  not not_32 (not_32_out, OP2);
  not not_33 (not_33_out, OP1);
  not not_34 (not_34_out, OP5);
  not not_35 (not_35_out, OP4);
  not not_36 (not_36_out, OP2);
  not not_37 (not_37_out, OP0);
  not not_38 (not_38_out, OP5);
  not not_39 (not_39_out, OP4);
  not not_40 (not_40_out, OP1);
  not not_41 (not_41_out, OP4);
  not not_42 (not_42_out, OP3);
  not not_43 (not_43_out, OP2);
  not not_44 (not_44_out, OP5);
  not not_45 (not_45_out, OP4);
  not not_46 (not_46_out, OP0);
  not not_47 (not_47_out, OP5);
  not not_48 (not_48_out, OP4);
  not not_49 (not_49_out, OP4);
  not not_50 (not_50_out, OP3);
  not not_51 (not_51_out, OP1);
  not not_52 (not_52_out, OP4);
  not not_53 (not_53_out, OP3);
  not not_54 (not_54_out, OP2);
  not not_55 (not_55_out, OP1);
  not not_56 (not_56_out, OP0);
  not not_57 (not_57_out, F5);
  not not_58 (not_58_out, F4);
  not not_59 (not_59_out, F3);
  not not_60 (not_60_out, F2);
  not not_61 (not_61_out, F1);
  not not_62 (not_62_out, F0);
  not not_63 (not_63_out, OP0);
  not not_64 (not_64_out, OP1);
  not not_65 (not_65_out, OP2);
  not not_66 (not_66_out, OP3);
  not not_67 (not_67_out, OP5);
  not not_68 (not_68_out, F0);
  not not_69 (not_69_out, F1);
  not not_70 (not_70_out, F2);
  not not_71 (not_71_out, F3);
  not not_72 (not_72_out, F4);
  not not_73 (not_73_out, F5);
  not not_74 (not_74_out, OP0);
  not not_75 (not_75_out, OP1);
  not not_76 (not_76_out, OP2);
  not not_77 (not_77_out, OP3);
  not not_78 (not_78_out, OP5);
  not not_79 (not_79_out, F0);
  not not_80 (not_80_out, F1);
  not not_81 (not_81_out, F2);
  not not_82 (not_82_out, F5);
  not not_83 (not_83_out, OP2);
  not not_84 (not_84_out, OP3);
  not not_85 (not_85_out, OP4);
  not not_86 (not_86_out, OP5);
  not not_87 (not_87_out, OP4);
  not not_88 (not_88_out, OP5);
  and and_1 (and_1_out, not_1_out, not_2_out, not_3_out, not_4_out, not_5_out, not_6_out, not_7_out, not_8_out, F3, not_9_out, not_10_out, not_11_out);
  and and_2 (and_2_out, not_12_out, not_13_out, not_14_out, not_15_out, OP1, not_16_out);
  and and_3 (and_3_out, not_17_out, not_18_out, not_19_out, not_20_out, OP1, OP0);
  and and_4 (and_4_out, not_21_out, not_22_out, OP3, not_23_out, not_24_out, not_25_out);
  and and_5 (and_5_out, not_26_out, not_27_out, OP3, OP2, not_28_out, not_29_out);
  and and_6 (and_6_out, not_30_out, not_31_out, OP3, not_32_out, not_33_out, OP0);
  and and_7 (and_7_out, not_34_out, not_35_out, OP3, not_36_out, OP1, not_37_out);
  and and_8 (and_8_out, not_38_out, not_39_out, OP3, OP2, not_40_out, OP0);
  and and_9 (and_9_out, OP5, not_41_out, not_42_out, not_43_out, OP1, OP0);
  and and_10 (and_10_out, not_44_out, not_45_out, OP3, OP2, OP1, not_46_out);
  and and_11 (and_11_out, not_47_out, not_48_out, OP3, OP2, OP1, OP0);
  and and_12 (and_12_out, OP5, not_49_out, not_50_out, OP2, not_51_out, OP0);
  and and_13 (and_13_out, OP5, not_52_out, not_53_out, not_54_out, not_55_out, not_56_out, not_57_out, not_58_out, not_59_out, not_60_out, not_61_out, not_62_out);
  and and_14 (and_14_out, not_63_out, not_64_out, not_65_out, not_66_out, OP4, not_67_out, not_68_out, not_69_out, not_70_out, not_71_out, not_72_out, not_73_out);
  and and_15 (and_15_out, not_74_out, not_75_out, not_76_out, not_77_out, OP4, not_78_out, not_79_out, not_80_out, not_81_out, F3, F4, not_82_out);
  and and_16 (and_16_out, OP1, not_83_out, not_84_out, not_85_out, not_86_out);
  and and_17 (and_17_out, OP0, OP1, OP2, OP3, not_87_out, not_88_out);
  or or_1 (clearRs, and_14_out, and_15_out, and_16_out, and_17_out);
  or or_2 (clearRt, and_1_out, and_2_out, and_3_out, and_4_out, and_5_out, and_6_out, and_7_out, and_8_out, and_9_out, and_10_out, and_11_out, and_12_out, and_13_out);
endmodule

// BHT状态
module \BHT状态转换电路  (
  input  [1:0] \现态 ,
  input  \分支成功 ,
  output [1:0] \次态 
);

  wire nand_1_out, nand_2_out, nand_3_out, nand_4_out, nand_5_out, nand_6_out, nand_7_out, nand_8_out,
       nand_9_out;

  nand nand_1 (nand_1_out, \现态 [0], \现态 [0]);
  nand nand_2 (nand_2_out, \现态 [0], \现态 [0]);
  nand nand_3 (nand_3_out, \分支成功 , \分支成功 );
  nand nand_4 (nand_4_out, \现态 [1], \现态 [1]);
  nand nand_5 (nand_5_out, \现态 [0], \现态 [0]);
  nand nand_6 (nand_6_out, \现态 [0], \分支成功 );
  nand nand_7 (nand_7_out, \现态 [1], nand_1_out);
  nand nand_8 (nand_8_out, \现态 [1], nand_2_out, nand_3_out);
  nand nand_9 (nand_9_out, nand_4_out, nand_5_out, \分支成功 );
  nand nand_10 (\次态 [1], nand_6_out, nand_7_out);
  nand nand_11 (\次态 [0], nand_8_out, nand_9_out);
endmodule

module NPC (
  input  [31:0] \JR指令目标地址 ,
  input  JR,
  input  [31:0] \J与JAL指令目标地址 ,
  input  \J或JAL ,
  input  [1:0] \预测结果 ,
  input  \成功分支 ,
  input  [31:0] \条件分支目标地址 ,
  input  [31:0] EX_PC_4,
  input  [31:0] IF_PC_4,
  input  [31:0] EPC,
  input  ERET,
  output [31:0] \BHT分支地址 ,
  output [31:0] PC_next
);

  wire and_1_out, and_2_out, and_3_out, and_4_out, and_5_out, nor_1_out, or_1_out;
  wire [31:0] controlled_buffer_1_out, controlled_buffer_3_out;

  assign controlled_buffer_1_out = JR ? \JR指令目标地址  : 32'bz;  // Controlled_Buffer controlled_buffer_1
  assign controlled_buffer_1_out = \J或JAL  ? \J与JAL指令目标地址  : 32'bz;  // Controlled_Buffer controlled_buffer_2
  and and_1 (and_1_out, \预测结果 [1], ~\预测结果 [0]);  // AND_Gate
  and and_2 (and_2_out, \预测结果 [1], \预测结果 [0]);
  or or_1 (or_1_out, JR, \J或JAL );
  Multiplexer #(.select(1), .width(32), .disabled("Z"), .enable("false")) multiplexer_1 (
    .in0(\条件分支目标地址 ), .in1(controlled_buffer_1_out), .out(\BHT分支地址 ), .sel(or_1_out));
  and and_3 (and_3_out, or_1_out, ~\预测结果 [1]);  // AND_Gate
  and and_4 (and_4_out, ~and_2_out, \成功分支 );  // AND_Gate
  and and_5 (and_5_out, and_1_out, ~\成功分支 );  // AND_Gate
  assign controlled_buffer_3_out = and_3_out ? controlled_buffer_1_out : 32'bz;  // Controlled_Buffer controlled_buffer_3
  assign controlled_buffer_3_out = and_4_out ? \条件分支目标地址  : 32'bz;  // Controlled_Buffer controlled_buffer_4
  assign controlled_buffer_3_out = and_5_out ? EX_PC_4 : 32'bz;  // Controlled_Buffer controlled_buffer_5
  nor nor_1 (nor_1_out, and_3_out, and_4_out, and_5_out);
  assign controlled_buffer_3_out = nor_1_out ? IF_PC_4 : 32'bz;  // Controlled_Buffer controlled_buffer_6
  Multiplexer #(.select(1), .width(32), .disabled("Z"), .enable("false")) multiplexer_2 (
    .in0(controlled_buffer_3_out), .in1(EPC), .out(PC_next), .sel(ERET));
endmodule

module CP0 (
  input  \同步置IE为1 ,
  input  \中断隐指令 ,
  input  [31:0] RDin,
  input  WE,
  input  [4:0] W_num,
  input  CLK,
  output IE,
  output [31:0] EPC
);

  wire bitselector_1_out, d_ff_1_q, d_ff_2_q, demultiplexer_1_out0, demultiplexer_1_out1, or_1_out;
  wire [31:0] register_1_q;

  BitSelector #(.width(5), .group(1)) bitselector_1 (.in(W_num), .out(bitselector_1_out), .sel(3'b000));
  Demultiplexer #(.select(1), .width(1), .tristate("false"), .disabled("Z"), .enable("false")) demultiplexer_1 (
    .out0(demultiplexer_1_out0), .out1(demultiplexer_1_out1), .in(WE), .sel(bitselector_1_out));
  or or_1 (or_1_out, \中断隐指令 , demultiplexer_1_out1);
  D_Flip_Flop #(.trigger("falling"), .Pre_Clr_Positions("LEGACY"), .NegatePresetClear("false"), .enable("true"), .NewFFLayout("false")) d_ff_1 (
    .clk(CLK), .D(\同步置IE为1 ), .Q(d_ff_1_q));  // open: Qn, preset, en, reset
  D_Flip_Flop #(.trigger("falling"), .Pre_Clr_Positions("LEGACY"), .NegatePresetClear("false"), .enable("true"), .NewFFLayout("false")) d_ff_2 (
    .clk(CLK), .D(\中断隐指令 ), .Q(d_ff_2_q));  // open: Qn, preset, en, reset
  Register #(.width(32), .trigger("falling"), .Select("low")) register_1 (
    .D(RDin), .en(demultiplexer_1_out0), .Q(register_1_q), .clk(CLK), .clr(d_ff_2_q), .preset(d_ff_1_q));  // open: cs
  Register #(.width(32), .trigger("falling"), .Select("low")) register_2 (
    .D(RDin), .en(or_1_out), .Q(EPC), .clk(CLK));  // open: clr
  BitSelector #(.width(32), .group(1)) bitselector_2 (.in(register_1_q), .out(IE), .sel({5{1'b0}}));
endmodule

module \中断周期状态转换电路  (
  input  CLK,
  input  IR,
  input  ERET,
  output \初态 ,
  output \中断隐周期 ,
  output \中断服务周期 
);

  wire and_1_out, and_2_out, and_3_out, d_ff_1_q, d_ff_2_q, d_ff_2_qn, not_1_out, or_1_out, or_2_out;

  D_Flip_Flop #(.trigger("rising"), .Pre_Clr_Positions("LEGACY"), .NegatePresetClear("false"), .enable("true"), .NewFFLayout("false")) d_ff_1 (
    .clk(CLK), .D(or_1_out), .Q(d_ff_1_q), .Qn(\初态 ));  // open: preset, en, reset
  D_Flip_Flop #(.trigger("rising"), .Pre_Clr_Positions("LEGACY"), .NegatePresetClear("false"), .enable("true"), .NewFFLayout("false")) d_ff_2 (
    .clk(CLK), .D(or_2_out), .Q(d_ff_2_q), .Qn(d_ff_2_qn));  // open: preset, en, reset
  not not_1 (not_1_out, ERET);
  and and_1 (and_1_out, d_ff_1_q, not_1_out);
  and and_2 (and_2_out, d_ff_2_qn, ERET);
  and and_3 (and_3_out, d_ff_2_qn, IR);
  or or_1 (or_1_out, IR, and_1_out);
  or or_2 (or_2_out, \初态 , and_2_out, and_3_out);
  and and_4 (\中断隐周期 , d_ff_1_q, d_ff_2_q);
  and and_5 (\中断服务周期 , d_ff_1_q, d_ff_2_qn);
endmodule

module \中断测试电路  (
  input  in_1,
  input  [3:0] in_2,
  input  in_3,
  input  [2:0] in_4
);

  wire button_1_out, button_2_out, clock_1_out, \中断按键参考电路_1_p3 , \中断按键参考电路_1_p6 ;
  wire [7:0] mckeyboard_1_p4, mckeyboard_2_p2, mckeyboard_3_p1, or_1_out;

  Clock #(.highDuration(1), .lowDuration(1)) clock_1 (.out(clock_1_out));
  assign or_1_out = mckeyboard_3_p1 | mckeyboard_2_p2 | mckeyboard_1_p4;  // OR_Gate or_1, 8 bits wide
  Button button_1 (.out(button_1_out));
  Button button_2 (.out(button_2_out));
  // Probe on or_1_out
  // MCKeyboard mckeyboard_1: pin names not known; wires that end beside it: in_2, in_3, or_1_out, mckeyboard_1_p4
  // MCKeyboard mckeyboard_2: pin names not known; wires that end beside it: in_4, mckeyboard_2_p2
  // MCKeyboard mckeyboard_3: pin names not known; wires that end beside it: mckeyboard_3_p1
  // 中断按键参考电路 中断按键参考电路_1: pin names not known; wires that end beside it: clock_1_out, button_1_out, \中断按键参考电路_1_p3 , button_2_out, in_1, \中断按键参考电路_1_p6 
  Bit_Extender #(.in_width(16), .out_width(14), .\type ("zero")) bit_extender_1 ();  // open: in, out
  CP0 cp0_1 (
    .CLK(clock_1_out), .IE(\中断按键参考电路_1_p3 ), .\同步置IE为1 (in_1), .\中断隐指令 (\中断按键参考电路_1_p6 ));  // open: RDin, WE, W_num, EPC
endmodule

module IO (
  input  EN,
  input  [31:0] data,
  input  [3:0] addr,
  input  CLK,
  output [31:0] out_5,
  output [31:0] out_6,
  output [31:0] out_7,
  output [31:0] out_8,
  output [31:0] out_9,
  output [31:0] out_10,
  output [31:0] out_11,
  output [31:0] out_12,
  output [31:0] out_13,
  output [31:0] out_14,
  output [31:0] out_15
);

  wire demultiplexer_1_out0, demultiplexer_1_out1, demultiplexer_1_out4, demultiplexer_1_out5,
       demultiplexer_1_out6, demultiplexer_1_out7, demultiplexer_1_out8, demultiplexer_1_out9,
       demultiplexer_1_out10, undriven, undriven_2;
  wire [31:0] demultiplexer_2_out0, demultiplexer_2_out1, demultiplexer_2_out4, demultiplexer_2_out5,
       demultiplexer_2_out6, demultiplexer_2_out7, demultiplexer_2_out8, demultiplexer_2_out9,
       demultiplexer_2_out10, demultiplexer_2_out11, demultiplexer_2_out12, demultiplexer_2_out13,
       demultiplexer_2_out14, demultiplexer_2_out15;

  Demultiplexer #(.select(4), .width(1), .tristate("false"), .disabled("Z"), .enable("false")) demultiplexer_1 (
    .out0(demultiplexer_1_out0), .out1(demultiplexer_1_out1), .out4(demultiplexer_1_out4),
    .out5(demultiplexer_1_out5), .out6(demultiplexer_1_out6), .out7(demultiplexer_1_out7),
    .out8(demultiplexer_1_out8), .out9(demultiplexer_1_out9), .out10(demultiplexer_1_out10), .in(EN),
    .sel(addr));  // open: out2, out3, out11, out12, out13, out14, out15
  Demultiplexer #(.select(4), .width(32), .tristate("false"), .disabled("Z"), .enable("false")) demultiplexer_2 (
    .out0(demultiplexer_2_out0), .out1(demultiplexer_2_out1), .out4(demultiplexer_2_out4),
    .out5(demultiplexer_2_out5), .out6(demultiplexer_2_out6), .out7(demultiplexer_2_out7),
    .out8(demultiplexer_2_out8), .out9(demultiplexer_2_out9), .out10(demultiplexer_2_out10),
    .out11(demultiplexer_2_out11), .out12(demultiplexer_2_out12), .out13(demultiplexer_2_out13),
    .out14(demultiplexer_2_out14), .out15(demultiplexer_2_out15), .in(data), .sel(addr));  // open: out2, out3
  Register #(.width(32), .trigger("rising"), .Select("low")) register_1 (
    .D(demultiplexer_2_out0), .en(demultiplexer_1_out0), .Q(out_5), .clk(CLK));  // open: clr
  Register #(.width(32), .trigger("rising"), .Select("low")) register_2 (
    .D(demultiplexer_2_out1), .en(demultiplexer_1_out1), .Q(out_6), .clk(CLK));  // open: clr
  Register #(.width(32), .trigger("rising"), .Select("low")) register_3 (
    .D(demultiplexer_2_out4), .en(demultiplexer_1_out4), .Q(out_7), .clk(CLK));  // open: clr
  Register #(.width(32), .trigger("rising"), .Select("low")) register_4 (
    .D(demultiplexer_2_out5), .en(demultiplexer_1_out5), .Q(out_8), .clk(CLK));  // open: clr
  Register #(.width(32), .trigger("rising"), .Select("low")) register_5 (
    .D(demultiplexer_2_out6), .en(demultiplexer_1_out6), .Q(out_9), .clk(CLK));  // open: clr
  Register #(.width(32), .trigger("rising"), .Select("low")) register_6 (
    .D(demultiplexer_2_out7), .en(demultiplexer_1_out7), .Q(out_10), .clk(CLK));  // open: clr
  Register #(.width(32), .trigger("rising"), .Select("low")) register_7 (
    .D(demultiplexer_2_out8), .en(demultiplexer_1_out8), .Q(out_11), .clk(CLK));  // open: clr
  Register #(.width(32), .trigger("rising"), .Select("low")) register_8 (
    .D(demultiplexer_2_out9), .en(demultiplexer_1_out9), .Q(out_12), .clk(CLK));  // open: clr
  Register #(.width(32), .trigger("rising"), .Select("low")) register_9 (
    .D(demultiplexer_2_out10), .en(demultiplexer_1_out10), .Q(out_13), .clk(CLK));  // open: clr
  Register #(.width(32), .trigger("rising"), .Select("low")) register_10 (
    .D(demultiplexer_2_out11), .en(undriven_2), .Q(out_14), .clk(CLK));  // open: clr
  Register #(.width(32), .trigger("rising"), .Select("low")) register_11 (
    .D(demultiplexer_2_out12), .en(undriven), .Q(out_15), .clk(CLK));  // open: clr
endmodule
