// Logisim project music_player.circ as structural Verilog: 27 circuits, main circuit ★Music Player
module Music_Player (
  input  [2:0] in_1,
  output RegWrite,
  output MemWrite,
  output [31:0] PC,
  output [31:0] IR,
  output [31:0] RDin,
  output [31:0] MDin,
  output [31:0] LedData
);

  wire alu_1_equal, alu_1_out_4, AluSrcB, and_1_out, and_3_out, and_4_out, and_5_out, and_7_out, Beq, BGE,
       Bne, CLK, CLK0, clock, clock_1_out, comparator_1_eq, comparator_2_eq, comparator_2_lt, d_ff_1_q,
       d_ff_2_q, d_ff_3_qn, d_ff_4_qn, ecall, f_en, Go, halt, JAL, JALR, JMP, MemToReg, multiplexer_14_out,
       nand_1_out, not_2_out, not_3_out, not_4_out, not_5_out, on_off, or_2_out, or_4_out, play, RST, S_type,
       SB, URET, \开始播放_p1 ;
  wire [0:0] or_1_out;
  wire [3:0] AluOP;
  wire [4:0] multiplexer_2_out, multiplexer_3_out, multiplexer_7_out;
  wire [7:0] adder_5_out, adder_6_out, addr, counter_2_q, counter_3_q, counter_5_q, counter_6_q, freq,
       multiplexer_10_out, num, register_2_q, register_3_q, register_4_q, register_6_q, shifter_3_out,
       sound_emitter_1_p1;
  wire [9:0] bit_extender_8_out, multiplexer_12_out;
  wire [12:0] CNT_num;
  wire [15:0] \总周期数 ;
  wire [31:0] adder_2_out, adder_3_out, adder_4_out, and_6_out, and_8_out, bit_extender_2_out,
       bit_extender_3_out, bit_extender_4_out, bit_extender_5_out, bit_extender_6_out, bit_extender_7_out,
       MemOut, multiplexer_1_out, multiplexer_4_out, multiplexer_5_out, multiplexer_6_out, multiplexer_9_out,
       multiplexer_11_out, multiplexer_13_out, PC_4, R1, R2, Result, Result2, SB_rst, shifter_1_out,
       shifter_2_out, shifter_4_out;

  Button \u_继续运行  (.out(Go));
  Button \u_总复位  (.out(RST));
  // DipSwitch #(.NSwitches(1)) 开始播放: pin names not known; wires that end beside it: \开始播放_p1 
  not not_1 (play, \开始播放_p1 );
  or or_1 (or_1_out[0], or_4_out, JALR);
  Multiplexer #(.select(2), .width(32), .disabled("Z"), .enable("false")) multiplexer_1 (
    .in0(PC_4), .in1(adder_2_out), .in2(adder_3_out), .in3(and_6_out), .out(multiplexer_1_out),
    .sel({JMP, or_1_out[0]}));
  Hex_Digit_Display hex_digit_display_1 (.value(LedData[31:28]));  // open: dp
  not not_2 (not_2_out, halt);
  Counter #(.width(16), .max('hffff), .ongoal("wrap"), .trigger("rising"), .behavior("new")) counter_1 (
    .count(not_2_out), .Q(\总周期数 ), .clk(CLK), .clr(RST));  // open: load, D, carry, preset, down
  not not_3 (not_3_out, halt);
  or or_2 (or_2_out, not_3_out, Go);
  Register #(.width(32), .trigger("rising"), .Select("low")) u_PC (
    .D(multiplexer_1_out), .en(or_2_out), .Q(PC), .clk(CLK), .clr(RST));
  Hex_Digit_Display hex_digit_display_2 (.value(LedData[23:20]));  // open: dp
  Hex_Digit_Display hex_digit_display_3 (.value(LedData[27:24]));  // open: dp
  or or_3 (JMP, JAL, JALR);
  // Probe on PC
  Hex_Digit_Display hex_digit_display_4 (.value(LedData[15:12]));  // open: dp
  Hex_Digit_Display hex_digit_display_5 (.value(LedData[19:16]));  // open: dp
  Comparator #(.width(32), .mode("twosComplement")) comparator_1 (
    .a(R1), .b(32'h22), .eq(comparator_1_eq));  // open: gt, lt
  Hex_Digit_Display hex_digit_display_6 (.value(LedData[7:4]));  // open: dp
  Hex_Digit_Display hex_digit_display_7 (.value(LedData[11:8]));  // open: dp
  // Probe on \总周期数 
  // sound_emitter sound_emitter_1: pin names not known; wires that end beside it: sound_emitter_1_p1
  Bit_Extender #(.in_width(32), .out_width(8), .\type ("zero")) bit_extender_1 (.in(LedData), .out(sound_emitter_1_p1));
  and and_1 (and_1_out, ecall, comparator_1_eq);
  and and_2 (halt, ecall, ~comparator_1_eq);  // AND_Gate
  // RiscV_Probe riscv_probe_1: pin names not known; wires that end beside it: IR
  Adder #(.width(32)) adder_1 (.a(PC), .b(32'h4), .out(PC_4));  // open: cin, cout
  Hex_Digit_Display hex_digit_display_8 (.value(LedData[3:0]));  // open: dp
  Register #(.width(32), .trigger("rising"), .Select("low")) register_1 (
    .D(R2), .en(and_1_out), .Q(LedData), .clk(CLK), .clr(RST));
  ROM #(.addrWidth(10), .dataWidth(32), .Select("high")) Instruction_Memory (.addr(PC[11:2]), .data(IR));
  \单周期硬布线控制器  \u_单周期硬布线控制器_1  (
    .Funct({IR[30], IR[25], IR[14:12]}), .OP(IR[6:2]), .ALU_OP(AluOP), .MemToReg(MemToReg),
    .MemWrite(MemWrite), .ALU_SRC(AluSrcB), .RegWrite(RegWrite), .ecall(ecall), .S_type(S_type), .Jalr(JALR),
    .Beq(Beq), .JAL(JAL), .Bne(Bne), .IR21(IR[21]), .uret(URET), .SB(SB), .BGE(BGE));  // open: r1_used, r2_used, CSRRSI, CSRRCI
  assign bit_extender_2_out = {{20{IR[31]}}, {IR[31], IR[7], IR[30:25], IR[11:8]}};  // Bit_Extender bit_extender_2
  assign bit_extender_3_out = {{12{IR[31]}}, {IR[31], IR[19:12], IR[20], IR[30:21]}};  // Bit_Extender bit_extender_3
  Shifter #(.width(32), .shift("ll")) shifter_1 (.in(bit_extender_2_out), .\dist (5'b00001), .out(shifter_1_out));
  Shifter #(.width(32), .shift("ll")) shifter_2 (.in(bit_extender_3_out), .\dist (5'b00001), .out(shifter_2_out));
  Multiplexer #(.select(1), .width(5), .disabled("Z"), .enable("false")) multiplexer_2 (
    .in0(IR[19:15]), .in1(5'b10001), .out(multiplexer_2_out), .sel(ecall));
  Multiplexer #(.select(1), .width(5), .disabled("Z"), .enable("false")) multiplexer_3 (
    .in0(IR[24:20]), .in1(5'b01010), .out(multiplexer_3_out), .sel(ecall));
  assign bit_extender_4_out = {{20{IR[31]}}, IR[31:20]};  // Bit_Extender bit_extender_4
  assign bit_extender_5_out = {{20{IR[31]}}, {IR[31:25], IR[11:7]}};  // Bit_Extender bit_extender_5
  // Probe on R1
  Multiplexer #(.select(1), .width(32), .disabled("Z"), .enable("false")) multiplexer_4 (
    .in0(bit_extender_4_out), .in1(bit_extender_5_out), .out(multiplexer_4_out), .sel(S_type));
  Adder #(.width(32)) adder_2 (.a(shifter_1_out), .b(PC), .out(adder_2_out));  // open: cin, cout
  Adder #(.width(32)) adder_3 (.a(shifter_2_out), .b(PC), .out(adder_3_out));  // open: cin, cout
  Regifile \u_寄存器堆  (
    .Din(RDin), .Clk(CLK), .R1(R1), .R2(R2), .WE(RegWrite), .W_num(IR[11:7]), .R1_num(multiplexer_2_out),
    .R2_num(multiplexer_3_out));
  or or_4 (or_4_out, and_4_out, and_5_out, and_3_out);
  and and_3 (and_3_out, Bne, ~alu_1_equal);  // AND_Gate
  // Probe on R2
  Multiplexer #(.select(1), .width(32), .disabled("Z"), .enable("false")) multiplexer_5 (
    .in0(R2), .in1(multiplexer_4_out), .out(multiplexer_5_out), .sel(AluSrcB));
  Adder #(.width(32)) adder_4 (.a(multiplexer_4_out), .b(R1), .out(adder_4_out));  // open: cin, cout
  and and_4 (and_4_out, BGE, alu_1_out_4);
  and and_5 (and_5_out, Beq, alu_1_equal);
  ALU alu_1 (
    .X(R1), .Y(multiplexer_5_out), .AluOP(AluOP), .Equal(alu_1_equal), .Result(Result), .Result_2(Result2),
    .out_4(alu_1_out_4));  // open: out_6
  assign and_6_out = adder_4_out & 32'hfffffffe;  // AND_Gate and_6, 32 bits wide
  D_Flip_Flop #(.trigger("rising"), .Pre_Clr_Positions("LEGACY"), .NegatePresetClear("false"), .enable("true"), .NewFFLayout("false")) d_ff_1 (
    .clk(f_en), .D(f_en), .Q(d_ff_1_q));  // open: Qn, preset, en, reset
  not not_4 (not_4_out, f_en);
  and and_7 (and_7_out, not_4_out, clock);
  Counter #(.width(8), .max('hff), .ongoal("stay"), .trigger("rising"), .behavior("new")) counter_2 (
    .D({8{1'b0}}), .count(f_en), .Q(counter_2_q), .clk(clock), .clr(not_5_out));  // open: load, carry, preset, down
  not not_5 (not_5_out, f_en);
  Counter #(.width(8), .max('hff), .ongoal("stay"), .trigger("rising"), .behavior("new")) counter_3 (
    .D({8{1'b0}}), .count(d_ff_1_q), .Q(counter_3_q), .clk(and_7_out), .clr(f_en));  // open: load, carry, preset, down
  D_Flip_Flop #(.trigger("high"), .Pre_Clr_Positions("LEGACY"), .NegatePresetClear("false"), .enable("true"), .NewFFLayout("false")) d_ff_2 (.Q(d_ff_2_q));  // open: clk, D, Qn, preset, en, reset
  // Probe on 13'hf0
  Multiplexer #(.select(2), .width(32), .disabled("Z"), .enable("false")) multiplexer_6 (
    .in0(32'hffffff00), .in1(32'hffff00ff), .in2(32'hff00ffff), .in3(32'hffffff), .out(multiplexer_6_out),
    .sel(Result[1:0]));
  Multiplexer #(.select(2), .width(5), .disabled("Z"), .enable("false")) multiplexer_7 (
    .in0({5{1'b0}}), .in1(5'b01000), .in2(5'b10000), .in3(5'b11000), .out(multiplexer_7_out),
    .sel(Result[1:0]));
  Register #(.width(8), .trigger("rising"), .Select("low")) register_2 (
    .D(counter_2_q), .Q(register_2_q), .clk(clock));  // open: en, clr
  Register #(.width(8), .trigger("rising"), .Select("low")) register_3 (
    .D(counter_3_q), .Q(register_3_q), .clk(clock));  // open: en, clr
  Comparator #(.width(13), .mode("twosComplement")) comparator_2 (
    .a(CNT_num), .b(13'hf0), .eq(comparator_2_eq), .lt(comparator_2_lt));  // open: gt
  Clock #(.highDuration(1), .lowDuration(1)) clock_1 (.out(clock_1_out));
  Multiplexer #(.select(1), .width(32), .disabled("Z"), .enable("false")) multiplexer_8 (
    .in0(R2), .in1(SB_rst), .out(MDin), .sel(SB));
  Counter #(.width(13), .max('h1fff), .ongoal("stay"), .trigger("rising"), .behavior("old")) counter_4 (
    .count(comparator_2_lt), .Q(CNT_num), .clk(clock_1_out));  // open: load, D, carry, clr, preset
  assign and_8_out = multiplexer_6_out & MemOut;  // AND_Gate and_8, 32 bits wide
  assign bit_extender_6_out = {{24{1'b0}}, R2[7:0]};  // Bit_Extender bit_extender_6
  Shifter #(.width(8), .shift("lr")) shifter_3 (.in(register_2_q), .\dist (in_1), .out(shifter_3_out));
  Register #(.width(8), .trigger("rising"), .Select("low")) register_4 (
    .D(freq), .Q(register_4_q), .clk(f_en));  // open: en, clr
  nand nand_1 (nand_1_out, d_ff_2_q, comparator_2_eq);
  Shifter #(.width(32), .shift("ll")) shifter_4 (
    .in(bit_extender_6_out), .\dist (multiplexer_7_out), .out(shifter_4_out));
  D_Flip_Flop #(.trigger("rising"), .Pre_Clr_Positions("LEGACY"), .NegatePresetClear("false"), .enable("true"), .NewFFLayout("false")) d_ff_3 (
    .clk(clock), .D(f_en), .Qn(d_ff_3_qn));  // open: Q, preset, en, reset
  assign CLK0 = nand_1_out ? clock_1_out : 1'bz;  // Controlled_Buffer controlled_buffer_1
  Pull_Resistor #(.pull(1)) pull_resistor_1 (.node(CLK0));
  assign SB_rst = and_8_out | shifter_4_out;  // OR_Gate or_5, 32 bits wide
  Multiplexer #(.select(1), .width(32), .disabled("Z"), .enable("false")) multiplexer_9 (
    .in0({{16{1'b0}}, shifter_3_out, register_4_q}), .in1({16'h100, register_3_q, 8'h80}),
    .out(multiplexer_9_out), .sel(d_ff_3_qn));
  assign bit_extender_7_out = {{24{1'b0}}, num};  // Bit_Extender bit_extender_7
  // Probe on multiplexer_9_out
  Demultiplexer #(.select(1), .width(1), .tristate("false"), .disabled("Z"), .enable("false")) demultiplexer_1 (
    .out0(CLK), .out1(clock), .in(CLK0), .sel(play));
  Multiplexer #(.select(1), .width(8), .disabled("Z"), .enable("false")) multiplexer_10 (
    .in0({8{1'b0}}), .in1(addr), .out(multiplexer_10_out), .sel(on_off));
  Multiplexer #(.select(1), .width(32), .disabled("Z"), .enable("false")) multiplexer_11 (
    .in0(bit_extender_7_out), .in1(multiplexer_9_out), .out(multiplexer_11_out), .sel(on_off));
  assign bit_extender_8_out = {{2{1'b0}}, multiplexer_10_out};  // Bit_Extender bit_extender_8
  D_Flip_Flop #(.trigger("rising"), .Pre_Clr_Positions("LEGACY"), .NegatePresetClear("false"), .enable("true"), .NewFFLayout("false")) d_ff_4 (
    .clk(clock), .D(f_en), .Qn(d_ff_4_qn));  // open: Q, preset, en, reset
  Multiplexer #(.select(1), .width(10), .disabled("Z"), .enable("false")) multiplexer_12 (
    .in0(Result[11:2]), .in1(bit_extender_8_out), .out(multiplexer_12_out), .sel(play));
  Multiplexer #(.select(1), .width(32), .disabled("Z"), .enable("false")) multiplexer_13 (
    .in0(MDin), .in1(multiplexer_11_out), .out(multiplexer_13_out), .sel(play));
  // Probe on freq
  // Probe on freq
  // MCKeyboard mckeyboard_1: pin names not known; wires that end beside it: freq, f_en
  Adder #(.width(8)) adder_5 (.a(8'h1), .b(counter_6_q), .out(adder_5_out));  // open: cin, cout
  Adder #(.width(8)) adder_6 (.a(counter_5_q), .b(8'h1), .out(adder_6_out));  // open: cin, cout
  Multiplexer #(.select(1), .width(1), .disabled("Z"), .enable("false")) multiplexer_14 (
    .in0(MemWrite), .in1(1'b1), .out(multiplexer_14_out), .sel(play));
  // sound_emitter sound_emitter_2: pin names not known; wires that end beside it: freq
  Counter #(.width(8), .max('hff), .ongoal("wrap"), .trigger("rising"), .behavior("new")) counter_5 (
    .load(d_ff_4_qn), .D(adder_5_out), .count(on_off), .Q(counter_5_q), .clk(f_en));  // open: carry, clr, preset, down
  Counter #(.width(8), .max('hff), .ongoal("wrap"), .trigger("falling"), .behavior("new")) counter_6 (
    .load(1'b1), .D(adder_6_out), .count(on_off), .Q(counter_6_q), .clk(f_en));  // open: carry, clr, preset, down
  RAM #(.addrWidth(10), .dataWidth(32), .bus("separate"), .Select("high")) ram_1 (
    .addr(multiplexer_12_out), .din(multiplexer_13_out), .data(MemOut), .str(multiplexer_14_out), .clk(CLK0));  // open: sel, ld, clr
  // DipSwitch #(.NSwitches(1)) dipswitch_1: pin names not known; wires that end beside it: RST, on_off
  Register #(.width(8), .trigger("rising"), .Select("low")) register_5 (
    .D(counter_5_q), .Q(num), .clk(clock));  // open: en, clr
  Register #(.width(8), .trigger("rising"), .Select("low")) register_6 (
    .D(counter_6_q), .Q(register_6_q), .clk(clock));  // open: en, clr
  // Probe on addr
  Multiplexer #(.select(1), .width(8), .disabled("Z"), .enable("false")) multiplexer_15 (
    .in0(num), .in1(register_6_q), .out(addr), .sel(d_ff_4_qn));
  Multiplexer #(.select(2), .width(32), .disabled("Z"), .enable("false")) multiplexer_16 (
    .in0(Result), .in1(MemOut), .in2(PC_4), .out(RDin), .sel({JMP, MemToReg}));  // open: in3

  // Other names for the same wires on the sheet: Result_0_1[1:0] = Result[1:0]

  // Notes on the sheet:
  //   数码管输出应该用寄存器锁存，否则显示数据只能一闪而过
  //   数码管输出
  //   位宽不匹配，取字地址
  //   指令存储器
  //   指令字
  //   contents of Instruction_Memory (hex, n*v repeats v):
  //   513 e13 2703 271713 2200893 4e2503 a55e93 ffefe93 73 e8663 fffe8e93 ff9ff06f 513 4e0e13 fcee1ee3
  //   a00893 73 fbdff06f
  //   JAL
  //   JALR
  //   URET
  //   Beq
  //   Bne
  //   MemToReg
  //   MemWrite
  //   AluOP
  //   AluSrcB
  //   RegWrite
  //   S_type
  //   beq\bne指令目的地址
  //   jal指令目的地址
  //   为方便自动评测，需要输出PC，IR，寄存器堆写如数据RDin
  //   计算出地址的最低有效位设为0
  //   jalr指令目的地址
  //   RAM写使能MemWrite、RAM写入数据MDin等信号
  //   正常音符音长计数器
  //   两音符间隔计数器
  //   控制位
  //   暂停节拍，不能为0
  //   戳工具置1进入计数暂停模式，ctrl+k时钟自动运行到对应节拍暂停
  //   ctrl+k关闭时钟连续运行，将控制位置零，进入单步调试模式调试
  //   用这个时钟源需要去掉电路中的其他时钟源
  //   SB指令支持电路
  //   第24位用于区分音符还是间隔，0：音符，1：间隔
  //   可计数暂停的时钟源
  //   数据存储器
  //   结束采样
  //   开始采样
  //   先开启时钟，再点开始采样开关，然后按钢琴键，录入完后关闭开关，总音符数存在0地址，音符和间隔交替存储
endmodule

module \键盘采样  (
);

  wire and_1_out, and_2_out, clock, d_ff_1_q, d_ff_2_qn, d_ff_3_qn, f_en, not_1_out, not_2_out, on_off;
  wire [7:0] adder_1_out, adder_2_out, addr, counter_1_q, counter_2_q, counter_3_q, counter_4_q, freq,
       multiplexer_3_out, num, register_1_q, register_2_q, register_3_q, register_5_q, shifter_1_out;
  wire [31:0] bit_extender_1_out, multiplexer_2_out, multiplexer_4_out;

  Clock #(.highDuration(1), .lowDuration(1)) clock_1 (.out(clock));
  D_Flip_Flop #(.trigger("rising"), .Pre_Clr_Positions("ABOVE_BELOW"), .NegatePresetClear("false"), .enable("false"), .NewFFLayout("true")) d_ff_1 (
    .clk(f_en), .D(f_en), .Q(d_ff_1_q));  // open: Qn, preset, reset
  Counter #(.width(8), .max('hff), .ongoal("wrap"), .trigger("rising"), .behavior("new")) counter_1 (
    .D({8{1'b0}}), .Q(counter_1_q), .clk(and_1_out), .clr(not_2_out));  // open: load, count, carry, preset, down
  and and_1 (and_1_out, f_en, clock);
  Counter #(.width(8), .max('hff), .ongoal("wrap"), .trigger("rising"), .behavior("new")) counter_2 (
    .D({8{1'b0}}), .count(d_ff_1_q), .Q(counter_2_q), .clk(and_2_out), .clr(f_en));  // open: load, carry, preset, down
  and and_2 (and_2_out, not_1_out, clock);
  not not_1 (not_1_out, f_en);
  D_Flip_Flop #(.trigger("rising"), .Pre_Clr_Positions("ABOVE_BELOW"), .NegatePresetClear("false"), .enable("false"), .NewFFLayout("true")) d_ff_2 (
    .clk(clock), .D(f_en), .Qn(d_ff_2_qn));  // open: Q, preset, reset
  Register #(.width(8), .trigger("rising"), .Select("low")) register_1 (
    .D(counter_1_q), .Q(register_1_q), .clk(clock));  // open: en, clr
  not not_2 (not_2_out, f_en);
  Register #(.width(8), .trigger("rising"), .Select("low")) register_2 (
    .D(counter_2_q), .Q(register_2_q), .clk(clock));  // open: en, clr
  Adder #(.width(8)) adder_1 (.a(8'h1), .b(counter_4_q), .out(adder_1_out));  // open: cin, cout
  Adder #(.width(8)) adder_2 (.a(counter_3_q), .b(8'h1), .out(adder_2_out));  // open: cin, cout
  Register #(.width(8), .trigger("rising"), .Select("low")) register_3 (
    .D(freq), .Q(register_3_q), .clk(f_en));  // open: en, clr
  Shifter #(.width(8), .shift("lr")) shifter_1 (.in(register_1_q), .\dist (3'b001), .out(shifter_1_out));
  Counter #(.width(8), .max('hff), .ongoal("wrap"), .trigger("rising"), .behavior("new")) counter_3 (
    .load(d_ff_2_qn), .D(adder_1_out), .count(on_off), .Q(counter_3_q), .clk(f_en));  // open: carry, clr, preset, down
  Counter #(.width(8), .max('hff), .ongoal("wrap"), .trigger("falling"), .behavior("new")) counter_4 (
    .load(1'b1), .D(adder_2_out), .count(on_off), .Q(counter_4_q), .clk(f_en));  // open: carry, clr, preset, down
  Register #(.width(8), .trigger("rising"), .Select("low")) register_4 (
    .D(counter_3_q), .Q(num), .clk(clock));  // open: en, clr
  Register #(.width(8), .trigger("rising"), .Select("low")) register_5 (
    .D(counter_4_q), .Q(register_5_q), .clk(clock));  // open: en, clr
  Multiplexer #(.select(1), .width(8), .disabled("Z"), .enable("false")) multiplexer_1 (
    .in0(num), .in1(register_5_q), .out(addr), .sel(d_ff_2_qn));
  D_Flip_Flop #(.trigger("rising"), .Pre_Clr_Positions("ABOVE_BELOW"), .NegatePresetClear("false"), .enable("false"), .NewFFLayout("true")) d_ff_3 (
    .clk(clock), .D(f_en), .Qn(d_ff_3_qn));  // open: Q, preset, reset
  // Probe on addr
  // Probe on multiplexer_2_out
  Multiplexer #(.select(1), .width(32), .disabled("Z"), .enable("false")) multiplexer_2 (
    .in0({{16{1'b0}}, register_1_q, register_3_q}), .in1({16'h100, register_2_q, {8{1'b0}}}),
    .out(multiplexer_2_out), .sel(d_ff_3_qn));
  assign bit_extender_1_out = {{24{1'b0}}, num};  // Bit_Extender bit_extender_1
  Multiplexer #(.select(1), .width(8), .disabled("Z"), .enable("false")) multiplexer_3 (
    .in0({8{1'b0}}), .in1(addr), .out(multiplexer_3_out), .sel(on_off));
  Multiplexer #(.select(1), .width(32), .disabled("Z"), .enable("false")) multiplexer_4 (
    .in0(bit_extender_1_out), .in1(multiplexer_2_out), .out(multiplexer_4_out), .sel(on_off));
  RAM #(.addrWidth(8), .dataWidth(32), .bus("separate"), .Select("low")) ram_1 (
    .addr(multiplexer_3_out), .din(multiplexer_4_out), .clk(clock));  // open: data, str, sel, ld, clr
  // Probe on freq
  // Probe on freq
  // MCKeyboard mckeyboard_1: pin names not known; wires that end beside it: freq, f_en
  // sound_emitter sound_emitter_1: pin names not known; wires that end beside it: freq
  // DipSwitch #(.NSwitches(1)) dipswitch_1: pin names not known; wires that end beside it: on_off

  // Notes on the sheet:
  //   正常音符音长计数器
  //   两音符间隔计数器
  //   第24位用于区分音符还是间隔，0：音符，1：间隔
  //   结束采样
  //   开始采样
  //   先开启时钟，再点开始采样开关，然后按钢琴键，录入完后关闭开关，总音符数存在0地址，音符和间隔交替存储
endmodule

module \单周期RISC_V  (
  output RegWrite,
  output MemWrite,
  output [31:0] PC,
  output [31:0] IR,
  output [31:0] RDin,
  output [31:0] MDin,
  output [31:0] LedData
);

  wire alu_1_equal, alu_1_out_4, AluSrcB, and_1_out, and_2_out, and_3_out, and_5_out, Beq, BGE, Bne, CLK,
       clock_1_out, comparator_1_eq, comparator_2_eq, comparator_2_lt, d_ff_1_q, ecall, Go, halt, JAL, JALR,
       JMP, MemToReg, nand_1_out, not_1_out, not_2_out, or_2_out, or_3_out, RST, S_type, SB, URET;
  wire [0:0] or_1_out;
  wire [3:0] AluOP;
  wire [4:0] multiplexer_2_out, multiplexer_3_out, multiplexer_7_out;
  wire [12:0] CNT_num;
  wire [15:0] \总周期数 ;
  wire [31:0] adder_2_out, adder_3_out, adder_4_out, and_4_out, and_7_out, bit_extender_1_out,
       bit_extender_2_out, bit_extender_3_out, bit_extender_4_out, bit_extender_5_out, MemOut,
       multiplexer_1_out, multiplexer_4_out, multiplexer_5_out, multiplexer_6_out, PC_4, R1, R2, Result,
       Result2, SB_rst, shifter_1_out, shifter_2_out, shifter_3_out;

  Button \u_继续运行  (.out(Go));
  Button \u_总复位  (.out(RST));
  or or_1 (or_1_out[0], or_3_out, JALR);
  Multiplexer #(.select(2), .width(32), .disabled("Z"), .enable("false")) multiplexer_1 (
    .in0(PC_4), .in1(adder_2_out), .in2(adder_3_out), .in3(and_4_out), .out(multiplexer_1_out),
    .sel({JMP, or_1_out[0]}));
  Hex_Digit_Display hex_digit_display_1 (.value(LedData[31:28]));  // open: dp
  // Probe on PC_4
  not not_1 (not_1_out, halt);
  or or_2 (or_2_out, not_1_out, Go);
  Register #(.width(32), .trigger("rising"), .Select("low")) u_PC (
    .D(multiplexer_1_out), .en(or_2_out), .Q(PC), .clk(CLK), .clr(RST));
  Hex_Digit_Display hex_digit_display_2 (.value(LedData[23:20]));  // open: dp
  Hex_Digit_Display hex_digit_display_3 (.value(LedData[27:24]));  // open: dp
  // Probe on adder_2_out
  // Probe on PC
  Hex_Digit_Display hex_digit_display_4 (.value(LedData[15:12]));  // open: dp
  Hex_Digit_Display hex_digit_display_5 (.value(LedData[19:16]));  // open: dp
  // Probe on adder_3_out
  Hex_Digit_Display hex_digit_display_6 (.value(LedData[7:4]));  // open: dp
  Hex_Digit_Display hex_digit_display_7 (.value(LedData[11:8]));  // open: dp
  // Probe on \总周期数 
  // Probe on and_4_out
  // RiscV_Probe riscv_probe_1: pin names not known; wires that end beside it: IR
  Adder #(.width(32)) adder_1 (.a(PC), .b(32'h4), .out(PC_4));  // open: cin, cout
  Hex_Digit_Display hex_digit_display_8 (.value(LedData[3:0]));  // open: dp
  ROM #(.addrWidth(10), .dataWidth(32), .Select("high")) Instruction_Memory (.addr(PC[11:2]), .data(IR));
  \单周期硬布线控制器  \u_单周期硬布线控制器_1  (
    .Funct({IR[30], IR[25], IR[14:12]}), .OP(IR[6:2]), .ALU_OP(AluOP), .MemToReg(MemToReg),
    .MemWrite(MemWrite), .ALU_SRC(AluSrcB), .RegWrite(RegWrite), .ecall(ecall), .S_type(S_type), .Jalr(JALR),
    .Beq(Beq), .JAL(JAL), .Bne(Bne), .IR21(IR[21]), .uret(URET), .SB(SB), .BGE(BGE));  // open: r1_used, r2_used, CSRRSI, CSRRCI
  assign bit_extender_1_out = {{20{IR[31]}}, {IR[31], IR[7], IR[30:25], IR[11:8]}};  // Bit_Extender bit_extender_1
  assign bit_extender_2_out = {{12{IR[31]}}, {IR[31], IR[19:12], IR[20], IR[30:21]}};  // Bit_Extender bit_extender_2
  Shifter #(.width(32), .shift("ll")) shifter_1 (.in(bit_extender_1_out), .\dist (5'b00001), .out(shifter_1_out));
  Shifter #(.width(32), .shift("ll")) shifter_2 (.in(bit_extender_2_out), .\dist (5'b00001), .out(shifter_2_out));
  Multiplexer #(.select(1), .width(5), .disabled("Z"), .enable("false")) multiplexer_2 (
    .in0(IR[19:15]), .in1(5'b10001), .out(multiplexer_2_out), .sel(ecall));
  Multiplexer #(.select(1), .width(5), .disabled("Z"), .enable("false")) multiplexer_3 (
    .in0(IR[24:20]), .in1(5'b01010), .out(multiplexer_3_out), .sel(ecall));
  assign bit_extender_3_out = {{20{IR[31]}}, IR[31:20]};  // Bit_Extender bit_extender_3
  assign bit_extender_4_out = {{20{IR[31]}}, {IR[31:25], IR[11:7]}};  // Bit_Extender bit_extender_4
  // Probe on R1
  Multiplexer #(.select(1), .width(32), .disabled("Z"), .enable("false")) multiplexer_4 (
    .in0(bit_extender_3_out), .in1(bit_extender_4_out), .out(multiplexer_4_out), .sel(S_type));
  Adder #(.width(32)) adder_2 (.a(shifter_1_out), .b(PC), .out(adder_2_out));  // open: cin, cout
  Adder #(.width(32)) adder_3 (.a(shifter_2_out), .b(PC), .out(adder_3_out));  // open: cin, cout
  Regifile \u_寄存器堆  (
    .Din(RDin), .Clk(CLK), .R1(R1), .R2(R2), .WE(RegWrite), .W_num(IR[11:7]), .R1_num(multiplexer_2_out),
    .R2_num(multiplexer_3_out));
  or or_3 (or_3_out, and_3_out, and_2_out, and_1_out);
  and and_1 (and_1_out, Bne, ~alu_1_equal);  // AND_Gate
  // Probe on R2
  Multiplexer #(.select(1), .width(32), .disabled("Z"), .enable("false")) multiplexer_5 (
    .in0(R2), .in1(multiplexer_4_out), .out(multiplexer_5_out), .sel(AluSrcB));
  Adder #(.width(32)) adder_4 (.a(multiplexer_4_out), .b(R1), .out(adder_4_out));  // open: cin, cout
  and and_2 (and_2_out, Beq, alu_1_equal);
  and and_3 (and_3_out, BGE, alu_1_out_4);
  ALU alu_1 (
    .X(R1), .Y(multiplexer_5_out), .AluOP(AluOP), .Equal(alu_1_equal), .Result(Result), .Result_2(Result2),
    .out_4(alu_1_out_4));  // open: out_6
  assign and_4_out = adder_4_out & 32'hfffffffe;  // AND_Gate and_4, 32 bits wide
  or or_4 (JMP, JAL, JALR);
  Multiplexer #(.select(2), .width(32), .disabled("Z"), .enable("false")) multiplexer_6 (
    .in0(32'hffffff00), .in1(32'hffff00ff), .in2(32'hff00ffff), .in3(32'hffffff), .out(multiplexer_6_out),
    .sel(Result[1:0]));
  Multiplexer #(.select(2), .width(5), .disabled("Z"), .enable("false")) multiplexer_7 (
    .in0({5{1'b0}}), .in1(5'b01000), .in2(5'b10000), .in3(5'b11000), .out(multiplexer_7_out),
    .sel(Result[1:0]));
  D_Flip_Flop #(.trigger("high"), .Pre_Clr_Positions("LEGACY"), .NegatePresetClear("false"), .enable("true"), .NewFFLayout("false")) d_ff_1 (.Q(d_ff_1_q));  // open: clk, D, Qn, preset, en, reset
  // Probe on 13'hf0
  Comparator #(.width(32), .mode("twosComplement")) comparator_1 (
    .a(R1), .b(32'h22), .eq(comparator_1_eq));  // open: gt, lt
  Comparator #(.width(13), .mode("twosComplement")) comparator_2 (
    .a(CNT_num), .b(13'hf0), .eq(comparator_2_eq), .lt(comparator_2_lt));  // open: gt
  Clock #(.highDuration(1), .lowDuration(1)) clock_1 (.out(clock_1_out));
  and and_5 (and_5_out, ecall, comparator_1_eq);
  and and_6 (halt, ecall, ~comparator_1_eq);  // AND_Gate
  Multiplexer #(.select(1), .width(32), .disabled("Z"), .enable("false")) multiplexer_8 (
    .in0(R2), .in1(SB_rst), .out(MDin), .sel(SB));
  assign and_7_out = multiplexer_6_out & MemOut;  // AND_Gate and_7, 32 bits wide
  assign bit_extender_5_out = {{24{1'b0}}, R2[7:0]};  // Bit_Extender bit_extender_5
  Counter #(.width(13), .max('h1fff), .ongoal("stay"), .trigger("rising"), .behavior("old")) counter_1 (
    .count(comparator_2_lt), .Q(CNT_num), .clk(clock_1_out));  // open: load, D, carry, clr, preset
  Shifter #(.width(32), .shift("ll")) shifter_3 (
    .in(bit_extender_5_out), .\dist (multiplexer_7_out), .out(shifter_3_out));
  nand nand_1 (nand_1_out, d_ff_1_q, comparator_2_eq);
  Register #(.width(32), .trigger("rising"), .Select("low")) register_1 (
    .D(R2), .en(and_5_out), .Q(LedData), .clk(CLK), .clr(RST));
  RAM #(.addrWidth(10), .dataWidth(32), .bus("separate"), .Select("high")) ram_1 (
    .addr(Result[11:2]), .din(MDin), .data(MemOut), .str(MemWrite), .clk(CLK), .clr(RST));  // open: sel, ld
  assign SB_rst = and_7_out | shifter_3_out;  // OR_Gate or_5, 32 bits wide
  assign CLK = nand_1_out ? clock_1_out : 1'bz;  // Controlled_Buffer controlled_buffer_1
  Pull_Resistor #(.pull(1)) pull_resistor_1 (.node(CLK));
  not not_2 (not_2_out, halt);
  Counter #(.width(16), .max('hffff), .ongoal("wrap"), .trigger("rising"), .behavior("new")) counter_2 (
    .count(not_2_out), .Q(\总周期数 ), .clk(CLK), .clr(RST));  // open: load, D, carry, preset, down
  Multiplexer #(.select(2), .width(32), .disabled("Z"), .enable("false")) multiplexer_9 (
    .in0(Result), .in1(MemOut), .in2(PC_4), .out(RDin), .sel({JMP, MemToReg}));  // open: in3

  // Notes on the sheet:
  //   数码管输出应该用寄存器锁存，否则显示数据只能一闪而过
  //   数码管输出
  //   位宽不匹配，取字地址
  //   指令探针
  //   指令存储器
  //   指令字
  //   contents of Instruction_Memory (hex, n*v repeats v):
  //   100493 100006f 100493 200913 300993 100006f 100493 200913 300993 100006f 100493 200913 300993
  //   100006f 100493 200913 300993 3a8000ef 100413 100493 1f49493 900533 2200893 73 24d493 48463 fedff06f
  //   900533 2200893 73 100493 249493 900533 2200893 73 48463 fedff06f 100493 1f49493 900533 2200893 73
  //   4034d493 900533 2200893 73 4044d493 900533 2200893 73 4044d493 900533 2200893 73 4044d493 900533
  //   2200893 73 4044d493 900533 2200893 73 4044d493 900533 2200893 73 4044d493 900533 2200893 73 4044d493
  //   900533 2200893 73 100413 1f41993 41f9d993 433 c00913 300b13 140413 f47413 800293 100313 499993
  //   89e9b3 1300533 2200893 73 406282b3 fe0294e3 140413 f00f93 1f47433 1c41413 800293 100313 49d993
  //   89e9b3 1300533 2200893 73 406282b3 fe0294e3 1c45413 406b0b33 b0463 f95ff06f 2b3 fff2c293 829293
  //   ff2e293 500533 2200893 73 fff00413 493 84a023 140413 448493 84a023 140413 448493 84a023 140413
  //   448493 84a023 140413 448493 84a023 140413 448493 84a023 140413 448493 84a023 140413 448493 84a023
  //   140413 448493 84a023 140413 448493 84a023 140413 448493 84a023 140413 448493 84a023 140413 448493
  //   84a023 140413 448493 84a023 140413 448493 84a023 140413 448493 84a023 140413 448493 140413 433
  //   3c00493 42983 4aa03 149a2b3 28663 134a023 1442023 ffc48493 fe9412e3 800533 2200893 73 440413 3c00493
  //   fc9416e3 3200893 73 100293 300313 800493 849493 7648493 900533 2200893 73 800e13 5494b3 6494b3
  //   900533 2200893 73 fffe0e13 fe0e14e3 a00893 73 fff00293 7700493 849493 7748493 900533 2200893 73
  //   1000e13 54c4b3 900533 2200893 73 fffe0e13 fe0e16e3 a00893 73 313 2000e13 493 100913 930023 900533
  //   2200893 73 12484b3 130313 fffe0e13 fe0e12e3 800e13 313 32483 900533 2200893 73 430313 fffe0e13
  //   fe0e14e3 a00893 73 f00493 900533 2200893 73 fff48493 fe04d8e3 a00893 73 a00893 73 413 140413 800533
  //   2200893 73 240413 800533 2200893 73 340413 800533 2200893 73 440413 800533 2200893 73 540413 800533
  //   2200893 73 640413 800533 2200893 73 740413 800533 2200893 73 840413 800533 2200893 2200893 73 8067
  //   JAL
  //   JALR
  //   URET
  //   Beq
  //   Bne
  //   MemToReg
  //   MemWrite
  //   AluOP
  //   AluSrcB
  //   RegWrite
  //   S_type
  //   beq\bne指令目的地址
  //   jal指令目的地址
  //   为方便自动评测，需要输出PC，IR，寄存器堆写如数据RDin
  //   计算出地址的最低有效位设为0
  //   jalr指令目的地址
  //   RAM写使能MemWrite、RAM写入数据MDin等信号
  //   控制位
  //   暂停节拍，不能为0
  //   戳工具置1进入计数暂停模式，ctrl+k时钟自动运行到对应节拍暂停
  //   ctrl+k关闭时钟连续运行，将控制位置零，进入单步调试模式调试
  //   用这个时钟源需要去掉电路中的其他时钟源
  //   数据存储器
  //   可计数暂停的时钟源
endmodule

// 单周期硬布线控制器
module \单周期硬布线控制器  (
  input  [4:0] OP,
  input  [4:0] Funct,
  input  IR21,
  output [3:0] ALU_OP,
  output uret,
  output MemToReg,
  output ecall,
  output MemWrite,
  output ALU_SRC,
  output RegWrite,
  output S_type,
  output Beq,
  output Bne,
  output Jalr,
  output JAL,
  output CSRRSI,
  output SB,
  output BGE,
  output CSRRCI,
  output r1_used,
  output r2_used
);

  wire \控制信号自动生成_1_ecall ;

  \运算控制器自动生成  \u_运算控制器自动生成_1  (
    .OP2(OP[0]), .OP3(OP[1]), .OP4(OP[2]), .OP5(OP[3]), .OP6(OP[4]), .F12(Funct[0]), .F13(Funct[1]),
    .F14(Funct[2]), .F25(Funct[3]), .F30(Funct[4]), .S0(ALU_OP[0]), .S1(ALU_OP[1]), .S2(ALU_OP[2]),
    .S3(ALU_OP[3]));
  \控制信号自动生成  \u_控制信号自动生成_1  (
    .OP2(OP[0]), .OP3(OP[1]), .MemToReg(MemToReg), .OP4(OP[2]), .OP5(OP[3]), .OP6(OP[4]), .F12(Funct[0]),
    .MemWrite(MemWrite), .F13(Funct[1]), .F14(Funct[2]), .F25(Funct[3]), .F30(Funct[4]), .ALU_SRC(ALU_SRC),
    .RegWrite(RegWrite), .ecall(\控制信号自动生成_1_ecall ), .S_Type(S_type), .BEQ(Beq), .BNE(Bne), .JALR(Jalr),
    .JAL(JAL), .SB(SB), .BGE(BGE), .r1_used(r1_used), .r2_used(r2_used), .CSRRSI(CSRRSI), .CSRRCI(CSRRCI));
  and and_1 (uret, IR21, \控制信号自动生成_1_ecall );
  and and_2 (ecall, ~IR21, \控制信号自动生成_1_ecall );  // AND_Gate

  // Other names for the same wires on the sheet: OP_CODE[4:0] = OP

  // Notes on the sheet:
  //   控制信号生成，产生数据通路需要的其他控制信号
  //   运算器控制器，根据指令生成运算器功能选择信号
endmodule

// 运算器控制器
module \运算控制器自动生成  (
  input  OP2,
  input  OP3,
  input  OP4,
  input  OP5,
  input  OP6,
  input  F12,
  input  F13,
  input  F14,
  input  F25,
  input  F30,
  output S0,
  output S1,
  output S2,
  output S3
);

  wire and_1_out, and_2_out, and_3_out, and_4_out, and_5_out, and_6_out, and_7_out, and_8_out, and_9_out,
       and_10_out, and_11_out, and_12_out, and_13_out, and_14_out, and_15_out, and_16_out, and_17_out,
       and_18_out, and_19_out, and_20_out, and_21_out, and_22_out, and_23_out, and_24_out, and_25_out,
       and_26_out, and_27_out, and_28_out, and_29_out, and_30_out, and_31_out, and_32_out, and_33_out,
       not_1_out, not_2_out, not_3_out, not_4_out, not_5_out, not_6_out, not_7_out, not_8_out, not_9_out,
       not_10_out, not_11_out, not_12_out, not_13_out, not_14_out, not_15_out, not_16_out, not_17_out,
       not_18_out, not_19_out, not_20_out, not_21_out, not_22_out, not_23_out, not_24_out, not_25_out,
       not_26_out, not_27_out, not_28_out, not_29_out, not_30_out, not_31_out, not_32_out, not_33_out,
       not_34_out, not_35_out, not_36_out, not_37_out, not_38_out, not_39_out, not_40_out, not_41_out,
       not_42_out, not_43_out, not_44_out, not_45_out, not_46_out, not_47_out, not_48_out, not_49_out,
       not_50_out, not_51_out, not_52_out, not_53_out, not_54_out, not_55_out, not_56_out, not_57_out,
       not_58_out, not_59_out, not_60_out, not_61_out, not_62_out, not_63_out, not_64_out, not_65_out,
       not_66_out, not_67_out, not_68_out, not_69_out, not_70_out, not_71_out, not_72_out, not_73_out,
       not_74_out, not_75_out, not_76_out, not_77_out, not_78_out, not_79_out, not_80_out, not_81_out,
       not_82_out, not_83_out, not_84_out, not_85_out, not_86_out, not_87_out, not_88_out, not_89_out,
       not_90_out, not_91_out, not_92_out, not_93_out, not_94_out, not_95_out, not_96_out, not_97_out,
       not_98_out, not_99_out, not_100_out, not_101_out, not_102_out, not_103_out, not_104_out, not_105_out,
       not_106_out, not_107_out, not_108_out, not_109_out, not_110_out, not_111_out, not_112_out,
       not_113_out, not_114_out, not_115_out, not_116_out, not_117_out, not_118_out, not_119_out,
       not_120_out, not_121_out, not_122_out, not_123_out, not_124_out, not_125_out, not_126_out,
       not_127_out, not_128_out, not_129_out, not_130_out, not_131_out, not_132_out, not_133_out,
       not_134_out, not_135_out, not_136_out, not_137_out, not_138_out, not_139_out, not_140_out,
       not_141_out, not_142_out, not_143_out, not_144_out, not_145_out, not_146_out, not_147_out,
       not_148_out, not_149_out, not_150_out, not_151_out, not_152_out, not_153_out, not_154_out,
       not_155_out, not_156_out, not_157_out, not_158_out, not_159_out, not_160_out, not_161_out,
       not_162_out, not_163_out, not_164_out, not_165_out, not_166_out, not_167_out, not_168_out,
       not_169_out, not_170_out, not_171_out, not_172_out, not_173_out, not_174_out, not_175_out,
       not_176_out, not_177_out, not_178_out, not_179_out, not_180_out, not_181_out, not_182_out,
       not_183_out, not_184_out, not_185_out, not_186_out, not_187_out, not_188_out, not_189_out,
       not_190_out, not_191_out, not_192_out, not_193_out, not_194_out, not_195_out, not_196_out,
       not_197_out, not_198_out;

  not not_1 (not_1_out, F30);
  not not_2 (not_2_out, F25);
  not not_3 (not_3_out, F14);
  not not_4 (not_4_out, F13);
  not not_5 (not_5_out, F12);
  not not_6 (not_6_out, OP6);
  not not_7 (not_7_out, OP3);
  not not_8 (not_8_out, OP2);
  not not_9 (not_9_out, F30);
  not not_10 (not_10_out, F25);
  not not_11 (not_11_out, OP6);
  not not_12 (not_12_out, OP3);
  not not_13 (not_13_out, OP2);
  not not_14 (not_14_out, F30);
  not not_15 (not_15_out, F25);
  not not_16 (not_16_out, F14);
  not not_17 (not_17_out, F12);
  not not_18 (not_18_out, OP6);
  not not_19 (not_19_out, OP3);
  not not_20 (not_20_out, OP2);
  not not_21 (not_21_out, F14);
  not not_22 (not_22_out, F13);
  not not_23 (not_23_out, F12);
  not not_24 (not_24_out, OP6);
  not not_25 (not_25_out, OP5);
  not not_26 (not_26_out, OP3);
  not not_27 (not_27_out, OP2);
  not not_28 (not_28_out, OP6);
  not not_29 (not_29_out, OP5);
  not not_30 (not_30_out, OP3);
  not not_31 (not_31_out, OP2);
  not not_32 (not_32_out, F13);
  not not_33 (not_33_out, F12);
  not not_34 (not_34_out, OP6);
  not not_35 (not_35_out, OP5);
  not not_36 (not_36_out, OP3);
  not not_37 (not_37_out, OP2);
  not not_38 (not_38_out, F14);
  not not_39 (not_39_out, F12);
  not not_40 (not_40_out, OP6);
  not not_41 (not_41_out, OP5);
  not not_42 (not_42_out, OP3);
  not not_43 (not_43_out, OP2);
  not not_44 (not_44_out, F25);
  not not_45 (not_45_out, F13);
  not not_46 (not_46_out, OP6);
  not not_47 (not_47_out, OP5);
  not not_48 (not_48_out, OP3);
  not not_49 (not_49_out, OP2);
  not not_50 (not_50_out, F14);
  not not_51 (not_51_out, F12);
  not not_52 (not_52_out, OP6);
  not not_53 (not_53_out, OP5);
  not not_54 (not_54_out, OP4);
  not not_55 (not_55_out, OP3);
  not not_56 (not_56_out, OP2);
  not not_57 (not_57_out, F30);
  not not_58 (not_58_out, F25);
  not not_59 (not_59_out, F13);
  not not_60 (not_60_out, F12);
  not not_61 (not_61_out, OP6);
  not not_62 (not_62_out, OP3);
  not not_63 (not_63_out, OP2);
  not not_64 (not_64_out, F13);
  not not_65 (not_65_out, OP4);
  not not_66 (not_66_out, OP3);
  not not_67 (not_67_out, OP2);
  not not_68 (not_68_out, F25);
  not not_69 (not_69_out, F14);
  not not_70 (not_70_out, F13);
  not not_71 (not_71_out, F12);
  not not_72 (not_72_out, OP6);
  not not_73 (not_73_out, OP3);
  not not_74 (not_74_out, OP2);
  not not_75 (not_75_out, F30);
  not not_76 (not_76_out, F25);
  not not_77 (not_77_out, OP6);
  not not_78 (not_78_out, OP3);
  not not_79 (not_79_out, OP2);
  not not_80 (not_80_out, F30);
  not not_81 (not_81_out, F25);
  not not_82 (not_82_out, F14);
  not not_83 (not_83_out, F12);
  not not_84 (not_84_out, OP6);
  not not_85 (not_85_out, OP3);
  not not_86 (not_86_out, OP2);
  not not_87 (not_87_out, OP6);
  not not_88 (not_88_out, OP5);
  not not_89 (not_89_out, OP3);
  not not_90 (not_90_out, OP2);
  not not_91 (not_91_out, F14);
  not not_92 (not_92_out, F12);
  not not_93 (not_93_out, OP6);
  not not_94 (not_94_out, OP5);
  not not_95 (not_95_out, OP3);
  not not_96 (not_96_out, OP2);
  not not_97 (not_97_out, F30);
  not not_98 (not_98_out, F25);
  not not_99 (not_99_out, F13);
  not not_100 (not_100_out, OP6);
  not not_101 (not_101_out, OP5);
  not not_102 (not_102_out, OP3);
  not not_103 (not_103_out, OP2);
  not not_104 (not_104_out, F13);
  not not_105 (not_105_out, OP4);
  not not_106 (not_106_out, OP3);
  not not_107 (not_107_out, OP2);
  not not_108 (not_108_out, F30);
  not not_109 (not_109_out, F25);
  not not_110 (not_110_out, F14);
  not not_111 (not_111_out, F13);
  not not_112 (not_112_out, F12);
  not not_113 (not_113_out, OP6);
  not not_114 (not_114_out, OP3);
  not not_115 (not_115_out, OP2);
  not not_116 (not_116_out, F25);
  not not_117 (not_117_out, F14);
  not not_118 (not_118_out, F13);
  not not_119 (not_119_out, F12);
  not not_120 (not_120_out, OP6);
  not not_121 (not_121_out, OP3);
  not not_122 (not_122_out, OP2);
  not not_123 (not_123_out, F30);
  not not_124 (not_124_out, F25);
  not not_125 (not_125_out, OP6);
  not not_126 (not_126_out, OP3);
  not not_127 (not_127_out, OP2);
  not not_128 (not_128_out, F30);
  not not_129 (not_129_out, F25);
  not not_130 (not_130_out, F14);
  not not_131 (not_131_out, OP6);
  not not_132 (not_132_out, OP3);
  not not_133 (not_133_out, OP2);
  not not_134 (not_134_out, F14);
  not not_135 (not_135_out, F13);
  not not_136 (not_136_out, F12);
  not not_137 (not_137_out, OP6);
  not not_138 (not_138_out, OP5);
  not not_139 (not_139_out, OP3);
  not not_140 (not_140_out, OP2);
  not not_141 (not_141_out, OP6);
  not not_142 (not_142_out, OP5);
  not not_143 (not_143_out, OP3);
  not not_144 (not_144_out, OP2);
  not not_145 (not_145_out, F14);
  not not_146 (not_146_out, F12);
  not not_147 (not_147_out, OP6);
  not not_148 (not_148_out, OP5);
  not not_149 (not_149_out, OP4);
  not not_150 (not_150_out, OP3);
  not not_151 (not_151_out, OP2);
  not not_152 (not_152_out, F30);
  not not_153 (not_153_out, F25);
  not not_154 (not_154_out, F12);
  not not_155 (not_155_out, OP6);
  not not_156 (not_156_out, OP3);
  not not_157 (not_157_out, OP2);
  not not_158 (not_158_out, F30);
  not not_159 (not_159_out, F25);
  not not_160 (not_160_out, F14);
  not not_161 (not_161_out, F12);
  not not_162 (not_162_out, OP6);
  not not_163 (not_163_out, OP3);
  not not_164 (not_164_out, OP2);
  not not_165 (not_165_out, F30);
  not not_166 (not_166_out, F25);
  not not_167 (not_167_out, F14);
  not not_168 (not_168_out, OP6);
  not not_169 (not_169_out, OP3);
  not not_170 (not_170_out, OP2);
  not not_171 (not_171_out, F12);
  not not_172 (not_172_out, OP6);
  not not_173 (not_173_out, OP5);
  not not_174 (not_174_out, OP3);
  not not_175 (not_175_out, OP2);
  not not_176 (not_176_out, F13);
  not not_177 (not_177_out, F12);
  not not_178 (not_178_out, OP6);
  not not_179 (not_179_out, OP5);
  not not_180 (not_180_out, OP3);
  not not_181 (not_181_out, OP2);
  not not_182 (not_182_out, F14);
  not not_183 (not_183_out, F12);
  not not_184 (not_184_out, OP6);
  not not_185 (not_185_out, OP5);
  not not_186 (not_186_out, OP3);
  not not_187 (not_187_out, OP2);
  not not_188 (not_188_out, F30);
  not not_189 (not_189_out, F25);
  not not_190 (not_190_out, F13);
  not not_191 (not_191_out, F12);
  not not_192 (not_192_out, OP6);
  not not_193 (not_193_out, OP3);
  not not_194 (not_194_out, OP2);
  not not_195 (not_195_out, F13);
  not not_196 (not_196_out, OP4);
  not not_197 (not_197_out, OP3);
  not not_198 (not_198_out, OP2);
  and and_1 (and_1_out, not_1_out, not_2_out, not_3_out, not_4_out, not_5_out, not_6_out, OP5, OP4, not_7_out, not_8_out);
  and and_2 (and_2_out, not_9_out, not_10_out, F14, F13, F12, not_11_out, OP5, OP4, not_12_out, not_13_out);
  and and_3 (and_3_out, not_14_out, not_15_out, not_16_out, F13, not_17_out, not_18_out, OP5, OP4, not_19_out, not_20_out);
  and and_4 (and_4_out, not_21_out, not_22_out, not_23_out, not_24_out, not_25_out, OP4, not_26_out, not_27_out);
  and and_5 (and_5_out, F14, F13, F12, not_28_out, not_29_out, OP4, not_30_out, not_31_out);
  and and_6 (and_6_out, F14, not_32_out, not_33_out, not_34_out, not_35_out, OP4, not_36_out, not_37_out);
  and and_7 (and_7_out, not_38_out, F13, not_39_out, not_40_out, not_41_out, OP4, not_42_out, not_43_out);
  and and_8 (and_8_out, F30, not_44_out, F14, not_45_out, F12, not_46_out, not_47_out, OP4, not_48_out, not_49_out);
  and and_9 (and_9_out, not_50_out, F13, not_51_out, not_52_out, not_53_out, not_54_out, not_55_out, not_56_out);
  and and_10 (and_10_out, not_57_out, not_58_out, F14, not_59_out, not_60_out, not_61_out, OP5, OP4, not_62_out, not_63_out);
  and and_11 (and_11_out, F14, not_64_out, F12, OP6, OP5, not_65_out, not_66_out, not_67_out);
  and and_12 (and_12_out, F30, not_68_out, not_69_out, not_70_out, not_71_out, not_72_out, OP5, OP4, not_73_out, not_74_out);
  and and_13 (and_13_out, not_75_out, not_76_out, F14, F13, F12, not_77_out, OP5, OP4, not_78_out, not_79_out);
  and and_14 (and_14_out, not_80_out, not_81_out, not_82_out, F13, not_83_out, not_84_out, OP5, OP4, not_85_out, not_86_out);
  and and_15 (and_15_out, F14, F13, F12, not_87_out, not_88_out, OP4, not_89_out, not_90_out);
  and and_16 (and_16_out, not_91_out, F13, not_92_out, not_93_out, not_94_out, OP4, not_95_out, not_96_out);
  and and_17 (and_17_out, not_97_out, not_98_out, F14, not_99_out, F12, not_100_out, not_101_out, OP4, not_102_out, not_103_out);
  and and_18 (and_18_out, F14, not_104_out, F12, OP6, OP5, not_105_out, not_106_out, not_107_out);
  and and_19 (and_19_out, not_108_out, not_109_out, not_110_out, not_111_out, not_112_out, not_113_out, OP5, OP4, not_114_out, not_115_out);
  and and_20 (and_20_out, F30, not_116_out, not_117_out, not_118_out, not_119_out, not_120_out, OP5, OP4, not_121_out, not_122_out);
  and and_21 (and_21_out, not_123_out, not_124_out, F14, F13, F12, not_125_out, OP5, OP4, not_126_out, not_127_out);
  and and_22 (and_22_out, not_128_out, not_129_out, not_130_out, F13, F12, not_131_out, OP5, OP4, not_132_out, not_133_out);
  and and_23 (and_23_out, not_134_out, not_135_out, not_136_out, not_137_out, not_138_out, OP4, not_139_out, not_140_out);
  and and_24 (and_24_out, F14, F13, F12, not_141_out, not_142_out, OP4, not_143_out, not_144_out);
  and and_25 (and_25_out, not_145_out, F13, not_146_out, not_147_out, not_148_out, not_149_out, not_150_out, not_151_out);
  and and_26 (and_26_out, not_152_out, not_153_out, F14, F13, not_154_out, not_155_out, OP5, OP4, not_156_out, not_157_out);
  and and_27 (and_27_out, not_158_out, not_159_out, not_160_out, F13, not_161_out, not_162_out, OP5, OP4, not_163_out, not_164_out);
  and and_28 (and_28_out, not_165_out, not_166_out, not_167_out, F13, F12, not_168_out, OP5, OP4, not_169_out, not_170_out);
  and and_29 (and_29_out, F14, F13, not_171_out, not_172_out, not_173_out, OP4, not_174_out, not_175_out);
  and and_30 (and_30_out, F14, not_176_out, not_177_out, not_178_out, not_179_out, OP4, not_180_out, not_181_out);
  and and_31 (and_31_out, not_182_out, F13, not_183_out, not_184_out, not_185_out, OP4, not_186_out, not_187_out);
  and and_32 (and_32_out, not_188_out, not_189_out, F14, not_190_out, not_191_out, not_192_out, OP5, OP4, not_193_out, not_194_out);
  and and_33 (and_33_out, F14, not_195_out, F12, OP6, OP5, not_196_out, not_197_out, not_198_out);
  or or_1 (S0, and_1_out, and_2_out, and_3_out, and_4_out, and_5_out, and_6_out, and_7_out, and_8_out, and_9_out, and_10_out, and_11_out);
  or or_2 (S1, and_12_out, and_13_out, and_14_out, and_15_out, and_16_out, and_17_out, and_18_out);
  or or_3 (S2, and_19_out, and_20_out, and_21_out, and_22_out, and_23_out, and_24_out, and_25_out);
  or or_4 (S3, and_26_out, and_27_out, and_28_out, and_29_out, and_30_out, and_31_out, and_32_out, and_33_out);
endmodule

// 控制信号生成
module \控制信号自动生成  (
  input  OP2,
  input  OP3,
  input  OP4,
  input  OP5,
  input  OP6,
  input  F12,
  input  F13,
  input  F14,
  input  F25,
  input  F30,
  output MemToReg,
  output MemWrite,
  output ALU_SRC,
  output RegWrite,
  output ecall,
  output S_Type,
  output BEQ,
  output BNE,
  output JALR,
  output JAL,
  output SB,
  output BGE,
  output r1_used,
  output r2_used,
  output CSRRSI,
  output CSRRCI
);

  wire and_3_out, and_4_out, and_5_out, and_6_out, and_7_out, and_8_out, and_9_out, and_10_out, and_11_out,
       and_12_out, and_13_out, and_14_out, and_15_out, and_16_out, and_17_out, and_18_out, and_27_out,
       and_28_out, and_29_out, and_30_out, and_31_out, and_32_out, and_33_out, and_34_out, and_35_out,
       and_36_out, and_37_out, and_38_out, and_39_out, and_40_out, and_41_out, and_42_out, and_43_out,
       and_44_out, not_1_out, not_2_out, not_3_out, not_4_out, not_5_out, not_6_out, not_7_out, not_8_out,
       not_9_out, not_10_out, not_11_out, not_12_out, not_13_out, not_14_out, not_15_out, not_16_out,
       not_17_out, not_18_out, not_19_out, not_20_out, not_21_out, not_22_out, not_23_out, not_24_out,
       not_25_out, not_26_out, not_27_out, not_28_out, not_29_out, not_30_out, not_31_out, not_32_out,
       not_33_out, not_34_out, not_35_out, not_36_out, not_37_out, not_38_out, not_39_out, not_40_out,
       not_41_out, not_42_out, not_43_out, not_44_out, not_45_out, not_46_out, not_47_out, not_48_out,
       not_49_out, not_50_out, not_51_out, not_52_out, not_53_out, not_54_out, not_55_out, not_56_out,
       not_57_out, not_58_out, not_59_out, not_60_out, not_61_out, not_62_out, not_63_out, not_64_out,
       not_65_out, not_66_out, not_67_out, not_68_out, not_69_out, not_70_out, not_71_out, not_72_out,
       not_73_out, not_74_out, not_75_out, not_76_out, not_77_out, not_78_out, not_79_out, not_80_out,
       not_81_out, not_82_out, not_83_out, not_84_out, not_85_out, not_86_out, not_87_out, not_88_out,
       not_89_out, not_90_out, not_91_out, not_92_out, not_93_out, not_94_out, not_95_out, not_96_out,
       not_97_out, not_98_out, not_99_out, not_100_out, not_101_out, not_102_out, not_103_out, not_104_out,
       not_105_out, not_106_out, not_107_out, not_108_out, not_109_out, not_110_out, not_111_out,
       not_112_out, not_113_out, not_114_out, not_115_out, not_116_out, not_117_out, not_118_out,
       not_119_out, not_120_out, not_121_out, not_122_out, not_123_out, not_124_out, not_125_out,
       not_126_out, not_127_out, not_128_out, not_129_out, not_130_out, not_131_out, not_132_out,
       not_133_out, not_134_out, not_135_out, not_136_out, not_137_out, not_138_out, not_139_out,
       not_140_out, not_141_out, not_142_out, not_143_out, not_144_out, not_145_out, not_146_out,
       not_147_out, not_148_out, not_149_out, not_150_out, not_151_out, not_152_out, not_153_out,
       not_154_out, not_155_out, not_156_out, not_157_out, not_158_out, not_159_out, not_160_out,
       not_161_out, not_162_out, not_163_out, not_164_out, not_165_out, not_166_out, not_167_out,
       not_168_out, not_169_out, not_170_out, not_171_out, not_172_out, not_173_out, not_174_out,
       not_175_out, not_176_out, not_177_out, not_178_out, not_179_out, not_180_out, not_181_out,
       not_182_out, not_183_out, not_184_out, not_185_out, not_186_out, not_187_out, not_188_out,
       not_189_out, not_190_out, not_191_out, not_192_out, not_193_out, not_194_out, not_195_out,
       not_196_out, not_197_out, not_198_out, not_199_out, not_200_out, not_201_out, not_202_out,
       not_203_out, not_204_out, not_205_out, not_206_out, not_207_out, not_208_out, not_209_out,
       not_210_out, not_211_out, not_212_out, not_213_out, not_214_out, not_215_out, not_216_out,
       not_217_out, not_218_out, not_219_out, not_220_out, not_221_out, not_222_out, not_223_out,
       not_224_out, not_225_out, not_226_out, not_227_out, not_228_out, not_229_out, not_230_out,
       not_231_out, not_232_out, not_233_out, not_234_out, not_235_out, not_236_out, not_237_out,
       not_238_out, not_239_out, not_240_out, not_241_out, not_242_out, not_243_out;

  not not_1 (not_1_out, OP2);
  not not_2 (not_2_out, OP3);
  not not_3 (not_3_out, OP4);
  not not_4 (not_4_out, OP5);
  not not_5 (not_5_out, OP6);
  not not_6 (not_6_out, F12);
  not not_7 (not_7_out, F14);
  not not_8 (not_8_out, OP2);
  not not_9 (not_9_out, OP3);
  not not_10 (not_10_out, OP4);
  not not_11 (not_11_out, OP6);
  not not_12 (not_12_out, F12);
  not not_13 (not_13_out, F14);
  not not_14 (not_14_out, OP2);
  not not_15 (not_15_out, OP3);
  not not_16 (not_16_out, OP5);
  not not_17 (not_17_out, OP6);
  not not_18 (not_18_out, F12);
  not not_19 (not_19_out, F14);
  not not_20 (not_20_out, OP2);
  not not_21 (not_21_out, OP3);
  not not_22 (not_22_out, OP4);
  not not_23 (not_23_out, OP6);
  not not_24 (not_24_out, F12);
  not not_25 (not_25_out, F14);
  not not_26 (not_26_out, OP2);
  not not_27 (not_27_out, OP3);
  not not_28 (not_28_out, OP5);
  not not_29 (not_29_out, OP6);
  not not_30 (not_30_out, F12);
  not not_31 (not_31_out, OP2);
  not not_32 (not_32_out, OP3);
  not not_33 (not_33_out, OP5);
  not not_34 (not_34_out, OP6);
  not not_35 (not_35_out, F13);
  not not_36 (not_36_out, F25);
  not not_37 (not_37_out, F30);
  not not_38 (not_38_out, OP2);
  not not_39 (not_39_out, OP3);
  not not_40 (not_40_out, OP5);
  not not_41 (not_41_out, OP6);
  not not_42 (not_42_out, F25);
  not not_43 (not_43_out, OP2);
  not not_44 (not_44_out, OP3);
  not not_45 (not_45_out, OP5);
  not not_46 (not_46_out, OP6);
  not not_47 (not_47_out, OP2);
  not not_48 (not_48_out, OP3);
  not not_49 (not_49_out, OP5);
  not not_50 (not_50_out, OP6);
  not not_51 (not_51_out, F12);
  not not_52 (not_52_out, F14);
  not not_53 (not_53_out, OP2);
  not not_54 (not_54_out, OP3);
  not not_55 (not_55_out, OP5);
  not not_56 (not_56_out, OP6);
  not not_57 (not_57_out, F12);
  not not_58 (not_58_out, OP2);
  not not_59 (not_59_out, OP3);
  not not_60 (not_60_out, OP6);
  not not_61 (not_61_out, F12);
  not not_62 (not_62_out, F13);
  not not_63 (not_63_out, F14);
  not not_64 (not_64_out, F25);
  not not_65 (not_65_out, OP2);
  not not_66 (not_66_out, OP3);
  not not_67 (not_67_out, OP6);
  not not_68 (not_68_out, F12);
  not not_69 (not_69_out, F25);
  not not_70 (not_70_out, F30);
  not not_71 (not_71_out, OP2);
  not not_72 (not_72_out, OP3);
  not not_73 (not_73_out, OP6);
  not not_74 (not_74_out, F13);
  not not_75 (not_75_out, F14);
  not not_76 (not_76_out, F25);
  not not_77 (not_77_out, F30);
  not not_78 (not_78_out, OP2);
  not not_79 (not_79_out, OP3);
  not not_80 (not_80_out, OP5);
  not not_81 (not_81_out, OP6);
  not not_82 (not_82_out, F25);
  not not_83 (not_83_out, OP2);
  not not_84 (not_84_out, OP3);
  not not_85 (not_85_out, OP5);
  not not_86 (not_86_out, OP6);
  not not_87 (not_87_out, OP2);
  not not_88 (not_88_out, OP3);
  not not_89 (not_89_out, OP6);
  not not_90 (not_90_out, F25);
  not not_91 (not_91_out, F30);
  not not_92 (not_92_out, OP4);
  not not_93 (not_93_out, F12);
  not not_94 (not_94_out, F13);
  not not_95 (not_95_out, F14);
  not not_96 (not_96_out, OP4);
  not not_97 (not_97_out, OP2);
  not not_98 (not_98_out, OP3);
  not not_99 (not_99_out, F12);
  not not_100 (not_100_out, F13);
  not not_101 (not_101_out, F14);
  not not_102 (not_102_out, F25);
  not not_103 (not_103_out, F30);
  not not_104 (not_104_out, OP2);
  not not_105 (not_105_out, OP3);
  not not_106 (not_106_out, OP4);
  not not_107 (not_107_out, OP6);
  not not_108 (not_108_out, F12);
  not not_109 (not_109_out, F14);
  not not_110 (not_110_out, OP2);
  not not_111 (not_111_out, OP3);
  not not_112 (not_112_out, OP4);
  not not_113 (not_113_out, F12);
  not not_114 (not_114_out, F13);
  not not_115 (not_115_out, F14);
  not not_116 (not_116_out, OP2);
  not not_117 (not_117_out, OP3);
  not not_118 (not_118_out, OP4);
  not not_119 (not_119_out, F13);
  not not_120 (not_120_out, F14);
  not not_121 (not_121_out, OP3);
  not not_122 (not_122_out, OP4);
  not not_123 (not_123_out, F12);
  not not_124 (not_124_out, F13);
  not not_125 (not_125_out, F14);
  not not_126 (not_126_out, OP4);
  not not_127 (not_127_out, OP2);
  not not_128 (not_128_out, OP3);
  not not_129 (not_129_out, OP4);
  not not_130 (not_130_out, OP6);
  not not_131 (not_131_out, F12);
  not not_132 (not_132_out, F13);
  not not_133 (not_133_out, F14);
  not not_134 (not_134_out, OP2);
  not not_135 (not_135_out, OP3);
  not not_136 (not_136_out, OP4);
  not not_137 (not_137_out, F13);
  not not_138 (not_138_out, OP2);
  not not_139 (not_139_out, OP3);
  not not_140 (not_140_out, OP4);
  not not_141 (not_141_out, OP6);
  not not_142 (not_142_out, F12);
  not not_143 (not_143_out, F14);
  not not_144 (not_144_out, OP2);
  not not_145 (not_145_out, OP3);
  not not_146 (not_146_out, OP4);
  not not_147 (not_147_out, F12);
  not not_148 (not_148_out, F13);
  not not_149 (not_149_out, F14);
  not not_150 (not_150_out, OP2);
  not not_151 (not_151_out, OP3);
  not not_152 (not_152_out, F12);
  not not_153 (not_153_out, F13);
  not not_154 (not_154_out, F14);
  not not_155 (not_155_out, F25);
  not not_156 (not_156_out, F30);
  not not_157 (not_157_out, OP3);
  not not_158 (not_158_out, OP4);
  not not_159 (not_159_out, F12);
  not not_160 (not_160_out, F13);
  not not_161 (not_161_out, F14);
  not not_162 (not_162_out, OP2);
  not not_163 (not_163_out, OP3);
  not not_164 (not_164_out, OP4);
  not not_165 (not_165_out, F13);
  not not_166 (not_166_out, OP2);
  not not_167 (not_167_out, OP3);
  not not_168 (not_168_out, OP5);
  not not_169 (not_169_out, OP6);
  not not_170 (not_170_out, F12);
  not not_171 (not_171_out, OP2);
  not not_172 (not_172_out, OP3);
  not not_173 (not_173_out, OP6);
  not not_174 (not_174_out, F12);
  not not_175 (not_175_out, F13);
  not not_176 (not_176_out, F14);
  not not_177 (not_177_out, F25);
  not not_178 (not_178_out, OP2);
  not not_179 (not_179_out, OP3);
  not not_180 (not_180_out, OP6);
  not not_181 (not_181_out, F12);
  not not_182 (not_182_out, F25);
  not not_183 (not_183_out, F30);
  not not_184 (not_184_out, OP2);
  not not_185 (not_185_out, OP3);
  not not_186 (not_186_out, OP6);
  not not_187 (not_187_out, F13);
  not not_188 (not_188_out, F14);
  not not_189 (not_189_out, F25);
  not not_190 (not_190_out, F30);
  not not_191 (not_191_out, OP2);
  not not_192 (not_192_out, OP3);
  not not_193 (not_193_out, OP5);
  not not_194 (not_194_out, OP6);
  not not_195 (not_195_out, F25);
  not not_196 (not_196_out, OP2);
  not not_197 (not_197_out, OP3);
  not not_198 (not_198_out, OP5);
  not not_199 (not_199_out, OP6);
  not not_200 (not_200_out, OP2);
  not not_201 (not_201_out, OP3);
  not not_202 (not_202_out, OP6);
  not not_203 (not_203_out, F25);
  not not_204 (not_204_out, F30);
  not not_205 (not_205_out, OP2);
  not not_206 (not_206_out, OP3);
  not not_207 (not_207_out, OP4);
  not not_208 (not_208_out, OP6);
  not not_209 (not_209_out, F12);
  not not_210 (not_210_out, F14);
  not not_211 (not_211_out, OP2);
  not not_212 (not_212_out, OP3);
  not not_213 (not_213_out, OP4);
  not not_214 (not_214_out, F12);
  not not_215 (not_215_out, F13);
  not not_216 (not_216_out, F14);
  not not_217 (not_217_out, OP2);
  not not_218 (not_218_out, OP3);
  not not_219 (not_219_out, OP6);
  not not_220 (not_220_out, F12);
  not not_221 (not_221_out, F13);
  not not_222 (not_222_out, F14);
  not not_223 (not_223_out, F25);
  not not_224 (not_224_out, OP2);
  not not_225 (not_225_out, OP3);
  not not_226 (not_226_out, OP4);
  not not_227 (not_227_out, F13);
  not not_228 (not_228_out, OP2);
  not not_229 (not_229_out, OP3);
  not not_230 (not_230_out, OP6);
  not not_231 (not_231_out, F14);
  not not_232 (not_232_out, F25);
  not not_233 (not_233_out, F30);
  not not_234 (not_234_out, OP2);
  not not_235 (not_235_out, OP3);
  not not_236 (not_236_out, OP6);
  not not_237 (not_237_out, F25);
  not not_238 (not_238_out, F30);
  not not_239 (not_239_out, F12);
  not not_240 (not_240_out, OP3);
  not not_241 (not_241_out, OP2);
  not not_242 (not_242_out, OP3);
  not not_243 (not_243_out, OP2);
  and and_1 (MemToReg, not_1_out, not_2_out, not_3_out, not_4_out, not_5_out, not_6_out, F13, not_7_out);
  and and_2 (MemWrite, not_8_out, not_9_out, not_10_out, OP5, not_11_out, not_12_out, not_13_out);
  and and_3 (and_3_out, not_14_out, not_15_out, not_16_out, not_17_out, not_18_out, F13, not_19_out);
  and and_4 (and_4_out, not_20_out, not_21_out, not_22_out, OP5, not_23_out, not_24_out, not_25_out);
  and and_5 (and_5_out, not_26_out, not_27_out, OP4, not_28_out, not_29_out, not_30_out);
  and and_6 (and_6_out, not_31_out, not_32_out, OP4, not_33_out, not_34_out, not_35_out, not_36_out, not_37_out);
  and and_7 (and_7_out, not_38_out, not_39_out, OP4, not_40_out, not_41_out, F14, not_42_out);
  and and_8 (and_8_out, not_43_out, not_44_out, OP4, not_45_out, not_46_out, F13, F14);
  and and_9 (and_9_out, not_47_out, not_48_out, not_49_out, not_50_out, not_51_out, F13, not_52_out);
  and and_10 (and_10_out, not_53_out, not_54_out, OP4, not_55_out, not_56_out, not_57_out);
  and and_11 (and_11_out, not_58_out, not_59_out, OP4, not_60_out, not_61_out, not_62_out, not_63_out, not_64_out);
  and and_12 (and_12_out, not_65_out, not_66_out, OP4, not_67_out, not_68_out, not_69_out, not_70_out);
  and and_13 (and_13_out, not_71_out, not_72_out, OP4, not_73_out, not_74_out, not_75_out, not_76_out, not_77_out);
  and and_14 (and_14_out, not_78_out, not_79_out, OP4, not_80_out, not_81_out, F14, not_82_out);
  and and_15 (and_15_out, not_83_out, not_84_out, OP4, not_85_out, not_86_out, F13, F14);
  and and_16 (and_16_out, not_87_out, not_88_out, OP4, OP5, not_89_out, F13, not_90_out, not_91_out);
  and and_17 (and_17_out, OP2, not_92_out, OP5, OP6, not_93_out, not_94_out, not_95_out);
  and and_18 (and_18_out, OP2, OP3, not_96_out, OP5, OP6);
  and and_19 (ecall, not_97_out, not_98_out, OP4, OP5, OP6, not_99_out, not_100_out, not_101_out, not_102_out, not_103_out);
  and and_20 (S_Type, not_104_out, not_105_out, not_106_out, OP5, not_107_out, not_108_out, not_109_out);
  and and_21 (BEQ, not_110_out, not_111_out, not_112_out, OP5, OP6, not_113_out, not_114_out, not_115_out);
  and and_22 (BNE, not_116_out, not_117_out, not_118_out, OP5, OP6, F12, not_119_out, not_120_out);
  and and_23 (JALR, OP2, not_121_out, not_122_out, OP5, OP6, not_123_out, not_124_out, not_125_out);
  and and_24 (JAL, OP2, OP3, not_126_out, OP5, OP6);
  and and_25 (SB, not_127_out, not_128_out, not_129_out, OP5, not_130_out, not_131_out, not_132_out, not_133_out);
  and and_26 (BGE, not_134_out, not_135_out, not_136_out, OP5, OP6, F12, not_137_out, F14);
  and and_27 (and_27_out, not_138_out, not_139_out, not_140_out, not_141_out, not_142_out, F13, not_143_out);
  and and_28 (and_28_out, not_144_out, not_145_out, not_146_out, OP5, not_147_out, not_148_out, not_149_out);
  and and_29 (and_29_out, not_150_out, not_151_out, OP5, not_152_out, not_153_out, not_154_out, not_155_out, not_156_out);
  and and_30 (and_30_out, not_157_out, not_158_out, OP5, OP6, not_159_out, not_160_out, not_161_out);
  and and_31 (and_31_out, not_162_out, not_163_out, not_164_out, OP5, OP6, F12, not_165_out);
  and and_32 (and_32_out, not_166_out, not_167_out, OP4, not_168_out, not_169_out, not_170_out);
  and and_33 (and_33_out, not_171_out, not_172_out, OP4, not_173_out, not_174_out, not_175_out, not_176_out, not_177_out);
  and and_34 (and_34_out, not_178_out, not_179_out, OP4, not_180_out, not_181_out, not_182_out, not_183_out);
  and and_35 (and_35_out, not_184_out, not_185_out, OP4, not_186_out, not_187_out, not_188_out, not_189_out, not_190_out);
  and and_36 (and_36_out, not_191_out, not_192_out, OP4, not_193_out, not_194_out, F14, not_195_out);
  and and_37 (and_37_out, not_196_out, not_197_out, OP4, not_198_out, not_199_out, F13, F14);
  and and_38 (and_38_out, not_200_out, not_201_out, OP4, OP5, not_202_out, F13, not_203_out, not_204_out);
  and and_39 (and_39_out, not_205_out, not_206_out, not_207_out, OP5, not_208_out, not_209_out, not_210_out);
  and and_40 (and_40_out, not_211_out, not_212_out, not_213_out, OP5, not_214_out, not_215_out, not_216_out);
  and and_41 (and_41_out, not_217_out, not_218_out, OP5, not_219_out, not_220_out, not_221_out, not_222_out, not_223_out);
  and and_42 (and_42_out, not_224_out, not_225_out, not_226_out, OP5, OP6, F12, not_227_out);
  and and_43 (and_43_out, not_228_out, not_229_out, OP4, OP5, not_230_out, not_231_out, not_232_out, not_233_out);
  and and_44 (and_44_out, not_234_out, not_235_out, OP4, OP5, not_236_out, F13, not_237_out, not_238_out);
  and and_45 (CSRRSI, F14, F13, not_239_out, OP6, OP5, OP4, not_240_out, not_241_out);
  and and_46 (CSRRCI, F14, F13, F12, OP6, OP5, OP4, not_242_out, not_243_out);
  or or_1 (ALU_SRC, and_3_out, and_4_out, and_5_out, and_6_out, and_7_out, and_8_out);
  or or_2 (r2_used, and_39_out, and_40_out, and_41_out, and_42_out, and_43_out, and_44_out);
  or or_3 (RegWrite, and_9_out, and_10_out, and_11_out, and_12_out, and_13_out, and_14_out, and_15_out, and_16_out, and_17_out, and_18_out);
  or or_4 (r1_used, and_27_out, and_28_out, and_29_out, and_30_out, and_31_out, and_32_out, and_33_out, and_34_out, and_35_out, and_36_out, and_37_out, and_38_out);
endmodule

// ALU
module ALU (
  input  [31:0] X,
  input  [31:0] Y,
  input  [3:0] AluOP,
  output out_4,
  output Equal,
  output out_6,
  output [31:0] Result,
  output [31:0] Result_2
);

  wire [0:0] comparator_1_lt, comparator_2_lt;
  wire [31:0] adder_1_out, AND_out, divider_1_out, divider_1_rem, multiplier_1_cout, multiplier_1_out,
       NOR_out, OR_out, shifter_1_out, shifter_2_out, shifter_3_out, subtractor_1_out, XOR_out;

  assign AND_out = X & Y;  // AND_Gate AND, 32 bits wide
  assign OR_out = X | Y;  // OR_Gate OR, 32 bits wide
  Shifter #(.width(32), .shift("ll")) shifter_1 (.in(X), .\dist (Y[4:0]), .out(shifter_1_out));
  Shifter #(.width(32), .shift("ar")) shifter_2 (.in(X), .\dist (Y[4:0]), .out(shifter_2_out));
  Shifter #(.width(32), .shift("lr")) shifter_3 (.in(X), .\dist (Y[4:0]), .out(shifter_3_out));
  Multiplier #(.width(32)) multiplier_1 (.a(X), .b(Y), .out(multiplier_1_out), .cout(multiplier_1_cout));  // open: cin
  Divider #(.width(32)) divider_1 (.a(X), .b(Y), .out(divider_1_out), .rem(divider_1_rem));  // open: upper
  Adder #(.width(32)) adder_1 (.a(X), .b(Y), .out(adder_1_out));  // open: cin, cout
  Subtractor #(.width(32)) subtractor_1 (.a(X), .b(Y), .out(subtractor_1_out));  // open: bin, bout
  assign XOR_out = X ^ Y;  // XOR_Gate XOR, 32 bits wide
  assign NOR_out = ~(X | Y);  // NOR_Gate NOR, 32 bits wide
  Comparator #(.width(32), .mode("twosComplement")) comparator_1 (
    .a(X), .b(Y), .eq(Equal), .lt(comparator_1_lt[0]));  // open: gt
  Comparator #(.width(32), .mode("unsigned")) comparator_2 (.a(X), .b(Y), .lt(comparator_2_lt[0]));  // open: gt, eq
  Multiplexer #(.select(4), .width(32), .disabled("Z"), .enable("false")) multiplexer_1 (
    .in0(shifter_1_out), .in1(shifter_2_out), .in2(shifter_3_out), .in3(multiplier_1_out),
    .in4(divider_1_out), .in5(adder_1_out), .in6(subtractor_1_out), .in7(AND_out), .in8(OR_out),
    .in9(XOR_out), .in10(NOR_out), .in11({{31{1'b0}}, comparator_1_lt[0]}),
    .in12({{31{1'b0}}, comparator_2_lt[0]}), .in13({32{1'b0}}), .in14({32{1'b0}}), .in15({32{1'b0}}),
    .out(Result), .sel(AluOP));
  Multiplexer #(.select(4), .width(32), .disabled("Z"), .enable("false")) multiplexer_2 (
    .in0({32{1'b0}}), .in1({32{1'b0}}), .in2({32{1'b0}}), .in3(multiplier_1_cout), .in4(divider_1_rem),
    .in5({32{1'b0}}), .in6({32{1'b0}}), .in7({32{1'b0}}), .in8({32{1'b0}}), .in9({32{1'b0}}),
    .in10({32{1'b0}}), .in11({32{1'b0}}), .in12({32{1'b0}}), .in13({32{1'b0}}), .in14({32{1'b0}}),
    .in15({32{1'b0}}), .out(Result_2), .sel(AluOP));
  Multiplexer #(.select(4), .width(1), .disabled("Z"), .enable("false")) multiplexer_3 (
    .in0(1'b0), .in1(1'b0), .in2(1'b0), .in3(1'b0), .in4(1'b0), .in5(1'b0), .in6(1'b0), .in7(1'b0),
    .in8(1'b0), .in9(1'b0), .in10(1'b0), .in11(comparator_1_lt[0]), .in12(comparator_2_lt[0]), .in13(1'b0),
    .in14(1'b0), .in15(1'b0), .out(out_6), .sel(AluOP));
  not not_1 (out_4, out_6);

  // Other names for the same wires on the sheet: Result2[31:0] = Result_2; S[3:0] = AluOP; tunnel = out_6;
  //   tunnel_t = out_4

  // Notes on the sheet:
  //   不要改变此引脚区域内容，也不要改变ALU封装形式
  //   输入引脚
  //   输出引脚
endmodule

module Regifile (
  input  [31:0] Din,
  input  Clk,
  input  WE,
  input  [4:0] R1_num,
  input  [4:0] W_num,
  input  [4:0] R2_num,
  output [31:0] R1,
  output [31:0] R2
);

  // RegisterFile registerfile_1: pin names not known; wires that end beside it: Din, Clk, WE, W_num, R1_num, R2_num, R1, R2
endmodule

module \理想流水线  (
  output RegWrite,
  output MemWrite,
  output [31:0] IF_PC,
  output [31:0] ID_PC,
  output [31:0] EX_PC,
  output [31:0] M_PC,
  output [31:0] WB_PC,
  output [31:0] RDin,
  output [31:0] MDin,
  output [31:0] LedData
);

  wire AluSrcB, and_1_out, and_2_out, Beq, BGE, Bne, CLK, clock_1_out, clock_2_out, comparator_1_eq,
       comparator_2_eq, comparator_2_lt, d_ff_1_q, ecall, \ex_mem流水寄存器_1_halt_2 , \ex_mem流水寄存器_1_memtoreg_2 ,
       \ex_mem流水寄存器_1_regwrite_2 , Go, halt, \id_ex流水寄存器_1_halt_2 , \id_ex流水寄存器_1_memtoreg_2 ,
       \id_ex流水寄存器_1_memwrite_2 , \id_ex流水寄存器_1_regwrite_2 , IR1, IR2, IR3, JAL, JALR, MemToReg, nand_1_out,
       not_1_out, not_2_out, not_3_out, RST, Run, S_type, SB, URET, W1, W2, W3, \单周期硬布线控制器_1_alu_src ,
       \单周期硬布线控制器_1_memtoreg , \单周期硬布线控制器_1_memwrite , \单周期硬布线控制器_1_regwrite ;
  wire [3:0] AluOP, \单周期硬布线控制器_1_alu_op ;
  wire [4:0] \ex_mem流水寄存器_1_w_num_2 , \id_ex流水寄存器_1_writereg_num_2 , multiplexer_1_out, multiplexer_2_out,
       W_num;
  wire [12:0] CNT_num;
  wire [15:0] \LoadUse次数 , \总周期数 , \插入气泡数 , \无条件分支数 , \条件分支成功数 ;
  wire [31:0] alu_1_result, bit_extender_1_out, bit_extender_2_out, bit_extender_3_out, bit_extender_4_out,
       EX_IR, \ex_mem流水寄存器_1_aluresult_2 , \id_ex流水寄存器_1_r1_2 , \id_ex流水寄存器_1_r2_2 ,
       \id_ex流水寄存器_1_signimm_2 , ID_IR, IF_IR, MEM_IR, \mem_wb流水寄存器_1_aluresult_2 , \mem_wb流水寄存器_1_rd_2 ,
       multiplexer_3_out, multiplexer_4_out, PC_4, R1, R2, ram_1_data, WB_IR;

  Button \u_总复位  (.out(RST));
  Button _1 (.out(IR1));
  Button _2 (.out(IR2));
  Button _3 (.out(IR3));
  // Probe on \总周期数 
  // Probe on \总周期数 
  Button \u_继续运行  (.out(Go));
  LED #(.active("true")) led_1 (.in(W1));
  LED #(.active("true")) led_2 (.in(W2));
  LED #(.active("true")) led_3 (.in(W3));
  Register #(.width(32), .trigger("rising"), .Select("low")) PC (.D(PC_4), .en(Run), .Q(IF_PC), .clk(CLK), .clr(RST));
  or or_1 (Run, Go, not_1_out);
  not not_1 (not_1_out, halt);
  not not_2 (not_2_out, halt);
  Counter #(.width(16), .max('hffff), .ongoal("wrap"), .trigger("rising"), .behavior("new")) counter_1 (
    .count(not_2_out), .Q(\总周期数 ), .clk(CLK), .clr(RST));  // open: load, D, carry, preset, down
  Hex_Digit_Display hex_digit_display_1 (.value(LedData[31:28]));  // open: dp
  // Probe on IF_PC[19:0]
  // RiscV_Probe riscv_probe_1: pin names not known; wires that end beside it: IF_IR
  Hex_Digit_Display hex_digit_display_2 (.value(LedData[27:24]));  // open: dp
  Hex_Digit_Display hex_digit_display_3 (.value(LedData[23:20]));  // open: dp
  // Probe on ID_PC[19:0]
  // RiscV_Probe riscv_probe_2: pin names not known; wires that end beside it: ID_IR
  Hex_Digit_Display hex_digit_display_4 (.value(LedData[19:16]));  // open: dp
  Hex_Digit_Display hex_digit_display_5 (.value(LedData[15:12]));  // open: dp
  ROM #(.addrWidth(10), .dataWidth(32), .Select("high")) \u_指令存储器  (.addr(IF_PC[11:2]), .data(IF_IR));
  Adder #(.width(32)) adder_1 (.a(IF_PC), .b(32'h4), .out(PC_4));  // open: cin, cout
  Hex_Digit_Display hex_digit_display_6 (.value(LedData[7:4]));  // open: dp
  Hex_Digit_Display hex_digit_display_7 (.value(LedData[11:8]));  // open: dp
  Clock #(.highDuration(1), .lowDuration(1)) clock_1 (.out(clock_1_out));
  // Probe on EX_PC[19:0]
  // RiscV_Probe riscv_probe_3: pin names not known; wires that end beside it: EX_IR, clock_1_out, CLK
  \IF_ID流水寄存器  \if_id流水寄存器_1  (
    .\指令字_IR (IF_IR), .PC(IF_PC), .\指令字_IR_2 (ID_IR), .PC_2(ID_PC), .RST(1'b0), .Run(Run), .CLK(CLK));  // open: PredictJump, PredictJump_2
  Hex_Digit_Display hex_digit_display_8 (.value(LedData[3:0]));  // open: dp
  // Probe on \总周期数 
  // Probe on M_PC[19:0]
  // RiscV_Probe riscv_probe_4: pin names not known; wires that end beside it: MEM_IR
  Comparator #(.width(32), .mode("twosComplement")) comparator_1 (
    .a(R1), .b(32'h22), .eq(comparator_1_eq));  // open: gt, lt
  // Probe on \总周期数 
  // Probe on \无条件分支数 
  // Probe on \条件分支成功数 
  // Probe on \插入气泡数 
  // Probe on \LoadUse次数 
  assign bit_extender_1_out = {{20{ID_IR[31]}}, ID_IR[31:20]};  // Bit_Extender bit_extender_1
  assign bit_extender_2_out = {{20{ID_IR[31]}}, {ID_IR[31:25], ID_IR[11:7]}};  // Bit_Extender bit_extender_2
  assign bit_extender_3_out = {{20{ID_IR[31]}}, {ID_IR[31], ID_IR[7], ID_IR[30:25], ID_IR[11:8]}};  // Bit_Extender bit_extender_3
  assign bit_extender_4_out = {{12{ID_IR[31]}}, {ID_IR[31], ID_IR[19:12], ID_IR[20], ID_IR[30:21]}};  // Bit_Extender bit_extender_4
  and and_1 (and_1_out, ecall, comparator_1_eq);
  and and_2 (and_2_out, ecall, ~comparator_1_eq);  // AND_Gate
  // Probe on IF_PC[11:0]
  // Probe on WB_PC[19:0]
  // RiscV_Probe riscv_probe_5: pin names not known; wires that end beside it: WB_IR
  \单周期硬布线控制器  \u_单周期硬布线控制器_1  (
    .Funct({ID_IR[30], ID_IR[25], ID_IR[14:12]}), .OP(ID_IR[6:2]), .ALU_OP(\单周期硬布线控制器_1_alu_op ),
    .MemToReg(\单周期硬布线控制器_1_memtoreg ), .MemWrite(\单周期硬布线控制器_1_memwrite ), .ALU_SRC(\单周期硬布线控制器_1_alu_src ),
    .RegWrite(\单周期硬布线控制器_1_regwrite ), .ecall(ecall), .S_type(S_type), .Jalr(JALR), .Beq(Beq), .JAL(JAL),
    .Bne(Bne), .IR21(ID_IR[21]), .uret(URET), .SB(SB), .BGE(BGE));  // open: r1_used, r2_used, CSRRSI, CSRRCI
  Multiplexer #(.select(1), .width(5), .disabled("Z"), .enable("false")) multiplexer_1 (
    .in0(ID_IR[19:15]), .in1(5'b10001), .out(multiplexer_1_out), .sel(ecall));
  Multiplexer #(.select(1), .width(5), .disabled("Z"), .enable("false")) multiplexer_2 (
    .in0(ID_IR[24:20]), .in1(5'b01010), .out(multiplexer_2_out), .sel(ecall));
  Multiplexer #(.select(1), .width(32), .disabled("Z"), .enable("false")) multiplexer_3 (
    .in0(bit_extender_1_out), .in1(bit_extender_2_out), .out(multiplexer_3_out), .sel(S_type));
  Register #(.width(32), .trigger("rising"), .Select("low")) register_1 (
    .D(R2), .en(and_1_out), .Q(LedData), .clk(CLK), .clr(RST));
  // Probe on ID_PC[11:0]
  // Probe on EX_PC[11:0]
  not not_3 (not_3_out, CLK);
  Regifile \u_寄存器堆  (
    .Din(RDin), .Clk(not_3_out), .R1(R1), .R2(R2), .WE(RegWrite), .W_num(W_num), .R1_num(multiplexer_1_out),
    .R2_num(multiplexer_2_out));
  // Probe on M_PC[11:0]
  D_Flip_Flop #(.trigger("high"), .Pre_Clr_Positions("LEGACY"), .NegatePresetClear("false"), .enable("true"), .NewFFLayout("false")) d_ff_1 (.Q(d_ff_1_q));  // open: clk, D, Qn, preset, en, reset
  // Probe on 13'hc
  \ID_EX流水寄存器  \id_ex流水寄存器_1  (
    .RegWrite(\单周期硬布线控制器_1_regwrite ), .MemToReg(\单周期硬布线控制器_1_memtoreg ), .MemWrite(\单周期硬布线控制器_1_memwrite ),
    .AluOP(\单周期硬布线控制器_1_alu_op ), .AluSrc(\单周期硬布线控制器_1_alu_src ), .RegWrite_2(\id_ex流水寄存器_1_regwrite_2 ),
    .MemToReg_2(\id_ex流水寄存器_1_memtoreg_2 ), .MemWrite_2(\id_ex流水寄存器_1_memwrite_2 ), .AluOP_2(AluOP),
    .AluSrc_2(AluSrcB), .Run(Run), .CLK(CLK), .\指令字_IR (ID_IR), .PC(ID_PC), .RST(1'b0), .\指令字_IR_2 (EX_IR),
    .PC_2(EX_PC), .SignImm(multiplexer_3_out), .SignImm_2(\id_ex流水寄存器_1_signimm_2 ),
    .WriteReg_num(ID_IR[11:7]), .WriteReg_num_2(\id_ex流水寄存器_1_writereg_num_2 ), .B_Imm12(bit_extender_3_out),
    .U_Imm20(bit_extender_4_out), .R1(R1), .R2(R2), .R1_2(\id_ex流水寄存器_1_r1_2 ), .R2_2(\id_ex流水寄存器_1_r2_2 ),
    .halt(and_2_out), .halt_2(\id_ex流水寄存器_1_halt_2 ));  // open: B_Imm12_2, U_Imm20_2, Jal, Jalr, Sb, Bge, Jal_2, Jalr_2, Sb_2, Bge_2, Beq, Bne, Beq_2, Bne_2, R1Foward, R1Foward_2, R2Foward, R2Foward_2, ecall, ecall_2, PredictJump, PredictJump_2, uret, uret_2
  // Probe on WB_PC[11:0]
  Comparator #(.width(13), .mode("twosComplement")) comparator_2 (
    .a(CNT_num), .b(13'hc), .eq(comparator_2_eq), .lt(comparator_2_lt));  // open: gt
  Clock #(.highDuration(1), .lowDuration(1)) clock_2 (.out(clock_2_out));
  nand nand_1 (nand_1_out, d_ff_1_q, comparator_2_eq);
  Counter #(.width(13), .max('h1fff), .ongoal("stay"), .trigger("rising"), .behavior("old")) counter_2 (
    .count(comparator_2_lt), .Q(CNT_num), .clk(clock_2_out));  // open: load, D, carry, clr, preset
  assign CLK = nand_1_out ? clock_2_out : 1'bz;  // Controlled_Buffer controlled_buffer_1
  Multiplexer #(.select(1), .width(32), .disabled("Z"), .enable("false")) multiplexer_4 (
    .in0(\id_ex流水寄存器_1_r2_2 ), .in1(\id_ex流水寄存器_1_signimm_2 ), .out(multiplexer_4_out), .sel(AluSrcB));
  Pull_Resistor #(.pull(1)) pull_resistor_1 (.node(CLK));
  ALU alu_1 (
    .X(\id_ex流水寄存器_1_r1_2 ), .Y(multiplexer_4_out), .AluOP(AluOP), .Result(alu_1_result));  // open: Equal, Result_2, out_4, out_6
  \EX_MEM流水寄存器  \ex_mem流水寄存器_1  (
    .MemToReg(\id_ex流水寄存器_1_memtoreg_2 ), .MemWrite(\id_ex流水寄存器_1_memwrite_2 ),
    .RegWrite(\id_ex流水寄存器_1_regwrite_2 ), .AluResult(alu_1_result), .WriteData(\id_ex流水寄存器_1_r2_2 ),
    .W_num(\id_ex流水寄存器_1_writereg_num_2 ), .IR(EX_IR), .PC(EX_PC), .MemToReg_2(\ex_mem流水寄存器_1_memtoreg_2 ),
    .MemWrite_2(MemWrite), .RegWrite_2(\ex_mem流水寄存器_1_regwrite_2 ),
    .AluResult_2(\ex_mem流水寄存器_1_aluresult_2 ), .WriteData_2(MDin), .W_num_2(\ex_mem流水寄存器_1_w_num_2 ),
    .IR_2(MEM_IR), .PC_2(M_PC), .RST(RST), .Run(Run), .CLK(CLK), .halt(\id_ex流水寄存器_1_halt_2 ),
    .halt_2(\ex_mem流水寄存器_1_halt_2 ));  // open: Jal, Jalr, Sb, Jal_2, Jalr_2, Sb_2, uret, uret_2
  RAM #(.addrWidth(10), .dataWidth(32), .bus("separate"), .Select("high")) ram_1 (
    .addr(\ex_mem流水寄存器_1_aluresult_2 [11:2]), .din(MDin), .data(ram_1_data), .str(MemWrite), .clk(CLK),
    .clr(RST));  // open: sel, ld
  \MEM_WB流水寄存器  \mem_wb流水寄存器_1  (
    .MemToReg(\ex_mem流水寄存器_1_memtoreg_2 ), .RegWrite(\ex_mem流水寄存器_1_regwrite_2 ),
    .AluResult(\ex_mem流水寄存器_1_aluresult_2 ), .RD(ram_1_data), .W_num(\ex_mem流水寄存器_1_w_num_2 ), .IR(MEM_IR),
    .PC(M_PC), .MemToReg_2(MemToReg), .RegWrite_2(RegWrite), .AluResult_2(\mem_wb流水寄存器_1_aluresult_2 ),
    .RD_2(\mem_wb流水寄存器_1_rd_2 ), .W_num_2(W_num), .IR_2(WB_IR), .PC_2(WB_PC), .RST(RST), .Run(Run),
    .CLK(CLK), .halt(\ex_mem流水寄存器_1_halt_2 ), .halt_2(halt));  // open: Jal, Jalr, Jal_2, Jalr_2, uret, uret_2
  Multiplexer #(.select(1), .width(32), .disabled("Z"), .enable("false")) multiplexer_5 (
    .in0(\mem_wb流水寄存器_1_aluresult_2 ), .in1(\mem_wb流水寄存器_1_rd_2 ), .out(RDin), .sel(MemToReg));

  // Other names for the same wires on the sheet: MEM_PC[31:0] = M_PC

  // Notes on the sheet:
  //   中断源
  //   时空图监测，可删除
  //   中断等待指示
  //   IF段
  //   数码管输出
  //   contents of 指令存储器 (hex, n*v repeats v):
  //   413 493 913 993 46413 14e493 296913 39e993 842023 942223 1242423 1342623 a00893 493 913 993 73
  //   指令字
  //   IR
  //   PC
  //   rs
  //   rt
  //   W#
  //   JAL
  //   JALR
  //   URET
  //   SB
  //   BGE
  //   OP
  //   Funct
  //   ID段
  //   Beq
  //   Bne
  //   MemToReg
  //   MemWrite
  //   AluOP
  //   AluSrcB
  //   RegWrite
  //   S_type
  //   控制位
  //   流水调试日志用
  //   暂停节拍，不能为0
  //   戳工具置1进入计数暂停模式，ctrl+k时钟自动运行到对应节拍暂停
  //   ctrl+k关闭时钟连续运行，将控制位置零，进入单步调试模式调试
  //   用这个时钟源需要去掉电路中的其他时钟源
  //   MemToReg
  //   MemWrite
  //   AluOP
  //   AluSrcB
  //   RegWrite
  //   R1
  //   R2
  //   SignImm
  //   W#
  //   halt
  //   IR
  //   PC
  //   可计数暂停的时钟源
  //   EX段
  //   为方便自动评测，需要输出流水线各段保存的PC值，注意是PC不是PC+4，另外ID段寄存器写入信息，Mem段内存写入信息也要输出
  //   MemToReg
  //   MemWrite
  //   RegWrite
  //   ALUResult
  //   W#
  //   halt
  //   IR
  //   PC
  //   MEM段
  //   数据存储器
  //   halt
  //   IR
  //   PC
  //   WB段
endmodule

module \气泡流水线  (
  output RegWrite,
  output MemWrite,
  output [31:0] IF_PC,
  output [31:0] ID_PC,
  output [31:0] EX_PC,
  output [31:0] M_PC,
  output [31:0] WB_PC,
  output [31:0] RDin,
  output [31:0] MDin,
  output [31:0] LedData
);

  wire ALU, ALU_t, AluSrcB, and_1_out, and_2_out, and_3_out, and_4_out, and_5_out, and_6_out, and_7_out,
       B_JMP, Beq, Bge, Bne, Branch, CLK, clock_1_out, clock_2_out, comparator_1_eq, comparator_2_eq,
       comparator_2_lt, d_ff_1_q, DataHazzard, ecall, \ex_mem流水寄存器_1_halt_2 , \ex_mem流水寄存器_1_jal_2 ,
       \ex_mem流水寄存器_1_jalr_2 , \ex_mem流水寄存器_1_memtoreg_2 , \ex_mem流水寄存器_1_regwrite_2 , \ex_mem流水寄存器_1_sb_2 ,
       EX_RegWrite, Go, halt, \id_ex流水寄存器_1_halt_2 , \id_ex流水寄存器_1_memtoreg_2 , \id_ex流水寄存器_1_memwrite_2 ,
       \id_ex流水寄存器_1_sb_2 , ID_S_type, IR1, IR2, IR3, JAL, JALR, \mem_wb流水寄存器_1_jal_2 ,
       \mem_wb流水寄存器_1_jalr_2 , MemToReg, nand_1_out, not_1_out, not_2_out, not_3_out, not_4_out, not_5_out,
       not_6_out, or_1_out, RST, Run, URET, W1, W2, W3, \单周期硬布线控制器_1_alu_src , \单周期硬布线控制器_1_beq ,
       \单周期硬布线控制器_1_bge , \单周期硬布线控制器_1_bne , \单周期硬布线控制器_1_jal , \单周期硬布线控制器_1_jalr , \单周期硬布线控制器_1_memtoreg ,
       \单周期硬布线控制器_1_memwrite , \单周期硬布线控制器_1_r1_used , \单周期硬布线控制器_1_r2_used , \单周期硬布线控制器_1_regwrite ,
       \单周期硬布线控制器_1_sb , \气泡相关处理逻辑_1_flush ;
  wire [1:0] or_4_out;
  wire [1:1] or_8_out;
  wire [3:0] AluOP, \单周期硬布线控制器_1_alu_op ;
  wire [4:0] EX_W_num, MEM_W_num, multiplexer_8_out, R1_num, R2_num, W_num;
  wire [12:0] CNT_num;
  wire [15:0] \LoadUse次数 , \总周期数 , \插入气泡数 , \无条件分支数 , \条件分支成功数 ;
  wire [31:0] adder_2_out, alu_1_result, ALUResult, and_9_out, bit_extender_1_out, bit_extender_2_out,
       bit_extender_3_out, bit_extender_4_out, bit_extender_5_out, BRANCH_PC, EX_IR,
       \id_ex流水寄存器_1_b_imm12_2 , \id_ex流水寄存器_1_r1_2 , \id_ex流水寄存器_1_r2_2 , \id_ex流水寄存器_1_signimm_2 ,
       \id_ex流水寄存器_1_u_imm20_2 , ID_IR, IF_IR, JAL_PC, JALR_PC, MEM_IR, \mem_wb流水寄存器_1_aluresult_2 ,
       \mem_wb流水寄存器_1_rd_2 , MemOut, multiplexer_1_out, multiplexer_4_out, multiplexer_5_out,
       multiplexer_7_out, PC_4, R1, R2, R2_MEM, SB_rst, shifter_1_out, shifter_2_out, shifter_3_out, WB_IR,
       WB_PC_4;

  Button \u_总复位  (.out(RST));
  Button _1 (.out(IR1));
  Button _2 (.out(IR2));
  Button _3 (.out(IR3));
  // Probe on \总周期数 
  // Probe on \总周期数 
  not not_1 (not_1_out, halt);
  Counter #(.width(16), .max('hffff), .ongoal("wrap"), .trigger("rising"), .behavior("new")) counter_1 (
    .count(not_1_out), .Q(\无条件分支数 ), .clk(or_1_out), .clr(RST));  // open: load, D, carry, preset, down
  or or_1 (or_1_out, JAL, JALR);
  Counter #(.width(16), .max('hffff), .ongoal("wrap"), .trigger("rising"), .behavior("new")) counter_2 (
    .count(not_1_out), .Q(\条件分支成功数 ), .clk(B_JMP), .clr(RST));  // open: load, D, carry, preset, down
  Counter #(.width(16), .max('hffff), .ongoal("wrap"), .trigger("rising"), .behavior("new")) counter_3 (
    .count(not_1_out), .Q(\插入气泡数 ), .clk(DataHazzard), .clr(RST));  // open: load, D, carry, preset, down
  Button \u_继续运行  (.out(Go));
  LED #(.active("true")) led_1 (.in(W1));
  LED #(.active("true")) led_2 (.in(W2));
  LED #(.active("true")) led_3 (.in(W3));
  Hex_Digit_Display hex_digit_display_1 (.value(LedData[31:28]));  // open: dp
  // Probe on IF_PC[19:0]
  // RiscV_Probe riscv_probe_1: pin names not known; wires that end beside it: IF_IR
  or or_2 (Run, Go, not_2_out);
  not not_2 (not_2_out, halt);
  not not_3 (not_3_out, halt);
  Counter #(.width(16), .max('hffff), .ongoal("wrap"), .trigger("rising"), .behavior("new")) counter_4 (
    .count(not_3_out), .Q(\总周期数 ), .clk(CLK), .clr(RST));  // open: load, D, carry, preset, down
  Hex_Digit_Display hex_digit_display_2 (.value(LedData[23:20]));  // open: dp
  Hex_Digit_Display hex_digit_display_3 (.value(LedData[27:24]));  // open: dp
  // Probe on ID_PC[19:0]
  // RiscV_Probe riscv_probe_2: pin names not known; wires that end beside it: ID_IR
  \气泡相关处理逻辑  \u_气泡相关处理逻辑_1  (
    .BranchTaken(Branch), .IR(ID_IR), .ecall(ecall), .R1Used(\单周期硬布线控制器_1_r1_used ),
    .EX_RegWrite(EX_RegWrite), .EX_rd(EX_W_num), .R2Used(\单周期硬布线控制器_1_r2_used ),
    .MEM_RegWrite(\ex_mem流水寄存器_1_regwrite_2 ), .MEM_rd(MEM_W_num), .Stall(DataHazzard),
    .Flush(\气泡相关处理逻辑_1_flush ));
  or or_3 (or_4_out[1], JAL, JALR);
  or or_4 (or_4_out[0], JALR, B_JMP);
  Multiplexer #(.select(2), .width(32), .disabled("Z"), .enable("false")) multiplexer_1 (
    .in0(PC_4), .in1(BRANCH_PC), .in2(JAL_PC), .in3(JALR_PC), .out(multiplexer_1_out), .sel(or_4_out));
  Hex_Digit_Display hex_digit_display_4 (.value(LedData[15:12]));  // open: dp
  Hex_Digit_Display hex_digit_display_5 (.value(LedData[19:16]));  // open: dp
  not not_4 (not_4_out, DataHazzard);
  and and_1 (and_1_out, Run, not_4_out);
  Register #(.width(32), .trigger("rising"), .Select("low")) PC (
    .D(multiplexer_1_out), .en(and_1_out), .Q(IF_PC), .clk(CLK), .clr(RST));
  Hex_Digit_Display hex_digit_display_6 (.value(LedData[7:4]));  // open: dp
  Hex_Digit_Display hex_digit_display_7 (.value(LedData[11:8]));  // open: dp
  Clock #(.highDuration(1), .lowDuration(1)) clock_1 (.out(clock_1_out));
  // Probe on EX_PC[19:0]
  // RiscV_Probe riscv_probe_3: pin names not known; wires that end beside it: clock_1_out, EX_IR, CLK
  Hex_Digit_Display hex_digit_display_8 (.value(LedData[3:0]));  // open: dp
  Adder #(.width(32)) adder_1 (.a(IF_PC), .b(32'h4), .out(PC_4));  // open: cin, cout
  // Probe on \总周期数 
  // Probe on M_PC[19:0]
  // RiscV_Probe riscv_probe_4: pin names not known; wires that end beside it: MEM_IR
  ROM #(.addrWidth(10), .dataWidth(32), .Select("high")) \u_指令存储器  (.addr(IF_PC[11:2]), .data(IF_IR));
  // Probe on \总周期数 
  // Probe on \无条件分支数 
  // Probe on \条件分支成功数 
  // Probe on \插入气泡数 
  // Probe on \LoadUse次数 
  \IF_ID流水寄存器  \if_id流水寄存器_1  (
    .\指令字_IR (IF_IR), .PC(IF_PC), .\指令字_IR_2 (ID_IR), .PC_2(ID_PC), .RST(Branch), .Run(and_2_out), .CLK(CLK));  // open: PredictJump, PredictJump_2
  and and_2 (and_2_out, Run, not_5_out);
  not not_5 (not_5_out, DataHazzard);
  // Probe on IF_PC[11:0]
  // Probe on WB_PC[19:0]
  // RiscV_Probe riscv_probe_5: pin names not known; wires that end beside it: WB_IR
  // Probe on ID_PC[11:0]
  // Probe on EX_PC[11:0]
  Comparator #(.width(32), .mode("twosComplement")) comparator_1 (
    .a(R1), .b(32'h22), .eq(comparator_1_eq));  // open: gt, lt
  // Probe on M_PC[11:0]
  D_Flip_Flop #(.trigger("high"), .Pre_Clr_Positions("LEGACY"), .NegatePresetClear("false"), .enable("true"), .NewFFLayout("false")) d_ff_1 (.Q(d_ff_1_q));  // open: clk, D, Qn, preset, en, reset
  // Probe on 13'hc
  \单周期硬布线控制器  \u_单周期硬布线控制器_1  (
    .Funct({ID_IR[30], ID_IR[25], ID_IR[14:12]}), .OP(ID_IR[6:2]), .ALU_OP(\单周期硬布线控制器_1_alu_op ),
    .MemToReg(\单周期硬布线控制器_1_memtoreg ), .MemWrite(\单周期硬布线控制器_1_memwrite ), .ALU_SRC(\单周期硬布线控制器_1_alu_src ),
    .RegWrite(\单周期硬布线控制器_1_regwrite ), .ecall(ecall), .S_type(ID_S_type), .Jalr(\单周期硬布线控制器_1_jalr ),
    .Beq(\单周期硬布线控制器_1_beq ), .JAL(\单周期硬布线控制器_1_jal ), .Bne(\单周期硬布线控制器_1_bne ), .IR21(ID_IR[21]), .uret(URET),
    .SB(\单周期硬布线控制器_1_sb ), .BGE(\单周期硬布线控制器_1_bge ), .r1_used(\单周期硬布线控制器_1_r1_used ),
    .r2_used(\单周期硬布线控制器_1_r2_used ));  // open: CSRRSI, CSRRCI
  Multiplexer #(.select(1), .width(5), .disabled("Z"), .enable("false")) multiplexer_2 (
    .in0(ID_IR[19:15]), .in1(5'b10001), .out(R1_num), .sel(ecall));
  Multiplexer #(.select(1), .width(5), .disabled("Z"), .enable("false")) multiplexer_3 (
    .in0(ID_IR[24:20]), .in1(5'b01010), .out(R2_num), .sel(ecall));
  assign bit_extender_1_out = {{20{ID_IR[31]}}, ID_IR[31:20]};  // Bit_Extender bit_extender_1
  assign bit_extender_2_out = {{20{ID_IR[31]}}, {ID_IR[31:25], ID_IR[11:7]}};  // Bit_Extender bit_extender_2
  assign bit_extender_3_out = {{20{ID_IR[31]}}, {ID_IR[31], ID_IR[7], ID_IR[30:25], ID_IR[11:8]}};  // Bit_Extender bit_extender_3
  assign bit_extender_4_out = {{12{ID_IR[31]}}, {ID_IR[31], ID_IR[19:12], ID_IR[20], ID_IR[30:21]}};  // Bit_Extender bit_extender_4
  and and_3 (and_3_out, ecall, comparator_1_eq);
  and and_4 (and_4_out, ecall, ~comparator_1_eq);  // AND_Gate
  // Probe on WB_PC[11:0]
  Comparator #(.width(13), .mode("twosComplement")) comparator_2 (
    .a(CNT_num), .b(13'hc), .eq(comparator_2_eq), .lt(comparator_2_lt));  // open: gt
  Clock #(.highDuration(1), .lowDuration(1)) clock_2 (.out(clock_2_out));
  Multiplexer #(.select(1), .width(32), .disabled("Z"), .enable("false")) multiplexer_4 (
    .in0(bit_extender_1_out), .in1(bit_extender_2_out), .out(multiplexer_4_out), .sel(ID_S_type));
  Register #(.width(32), .trigger("rising"), .Select("low")) register_1 (
    .D(R2), .en(and_3_out), .Q(LedData), .clk(CLK), .clr(RST));
  nand nand_1 (nand_1_out, d_ff_1_q, comparator_2_eq);
  Counter #(.width(13), .max('h1fff), .ongoal("stay"), .trigger("rising"), .behavior("old")) counter_5 (
    .count(comparator_2_lt), .Q(CNT_num), .clk(clock_2_out));  // open: load, D, carry, clr, preset
  not not_6 (not_6_out, CLK);
  Regifile \u_寄存器堆  (
    .Din(RDin), .Clk(not_6_out), .R1(R1), .R2(R2), .WE(RegWrite), .W_num(W_num), .R1_num(R1_num),
    .R2_num(R2_num));
  assign CLK = nand_1_out ? clock_2_out : 1'bz;  // Controlled_Buffer controlled_buffer_1
  \ID_EX流水寄存器  \id_ex流水寄存器_1  (
    .RegWrite(\单周期硬布线控制器_1_regwrite ), .MemToReg(\单周期硬布线控制器_1_memtoreg ), .MemWrite(\单周期硬布线控制器_1_memwrite ),
    .AluOP(\单周期硬布线控制器_1_alu_op ), .AluSrc(\单周期硬布线控制器_1_alu_src ), .RegWrite_2(EX_RegWrite),
    .MemToReg_2(\id_ex流水寄存器_1_memtoreg_2 ), .MemWrite_2(\id_ex流水寄存器_1_memwrite_2 ), .AluOP_2(AluOP),
    .AluSrc_2(AluSrcB), .Run(Run), .CLK(CLK), .\指令字_IR (ID_IR), .PC(ID_PC), .RST(\气泡相关处理逻辑_1_flush ),
    .\指令字_IR_2 (EX_IR), .PC_2(EX_PC), .SignImm(multiplexer_4_out), .SignImm_2(\id_ex流水寄存器_1_signimm_2 ),
    .WriteReg_num(ID_IR[11:7]), .WriteReg_num_2(EX_W_num), .B_Imm12(bit_extender_3_out),
    .U_Imm20(bit_extender_4_out), .B_Imm12_2(\id_ex流水寄存器_1_b_imm12_2 ), .U_Imm20_2(\id_ex流水寄存器_1_u_imm20_2 ),
    .R1(R1), .R2(R2), .R1_2(\id_ex流水寄存器_1_r1_2 ), .R2_2(\id_ex流水寄存器_1_r2_2 ), .halt(and_4_out),
    .halt_2(\id_ex流水寄存器_1_halt_2 ), .Jal(\单周期硬布线控制器_1_jal ), .Jalr(\单周期硬布线控制器_1_jalr ),
    .Sb(\单周期硬布线控制器_1_sb ), .Bge(\单周期硬布线控制器_1_bge ), .Jal_2(JAL), .Jalr_2(JALR), .Sb_2(\id_ex流水寄存器_1_sb_2 ),
    .Bge_2(Bge), .Beq(\单周期硬布线控制器_1_beq ), .Bne(\单周期硬布线控制器_1_bne ), .Beq_2(Beq), .Bne_2(Bne));  // open: R1Foward, R1Foward_2, R2Foward, R2Foward_2, ecall, ecall_2, PredictJump, PredictJump_2, uret, uret_2
  Pull_Resistor #(.pull(1)) pull_resistor_1 (.node(CLK));
  Shifter #(.width(32), .shift("ll")) shifter_1 (.in(\id_ex流水寄存器_1_b_imm12_2 ), .\dist (5'b00001), .out(shifter_1_out));
  Shifter #(.width(32), .shift("ll")) shifter_2 (.in(\id_ex流水寄存器_1_u_imm20_2 ), .\dist (5'b00001), .out(shifter_2_out));
  Adder #(.width(32)) adder_2 (
    .a(\id_ex流水寄存器_1_r1_2 ), .b(\id_ex流水寄存器_1_signimm_2 ), .out(adder_2_out));  // open: cin, cout
  Multiplexer #(.select(1), .width(32), .disabled("Z"), .enable("false")) multiplexer_5 (
    .in0(\id_ex流水寄存器_1_r2_2 ), .in1(\id_ex流水寄存器_1_signimm_2 ), .out(multiplexer_5_out), .sel(AluSrcB));
  and and_5 (and_5_out, Bne, ~ALU);  // AND_Gate
  and and_6 (and_6_out, Beq, ALU);
  and and_7 (and_7_out, Bge, ALU_t);
  ALU alu_1 (
    .X(\id_ex流水寄存器_1_r1_2 ), .Y(multiplexer_5_out), .AluOP(AluOP), .Equal(ALU), .Result(alu_1_result),
    .out_4(ALU_t));  // open: Result_2, out_6
  assign JALR_PC = 32'hfffffffe & adder_2_out;  // AND_Gate and_8, 32 bits wide
  Adder #(.width(32)) adder_3 (.a(EX_PC), .b(shifter_1_out), .out(BRANCH_PC));  // open: cin, cout
  Adder #(.width(32)) adder_4 (.a(EX_PC), .b(shifter_2_out), .out(JAL_PC));  // open: cin, cout
  or or_5 (B_JMP, and_5_out, and_6_out, and_7_out);
  or or_6 (Branch, B_JMP, JAL, JALR);
  \EX_MEM流水寄存器  \ex_mem流水寄存器_1  (
    .MemToReg(\id_ex流水寄存器_1_memtoreg_2 ), .MemWrite(\id_ex流水寄存器_1_memwrite_2 ), .RegWrite(EX_RegWrite),
    .AluResult(alu_1_result), .WriteData(\id_ex流水寄存器_1_r2_2 ), .W_num(EX_W_num), .IR(EX_IR), .PC(EX_PC),
    .MemToReg_2(\ex_mem流水寄存器_1_memtoreg_2 ), .MemWrite_2(MemWrite), .RegWrite_2(\ex_mem流水寄存器_1_regwrite_2 ),
    .AluResult_2(ALUResult), .WriteData_2(R2_MEM), .W_num_2(MEM_W_num), .IR_2(MEM_IR), .PC_2(M_PC),
    .RST(RST), .Run(Run), .CLK(CLK), .halt(\id_ex流水寄存器_1_halt_2 ), .halt_2(\ex_mem流水寄存器_1_halt_2 ),
    .Jal(JAL), .Jalr(JALR), .Sb(\id_ex流水寄存器_1_sb_2 ), .Jal_2(\ex_mem流水寄存器_1_jal_2 ),
    .Jalr_2(\ex_mem流水寄存器_1_jalr_2 ), .Sb_2(\ex_mem流水寄存器_1_sb_2 ));  // open: uret, uret_2
  Multiplexer #(.select(1), .width(32), .disabled("Z"), .enable("false")) multiplexer_6 (
    .in0(R2_MEM), .in1(SB_rst), .out(MDin), .sel(\ex_mem流水寄存器_1_sb_2 ));
  Multiplexer #(.select(2), .width(32), .disabled("Z"), .enable("false")) multiplexer_7 (
    .in0(32'hffffff00), .in1(32'hffff00ff), .in2(32'hff00ffff), .in3(32'hffffff), .out(multiplexer_7_out),
    .sel(ALUResult[1:0]));
  Multiplexer #(.select(2), .width(5), .disabled("Z"), .enable("false")) multiplexer_8 (
    .in0({5{1'b0}}), .in1(5'b01000), .in2(5'b10000), .in3(5'b11000), .out(multiplexer_8_out),
    .sel(ALUResult[1:0]));
  RAM #(.addrWidth(10), .dataWidth(32), .bus("separate"), .Select("high")) ram_1 (
    .addr(ALUResult[11:2]), .din(MDin), .data(MemOut), .str(MemWrite), .clk(CLK), .clr(RST));  // open: sel, ld
  assign and_9_out = MemOut & multiplexer_7_out;  // AND_Gate and_9, 32 bits wide
  assign bit_extender_5_out = {{24{1'b0}}, R2_MEM[7:0]};  // Bit_Extender bit_extender_5
  Shifter #(.width(32), .shift("ll")) shifter_3 (
    .in(bit_extender_5_out), .\dist (multiplexer_8_out), .out(shifter_3_out));
  assign SB_rst = and_9_out | shifter_3_out;  // OR_Gate or_7, 32 bits wide
  \MEM_WB流水寄存器  \mem_wb流水寄存器_1  (
    .MemToReg(\ex_mem流水寄存器_1_memtoreg_2 ), .RegWrite(\ex_mem流水寄存器_1_regwrite_2 ), .AluResult(ALUResult),
    .RD(MemOut), .W_num(MEM_W_num), .IR(MEM_IR), .PC(M_PC), .MemToReg_2(MemToReg), .RegWrite_2(RegWrite),
    .AluResult_2(\mem_wb流水寄存器_1_aluresult_2 ), .RD_2(\mem_wb流水寄存器_1_rd_2 ), .W_num_2(W_num), .IR_2(WB_IR),
    .PC_2(WB_PC), .RST(RST), .Run(Run), .CLK(CLK), .halt(\ex_mem流水寄存器_1_halt_2 ), .halt_2(halt),
    .Jal(\ex_mem流水寄存器_1_jal_2 ), .Jalr(\ex_mem流水寄存器_1_jalr_2 ), .Jal_2(\mem_wb流水寄存器_1_jal_2 ),
    .Jalr_2(\mem_wb流水寄存器_1_jalr_2 ));  // open: uret, uret_2
  or or_8 (or_8_out[1], \mem_wb流水寄存器_1_jal_2 , \mem_wb流水寄存器_1_jalr_2 );
  Multiplexer #(.select(2), .width(32), .disabled("Z"), .enable("false")) multiplexer_9 (
    .in0(\mem_wb流水寄存器_1_aluresult_2 ), .in1(\mem_wb流水寄存器_1_rd_2 ), .in2(WB_PC_4), .out(RDin),
    .sel({or_8_out[1], MemToReg}));  // open: in3
  Adder #(.width(32)) adder_5 (.a(WB_PC), .b(32'h4), .out(WB_PC_4));  // open: cin, cout

  // Other names for the same wires on the sheet: MEM_PC[31:0] = M_PC

  // Notes on the sheet:
  //   中断源
  //   时空图监测，可删除
  //   中断等待指示
  //   数码管输出
  //   IF段
  //   contents of 指令存储器 (hex, n*v repeats v):
  //   100493 100006f 100493 200913 300993 100006f 100493 200913 300993 100006f 100493 200913 300993
  //   100006f 100493 200913 300993 3a8000ef 100413 100493 1f49493 900533 2200893 73 24d493 48463 fedff06f
  //   900533 2200893 73 100493 249493 900533 2200893 73 48463 fedff06f 100493 1f49493 900533 2200893 73
  //   4034d493 900533 2200893 73 4044d493 900533 2200893 73 4044d493 900533 2200893 73 4044d493 900533
  //   2200893 73 4044d493 900533 2200893 73 4044d493 900533 2200893 73 4044d493 900533 2200893 73 4044d493
  //   900533 2200893 73 100413 1f41993 41f9d993 433 c00913 300b13 140413 f47413 800293 100313 499993
  //   89e9b3 1300533 2200893 73 406282b3 fe0294e3 140413 f00f93 1f47433 1c41413 800293 100313 49d993
  //   89e9b3 1300533 2200893 73 406282b3 fe0294e3 1c45413 406b0b33 b0463 f95ff06f 2b3 fff2c293 829293
  //   ff2e293 500533 2200893 73 fff00413 493 84a023 140413 448493 84a023 140413 448493 84a023 140413
  //   448493 84a023 140413 448493 84a023 140413 448493 84a023 140413 448493 84a023 140413 448493 84a023
  //   140413 448493 84a023 140413 448493 84a023 140413 448493 84a023 140413 448493 84a023 140413 448493
  //   84a023 140413 448493 84a023 140413 448493 84a023 140413 448493 84a023 140413 448493 140413 433
  //   3c00493 42983 4aa03 149a2b3 28663 134a023 1442023 ffc48493 fe9412e3 800533 2200893 73 440413 3c00493
  //   fc9416e3 3200893 73 100293 300313 800493 849493 7648493 900533 2200893 73 800e13 5494b3 6494b3
  //   900533 2200893 73 fffe0e13 fe0e14e3 a00893 73 fff00293 7700493 849493 7748493 900533 2200893 73
  //   1000e13 54c4b3 900533 2200893 73 fffe0e13 fe0e16e3 a00893 73 313 2000e13 493 100913 930023 900533
  //   2200893 73 12484b3 130313 fffe0e13 fe0e12e3 800e13 313 32483 900533 2200893 73 430313 fffe0e13
  //   fe0e14e3 a00893 73 f00493 900533 2200893 73 fff48493 fe04d8e3 a00893 73 a00893 73 413 140413 800533
  //   2200893 73 240413 800533 2200893 73 340413 800533 2200893 73 440413 800533 2200893 73 540413 800533
  //   2200893 73 640413 800533 2200893 73 740413 800533 2200893 73 840413 800533 2200893 2200893 73 8067
  //   指令字
  //   IR
  //   PC
  //   控制位
  //   rs
  //   rt
  //   I型指令立即数
  //   S型指令立即数
  //   W#
  //   B型指令立即数
  //   J型指令立即数
  //   流水调试日志用
  //   暂停节拍，不能为0
  //   JAL
  //   Beq
  //   JALR
  //   Bne
  //   URET
  //   SB
  //   BGE
  //   OP
  //   Funct
  //   戳工具置1进入计数暂停模式，ctrl+k时钟自动运行到对应节拍暂停
  //   ctrl+k关闭时钟连续运行，将控制位置零，进入单步调试模式调试
  //   ID段
  //   MemToReg
  //   MemWrite
  //   AluOP
  //   AluSrcB
  //   RegWrite
  //   S_type
  //   可计数暂停的时钟源
  //   Beq
  //   Bne
  //   MemToReg
  //   MemWrite
  //   AluOP
  //   AluSrcB
  //   RegWrite
  //   JAL
  //   JALR
  //   SB
  //   BGE
  //   R1
  //   R2
  //   SignImm
  //   W#
  //   halt
  //   IR
  //   PC
  //   EX段
  //   BranchTaken相关逻辑
  //   为方便自动评测，需要输出流水线各段保存的PC值，注意是PC不是PC+4，另外ID段寄存器写入信息，Mem段内存写入信息也要输出
  //   jalr指令目的地址
  //   beq\bne\bge指令目的地址
  //   jal指令目的地址
  //   MemToReg
  //   MemWrite
  //   RegWrite
  //   JAL
  //   JALR
  //   SB
  //   W#
  //   halt
  //   IR
  //   PC
  //   数据存储器
  //   MEM段
  //   SB指令实现
  //   MemOut
  //   JAL
  //   W#
  //   halt
  //   IR
  //   PC
  //   JALR
  //   ALUResult
  //   MemOut
  //   WB段
  //   WB段PC+4生成
endmodule
module \重定向流水线  (
  output RegWrite,
  output MemWrite,
  output [31:0] IF_PC,
  output [31:0] ID_PC,
  output [31:0] EX_PC,
  output [31:0] M_PC,
  output [31:0] WB_PC,
  output [31:0] RDin,
  output [31:0] MDin,
  output [31:0] LedData
);

  wire ALU, ALU_t, AluSrcB, and_1_out, and_2_out, and_3_out, and_4_out, and_5_out, and_6_out, and_7_out,
       B_JMP, Beq, Bge, Bne, Branch, CLK, clock_1_out, clock_2_out, comparator_1_eq, comparator_2_eq,
       comparator_2_lt, d_ff_1_q, ecall, EX_ecall, EX_MemToReg, \ex_mem流水寄存器_1_halt_2 ,
       \ex_mem流水寄存器_1_jal_2 , \ex_mem流水寄存器_1_jalr_2 , \ex_mem流水寄存器_1_memtoreg_2 , \ex_mem流水寄存器_1_regwrite_2 ,
       \ex_mem流水寄存器_1_sb_2 , EX_RegWrite, Go, halt, \id_ex流水寄存器_1_halt_2 , \id_ex流水寄存器_1_memwrite_2 ,
       \id_ex流水寄存器_1_sb_2 , ID_S_type, IR1, IR2, IR3, JAL, JALR, LoadUse, \mem_wb流水寄存器_1_jal_2 ,
       \mem_wb流水寄存器_1_jalr_2 , MemToReg, nand_1_out, not_1_out, not_2_out, not_3_out, not_4_out, not_5_out,
       not_6_out, not_7_out, not_8_out, not_9_out, or_4_out, or_5_out, or_6_out, RST, Run, URET, W1, W2, W3,
       \单周期硬布线控制器_1_alu_src , \单周期硬布线控制器_1_beq , \单周期硬布线控制器_1_bge , \单周期硬布线控制器_1_bne , \单周期硬布线控制器_1_jal ,
       \单周期硬布线控制器_1_jalr , \单周期硬布线控制器_1_memtoreg , \单周期硬布线控制器_1_memwrite , \单周期硬布线控制器_1_r1_used ,
       \单周期硬布线控制器_1_r2_used , \单周期硬布线控制器_1_regwrite , \单周期硬布线控制器_1_sb , \重定向相关处理逻辑_1_flush ;
  wire [1:0] \id_ex流水寄存器_1_r1foward_2 , \id_ex流水寄存器_1_r2foward_2 , or_3_out, \重定向相关处理逻辑_1_r1foward ,
       \重定向相关处理逻辑_1_r2foward ;
  wire [1:1] or_10_out;
  wire [3:0] AluOP, \单周期硬布线控制器_1_alu_op ;
  wire [4:0] EX_W_num, MEM_W_num, multiplexer_10_out, R1_num, R2_num, W_num;
  wire [12:0] CNT_num;
  wire [15:0] \LoadUse次数 , \总周期数 , \插入气泡数 , \无条件分支数 , \条件分支成功数 ;
  wire [31:0] adder_2_out, alu_1_result, and_9_out, bit_extender_1_out, bit_extender_2_out,
       bit_extender_3_out, bit_extender_4_out, bit_extender_5_out, BRANCH_PC, EX_IR,
       \id_ex流水寄存器_1_b_imm12_2 , \id_ex流水寄存器_1_r1_2 , \id_ex流水寄存器_1_r2_2 , \id_ex流水寄存器_1_signimm_2 ,
       \id_ex流水寄存器_1_u_imm20_2 , ID_IR, IF_IR, JAL_PC, JALR_PC, MEM_ALUResult, MEM_IR,
       \mem_wb流水寄存器_1_aluresult_2 , \mem_wb流水寄存器_1_rd_2 , MemOut, multiplexer_1_out, multiplexer_4_out,
       multiplexer_7_out, multiplexer_9_out, PC_4, R1, R2, R2_MEM, regifile_1_r1, regifile_1_r2, SB_rst,
       shifter_1_out, shifter_2_out, shifter_3_out, WB_IR, WB_PC_4;

  Button \u_总复位  (.out(RST));
  Button _1 (.out(IR1));
  Button _2 (.out(IR2));
  Button _3 (.out(IR3));
  // Probe on \总周期数 
  // Probe on \总周期数 
  Button \u_继续运行  (.out(Go));
  LED #(.active("true")) led_1 (.in(W1));
  LED #(.active("true")) led_2 (.in(W2));
  LED #(.active("true")) led_3 (.in(W3));
  Hex_Digit_Display hex_digit_display_1 (.value(LedData[31:28]));  // open: dp
  // Probe on IF_PC[19:0]
  // RiscV_Probe riscv_probe_1: pin names not known; wires that end beside it: IF_IR
  or or_1 (Run, Go, not_1_out);
  not not_1 (not_1_out, halt);
  not not_2 (not_2_out, halt);
  Counter #(.width(16), .max('hffff), .ongoal("wrap"), .trigger("rising"), .behavior("new")) counter_1 (
    .count(not_2_out), .Q(\总周期数 ), .clk(CLK), .clr(RST));  // open: load, D, carry, preset, down
  Hex_Digit_Display hex_digit_display_2 (.value(LedData[27:24]));  // open: dp
  Hex_Digit_Display hex_digit_display_3 (.value(LedData[23:20]));  // open: dp
  // Probe on ID_PC[19:0]
  // RiscV_Probe riscv_probe_2: pin names not known; wires that end beside it: ID_IR
  \重定向相关处理逻辑  \u_重定向相关处理逻辑_1  (
    .BranchTaken(Branch), .IR(ID_IR), .ecall(ecall), .EX_MemRead(EX_MemToReg),
    .R1Used(\单周期硬布线控制器_1_r1_used ), .EX_RegWrite(EX_RegWrite), .EX_rd(EX_W_num),
    .R2Used(\单周期硬布线控制器_1_r2_used ), .MEM_RegWrite(\ex_mem流水寄存器_1_regwrite_2 ), .MEM_rd(MEM_W_num),
    .Stall(LoadUse), .Flush(\重定向相关处理逻辑_1_flush ), .R1Foward(\重定向相关处理逻辑_1_r1foward ),
    .R2Foward(\重定向相关处理逻辑_1_r2foward ));
  or or_2 (or_3_out[1], JAL, JALR);
  or or_3 (or_3_out[0], JALR, B_JMP);
  Multiplexer #(.select(2), .width(32), .disabled("Z"), .enable("false")) multiplexer_1 (
    .in0(PC_4), .in1(BRANCH_PC), .in2(JAL_PC), .in3(JALR_PC), .out(multiplexer_1_out), .sel(or_3_out));
  Hex_Digit_Display hex_digit_display_4 (.value(LedData[15:12]));  // open: dp
  Hex_Digit_Display hex_digit_display_5 (.value(LedData[19:16]));  // open: dp
  not not_3 (not_3_out, LoadUse);
  and and_1 (and_1_out, Run, not_3_out);
  Register #(.width(32), .trigger("rising"), .Select("low")) PC (
    .D(multiplexer_1_out), .en(and_1_out), .Q(IF_PC), .clk(CLK), .clr(RST));
  Hex_Digit_Display hex_digit_display_6 (.value(LedData[7:4]));  // open: dp
  Hex_Digit_Display hex_digit_display_7 (.value(LedData[11:8]));  // open: dp
  Clock #(.highDuration(1), .lowDuration(1)) clock_1 (.out(clock_1_out));
  // Probe on EX_PC[19:0]
  // RiscV_Probe riscv_probe_3: pin names not known; wires that end beside it: clock_1_out, EX_IR, CLK
  Hex_Digit_Display hex_digit_display_8 (.value(LedData[3:0]));  // open: dp
  Adder #(.width(32)) adder_1 (.a(IF_PC), .b(32'h4), .out(PC_4));  // open: cin, cout
  // Probe on \总周期数 
  // Probe on M_PC[19:0]
  // RiscV_Probe riscv_probe_4: pin names not known; wires that end beside it: MEM_IR
  ROM #(.addrWidth(10), .dataWidth(32), .Select("high")) \u_指令存储器  (.addr(IF_PC[11:2]), .data(IF_IR));
  // Probe on \总周期数 
  // Probe on \无条件分支数 
  // Probe on \条件分支成功数 
  // Probe on \插入气泡数 
  // Probe on \LoadUse次数 
  or or_4 (or_4_out, Branch, RST);
  \IF_ID流水寄存器  \if_id流水寄存器_1  (
    .\指令字_IR (IF_IR), .PC(IF_PC), .\指令字_IR_2 (ID_IR), .PC_2(ID_PC), .RST(or_4_out), .Run(and_2_out), .CLK(CLK));  // open: PredictJump, PredictJump_2
  and and_2 (and_2_out, Run, not_4_out);
  not not_4 (not_4_out, LoadUse);
  // Probe on IF_PC[11:0]
  // Probe on WB_PC[19:0]
  // RiscV_Probe riscv_probe_5: pin names not known; wires that end beside it: WB_IR
  // Probe on ID_PC[11:0]
  // Probe on EX_PC[11:0]
  Comparator #(.width(32), .mode("twosComplement")) comparator_1 (
    .a(R1), .b(32'h22), .eq(comparator_1_eq));  // open: gt, lt
  // Probe on M_PC[11:0]
  D_Flip_Flop #(.trigger("high"), .Pre_Clr_Positions("LEGACY"), .NegatePresetClear("false"), .enable("true"), .NewFFLayout("false")) d_ff_1 (.Q(d_ff_1_q));  // open: clk, D, Qn, preset, en, reset
  // Probe on 13'hc
  \单周期硬布线控制器  \u_单周期硬布线控制器_1  (
    .Funct({ID_IR[30], ID_IR[25], ID_IR[14:12]}), .OP(ID_IR[6:2]), .ALU_OP(\单周期硬布线控制器_1_alu_op ),
    .MemToReg(\单周期硬布线控制器_1_memtoreg ), .MemWrite(\单周期硬布线控制器_1_memwrite ), .ALU_SRC(\单周期硬布线控制器_1_alu_src ),
    .RegWrite(\单周期硬布线控制器_1_regwrite ), .ecall(ecall), .S_type(ID_S_type), .Jalr(\单周期硬布线控制器_1_jalr ),
    .Beq(\单周期硬布线控制器_1_beq ), .JAL(\单周期硬布线控制器_1_jal ), .Bne(\单周期硬布线控制器_1_bne ), .IR21(ID_IR[21]), .uret(URET),
    .SB(\单周期硬布线控制器_1_sb ), .BGE(\单周期硬布线控制器_1_bge ), .r1_used(\单周期硬布线控制器_1_r1_used ),
    .r2_used(\单周期硬布线控制器_1_r2_used ));  // open: CSRRSI, CSRRCI
  Multiplexer #(.select(1), .width(5), .disabled("Z"), .enable("false")) multiplexer_2 (
    .in0(ID_IR[19:15]), .in1(5'b10001), .out(R1_num), .sel(ecall));
  Multiplexer #(.select(1), .width(5), .disabled("Z"), .enable("false")) multiplexer_3 (
    .in0(ID_IR[24:20]), .in1(5'b01010), .out(R2_num), .sel(ecall));
  assign bit_extender_1_out = {{20{ID_IR[31]}}, ID_IR[31:20]};  // Bit_Extender bit_extender_1
  assign bit_extender_2_out = {{20{ID_IR[31]}}, {ID_IR[31:25], ID_IR[11:7]}};  // Bit_Extender bit_extender_2
  assign bit_extender_3_out = {{20{ID_IR[31]}}, {ID_IR[31], ID_IR[7], ID_IR[30:25], ID_IR[11:8]}};  // Bit_Extender bit_extender_3
  assign bit_extender_4_out = {{12{ID_IR[31]}}, {ID_IR[31], ID_IR[19:12], ID_IR[20], ID_IR[30:21]}};  // Bit_Extender bit_extender_4
  and and_3 (and_3_out, EX_ecall, comparator_1_eq);
  and and_4 (and_4_out, EX_ecall, ~comparator_1_eq);  // AND_Gate
  // Probe on WB_PC[11:0]
  Comparator #(.width(13), .mode("twosComplement")) comparator_2 (
    .a(CNT_num), .b(13'hc), .eq(comparator_2_eq), .lt(comparator_2_lt));  // open: gt
  Clock #(.highDuration(1), .lowDuration(1)) clock_2 (.out(clock_2_out));
  not not_5 (not_5_out, CLK);
  Regifile regifile_1 (
    .Din(RDin), .Clk(not_5_out), .R1(regifile_1_r1), .R2(regifile_1_r2), .WE(RegWrite), .W_num(W_num),
    .R1_num(R1_num), .R2_num(R2_num));
  Multiplexer #(.select(1), .width(32), .disabled("Z"), .enable("false")) multiplexer_4 (
    .in0(bit_extender_1_out), .in1(bit_extender_2_out), .out(multiplexer_4_out), .sel(ID_S_type));
  Register #(.width(32), .trigger("rising"), .Select("low")) register_1 (
    .D(R2), .en(and_3_out), .Q(LedData), .clk(CLK), .clr(RST));
  nand nand_1 (nand_1_out, d_ff_1_q, comparator_2_eq);
  Counter #(.width(13), .max('h1fff), .ongoal("stay"), .trigger("rising"), .behavior("old")) counter_2 (
    .count(comparator_2_lt), .Q(CNT_num), .clk(clock_2_out));  // open: load, D, carry, clr, preset
  assign CLK = nand_1_out ? clock_2_out : 1'bz;  // Controlled_Buffer controlled_buffer_1
  or or_5 (or_5_out, \重定向相关处理逻辑_1_flush , RST);
  \ID_EX流水寄存器  \id_ex流水寄存器_1  (
    .RegWrite(\单周期硬布线控制器_1_regwrite ), .MemToReg(\单周期硬布线控制器_1_memtoreg ), .MemWrite(\单周期硬布线控制器_1_memwrite ),
    .AluOP(\单周期硬布线控制器_1_alu_op ), .AluSrc(\单周期硬布线控制器_1_alu_src ), .RegWrite_2(EX_RegWrite),
    .MemToReg_2(EX_MemToReg), .MemWrite_2(\id_ex流水寄存器_1_memwrite_2 ), .AluOP_2(AluOP), .AluSrc_2(AluSrcB),
    .Run(Run), .CLK(CLK), .\指令字_IR (ID_IR), .PC(ID_PC), .RST(or_5_out), .\指令字_IR_2 (EX_IR), .PC_2(EX_PC),
    .SignImm(multiplexer_4_out), .SignImm_2(\id_ex流水寄存器_1_signimm_2 ), .WriteReg_num(ID_IR[11:7]),
    .WriteReg_num_2(EX_W_num), .B_Imm12(bit_extender_3_out), .U_Imm20(bit_extender_4_out),
    .B_Imm12_2(\id_ex流水寄存器_1_b_imm12_2 ), .U_Imm20_2(\id_ex流水寄存器_1_u_imm20_2 ), .R1(regifile_1_r1),
    .R2(regifile_1_r2), .R1_2(\id_ex流水寄存器_1_r1_2 ), .R2_2(\id_ex流水寄存器_1_r2_2 ), .halt(and_4_out),
    .halt_2(\id_ex流水寄存器_1_halt_2 ), .Jal(\单周期硬布线控制器_1_jal ), .Jalr(\单周期硬布线控制器_1_jalr ),
    .Sb(\单周期硬布线控制器_1_sb ), .Bge(\单周期硬布线控制器_1_bge ), .Jal_2(JAL), .Jalr_2(JALR), .Sb_2(\id_ex流水寄存器_1_sb_2 ),
    .Bge_2(Bge), .Beq(\单周期硬布线控制器_1_beq ), .Bne(\单周期硬布线控制器_1_bne ), .Beq_2(Beq), .Bne_2(Bne),
    .R1Foward(\重定向相关处理逻辑_1_r1foward ), .R1Foward_2(\id_ex流水寄存器_1_r1foward_2 ),
    .R2Foward(\重定向相关处理逻辑_1_r2foward ), .R2Foward_2(\id_ex流水寄存器_1_r2foward_2 ), .ecall(ecall),
    .ecall_2(EX_ecall));  // open: PredictJump, PredictJump_2, uret, uret_2
  Pull_Resistor #(.pull(1)) pull_resistor_1 (.node(CLK));
  Shifter #(.width(32), .shift("ll")) shifter_1 (.in(\id_ex流水寄存器_1_b_imm12_2 ), .\dist (5'b00001), .out(shifter_1_out));
  Shifter #(.width(32), .shift("ll")) shifter_2 (.in(\id_ex流水寄存器_1_u_imm20_2 ), .\dist (5'b00001), .out(shifter_2_out));
  not not_6 (not_6_out, halt);
  or or_6 (or_6_out, JAL, JALR);
  Multiplexer #(.select(2), .width(32), .disabled("Z"), .enable("false")) multiplexer_5 (
    .in0(\id_ex流水寄存器_1_r1_2 ), .in1(RDin), .in2(MEM_ALUResult), .out(R1), .sel(\id_ex流水寄存器_1_r1foward_2 ));  // open: in3
  Multiplexer #(.select(2), .width(32), .disabled("Z"), .enable("false")) multiplexer_6 (
    .in0(\id_ex流水寄存器_1_r2_2 ), .in1(RDin), .in2(MEM_ALUResult), .out(R2), .sel(\id_ex流水寄存器_1_r2foward_2 ));  // open: in3
  Counter #(.width(16), .max('hffff), .ongoal("wrap"), .trigger("rising"), .behavior("new")) counter_3 (
    .count(not_6_out), .Q(\无条件分支数 ), .clk(or_6_out), .clr(RST));  // open: load, D, carry, preset, down
  Multiplexer #(.select(1), .width(32), .disabled("Z"), .enable("false")) multiplexer_7 (
    .in0(R2), .in1(\id_ex流水寄存器_1_signimm_2 ), .out(multiplexer_7_out), .sel(AluSrcB));
  Adder #(.width(32)) adder_2 (.a(R1), .b(\id_ex流水寄存器_1_signimm_2 ), .out(adder_2_out));  // open: cin, cout
  and and_5 (and_5_out, Bne, ~ALU);  // AND_Gate
  and and_6 (and_6_out, Beq, ALU);
  and and_7 (and_7_out, Bge, ALU_t);
  ALU alu_1 (
    .X(R1), .Y(multiplexer_7_out), .AluOP(AluOP), .Equal(ALU), .Result(alu_1_result), .out_4(ALU_t));  // open: Result_2, out_6
  Adder #(.width(32)) adder_3 (.a(EX_PC), .b(shifter_1_out), .out(BRANCH_PC));  // open: cin, cout
  Adder #(.width(32)) adder_4 (.a(EX_PC), .b(shifter_2_out), .out(JAL_PC));  // open: cin, cout
  or or_7 (B_JMP, and_5_out, and_6_out, and_7_out);
  not not_7 (not_7_out, halt);
  Counter #(.width(16), .max('hffff), .ongoal("wrap"), .trigger("rising"), .behavior("new")) counter_4 (
    .count(not_7_out), .Q(\条件分支成功数 ), .clk(B_JMP), .clr(RST));  // open: load, D, carry, preset, down
  assign JALR_PC = 32'hfffffffe & adder_2_out;  // AND_Gate and_8, 32 bits wide
  or or_8 (Branch, B_JMP, JAL, JALR);
  \EX_MEM流水寄存器  \ex_mem流水寄存器_1  (
    .MemToReg(EX_MemToReg), .MemWrite(\id_ex流水寄存器_1_memwrite_2 ), .RegWrite(EX_RegWrite),
    .AluResult(alu_1_result), .WriteData(R2), .W_num(EX_W_num), .IR(EX_IR), .PC(EX_PC),
    .MemToReg_2(\ex_mem流水寄存器_1_memtoreg_2 ), .MemWrite_2(MemWrite), .RegWrite_2(\ex_mem流水寄存器_1_regwrite_2 ),
    .AluResult_2(MEM_ALUResult), .WriteData_2(R2_MEM), .W_num_2(MEM_W_num), .IR_2(MEM_IR), .PC_2(M_PC),
    .RST(RST), .Run(Run), .CLK(CLK), .halt(\id_ex流水寄存器_1_halt_2 ), .halt_2(\ex_mem流水寄存器_1_halt_2 ),
    .Jal(JAL), .Jalr(JALR), .Sb(\id_ex流水寄存器_1_sb_2 ), .Jal_2(\ex_mem流水寄存器_1_jal_2 ),
    .Jalr_2(\ex_mem流水寄存器_1_jalr_2 ), .Sb_2(\ex_mem流水寄存器_1_sb_2 ));  // open: uret, uret_2
  not not_8 (not_8_out, halt);
  Counter #(.width(16), .max('hffff), .ongoal("wrap"), .trigger("rising"), .behavior("new")) counter_5 (
    .count(not_8_out), .Q(\插入气泡数 ), .clk(LoadUse), .clr(RST));  // open: load, D, carry, preset, down
  Multiplexer #(.select(1), .width(32), .disabled("Z"), .enable("false")) multiplexer_8 (
    .in0(R2_MEM), .in1(SB_rst), .out(MDin), .sel(\ex_mem流水寄存器_1_sb_2 ));
  Multiplexer #(.select(2), .width(32), .disabled("Z"), .enable("false")) multiplexer_9 (
    .in0(32'hffffff00), .in1(32'hffff00ff), .in2(32'hff00ffff), .in3(32'hffffff), .out(multiplexer_9_out),
    .sel(MEM_ALUResult[1:0]));
  Multiplexer #(.select(2), .width(5), .disabled("Z"), .enable("false")) multiplexer_10 (
    .in0({5{1'b0}}), .in1(5'b01000), .in2(5'b10000), .in3(5'b11000), .out(multiplexer_10_out),
    .sel(MEM_ALUResult[1:0]));
  not not_9 (not_9_out, halt);
  Counter #(.width(16), .max('hffff), .ongoal("wrap"), .trigger("rising"), .behavior("new")) counter_6 (
    .count(not_9_out), .Q(\LoadUse次数 ), .clk(LoadUse), .clr(RST));  // open: load, D, carry, preset, down
  RAM #(.addrWidth(10), .dataWidth(32), .bus("separate"), .Select("high")) ram_1 (
    .addr(MEM_ALUResult[11:2]), .din(MDin), .data(MemOut), .str(MemWrite), .clk(CLK), .clr(RST));  // open: sel, ld
  assign and_9_out = MemOut & multiplexer_9_out;  // AND_Gate and_9, 32 bits wide
  assign bit_extender_5_out = {{24{1'b0}}, R2_MEM[7:0]};  // Bit_Extender bit_extender_5
  Shifter #(.width(32), .shift("ll")) shifter_3 (
    .in(bit_extender_5_out), .\dist (multiplexer_10_out), .out(shifter_3_out));
  assign SB_rst = and_9_out | shifter_3_out;  // OR_Gate or_9, 32 bits wide
  \MEM_WB流水寄存器  \mem_wb流水寄存器_1  (
    .MemToReg(\ex_mem流水寄存器_1_memtoreg_2 ), .RegWrite(\ex_mem流水寄存器_1_regwrite_2 ), .AluResult(MEM_ALUResult),
    .RD(MemOut), .W_num(MEM_W_num), .IR(MEM_IR), .PC(M_PC), .MemToReg_2(MemToReg), .RegWrite_2(RegWrite),
    .AluResult_2(\mem_wb流水寄存器_1_aluresult_2 ), .RD_2(\mem_wb流水寄存器_1_rd_2 ), .W_num_2(W_num), .IR_2(WB_IR),
    .PC_2(WB_PC), .RST(RST), .Run(Run), .CLK(CLK), .halt(\ex_mem流水寄存器_1_halt_2 ), .halt_2(halt),
    .Jal(\ex_mem流水寄存器_1_jal_2 ), .Jalr(\ex_mem流水寄存器_1_jalr_2 ), .Jal_2(\mem_wb流水寄存器_1_jal_2 ),
    .Jalr_2(\mem_wb流水寄存器_1_jalr_2 ));  // open: uret, uret_2
  or or_10 (or_10_out[1], \mem_wb流水寄存器_1_jal_2 , \mem_wb流水寄存器_1_jalr_2 );
  Multiplexer #(.select(2), .width(32), .disabled("Z"), .enable("false")) multiplexer_11 (
    .in0(\mem_wb流水寄存器_1_aluresult_2 ), .in1(\mem_wb流水寄存器_1_rd_2 ), .in2(WB_PC_4), .out(RDin),
    .sel({or_10_out[1], MemToReg}));  // open: in3
  Adder #(.width(32)) adder_5 (.a(WB_PC), .b(32'h4), .out(WB_PC_4));  // open: cin, cout

  // Other names for the same wires on the sheet: MEM_PC[31:0] = M_PC

  // Notes on the sheet:
  //   中断源
  //   时空图监测，可删除
  //   中断等待指示
  //   数码管输出
  //   IF段
  //   contents of 指令存储器 (hex, n*v repeats v):
  //   100493 100006f 100493 200913 300993 100006f 100493 200913 300993 100006f 100493 200913 300993
  //   100006f 100493 200913 300993 3a8000ef 100413 100493 1f49493 900533 2200893 73 24d493 48463 fedff06f
  //   900533 2200893 73 100493 249493 900533 2200893 73 48463 fedff06f 100493 1f49493 900533 2200893 73
  //   4034d493 900533 2200893 73 4044d493 900533 2200893 73 4044d493 900533 2200893 73 4044d493 900533
  //   2200893 73 4044d493 900533 2200893 73 4044d493 900533 2200893 73 4044d493 900533 2200893 73 4044d493
  //   900533 2200893 73 100413 1f41993 41f9d993 433 c00913 300b13 140413 f47413 800293 100313 499993
  //   89e9b3 1300533 2200893 73 406282b3 fe0294e3 140413 f00f93 1f47433 1c41413 800293 100313 49d993
  //   89e9b3 1300533 2200893 73 406282b3 fe0294e3 1c45413 406b0b33 b0463 f95ff06f 2b3 fff2c293 829293
  //   ff2e293 500533 2200893 73 fff00413 493 84a023 140413 448493 84a023 140413 448493 84a023 140413
  //   448493 84a023 140413 448493 84a023 140413 448493 84a023 140413 448493 84a023 140413 448493 84a023
  //   140413 448493 84a023 140413 448493 84a023 140413 448493 84a023 140413 448493 84a023 140413 448493
  //   84a023 140413 448493 84a023 140413 448493 84a023 140413 448493 84a023 140413 448493 140413 433
  //   3c00493 42983 4aa03 149a2b3 28663 134a023 1442023 ffc48493 fe9412e3 800533 2200893 73 440413 3c00493
  //   fc9416e3 3200893 73 100293 300313 800493 849493 7648493 900533 2200893 73 800e13 5494b3 6494b3
  //   900533 2200893 73 fffe0e13 fe0e14e3 a00893 73 fff00293 7700493 849493 7748493 900533 2200893 73
  //   1000e13 54c4b3 900533 2200893 73 fffe0e13 fe0e16e3 a00893 73 313 2000e13 493 100913 930023 900533
  //   2200893 73 12484b3 130313 fffe0e13 fe0e12e3 800e13 313 32483 900533 2200893 73 430313 fffe0e13
  //   fe0e14e3 a00893 73 f00493 900533 2200893 73 fff48493 fe04d8e3 a00893 73 a00893 73 413 140413 800533
  //   2200893 73 240413 800533 2200893 73 340413 800533 2200893 73 440413 800533 2200893 73 540413 800533
  //   2200893 73 640413 800533 2200893 73 740413 800533 2200893 73 840413 800533 2200893 2200893 73 8067
  //   指令字
  //   IR
  //   PC
  //   控制位
  //   rs
  //   rt
  //   I型指令立即数
  //   S型指令立即数
  //   W#
  //   B型指令立即数
  //   J型指令立即数
  //   流水调试日志用
  //   暂停节拍，不能为0
  //   JAL
  //   Beq
  //   JALR
  //   Bne
  //   URET
  //   SB
  //   BGE
  //   OP
  //   Funct
  //   戳工具置1进入计数暂停模式，ctrl+k时钟自动运行到对应节拍暂停
  //   ctrl+k关闭时钟连续运行，将控制位置零，进入单步调试模式调试
  //   ID段
  //   MemToReg
  //   MemWrite
  //   AluOP
  //   AluSrcB
  //   RegWrite
  //   S_type
  //   可计数暂停的时钟源
  //   Beq
  //   Bne
  //   MemToReg
  //   MemWrite
  //   AluOP
  //   AluSrcB
  //   RegWrite
  //   JAL
  //   JALR
  //   SB
  //   BGE
  //   R1
  //   R2
  //   SignImm
  //   W#
  //   halt
  //   IR
  //   PC
  //   EX段
  //   BranchTaken相关逻辑
  //   为方便自动评测，需要输出流水线各段保存的PC值，注意是PC不是PC+4，另外ID段寄存器写入信息，Mem段内存写入信息也要输出
  //   jalr指令目的地址
  //   beq\bne\bge指令目的地址
  //   jal指令目的地址
  //   MemToReg
  //   MemWrite
  //   RegWrite
  //   JAL
  //   JALR
  //   SB
  //   ALUResult
  //   W#
  //   halt
  //   IR
  //   PC
  //   数据存储器
  //   MEM段
  //   SB指令实现
  //   MemOut
  //   JAL
  //   W#
  //   halt
  //   IR
  //   PC
  //   JALR
  //   ALUResult
  //   MemOut
  //   WB段
  //   WB段PC+4生成
endmodule

module \中断按键参考电路  (
  input  \同步清零信号 ,
  output \与中断屏蔽位与 
);

  wire \_1号中断_out , and_1_out, clock_1_out, d_ff_1_q, or_1_out, or_2_out;

  Clock #(.highDuration(1), .lowDuration(1)) clock_1 (.out(clock_1_out));
  Button \_1号中断  (.out(\_1号中断_out ));
  or or_1 (or_1_out, \与中断屏蔽位与 , d_ff_1_q);
  LED #(.active("true")) \_1号中断等待指示灯  (.in(or_1_out));
  D_Flip_Flop #(.trigger("rising"), .Pre_Clr_Positions("LEGACY"), .NegatePresetClear("false"), .enable("true"), .NewFFLayout("false")) d_ff_1 (
    .clk(\_1号中断_out ), .D(1'b1), .Q(d_ff_1_q), .reset(\与中断屏蔽位与 ));  // open: Qn, preset, en
  or or_2 (or_2_out, d_ff_1_q, \与中断屏蔽位与 );
  and and_1 (and_1_out, or_2_out, ~\同步清零信号 );  // AND_Gate
  D_Flip_Flop #(.trigger("rising"), .Pre_Clr_Positions("LEGACY"), .NegatePresetClear("false"), .enable("true"), .NewFFLayout("false")) IR1 (
    .clk(clock_1_out), .D(and_1_out), .Q(\与中断屏蔽位与 ));  // open: Qn, preset, en, reset

  // Notes on the sheet:
  //   中断信号采样参考电路
  //   Reset 
endmodule

module \单周期_单级中断  (
  input  IR1,
  input  IR2,
  input  IR3,
  output RegWrite,
  output MemWrite,
  output [31:0] PC,
  output [31:0] IR,
  output [31:0] RDin,
  output [31:0] MDin,
  output [31:0] LedData
);

  wire _1_out, _2_out, _3_out, alu_1_equal, alu_1_out_4, AluSrcB, and_1_out, and_2_out, and_3_out, and_4_out,
       and_6_out, and_7_out, and_9_out, and_10_out, Beq, BGE, Bne, CLK, clock_2_out, CLR1, CLR2, CLR3,
       comparator_1_eq, comparator_2_eq, comparator_3_eq, comparator_4_eq, comparator_5_eq, comparator_5_lt,
       comparator_6_eq, d_ff_1_q, d_ff_2_q, d_ff_3_q, d_ff_5_q, ecall, Go, halt, IE, INT1, INT2, INT3,
       INT_Request, intR, IR1_t, IR2_t, IR3_t, IRA, IRB, IRC, JAL, JALR, JMP, MemToReg, nand_1_out,
       not_1_out, not_2_out, or_3_out, or_8_out, or_9_out, or_10_out, or_13_out, register_1_q, Run, S_type,
       SB, URET, W1, W2, W3;
  wire [0:0] or_1_out;
  wire [1:0] INT_NUM, register_2_q;
  wire [3:0] AluOP;
  wire [4:0] multiplexer_4_out, multiplexer_5_out, multiplexer_10_out;
  wire [12:0] CNT_num;
  wire [15:0] \总周期数 ;
  wire [31:0] adder_2_out, adder_3_out, adder_4_out, and_8_out, and_12_out, bit_extender_1_out,
       bit_extender_2_out, bit_extender_3_out, bit_extender_4_out, bit_extender_5_out, EPCAddr, INTAddr,
       MemOut, multiplexer_1_out, multiplexer_6_out, multiplexer_8_out, multiplexer_9_out, PC_4, PC_q, R1,
       R2, Result, Result2, RETAddr, SB_rst, shifter_1_out, shifter_2_out, shifter_3_out;

  Clock #(.highDuration(1), .lowDuration(1)) clock_1 ();  // open: out
  Button _1 (.out(_1_out));
  Button _2 (.out(_2_out));
  Button _3 (.out(_3_out));
  or or_1 (or_1_out[0], or_13_out, JALR);
  Button \u_继续运行  (.out(Go));
  LED #(.active("true")) led_1 (.in(W1));
  LED #(.active("true")) led_2 (.in(W2));
  LED #(.active("true")) led_3 (.in(W3));
  not not_1 (not_1_out, halt);
  or or_2 (Run, not_1_out, Go);
  // Probe on PC
  Multiplexer #(.select(2), .width(32), .disabled("Z"), .enable("false")) multiplexer_1 (
    .in0(PC_4), .in1(adder_2_out), .in2(adder_3_out), .in3(and_8_out), .out(multiplexer_1_out),
    .sel({JMP, or_1_out[0]}));
  Hex_Digit_Display hex_digit_display_1 (.value(LedData[31:28]));  // open: dp
  Comparator #(.width(16), .mode("twosComplement")) comparator_1 (
    .a(16'h23b), .b(\总周期数 ), .eq(comparator_1_eq));  // open: gt, lt
  Comparator #(.width(16), .mode("twosComplement")) comparator_2 (
    .a(\总周期数 ), .b(16'h1), .eq(comparator_2_eq));  // open: gt, lt
  Comparator #(.width(16), .mode("twosComplement")) comparator_3 (
    .a(\总周期数 ), .b(16'h4), .eq(comparator_3_eq));  // open: gt, lt
  Comparator #(.width(16), .mode("twosComplement")) comparator_4 (
    .a(\总周期数 ), .b(16'h7), .eq(comparator_4_eq));  // open: gt, lt
  // RiscV_Probe riscv_probe_1: pin names not known; wires that end beside it: IR
  Multiplexer #(.select(1), .width(32), .disabled("Z"), .enable("false")) multiplexer_2 (
    .in0(multiplexer_1_out), .in1(EPCAddr), .out(RETAddr), .sel(URET));
  Hex_Digit_Display hex_digit_display_2 (.value(LedData[23:20]));  // open: dp
  Hex_Digit_Display hex_digit_display_3 (.value(LedData[27:24]));  // open: dp
  or or_3 (or_3_out, comparator_1_eq, comparator_2_eq);
  Pull_Resistor #(.pull(0)) pull_resistor_1 (.node(IRA));
  assign IRA = or_3_out ? ~CLK : 1'bz;  // Controlled_Inverter controlled_inverter_1
  Pull_Resistor #(.pull(0)) pull_resistor_2 (.node(IRB));
  assign IRB = comparator_3_eq ? ~CLK : 1'bz;  // Controlled_Inverter controlled_inverter_2
  Pull_Resistor #(.pull(0)) pull_resistor_3 (.node(IRC));
  assign IRC = comparator_4_eq ? ~CLK : 1'bz;  // Controlled_Inverter controlled_inverter_3
  Register #(.width(32), .trigger("rising"), .Select("low")) u_PC (
    .D(RETAddr), .en(Run), .Q(PC_q), .clk(CLK));  // open: clr
  Hex_Digit_Display hex_digit_display_4 (.value(LedData[15:12]));  // open: dp
  Hex_Digit_Display hex_digit_display_5 (.value(LedData[19:16]));  // open: dp
  Register #(.width(1), .trigger("rising"), .Select("low")) register_1 (
    .D(INT_Request), .Q(register_1_q), .clk(CLK));  // open: en, clr
  Hex_Digit_Display hex_digit_display_6 (.value(LedData[7:4]));  // open: dp
  Hex_Digit_Display hex_digit_display_7 (.value(LedData[11:8]));  // open: dp
  // Probe on \总周期数 
  Multiplexer #(.select(1), .width(32), .disabled("Z"), .enable("false")) multiplexer_3 (
    .in0(PC_q), .in1(INTAddr), .out(PC), .sel(register_1_q));
  Hex_Digit_Display hex_digit_display_8 (.value(LedData[3:0]));  // open: dp
  or or_4 (W1, INT1, d_ff_1_q);
  or or_5 (W2, INT2, d_ff_2_q);
  or or_6 (W3, INT3, d_ff_3_q);
  D_Flip_Flop #(.trigger("rising"), .Pre_Clr_Positions("LEGACY"), .NegatePresetClear("false"), .enable("true"), .NewFFLayout("false")) d_ff_1 (
    .clk(IRA), .D(1'b1), .Q(d_ff_1_q), .reset(INT1));  // open: Qn, preset, en
  D_Flip_Flop #(.trigger("rising"), .Pre_Clr_Positions("LEGACY"), .NegatePresetClear("false"), .enable("true"), .NewFFLayout("false")) d_ff_2 (
    .clk(IRB), .D(1'b1), .Q(d_ff_2_q), .reset(INT2));  // open: Qn, preset, en
  D_Flip_Flop #(.trigger("rising"), .Pre_Clr_Positions("LEGACY"), .NegatePresetClear("false"), .enable("true"), .NewFFLayout("false")) d_ff_3 (
    .clk(IRC), .D(1'b1), .Q(d_ff_3_q), .reset(INT3));  // open: Qn, preset, en
  Adder #(.width(32)) adder_1 (.a(PC), .b(32'h4), .out(PC_4));  // open: cin, cout
  or or_7 (IR1_t, IR1, IRA);
  or or_8 (or_8_out, d_ff_1_q, INT1);
  or or_9 (or_9_out, d_ff_2_q, INT2);
  or or_10 (or_10_out, d_ff_3_q, INT3);
  // RiscV_Probe riscv_probe_2: pin names not known; wires that end beside it: IR
  ROM #(.addrWidth(10), .dataWidth(32), .Select("high")) Instruction_Memory (.addr(PC[11:2]), .data(IR));
  or or_11 (IR2_t, IR2, IRB);
  and and_1 (and_1_out, or_8_out, ~CLR1);  // AND_Gate
  and and_2 (and_2_out, or_9_out, ~CLR2);  // AND_Gate
  and and_3 (and_3_out, or_10_out, ~CLR3);  // AND_Gate
  D_Flip_Flop #(.trigger("rising"), .Pre_Clr_Positions("LEGACY"), .NegatePresetClear("false"), .enable("true"), .NewFFLayout("false")) \u_中断请求寄存器IR  (
    .clk(CLK), .D(and_1_out), .Q(INT1));  // open: Qn, preset, en, reset
  D_Flip_Flop #(.trigger("rising"), .Pre_Clr_Positions("LEGACY"), .NegatePresetClear("false"), .enable("true"), .NewFFLayout("false")) \u_中断请求寄存器IR_2  (
    .clk(CLK), .D(and_2_out), .Q(INT2));  // open: Qn, preset, en, reset
  D_Flip_Flop #(.trigger("rising"), .Pre_Clr_Positions("LEGACY"), .NegatePresetClear("false"), .enable("true"), .NewFFLayout("false")) \u_中断请求寄存器IR_3  (
    .clk(CLK), .D(and_3_out), .Q(INT3));  // open: Qn, preset, en, reset
  \单周期硬布线控制器  \u_单周期硬布线控制器_1  (
    .Funct({IR[30], IR[25], IR[14:12]}), .OP(IR[6:2]), .ALU_OP(AluOP), .MemToReg(MemToReg),
    .MemWrite(MemWrite), .ALU_SRC(AluSrcB), .RegWrite(RegWrite), .ecall(ecall), .S_type(S_type), .Jalr(JALR),
    .Beq(Beq), .JAL(JAL), .Bne(Bne), .IR21(IR[21]), .uret(URET), .SB(SB), .BGE(BGE));  // open: r1_used, r2_used, CSRRSI, CSRRCI
  or or_12 (IR3_t, IR3, IRC);
  assign bit_extender_1_out = {{20{IR[31]}}, {IR[31], IR[7], IR[30:25], IR[11:8]}};  // Bit_Extender bit_extender_1
  assign bit_extender_2_out = {{12{IR[31]}}, {IR[31], IR[19:12], IR[20], IR[30:21]}};  // Bit_Extender bit_extender_2
  Shifter #(.width(32), .shift("ll")) shifter_1 (.in(bit_extender_1_out), .\dist (5'b00001), .out(shifter_1_out));
  Shifter #(.width(32), .shift("ll")) shifter_2 (.in(bit_extender_2_out), .\dist (5'b00001), .out(shifter_2_out));
  Priority_Encoder #(.select(2), .disabled("Z")) priority_encoder_1 (
    .in0(INT1), .in1(INT2), .in2(INT3), .out(INT_NUM), .gs(intR));  // open: in3, en_out, en_in
  and and_4 (and_4_out, intR, ~URET);  // AND_Gate
  // Probe on INT_NUM
  Register #(.width(2), .trigger("rising"), .Select("low")) register_2 (
    .D(INT_NUM), .en(INT_Request), .Q(register_2_q), .clk(CLK));  // open: clr
  Register #(.width(32), .trigger("rising"), .Select("low")) \EPC寄存器  (
    .D(RETAddr), .en(INT_Request), .Q(EPCAddr), .clk(CLK));  // open: clr
  Multiplexer #(.select(1), .width(5), .disabled("Z"), .enable("false")) multiplexer_4 (
    .in0(IR[19:15]), .in1(5'b10001), .out(multiplexer_4_out), .sel(ecall));
  Multiplexer #(.select(1), .width(5), .disabled("Z"), .enable("false")) multiplexer_5 (
    .in0(IR[24:20]), .in1(5'b01010), .out(multiplexer_5_out), .sel(ecall));
  assign bit_extender_3_out = {{20{IR[31]}}, IR[31:20]};  // Bit_Extender bit_extender_3
  assign bit_extender_4_out = {{20{IR[31]}}, {IR[31:25], IR[11:7]}};  // Bit_Extender bit_extender_4
  D_Flip_Flop #(.trigger("rising"), .Pre_Clr_Positions("LEGACY"), .NegatePresetClear("false"), .enable("true"), .NewFFLayout("false")) d_ff_4 (
    .clk(CLK), .D(and_4_out), .Qn(IE));  // open: Q, preset, en, reset
  // Probe on register_2_q
  Demultiplexer #(.select(2), .width(1), .tristate("false"), .disabled("Z"), .enable("false")) demultiplexer_1 (
    .out0(CLR1), .out1(CLR2), .out2(CLR3), .in(URET), .sel(register_2_q));  // open: out3
  // Probe on R1
  and and_5 (INT_Request, IE, intR);
  Regifile \u_寄存器堆  (
    .Din(RDin), .Clk(CLK), .R1(R1), .R2(R2), .WE(RegWrite), .W_num(IR[11:7]), .R1_num(multiplexer_4_out),
    .R2_num(multiplexer_5_out));
  Multiplexer #(.select(1), .width(32), .disabled("Z"), .enable("false")) multiplexer_6 (
    .in0(bit_extender_3_out), .in1(bit_extender_4_out), .out(multiplexer_6_out), .sel(S_type));
  Adder #(.width(32)) adder_2 (.a(shifter_1_out), .b(PC), .out(adder_2_out));  // open: cin, cout
  Adder #(.width(32)) adder_3 (.a(shifter_2_out), .b(PC), .out(adder_3_out));  // open: cin, cout
  Multiplexer #(.select(2), .width(32), .disabled("Z"), .enable("false")) multiplexer_7 (
    .in0(32'h30ac), .in1(32'h3150), .in2(32'h31f4), .out(INTAddr), .sel(INT_NUM));  // open: in3
  or or_13 (or_13_out, and_9_out, and_6_out, and_7_out);
  // Probe on R2
  Multiplexer #(.select(1), .width(32), .disabled("Z"), .enable("false")) multiplexer_8 (
    .in0(R2), .in1(multiplexer_6_out), .out(multiplexer_8_out), .sel(AluSrcB));
  and and_6 (and_6_out, Beq, alu_1_equal);
  and and_7 (and_7_out, Bne, ~alu_1_equal);  // AND_Gate
  ALU alu_1 (
    .X(R1), .Y(multiplexer_8_out), .AluOP(AluOP), .Equal(alu_1_equal), .Result(Result), .Result_2(Result2),
    .out_4(alu_1_out_4));  // open: out_6
  Adder #(.width(32)) adder_4 (.a(multiplexer_6_out), .b(R1), .out(adder_4_out));  // open: cin, cout
  assign and_8_out = adder_4_out & 32'hfffffffe;  // AND_Gate and_8, 32 bits wide
  D_Flip_Flop #(.trigger("high"), .Pre_Clr_Positions("LEGACY"), .NegatePresetClear("false"), .enable("true"), .NewFFLayout("false")) d_ff_5 (.Q(d_ff_5_q));  // open: clk, D, Qn, preset, en, reset
  // Probe on 13'hf0
  and and_9 (and_9_out, BGE, alu_1_out_4);
  Comparator #(.width(13), .mode("twosComplement")) comparator_5 (
    .a(CNT_num), .b(13'hf0), .eq(comparator_5_eq), .lt(comparator_5_lt));  // open: gt
  Clock #(.highDuration(1), .lowDuration(1)) clock_2 (.out(clock_2_out));
  Multiplexer #(.select(2), .width(32), .disabled("Z"), .enable("false")) multiplexer_9 (
    .in0(32'hffffff00), .in1(32'hffff00ff), .in2(32'hff00ffff), .in3(32'hffffff), .out(multiplexer_9_out),
    .sel(Result[1:0]));
  Multiplexer #(.select(2), .width(5), .disabled("Z"), .enable("false")) multiplexer_10 (
    .in0({5{1'b0}}), .in1(5'b01000), .in2(5'b10000), .in3(5'b11000), .out(multiplexer_10_out),
    .sel(Result[1:0]));
  Counter #(.width(13), .max('h1fff), .ongoal("stay"), .trigger("rising"), .behavior("old")) counter_1 (
    .count(comparator_5_lt), .Q(CNT_num), .clk(clock_2_out));  // open: load, D, carry, clr, preset
  or or_14 (JMP, JAL, JALR);
  Comparator #(.width(32), .mode("twosComplement")) comparator_6 (
    .a(R1), .b(32'ha), .eq(comparator_6_eq));  // open: gt, lt
  nand nand_1 (nand_1_out, d_ff_5_q, comparator_5_eq);
  and and_10 (and_10_out, ecall, ~comparator_6_eq);  // AND_Gate
  and and_11 (halt, ecall, comparator_6_eq);
  Multiplexer #(.select(1), .width(32), .disabled("Z"), .enable("false")) multiplexer_11 (
    .in0(R2), .in1(SB_rst), .out(MDin), .sel(SB));
  assign and_12_out = multiplexer_9_out & MemOut;  // AND_Gate and_12, 32 bits wide
  assign bit_extender_5_out = {{24{1'b0}}, R2[7:0]};  // Bit_Extender bit_extender_5
  assign CLK = nand_1_out ? clock_2_out : 1'bz;  // Controlled_Buffer controlled_buffer_1
  Pull_Resistor #(.pull(1)) pull_resistor_4 (.node(CLK));
  Shifter #(.width(32), .shift("ll")) shifter_3 (
    .in(bit_extender_5_out), .\dist (multiplexer_10_out), .out(shifter_3_out));
  Register #(.width(32), .trigger("rising"), .Select("low")) register_3 (
    .D(R2), .en(and_10_out), .Q(LedData), .clk(CLK));  // open: clr
  RAM #(.addrWidth(10), .dataWidth(32), .bus("separate"), .Select("high")) ram_1 (
    .addr(Result[11:2]), .din(MDin), .data(MemOut), .str(MemWrite), .clk(CLK));  // open: sel, ld, clr
  assign SB_rst = and_12_out | shifter_3_out;  // OR_Gate or_15, 32 bits wide
  not not_2 (not_2_out, halt);
  Counter #(.width(16), .max('hffff), .ongoal("wrap"), .trigger("rising"), .behavior("new")) counter_2 (
    .count(not_2_out), .Q(\总周期数 ), .clk(CLK));  // open: load, D, carry, clr, preset, down
  Multiplexer #(.select(2), .width(32), .disabled("Z"), .enable("false")) multiplexer_12 (
    .in0(Result), .in1(MemOut), .in2(PC_4), .out(RDin), .sel({JMP, MemToReg}));  // open: in3

  // Notes on the sheet:
  //   中断源
  //   中断等待指示
  //   总复位信号应将除ROM以外所有存储组件全部清零
  //   单级中断测试信号模拟器
  //   数码管输出
  //   数码管输出应该用寄存器锁存，否则显示数据只能一闪而过
  //   指令探针
  //   指令存储器
  //   指令字
  //   contents of Instruction_Memory (hex, n*v repeats v):
  //   7d000113 100413 1f41993 41f9d993 433 c00913 800b13 140413 f47413 800293 100313 499993 89e9b3 1300533
  //   2200893 73 406282b3 fe0294e3 140413 f00f93 1f47433 1c41413 800293 100313 49d993 89e9b3 1300533
  //   2200893 73 406282b3 fe0294e3 1c45413 406b0b33 b0463 f95ff06f 2b3 fff2c293 1029293 fff2e293 500533
  //   2200893 73 f5dff06f 1112023 410113 a12023 410113 812023 410113 1312023 410113 1412023 410113 1512023
  //   410113 1612023 410113 100b13 300a13 100a93 1600433 441413 14469b3 1300533 2200893 73 fe0416e3
  //   415a0a33 fe0a10e3 ffc10113 12b03 ffc10113 12a83 ffc10113 12a03 ffc10113 12983 ffc10113 12403
  //   ffc10113 12503 ffc10113 12883 200073 1112023 410113 a12023 410113 812023 410113 1312023 410113
  //   1412023 410113 1512023 410113 1612023 410113 200b13 300a13 100a93 1600433 441413 14469b3 1300533
  //   2200893 73 fe0416e3 415a0a33 fe0a10e3 ffc10113 12b03 ffc10113 12a83 ffc10113 12a03 ffc10113 12983
  //   ffc10113 12403 ffc10113 12503 ffc10113 12883 200073 1112023 410113 a12023 410113 812023 410113
  //   1312023 410113 1412023 410113 1512023 410113 1612023 410113 300b13 300a13 100a93 1600433 441413
  //   14469b3 1300533 2200893 73 fe0416e3 415a0a33 fe0a10e3 ffc10113 12b03 ffc10113 12a83 ffc10113 12a03
  //   ffc10113 12983 ffc10113 12403 ffc10113 12503 ffc10113 12883 200073
  //   Reset 
  //   Reset 
  //   Reset 
  //   JAL
  //   JALR
  //   URET
  //   Beq
  //   Bne
  //   AluOP
  //   AluSrcB
  //   RegWrite
  //   S_type
  //   MemToReg
  //   MemWrite
  //   beq\bne指令目的地址
  //   jal指令目的地址
  //   为方便自动评测，需要输出PC，IR，寄存器堆写如数据RDin
  //   RAM写使能MemWrite、RAM写入数据MDin等信号
  //   中断请求
  //   计算出地址的最低有效位设为0
  //   jalr指令目的地址
  //   中断地址
  //   控制位
  //   暂停节拍，不能为0
  //   戳工具置1进入计数暂停模式，ctrl+k时钟自动运行到对应节拍暂停
  //   ctrl+k关闭时钟连续运行，将控制位置零，进入单步调试模式调试
  //   用这个时钟源需要去掉电路中的其他时钟源
  //   可计数暂停的时钟源
  //   数据存储器
endmodule

module \单周期_多级中断  (
  input  IR1,
  input  IR2,
  input  IR3,
  output RegWrite,
  output MemWrite,
  output [31:0] PC,
  output [31:0] IR,
  output [31:0] RDin,
  output [31:0] MDin,
  output [31:0] LedData
);

  wire alu_1_equal, alu_1_out_4, AluSrcB, and_1_out, and_2_out, and_3_out, and_4_out, and_5_out, and_6_out,
       and_8_out, Beq, BGE, Bne, CLK, clock_1_out, clock_2_out, CLR1, CLR2, CLR3, comparator_1_eq,
       comparator_2_eq, comparator_3_eq, comparator_4_eq, comparator_5_eq, comparator_6_eq, comparator_6_lt,
       comparator_7_eq, comparator_8_eq, CSRRCI, CSRRSI, d_ff_1_q, d_ff_2_q, d_ff_3_q, d_ff_4_q,
       decoder_1_out0, decoder_1_out1, decoder_1_out2, decoder_2_out1, decoder_2_out2, decoder_2_out3, ecall,
       Go, halt, IE, INT, INT1, INT2, INT3, INT_NUM_CUR, INT_Request, INT_Select, IR1_t, IR2_t, IR3_t, IRA,
       IRB, IRC, JAL, JALR, JMP, MemToReg, nand_1_out, nor_1_out, not_1_out, not_2_out, not_4_out, not_5_out,
       or_3_out, or_4_out, or_10_out, or_11_out, or_12_out, or_14_out, or_15_out, or_16_out, register_3_q,
       register_5_q, register_6_q, register_7_q, Run, S_type, SB, URET, W1, W2, W3;
  wire [0:0] or_1_out;
  wire [1:0] counter_1_q, INT_NUM, INT_OLD_q, multiplexer_12_out;
  wire [3:0] AluOP;
  wire [4:0] multiplexer_4_out, multiplexer_5_out, multiplexer_11_out;
  wire [12:0] CNT_num;
  wire [15:0] \总周期数 ;
  wire [31:0] adder_2_out, adder_3_out, adder_4_out, and_7_out, and_10_out, bit_extender_1_out,
       bit_extender_2_out, bit_extender_3_out, bit_extender_4_out, bit_extender_5_out, EPCAddr, \EPC寄存器_2_q ,
       \EPC寄存器_3_q , \EPC寄存器_q , INTAddr, MemOut, multiplexer_1_out, multiplexer_6_out, multiplexer_7_out,
       multiplexer_10_out, PC_4, PC_q, R1, R2, Result, Result2, RETAddr, SB_rst, shifter_1_out,
       shifter_2_out, shifter_3_out;

  Clock #(.highDuration(1), .lowDuration(1)) clock_1 (.out(clock_1_out));
  Button _1 ();  // open: out
  Button _2 ();  // open: out
  Button _3 ();  // open: out
  Button \u_继续运行  (.out(Go));
  LED #(.active("true")) led_1 (.in(W1));
  LED #(.active("true")) led_2 (.in(W2));
  LED #(.active("true")) led_3 (.in(W3));
  or or_1 (or_1_out[0], or_16_out, JALR);
  Hex_Digit_Display hex_digit_display_1 (.value(LedData[31:28]));  // open: dp
  Comparator #(.width(16), .mode("twosComplement")) comparator_1 (
    .a(\总周期数 ), .b(16'h7), .eq(comparator_1_eq));  // open: gt, lt
  Comparator #(.width(16), .mode("twosComplement")) comparator_2 (
    .a(\总周期数 ), .b(16'h241), .eq(comparator_2_eq));  // open: gt, lt
  not not_1 (not_1_out, halt);
  or or_2 (Run, not_1_out, Go);
  // Probe on PC
  Multiplexer #(.select(2), .width(32), .disabled("Z"), .enable("false")) multiplexer_1 (
    .in0(PC_4), .in1(adder_2_out), .in2(adder_3_out), .in3(and_7_out), .out(multiplexer_1_out),
    .sel({JMP, or_1_out[0]}));
  Multiplexer #(.select(1), .width(32), .disabled("Z"), .enable("false")) multiplexer_2 (
    .in0(multiplexer_1_out), .in1(EPCAddr), .out(RETAddr), .sel(URET));
  Hex_Digit_Display hex_digit_display_2 (.value(LedData[23:20]));  // open: dp
  Hex_Digit_Display hex_digit_display_3 (.value(LedData[27:24]));  // open: dp
  Comparator #(.width(16), .mode("twosComplement")) comparator_3 (
    .a(16'h258), .b(\总周期数 ), .eq(comparator_3_eq));  // open: gt, lt
  or or_3 (or_3_out, comparator_3_eq, comparator_4_eq);
  Comparator #(.width(16), .mode("twosComplement")) comparator_4 (
    .a(\总周期数 ), .b(16'h1), .eq(comparator_4_eq));  // open: gt, lt
  Comparator #(.width(16), .mode("twosComplement")) comparator_5 (
    .a(\总周期数 ), .b(16'h4), .eq(comparator_5_eq));  // open: gt, lt
  or or_4 (or_4_out, comparator_1_eq, comparator_2_eq);
  // RiscV_Probe riscv_probe_1: pin names not known; wires that end beside it: IR
  Hex_Digit_Display hex_digit_display_4 (.value(LedData[19:16]));  // open: dp
  Hex_Digit_Display hex_digit_display_5 (.value(LedData[15:12]));  // open: dp
  Pull_Resistor #(.pull(0)) pull_resistor_1 (.node(IRA));
  assign IRA = or_3_out ? ~CLK : 1'bz;  // Controlled_Inverter controlled_inverter_1
  Pull_Resistor #(.pull(0)) pull_resistor_2 (.node(IRB));
  assign IRB = comparator_5_eq ? ~CLK : 1'bz;  // Controlled_Inverter controlled_inverter_2
  Pull_Resistor #(.pull(0)) pull_resistor_3 (.node(IRC));
  assign IRC = or_4_out ? ~CLK : 1'bz;  // Controlled_Inverter controlled_inverter_3
  Register #(.width(32), .trigger("rising"), .Select("low")) u_PC (
    .D(RETAddr), .en(Run), .Q(PC_q), .clk(CLK));  // open: clr
  Hex_Digit_Display hex_digit_display_6 (.value(LedData[11:8]));  // open: dp
  Hex_Digit_Display hex_digit_display_7 (.value(LedData[7:4]));  // open: dp
  // Probe on \总周期数 
  Register #(.width(1), .trigger("rising"), .Select("low")) register_1 (
    .D(INT_Request), .Q(INT_Select), .clk(CLK));  // open: en, clr
  Multiplexer #(.select(1), .width(32), .disabled("Z"), .enable("false")) multiplexer_3 (
    .in0(PC_q), .in1(INTAddr), .out(PC), .sel(INT_Select));
  Hex_Digit_Display hex_digit_display_8 (.value(LedData[3:0]));  // open: dp
  or or_5 (W1, INT1, d_ff_1_q);
  or or_6 (W2, INT2, d_ff_2_q);
  or or_7 (W3, INT3, d_ff_3_q);
  or or_8 (IR1_t, IR1, IRA);
  D_Flip_Flop #(.trigger("rising"), .Pre_Clr_Positions("LEGACY"), .NegatePresetClear("false"), .enable("true"), .NewFFLayout("false")) d_ff_1 (
    .clk(IRA), .D(1'b1), .Q(d_ff_1_q), .reset(INT1));  // open: Qn, preset, en
  D_Flip_Flop #(.trigger("rising"), .Pre_Clr_Positions("LEGACY"), .NegatePresetClear("false"), .enable("true"), .NewFFLayout("false")) d_ff_2 (
    .clk(IRB), .D(1'b1), .Q(d_ff_2_q), .reset(INT2));  // open: Qn, preset, en
  D_Flip_Flop #(.trigger("rising"), .Pre_Clr_Positions("LEGACY"), .NegatePresetClear("false"), .enable("true"), .NewFFLayout("false")) d_ff_3 (
    .clk(IRC), .D(1'b1), .Q(d_ff_3_q), .reset(INT3));  // open: Qn, preset, en
  // RiscV_Probe riscv_probe_2: pin names not known; wires that end beside it: IR
  Adder #(.width(32)) adder_1 (.a(PC), .b(32'h4), .out(PC_4));  // open: cin, cout
  or or_9 (IR2_t, IR2, IRB);
  or or_10 (or_10_out, d_ff_1_q, INT1);
  and and_1 (and_1_out, or_10_out, ~CLR1);  // AND_Gate
  or or_11 (or_11_out, d_ff_2_q, INT2);
  and and_2 (and_2_out, or_11_out, ~CLR2);  // AND_Gate
  or or_12 (or_12_out, d_ff_3_q, INT3);
  and and_3 (and_3_out, or_12_out, ~CLR3);  // AND_Gate
  ROM #(.addrWidth(10), .dataWidth(32), .Select("high")) Instruction_Memory (.addr(PC[11:2]), .data(IR));
  D_Flip_Flop #(.trigger("rising"), .Pre_Clr_Positions("LEGACY"), .NegatePresetClear("false"), .enable("true"), .NewFFLayout("false")) \u_中断请求寄存器IR  (
    .clk(CLK), .D(and_1_out), .Q(INT1));  // open: Qn, preset, en, reset
  D_Flip_Flop #(.trigger("rising"), .Pre_Clr_Positions("LEGACY"), .NegatePresetClear("false"), .enable("true"), .NewFFLayout("false")) \u_中断请求寄存器IR_2  (
    .clk(CLK), .D(and_2_out), .Q(INT2));  // open: Qn, preset, en, reset
  D_Flip_Flop #(.trigger("rising"), .Pre_Clr_Positions("LEGACY"), .NegatePresetClear("false"), .enable("true"), .NewFFLayout("false")) \u_中断请求寄存器IR_3  (
    .clk(CLK), .D(and_3_out), .Q(INT3));  // open: Qn, preset, en, reset
  or or_13 (IR3_t, IR3, IRC);
  \单周期硬布线控制器  \u_单周期硬布线控制器_1  (
    .Funct({IR[30], IR[25], IR[14:12]}), .OP(IR[6:2]), .ALU_OP(AluOP), .MemToReg(MemToReg),
    .MemWrite(MemWrite), .ALU_SRC(AluSrcB), .RegWrite(RegWrite), .ecall(ecall), .S_type(S_type), .Jalr(JALR),
    .Beq(Beq), .JAL(JAL), .Bne(Bne), .IR21(IR[21]), .uret(URET), .SB(SB), .BGE(BGE), .CSRRSI(CSRRSI),
    .CSRRCI(CSRRCI));  // open: r1_used, r2_used
  assign bit_extender_1_out = {{20{IR[31]}}, {IR[31], IR[7], IR[30:25], IR[11:8]}};  // Bit_Extender bit_extender_1
  assign bit_extender_2_out = {{12{IR[31]}}, {IR[31], IR[19:12], IR[20], IR[30:21]}};  // Bit_Extender bit_extender_2
  Register #(.width(1), .trigger("rising"), .Select("low")) register_2 (
    .D(1'b0), .Q(INT_Request), .clk(CLK), .clr(not_2_out), .preset(INT));  // open: en, cs
  not not_2 (not_2_out, INT);
  Shifter #(.width(32), .shift("ll")) shifter_1 (.in(bit_extender_1_out), .\dist (5'b00001), .out(shifter_1_out));
  Shifter #(.width(32), .shift("ll")) shifter_2 (.in(bit_extender_2_out), .\dist (5'b00001), .out(shifter_2_out));
  or or_14 (or_14_out, INT_Select, CSRRCI);
  nor nor_1 (nor_1_out, URET, CSRRSI);
  or or_15 (or_15_out, INT_Request, URET);
  Multiplexer #(.select(1), .width(5), .disabled("Z"), .enable("false")) multiplexer_4 (
    .in0(IR[19:15]), .in1(5'b10001), .out(multiplexer_4_out), .sel(ecall));
  Multiplexer #(.select(1), .width(5), .disabled("Z"), .enable("false")) multiplexer_5 (
    .in0(IR[24:20]), .in1(5'b01010), .out(multiplexer_5_out), .sel(ecall));
  assign bit_extender_3_out = {{20{IR[31]}}, IR[31:20]};  // Bit_Extender bit_extender_3
  assign bit_extender_4_out = {{20{IR[31]}}, {IR[31:25], IR[11:7]}};  // Bit_Extender bit_extender_4
  not not_3 (IE, register_3_q);
  Register #(.width(1), .trigger("rising"), .Select("low")) register_3 (
    .D(1'b0), .Q(register_3_q), .clk(nor_1_out), .preset(or_14_out));  // open: en, clr, cs
  Counter #(.width(2), .max('h3), .ongoal("wrap"), .trigger("rising"), .behavior("new")) counter_1 (
    .count(or_15_out), .Q(counter_1_q), .clk(CLK), .down(URET));  // open: load, D, carry, clr, preset
  // Probe on R1
  Multiplexer #(.select(1), .width(32), .disabled("Z"), .enable("false")) multiplexer_6 (
    .in0(bit_extender_3_out), .in1(bit_extender_4_out), .out(multiplexer_6_out), .sel(S_type));
  Adder #(.width(32)) adder_2 (.a(shifter_1_out), .b(PC), .out(adder_2_out));  // open: cin, cout
  Adder #(.width(32)) adder_3 (.a(shifter_2_out), .b(PC), .out(adder_3_out));  // open: cin, cout
  Decoder #(.select(2), .tristate("false"), .disabled("Z"), .enable("false")) decoder_1 (
    .out0(decoder_1_out0), .out1(decoder_1_out1), .out2(decoder_1_out2), .sel(counter_1_q));  // open: out3
  Regifile \u_寄存器堆  (
    .Din(RDin), .Clk(CLK), .R1(R1), .R2(R2), .WE(RegWrite), .W_num(IR[11:7]), .R1_num(multiplexer_4_out),
    .R2_num(multiplexer_5_out));
  or or_16 (or_16_out, and_5_out, and_6_out, and_4_out);
  and and_4 (and_4_out, Bne, ~alu_1_equal);  // AND_Gate
  // Probe on R2
  Multiplexer #(.select(1), .width(32), .disabled("Z"), .enable("false")) multiplexer_7 (
    .in0(R2), .in1(multiplexer_6_out), .out(multiplexer_7_out), .sel(AluSrcB));
  Adder #(.width(32)) adder_4 (.a(multiplexer_6_out), .b(R1), .out(adder_4_out));  // open: cin, cout
  D_Flip_Flop #(.trigger("high"), .Pre_Clr_Positions("LEGACY"), .NegatePresetClear("false"), .enable("true"), .NewFFLayout("false")) d_ff_4 (.Q(d_ff_4_q));  // open: clk, D, Qn, preset, en, reset
  // Probe on 13'hf0
  Priority_Encoder #(.select(2), .disabled("Z")) priority_encoder_1 (
    .in0(1'b1), .in1(INT1), .in2(INT2), .in3(INT3), .out(INT_NUM));  // open: gs, en_out, en_in
  Register #(.width(32), .trigger("rising"), .Select("low")) \EPC寄存器  (
    .D(RETAddr), .en(decoder_1_out0), .Q(\EPC寄存器_q ), .clk(CLK));  // open: clr
  Register #(.width(32), .trigger("rising"), .Select("low")) \EPC寄存器_2  (
    .D(RETAddr), .en(decoder_1_out1), .Q(\EPC寄存器_2_q ), .clk(CLK));  // open: clr
  Register #(.width(32), .trigger("rising"), .Select("low")) \EPC寄存器_3  (
    .D(RETAddr), .en(decoder_1_out2), .Q(\EPC寄存器_3_q ), .clk(CLK));  // open: clr
  and and_5 (and_5_out, BGE, alu_1_out_4);
  and and_6 (and_6_out, Beq, alu_1_equal);
  ALU alu_1 (
    .X(R1), .Y(multiplexer_7_out), .AluOP(AluOP), .Equal(alu_1_equal), .Result(Result), .Result_2(Result2),
    .out_4(alu_1_out_4));  // open: out_6
  assign and_7_out = adder_4_out & 32'hfffffffe;  // AND_Gate and_7, 32 bits wide
  Comparator #(.width(13), .mode("twosComplement")) comparator_6 (
    .a(CNT_num), .b(13'hf0), .eq(comparator_6_eq), .lt(comparator_6_lt));  // open: gt
  Clock #(.highDuration(1), .lowDuration(1)) clock_2 (.out(clock_2_out));
  Counter #(.width(13), .max('h1fff), .ongoal("stay"), .trigger("rising"), .behavior("old")) counter_2 (
    .count(comparator_6_lt), .Q(CNT_num), .clk(clock_2_out));  // open: load, D, carry, clr, preset
  Multiplexer #(.select(2), .width(32), .disabled("Z"), .enable("false")) multiplexer_8 (
    .in1(32'h30ac), .in2(32'h3158), .in3(32'h3204), .out(INTAddr), .sel(INT_NUM));  // open: in0
  Multiplexer #(.select(2), .width(32), .disabled("Z"), .enable("false")) multiplexer_9 (
    .in1(\EPC寄存器_q ), .in2(\EPC寄存器_2_q ), .in3(\EPC寄存器_3_q ), .out(EPCAddr), .sel(counter_1_q));  // open: in0
  or or_17 (JMP, JAL, JALR);
  Multiplexer #(.select(2), .width(32), .disabled("Z"), .enable("false")) multiplexer_10 (
    .in0(32'hffffff00), .in1(32'hffff00ff), .in2(32'hff00ffff), .in3(32'hffffff), .out(multiplexer_10_out),
    .sel(Result[1:0]));
  Multiplexer #(.select(2), .width(5), .disabled("Z"), .enable("false")) multiplexer_11 (
    .in0({5{1'b0}}), .in1(5'b01000), .in2(5'b10000), .in3(5'b11000), .out(multiplexer_11_out),
    .sel(Result[1:0]));
  nand nand_1 (nand_1_out, d_ff_4_q, comparator_6_eq);
  Comparator #(.width(32), .mode("twosComplement")) comparator_7 (
    .a(R1), .b(32'ha), .eq(comparator_7_eq));  // open: gt, lt
  assign CLK = nand_1_out ? clock_2_out : 1'bz;  // Controlled_Buffer controlled_buffer_1
  Pull_Resistor #(.pull(1)) pull_resistor_4 (.node(CLK));
  Multiplexer #(.select(1), .width(2), .disabled("Z"), .enable("false")) multiplexer_12 (
    .in0(multiplexer_12_out), .in1(INT_NUM), .out(multiplexer_12_out), .sel(IE));
  and and_8 (and_8_out, ecall, ~comparator_7_eq);  // AND_Gate
  and and_9 (halt, ecall, comparator_7_eq);
  Multiplexer #(.select(1), .width(32), .disabled("Z"), .enable("false")) multiplexer_13 (
    .in0(R2), .in1(SB_rst), .out(MDin), .sel(SB));
  assign and_10_out = multiplexer_10_out & MemOut;  // AND_Gate and_10, 32 bits wide
  assign bit_extender_5_out = {{24{1'b0}}, R2[7:0]};  // Bit_Extender bit_extender_5
  Register #(.width(2), .trigger("rising"), .Select("low")) INT_OLD (
    .D(multiplexer_12_out), .Q(INT_OLD_q), .clk(CLK));  // open: en, clr
  Decoder #(.select(2), .tristate("false"), .disabled("Z"), .enable("false")) decoder_2 (
    .out1(decoder_2_out1), .out2(decoder_2_out2), .out3(decoder_2_out3), .sel(INT_NUM));  // open: out0
  Shifter #(.width(32), .shift("ll")) shifter_3 (
    .in(bit_extender_5_out), .\dist (multiplexer_11_out), .out(shifter_3_out));
  Demultiplexer #(.select(2), .width(1), .tristate("false"), .disabled("Z"), .enable("false")) demultiplexer_1 (
    .out1(CLR1), .out2(CLR2), .out3(CLR3), .in(URET), .sel(INT_OLD_q));  // open: out0
  Register #(.width(32), .trigger("rising"), .Select("low")) register_4 (
    .D(R2), .en(and_8_out), .Q(LedData), .clk(CLK));  // open: clr
  RAM #(.addrWidth(10), .dataWidth(32), .bus("separate"), .Select("high")) ram_1 (
    .addr(Result[11:2]), .din(MDin), .data(MemOut), .str(MemWrite), .clk(CLK));  // open: sel, ld, clr
  assign SB_rst = and_10_out | shifter_3_out;  // OR_Gate or_18, 32 bits wide
  Comparator #(.width(2), .mode("twosComplement")) comparator_8 (
    .a(multiplexer_12_out), .b(INT_OLD_q), .eq(comparator_8_eq));  // open: gt, lt
  not not_4 (not_4_out, comparator_8_eq);
  Register #(.width(1), .trigger("rising"), .Select("low")) register_5 (
    .D(1'b1), .en(decoder_2_out1), .Q(register_5_q), .clk(INT_Select), .clr(CLR1));
  Register #(.width(1), .trigger("rising"), .Select("low")) register_6 (
    .D(1'b1), .en(decoder_2_out2), .Q(register_6_q), .clk(INT_Select), .clr(CLR2));
  Register #(.width(1), .trigger("rising"), .Select("low")) register_7 (
    .D(1'b1), .en(decoder_2_out3), .Q(register_7_q), .clk(INT_Select), .clr(CLR3));
  and and_11 (INT, not_4_out, ~INT_NUM_CUR);  // AND_Gate
  Multiplexer #(.select(2), .width(1), .disabled("Z"), .enable("false")) multiplexer_14 (
    .in0(1'b1), .in1(register_5_q), .in2(register_6_q), .in3(register_7_q), .out(INT_NUM_CUR), .sel(INT_NUM));
  not not_5 (not_5_out, halt);
  Counter #(.width(16), .max('hffff), .ongoal("wrap"), .trigger("rising"), .behavior("new")) counter_3 (
    .count(not_5_out), .Q(\总周期数 ), .clk(CLK));  // open: load, D, carry, clr, preset, down
  Multiplexer #(.select(2), .width(32), .disabled("Z"), .enable("false")) multiplexer_15 (
    .in0(Result), .in1(MemOut), .in2(PC_4), .out(RDin), .sel({JMP, MemToReg}));  // open: in3

  // Notes on the sheet:
  //   中断源
  //   中断等待指示
  //   总复位信号应将除ROM以外所有存储组件全部清零
  //   多级中断测试信号模拟器
  //   数码管输出
  //   数码管输出应该用寄存器锁存，否则显示数据只能一闪而过
  //   指令探针
  //   指令存储器
  //   指令字
  //   contents of Instruction_Memory (hex, n*v repeats v):
  //   7d000113 100413 1f41993 41f9d993 433 c00913 800b13 140413 f47413 800293 100313 499993 89e9b3 1300533
  //   2200893 73 406282b3 fe0294e3 140413 f00f93 1f47433 1c41413 800293 100313 49d993 89e9b3 1300533
  //   2200893 73 406282b3 fe0294e3 1c45413 406b0b33 b0463 f95ff06f 2b3 fff2c293 1029293 fff2e293 500533
  //   2200893 73 f5dff06f 1112023 410113 a12023 410113 812023 410113 1312023 410113 1412023 410113 1512023
  //   410113 1612023 410113 40e073 100b13 300a13 100a93 1600433 441413 14469b3 1300533 2200893 73 fe0416e3
  //   415a0a33 fe0a10e3 40f073 ffc10113 12b03 ffc10113 12a83 ffc10113 12a03 ffc10113 12983 ffc10113 12403
  //   ffc10113 12503 ffc10113 12883 200073 1112023 410113 a12023 410113 812023 410113 1312023 410113
  //   1412023 410113 1512023 410113 1612023 410113 40e073 200b13 300a13 100a93 1600433 441413 14469b3
  //   1300533 2200893 73 fe0416e3 415a0a33 fe0a10e3 40f073 ffc10113 12b03 ffc10113 12a83 ffc10113 12a03
  //   ffc10113 12983 ffc10113 12403 ffc10113 12503 ffc10113 12883 200073 1112023 410113 a12023 410113
  //   812023 410113 1312023 410113 1412023 410113 1512023 410113 1612023 410113 40e073 300b13 300a13
  //   100a93 1600433 441413 14469b3 1300533 2200893 73 fe0416e3 415a0a33 fe0a10e3 40f073 ffc10113 12b03
  //   ffc10113 12a83 ffc10113 12a03 ffc10113 12983 ffc10113 12403 ffc10113 12503 ffc10113 12883 200073
  //   Reset 
  //   Reset 
  //   Reset 
  //   JAL
  //   JALR
  //   URET
  //   Beq
  //   Bne
  //   MemToReg
  //   MemWrite
  //   AluOP
  //   AluSrcB
  //   RegWrite
  //   S_type
  //   为方便自动评测，需要输出PC，IR，寄存器堆写如数据RDin
  //   beq\bne指令目的地址
  //   jal指令目的地址
  //   RAM写使能MemWrite、RAM写入数据MDin等信号
  //   计算出地址的最低有效位设为0
  //   jalr指令目的地址
  //   控制位
  //   暂停节拍，不能为0
  //   戳工具置1进入计数暂停模式，ctrl+k时钟自动运行到对应节拍暂停
  //   ctrl+k关闭时钟连续运行，将控制位置零，进入单步调试模式调试
  //   用这个时钟源需要去掉电路中的其他时钟源
  //   中断地址
  //   可计数暂停的时钟源
  //   数据存储器
endmodule

module \流水线_单级中断  (
  output RegWrite,
  output MemWrite,
  output [31:0] IF_PC,
  output [31:0] ID_PC,
  output [31:0] EX_PC,
  output [31:0] M_PC,
  output [31:0] WB_PC,
  output [31:0] RDin,
  output [31:0] MDin,
  output [31:0] LedData
);

  wire _1_out, _2_out, _3_out, ALU, ALU_t, AluSrcB, and_1_out, and_3_out, and_4_out, and_5_out, and_6_out,
       and_7_out, and_8_out, and_11_out, and_12_out, and_13_out, and_14_out, B_JMP, Beq, Bge, Bne, Branch,
       Branch_Pre1, Branch_Pre2, CLK, clock_1_out, clock_2_out, CLR1, CLR2, CLR3, comparator_1_eq,
       comparator_2_eq, comparator_3_eq, comparator_4_eq, comparator_5_eq, comparator_6_eq, comparator_7_eq,
       comparator_7_lt, comparator_8_eq, d_ff_1_q, d_ff_2_q, d_ff_3_q, d_ff_4_q, ecall, EX_ecall,
       EX_MemToReg, \ex_mem流水寄存器_1_halt_2 , \ex_mem流水寄存器_1_jal_2 , \ex_mem流水寄存器_1_jalr_2 ,
       \ex_mem流水寄存器_1_memtoreg_2 , \ex_mem流水寄存器_1_regwrite_2 , \ex_mem流水寄存器_1_sb_2 , EX_RegWrite, EX_URET,
       Go, halt, \id_ex流水寄存器_1_halt_2 , \id_ex流水寄存器_1_memwrite_2 , \id_ex流水寄存器_1_sb_2 , ID_S_type, ID_URET,
       IE, IE_q, IF_URET, INT1, INT2, INT3, INT_Request, INT_Select, intR, IR1, IR2, IR3, JAL, JALR, LoadUse,
       LoadUse_Pre1, \mem_wb流水寄存器_1_jal_2 , \mem_wb流水寄存器_1_jalr_2 , MemToReg, multiplexer_5_out,
       multiplexer_9_out, multiplexer_13_out, nand_1_out, nor_1_out, not_1_out, not_2_out, not_3_out,
       not_4_out, not_5_out, not_6_out, not_7_out, not_8_out, not_9_out, not_10_out, not_13_out, or_3_out,
       or_4_out, or_5_out, or_6_out, or_7_out, or_10_out, or_17_out, or_18_out, or_19_out, register_2_q, RST,
       Run, W1, W2, W3, \单周期硬布线控制器_1_alu_src , \单周期硬布线控制器_1_beq , \单周期硬布线控制器_1_bge , \单周期硬布线控制器_1_bne ,
       \单周期硬布线控制器_1_jal , \单周期硬布线控制器_1_jalr , \单周期硬布线控制器_1_memtoreg , \单周期硬布线控制器_1_memwrite ,
       \单周期硬布线控制器_1_r1_used , \单周期硬布线控制器_1_r2_used , \单周期硬布线控制器_1_regwrite , \单周期硬布线控制器_1_sb ,
       \重定向相关处理逻辑_1_flush ;
  wire [1:0] \id_ex流水寄存器_1_r1foward_2 , \id_ex流水寄存器_1_r2foward_2 , INT_NUM, or_2_out, register_7_q,
       \重定向相关处理逻辑_1_r1foward , \重定向相关处理逻辑_1_r2foward ;
  wire [1:1] or_13_out;
  wire [3:0] AluOP, \单周期硬布线控制器_1_alu_op ;
  wire [4:0] EX_W_num, MEM_W_num, multiplexer_16_out, R1_num, R2_num, W_num;
  wire [12:0] CNT_num;
  wire [15:0] \LoadUse次数 , \总周期数 , \插入气泡数 , \无条件分支数 , \条件分支成功数 ;
  wire [31:0] adder_2_out, alu_1_result, and_10_out, bit_extender_1_out, bit_extender_2_out,
       bit_extender_3_out, bit_extender_4_out, bit_extender_5_out, BRANCH_PC, BreakPoint, EPCAddr, EX_IR,
       \id_ex流水寄存器_1_b_imm12_2 , \id_ex流水寄存器_1_r1_2 , \id_ex流水寄存器_1_r2_2 , \id_ex流水寄存器_1_signimm_2 ,
       \id_ex流水寄存器_1_u_imm20_2 , ID_IR, IF_IR, INTAddr, JAL_PC, JALR_PC, JMPAddr, MEM_ALUResult, MEM_IR,
       \mem_wb流水寄存器_1_aluresult_2 , \mem_wb流水寄存器_1_rd_2 , MemOut, multiplexer_2_out, multiplexer_3_out,
       multiplexer_8_out, multiplexer_12_out, multiplexer_15_out, PC_2_q, PC_4, R1, R2, R2_MEM,
       regifile_1_r1, regifile_1_r2, SB_rst, shifter_1_out, shifter_2_out, shifter_3_out, WB_IR, WB_PC_4;

  Button \u_总复位  (.out(RST));
  Button _1 (.out(_1_out));
  Button _2 (.out(_2_out));
  Button _3 (.out(_3_out));
  // Probe on \总周期数 
  // Probe on \总周期数 
  Button \u_继续运行  (.out(Go));
  LED #(.active("true")) led_1 (.in(W1));
  LED #(.active("true")) led_2 (.in(W2));
  LED #(.active("true")) led_3 (.in(W3));
  Hex_Digit_Display hex_digit_display_1 (.value(LedData[31:28]));  // open: dp
  // Probe on IF_PC[19:0]
  // RiscV_Probe riscv_probe_1: pin names not known; wires that end beside it: _1_out, _2_out, _3_out, IR1, IR2, IR3, IF_IR
  Comparator #(.width(16), .mode("twosComplement")) comparator_1 (
    .a(16'h23b), .b(\总周期数 ), .eq(comparator_1_eq));  // open: gt, lt
  Comparator #(.width(16), .mode("twosComplement")) comparator_2 (
    .a(\总周期数 ), .b(16'h1), .eq(comparator_2_eq));  // open: gt, lt
  Comparator #(.width(16), .mode("twosComplement")) comparator_3 (
    .a(\总周期数 ), .b(16'h4), .eq(comparator_3_eq));  // open: gt, lt
  Comparator #(.width(16), .mode("twosComplement")) comparator_4 (
    .a(\总周期数 ), .b(16'h7), .eq(comparator_4_eq));  // open: gt, lt
  or or_1 (or_2_out[1], JAL, JALR);
  or or_2 (or_2_out[0], JALR, B_JMP);
  Multiplexer #(.select(2), .width(32), .disabled("Z"), .enable("false")) multiplexer_1 (
    .in0(PC_4), .in1(BRANCH_PC), .in2(JAL_PC), .in3(JALR_PC), .out(JMPAddr), .sel(or_2_out));
  Hex_Digit_Display hex_digit_display_2 (.value(LedData[23:20]));  // open: dp
  Hex_Digit_Display hex_digit_display_3 (.value(LedData[27:24]));  // open: dp
  // Probe on ID_PC[19:0]
  // RiscV_Probe riscv_probe_2: pin names not known; wires that end beside it: ID_IR
  or or_3 (or_3_out, comparator_1_eq, comparator_2_eq);
  Pull_Resistor #(.pull(0)) pull_resistor_1 (.node(IR1));
  assign IR1 = or_3_out ? ~CLK : 1'bz;  // Controlled_Inverter controlled_inverter_1
  Pull_Resistor #(.pull(0)) pull_resistor_2 (.node(IR2));
  assign IR2 = comparator_3_eq ? ~CLK : 1'bz;  // Controlled_Inverter controlled_inverter_2
  Pull_Resistor #(.pull(0)) pull_resistor_3 (.node(IR3));
  assign IR3 = comparator_4_eq ? ~CLK : 1'bz;  // Controlled_Inverter controlled_inverter_3
  Hex_Digit_Display hex_digit_display_4 (.value(LedData[19:16]));  // open: dp
  Hex_Digit_Display hex_digit_display_5 (.value(LedData[15:12]));  // open: dp
  Multiplexer #(.select(1), .width(32), .disabled("Z"), .enable("false")) multiplexer_2 (
    .in0(JMPAddr), .in1(EPCAddr), .out(multiplexer_2_out), .sel(IF_URET));
  Register #(.width(32), .trigger("rising"), .Select("low")) PC (.D(JMPAddr), .clk(CLK), .clr(RST));  // open: en, Q
  Hex_Digit_Display hex_digit_display_6 (.value(LedData[11:8]));  // open: dp
  Hex_Digit_Display hex_digit_display_7 (.value(LedData[7:4]));  // open: dp
  Clock #(.highDuration(1), .lowDuration(1)) clock_1 (.out(clock_1_out));
  // Probe on EX_PC[19:0]
  // RiscV_Probe riscv_probe_3: pin names not known; wires that end beside it: clock_1_out, EX_IR, CLK
  Hex_Digit_Display hex_digit_display_8 (.value(LedData[3:0]));  // open: dp
  Multiplexer #(.select(1), .width(32), .disabled("Z"), .enable("false")) multiplexer_3 (
    .in0(multiplexer_2_out), .in1(PC_4), .out(multiplexer_3_out), .sel(INT_Select));
  Comparator #(.width(5), .mode("unsigned")) comparator_5 (
    .a(IF_IR[6:2]), .b(5'b11100), .eq(comparator_5_eq));  // open: gt, lt
  Comparator #(.width(5), .mode("unsigned")) comparator_6 (
    .a({IF_IR[30], IF_IR[25], IF_IR[14:12]}), .b({5{1'b0}}), .eq(comparator_6_eq));  // open: gt, lt
  // Probe on \总周期数 
  // Probe on M_PC[19:0]
  // RiscV_Probe riscv_probe_4: pin names not known; wires that end beside it: MEM_IR
  \重定向相关处理逻辑  \u_重定向相关处理逻辑_1  (
    .BranchTaken(Branch), .IR(ID_IR), .ecall(ecall), .EX_MemRead(EX_MemToReg),
    .R1Used(\单周期硬布线控制器_1_r1_used ), .EX_RegWrite(EX_RegWrite), .EX_rd(EX_W_num),
    .R2Used(\单周期硬布线控制器_1_r2_used ), .MEM_RegWrite(\ex_mem流水寄存器_1_regwrite_2 ), .MEM_rd(MEM_W_num),
    .Stall(LoadUse), .Flush(\重定向相关处理逻辑_1_flush ), .R1Foward(\重定向相关处理逻辑_1_r1foward ),
    .R2Foward(\重定向相关处理逻辑_1_r2foward ));
  not not_1 (not_1_out, LoadUse);
  and and_1 (and_1_out, Run, not_1_out);
  Register #(.width(32), .trigger("rising"), .Select("low")) PC_2 (
    .D(multiplexer_3_out), .en(and_1_out), .Q(PC_2_q), .clk(CLK), .clr(RST));
  and and_2 (IF_URET, comparator_5_eq, comparator_6_eq, IF_IR[21]);
  // Probe on \总周期数 
  // Probe on \无条件分支数 
  // Probe on \条件分支成功数 
  // Probe on \插入气泡数 
  // Probe on \LoadUse次数 
  Multiplexer #(.select(1), .width(32), .disabled("Z"), .enable("false")) multiplexer_4 (
    .in0(PC_2_q), .in1(INTAddr), .out(IF_PC), .sel(INT_Select));
  // Probe on IF_PC[11:0]
  // Probe on WB_PC[19:0]
  // RiscV_Probe riscv_probe_5: pin names not known; wires that end beside it: WB_IR
  Multiplexer #(.select(1), .width(1), .disabled("Z"), .enable("false")) multiplexer_5 (
    .in0(1'b1), .in1(CLK), .out(multiplexer_5_out), .sel(INT_Select));
  // Probe on EX_PC[11:0]
  // Probe on ID_PC[11:0]
  Register #(.width(1), .trigger("rising"), .Select("low")) register_1 (
    .D(1'b1), .Q(INT_Select), .clk(INT_Request), .clr(or_4_out));  // open: en
  or or_4 (or_4_out, RST, register_2_q);
  Register #(.width(1), .trigger("rising"), .Select("low")) register_2 (
    .D(1'b1), .Q(register_2_q), .clk(multiplexer_5_out), .clr(or_5_out));  // open: en
  or or_5 (or_5_out, register_2_q, RST);
  ROM #(.addrWidth(10), .dataWidth(32), .Select("high")) \u_指令存储器  (.addr(IF_PC[11:2]), .data(IF_IR));
  Adder #(.width(32)) adder_1 (.a(IF_PC), .b(32'h4), .out(PC_4));  // open: cin, cout
  // Probe on M_PC[11:0]
  D_Flip_Flop #(.trigger("high"), .Pre_Clr_Positions("LEGACY"), .NegatePresetClear("false"), .enable("true"), .NewFFLayout("false")) d_ff_1 (.Q(d_ff_1_q));  // open: clk, D, Qn, preset, en, reset
  // Probe on 13'hc
  \IF_ID流水寄存器  \if_id流水寄存器_1  (
    .\指令字_IR (IF_IR), .PC(IF_PC), .\指令字_IR_2 (ID_IR), .PC_2(ID_PC), .RST(Branch), .Run(and_3_out), .CLK(CLK));  // open: PredictJump, PredictJump_2
  and and_3 (and_3_out, Run, not_2_out);
  not not_2 (not_2_out, LoadUse);
  // Probe on WB_PC[11:0]
  Comparator #(.width(13), .mode("twosComplement")) comparator_7 (
    .a(CNT_num), .b(13'hc), .eq(comparator_7_eq), .lt(comparator_7_lt));  // open: gt
  Clock #(.highDuration(1), .lowDuration(1)) clock_2 (.out(clock_2_out));
  nand nand_1 (nand_1_out, d_ff_1_q, comparator_7_eq);
  Counter #(.width(13), .max('h1fff), .ongoal("stay"), .trigger("rising"), .behavior("old")) counter_1 (
    .count(comparator_7_lt), .Q(CNT_num), .clk(clock_2_out));  // open: load, D, carry, clr, preset
  Comparator #(.width(32), .mode("twosComplement")) comparator_8 (
    .a(R1), .b(32'ha), .eq(comparator_8_eq));  // open: gt, lt
  assign CLK = nand_1_out ? clock_2_out : 1'bz;  // Controlled_Buffer controlled_buffer_1
  Multiplexer #(.select(1), .width(5), .disabled("Z"), .enable("false")) multiplexer_6 (
    .in0(ID_IR[19:15]), .in1(5'b10001), .out(R1_num), .sel(ecall));
  Multiplexer #(.select(1), .width(5), .disabled("Z"), .enable("false")) multiplexer_7 (
    .in0(ID_IR[24:20]), .in1(5'b01010), .out(R2_num), .sel(ecall));
  assign bit_extender_1_out = {{20{ID_IR[31]}}, ID_IR[31:20]};  // Bit_Extender bit_extender_1
  assign bit_extender_2_out = {{20{ID_IR[31]}}, {ID_IR[31:25], ID_IR[11:7]}};  // Bit_Extender bit_extender_2
  assign bit_extender_3_out = {{20{ID_IR[31]}}, {ID_IR[31], ID_IR[7], ID_IR[30:25], ID_IR[11:8]}};  // Bit_Extender bit_extender_3
  assign bit_extender_4_out = {{12{ID_IR[31]}}, {ID_IR[31], ID_IR[19:12], ID_IR[20], ID_IR[30:21]}};  // Bit_Extender bit_extender_4
  and and_4 (and_4_out, EX_ecall, ~comparator_8_eq);  // AND_Gate
  and and_5 (and_5_out, EX_ecall, comparator_8_eq);
  Pull_Resistor #(.pull(1)) pull_resistor_4 (.node(CLK));
  \单周期硬布线控制器  \u_单周期硬布线控制器_1  (
    .Funct({ID_IR[30], ID_IR[25], ID_IR[14:12]}), .OP(ID_IR[6:2]), .ALU_OP(\单周期硬布线控制器_1_alu_op ),
    .MemToReg(\单周期硬布线控制器_1_memtoreg ), .MemWrite(\单周期硬布线控制器_1_memwrite ), .ALU_SRC(\单周期硬布线控制器_1_alu_src ),
    .RegWrite(\单周期硬布线控制器_1_regwrite ), .ecall(ecall), .S_type(ID_S_type), .Jalr(\单周期硬布线控制器_1_jalr ),
    .Beq(\单周期硬布线控制器_1_beq ), .JAL(\单周期硬布线控制器_1_jal ), .Bne(\单周期硬布线控制器_1_bne ), .IR21(ID_IR[21]),
    .uret(ID_URET), .SB(\单周期硬布线控制器_1_sb ), .BGE(\单周期硬布线控制器_1_bge ), .r1_used(\单周期硬布线控制器_1_r1_used ),
    .r2_used(\单周期硬布线控制器_1_r2_used ));  // open: CSRRSI, CSRRCI
  not not_3 (not_3_out, CLK);
  Multiplexer #(.select(1), .width(32), .disabled("Z"), .enable("false")) multiplexer_8 (
    .in0(bit_extender_1_out), .in1(bit_extender_2_out), .out(multiplexer_8_out), .sel(ID_S_type));
  Register #(.width(32), .trigger("rising"), .Select("low")) register_3 (
    .D(R2), .en(and_4_out), .Q(LedData), .clk(CLK), .clr(RST));
  not not_4 (not_4_out, halt);
  or or_6 (or_6_out, JAL, JALR);
  Regifile regifile_1 (
    .Din(RDin), .Clk(not_3_out), .R1(regifile_1_r1), .R2(regifile_1_r2), .WE(RegWrite), .W_num(W_num),
    .R1_num(R1_num), .R2_num(R2_num));
  Counter #(.width(16), .max('hffff), .ongoal("wrap"), .trigger("rising"), .behavior("new")) counter_2 (
    .count(not_4_out), .Q(\无条件分支数 ), .clk(or_6_out));  // open: load, D, carry, clr, preset, down
  \ID_EX流水寄存器  \id_ex流水寄存器_1  (
    .RegWrite(\单周期硬布线控制器_1_regwrite ), .MemToReg(\单周期硬布线控制器_1_memtoreg ), .MemWrite(\单周期硬布线控制器_1_memwrite ),
    .AluOP(\单周期硬布线控制器_1_alu_op ), .AluSrc(\单周期硬布线控制器_1_alu_src ), .RegWrite_2(EX_RegWrite),
    .MemToReg_2(EX_MemToReg), .MemWrite_2(\id_ex流水寄存器_1_memwrite_2 ), .AluOP_2(AluOP), .AluSrc_2(AluSrcB),
    .Run(Run), .CLK(CLK), .\指令字_IR (ID_IR), .PC(ID_PC), .RST(or_7_out), .\指令字_IR_2 (EX_IR), .PC_2(EX_PC),
    .SignImm(multiplexer_8_out), .SignImm_2(\id_ex流水寄存器_1_signimm_2 ), .WriteReg_num(ID_IR[11:7]),
    .WriteReg_num_2(EX_W_num), .B_Imm12(bit_extender_3_out), .U_Imm20(bit_extender_4_out),
    .B_Imm12_2(\id_ex流水寄存器_1_b_imm12_2 ), .U_Imm20_2(\id_ex流水寄存器_1_u_imm20_2 ), .R1(regifile_1_r1),
    .R2(regifile_1_r2), .R1_2(\id_ex流水寄存器_1_r1_2 ), .R2_2(\id_ex流水寄存器_1_r2_2 ), .halt(and_5_out),
    .halt_2(\id_ex流水寄存器_1_halt_2 ), .Jal(\单周期硬布线控制器_1_jal ), .Jalr(\单周期硬布线控制器_1_jalr ),
    .Sb(\单周期硬布线控制器_1_sb ), .Bge(\单周期硬布线控制器_1_bge ), .Jal_2(JAL), .Jalr_2(JALR), .Sb_2(\id_ex流水寄存器_1_sb_2 ),
    .Bge_2(Bge), .Beq(\单周期硬布线控制器_1_beq ), .Bne(\单周期硬布线控制器_1_bne ), .Beq_2(Beq), .Bne_2(Bne),
    .R1Foward(\重定向相关处理逻辑_1_r1foward ), .R1Foward_2(\id_ex流水寄存器_1_r1foward_2 ),
    .R2Foward(\重定向相关处理逻辑_1_r2foward ), .R2Foward_2(\id_ex流水寄存器_1_r2foward_2 ), .ecall(ecall),
    .ecall_2(EX_ecall), .uret(ID_URET), .uret_2(EX_URET));  // open: PredictJump, PredictJump_2
  Multiplexer #(.select(1), .width(1), .disabled("Z"), .enable("false")) multiplexer_9 (
    .in0(INT_Select), .in1(1'b0), .out(multiplexer_9_out), .sel(ID_URET));
  or or_7 (or_7_out, \重定向相关处理逻辑_1_flush , multiplexer_9_out);
  not not_5 (not_5_out, halt);
  Counter #(.width(16), .max('hffff), .ongoal("wrap"), .trigger("rising"), .behavior("new")) counter_3 (
    .count(not_5_out), .Q(\条件分支成功数 ), .clk(B_JMP));  // open: load, D, carry, clr, preset, down
  Multiplexer #(.select(2), .width(32), .disabled("Z"), .enable("false")) multiplexer_10 (
    .in0(\id_ex流水寄存器_1_r1_2 ), .in1(RDin), .in2(MEM_ALUResult), .out(R1), .sel(\id_ex流水寄存器_1_r1foward_2 ));  // open: in3
  Multiplexer #(.select(2), .width(32), .disabled("Z"), .enable("false")) multiplexer_11 (
    .in0(\id_ex流水寄存器_1_r2_2 ), .in1(RDin), .in2(MEM_ALUResult), .out(R2), .sel(\id_ex流水寄存器_1_r2foward_2 ));  // open: in3
  Shifter #(.width(32), .shift("ll")) shifter_1 (.in(\id_ex流水寄存器_1_b_imm12_2 ), .\dist (5'b00001), .out(shifter_1_out));
  Shifter #(.width(32), .shift("ll")) shifter_2 (.in(\id_ex流水寄存器_1_u_imm20_2 ), .\dist (5'b00001), .out(shifter_2_out));
  Multiplexer #(.select(1), .width(32), .disabled("Z"), .enable("false")) multiplexer_12 (
    .in0(R2), .in1(\id_ex流水寄存器_1_signimm_2 ), .out(multiplexer_12_out), .sel(AluSrcB));
  Adder #(.width(32)) adder_2 (.a(R1), .b(\id_ex流水寄存器_1_signimm_2 ), .out(adder_2_out));  // open: cin, cout
  and and_6 (and_6_out, Bne, ~ALU);  // AND_Gate
  and and_7 (and_7_out, Beq, ALU);
  and and_8 (and_8_out, Bge, ALU_t);
  not not_6 (not_6_out, halt);
  ALU alu_1 (
    .X(R1), .Y(multiplexer_12_out), .AluOP(AluOP), .Equal(ALU), .Result(alu_1_result), .out_4(ALU_t));  // open: Result_2, out_6
  Adder #(.width(32)) adder_3 (.a(EX_PC), .b(shifter_1_out), .out(BRANCH_PC));  // open: cin, cout
  Adder #(.width(32)) adder_4 (.a(EX_PC), .b(shifter_2_out), .out(JAL_PC));  // open: cin, cout
  or or_8 (B_JMP, and_6_out, and_7_out, and_8_out);
  Counter #(.width(16), .max('hffff), .ongoal("wrap"), .trigger("rising"), .behavior("new")) counter_4 (
    .count(not_6_out), .Q(\插入气泡数 ), .clk(LoadUse));  // open: load, D, carry, clr, preset, down
  assign JALR_PC = 32'hfffffffe & adder_2_out;  // AND_Gate and_9, 32 bits wide
  or or_9 (Branch, B_JMP, JAL, JALR);
  not not_7 (not_7_out, halt);
  Counter #(.width(16), .max('hffff), .ongoal("wrap"), .trigger("rising"), .behavior("new")) counter_5 (
    .count(not_7_out), .Q(\LoadUse次数 ), .clk(LoadUse));  // open: load, D, carry, clr, preset, down
  Multiplexer #(.select(1), .width(1), .disabled("Z"), .enable("false")) multiplexer_13 (
    .in0(INT_Select), .in1(1'b0), .out(multiplexer_13_out), .sel(ID_URET));
  or or_10 (or_10_out, RST, multiplexer_13_out);
  \EX_MEM流水寄存器  \ex_mem流水寄存器_1  (
    .MemToReg(EX_MemToReg), .MemWrite(\id_ex流水寄存器_1_memwrite_2 ), .RegWrite(EX_RegWrite),
    .AluResult(alu_1_result), .WriteData(R2), .W_num(EX_W_num), .IR(EX_IR), .PC(EX_PC),
    .MemToReg_2(\ex_mem流水寄存器_1_memtoreg_2 ), .MemWrite_2(MemWrite), .RegWrite_2(\ex_mem流水寄存器_1_regwrite_2 ),
    .AluResult_2(MEM_ALUResult), .WriteData_2(R2_MEM), .W_num_2(MEM_W_num), .IR_2(MEM_IR), .PC_2(M_PC),
    .RST(or_10_out), .Run(Run), .CLK(CLK), .halt(\id_ex流水寄存器_1_halt_2 ), .halt_2(\ex_mem流水寄存器_1_halt_2 ),
    .Jal(JAL), .Jalr(JALR), .Sb(\id_ex流水寄存器_1_sb_2 ), .Jal_2(\ex_mem流水寄存器_1_jal_2 ),
    .Jalr_2(\ex_mem流水寄存器_1_jalr_2 ), .Sb_2(\ex_mem流水寄存器_1_sb_2 ), .uret(EX_URET));  // open: uret_2
  Multiplexer #(.select(1), .width(32), .disabled("Z"), .enable("false")) multiplexer_14 (
    .in0(R2_MEM), .in1(SB_rst), .out(MDin), .sel(\ex_mem流水寄存器_1_sb_2 ));
  Multiplexer #(.select(2), .width(32), .disabled("Z"), .enable("false")) multiplexer_15 (
    .in0(32'hffffff00), .in1(32'hffff00ff), .in2(32'hff00ffff), .in3(32'hffffff), .out(multiplexer_15_out),
    .sel(MEM_ALUResult[1:0]));
  Multiplexer #(.select(2), .width(5), .disabled("Z"), .enable("false")) multiplexer_16 (
    .in0({5{1'b0}}), .in1(5'b01000), .in2(5'b10000), .in3(5'b11000), .out(multiplexer_16_out),
    .sel(MEM_ALUResult[1:0]));
  not not_8 (not_8_out, halt);
  not not_9 (not_9_out, halt);
  or or_11 (Run, Go, not_8_out);
  Counter #(.width(16), .max('hffff), .ongoal("wrap"), .trigger("rising"), .behavior("new")) counter_6 (
    .count(not_9_out), .Q(\总周期数 ), .clk(CLK));  // open: load, D, carry, clr, preset, down
  RAM #(.addrWidth(10), .dataWidth(32), .bus("separate"), .Select("high")) ram_1 (
    .addr(MEM_ALUResult[11:2]), .din(MDin), .data(MemOut), .str(MemWrite), .clk(CLK));  // open: sel, ld, clr
  assign and_10_out = MemOut & multiplexer_15_out;  // AND_Gate and_10, 32 bits wide
  assign bit_extender_5_out = {{24{1'b0}}, R2_MEM[7:0]};  // Bit_Extender bit_extender_5
  assign SB_rst = and_10_out | shifter_3_out;  // OR_Gate or_12, 32 bits wide
  Shifter #(.width(32), .shift("ll")) shifter_3 (
    .in(bit_extender_5_out), .\dist (multiplexer_16_out), .out(shifter_3_out));
  \MEM_WB流水寄存器  \mem_wb流水寄存器_1  (
    .MemToReg(\ex_mem流水寄存器_1_memtoreg_2 ), .RegWrite(\ex_mem流水寄存器_1_regwrite_2 ), .AluResult(MEM_ALUResult),
    .RD(MemOut), .W_num(MEM_W_num), .IR(MEM_IR), .PC(M_PC), .MemToReg_2(MemToReg), .RegWrite_2(RegWrite),
    .AluResult_2(\mem_wb流水寄存器_1_aluresult_2 ), .RD_2(\mem_wb流水寄存器_1_rd_2 ), .W_num_2(W_num), .IR_2(WB_IR),
    .PC_2(WB_PC), .RST(RST), .Run(Run), .CLK(CLK), .halt(\ex_mem流水寄存器_1_halt_2 ), .halt_2(halt),
    .Jal(\ex_mem流水寄存器_1_jal_2 ), .Jalr(\ex_mem流水寄存器_1_jalr_2 ), .Jal_2(\mem_wb流水寄存器_1_jal_2 ),
    .Jalr_2(\mem_wb流水寄存器_1_jalr_2 ));  // open: uret, uret_2
  or or_13 (or_13_out[1], \mem_wb流水寄存器_1_jal_2 , \mem_wb流水寄存器_1_jalr_2 );
  Multiplexer #(.select(2), .width(32), .disabled("Z"), .enable("false")) multiplexer_17 (
    .in0(\mem_wb流水寄存器_1_aluresult_2 ), .in1(\mem_wb流水寄存器_1_rd_2 ), .in2(WB_PC_4), .out(RDin),
    .sel({or_13_out[1], MemToReg}));  // open: in3
  Adder #(.width(32)) adder_5 (.a(WB_PC), .b(32'h4), .out(WB_PC_4));  // open: cin, cout
  or or_14 (W1, INT1, d_ff_2_q);
  or or_15 (W2, INT2, d_ff_3_q);
  or or_16 (W3, INT3, d_ff_4_q);
  Priority_Encoder #(.select(2), .disabled("Z")) priority_encoder_1 (
    .in0(INT1), .in1(INT2), .in2(INT3), .out(INT_NUM), .gs(intR));  // open: in3, en_out, en_in
  nor nor_1 (nor_1_out, EX_URET, ID_URET);
  not not_10 (not_10_out, IF_URET);
  Register #(.width(1), .trigger("rising"), .Select("low")) register_4 (
    .D(Branch), .Q(Branch_Pre1), .clk(CLK), .clr(RST));  // open: en
  Register #(.width(1), .trigger("rising"), .Select("low")) register_5 (
    .D(LoadUse), .Q(LoadUse_Pre1), .clk(CLK), .clr(RST));  // open: en
  D_Flip_Flop #(.trigger("rising"), .Pre_Clr_Positions("LEGACY"), .NegatePresetClear("false"), .enable("true"), .NewFFLayout("false")) d_ff_2 (
    .clk(IR1), .D(1'b1), .Q(d_ff_2_q), .reset(INT1));  // open: Qn, preset, en
  D_Flip_Flop #(.trigger("rising"), .Pre_Clr_Positions("LEGACY"), .NegatePresetClear("false"), .enable("true"), .NewFFLayout("false")) d_ff_3 (
    .clk(IR2), .D(1'b1), .Q(d_ff_3_q), .reset(INT2));  // open: Qn, preset, en
  D_Flip_Flop #(.trigger("rising"), .Pre_Clr_Positions("LEGACY"), .NegatePresetClear("false"), .enable("true"), .NewFFLayout("false")) d_ff_4 (
    .clk(IR3), .D(1'b1), .Q(d_ff_4_q), .reset(INT3));  // open: Qn, preset, en
  and and_11 (and_11_out, intR, IE);
  Register #(.width(32), .trigger("rising"), .Select("low")) \EPC寄存器  (
    .D(BreakPoint), .en(nor_1_out), .Q(EPCAddr), .clk(INT_Request), .clr(RST));
  Register #(.width(1), .trigger("rising"), .Select("low")) u_IE (
    .D(1'b0), .Q(IE_q), .clk(not_10_out), .clr(RST), .preset(INT_Request));  // open: en, cs
  not not_11 (IE, IE_q);
  or or_17 (or_17_out, d_ff_2_q, INT1);
  and and_12 (and_12_out, or_17_out, ~CLR1);  // AND_Gate
  or or_18 (or_18_out, d_ff_3_q, INT2);
  and and_13 (and_13_out, or_18_out, ~CLR2);  // AND_Gate
  or or_19 (or_19_out, d_ff_4_q, INT3);
  and and_14 (and_14_out, or_19_out, ~CLR3);  // AND_Gate
  not not_12 (INT_Request, not_13_out);
  not not_13 (not_13_out, and_11_out);
  Register #(.width(1), .trigger("rising"), .Select("low")) register_6 (
    .D(Branch_Pre1), .Q(Branch_Pre2));  // open: en, clk, clr
  D_Flip_Flop #(.trigger("rising"), .Pre_Clr_Positions("LEGACY"), .NegatePresetClear("false"), .enable("true"), .NewFFLayout("false")) \u_中断请求寄存器IR  (
    .clk(CLK), .D(and_12_out), .Q(INT1));  // open: Qn, preset, en, reset
  D_Flip_Flop #(.trigger("rising"), .Pre_Clr_Positions("LEGACY"), .NegatePresetClear("false"), .enable("true"), .NewFFLayout("false")) \u_中断请求寄存器IR_2  (
    .clk(CLK), .D(and_13_out), .Q(INT2));  // open: Qn, preset, en, reset
  D_Flip_Flop #(.trigger("rising"), .Pre_Clr_Positions("LEGACY"), .NegatePresetClear("false"), .enable("true"), .NewFFLayout("false")) \u_中断请求寄存器IR_3  (
    .clk(CLK), .D(and_14_out), .Q(INT3));  // open: Qn, preset, en, reset
  Multiplexer #(.select(2), .width(32), .disabled("Z"), .enable("false")) multiplexer_18 (
    .in0(32'h30ac), .in1(32'h3150), .in2(32'h31f4), .out(INTAddr), .sel(INT_NUM));  // open: in3
  Register #(.width(2), .trigger("rising"), .Select("low")) register_7 (
    .D(INT_NUM), .Q(register_7_q), .clk(INT_Request), .clr(RST));  // open: en
  Demultiplexer #(.select(2), .width(1), .tristate("false"), .disabled("Z"), .enable("false")) demultiplexer_1 (
    .out0(CLR1), .out1(CLR2), .out2(CLR3), .in(IF_URET), .sel(register_7_q));  // open: out3
  // Probe on {Branch_Pre2, LoadUse_Pre1, Branch_Pre1}
  Multiplexer #(.select(3), .width(32), .disabled("Z"), .enable("false")) multiplexer_19 (
    .in0(EX_PC), .in1(JMPAddr), .in2(ID_PC), .in4(ID_PC), .out(BreakPoint),
    .sel({Branch_Pre2, LoadUse_Pre1, Branch_Pre1}));  // open: in3, in5, in6, in7
  Register #(.width(3), .trigger("rising"), .Select("low")) register_8 (
    .D({Branch_Pre2, LoadUse_Pre1, Branch_Pre1}), .clk(INT_Request), .clr(RST));  // open: en, Q

  // Other names for the same wires on the sheet: MEM_PC[31:0] = M_PC

  // Notes on the sheet:
  //   中断源
  //   时空图监测，可删除
  //   中断等待指示
  //   单级中断测试信号模拟器
  //   数码管输出
  //   控制位
  //   IF段
  //   contents of 指令存储器 (hex, n*v repeats v):
  //   7d000113 100413 1f41993 41f9d993 433 c00913 800b13 140413 f47413 800293 100313 499993 89e9b3 1300533
  //   2200893 73 406282b3 fe0294e3 140413 f00f93 1f47433 1c41413 800293 100313 49d993 89e9b3 1300533
  //   2200893 73 406282b3 fe0294e3 1c45413 406b0b33 b0463 f95ff06f 2b3 fff2c293 1029293 fff2e293 500533
  //   2200893 73 f5dff06f 1112023 410113 a12023 410113 812023 410113 1312023 410113 1412023 410113 1512023
  //   410113 1612023 410113 100b13 300a13 100a93 1600433 441413 14469b3 1300533 2200893 73 fe0416e3
  //   415a0a33 fe0a10e3 ffc10113 12b03 ffc10113 12a83 ffc10113 12a03 ffc10113 12983 ffc10113 12403
  //   ffc10113 12503 ffc10113 12883 200073 1112023 410113 a12023 410113 812023 410113 1312023 410113
  //   1412023 410113 1512023 410113 1612023 410113 200b13 300a13 100a93 1600433 441413 14469b3 1300533
  //   2200893 73 fe0416e3 415a0a33 fe0a10e3 ffc10113 12b03 ffc10113 12a83 ffc10113 12a03 ffc10113 12983
  //   ffc10113 12403 ffc10113 12503 ffc10113 12883 200073 1112023 410113 a12023 410113 812023 410113
  //   1312023 410113 1412023 410113 1512023 410113 1612023 410113 300b13 300a13 100a93 1600433 441413
  //   14469b3 1300533 2200893 73 fe0416e3 415a0a33 fe0a10e3 ffc10113 12b03 ffc10113 12a83 ffc10113 12a03
  //   ffc10113 12983 ffc10113 12403 ffc10113 12503 ffc10113 12883 200073
  //   流水调试日志用
  //   暂停节拍，不能为0
  //   指令字
  //   戳工具置1进入计数暂停模式，ctrl+k时钟自动运行到对应节拍暂停
  //   ctrl+k关闭时钟连续运行，将控制位置零，进入单步调试模式调试
  //   IR
  //   PC
  //   rs
  //   rt
  //   I型指令立即数
  //   S型指令立即数
  //   W#
  //   B型指令立即数
  //   J型指令立即数
  //   可计数暂停的时钟源
  //   JAL
  //   JALR
  //   URET
  //   SB
  //   BGE
  //   OP
  //   Funct
  //   ID段
  //   Beq
  //   Bne
  //   MemToReg
  //   MemWrite
  //   AluOP
  //   AluSrcB
  //   RegWrite
  //   S_type
  //   为方便自动评测，需要输出流水线各段保存的PC值，注意是PC不是PC+4，另外ID段寄存器写入信息，Mem段内存写入信息也要输出
  //   Beq
  //   Bne
  //   MemToReg
  //   MemWrite
  //   AluOP
  //   AluSrcB
  //   RegWrite
  //   JAL
  //   JALR
  //   SB
  //   BGE
  //   R1
  //   R2
  //   SignImm
  //   W#
  //   halt
  //   IR
  //   PC
  //   EX段
  //   BranchTaken相关逻辑
  //   beq\bne\bge指令目的地址
  //   jal指令目的地址
  //   jalr指令目的地址
  //   MemToReg
  //   MemWrite
  //   RegWrite
  //   JAL
  //   JALR
  //   SB
  //   ALUResult
  //   W#
  //   halt
  //   IR
  //   PC
  //   MEM段
  //   数据存储器
  //   SB指令实现
  //   MemOut
  //   JAL
  //   JALR
  //   ALUResult
  //   MemOut
  //   W#
  //   halt
  //   IR
  //   PC
  //   WB段
  //   WB段PC+4生成
  //   前一个周期的分支情况
  //   前一个周期的Load_Use情况
  //   Reset 
  //   Reset 
  //   Reset 
  //   前两个周期的分支情况
  //   中断地址
endmodule

module \封装正确性测试  (
);

  wire IR1, IR2, IR3, MemW, RegW;
  wire [31:0] EX_PC, ID_PC, IF_PC, IR, LED, MDin, MDinr, MEM_PC, PC, RDin, RDinr, WB_PC;

  \单周期RISC_V  \u_单周期risc_v_1  (
    .RegWrite(RegW), .MemWrite(MemW), .PC(PC), .IR(IR), .RDin(RDin), .MDin(MDin), .LedData(LED));
  \气泡流水线  \u_气泡流水线_1  (
    .RegWrite(RegW), .MemWrite(MemW), .IF_PC(IF_PC), .ID_PC(ID_PC), .EX_PC(EX_PC), .M_PC(MEM_PC),
    .WB_PC(WB_PC), .RDin(RDinr), .MDin(MDinr), .LedData(LED));
  \单周期_单级中断  \u_单周期_单级中断_1  (
    .IR1(IR1), .IR2(IR2), .IR3(IR3), .RegWrite(RegW), .MemWrite(MemW), .PC(PC), .IR(IR), .RDin(RDin),
    .MDin(MDin), .LedData(LED));
  \理想流水线  \u_理想流水线_1  (
    .RegWrite(RegW), .MemWrite(MemW), .IF_PC(IF_PC), .ID_PC(ID_PC), .EX_PC(EX_PC), .M_PC(MEM_PC),
    .WB_PC(WB_PC), .RDin(RDinr), .MDin(MDinr), .LedData(LED));
  \重定向流水线  \u_重定向流水线_1  (
    .RegWrite(RegW), .MemWrite(MemW), .IF_PC(IF_PC), .ID_PC(ID_PC), .EX_PC(EX_PC), .M_PC(MEM_PC),
    .WB_PC(WB_PC), .RDin(RDinr), .MDin(MDinr), .LedData(LED));
  \单周期_多级中断  \u_单周期_多级中断_1  (
    .IR1(IR1), .IR2(IR2), .IR3(IR3), .RegWrite(RegW), .MemWrite(MemW), .PC(PC), .IR(IR), .RDin(RDin),
    .MDin(MDin), .LedData(LED));

  // Notes on the sheet:
  //   单周期封装测试
  //   气泡流水封装测试
  //   单周期+单级中断封装测试
  //   请检查上面封装有无位宽不匹配，引脚标签是否和连接的标签相对应，否则无法在educoder平台上正确测试
  //   理想流水封装测试
  //   重定向流水封装测试
  //   单周期+多级中断封装测试
endmodule

// IF/ID
module \IF_ID流水寄存器  (
  input  [31:0] \指令字_IR ,
  input  PredictJump,
  input  [31:0] PC,
  input  RST,
  input  Run,
  input  CLK,
  output [31:0] \指令字_IR_2 ,
  output PredictJump_2,
  output [31:0] PC_2
);

  wire multiplexer_2_out;
  wire [31:0] multiplexer_1_out, multiplexer_3_out;

  Multiplexer #(.select(1), .width(32), .disabled("Z"), .enable("false")) multiplexer_1 (
    .in0(\指令字_IR ), .in1({32{1'b0}}), .out(multiplexer_1_out), .sel(RST));
  Multiplexer #(.select(1), .width(1), .disabled("Z"), .enable("false")) multiplexer_2 (
    .in0(PredictJump), .in1(1'b0), .out(multiplexer_2_out), .sel(RST));
  Multiplexer #(.select(1), .width(32), .disabled("Z"), .enable("false")) multiplexer_3 (
    .in0(PC), .in1({32{1'b0}}), .out(multiplexer_3_out), .sel(RST));
  Register #(.width(32), .trigger("rising"), .Select("low")) register_1 (
    .D(multiplexer_1_out), .en(Run), .Q(\指令字_IR_2 ), .clk(CLK));  // open: clr
  Register #(.width(1), .trigger("rising"), .Select("low")) register_2 (
    .D(multiplexer_2_out), .en(Run), .Q(PredictJump_2), .clk(CLK));  // open: clr
  Register #(.width(32), .trigger("rising"), .Select("low")) register_3 (
    .D(multiplexer_3_out), .en(Run), .Q(PC_2), .clk(CLK));  // open: clr
endmodule

// ID/EX
module \ID_EX流水寄存器  (
  input  Beq,
  input  Bne,
  input  RegWrite,
  input  MemToReg,
  input  MemWrite,
  input  [3:0] AluOP,
  input  AluSrc,
  input  Jal,
  input  Jalr,
  input  Sb,
  input  Bge,
  input  [1:0] R1Foward,
  input  [1:0] R2Foward,
  input  [31:0] R1,
  input  [31:0] R2,
  input  [4:0] WriteReg_num,
  input  ecall,
  input  [31:0] SignImm,
  input  [31:0] B_Imm12,
  input  [31:0] U_Imm20,
  input  PredictJump,
  input  halt,
  input  [31:0] \指令字_IR ,
  input  [31:0] PC,
  input  uret,
  input  RST,
  input  Run,
  input  CLK,
  output Beq_2,
  output Bne_2,
  output RegWrite_2,
  output MemToReg_2,
  output MemWrite_2,
  output [3:0] AluOP_2,
  output AluSrc_2,
  output Jal_2,
  output Jalr_2,
  output Sb_2,
  output Bge_2,
  output [1:0] R1Foward_2,
  output [1:0] R2Foward_2,
  output [31:0] R1_2,
  output [31:0] R2_2,
  output [4:0] WriteReg_num_2,
  output ecall_2,
  output [31:0] SignImm_2,
  output [31:0] B_Imm12_2,
  output [31:0] U_Imm20_2,
  output PredictJump_2,
  output halt_2,
  output [31:0] \指令字_IR_2 ,
  output [31:0] PC_2,
  output uret_2
);

  wire multiplexer_1_out, multiplexer_2_out, multiplexer_3_out, multiplexer_4_out, multiplexer_5_out,
       multiplexer_7_out, multiplexer_8_out, multiplexer_9_out, multiplexer_10_out, multiplexer_11_out,
       multiplexer_17_out, multiplexer_21_out, multiplexer_22_out, multiplexer_25_out;
  wire [1:0] multiplexer_12_out, multiplexer_13_out;
  wire [3:0] multiplexer_6_out;
  wire [4:0] multiplexer_16_out;
  wire [31:0] multiplexer_14_out, multiplexer_15_out, multiplexer_18_out, multiplexer_19_out,
       multiplexer_20_out, multiplexer_23_out, multiplexer_24_out, undriven;

  Multiplexer #(.select(1), .width(1), .disabled("Z"), .enable("false")) multiplexer_1 (
    .in0(Beq), .in1(1'b0), .out(multiplexer_1_out), .sel(RST));
  Multiplexer #(.select(1), .width(1), .disabled("Z"), .enable("false")) multiplexer_2 (
    .in0(Bne), .in1(1'b0), .out(multiplexer_2_out), .sel(RST));
  Multiplexer #(.select(1), .width(1), .disabled("Z"), .enable("false")) multiplexer_3 (
    .in0(RegWrite), .in1(1'b0), .out(multiplexer_3_out), .sel(RST));
  Multiplexer #(.select(1), .width(1), .disabled("Z"), .enable("false")) multiplexer_4 (
    .in0(MemToReg), .in1(1'b0), .out(multiplexer_4_out), .sel(RST));
  Multiplexer #(.select(1), .width(1), .disabled("Z"), .enable("false")) multiplexer_5 (
    .in0(MemWrite), .in1(1'b0), .out(multiplexer_5_out), .sel(RST));
  Multiplexer #(.select(1), .width(4), .disabled("Z"), .enable("false")) multiplexer_6 (
    .in0(AluOP), .in1(4'b0000), .out(multiplexer_6_out), .sel(RST));
  Multiplexer #(.select(1), .width(1), .disabled("Z"), .enable("false")) multiplexer_7 (
    .in0(AluSrc), .in1(1'b0), .out(multiplexer_7_out), .sel(RST));
  Multiplexer #(.select(1), .width(1), .disabled("Z"), .enable("false")) multiplexer_8 (
    .in0(Jal), .in1(1'b0), .out(multiplexer_8_out), .sel(RST));
  Multiplexer #(.select(1), .width(1), .disabled("Z"), .enable("false")) multiplexer_9 (
    .in0(Jalr), .in1(1'b0), .out(multiplexer_9_out), .sel(RST));
  Multiplexer #(.select(1), .width(1), .disabled("Z"), .enable("false")) multiplexer_10 (
    .in0(Sb), .in1(1'b0), .out(multiplexer_10_out), .sel(RST));
  Multiplexer #(.select(1), .width(1), .disabled("Z"), .enable("false")) multiplexer_11 (
    .in0(Bge), .in1(1'b0), .out(multiplexer_11_out), .sel(RST));
  Multiplexer #(.select(1), .width(2), .disabled("Z"), .enable("false")) multiplexer_12 (
    .in0(R1Foward), .in1(2'b00), .out(multiplexer_12_out), .sel(RST));
  Multiplexer #(.select(1), .width(2), .disabled("Z"), .enable("false")) multiplexer_13 (
    .in0(R2Foward), .in1(2'b00), .out(multiplexer_13_out), .sel(RST));
  Multiplexer #(.select(1), .width(32), .disabled("Z"), .enable("false")) multiplexer_14 (
    .in0(R1), .in1({32{1'b0}}), .out(multiplexer_14_out), .sel(RST));
  Multiplexer #(.select(1), .width(32), .disabled("Z"), .enable("false")) multiplexer_15 (
    .in0(R2), .in1({32{1'b0}}), .out(multiplexer_15_out), .sel(RST));
  Multiplexer #(.select(1), .width(5), .disabled("Z"), .enable("false")) multiplexer_16 (
    .in0(WriteReg_num), .in1({5{1'b0}}), .out(multiplexer_16_out), .sel(RST));
  Multiplexer #(.select(1), .width(1), .disabled("Z"), .enable("false")) multiplexer_17 (
    .in0(ecall), .in1(1'b0), .out(multiplexer_17_out), .sel(RST));
  Multiplexer #(.select(1), .width(32), .disabled("Z"), .enable("false")) multiplexer_18 (
    .in0(SignImm), .in1({32{1'b0}}), .out(multiplexer_18_out), .sel(RST));
  Multiplexer #(.select(1), .width(32), .disabled("Z"), .enable("false")) multiplexer_19 (
    .in0(B_Imm12), .in1({32{1'b0}}), .out(multiplexer_19_out), .sel(RST));
  Multiplexer #(.select(1), .width(32), .disabled("Z"), .enable("false")) multiplexer_20 (
    .in0(U_Imm20), .in1({32{1'b0}}), .out(multiplexer_20_out), .sel(RST));
  Multiplexer #(.select(1), .width(1), .disabled("Z"), .enable("false")) multiplexer_21 (
    .in0(PredictJump), .in1(1'b0), .out(multiplexer_21_out), .sel(RST));
  Multiplexer #(.select(1), .width(1), .disabled("Z"), .enable("false")) multiplexer_22 (
    .in0(halt), .in1(1'b0), .out(multiplexer_22_out), .sel(RST));
  Multiplexer #(.select(1), .width(32), .disabled("Z"), .enable("false")) multiplexer_23 (
    .in0(\指令字_IR ), .in1(undriven), .out(multiplexer_23_out), .sel(RST));
  Multiplexer #(.select(1), .width(32), .disabled("Z"), .enable("false")) multiplexer_24 (
    .in0(PC), .in1(undriven), .out(multiplexer_24_out), .sel(RST));
  Multiplexer #(.select(1), .width(1), .disabled("Z"), .enable("false")) multiplexer_25 (
    .in0(uret), .in1(1'b0), .out(multiplexer_25_out), .sel(RST));
  Register #(.width(1), .trigger("rising"), .Select("low")) register_1 (
    .D(multiplexer_1_out), .en(Run), .Q(Beq_2), .clk(CLK));  // open: clr
  Register #(.width(1), .trigger("rising"), .Select("low")) register_2 (
    .D(multiplexer_2_out), .en(Run), .Q(Bne_2), .clk(CLK));  // open: clr
  Register #(.width(1), .trigger("rising"), .Select("low")) register_3 (
    .D(multiplexer_3_out), .en(Run), .Q(RegWrite_2), .clk(CLK));  // open: clr
  Register #(.width(1), .trigger("rising"), .Select("low")) register_4 (
    .D(multiplexer_4_out), .en(Run), .Q(MemToReg_2), .clk(CLK));  // open: clr
  Register #(.width(1), .trigger("rising"), .Select("low")) register_5 (
    .D(multiplexer_5_out), .en(Run), .Q(MemWrite_2), .clk(CLK));  // open: clr
  Register #(.width(4), .trigger("rising"), .Select("low")) register_6 (
    .D(multiplexer_6_out), .en(Run), .Q(AluOP_2), .clk(CLK));  // open: clr
  Register #(.width(1), .trigger("rising"), .Select("low")) register_7 (
    .D(multiplexer_7_out), .en(Run), .Q(AluSrc_2), .clk(CLK));  // open: clr
  Register #(.width(1), .trigger("rising"), .Select("low")) register_8 (
    .D(multiplexer_8_out), .en(Run), .Q(Jal_2), .clk(CLK));  // open: clr
  Register #(.width(1), .trigger("rising"), .Select("low")) register_9 (
    .D(multiplexer_9_out), .en(Run), .Q(Jalr_2), .clk(CLK));  // open: clr
  Register #(.width(1), .trigger("rising"), .Select("low")) register_10 (
    .D(multiplexer_10_out), .en(Run), .Q(Sb_2), .clk(CLK));  // open: clr
  Register #(.width(1), .trigger("rising"), .Select("low")) register_11 (
    .D(multiplexer_11_out), .en(Run), .Q(Bge_2), .clk(CLK));  // open: clr
  Register #(.width(2), .trigger("rising"), .Select("low")) register_12 (
    .D(multiplexer_12_out), .en(Run), .Q(R1Foward_2), .clk(CLK));  // open: clr
  Register #(.width(2), .trigger("rising"), .Select("low")) register_13 (
    .D(multiplexer_13_out), .en(Run), .Q(R2Foward_2), .clk(CLK));  // open: clr
  Register #(.width(32), .trigger("rising"), .Select("low")) register_14 (
    .D(multiplexer_14_out), .en(Run), .Q(R1_2), .clk(CLK));  // open: clr
  Register #(.width(32), .trigger("rising"), .Select("low")) register_15 (
    .D(multiplexer_15_out), .en(Run), .Q(R2_2), .clk(CLK));  // open: clr
  Register #(.width(5), .trigger("rising"), .Select("low")) register_16 (
    .D(multiplexer_16_out), .en(Run), .Q(WriteReg_num_2), .clk(CLK));  // open: clr
  Register #(.width(1), .trigger("rising"), .Select("low")) register_17 (
    .D(multiplexer_17_out), .en(Run), .Q(ecall_2), .clk(CLK));  // open: clr
  Register #(.width(32), .trigger("rising"), .Select("low")) register_18 (
    .D(multiplexer_18_out), .en(Run), .Q(SignImm_2), .clk(CLK));  // open: clr
  Register #(.width(32), .trigger("rising"), .Select("low")) register_19 (
    .D(multiplexer_19_out), .en(Run), .Q(B_Imm12_2), .clk(CLK));  // open: clr
  Register #(.width(32), .trigger("rising"), .Select("low")) register_20 (
    .D(multiplexer_20_out), .en(Run), .Q(U_Imm20_2), .clk(CLK));  // open: clr
  Register #(.width(1), .trigger("rising"), .Select("low")) register_21 (
    .D(multiplexer_21_out), .en(Run), .Q(PredictJump_2), .clk(CLK));  // open: clr
  Register #(.width(1), .trigger("rising"), .Select("low")) register_22 (
    .D(multiplexer_22_out), .en(Run), .Q(halt_2), .clk(CLK));  // open: clr
  Register #(.width(32), .trigger("rising"), .Select("low")) register_23 (
    .D(multiplexer_23_out), .en(Run), .Q(\指令字_IR_2 ), .clk(CLK));  // open: clr
  Register #(.width(32), .trigger("rising"), .Select("low")) register_24 (
    .D(multiplexer_24_out), .Q(PC_2), .clk(CLK));  // open: en, clr
  Register #(.width(1), .trigger("rising"), .Select("low")) register_25 (
    .D(multiplexer_25_out), .en(Run), .Q(uret_2), .clk(CLK));  // open: clr
endmodule

// EX/MEM
module \EX_MEM流水寄存器  (
  input  MemToReg,
  input  MemWrite,
  input  RegWrite,
  input  Jal,
  input  Jalr,
  input  Sb,
  input  [31:0] AluResult,
  input  [31:0] WriteData,
  input  [4:0] W_num,
  input  halt,
  input  [31:0] IR,
  input  [31:0] PC,
  input  uret,
  input  RST,
  input  Run,
  input  CLK,
  output MemToReg_2,
  output MemWrite_2,
  output RegWrite_2,
  output Jal_2,
  output Jalr_2,
  output Sb_2,
  output [31:0] AluResult_2,
  output [31:0] WriteData_2,
  output [4:0] W_num_2,
  output halt_2,
  output [31:0] IR_2,
  output [31:0] PC_2,
  output uret_2
);

  Register #(.width(1), .trigger("rising"), .Select("low")) register_1 (
    .D(MemToReg), .en(Run), .Q(MemToReg_2), .clk(CLK), .clr(RST));
  Register #(.width(1), .trigger("rising"), .Select("low")) register_2 (
    .D(MemWrite), .en(Run), .Q(MemWrite_2), .clk(CLK), .clr(RST));
  Register #(.width(1), .trigger("rising"), .Select("low")) register_3 (
    .D(RegWrite), .en(Run), .Q(RegWrite_2), .clk(CLK), .clr(RST));
  Register #(.width(1), .trigger("rising"), .Select("low")) register_4 (
    .D(Jal), .en(Run), .Q(Jal_2), .clk(CLK), .clr(RST));
  Register #(.width(1), .trigger("rising"), .Select("low")) register_5 (
    .D(Jalr), .en(Run), .Q(Jalr_2), .clk(CLK), .clr(RST));
  Register #(.width(1), .trigger("rising"), .Select("low")) register_6 (
    .D(Sb), .en(Run), .Q(Sb_2), .clk(CLK), .clr(RST));
  Register #(.width(32), .trigger("rising"), .Select("low")) register_7 (
    .D(AluResult), .en(Run), .Q(AluResult_2), .clk(CLK), .clr(RST));
  Register #(.width(32), .trigger("rising"), .Select("low")) register_8 (
    .D(WriteData), .en(Run), .Q(WriteData_2), .clk(CLK), .clr(RST));
  Register #(.width(5), .trigger("rising"), .Select("low")) register_9 (
    .D(W_num), .en(Run), .Q(W_num_2), .clk(CLK), .clr(RST));
  Register #(.width(1), .trigger("rising"), .Select("low")) register_10 (
    .D(halt), .en(Run), .Q(halt_2), .clk(CLK), .clr(RST));
  Register #(.width(32), .trigger("rising"), .Select("low")) register_11 (
    .D(IR), .en(Run), .Q(IR_2), .clk(CLK), .clr(RST));
  Register #(.width(32), .trigger("rising"), .Select("low")) register_12 (
    .D(PC), .en(Run), .Q(PC_2), .clk(CLK), .clr(RST));
  Register #(.width(1), .trigger("rising"), .Select("low")) register_13 (
    .D(uret), .en(Run), .Q(uret_2), .clk(CLK));  // open: clr
endmodule

// MEM/WB
module \MEM_WB流水寄存器  (
  input  MemToReg,
  input  RegWrite,
  input  Jal,
  input  Jalr,
  input  [31:0] AluResult,
  input  [31:0] RD,
  input  [4:0] W_num,
  input  halt,
  input  [31:0] IR,
  input  [31:0] PC,
  input  uret,
  input  RST,
  input  Run,
  input  CLK,
  output MemToReg_2,
  output RegWrite_2,
  output Jal_2,
  output Jalr_2,
  output [31:0] AluResult_2,
  output [31:0] RD_2,
  output [4:0] W_num_2,
  output halt_2,
  output [31:0] IR_2,
  output [31:0] PC_2,
  output uret_2
);

  Register #(.width(1), .trigger("rising"), .Select("low")) register_1 (
    .D(MemToReg), .en(Run), .Q(MemToReg_2), .clk(CLK), .clr(RST));
  Register #(.width(1), .trigger("rising"), .Select("low")) register_2 (
    .D(RegWrite), .en(Run), .Q(RegWrite_2), .clk(CLK), .clr(RST));
  Register #(.width(1), .trigger("rising"), .Select("low")) register_3 (
    .D(Jal), .Q(Jal_2), .clk(CLK), .clr(RST));  // open: en
  Register #(.width(1), .trigger("rising"), .Select("low")) register_4 (
    .D(Jalr), .Q(Jalr_2), .clk(CLK), .clr(RST));  // open: en
  Register #(.width(32), .trigger("rising"), .Select("low")) register_5 (
    .D(AluResult), .en(Run), .Q(AluResult_2), .clk(CLK), .clr(RST));
  Register #(.width(32), .trigger("rising"), .Select("low")) register_6 (
    .D(RD), .en(Run), .Q(RD_2), .clk(CLK), .clr(RST));
  Register #(.width(5), .trigger("rising"), .Select("low")) register_7 (
    .D(W_num), .en(Run), .Q(W_num_2), .clk(CLK), .clr(RST));
  Register #(.width(1), .trigger("rising"), .Select("low")) register_8 (
    .D(halt), .en(Run), .Q(halt_2), .clk(CLK), .clr(RST));
  Register #(.width(32), .trigger("rising"), .Select("low")) register_9 (
    .D(IR), .en(Run), .Q(IR_2), .clk(CLK), .clr(RST));
  Register #(.width(32), .trigger("rising"), .Select("low")) register_10 (
    .D(PC), .en(Run), .Q(PC_2), .clk(CLK), .clr(RST));
  Register #(.width(1), .trigger("rising"), .Select("low")) register_11 (
    .D(uret), .en(Run), .Q(uret_2), .clk(CLK));  // open: clr
endmodule
module \气泡相关处理逻辑  (
  input  BranchTaken,
  input  [31:0] IR,
  input  ecall,
  input  R1Used,
  input  EX_RegWrite,
  input  [4:0] EX_rd,
  input  R2Used,
  input  MEM_RegWrite,
  input  [4:0] MEM_rd,
  output Stall,
  output Flush
);

  wire and_1_out, and_2_out, and_3_out, and_4_out, and_5_out, and_6_out, and_7_out, and_8_out,
       comparator_1_eq, comparator_2_eq, comparator_3_eq, comparator_4_eq, comparator_5_eq, comparator_6_eq,
       comparator_7_eq, comparator_8_eq, comparator_9_eq, comparator_10_eq, comparator_11_eq,
       comparator_12_eq, not_1_out, not_2_out, not_3_out, not_4_out, or_1_out, or_2_out, or_3_out, or_4_out;

  not not_1 (not_1_out, comparator_1_eq);
  Comparator #(.width(5), .mode("twosComplement")) comparator_1 (
    .a(IR[19:15]), .b({5{1'b0}}), .eq(comparator_1_eq));  // open: gt, lt
  Comparator #(.width(5), .mode("twosComplement")) comparator_2 (
    .a(IR[19:15]), .b(EX_rd), .eq(comparator_2_eq));  // open: gt, lt
  not not_2 (not_2_out, comparator_3_eq);
  Comparator #(.width(5), .mode("twosComplement")) comparator_3 (
    .a(IR[24:20]), .b({5{1'b0}}), .eq(comparator_3_eq));  // open: gt, lt
  Comparator #(.width(5), .mode("twosComplement")) comparator_4 (
    .a(IR[24:20]), .b(EX_rd), .eq(comparator_4_eq));  // open: gt, lt
  not not_3 (not_3_out, comparator_5_eq);
  Comparator #(.width(5), .mode("twosComplement")) comparator_5 (
    .a(IR[19:15]), .b({5{1'b0}}), .eq(comparator_5_eq));  // open: gt, lt
  Comparator #(.width(5), .mode("twosComplement")) comparator_6 (
    .a(IR[19:15]), .b(MEM_rd), .eq(comparator_6_eq));  // open: gt, lt
  Comparator #(.width(5), .mode("twosComplement")) comparator_7 (
    .a(IR[24:20]), .b({5{1'b0}}), .eq(comparator_7_eq));  // open: gt, lt
  not not_4 (not_4_out, comparator_7_eq);
  Comparator #(.width(5), .mode("twosComplement")) comparator_8 (
    .a(IR[24:20]), .b(MEM_rd), .eq(comparator_8_eq));  // open: gt, lt
  Comparator #(.width(5), .mode("twosComplement")) comparator_9 (
    .a(5'b10001), .b(EX_rd), .eq(comparator_9_eq));  // open: gt, lt
  Comparator #(.width(5), .mode("twosComplement")) comparator_10 (
    .a(EX_rd), .b(5'b01010), .eq(comparator_10_eq));  // open: gt, lt
  Comparator #(.width(5), .mode("twosComplement")) comparator_11 (
    .a(5'b10001), .b(MEM_rd), .eq(comparator_11_eq));  // open: gt, lt
  Comparator #(.width(5), .mode("twosComplement")) comparator_12 (
    .a(MEM_rd), .b(5'b01010), .eq(comparator_12_eq));  // open: gt, lt
  and and_1 (and_1_out, ecall, EX_RegWrite);
  or or_1 (or_1_out, comparator_9_eq, comparator_10_eq);
  and and_2 (and_2_out, ecall, MEM_RegWrite);
  or or_2 (or_2_out, comparator_11_eq, comparator_12_eq);
  and and_3 (and_3_out, R1Used, not_1_out, EX_RegWrite, comparator_2_eq);
  and and_4 (and_4_out, R2Used, not_2_out, EX_RegWrite, comparator_4_eq);
  and and_5 (and_5_out, R1Used, not_3_out, MEM_RegWrite, comparator_6_eq);
  and and_6 (and_6_out, R2Used, not_4_out, MEM_RegWrite, comparator_8_eq);
  and and_7 (and_7_out, and_1_out, or_1_out);
  and and_8 (and_8_out, and_2_out, or_2_out);
  or or_3 (or_3_out, and_3_out, and_4_out, and_5_out, and_6_out);
  or or_4 (or_4_out, and_7_out, and_8_out);
  or or_5 (Stall, or_3_out, or_4_out);
  or or_6 (Flush, Stall, BranchTaken);

  // Other names for the same wires on the sheet: DataHazzard = Stall; R1[4:0] = IR[19:15]; R2[4:0] = IR[24:20];
  //   r1_used = R1Used; r2_used = R2Used

  // Notes on the sheet:
  //   ecall部分处理
  //   气泡处理输入
  //   相关处理逻辑和气泡处理输出
endmodule

module \重定向相关处理逻辑  (
  input  BranchTaken,
  input  [31:0] IR,
  input  ecall,
  input  EX_MemRead,
  input  R1Used,
  input  EX_RegWrite,
  input  [4:0] EX_rd,
  input  R2Used,
  input  MEM_RegWrite,
  input  [4:0] MEM_rd,
  output Stall,
  output Flush,
  output [1:0] R1Foward,
  output [1:0] R2Foward
);

  wire and_1_out, and_2_out, and_3_out, and_4_out, and_7_out, and_8_out, and_9_out, and_10_out, and_11_out,
       and_12_out, comparator_1_eq, comparator_2_eq, comparator_3_eq, comparator_4_eq, comparator_5_eq,
       comparator_6_eq, comparator_7_eq, comparator_8_eq, comparator_9_eq, comparator_10_eq,
       comparator_11_eq, comparator_12_eq, comparator_13_eq, comparator_14_eq, comparator_15_eq,
       comparator_16_eq, ecall1, ecall2, ecall3, ecall4, not_1_out, not_2_out, not_3_out, not_4_out,
       not_5_out, not_6_out, or_2_out, or_4_out;

  Comparator #(.width(5), .mode("twosComplement")) comparator_1 (
    .a(IR[19:15]), .b({5{1'b0}}), .eq(comparator_1_eq));  // open: gt, lt
  Comparator #(.width(5), .mode("twosComplement")) comparator_2 (
    .a(IR[19:15]), .b({5{1'b0}}), .eq(comparator_2_eq));  // open: gt, lt
  Comparator #(.width(5), .mode("twosComplement")) comparator_3 (
    .a(IR[24:20]), .b({5{1'b0}}), .eq(comparator_3_eq));  // open: gt, lt
  Comparator #(.width(5), .mode("twosComplement")) comparator_4 (
    .a(IR[24:20]), .b({5{1'b0}}), .eq(comparator_4_eq));  // open: gt, lt
  not not_1 (not_1_out, comparator_1_eq);
  Comparator #(.width(5), .mode("twosComplement")) comparator_5 (
    .a(IR[19:15]), .b(EX_rd), .eq(comparator_5_eq));  // open: gt, lt
  not not_2 (not_2_out, comparator_2_eq);
  Comparator #(.width(5), .mode("twosComplement")) comparator_6 (
    .a(IR[19:15]), .b(MEM_rd), .eq(comparator_6_eq));  // open: gt, lt
  not not_3 (not_3_out, comparator_3_eq);
  Comparator #(.width(5), .mode("twosComplement")) comparator_7 (
    .a(IR[24:20]), .b(EX_rd), .eq(comparator_7_eq));  // open: gt, lt
  not not_4 (not_4_out, comparator_4_eq);
  Comparator #(.width(5), .mode("twosComplement")) comparator_8 (
    .a(IR[24:20]), .b(MEM_rd), .eq(comparator_8_eq));  // open: gt, lt
  and and_1 (and_1_out, R1Used, not_1_out, EX_RegWrite, comparator_5_eq);
  and and_2 (and_2_out, R1Used, not_2_out, MEM_RegWrite, comparator_6_eq);
  and and_3 (and_3_out, R2Used, not_3_out, EX_RegWrite, comparator_7_eq);
  and and_4 (and_4_out, R2Used, not_4_out, MEM_RegWrite, comparator_8_eq);
  or or_1 (R1Foward[1], and_1_out, ecall1);
  or or_2 (or_2_out, and_2_out, ecall2);
  or or_3 (R2Foward[1], and_3_out, ecall3);
  or or_4 (or_4_out, and_4_out, ecall4);
  and and_5 (R1Foward[0], ~R1Foward[1], or_2_out);  // AND_Gate
  and and_6 (R2Foward[0], ~R2Foward[1], or_4_out);  // AND_Gate
  Comparator #(.width(5), .mode("twosComplement")) comparator_9 (
    .a(IR[19:15]), .b({5{1'b0}}), .eq(comparator_9_eq));  // open: gt, lt
  Comparator #(.width(5), .mode("twosComplement")) comparator_10 (
    .a(IR[24:20]), .b({5{1'b0}}), .eq(comparator_10_eq));  // open: gt, lt
  not not_5 (not_5_out, comparator_9_eq);
  Comparator #(.width(5), .mode("twosComplement")) comparator_11 (
    .a(IR[19:15]), .b(EX_rd), .eq(comparator_11_eq));  // open: gt, lt
  not not_6 (not_6_out, comparator_10_eq);
  Comparator #(.width(5), .mode("twosComplement")) comparator_12 (
    .a(IR[24:20]), .b(EX_rd), .eq(comparator_12_eq));  // open: gt, lt
  and and_7 (and_7_out, ecall, EX_RegWrite);
  Comparator #(.width(5), .mode("twosComplement")) comparator_13 (
    .a(EX_rd), .b(5'b10001), .eq(comparator_13_eq));  // open: gt, lt
  and and_8 (and_8_out, ecall, MEM_RegWrite);
  Comparator #(.width(5), .mode("twosComplement")) comparator_14 (
    .a(MEM_rd), .b(5'b10001), .eq(comparator_14_eq));  // open: gt, lt
  and and_9 (and_9_out, ecall, EX_RegWrite);
  Comparator #(.width(5), .mode("twosComplement")) comparator_15 (
    .a(EX_rd), .b(5'b01010), .eq(comparator_15_eq));  // open: gt, lt
  and and_10 (and_10_out, ecall, MEM_RegWrite);
  Comparator #(.width(5), .mode("twosComplement")) comparator_16 (
    .a(MEM_rd), .b(5'b01010), .eq(comparator_16_eq));  // open: gt, lt
  or or_5 (Flush, Stall, BranchTaken);
  and and_11 (and_11_out, R1Used, not_5_out, EX_MemRead, comparator_11_eq);
  and and_12 (and_12_out, R2Used, not_6_out, EX_MemRead, comparator_12_eq);
  and and_13 (ecall1, and_7_out, comparator_13_eq);
  and and_14 (ecall2, and_8_out, comparator_14_eq);
  and and_15 (ecall3, and_9_out, comparator_15_eq);
  and and_16 (ecall4, and_10_out, comparator_16_eq);
  or or_6 (Stall, and_11_out, and_12_out);

  // Other names for the same wires on the sheet: R1[4:0] = IR[19:15]; R2[4:0] = IR[24:20]; LoadUse = Stall;
  //   r1_used = R1Used; r2_used = R2Used

  // Notes on the sheet:
  //   重定向处理输入
  //   相关处理逻辑和重定向输出
endmodule

module \动态分支预测  (
  output RegWrite,
  output MemWrite,
  output [31:0] IF_PC,
  output [31:0] ID_PC,
  output [31:0] EX_PC,
  output [31:0] M_PC,
  output [31:0] WB_PC,
  output [31:0] RDin,
  output [31:0] MDin,
  output [31:0] LedData
);

  wire ALU, ALU_t, AluSrcB, and_1_out, and_2_out, and_3_out, and_4_out, and_5_out, and_6_out, and_7_out,
       and_10_out, B_JMP, Beq, Bge, Bne, Branch, CLK, clock_1_out, clock_2_out, comparator_1_eq,
       comparator_2_eq, comparator_2_lt, comparator_3_eq, d_ff_1_q, ecall, EX_Branch, EX_ecall, EX_MemToReg,
       \ex_mem流水寄存器_1_halt_2 , \ex_mem流水寄存器_1_jal_2 , \ex_mem流水寄存器_1_jalr_2 , \ex_mem流水寄存器_1_memtoreg_2 ,
       \ex_mem流水寄存器_1_regwrite_2 , \ex_mem流水寄存器_1_sb_2 , EX_PredictJump, EX_RegWrite, Go, halt,
       \id_ex流水寄存器_1_halt_2 , \id_ex流水寄存器_1_memwrite_2 , \id_ex流水寄存器_1_sb_2 , ID_S_type,
       \if_id流水寄存器_1_predictjump_2 , IR1, IR2, IR3, JAL, JALR, LoadUse, \mem_wb流水寄存器_1_jal_2 ,
       \mem_wb流水寄存器_1_jalr_2 , MemToReg, nand_1_out, not_1_out, not_2_out, not_3_out, not_4_out, not_5_out,
       not_6_out, not_8_out, not_9_out, not_10_out, not_11_out, not_12_out, or_5_out, or_8_out, PredictErr,
       PredictJump, RST, Run, URET, W1, W2, W3, \动态分支预测相关处理逻辑_1_flush , \单周期硬布线控制器_1_alu_src ,
       \单周期硬布线控制器_1_beq , \单周期硬布线控制器_1_bge , \单周期硬布线控制器_1_bne , \单周期硬布线控制器_1_jal , \单周期硬布线控制器_1_jalr ,
       \单周期硬布线控制器_1_memtoreg , \单周期硬布线控制器_1_memwrite , \单周期硬布线控制器_1_r1_used , \单周期硬布线控制器_1_r2_used ,
       \单周期硬布线控制器_1_regwrite , \单周期硬布线控制器_1_sb ;
  wire [1:0] \id_ex流水寄存器_1_r1foward_2 , \id_ex流水寄存器_1_r2foward_2 , or_3_out, \动态分支预测相关处理逻辑_1_r1foward ,
       \动态分支预测相关处理逻辑_1_r2foward ;
  wire [1:1] or_10_out;
  wire [3:0] AluOP, \单周期硬布线控制器_1_alu_op ;
  wire [4:0] EX_W_num, MEM_W_num, multiplexer_13_out, R1_num, R2_num, W_num;
  wire [12:0] CNT_num;
  wire [15:0] \LoadUse次数 , \总周期数 , \插入气泡数 , \无条件分支数 , \条件分支成功数 , \预测失败数 , \预测成功数 ;
  wire [31:0] adder_2_out, alu_1_result, and_9_out, bit_extender_1_out, bit_extender_2_out,
       bit_extender_3_out, bit_extender_4_out, bit_extender_5_out, BRANCH_PC, BranchAddr, btb_1_jumpaddr,
       EX_IR, EX_PC_4, \id_ex流水寄存器_1_b_imm12_2 , \id_ex流水寄存器_1_r1_2 , \id_ex流水寄存器_1_r2_2 ,
       \id_ex流水寄存器_1_signimm_2 , \id_ex流水寄存器_1_u_imm20_2 , ID_IR, IF_IR, JAL_PC, JALR_PC, MEM_ALUResult,
       MEM_IR, \mem_wb流水寄存器_1_aluresult_2 , \mem_wb流水寄存器_1_rd_2 , MemOut, multiplexer_2_out,
       multiplexer_3_out, multiplexer_4_out, multiplexer_7_out, multiplexer_10_out, multiplexer_12_out, PC_4,
       R1, R2, R2_MEM, regifile_1_r1, regifile_1_r2, SB_rst, shifter_1_out, shifter_2_out, shifter_3_out,
       WB_IR, WB_PC_4;

  Button \u_总复位  (.out(RST));
  Button _1 (.out(IR1));
  Button _2 (.out(IR2));
  Button _3 (.out(IR3));
  // Probe on \总周期数 
  // Probe on \总周期数 
  Button \u_继续运行  (.out(Go));
  LED #(.active("true")) led_1 (.in(W1));
  LED #(.active("true")) led_2 (.in(W2));
  LED #(.active("true")) led_3 (.in(W3));
  or or_1 (Run, Go, not_1_out);
  not not_1 (not_1_out, halt);
  not not_2 (not_2_out, halt);
  Counter #(.width(16), .max('hffff), .ongoal("wrap"), .trigger("rising"), .behavior("new")) counter_1 (
    .count(not_2_out), .Q(\总周期数 ), .clk(CLK), .clr(RST));  // open: load, D, carry, preset, down
  Hex_Digit_Display hex_digit_display_1 (.value(LedData[31:28]));  // open: dp
  // Probe on IF_PC[19:0]
  // RiscV_Probe riscv_probe_1: pin names not known; wires that end beside it: IF_IR
  or or_2 (or_3_out[1], JAL, JALR);
  or or_3 (or_3_out[0], JALR, B_JMP);
  Multiplexer #(.select(2), .width(32), .disabled("Z"), .enable("false")) multiplexer_1 (
    .in0(PC_4), .in1(BRANCH_PC), .in2(JAL_PC), .in3(JALR_PC), .out(BranchAddr), .sel(or_3_out));
  Multiplexer #(.select(1), .width(32), .disabled("Z"), .enable("false")) multiplexer_2 (
    .in0(EX_PC_4), .in1(BranchAddr), .out(multiplexer_2_out), .sel(Branch));
  BTB btb_1 (
    .CLK(CLK), .EX_Branch(EX_Branch), .EX_BranchTaken(Branch), .PredictJump(PredictJump), .PC(IF_PC),
    .EX_PC(EX_PC), .EX_BranchAddr(BranchAddr), .JumpAddr(btb_1_jumpaddr));
  or or_4 (EX_Branch, Bne, Beq, Bge, JAL, JALR);
  Hex_Digit_Display hex_digit_display_2 (.value(LedData[23:20]));  // open: dp
  Hex_Digit_Display hex_digit_display_3 (.value(LedData[27:24]));  // open: dp
  // Probe on ID_PC[19:0]
  // RiscV_Probe riscv_probe_2: pin names not known; wires that end beside it: ID_IR
  \动态分支预测相关处理逻辑  \u_动态分支预测相关处理逻辑_1  (
    .PredictErr(PredictErr), .IR(ID_IR), .ecall(ecall), .EX_MemRead(EX_MemToReg),
    .R1Used(\单周期硬布线控制器_1_r1_used ), .EX_RegWrite(EX_RegWrite), .EX_rd(EX_W_num),
    .R2Used(\单周期硬布线控制器_1_r2_used ), .MEM_RegWrite(\ex_mem流水寄存器_1_regwrite_2 ), .MEM_rd(MEM_W_num),
    .Stall(LoadUse), .Flush(\动态分支预测相关处理逻辑_1_flush ), .R1Foward(\动态分支预测相关处理逻辑_1_r1foward ),
    .R2Foward(\动态分支预测相关处理逻辑_1_r2foward ));
  Multiplexer #(.select(1), .width(32), .disabled("Z"), .enable("false")) multiplexer_3 (
    .in0(multiplexer_4_out), .in1(multiplexer_2_out), .out(multiplexer_3_out), .sel(PredictErr));
  Hex_Digit_Display hex_digit_display_4 (.value(LedData[19:16]));  // open: dp
  Hex_Digit_Display hex_digit_display_5 (.value(LedData[15:12]));  // open: dp
  not not_3 (not_3_out, LoadUse);
  and and_1 (and_1_out, not_3_out, Run);
  Multiplexer #(.select(1), .width(32), .disabled("Z"), .enable("false")) multiplexer_4 (
    .in0(PC_4), .in1(btb_1_jumpaddr), .out(multiplexer_4_out), .sel(PredictJump));
  Hex_Digit_Display hex_digit_display_6 (.value(LedData[11:8]));  // open: dp
  Hex_Digit_Display hex_digit_display_7 (.value(LedData[7:4]));  // open: dp
  Clock #(.highDuration(1), .lowDuration(1)) clock_1 (.out(clock_1_out));
  // Probe on EX_PC[19:0]
  // RiscV_Probe riscv_probe_3: pin names not known; wires that end beside it: clock_1_out, EX_IR, CLK
  Register #(.width(32), .trigger("rising"), .Select("low")) PC (
    .D(multiplexer_3_out), .en(and_1_out), .Q(IF_PC), .clk(CLK), .clr(RST));
  Hex_Digit_Display hex_digit_display_8 (.value(LedData[3:0]));  // open: dp
  // Probe on \总周期数 
  // Probe on \无条件分支数 
  // Probe on \条件分支成功数 
  // Probe on \插入气泡数 
  // Probe on \LoadUse次数 
  // Probe on M_PC[19:0]
  // RiscV_Probe riscv_probe_4: pin names not known; wires that end beside it: MEM_IR
  ROM #(.addrWidth(10), .dataWidth(32), .Select("high")) \u_指令存储器  (.addr(IF_PC[11:2]), .data(IF_IR));
  Adder #(.width(32)) adder_1 (.a(IF_PC), .b(32'h4), .out(PC_4));  // open: cin, cout
  // Probe on \总周期数 
  \IF_ID流水寄存器  \if_id流水寄存器_1  (
    .\指令字_IR (IF_IR), .PC(IF_PC), .\指令字_IR_2 (ID_IR), .PC_2(ID_PC), .RST(PredictErr), .Run(and_2_out),
    .CLK(CLK), .PredictJump(PredictJump), .PredictJump_2(\if_id流水寄存器_1_predictjump_2 ));
  and and_2 (and_2_out, Run, not_4_out);
  not not_4 (not_4_out, LoadUse);
  // Probe on \预测成功数 
  // Probe on IF_PC[11:0]
  // Probe on \预测失败数 
  // Probe on WB_PC[19:0]
  // RiscV_Probe riscv_probe_5: pin names not known; wires that end beside it: WB_IR
  // Probe on ID_PC[11:0]
  // Probe on EX_PC[11:0]
  Comparator #(.width(32), .mode("twosComplement")) comparator_1 (
    .a(R1), .b(32'h22), .eq(comparator_1_eq));  // open: gt, lt
  // Probe on M_PC[11:0]
  D_Flip_Flop #(.trigger("high"), .Pre_Clr_Positions("LEGACY"), .NegatePresetClear("false"), .enable("true"), .NewFFLayout("false")) d_ff_1 (.Q(d_ff_1_q));  // open: clk, D, Qn, preset, en, reset
  // Probe on 13'h70
  \单周期硬布线控制器  \u_单周期硬布线控制器_1  (
    .Funct({ID_IR[30], ID_IR[25], ID_IR[14:12]}), .OP(ID_IR[6:2]), .ALU_OP(\单周期硬布线控制器_1_alu_op ),
    .MemToReg(\单周期硬布线控制器_1_memtoreg ), .MemWrite(\单周期硬布线控制器_1_memwrite ), .ALU_SRC(\单周期硬布线控制器_1_alu_src ),
    .RegWrite(\单周期硬布线控制器_1_regwrite ), .ecall(ecall), .S_type(ID_S_type), .Jalr(\单周期硬布线控制器_1_jalr ),
    .Beq(\单周期硬布线控制器_1_beq ), .JAL(\单周期硬布线控制器_1_jal ), .Bne(\单周期硬布线控制器_1_bne ), .IR21(ID_IR[21]), .uret(URET),
    .SB(\单周期硬布线控制器_1_sb ), .BGE(\单周期硬布线控制器_1_bge ), .r1_used(\单周期硬布线控制器_1_r1_used ),
    .r2_used(\单周期硬布线控制器_1_r2_used ));  // open: CSRRSI, CSRRCI
  Multiplexer #(.select(1), .width(5), .disabled("Z"), .enable("false")) multiplexer_5 (
    .in0(ID_IR[19:15]), .in1(5'b10001), .out(R1_num), .sel(ecall));
  Multiplexer #(.select(1), .width(5), .disabled("Z"), .enable("false")) multiplexer_6 (
    .in0(ID_IR[24:20]), .in1(5'b01010), .out(R2_num), .sel(ecall));
  assign bit_extender_1_out = {{20{ID_IR[31]}}, ID_IR[31:20]};  // Bit_Extender bit_extender_1
  assign bit_extender_2_out = {{20{ID_IR[31]}}, {ID_IR[31:25], ID_IR[11:7]}};  // Bit_Extender bit_extender_2
  assign bit_extender_3_out = {{20{ID_IR[31]}}, {ID_IR[31], ID_IR[7], ID_IR[30:25], ID_IR[11:8]}};  // Bit_Extender bit_extender_3
  assign bit_extender_4_out = {{12{ID_IR[31]}}, {ID_IR[31], ID_IR[19:12], ID_IR[20], ID_IR[30:21]}};  // Bit_Extender bit_extender_4
  and and_3 (and_3_out, EX_ecall, comparator_1_eq);
  and and_4 (and_4_out, EX_ecall, ~comparator_1_eq);  // AND_Gate
  // Probe on WB_PC[11:0]
  Comparator #(.width(13), .mode("twosComplement")) comparator_2 (
    .a(CNT_num), .b(13'h70), .eq(comparator_2_eq), .lt(comparator_2_lt));  // open: gt
  Clock #(.highDuration(1), .lowDuration(1)) clock_2 (.out(clock_2_out));
  not not_5 (not_5_out, CLK);
  Regifile regifile_1 (
    .Din(RDin), .Clk(not_5_out), .R1(regifile_1_r1), .R2(regifile_1_r2), .WE(RegWrite), .W_num(W_num),
    .R1_num(R1_num), .R2_num(R2_num));
  Multiplexer #(.select(1), .width(32), .disabled("Z"), .enable("false")) multiplexer_7 (
    .in0(bit_extender_1_out), .in1(bit_extender_2_out), .out(multiplexer_7_out), .sel(ID_S_type));
  Register #(.width(32), .trigger("rising"), .Select("low")) register_1 (
    .D(R2), .en(and_3_out), .Q(LedData), .clk(CLK), .clr(RST));
  nand nand_1 (nand_1_out, d_ff_1_q, comparator_2_eq);
  Counter #(.width(13), .max('h1fff), .ongoal("stay"), .trigger("rising"), .behavior("old")) counter_2 (
    .count(comparator_2_lt), .Q(CNT_num), .clk(clock_2_out));  // open: load, D, carry, clr, preset
  assign CLK = nand_1_out ? clock_2_out : 1'bz;  // Controlled_Buffer controlled_buffer_1
  \ID_EX流水寄存器  \id_ex流水寄存器_1  (
    .RegWrite(\单周期硬布线控制器_1_regwrite ), .MemToReg(\单周期硬布线控制器_1_memtoreg ), .MemWrite(\单周期硬布线控制器_1_memwrite ),
    .AluOP(\单周期硬布线控制器_1_alu_op ), .AluSrc(\单周期硬布线控制器_1_alu_src ), .RegWrite_2(EX_RegWrite),
    .MemToReg_2(EX_MemToReg), .MemWrite_2(\id_ex流水寄存器_1_memwrite_2 ), .AluOP_2(AluOP), .AluSrc_2(AluSrcB),
    .Run(Run), .CLK(CLK), .\指令字_IR (ID_IR), .PC(ID_PC), .RST(\动态分支预测相关处理逻辑_1_flush ), .\指令字_IR_2 (EX_IR),
    .PC_2(EX_PC), .SignImm(multiplexer_7_out), .SignImm_2(\id_ex流水寄存器_1_signimm_2 ),
    .WriteReg_num(ID_IR[11:7]), .WriteReg_num_2(EX_W_num), .B_Imm12(bit_extender_3_out),
    .U_Imm20(bit_extender_4_out), .B_Imm12_2(\id_ex流水寄存器_1_b_imm12_2 ), .U_Imm20_2(\id_ex流水寄存器_1_u_imm20_2 ),
    .R1(regifile_1_r1), .R2(regifile_1_r2), .R1_2(\id_ex流水寄存器_1_r1_2 ), .R2_2(\id_ex流水寄存器_1_r2_2 ),
    .halt(and_4_out), .halt_2(\id_ex流水寄存器_1_halt_2 ), .Jal(\单周期硬布线控制器_1_jal ), .Jalr(\单周期硬布线控制器_1_jalr ),
    .Sb(\单周期硬布线控制器_1_sb ), .Bge(\单周期硬布线控制器_1_bge ), .Jal_2(JAL), .Jalr_2(JALR), .Sb_2(\id_ex流水寄存器_1_sb_2 ),
    .Bge_2(Bge), .Beq(\单周期硬布线控制器_1_beq ), .Bne(\单周期硬布线控制器_1_bne ), .Beq_2(Beq), .Bne_2(Bne),
    .R1Foward(\动态分支预测相关处理逻辑_1_r1foward ), .R1Foward_2(\id_ex流水寄存器_1_r1foward_2 ),
    .R2Foward(\动态分支预测相关处理逻辑_1_r2foward ), .R2Foward_2(\id_ex流水寄存器_1_r2foward_2 ), .ecall(ecall),
    .ecall_2(EX_ecall), .PredictJump(\if_id流水寄存器_1_predictjump_2 ), .PredictJump_2(EX_PredictJump));  // open: uret, uret_2
  Pull_Resistor #(.pull(1)) pull_resistor_1 (.node(CLK));
  Shifter #(.width(32), .shift("ll")) shifter_1 (.in(\id_ex流水寄存器_1_b_imm12_2 ), .\dist (5'b00001), .out(shifter_1_out));
  Shifter #(.width(32), .shift("ll")) shifter_2 (.in(\id_ex流水寄存器_1_u_imm20_2 ), .\dist (5'b00001), .out(shifter_2_out));
  not not_6 (not_6_out, halt);
  or or_5 (or_5_out, JAL, JALR);
  Comparator #(.width(1), .mode("twosComplement")) comparator_3 (
    .a(EX_PredictJump), .b(Branch), .eq(comparator_3_eq));  // open: gt, lt
  Multiplexer #(.select(2), .width(32), .disabled("Z"), .enable("false")) multiplexer_8 (
    .in0(\id_ex流水寄存器_1_r1_2 ), .in1(RDin), .in2(MEM_ALUResult), .out(R1), .sel(\id_ex流水寄存器_1_r1foward_2 ));  // open: in3
  Multiplexer #(.select(2), .width(32), .disabled("Z"), .enable("false")) multiplexer_9 (
    .in0(\id_ex流水寄存器_1_r2_2 ), .in1(RDin), .in2(MEM_ALUResult), .out(R2), .sel(\id_ex流水寄存器_1_r2foward_2 ));  // open: in3
  Counter #(.width(16), .max('hffff), .ongoal("wrap"), .trigger("rising"), .behavior("new")) counter_3 (
    .count(not_6_out), .Q(\无条件分支数 ), .clk(or_5_out), .clr(RST));  // open: load, D, carry, preset, down
  not not_7 (PredictErr, comparator_3_eq);
  Multiplexer #(.select(1), .width(32), .disabled("Z"), .enable("false")) multiplexer_10 (
    .in0(R2), .in1(\id_ex流水寄存器_1_signimm_2 ), .out(multiplexer_10_out), .sel(AluSrcB));
  Adder #(.width(32)) adder_2 (.a(R1), .b(\id_ex流水寄存器_1_signimm_2 ), .out(adder_2_out));  // open: cin, cout
  and and_5 (and_5_out, Bne, ~ALU);  // AND_Gate
  and and_6 (and_6_out, Beq, ALU);
  and and_7 (and_7_out, Bge, ALU_t);
  ALU alu_1 (
    .X(R1), .Y(multiplexer_10_out), .AluOP(AluOP), .Equal(ALU), .Result(alu_1_result), .out_4(ALU_t));  // open: Result_2, out_6
  Adder #(.width(32)) adder_3 (.a(EX_PC), .b(shifter_1_out), .out(BRANCH_PC));  // open: cin, cout
  Adder #(.width(32)) adder_4 (.a(EX_PC), .b(shifter_2_out), .out(JAL_PC));  // open: cin, cout
  or or_6 (B_JMP, and_5_out, and_6_out, and_7_out);
  not not_8 (not_8_out, halt);
  Counter #(.width(16), .max('hffff), .ongoal("wrap"), .trigger("rising"), .behavior("new")) counter_4 (
    .count(not_8_out), .Q(\条件分支成功数 ), .clk(B_JMP), .clr(RST));  // open: load, D, carry, preset, down
  assign JALR_PC = 32'hfffffffe & adder_2_out;  // AND_Gate and_8, 32 bits wide
  or or_7 (Branch, B_JMP, JAL, JALR);
  \EX_MEM流水寄存器  \ex_mem流水寄存器_1  (
    .MemToReg(EX_MemToReg), .MemWrite(\id_ex流水寄存器_1_memwrite_2 ), .RegWrite(EX_RegWrite),
    .AluResult(alu_1_result), .WriteData(R2), .W_num(EX_W_num), .IR(EX_IR), .PC(EX_PC),
    .MemToReg_2(\ex_mem流水寄存器_1_memtoreg_2 ), .MemWrite_2(MemWrite), .RegWrite_2(\ex_mem流水寄存器_1_regwrite_2 ),
    .AluResult_2(MEM_ALUResult), .WriteData_2(R2_MEM), .W_num_2(MEM_W_num), .IR_2(MEM_IR), .PC_2(M_PC),
    .RST(RST), .Run(Run), .CLK(CLK), .halt(\id_ex流水寄存器_1_halt_2 ), .halt_2(\ex_mem流水寄存器_1_halt_2 ),
    .Jal(JAL), .Jalr(JALR), .Sb(\id_ex流水寄存器_1_sb_2 ), .Jal_2(\ex_mem流水寄存器_1_jal_2 ),
    .Jalr_2(\ex_mem流水寄存器_1_jalr_2 ), .Sb_2(\ex_mem流水寄存器_1_sb_2 ));  // open: uret, uret_2
  or or_8 (or_8_out, PredictErr, LoadUse);
  not not_9 (not_9_out, halt);
  Counter #(.width(16), .max('hffff), .ongoal("wrap"), .trigger("rising"), .behavior("old")) counter_5 (
    .count(or_8_out), .Q(\插入气泡数 ), .clk(CLK), .clr(RST));  // open: load, D, carry, preset
  Multiplexer #(.select(1), .width(32), .disabled("Z"), .enable("false")) multiplexer_11 (
    .in0(R2_MEM), .in1(SB_rst), .out(MDin), .sel(\ex_mem流水寄存器_1_sb_2 ));
  Multiplexer #(.select(2), .width(32), .disabled("Z"), .enable("false")) multiplexer_12 (
    .in0(32'hffffff00), .in1(32'hffff00ff), .in2(32'hff00ffff), .in3(32'hffffff), .out(multiplexer_12_out),
    .sel(MEM_ALUResult[1:0]));
  Multiplexer #(.select(2), .width(5), .disabled("Z"), .enable("false")) multiplexer_13 (
    .in0({5{1'b0}}), .in1(5'b01000), .in2(5'b10000), .in3(5'b11000), .out(multiplexer_13_out),
    .sel(MEM_ALUResult[1:0]));
  RAM #(.addrWidth(10), .dataWidth(32), .bus("separate"), .Select("high")) ram_1 (
    .addr(MEM_ALUResult[11:2]), .din(MDin), .data(MemOut), .str(MemWrite), .clk(CLK));  // open: sel, ld, clr
  not not_10 (not_10_out, halt);
  Counter #(.width(16), .max('hffff), .ongoal("wrap"), .trigger("rising"), .behavior("old")) counter_6 (
    .count(LoadUse), .Q(\LoadUse次数 ), .clk(CLK), .clr(RST));  // open: load, D, carry, preset
  assign and_9_out = MemOut & multiplexer_12_out;  // AND_Gate and_9, 32 bits wide
  assign bit_extender_5_out = {{24{1'b0}}, R2_MEM[7:0]};  // Bit_Extender bit_extender_5
  Shifter #(.width(32), .shift("ll")) shifter_3 (
    .in(bit_extender_5_out), .\dist (multiplexer_13_out), .out(shifter_3_out));
  assign SB_rst = and_9_out | shifter_3_out;  // OR_Gate or_9, 32 bits wide
  \MEM_WB流水寄存器  \mem_wb流水寄存器_1  (
    .MemToReg(\ex_mem流水寄存器_1_memtoreg_2 ), .RegWrite(\ex_mem流水寄存器_1_regwrite_2 ), .AluResult(MEM_ALUResult),
    .RD(MemOut), .W_num(MEM_W_num), .IR(MEM_IR), .PC(M_PC), .MemToReg_2(MemToReg), .RegWrite_2(RegWrite),
    .AluResult_2(\mem_wb流水寄存器_1_aluresult_2 ), .RD_2(\mem_wb流水寄存器_1_rd_2 ), .W_num_2(W_num), .IR_2(WB_IR),
    .PC_2(WB_PC), .RST(RST), .Run(Run), .CLK(CLK), .halt(\ex_mem流水寄存器_1_halt_2 ), .halt_2(halt),
    .Jal(\ex_mem流水寄存器_1_jal_2 ), .Jalr(\ex_mem流水寄存器_1_jalr_2 ), .Jal_2(\mem_wb流水寄存器_1_jal_2 ),
    .Jalr_2(\mem_wb流水寄存器_1_jalr_2 ));  // open: uret, uret_2
  not not_11 (not_11_out, halt);
  and and_10 (and_10_out, ~PredictErr, EX_Branch);  // AND_Gate
  or or_10 (or_10_out[1], \mem_wb流水寄存器_1_jal_2 , \mem_wb流水寄存器_1_jalr_2 );
  Multiplexer #(.select(2), .width(32), .disabled("Z"), .enable("false")) multiplexer_14 (
    .in0(\mem_wb流水寄存器_1_aluresult_2 ), .in1(\mem_wb流水寄存器_1_rd_2 ), .in2(WB_PC_4), .out(RDin),
    .sel({or_10_out[1], MemToReg}));  // open: in3
  Adder #(.width(32)) adder_5 (.a(WB_PC), .b(32'h4), .out(WB_PC_4));  // open: cin, cout
  Adder #(.width(32)) adder_6 (.a(EX_PC), .b(32'h4), .out(EX_PC_4));  // open: cin, cout
  Counter #(.width(16), .max('hffff), .ongoal("wrap"), .trigger("rising"), .behavior("old")) counter_7 (
    .count(and_10_out), .Q(\预测成功数 ), .clk(CLK), .clr(RST));  // open: load, D, carry, preset
  not not_12 (not_12_out, halt);
  Counter #(.width(16), .max('hffff), .ongoal("wrap"), .trigger("rising"), .behavior("old")) counter_8 (
    .count(PredictErr), .Q(\预测失败数 ), .clk(CLK), .clr(RST));  // open: load, D, carry, preset

  // Other names for the same wires on the sheet: MEM_PC[31:0] = M_PC

  // Notes on the sheet:
  //   中断源
  //   时空图监测，可删除
  //   中断等待指示
  //   PC
  //   EX.Branch代表是分支跳转指令，不一定满足跳转条件
  //   PredictJump
  //   JumpAddr
  //   数码管输出
  //   IF段
  //   contents of 指令存储器 (hex, n*v repeats v):
  //   100493 100006f 100493 200913 300993 100006f 100493 200913 300993 100006f 100493 200913 300993
  //   100006f 100493 200913 300993 3a8000ef 100413 100493 1f49493 900533 2200893 73 24d493 48463 fedff06f
  //   900533 2200893 73 100493 249493 900533 2200893 73 48463 fedff06f 100493 1f49493 900533 2200893 73
  //   4034d493 900533 2200893 73 4044d493 900533 2200893 73 4044d493 900533 2200893 73 4044d493 900533
  //   2200893 73 4044d493 900533 2200893 73 4044d493 900533 2200893 73 4044d493 900533 2200893 73 4044d493
  //   900533 2200893 73 100413 1f41993 41f9d993 433 c00913 300b13 140413 f47413 800293 100313 499993
  //   89e9b3 1300533 2200893 73 406282b3 fe0294e3 140413 f00f93 1f47433 1c41413 800293 100313 49d993
  //   89e9b3 1300533 2200893 73 406282b3 fe0294e3 1c45413 406b0b33 b0463 f95ff06f 2b3 fff2c293 829293
  //   ff2e293 500533 2200893 73 fff00413 493 84a023 140413 448493 84a023 140413 448493 84a023 140413
  //   448493 84a023 140413 448493 84a023 140413 448493 84a023 140413 448493 84a023 140413 448493 84a023
  //   140413 448493 84a023 140413 448493 84a023 140413 448493 84a023 140413 448493 84a023 140413 448493
  //   84a023 140413 448493 84a023 140413 448493 84a023 140413 448493 84a023 140413 448493 140413 433
  //   3c00493 42983 4aa03 149a2b3 28663 134a023 1442023 ffc48493 fe9412e3 800533 2200893 73 440413 3c00493
  //   fc9416e3 3200893 73 100293 300313 800493 849493 7648493 900533 2200893 73 800e13 5494b3 6494b3
  //   900533 2200893 73 fffe0e13 fe0e14e3 a00893 73 fff00293 7700493 849493 7748493 900533 2200893 73
  //   1000e13 54c4b3 900533 2200893 73 fffe0e13 fe0e16e3 a00893 73 313 2000e13 493 100913 930023 900533
  //   2200893 73 12484b3 130313 fffe0e13 fe0e12e3 800e13 313 32483 900533 2200893 73 430313 fffe0e13
  //   fe0e14e3 a00893 73 f00493 900533 2200893 73 fff48493 fe04d8e3 a00893 73 a00893 73 413 140413 800533
  //   2200893 73 240413 800533 2200893 73 340413 800533 2200893 73 440413 800533 2200893 73 540413 800533
  //   2200893 73 640413 800533 2200893 73 740413 800533 2200893 73 840413 800533 2200893 2200893 73 8067
  //   指令字
  //   IR
  //   PC
  //   控制位
  //   rs
  //   rt
  //   I型指令立即数
  //   S型指令立即数
  //   W#
  //   B型指令立即数
  //   J型指令立即数
  //   流水调试日志用
  //   暂停节拍，不能为0
  //   JAL
  //   Beq
  //   JALR
  //   Bne
  //   URET
  //   SB
  //   BGE
  //   OP
  //   Funct
  //   戳工具置1进入计数暂停模式，ctrl+k时钟自动运行到对应节拍暂停
  //   ctrl+k关闭时钟连续运行，将控制位置零，进入单步调试模式调试
  //   ID段
  //   MemToReg
  //   MemWrite
  //   AluOP
  //   AluSrcB
  //   RegWrite
  //   S_type
  //   可计数暂停的时钟源
  //   Beq
  //   Bne
  //   MemToReg
  //   MemWrite
  //   AluOP
  //   AluSrcB
  //   RegWrite
  //   JAL
  //   JALR
  //   SB
  //   BGE
  //   R1
  //   R2
  //   SignImm
  //   W#
  //   halt
  //   IR
  //   PC
  //   EX段
  //   BranchTaken相关逻辑
  //   为方便自动评测，需要输出流水线各段保存的PC值，注意是PC不是PC+4，另外ID段寄存器写入信息，Mem段内存写入信息也要输出
  //   jalr指令目的地址
  //   beq\bne\bge指令目的地址
  //   jal指令目的地址
  //   MemToReg
  //   MemWrite
  //   RegWrite
  //   JAL
  //   JALR
  //   SB
  //   ALUResult
  //   W#
  //   halt
  //   IR
  //   PC
  //   数据存储器
  //   MEM段
  //   SB指令实现
  //   MemOut
  //   JAL
  //   W#
  //   halt
  //   IR
  //   PC
  //   JALR
  //   ALUResult
  //   MemOut
  //   WB段
  //   WB段PC+4生成
  //   EX段PC+4生成
endmodule

module BTB (
  input  CLK,
  input  EX_Branch,
  input  EX_BranchTaken,
  input  [31:0] PC,
  input  [31:0] EX_PC,
  input  [31:0] EX_BranchAddr,
  output PredictJump,
  output [31:0] JumpAddr
);

  wire and_17_out, and_18_out, and_19_out, and_20_out, and_21_out, and_22_out, and_23_out, and_24_out,
       and_26_out, cache_full, comparator_1_eq, comparator_2_eq, comparator_3_eq, comparator_4_eq,
       comparator_5_eq, comparator_6_eq, comparator_7_eq, comparator_8_eq, comparator_9_eq, comparator_10_eq,
       comparator_11_eq, comparator_12_eq, comparator_13_eq, comparator_14_eq, comparator_15_eq,
       comparator_16_eq, d_ff_1_q, d_ff_2_q, d_ff_3_q, d_ff_4_q, d_ff_5_q, d_ff_6_q, d_ff_7_q, d_ff_8_q,
       EX_Hit, EX_Miss, hit0, hit1, hit2, hit3, hit4, hit5, hit6, hit7, L0, L1, L2, L3, L4, L5, L6, L7,
       not_1_out, not_2_out, not_3_out, not_4_out, not_5_out, not_6_out, not_7_out, not_8_out, or_1_out,
       or_2_out, or_3_out, or_4_out, or_5_out, or_6_out, or_7_out, or_8_out, valid0, valid1, valid2, valid3,
       valid4, valid5, valid6, valid7, write0, write1, write2, write3, write4, write5, write6, write7;
  wire [0:0] controlled_buffer_9_out, controlled_buffer_10_out, controlled_buffer_11_out,
       controlled_buffer_12_out, controlled_buffer_13_out, controlled_buffer_14_out,
       controlled_buffer_15_out, controlled_buffer_16_out;
  wire [1:0] predict0, predict1, predict2, predict3, predict4, predict5, predict6, predict7,
       \双预测位状态转换_1_nextlow , \双预测位状态转换_2_nextlow , \双预测位状态转换_3_nextlow , \双预测位状态转换_4_nextlow ,
       \双预测位状态转换_5_nextlow , \双预测位状态转换_6_nextlow , \双预测位状态转换_7_nextlow , \双预测位状态转换_8_nextlow ;
  wire [2:0] \max3_归并比较_1_max_num , \max3_归并比较_2_max_num , \max3_归并比较_3_max_num , \max3_归并比较_4_max_num ,
       \max3_归并比较_5_max_num , \max3_归并比较_6_max_num , \max3_归并比较_7_max_num , multiplexer_1_out,
       priority_encoder_1_out;
  wire [15:0] cnt0, cnt1, cnt2, cnt3, cnt4, cnt5, cnt6, cnt7, \max3_归并比较_1_max , \max3_归并比较_2_max ,
       \max3_归并比较_3_max , \max3_归并比较_4_max , \max3_归并比较_5_max , \max3_归并比较_6_max , \max3_归并比较_7_max ;
  wire [31:0] register_17_q, register_18_q, register_19_q, register_20_q, register_21_q, register_22_q,
       register_23_q, register_24_q, tag0, tag1, tag2, tag3, tag4, tag5, tag6, tag7;

  LED #(.active("true")) led_1 (.in(valid0));
  Register #(.width(1), .trigger("rising"), .Select("low")) register_1 (
    .D(1'b1), .en(write0), .Q(valid0), .clk(CLK));  // open: clr
  LED #(.active("true")) led_2 (.in(valid1));
  Register #(.width(1), .trigger("rising"), .Select("low")) register_2 (
    .D(1'b1), .en(write1), .Q(valid1), .clk(CLK));  // open: clr
  LED #(.active("true")) led_3 (.in(valid2));
  Register #(.width(1), .trigger("rising"), .Select("low")) register_3 (
    .D(1'b1), .en(write2), .Q(valid2), .clk(CLK));  // open: clr
  LED #(.active("true")) led_4 (.in(valid3));
  Register #(.width(1), .trigger("rising"), .Select("low")) register_4 (
    .D(1'b1), .en(write3), .Q(valid3), .clk(CLK));  // open: clr
  LED #(.active("true")) led_5 (.in(valid4));
  Register #(.width(1), .trigger("rising"), .Select("low")) register_5 (
    .D(1'b1), .en(write4), .Q(valid4), .clk(CLK));  // open: clr
  LED #(.active("true")) led_6 (.in(valid5));
  Register #(.width(1), .trigger("rising"), .Select("low")) register_6 (
    .D(1'b1), .en(write5), .Q(valid5), .clk(CLK));  // open: clr
  LED #(.active("true")) led_7 (.in(valid6));
  Register #(.width(1), .trigger("rising"), .Select("low")) register_7 (
    .D(1'b1), .en(write6), .Q(valid6), .clk(CLK));  // open: clr
  LED #(.active("true")) led_8 (.in(valid7));
  Register #(.width(1), .trigger("rising"), .Select("low")) register_8 (
    .D(1'b1), .en(write7), .Q(valid7), .clk(CLK));  // open: clr
  // Probe on tag0
  Register #(.width(32), .trigger("rising"), .Select("low")) register_9 (
    .D(EX_PC), .en(write0), .Q(tag0), .clk(CLK));  // open: clr
  // Probe on tag1
  Register #(.width(32), .trigger("rising"), .Select("low")) register_10 (
    .D(EX_PC), .en(write1), .Q(tag1), .clk(CLK));  // open: clr
  // Probe on tag2
  Register #(.width(32), .trigger("rising"), .Select("low")) register_11 (
    .D(EX_PC), .en(write2), .Q(tag2), .clk(CLK));  // open: clr
  // Probe on tag3
  Register #(.width(32), .trigger("rising"), .Select("low")) register_12 (
    .D(EX_PC), .en(write3), .Q(tag3), .clk(CLK));  // open: clr
  // Probe on tag4
  Register #(.width(32), .trigger("rising"), .Select("low")) register_13 (
    .D(EX_PC), .en(write4), .Q(tag4), .clk(CLK));  // open: clr
  // Probe on tag5
  Register #(.width(32), .trigger("rising"), .Select("low")) register_14 (
    .D(EX_PC), .en(write5), .Q(tag5), .clk(CLK));  // open: clr
  // Probe on tag6
  Register #(.width(32), .trigger("rising"), .Select("low")) register_15 (
    .D(EX_PC), .en(write6), .Q(tag6), .clk(CLK));  // open: clr
  // Probe on tag7
  Register #(.width(32), .trigger("rising"), .Select("low")) register_16 (
    .D(EX_PC), .en(write7), .Q(tag7), .clk(CLK));  // open: clr
  Counter #(.width(16), .max('hffff), .ongoal("wrap"), .trigger("rising"), .behavior("new")) counter_1 (
    .Q(cnt0), .clk(CLK), .clr(d_ff_1_q));  // open: load, D, count, carry, preset, down
  or or_1 (or_1_out, write0, L0);
  Counter #(.width(16), .max('hffff), .ongoal("wrap"), .trigger("rising"), .behavior("new")) counter_2 (
    .Q(cnt1), .clk(CLK), .clr(d_ff_2_q));  // open: load, D, count, carry, preset, down
  or or_2 (or_2_out, write1, L1);
  Counter #(.width(16), .max('hffff), .ongoal("wrap"), .trigger("rising"), .behavior("new")) counter_3 (
    .Q(cnt2), .clk(CLK), .clr(d_ff_3_q));  // open: load, D, count, carry, preset, down
  or or_3 (or_3_out, write2, L2);
  Counter #(.width(16), .max('hffff), .ongoal("wrap"), .trigger("rising"), .behavior("new")) counter_4 (
    .Q(cnt3), .clk(CLK), .clr(d_ff_4_q));  // open: load, D, count, carry, preset, down
  or or_4 (or_4_out, write3, L3);
  Counter #(.width(16), .max('hffff), .ongoal("wrap"), .trigger("rising"), .behavior("new")) counter_5 (
    .Q(cnt4), .clk(CLK), .clr(d_ff_5_q));  // open: load, D, count, carry, preset, down
  or or_5 (or_5_out, write4, L4);
  Counter #(.width(16), .max('hffff), .ongoal("wrap"), .trigger("rising"), .behavior("new")) counter_6 (
    .Q(cnt5), .clk(CLK), .clr(d_ff_6_q));  // open: load, D, count, carry, preset, down
  or or_6 (or_6_out, write5, L5);
  Counter #(.width(16), .max('hffff), .ongoal("wrap"), .trigger("rising"), .behavior("new")) counter_7 (
    .Q(cnt6), .clk(CLK), .clr(d_ff_7_q));  // open: load, D, count, carry, preset, down
  or or_7 (or_7_out, write6, L6);
  Counter #(.width(16), .max('hffff), .ongoal("wrap"), .trigger("rising"), .behavior("new")) counter_8 (
    .Q(cnt7), .clk(CLK), .clr(d_ff_8_q));  // open: load, D, count, carry, preset, down
  or or_8 (or_8_out, write7, L7);
  // Probe on cnt0
  D_Flip_Flop #(.trigger("rising"), .Pre_Clr_Positions("ABOVE_BELOW"), .NegatePresetClear("false"), .enable("false"), .NewFFLayout("true")) d_ff_1 (
    .clk(CLK), .D(or_1_out), .Q(d_ff_1_q));  // open: Qn, preset, reset
  // Probe on cnt1
  D_Flip_Flop #(.trigger("rising"), .Pre_Clr_Positions("ABOVE_BELOW"), .NegatePresetClear("false"), .enable("false"), .NewFFLayout("true")) d_ff_2 (
    .clk(CLK), .D(or_2_out), .Q(d_ff_2_q));  // open: Qn, preset, reset
  // Probe on cnt2
  D_Flip_Flop #(.trigger("rising"), .Pre_Clr_Positions("ABOVE_BELOW"), .NegatePresetClear("false"), .enable("false"), .NewFFLayout("true")) d_ff_3 (
    .clk(CLK), .D(or_3_out), .Q(d_ff_3_q));  // open: Qn, preset, reset
  // Probe on cnt3
  D_Flip_Flop #(.trigger("rising"), .Pre_Clr_Positions("ABOVE_BELOW"), .NegatePresetClear("false"), .enable("false"), .NewFFLayout("true")) d_ff_4 (
    .clk(CLK), .D(or_4_out), .Q(d_ff_4_q));  // open: Qn, preset, reset
  // Probe on cnt4
  D_Flip_Flop #(.trigger("rising"), .Pre_Clr_Positions("ABOVE_BELOW"), .NegatePresetClear("false"), .enable("false"), .NewFFLayout("true")) d_ff_5 (
    .clk(CLK), .D(or_5_out), .Q(d_ff_5_q));  // open: Qn, preset, reset
  // Probe on cnt5
  D_Flip_Flop #(.trigger("rising"), .Pre_Clr_Positions("ABOVE_BELOW"), .NegatePresetClear("false"), .enable("false"), .NewFFLayout("true")) d_ff_6 (
    .clk(CLK), .D(or_6_out), .Q(d_ff_6_q));  // open: Qn, preset, reset
  // Probe on cnt6
  D_Flip_Flop #(.trigger("rising"), .Pre_Clr_Positions("ABOVE_BELOW"), .NegatePresetClear("false"), .enable("false"), .NewFFLayout("true")) d_ff_7 (
    .clk(CLK), .D(or_7_out), .Q(d_ff_7_q));  // open: Qn, preset, reset
  // Probe on cnt7
  D_Flip_Flop #(.trigger("rising"), .Pre_Clr_Positions("ABOVE_BELOW"), .NegatePresetClear("false"), .enable("false"), .NewFFLayout("true")) d_ff_8 (
    .clk(CLK), .D(or_8_out), .Q(d_ff_8_q));  // open: Qn, preset, reset
  // Probe on register_17_q
  Register #(.width(32), .trigger("rising"), .Select("low")) register_17 (
    .D(EX_BranchAddr), .en(write0), .Q(register_17_q), .clk(CLK));  // open: clr
  // Probe on register_18_q
  Register #(.width(32), .trigger("rising"), .Select("low")) register_18 (
    .D(EX_BranchAddr), .en(write1), .Q(register_18_q), .clk(CLK));  // open: clr
  // Probe on register_19_q
  Register #(.width(32), .trigger("rising"), .Select("low")) register_19 (
    .D(EX_BranchAddr), .en(write2), .Q(register_19_q), .clk(CLK));  // open: clr
  // Probe on register_20_q
  Register #(.width(32), .trigger("rising"), .Select("low")) register_20 (
    .D(EX_BranchAddr), .en(write3), .Q(register_20_q), .clk(CLK));  // open: clr
  // Probe on register_21_q
  Register #(.width(32), .trigger("rising"), .Select("low")) register_21 (
    .D(EX_BranchAddr), .en(write4), .Q(register_21_q), .clk(CLK));  // open: clr
  // Probe on register_22_q
  Register #(.width(32), .trigger("rising"), .Select("low")) register_22 (
    .D(EX_BranchAddr), .en(write5), .Q(register_22_q), .clk(CLK));  // open: clr
  // Probe on register_23_q
  Register #(.width(32), .trigger("rising"), .Select("low")) register_23 (
    .D(EX_BranchAddr), .en(write6), .Q(register_23_q), .clk(CLK));  // open: clr
  // Probe on register_24_q
  Register #(.width(32), .trigger("rising"), .Select("low")) register_24 (
    .D(EX_BranchAddr), .en(write7), .Q(register_24_q), .clk(CLK));  // open: clr
  assign JumpAddr = L0 ? register_17_q : 32'bz;  // Controlled_Buffer controlled_buffer_1
  assign JumpAddr = L1 ? register_18_q : 32'bz;  // Controlled_Buffer controlled_buffer_2
  assign JumpAddr = L2 ? register_19_q : 32'bz;  // Controlled_Buffer controlled_buffer_3
  assign JumpAddr = L3 ? register_20_q : 32'bz;  // Controlled_Buffer controlled_buffer_4
  assign JumpAddr = L4 ? register_21_q : 32'bz;  // Controlled_Buffer controlled_buffer_5
  assign JumpAddr = L5 ? register_22_q : 32'bz;  // Controlled_Buffer controlled_buffer_6
  assign JumpAddr = L6 ? register_23_q : 32'bz;  // Controlled_Buffer controlled_buffer_7
  assign JumpAddr = L7 ? register_24_q : 32'bz;  // Controlled_Buffer controlled_buffer_8
  Comparator #(.width(32), .mode("twosComplement")) comparator_1 (
    .a(tag0), .b(PC), .eq(comparator_1_eq));  // open: gt, lt
  Comparator #(.width(32), .mode("twosComplement")) comparator_2 (
    .a(tag0), .b(EX_PC), .eq(comparator_2_eq));  // open: gt, lt
  Comparator #(.width(32), .mode("twosComplement")) comparator_3 (
    .a(tag1), .b(PC), .eq(comparator_3_eq));  // open: gt, lt
  Comparator #(.width(32), .mode("twosComplement")) comparator_4 (
    .a(tag1), .b(EX_PC), .eq(comparator_4_eq));  // open: gt, lt
  Comparator #(.width(32), .mode("twosComplement")) comparator_5 (
    .a(tag2), .b(PC), .eq(comparator_5_eq));  // open: gt, lt
  Comparator #(.width(32), .mode("twosComplement")) comparator_6 (
    .a(tag2), .b(EX_PC), .eq(comparator_6_eq));  // open: gt, lt
  Comparator #(.width(32), .mode("twosComplement")) comparator_7 (
    .a(tag3), .b(PC), .eq(comparator_7_eq));  // open: gt, lt
  Comparator #(.width(32), .mode("twosComplement")) comparator_8 (
    .a(tag3), .b(EX_PC), .eq(comparator_8_eq));  // open: gt, lt
  Comparator #(.width(32), .mode("twosComplement")) comparator_9 (
    .a(tag4), .b(PC), .eq(comparator_9_eq));  // open: gt, lt
  Comparator #(.width(32), .mode("twosComplement")) comparator_10 (
    .a(tag4), .b(EX_PC), .eq(comparator_10_eq));  // open: gt, lt
  Comparator #(.width(32), .mode("twosComplement")) comparator_11 (
    .a(tag5), .b(PC), .eq(comparator_11_eq));  // open: gt, lt
  Comparator #(.width(32), .mode("twosComplement")) comparator_12 (
    .a(tag5), .b(EX_PC), .eq(comparator_12_eq));  // open: gt, lt
  Comparator #(.width(32), .mode("twosComplement")) comparator_13 (
    .a(tag6), .b(PC), .eq(comparator_13_eq));  // open: gt, lt
  Comparator #(.width(32), .mode("twosComplement")) comparator_14 (
    .a(tag6), .b(EX_PC), .eq(comparator_14_eq));  // open: gt, lt
  Comparator #(.width(32), .mode("twosComplement")) comparator_15 (
    .a(tag7), .b(PC), .eq(comparator_15_eq));  // open: gt, lt
  Comparator #(.width(32), .mode("twosComplement")) comparator_16 (
    .a(tag7), .b(EX_PC), .eq(comparator_16_eq));  // open: gt, lt
  and and_1 (L0, valid0, comparator_1_eq);
  and and_2 (hit0, valid0, comparator_2_eq);
  and and_3 (L1, valid1, comparator_3_eq);
  and and_4 (hit1, valid1, comparator_4_eq);
  and and_5 (L2, valid2, comparator_5_eq);
  and and_6 (hit2, valid2, comparator_6_eq);
  and and_7 (L3, valid3, comparator_7_eq);
  and and_8 (hit3, valid3, comparator_8_eq);
  and and_9 (L4, valid4, comparator_9_eq);
  and and_10 (hit4, valid4, comparator_10_eq);
  and and_11 (L5, valid5, comparator_11_eq);
  and and_12 (hit5, valid5, comparator_12_eq);
  and and_13 (L6, valid6, comparator_13_eq);
  and and_14 (hit6, valid6, comparator_14_eq);
  and and_15 (L7, valid7, comparator_15_eq);
  and and_16 (hit7, valid7, comparator_16_eq);
  \双预测位状态转换  \u_双预测位状态转换_1  (
    .High(predict0[1]), .Low(predict0[0]), .Jump(EX_BranchTaken), .NextHigh(\双预测位状态转换_1_nextlow [1]),
    .NextLow(\双预测位状态转换_1_nextlow [0]));
  \双预测位状态转换  \u_双预测位状态转换_2  (
    .High(predict1[1]), .Low(predict1[0]), .Jump(EX_BranchTaken), .NextHigh(\双预测位状态转换_2_nextlow [1]),
    .NextLow(\双预测位状态转换_2_nextlow [0]));
  \双预测位状态转换  \u_双预测位状态转换_3  (
    .High(predict2[1]), .Low(predict2[0]), .Jump(EX_BranchTaken), .NextHigh(\双预测位状态转换_3_nextlow [1]),
    .NextLow(\双预测位状态转换_3_nextlow [0]));
  \双预测位状态转换  \u_双预测位状态转换_4  (
    .High(predict3[1]), .Low(predict3[0]), .Jump(EX_BranchTaken), .NextHigh(\双预测位状态转换_4_nextlow [1]),
    .NextLow(\双预测位状态转换_4_nextlow [0]));
  \双预测位状态转换  \u_双预测位状态转换_5  (
    .High(predict4[1]), .Low(predict4[0]), .Jump(EX_BranchTaken), .NextHigh(\双预测位状态转换_5_nextlow [1]),
    .NextLow(\双预测位状态转换_5_nextlow [0]));
  \双预测位状态转换  \u_双预测位状态转换_6  (
    .High(predict5[1]), .Low(predict5[0]), .Jump(EX_BranchTaken), .NextHigh(\双预测位状态转换_6_nextlow [1]),
    .NextLow(\双预测位状态转换_6_nextlow [0]));
  \双预测位状态转换  \u_双预测位状态转换_7  (
    .High(predict6[1]), .Low(predict6[0]), .Jump(EX_BranchTaken), .NextHigh(\双预测位状态转换_7_nextlow [1]),
    .NextLow(\双预测位状态转换_7_nextlow [0]));
  \双预测位状态转换  \u_双预测位状态转换_8  (
    .High(predict7[1]), .Low(predict7[0]), .Jump(EX_BranchTaken), .NextHigh(\双预测位状态转换_8_nextlow [1]),
    .NextLow(\双预测位状态转换_8_nextlow [0]));
  and and_17 (and_17_out, EX_Branch, hit0);
  and and_18 (and_18_out, EX_Branch, hit1);
  and and_19 (and_19_out, EX_Branch, hit2);
  and and_20 (and_20_out, EX_Branch, hit3);
  and and_21 (and_21_out, EX_Branch, hit4);
  and and_22 (and_22_out, EX_Branch, hit5);
  and and_23 (and_23_out, EX_Branch, hit6);
  and and_24 (and_24_out, EX_Branch, hit7);
  Register #(.width(2), .trigger("rising"), .Select("low")) register_25 (
    .D(\双预测位状态转换_1_nextlow ), .en(and_17_out), .Q(predict0), .clk(CLK));  // open: clr
  Register #(.width(2), .trigger("rising"), .Select("low")) register_26 (
    .D(\双预测位状态转换_2_nextlow ), .en(and_18_out), .Q(predict1), .clk(CLK));  // open: clr
  Register #(.width(2), .trigger("rising"), .Select("low")) register_27 (
    .D(\双预测位状态转换_3_nextlow ), .en(and_19_out), .Q(predict2), .clk(CLK));  // open: clr
  Register #(.width(2), .trigger("rising"), .Select("low")) register_28 (
    .D(\双预测位状态转换_4_nextlow ), .en(and_20_out), .Q(predict3), .clk(CLK));  // open: clr
  Register #(.width(2), .trigger("rising"), .Select("low")) register_29 (
    .D(\双预测位状态转换_5_nextlow ), .en(and_21_out), .Q(predict4), .clk(CLK));  // open: clr
  Register #(.width(2), .trigger("rising"), .Select("low")) register_30 (
    .D(\双预测位状态转换_6_nextlow ), .en(and_22_out), .Q(predict5), .clk(CLK));  // open: clr
  Register #(.width(2), .trigger("rising"), .Select("low")) register_31 (
    .D(\双预测位状态转换_7_nextlow ), .en(and_23_out), .Q(predict6), .clk(CLK));  // open: clr
  Register #(.width(2), .trigger("rising"), .Select("low")) register_32 (
    .D(\双预测位状态转换_8_nextlow ), .en(and_24_out), .Q(predict7), .clk(CLK));  // open: clr
  assign {PredictJump, controlled_buffer_9_out[0]} = L0 ? predict0 : 2'bz;  // Controlled_Buffer controlled_buffer_9
  assign {PredictJump, controlled_buffer_10_out[0]} = L1 ? predict1 : 2'bz;  // Controlled_Buffer controlled_buffer_10
  assign {PredictJump, controlled_buffer_11_out[0]} = L2 ? predict2 : 2'bz;  // Controlled_Buffer controlled_buffer_11
  assign {PredictJump, controlled_buffer_12_out[0]} = L3 ? predict3 : 2'bz;  // Controlled_Buffer controlled_buffer_12
  assign {PredictJump, controlled_buffer_13_out[0]} = L4 ? predict4 : 2'bz;  // Controlled_Buffer controlled_buffer_13
  assign {PredictJump, controlled_buffer_14_out[0]} = L5 ? predict5 : 2'bz;  // Controlled_Buffer controlled_buffer_14
  assign {PredictJump, controlled_buffer_15_out[0]} = L6 ? predict6 : 2'bz;  // Controlled_Buffer controlled_buffer_15
  assign {PredictJump, controlled_buffer_16_out[0]} = L7 ? predict7 : 2'bz;  // Controlled_Buffer controlled_buffer_16
  Pull_Resistor #(.pull(0)) pull_resistor_1 (.node(PredictJump));
  Pull_Resistor #(.pull(0)) pull_resistor_2 (.node(PredictJump));
  Pull_Resistor #(.pull(0)) pull_resistor_3 (.node(PredictJump));
  Pull_Resistor #(.pull(0)) pull_resistor_4 (.node(PredictJump));
  Pull_Resistor #(.pull(0)) pull_resistor_5 (.node(PredictJump));
  Pull_Resistor #(.pull(0)) pull_resistor_6 (.node(PredictJump));
  Pull_Resistor #(.pull(0)) pull_resistor_7 (.node(PredictJump));
  Pull_Resistor #(.pull(0)) pull_resistor_8 (.node(PredictJump));
  not not_1 (not_1_out, valid0);
  not not_2 (not_2_out, valid1);
  not not_3 (not_3_out, valid2);
  not not_4 (not_4_out, valid3);
  not not_5 (not_5_out, valid4);
  not not_6 (not_6_out, valid5);
  not not_7 (not_7_out, valid6);
  not not_8 (not_8_out, valid7);
  \MAX3_归并比较  \max3_归并比较_1  (
    .Y(cnt1), .X(cnt0), .Y_num(3'b001), .X_num(3'b000), .MAX(\max3_归并比较_1_max ),
    .Max_num(\max3_归并比较_1_max_num ));
  \MAX3_归并比较  \max3_归并比较_2  (
    .Y(cnt3), .X(cnt2), .Y_num(3'b011), .X_num(3'b010), .MAX(\max3_归并比较_2_max ),
    .Max_num(\max3_归并比较_2_max_num ));
  \MAX3_归并比较  \max3_归并比较_3  (
    .Y(cnt5), .X(cnt4), .Y_num(3'b101), .X_num(3'b100), .MAX(\max3_归并比较_3_max ),
    .Max_num(\max3_归并比较_3_max_num ));
  \MAX3_归并比较  \max3_归并比较_4  (
    .Y(cnt7), .X(cnt6), .Y_num(3'b111), .X_num(3'b110), .MAX(\max3_归并比较_4_max ),
    .Max_num(\max3_归并比较_4_max_num ));
  Priority_Encoder #(.select(3), .disabled("Z")) priority_encoder_1 (
    .in0(not_1_out), .in1(not_2_out), .in2(not_3_out), .in3(not_4_out), .in4(not_5_out), .in5(not_6_out),
    .in6(not_7_out), .in7(not_8_out), .out(priority_encoder_1_out));  // open: gs, en_out, en_in
  \MAX3_归并比较  \max3_归并比较_5  (
    .Y(\max3_归并比较_2_max ), .X(\max3_归并比较_1_max ), .Y_num(\max3_归并比较_2_max_num ),
    .X_num(\max3_归并比较_1_max_num ), .MAX(\max3_归并比较_5_max ), .Max_num(\max3_归并比较_5_max_num ));
  \MAX3_归并比较  \max3_归并比较_6  (
    .Y(\max3_归并比较_4_max ), .X(\max3_归并比较_3_max ), .Y_num(\max3_归并比较_4_max_num ),
    .X_num(\max3_归并比较_3_max_num ), .MAX(\max3_归并比较_6_max ), .Max_num(\max3_归并比较_6_max_num ));
  and and_25 (cache_full, valid0, valid1, valid2, valid3, valid4, valid5, valid6, valid7);
  or or_9 (EX_Hit, hit0, hit1, hit2, hit3, hit4, hit5, hit6, hit7);
  not not_9 (EX_Miss, EX_Hit);
  \MAX3_归并比较  \max3_归并比较_7  (
    .Y(\max3_归并比较_6_max ), .X(\max3_归并比较_5_max ), .Y_num(\max3_归并比较_6_max_num ),
    .X_num(\max3_归并比较_5_max_num ), .MAX(\max3_归并比较_7_max ), .Max_num(\max3_归并比较_7_max_num ));
  // Probe on \max3_归并比较_7_max 
  // Probe on priority_encoder_1_out
  Multiplexer #(.select(1), .width(3), .disabled("Z"), .enable("false")) multiplexer_1 (
    .in0(priority_encoder_1_out), .in1(\max3_归并比较_7_max_num ), .out(multiplexer_1_out), .sel(cache_full));
  // Probe on \max3_归并比较_7_max_num 
  // Probe on multiplexer_1_out
  Decoder #(.select(3), .tristate("false"), .disabled(0), .enable("true")) decoder_1 (
    .out0(write0), .out1(write1), .out2(write2), .out3(write3), .out4(write4), .out5(write5), .out6(write6),
    .out7(write7), .sel(multiplexer_1_out), .en(and_26_out));
  and and_26 (and_26_out, EX_Miss, EX_Branch);

  // Notes on the sheet:
  //   分支历史表BTB输入
  //   cache槽设计
  //   cache槽设计
  //   cache槽设计
  //   cache槽设计
  //   cache槽设计
  //   cache槽设计
  //   cache槽设计
  //   cache槽设计
  //   分支历史表BTB输出
  //   查找逻辑
  //   写入逻辑
  //   查找逻辑
  //   写入逻辑
  //   查找逻辑
  //   写入逻辑
  //   查找逻辑
  //   写入逻辑
  //   查找逻辑
  //   写入逻辑
  //   查找逻辑
  //   写入逻辑
  //   查找逻辑
  //   写入逻辑
  //   查找逻辑
  //   写入逻辑
  //   预测位状态机更新逻辑
  //   预测位状态机更新逻辑
  //   预测位状态机更新逻辑
  //   预测位状态机更新逻辑
  //   预测位状态机更新逻辑
  //   预测位状态机更新逻辑
  //   预测位状态机更新逻辑
  //   预测位状态机更新逻辑
  //   默认为0
  //   默认为0
  //   默认为0
  //   默认为0
  //   默认为0
  //   默认为0
  //   默认为0
  //   默认为0
endmodule

module \双预测位状态转换  (
  input  High,
  input  Low,
  input  Jump,
  output NextHigh,
  output NextLow
);

  wire and_1_out, and_2_out, and_3_out, and_4_out, not_1_out, not_2_out, not_3_out, not_4_out, not_5_out;

  not not_1 (not_1_out, Low);
  not not_2 (not_2_out, High);
  not not_3 (not_3_out, Low);
  not not_4 (not_4_out, Low);
  not not_5 (not_5_out, Jump);
  and and_1 (and_1_out, Low, Jump);
  and and_2 (and_2_out, High, not_1_out);
  and and_3 (and_3_out, not_2_out, not_3_out, Jump);
  and and_4 (and_4_out, High, not_4_out, not_5_out);
  or or_1 (NextHigh, and_1_out, and_2_out);
  or or_2 (NextLow, and_3_out, and_4_out);
endmodule

// MAX3
module \MAX3_归并比较  (
  input  [15:0] Y,
  input  [15:0] X,
  input  [2:0] Y_num,
  input  [2:0] X_num,
  output [15:0] MAX,
  output [2:0] Max_num
);

  wire comparator_1_eq, comparator_1_gt, or_1_out;

  Multiplexer #(.select(1), .width(16), .disabled("Z"), .enable("false")) multiplexer_1 (
    .in0(Y), .in1(X), .out(MAX), .sel(or_1_out));
  Comparator #(.width(16), .mode("unsigned")) comparator_1 (
    .a(X), .b(Y), .gt(comparator_1_gt), .eq(comparator_1_eq));  // open: lt
  or or_1 (or_1_out, comparator_1_gt, comparator_1_eq);
  Multiplexer #(.select(1), .width(3), .disabled("Z"), .enable("false")) multiplexer_2 (
    .in0(Y_num), .in1(X_num), .out(Max_num), .sel(or_1_out));

  // Notes on the sheet:
  //   输出两个输入中的较大值，并输出较大值的3位编号
endmodule

module \动态分支预测相关处理逻辑  (
  input  PredictErr,
  input  [31:0] IR,
  input  ecall,
  input  EX_MemRead,
  input  R1Used,
  input  EX_RegWrite,
  input  [4:0] EX_rd,
  input  R2Used,
  input  MEM_RegWrite,
  input  [4:0] MEM_rd,
  output Stall,
  output Flush,
  output [1:0] R1Foward,
  output [1:0] R2Foward
);

  wire and_1_out, and_2_out, and_3_out, and_4_out, and_7_out, and_8_out, and_9_out, and_10_out, and_11_out,
       and_12_out, comparator_1_eq, comparator_2_eq, comparator_3_eq, comparator_4_eq, comparator_5_eq,
       comparator_6_eq, comparator_7_eq, comparator_8_eq, comparator_9_eq, comparator_10_eq,
       comparator_11_eq, comparator_12_eq, comparator_13_eq, comparator_14_eq, comparator_15_eq,
       comparator_16_eq, ecall1, ecall2, ecall3, ecall4, not_1_out, not_2_out, not_3_out, not_4_out,
       not_5_out, not_6_out, or_2_out, or_4_out;

  Comparator #(.width(5), .mode("twosComplement")) comparator_1 (
    .a(IR[19:15]), .b({5{1'b0}}), .eq(comparator_1_eq));  // open: gt, lt
  Comparator #(.width(5), .mode("twosComplement")) comparator_2 (
    .a(IR[19:15]), .b({5{1'b0}}), .eq(comparator_2_eq));  // open: gt, lt
  Comparator #(.width(5), .mode("twosComplement")) comparator_3 (
    .a(IR[24:20]), .b({5{1'b0}}), .eq(comparator_3_eq));  // open: gt, lt
  Comparator #(.width(5), .mode("twosComplement")) comparator_4 (
    .a(IR[24:20]), .b({5{1'b0}}), .eq(comparator_4_eq));  // open: gt, lt
  not not_1 (not_1_out, comparator_1_eq);
  Comparator #(.width(5), .mode("twosComplement")) comparator_5 (
    .a(IR[19:15]), .b(EX_rd), .eq(comparator_5_eq));  // open: gt, lt
  not not_2 (not_2_out, comparator_2_eq);
  Comparator #(.width(5), .mode("twosComplement")) comparator_6 (
    .a(IR[19:15]), .b(MEM_rd), .eq(comparator_6_eq));  // open: gt, lt
  not not_3 (not_3_out, comparator_3_eq);
  Comparator #(.width(5), .mode("twosComplement")) comparator_7 (
    .a(IR[24:20]), .b(EX_rd), .eq(comparator_7_eq));  // open: gt, lt
  not not_4 (not_4_out, comparator_4_eq);
  Comparator #(.width(5), .mode("twosComplement")) comparator_8 (
    .a(IR[24:20]), .b(MEM_rd), .eq(comparator_8_eq));  // open: gt, lt
  and and_1 (and_1_out, R1Used, not_1_out, EX_RegWrite, comparator_5_eq);
  and and_2 (and_2_out, R1Used, not_2_out, MEM_RegWrite, comparator_6_eq);
  and and_3 (and_3_out, R2Used, not_3_out, EX_RegWrite, comparator_7_eq);
  and and_4 (and_4_out, R2Used, not_4_out, MEM_RegWrite, comparator_8_eq);
  or or_1 (R1Foward[1], and_1_out, ecall1);
  or or_2 (or_2_out, and_2_out, ecall2);
  or or_3 (R2Foward[1], and_3_out, ecall3);
  or or_4 (or_4_out, and_4_out, ecall4);
  and and_5 (R1Foward[0], ~R1Foward[1], or_2_out);  // AND_Gate
  and and_6 (R2Foward[0], ~R2Foward[1], or_4_out);  // AND_Gate
  Comparator #(.width(5), .mode("twosComplement")) comparator_9 (
    .a(IR[19:15]), .b({5{1'b0}}), .eq(comparator_9_eq));  // open: gt, lt
  Comparator #(.width(5), .mode("twosComplement")) comparator_10 (
    .a(IR[24:20]), .b({5{1'b0}}), .eq(comparator_10_eq));  // open: gt, lt
  not not_5 (not_5_out, comparator_9_eq);
  Comparator #(.width(5), .mode("twosComplement")) comparator_11 (
    .a(IR[19:15]), .b(EX_rd), .eq(comparator_11_eq));  // open: gt, lt
  not not_6 (not_6_out, comparator_10_eq);
  Comparator #(.width(5), .mode("twosComplement")) comparator_12 (
    .a(IR[24:20]), .b(EX_rd), .eq(comparator_12_eq));  // open: gt, lt
  and and_7 (and_7_out, ecall, EX_RegWrite);
  Comparator #(.width(5), .mode("twosComplement")) comparator_13 (
    .a(EX_rd), .b(5'b10001), .eq(comparator_13_eq));  // open: gt, lt
  and and_8 (and_8_out, ecall, MEM_RegWrite);
  Comparator #(.width(5), .mode("twosComplement")) comparator_14 (
    .a(MEM_rd), .b(5'b10001), .eq(comparator_14_eq));  // open: gt, lt
  and and_9 (and_9_out, ecall, EX_RegWrite);
  Comparator #(.width(5), .mode("twosComplement")) comparator_15 (
    .a(EX_rd), .b(5'b01010), .eq(comparator_15_eq));  // open: gt, lt
  and and_10 (and_10_out, ecall, MEM_RegWrite);
  Comparator #(.width(5), .mode("twosComplement")) comparator_16 (
    .a(MEM_rd), .b(5'b01010), .eq(comparator_16_eq));  // open: gt, lt
  or or_5 (Flush, Stall, PredictErr);
  and and_11 (and_11_out, R1Used, not_5_out, EX_MemRead, comparator_11_eq);
  and and_12 (and_12_out, R2Used, not_6_out, EX_MemRead, comparator_12_eq);
  and and_13 (ecall1, and_7_out, comparator_13_eq);
  and and_14 (ecall2, and_8_out, comparator_14_eq);
  and and_15 (ecall3, and_9_out, comparator_15_eq);
  and and_16 (ecall4, and_10_out, comparator_16_eq);
  or or_6 (Stall, and_11_out, and_12_out);

  // Other names for the same wires on the sheet: R1[4:0] = IR[19:15]; R2[4:0] = IR[24:20]; LoadUse = Stall;
  //   r1_used = R1Used; r2_used = R2Used

  // Notes on the sheet:
  //   动态分支预测输入
  //   相关处理逻辑和动态分支预测输出
endmodule
